// Logisim project Frogger.circ as structural Verilog: 3 circuits, main circuit main
module main (
);

  wire _0, _1, _1bAnim, _2, _3, _4, _5, _6, _7, _8, _9, _10, _11, _12, boliddriver_1_outflag,
       boliddriver_2_outflag, boliddriver_3_outflag, bump, carconnectorv2_1_outflag,
       carconnectorv2_2_outflag, carconnectorv2_3_outflag, clock, computeintresection_1_outintersect,
       computeintresection_2_outintersect, computeintresection_3_outintersect,
       computeintresection_4_outintersect, controlled_buffer_2_out, \event , finishcomputer_1_die, good_jump,
       heightflag_7_p3, I_Osel, IAck, in_out, intersection, IRQ, keyboard_2_p2, level_clock,
       log_1x1_1_outflag, log_1x1_2_outflag, log_1x1_3_outflag, log_1x1_4_outflag, log_2x1_1_outflag,
       log_2x1_2_outflag, log_2x1_3_outflag, log_2x1_4_outflag, log_3x2_1_outflag, log_3x2_2_outflag,
       log_3x2_3_outflag, log_3x2_4_outflag, n2_1turtlesintersector_1_outintersect, not_1_out, not_2_out,
       number_of_saved_frogs_victory_lose_1_event, or_3_out, pull_resistor_1_node, res, rescue, restartGame,
       s_r_ff_1_q, s_r_ff_1_qn, smalllogintersect_1_outintersect, stop, stop_out, suvdriver_1_outflag,
       suvdriver_2_outflag, suvdriver_3_outflag, swampdriver_1_p26, swampdriver_1_p27, swampdriver_1_p28,
       swampdriver_1_p29, swampdriver_1_p30, swampdriver_2_p24, swampdriver_2_p25, swampdriver_2_p26,
       swampdriver_2_p27, swampdriver_2_p28, swampdriver_3_p26, swampdriver_3_p27, swampdriver_3_p28,
       swampdriver_3_p29, swampdriver_3_p30, swampdriver_4_p26, swampdriver_4_p27, swampdriver_4_p28,
       swampdriver_4_p29, swampdriver_4_p30, swampdriver_5_p27, swampdriver_5_p28, swampdriver_5_p29,
       swampdriver_5_p30, swampdriver_5_p31, swampdriver_6_p26, swampdriver_6_p27, swampdriver_6_p28,
       swampdriver_6_p29, swampdriver_6_p30, time_is_gone, truckdriver_1_outflag, truckdriver_2_outflag,
       truckdriver_3_outflag, truckdriver_4_outflag, truckdriver_5_outflag, truckdriver_6_outflag,
       turtle_2x1_1_outflag, turtle_2x1_2_outflag, turtle_2x1_3_outflag, turtle_2x1_4_outflag,
       turtle_3x1_1_animstate_2, turtle_3x1_1_outflag, turtle_3x1_2_animstate_2, turtle_3x1_2_outflag,
       turtle_3x1_3_animstate_2, turtle_3x1_3_outflag, turtle_3x1_4_outflag, waterintersect_1_outintersect,
       waterintersect_2_outintersect, waterintersect_3_outintersect, win;
  wire [1:0] boliddriver_1_outbackshiftd, boliddriver_1_outplayershiftd, boliddriver_2_outbackshiftd,
       boliddriver_2_outplayershiftd, boliddriver_3_outbackshiftd, boliddriver_3_outplayershiftd,
       carconnectorv2_1_outbackshiftd, carconnectorv2_1_outplayershiftd, carconnectorv2_2_outbackshiftd,
       carconnectorv2_2_outplayershiftd, carconnectorv2_3_outbackshiftd, carconnectorv2_3_outplayershiftd,
       finishconnector_1_circnumber_2, finishconnector_2_circnumber_2, finishconnector_3_circnumber_2,
       finishconnector_4_circnumber_2, keyboard_2_p9, leftshifter_1_shiftd, leftshifter_2_shiftd,
       leftshifter_3_shiftd, leftshifter_4_shiftd, leftshifter_5_shiftd, log_1x1_1_outbackshiftd,
       log_1x1_1_outplayershiftd, log_1x1_2_outbackshiftd, log_1x1_2_outplayershiftd,
       log_1x1_3_outbackshiftd, log_1x1_3_outplayershiftd, log_1x1_4_outbackshiftd,
       log_1x1_4_outplayershiftd, log_2x1_1_outbackshiftd, log_2x1_1_outplayershiftd,
       log_2x1_2_outbackshiftd, log_2x1_2_outplayershiftd, log_2x1_3_outbackshiftd,
       log_2x1_3_outplayershiftd, log_2x1_4_outbackshiftd, log_2x1_4_outplayershiftd,
       log_3x2_1_outbackshiftd, log_3x2_1_outplayershiftd, log_3x2_2_outbackshiftd,
       log_3x2_2_outplayershiftd, log_3x2_3_outbackshiftd, log_3x2_3_outplayershiftd,
       log_3x2_4_outbackshiftd, log_3x2_4_outplayershiftd, rightshifter_1_shiftd, rightshifter_2_shiftd,
       rightshifter_3_p7, rightshifter_4_shiftd, rightshifter_5_shiftd, suvdriver_1_outbackshiftd,
       suvdriver_1_outplayershiftd, suvdriver_2_outbackshiftd, suvdriver_2_outplayershiftd,
       suvdriver_3_outbackshiftd, suvdriver_3_outplayershiftd, truckdriver_1_outbackshiftd,
       truckdriver_1_outplayershiftd, truckdriver_2_outbackshiftd, truckdriver_2_outplayershiftd,
       truckdriver_3_outbackshiftd, truckdriver_3_outplayershiftd, truckdriver_4_outbackshiftd,
       truckdriver_4_outplayershiftd, truckdriver_5_outbackshiftd, truckdriver_5_outplayershiftd,
       truckdriver_6_outbackshiftd, truckdriver_6_outplayershiftd, turtle_2x1_1_outbackshiftd,
       turtle_2x1_1_outplayershiftd, turtle_2x1_2_outbackshiftd, turtle_2x1_2_outplayershiftd,
       turtle_2x1_3_outbackshiftd, turtle_2x1_3_outplayershiftd, turtle_2x1_4_outbackshiftd,
       turtle_2x1_4_outplayershiftd, turtle_3x1_1_outbackshiftd, turtle_3x1_1_outplayershiftd,
       turtle_3x1_2_outbackshiftd, turtle_3x1_2_outplayershiftd, turtle_3x1_3_outbackshiftd,
       turtle_3x1_3_outplayershiftd, turtle_3x1_4_outbackshiftd, turtle_3x1_4_outplayershiftd;
  wire [2:0] leftshifter_1_keyborder, leftshifter_2_keyborder, lKB, rightshifter_1_rkb, rightshifter_2_rkb,
       rightshifter_3_p1, rKB, vector;
  wire [3:0] current_score_1_the_first_digit, current_score_1_the_second_digit,
       current_score_1_the_third_digit, finishcomputer_1_positions, finishconnector_1_positions_2,
       finishconnector_2_positions_2, finishconnector_3_positions_2, finishconnector_4_positions_2, I_Oadr,
       lives_1_number_of_lives, max_height_1_max_height, n2_1turtlesintersector_1_animstate,
       number_of_saved_frogs_victory_lose_1_number_of_survivors, record_score_1_the_first_digit,
       record_score_1_the_second_digit, record_score_1_the_third_digit, timer_1_the_first_digit,
       timer_1_the_second_digit, turtle_2x1_1_animstate_2, turtle_2x1_2_animstate_2,
       turtle_2x1_3_animstate_2, Y;
  wire [4:0] boliddriver_1_outplayershiftm, boliddriver_1_outputbackshiftm, boliddriver_2_outplayershiftm,
       boliddriver_2_outputbackshiftm, boliddriver_3_outplayershiftm, boliddriver_3_outputbackshiftm,
       carconnectorv2_1_outplayershiftm, carconnectorv2_1_outputbackshiftm, carconnectorv2_2_outplayershiftm,
       carconnectorv2_2_outputbackshiftm, carconnectorv2_3_outplayershiftm,
       carconnectorv2_3_outputbackshiftm, keyboard_2_p8, leftshifter_1_shiftm, leftshifter_2_shiftm,
       leftshifter_3_shiftm, leftshifter_4_shiftm, leftshifter_5_shiftm, log_1x1_1_outplayershiftm,
       log_1x1_1_outputbackshiftm, log_1x1_2_outplayershiftm, log_1x1_2_outputbackshiftm,
       log_1x1_3_outplayershiftm, log_1x1_3_outputbackshiftm, log_1x1_4_outplayershiftm,
       log_1x1_4_outputbackshiftm, log_2x1_1_outplayershiftm, log_2x1_1_outputbackshiftm,
       log_2x1_2_outplayershiftm, log_2x1_2_outputbackshiftm, log_2x1_3_outplayershiftm,
       log_2x1_3_outputbackshiftm, log_2x1_4_outplayershiftm, log_2x1_4_outputbackshiftm,
       log_3x2_1_outplayershiftm, log_3x2_1_outputbackshiftm, log_3x2_2_outplayershiftm,
       log_3x2_2_outputbackshiftm, log_3x2_3_outplayershiftm, log_3x2_3_outputbackshiftm,
       log_3x2_4_outplayershiftm, log_3x2_4_outputbackshiftm, rightshifter_1_shiftm, rightshifter_2_shiftm,
       rightshifter_3_p4, rightshifter_4_shiftm, rightshifter_5_shiftm, suvdriver_1_outplayershiftm,
       suvdriver_1_outputbackshiftm, suvdriver_2_outplayershiftm, suvdriver_2_outputbackshiftm,
       suvdriver_3_outplayershiftm, suvdriver_3_outputbackshiftm, truckdriver_1_outplayershiftm,
       truckdriver_1_outputbackshiftm, truckdriver_2_outplayershiftm, truckdriver_2_outputbackshiftm,
       truckdriver_3_outplayershiftm, truckdriver_3_outputbackshiftm, truckdriver_4_outplayershiftm,
       truckdriver_4_outputbackshiftm, truckdriver_5_outplayershiftm, truckdriver_5_outputbackshiftm,
       truckdriver_6_outplayershiftm, truckdriver_6_outputbackshiftm, turtle_2x1_1_outplayershiftm,
       turtle_2x1_1_outputbackshiftm, turtle_2x1_2_outplayershiftm, turtle_2x1_2_outputbackshiftm,
       turtle_2x1_3_outplayershiftm, turtle_2x1_3_outputbackshiftm, turtle_2x1_4_outplayershiftm,
       turtle_2x1_4_outputbackshiftm, turtle_3x1_1_outplayershiftm, turtle_3x1_1_outputbackshiftm,
       turtle_3x1_2_outplayershiftm, turtle_3x1_2_outputbackshiftm, turtle_3x1_3_outplayershiftm,
       turtle_3x1_3_outputbackshiftm, turtle_3x1_4_outplayershiftm, turtle_3x1_4_outputbackshiftm;
  wire [6:0] keyboard_1_data;
  wire [7:0] I_Odat;
  wire [14:0] lives_1_the_1_st_line_of_the_picture, lives_1_the_1_st_line_of_the_picture_2,
       lives_1_the_1_st_line_of_the_picture_3, lives_1_the_2_nd_line_of_the_picture,
       lives_1_the_2_nd_line_of_the_picture_2, lives_1_the_2_nd_line_of_the_picture_3,
       lives_1_the_3_rd_line_of_the_picture, lives_1_the_3_rd_line_of_the_picture_2,
       lives_1_the_3_rd_line_of_the_picture_3, lives_1_the_4_th_line_of_the_picture,
       lives_1_the_4_th_line_of_the_picture_2, lives_1_the_4_th_line_of_the_picture_3,
       lives_1_the_5_th_line_of_the_picture, lives_1_the_5_th_line_of_the_picture_2,
       lives_1_the_5_th_line_of_the_picture_3, lives_1_the_6_th_line_of_the_picture,
       lives_1_the_6_th_line_of_the_picture_2, lives_1_the_6_th_line_of_the_picture_3,
       lives_1_the_7_th_line_of_the_picture, lives_1_the_7_th_line_of_the_picture_2,
       lives_1_the_7_th_line_of_the_picture_3, lives_1_the_8_th_line_of_the_picture,
       lives_1_the_8_th_line_of_the_picture_2, lives_1_the_8_th_line_of_the_picture_3,
       lives_1_the_9_th_line_of_the_picture, lives_1_the_9_th_line_of_the_picture_2,
       lives_1_the_9_th_line_of_the_picture_3, lives_1_the_10_th_line_of_the_picture,
       lives_1_the_10_th_line_of_the_picture_2, lives_1_the_10_th_line_of_the_picture_3,
       lives_1_the_11_th_line_of_the_picture, lives_1_the_11_th_line_of_the_picture_2,
       lives_1_the_11_th_line_of_the_picture_3, lives_1_the_12_th_line_of_the_picture,
       lives_1_the_12_th_line_of_the_picture_2, lives_1_the_12_th_line_of_the_picture_3,
       lives_1_the_13_th_line_of_the_picture, lives_1_the_13_th_line_of_the_picture_2,
       lives_1_the_13_th_line_of_the_picture_3, lives_1_the_14_th_line_of_the_picture,
       lives_1_the_14_th_line_of_the_picture_2, lives_1_the_14_th_line_of_the_picture_3,
       lives_1_the_15_th_line_of_the_picture, lives_1_the_15_th_line_of_the_picture_2,
       lives_1_the_15_th_line_of_the_picture_3;
  wire [19:0] digits_1_the_1_st_line_of_the_picture, digits_1_the_2_nd_line_of_the_picture,
       digits_1_the_3_rd_line_of_the_picture, digits_1_the_4_th_line_of_the_picture,
       digits_1_the_5_th_line_of_the_picture, digits_1_the_6_th_line_of_the_picture,
       digits_1_the_7_th_line_of_the_picture, digits_1_the_8_th_line_of_the_picture,
       digits_1_the_9_th_line_of_the_picture, digits_1_the_10_th_line_of_the_picture,
       digits_1_the_11_th_line_of_the_picture, digits_1_the_12_th_line_of_the_picture,
       digits_1_the_13_th_line_of_the_picture, digits_1_the_14_th_line_of_the_picture,
       digits_1_the_15_th_line_of_the_picture, digits_1_the_16_th_line_of_the_picture,
       digits_1_the_17_th_line_of_the_picture, digits_1_the_18_th_line_of_the_picture,
       digits_1_the_19_th_line_of_the_picture, digits_1_the_20_th_line_of_the_picture,
       digits_1_the_21_st_line_of_the_picture, digits_1_the_22_nd_line_of_the_picture,
       digits_1_the_23_rd_line_of_the_picture, digits_1_the_24_th_line_of_the_picture,
       digits_1_the_25_th_line_of_the_picture, digits_1_the_26_th_line_of_the_picture,
       digits_1_the_27_th_line_of_the_picture, digits_1_the_28_th_line_of_the_picture,
       digits_1_the_29_th_line_of_the_picture, digits_1_the_30_th_line_of_the_picture,
       digits_2_the_1_st_line_of_the_picture, digits_2_the_2_nd_line_of_the_picture,
       digits_2_the_3_rd_line_of_the_picture, digits_2_the_4_th_line_of_the_picture,
       digits_2_the_5_th_line_of_the_picture, digits_2_the_6_th_line_of_the_picture,
       digits_2_the_7_th_line_of_the_picture, digits_2_the_8_th_line_of_the_picture,
       digits_2_the_9_th_line_of_the_picture, digits_2_the_10_th_line_of_the_picture,
       digits_2_the_11_th_line_of_the_picture, digits_2_the_12_th_line_of_the_picture,
       digits_2_the_13_th_line_of_the_picture, digits_2_the_14_th_line_of_the_picture,
       digits_2_the_15_th_line_of_the_picture, digits_2_the_16_th_line_of_the_picture,
       digits_2_the_17_th_line_of_the_picture, digits_2_the_18_th_line_of_the_picture,
       digits_2_the_19_th_line_of_the_picture, digits_2_the_20_th_line_of_the_picture,
       digits_2_the_21_st_line_of_the_picture, digits_2_the_22_nd_line_of_the_picture,
       digits_2_the_23_rd_line_of_the_picture, digits_2_the_24_th_line_of_the_picture,
       digits_2_the_25_th_line_of_the_picture, digits_2_the_26_th_line_of_the_picture,
       digits_2_the_27_th_line_of_the_picture, digits_2_the_28_th_line_of_the_picture,
       digits_2_the_29_th_line_of_the_picture, digits_2_the_30_th_line_of_the_picture,
       digits_3_the_1_st_line_of_the_picture, digits_3_the_2_nd_line_of_the_picture,
       digits_3_the_3_rd_line_of_the_picture, digits_3_the_4_th_line_of_the_picture,
       digits_3_the_5_th_line_of_the_picture, digits_3_the_6_th_line_of_the_picture,
       digits_3_the_7_th_line_of_the_picture, digits_3_the_8_th_line_of_the_picture,
       digits_3_the_9_th_line_of_the_picture, digits_3_the_10_th_line_of_the_picture,
       digits_3_the_11_th_line_of_the_picture, digits_3_the_12_th_line_of_the_picture,
       digits_3_the_13_th_line_of_the_picture, digits_3_the_14_th_line_of_the_picture,
       digits_3_the_15_th_line_of_the_picture, digits_3_the_16_th_line_of_the_picture,
       digits_3_the_17_th_line_of_the_picture, digits_3_the_18_th_line_of_the_picture,
       digits_3_the_19_th_line_of_the_picture, digits_3_the_20_th_line_of_the_picture,
       digits_3_the_21_st_line_of_the_picture, digits_3_the_22_nd_line_of_the_picture,
       digits_3_the_23_rd_line_of_the_picture, digits_3_the_24_th_line_of_the_picture,
       digits_3_the_25_th_line_of_the_picture, digits_3_the_26_th_line_of_the_picture,
       digits_3_the_27_th_line_of_the_picture, digits_3_the_28_th_line_of_the_picture,
       digits_3_the_29_th_line_of_the_picture, digits_3_the_30_th_line_of_the_picture,
       digits_4_the_1_st_line_of_the_picture, digits_4_the_2_nd_line_of_the_picture,
       digits_4_the_3_rd_line_of_the_picture, digits_4_the_4_th_line_of_the_picture,
       digits_4_the_5_th_line_of_the_picture, digits_4_the_6_th_line_of_the_picture,
       digits_4_the_7_th_line_of_the_picture, digits_4_the_8_th_line_of_the_picture,
       digits_4_the_9_th_line_of_the_picture, digits_4_the_10_th_line_of_the_picture,
       digits_4_the_11_th_line_of_the_picture, digits_4_the_12_th_line_of_the_picture,
       digits_4_the_13_th_line_of_the_picture, digits_4_the_14_th_line_of_the_picture,
       digits_4_the_15_th_line_of_the_picture, digits_4_the_16_th_line_of_the_picture,
       digits_4_the_17_th_line_of_the_picture, digits_4_the_18_th_line_of_the_picture,
       digits_4_the_19_th_line_of_the_picture, digits_4_the_20_th_line_of_the_picture,
       digits_4_the_21_st_line_of_the_picture, digits_4_the_22_nd_line_of_the_picture,
       digits_4_the_23_rd_line_of_the_picture, digits_4_the_24_th_line_of_the_picture,
       digits_4_the_25_th_line_of_the_picture, digits_4_the_26_th_line_of_the_picture,
       digits_4_the_27_th_line_of_the_picture, digits_4_the_28_th_line_of_the_picture,
       digits_4_the_29_th_line_of_the_picture, digits_4_the_30_th_line_of_the_picture,
       digits_5_the_1_st_line_of_the_picture, digits_5_the_2_nd_line_of_the_picture,
       digits_5_the_3_rd_line_of_the_picture, digits_5_the_4_th_line_of_the_picture,
       digits_5_the_5_th_line_of_the_picture, digits_5_the_6_th_line_of_the_picture,
       digits_5_the_7_th_line_of_the_picture, digits_5_the_8_th_line_of_the_picture,
       digits_5_the_9_th_line_of_the_picture, digits_5_the_10_th_line_of_the_picture,
       digits_5_the_11_th_line_of_the_picture, digits_5_the_12_th_line_of_the_picture,
       digits_5_the_13_th_line_of_the_picture, digits_5_the_14_th_line_of_the_picture,
       digits_5_the_15_th_line_of_the_picture, digits_5_the_16_th_line_of_the_picture,
       digits_5_the_17_th_line_of_the_picture, digits_5_the_18_th_line_of_the_picture,
       digits_5_the_19_th_line_of_the_picture, digits_5_the_20_th_line_of_the_picture,
       digits_5_the_21_st_line_of_the_picture, digits_5_the_22_nd_line_of_the_picture,
       digits_5_the_23_rd_line_of_the_picture, digits_5_the_24_th_line_of_the_picture,
       digits_5_the_25_th_line_of_the_picture, digits_5_the_26_th_line_of_the_picture,
       digits_5_the_27_th_line_of_the_picture, digits_5_the_28_th_line_of_the_picture,
       digits_5_the_29_th_line_of_the_picture, digits_5_the_30_th_line_of_the_picture,
       digits_6_the_1_st_line_of_the_picture, digits_6_the_2_nd_line_of_the_picture,
       digits_6_the_3_rd_line_of_the_picture, digits_6_the_4_th_line_of_the_picture,
       digits_6_the_5_th_line_of_the_picture, digits_6_the_6_th_line_of_the_picture,
       digits_6_the_7_th_line_of_the_picture, digits_6_the_8_th_line_of_the_picture,
       digits_6_the_9_th_line_of_the_picture, digits_6_the_10_th_line_of_the_picture,
       digits_6_the_11_th_line_of_the_picture, digits_6_the_12_th_line_of_the_picture,
       digits_6_the_13_th_line_of_the_picture, digits_6_the_14_th_line_of_the_picture,
       digits_6_the_15_th_line_of_the_picture, digits_6_the_16_th_line_of_the_picture,
       digits_6_the_17_th_line_of_the_picture, digits_6_the_18_th_line_of_the_picture,
       digits_6_the_19_th_line_of_the_picture, digits_6_the_20_th_line_of_the_picture,
       digits_6_the_21_st_line_of_the_picture, digits_6_the_22_nd_line_of_the_picture,
       digits_6_the_23_rd_line_of_the_picture, digits_6_the_24_th_line_of_the_picture,
       digits_6_the_25_th_line_of_the_picture, digits_6_the_26_th_line_of_the_picture,
       digits_6_the_27_th_line_of_the_picture, digits_6_the_28_th_line_of_the_picture,
       digits_6_the_29_th_line_of_the_picture, digits_6_the_30_th_line_of_the_picture,
       digits_7_the_1_st_line_of_the_picture, digits_7_the_2_nd_line_of_the_picture,
       digits_7_the_3_rd_line_of_the_picture, digits_7_the_4_th_line_of_the_picture,
       digits_7_the_5_th_line_of_the_picture, digits_7_the_6_th_line_of_the_picture,
       digits_7_the_7_th_line_of_the_picture, digits_7_the_8_th_line_of_the_picture,
       digits_7_the_9_th_line_of_the_picture, digits_7_the_10_th_line_of_the_picture,
       digits_7_the_11_th_line_of_the_picture, digits_7_the_12_th_line_of_the_picture,
       digits_7_the_13_th_line_of_the_picture, digits_7_the_14_th_line_of_the_picture,
       digits_7_the_15_th_line_of_the_picture, digits_7_the_16_th_line_of_the_picture,
       digits_7_the_17_th_line_of_the_picture, digits_7_the_18_th_line_of_the_picture,
       digits_7_the_19_th_line_of_the_picture, digits_7_the_20_th_line_of_the_picture,
       digits_7_the_21_st_line_of_the_picture, digits_7_the_22_nd_line_of_the_picture,
       digits_7_the_23_rd_line_of_the_picture, digits_7_the_24_th_line_of_the_picture,
       digits_7_the_25_th_line_of_the_picture, digits_7_the_26_th_line_of_the_picture,
       digits_7_the_27_th_line_of_the_picture, digits_7_the_28_th_line_of_the_picture,
       digits_7_the_29_th_line_of_the_picture, digits_7_the_30_th_line_of_the_picture,
       digits_8_the_1_st_line_of_the_picture, digits_8_the_2_nd_line_of_the_picture,
       digits_8_the_3_rd_line_of_the_picture, digits_8_the_4_th_line_of_the_picture,
       digits_8_the_5_th_line_of_the_picture, digits_8_the_6_th_line_of_the_picture,
       digits_8_the_7_th_line_of_the_picture, digits_8_the_8_th_line_of_the_picture,
       digits_8_the_9_th_line_of_the_picture, digits_8_the_10_th_line_of_the_picture,
       digits_8_the_11_th_line_of_the_picture, digits_8_the_12_th_line_of_the_picture,
       digits_8_the_13_th_line_of_the_picture, digits_8_the_14_th_line_of_the_picture,
       digits_8_the_15_th_line_of_the_picture, digits_8_the_16_th_line_of_the_picture,
       digits_8_the_17_th_line_of_the_picture, digits_8_the_18_th_line_of_the_picture,
       digits_8_the_19_th_line_of_the_picture, digits_8_the_20_th_line_of_the_picture,
       digits_8_the_21_st_line_of_the_picture, digits_8_the_22_nd_line_of_the_picture,
       digits_8_the_23_rd_line_of_the_picture, digits_8_the_24_th_line_of_the_picture,
       digits_8_the_25_th_line_of_the_picture, digits_8_the_26_th_line_of_the_picture,
       digits_8_the_27_th_line_of_the_picture, digits_8_the_28_th_line_of_the_picture,
       digits_8_the_29_th_line_of_the_picture, digits_8_the_30_th_line_of_the_picture,
       digits_9_the_1_st_line_of_the_picture, digits_9_the_2_nd_line_of_the_picture,
       digits_9_the_3_rd_line_of_the_picture, digits_9_the_4_th_line_of_the_picture,
       digits_9_the_5_th_line_of_the_picture, digits_9_the_6_th_line_of_the_picture,
       digits_9_the_7_th_line_of_the_picture, digits_9_the_8_th_line_of_the_picture,
       digits_9_the_9_th_line_of_the_picture, digits_9_the_10_th_line_of_the_picture,
       digits_9_the_11_th_line_of_the_picture, digits_9_the_12_th_line_of_the_picture,
       digits_9_the_13_th_line_of_the_picture, digits_9_the_14_th_line_of_the_picture,
       digits_9_the_15_th_line_of_the_picture, digits_9_the_16_th_line_of_the_picture,
       digits_9_the_17_th_line_of_the_picture, digits_9_the_18_th_line_of_the_picture,
       digits_9_the_19_th_line_of_the_picture, digits_9_the_20_th_line_of_the_picture,
       digits_9_the_21_st_line_of_the_picture, digits_9_the_22_nd_line_of_the_picture,
       digits_9_the_23_rd_line_of_the_picture, digits_9_the_24_th_line_of_the_picture,
       digits_9_the_25_th_line_of_the_picture, digits_9_the_26_th_line_of_the_picture,
       digits_9_the_27_th_line_of_the_picture, digits_9_the_28_th_line_of_the_picture,
       digits_9_the_29_th_line_of_the_picture, digits_9_the_30_th_line_of_the_picture,
       digits_10_the_1_st_line_of_the_picture, digits_10_the_2_nd_line_of_the_picture,
       digits_10_the_3_rd_line_of_the_picture, digits_10_the_4_th_line_of_the_picture,
       digits_10_the_5_th_line_of_the_picture, digits_10_the_6_th_line_of_the_picture,
       digits_10_the_7_th_line_of_the_picture, digits_10_the_8_th_line_of_the_picture,
       digits_10_the_9_th_line_of_the_picture, digits_10_the_10_th_line_of_the_picture,
       digits_10_the_11_th_line_of_the_picture, digits_10_the_12_th_line_of_the_picture,
       digits_10_the_13_th_line_of_the_picture, digits_10_the_14_th_line_of_the_picture,
       digits_10_the_15_th_line_of_the_picture, digits_10_the_16_th_line_of_the_picture,
       digits_10_the_17_th_line_of_the_picture, digits_10_the_18_th_line_of_the_picture,
       digits_10_the_19_th_line_of_the_picture, digits_10_the_20_th_line_of_the_picture,
       digits_10_the_21_st_line_of_the_picture, digits_10_the_22_nd_line_of_the_picture,
       digits_10_the_23_rd_line_of_the_picture, digits_10_the_24_th_line_of_the_picture,
       digits_10_the_25_th_line_of_the_picture, digits_10_the_26_th_line_of_the_picture,
       digits_10_the_27_th_line_of_the_picture, digits_10_the_28_th_line_of_the_picture,
       digits_10_the_29_th_line_of_the_picture, digits_10_the_30_th_line_of_the_picture;
  wire [26:0] number_of_saved_frogs_victory_lose_1_the_1_st_line_of_the_picture,
       number_of_saved_frogs_victory_lose_1_the_2_nd_line_of_the_picture,
       number_of_saved_frogs_victory_lose_1_the_3_rd_line_of_the_picture,
       number_of_saved_frogs_victory_lose_1_the_4_th_line_of_the_picture,
       number_of_saved_frogs_victory_lose_1_the_5_th_line_of_the_picture,
       number_of_saved_frogs_victory_lose_1_the_6_th_line_of_the_picture,
       number_of_saved_frogs_victory_lose_1_the_7_th_line_of_the_picture,
       number_of_saved_frogs_victory_lose_1_the_8_th_line_of_the_picture,
       number_of_saved_frogs_victory_lose_1_the_9_th_line_of_the_picture,
       number_of_saved_frogs_victory_lose_1_the_10_th_line_of_the_picture,
       number_of_saved_frogs_victory_lose_1_the_11_th_line_of_the_picture,
       number_of_saved_frogs_victory_lose_1_the_12_th_line_of_the_picture,
       number_of_saved_frogs_victory_lose_1_the_13_th_line_of_the_picture,
       number_of_saved_frogs_victory_lose_1_the_14_th_line_of_the_picture,
       number_of_saved_frogs_victory_lose_1_the_15_th_line_of_the_picture,
       number_of_saved_frogs_victory_lose_1_the_16_th_line_of_the_picture,
       number_of_saved_frogs_victory_lose_1_the_17_th_line_of_the_picture,
       number_of_saved_frogs_victory_lose_1_the_18_th_line_of_the_picture,
       number_of_saved_frogs_victory_lose_1_the_19_th_line_of_the_picture,
       number_of_saved_frogs_victory_lose_1_the_20_th_line_of_the_picture,
       number_of_saved_frogs_victory_lose_1_the_21_st_line_of_the_picture,
       number_of_saved_frogs_victory_lose_1_the_22_nd_line_of_the_picture,
       number_of_saved_frogs_victory_lose_1_the_23_rd_line_of_the_picture;
  wire [29:0] boliddriver_1_tobackground, boliddriver_1_tobackground_2, boliddriver_1_tobackground_3,
       boliddriver_1_tobackground_4, boliddriver_1_tobackground_5, boliddriver_1_tobackground_6,
       boliddriver_1_tobackground_7, boliddriver_1_tobackground_8, boliddriver_1_tobackground_9,
       boliddriver_1_tobackground_10, boliddriver_1_tofront, boliddriver_1_tofront_2,
       boliddriver_1_tofront_3, boliddriver_1_tofront_4, boliddriver_1_tofront_5, boliddriver_1_tofront_6,
       boliddriver_1_tofront_7, boliddriver_1_tofront_8, boliddriver_1_tofront_9, boliddriver_1_tofront_10,
       boliddriver_2_tobackground, boliddriver_2_tobackground_2, boliddriver_2_tobackground_3,
       boliddriver_2_tobackground_4, boliddriver_2_tobackground_5, boliddriver_2_tobackground_6,
       boliddriver_2_tobackground_7, boliddriver_2_tobackground_8, boliddriver_2_tobackground_9,
       boliddriver_2_tobackground_10, boliddriver_2_tofront, boliddriver_2_tofront_2,
       boliddriver_2_tofront_3, boliddriver_2_tofront_4, boliddriver_2_tofront_5, boliddriver_2_tofront_6,
       boliddriver_2_tofront_7, boliddriver_2_tofront_8, boliddriver_2_tofront_9, boliddriver_2_tofront_10,
       boliddriver_3_tobackground, boliddriver_3_tobackground_2, boliddriver_3_tobackground_3,
       boliddriver_3_tobackground_4, boliddriver_3_tobackground_5, boliddriver_3_tobackground_6,
       boliddriver_3_tobackground_7, boliddriver_3_tobackground_8, boliddriver_3_tobackground_9,
       boliddriver_3_tobackground_10, boliddriver_3_tofront, boliddriver_3_tofront_2,
       boliddriver_3_tofront_3, boliddriver_3_tofront_4, boliddriver_3_tofront_5, boliddriver_3_tofront_6,
       boliddriver_3_tofront_7, boliddriver_3_tofront_8, boliddriver_3_tofront_9, boliddriver_3_tofront_10,
       boliddriver_4_tobackground, boliddriver_4_tobackground_2, boliddriver_4_tobackground_3,
       boliddriver_4_tobackground_4, boliddriver_4_tobackground_5, boliddriver_4_tobackground_6,
       boliddriver_4_tobackground_7, boliddriver_4_tobackground_8, boliddriver_4_tobackground_9,
       boliddriver_4_tobackground_10, boliddriver_4_tofront, boliddriver_4_tofront_2,
       boliddriver_4_tofront_3, boliddriver_4_tofront_4, boliddriver_4_tofront_5, boliddriver_4_tofront_6,
       boliddriver_4_tofront_7, boliddriver_4_tofront_8, boliddriver_4_tofront_9, boliddriver_4_tofront_10,
       carconnectorv2_1_tobackground, carconnectorv2_1_tobackground_2, carconnectorv2_1_tobackground_3,
       carconnectorv2_1_tobackground_4, carconnectorv2_1_tobackground_5, carconnectorv2_1_tobackground_6,
       carconnectorv2_1_tobackground_7, carconnectorv2_1_tobackground_8, carconnectorv2_1_tobackground_9,
       carconnectorv2_1_tobackground_10, carconnectorv2_1_tofront, carconnectorv2_1_tofront_2,
       carconnectorv2_1_tofront_3, carconnectorv2_1_tofront_4, carconnectorv2_1_tofront_5,
       carconnectorv2_1_tofront_6, carconnectorv2_1_tofront_7, carconnectorv2_1_tofront_8,
       carconnectorv2_1_tofront_9, carconnectorv2_1_tofront_10, carconnectorv2_2_tobackground,
       carconnectorv2_2_tobackground_2, carconnectorv2_2_tobackground_3, carconnectorv2_2_tobackground_4,
       carconnectorv2_2_tobackground_5, carconnectorv2_2_tobackground_6, carconnectorv2_2_tobackground_7,
       carconnectorv2_2_tobackground_8, carconnectorv2_2_tobackground_9, carconnectorv2_2_tobackground_10,
       carconnectorv2_2_tofront, carconnectorv2_2_tofront_2, carconnectorv2_2_tofront_3,
       carconnectorv2_2_tofront_4, carconnectorv2_2_tofront_5, carconnectorv2_2_tofront_6,
       carconnectorv2_2_tofront_7, carconnectorv2_2_tofront_8, carconnectorv2_2_tofront_9,
       carconnectorv2_2_tofront_10, carconnectorv2_3_tobackground, carconnectorv2_3_tobackground_2,
       carconnectorv2_3_tobackground_3, carconnectorv2_3_tobackground_4, carconnectorv2_3_tobackground_5,
       carconnectorv2_3_tobackground_6, carconnectorv2_3_tobackground_7, carconnectorv2_3_tobackground_8,
       carconnectorv2_3_tobackground_9, carconnectorv2_3_tobackground_10, carconnectorv2_3_tofront,
       carconnectorv2_3_tofront_2, carconnectorv2_3_tofront_3, carconnectorv2_3_tofront_4,
       carconnectorv2_3_tofront_5, carconnectorv2_3_tofront_6, carconnectorv2_3_tofront_7,
       carconnectorv2_3_tofront_8, carconnectorv2_3_tofront_9, carconnectorv2_3_tofront_10,
       carconnectorv2_4_tobackground, carconnectorv2_4_tobackground_2, carconnectorv2_4_tobackground_3,
       carconnectorv2_4_tobackground_4, carconnectorv2_4_tobackground_5, carconnectorv2_4_tobackground_6,
       carconnectorv2_4_tobackground_7, carconnectorv2_4_tobackground_8, carconnectorv2_4_tobackground_9,
       carconnectorv2_4_tobackground_10, carconnectorv2_4_tofront, carconnectorv2_4_tofront_2,
       carconnectorv2_4_tofront_3, carconnectorv2_4_tofront_4, carconnectorv2_4_tofront_5,
       carconnectorv2_4_tofront_6, carconnectorv2_4_tofront_7, carconnectorv2_4_tofront_8,
       carconnectorv2_4_tofront_9, carconnectorv2_4_tofront_10, finishconnector_1_tobackground,
       finishconnector_1_tobackground_2, finishconnector_1_tobackground_3, finishconnector_1_tobackground_4,
       finishconnector_1_tobackground_5, finishconnector_1_tobackground_6, finishconnector_1_tobackground_7,
       finishconnector_1_tobackground_8, finishconnector_1_tobackground_9, finishconnector_1_tobackground_10,
       finishconnector_1_tobackground_11, finishconnector_1_tobackground_12, finishconnector_2_tobackground,
       finishconnector_2_tobackground_2, finishconnector_2_tobackground_3, finishconnector_2_tobackground_4,
       finishconnector_2_tobackground_5, finishconnector_2_tobackground_6, finishconnector_2_tobackground_7,
       finishconnector_2_tobackground_8, finishconnector_2_tobackground_9, finishconnector_2_tobackground_10,
       finishconnector_2_tobackground_11, finishconnector_2_tobackground_12, finishconnector_3_tobackground,
       finishconnector_3_tobackground_2, finishconnector_3_tobackground_3, finishconnector_3_tobackground_4,
       finishconnector_3_tobackground_5, finishconnector_3_tobackground_6, finishconnector_3_tobackground_7,
       finishconnector_3_tobackground_8, finishconnector_3_tobackground_9, finishconnector_3_tobackground_10,
       finishconnector_3_tobackground_11, finishconnector_3_tobackground_12, finishconnector_4_tobackground,
       finishconnector_4_tobackground_2, finishconnector_4_tobackground_3, finishconnector_4_tobackground_4,
       finishconnector_4_tobackground_5, finishconnector_4_tobackground_6, finishconnector_4_tobackground_7,
       finishconnector_4_tobackground_8, finishconnector_4_tobackground_9, finishconnector_4_tobackground_10,
       finishconnector_4_tobackground_11, finishconnector_4_tobackground_12, log_1x1_1_tobackground,
       log_1x1_1_tobackground_2, log_1x1_1_tobackground_3, log_1x1_1_tobackground_4,
       log_1x1_1_tobackground_5, log_1x1_1_tobackground_6, log_1x1_1_tobackground_7,
       log_1x1_1_tobackground_8, log_1x1_1_tobackground_9, log_1x1_1_tobackground_10, log_1x1_1_tofront,
       log_1x1_1_tofront_2, log_1x1_1_tofront_3, log_1x1_1_tofront_4, log_1x1_1_tofront_5,
       log_1x1_1_tofront_6, log_1x1_1_tofront_7, log_1x1_1_tofront_8, log_1x1_1_tofront_9,
       log_1x1_1_tofront_10, log_1x1_2_tobackground, log_1x1_2_tobackground_2, log_1x1_2_tobackground_3,
       log_1x1_2_tobackground_4, log_1x1_2_tobackground_5, log_1x1_2_tobackground_6,
       log_1x1_2_tobackground_7, log_1x1_2_tobackground_8, log_1x1_2_tobackground_9,
       log_1x1_2_tobackground_10, log_1x1_2_tofront, log_1x1_2_tofront_2, log_1x1_2_tofront_3,
       log_1x1_2_tofront_4, log_1x1_2_tofront_5, log_1x1_2_tofront_6, log_1x1_2_tofront_7,
       log_1x1_2_tofront_8, log_1x1_2_tofront_9, log_1x1_2_tofront_10, log_1x1_3_tobackground,
       log_1x1_3_tobackground_2, log_1x1_3_tobackground_3, log_1x1_3_tobackground_4,
       log_1x1_3_tobackground_5, log_1x1_3_tobackground_6, log_1x1_3_tobackground_7,
       log_1x1_3_tobackground_8, log_1x1_3_tobackground_9, log_1x1_3_tobackground_10, log_1x1_3_tofront,
       log_1x1_3_tofront_2, log_1x1_3_tofront_3, log_1x1_3_tofront_4, log_1x1_3_tofront_5,
       log_1x1_3_tofront_6, log_1x1_3_tofront_7, log_1x1_3_tofront_8, log_1x1_3_tofront_9,
       log_1x1_3_tofront_10, log_1x1_4_tobackground, log_1x1_4_tobackground_2, log_1x1_4_tobackground_3,
       log_1x1_4_tobackground_4, log_1x1_4_tobackground_5, log_1x1_4_tobackground_6,
       log_1x1_4_tobackground_7, log_1x1_4_tobackground_8, log_1x1_4_tobackground_9,
       log_1x1_4_tobackground_10, log_1x1_4_tofront, log_1x1_4_tofront_2, log_1x1_4_tofront_3,
       log_1x1_4_tofront_4, log_1x1_4_tofront_5, log_1x1_4_tofront_6, log_1x1_4_tofront_7,
       log_1x1_4_tofront_8, log_1x1_4_tofront_9, log_1x1_4_tofront_10, log_2x1_1_tobackground,
       log_2x1_1_tobackground_2, log_2x1_1_tobackground_3, log_2x1_1_tobackground_4,
       log_2x1_1_tobackground_5, log_2x1_1_tobackground_6, log_2x1_1_tobackground_7,
       log_2x1_1_tobackground_8, log_2x1_1_tobackground_9, log_2x1_1_tobackground_10, log_2x1_1_tofront,
       log_2x1_1_tofront_2, log_2x1_1_tofront_3, log_2x1_1_tofront_4, log_2x1_1_tofront_5,
       log_2x1_1_tofront_6, log_2x1_1_tofront_7, log_2x1_1_tofront_8, log_2x1_1_tofront_9,
       log_2x1_1_tofront_10, log_2x1_2_tobackground, log_2x1_2_tobackground_2, log_2x1_2_tobackground_3,
       log_2x1_2_tobackground_4, log_2x1_2_tobackground_5, log_2x1_2_tobackground_6,
       log_2x1_2_tobackground_7, log_2x1_2_tobackground_8, log_2x1_2_tobackground_9,
       log_2x1_2_tobackground_10, log_2x1_2_tofront, log_2x1_2_tofront_2, log_2x1_2_tofront_3,
       log_2x1_2_tofront_4, log_2x1_2_tofront_5, log_2x1_2_tofront_6, log_2x1_2_tofront_7,
       log_2x1_2_tofront_8, log_2x1_2_tofront_9, log_2x1_2_tofront_10, log_2x1_3_tobackground,
       log_2x1_3_tobackground_2, log_2x1_3_tobackground_3, log_2x1_3_tobackground_4,
       log_2x1_3_tobackground_5, log_2x1_3_tobackground_6, log_2x1_3_tobackground_7,
       log_2x1_3_tobackground_8, log_2x1_3_tobackground_9, log_2x1_3_tobackground_10, log_2x1_3_tofront,
       log_2x1_3_tofront_2, log_2x1_3_tofront_3, log_2x1_3_tofront_4, log_2x1_3_tofront_5,
       log_2x1_3_tofront_6, log_2x1_3_tofront_7, log_2x1_3_tofront_8, log_2x1_3_tofront_9,
       log_2x1_3_tofront_10, log_2x1_4_tobackground, log_2x1_4_tobackground_2, log_2x1_4_tobackground_3,
       log_2x1_4_tobackground_4, log_2x1_4_tobackground_5, log_2x1_4_tobackground_6,
       log_2x1_4_tobackground_7, log_2x1_4_tobackground_8, log_2x1_4_tobackground_9,
       log_2x1_4_tobackground_10, log_2x1_4_tofront, log_2x1_4_tofront_2, log_2x1_4_tofront_3,
       log_2x1_4_tofront_4, log_2x1_4_tofront_5, log_2x1_4_tofront_6, log_2x1_4_tofront_7,
       log_2x1_4_tofront_8, log_2x1_4_tofront_9, log_2x1_4_tofront_10, log_3x2_1_tobackground,
       log_3x2_1_tobackground_2, log_3x2_1_tobackground_3, log_3x2_1_tobackground_4,
       log_3x2_1_tobackground_5, log_3x2_1_tobackground_6, log_3x2_1_tobackground_7,
       log_3x2_1_tobackground_8, log_3x2_1_tobackground_9, log_3x2_1_tobackground_10, log_3x2_1_tofront,
       log_3x2_1_tofront_2, log_3x2_1_tofront_3, log_3x2_1_tofront_4, log_3x2_1_tofront_5,
       log_3x2_1_tofront_6, log_3x2_1_tofront_7, log_3x2_1_tofront_8, log_3x2_1_tofront_9,
       log_3x2_1_tofront_10, log_3x2_2_tobackground, log_3x2_2_tobackground_2, log_3x2_2_tobackground_3,
       log_3x2_2_tobackground_4, log_3x2_2_tobackground_5, log_3x2_2_tobackground_6,
       log_3x2_2_tobackground_7, log_3x2_2_tobackground_8, log_3x2_2_tobackground_9,
       log_3x2_2_tobackground_10, log_3x2_2_tofront, log_3x2_2_tofront_2, log_3x2_2_tofront_3,
       log_3x2_2_tofront_4, log_3x2_2_tofront_5, log_3x2_2_tofront_6, log_3x2_2_tofront_7,
       log_3x2_2_tofront_8, log_3x2_2_tofront_9, log_3x2_2_tofront_10, log_3x2_3_tobackground,
       log_3x2_3_tobackground_2, log_3x2_3_tobackground_3, log_3x2_3_tobackground_4,
       log_3x2_3_tobackground_5, log_3x2_3_tobackground_6, log_3x2_3_tobackground_7,
       log_3x2_3_tobackground_8, log_3x2_3_tobackground_9, log_3x2_3_tobackground_10, log_3x2_3_tofront,
       log_3x2_3_tofront_2, log_3x2_3_tofront_3, log_3x2_3_tofront_4, log_3x2_3_tofront_5,
       log_3x2_3_tofront_6, log_3x2_3_tofront_7, log_3x2_3_tofront_8, log_3x2_3_tofront_9,
       log_3x2_3_tofront_10, log_3x2_4_tobackground, log_3x2_4_tobackground_2, log_3x2_4_tobackground_3,
       log_3x2_4_tobackground_4, log_3x2_4_tobackground_5, log_3x2_4_tobackground_6,
       log_3x2_4_tobackground_7, log_3x2_4_tobackground_8, log_3x2_4_tobackground_9,
       log_3x2_4_tobackground_10, log_3x2_4_tofront, log_3x2_4_tofront_2, log_3x2_4_tofront_3,
       log_3x2_4_tofront_4, log_3x2_4_tofront_5, log_3x2_4_tofront_6, log_3x2_4_tofront_7,
       log_3x2_4_tofront_8, log_3x2_4_tofront_9, log_3x2_4_tofront_10, suvdriver_1_tobackground,
       suvdriver_1_tobackground_2, suvdriver_1_tobackground_3, suvdriver_1_tobackground_4,
       suvdriver_1_tobackground_5, suvdriver_1_tobackground_6, suvdriver_1_tobackground_7,
       suvdriver_1_tobackground_8, suvdriver_1_tobackground_9, suvdriver_1_tobackground_10,
       suvdriver_1_tofront, suvdriver_1_tofront_2, suvdriver_1_tofront_3, suvdriver_1_tofront_4,
       suvdriver_1_tofront_5, suvdriver_1_tofront_6, suvdriver_1_tofront_7, suvdriver_1_tofront_8,
       suvdriver_1_tofront_9, suvdriver_1_tofront_10, suvdriver_2_tobackground, suvdriver_2_tobackground_2,
       suvdriver_2_tobackground_3, suvdriver_2_tobackground_4, suvdriver_2_tobackground_5,
       suvdriver_2_tobackground_6, suvdriver_2_tobackground_7, suvdriver_2_tobackground_8,
       suvdriver_2_tobackground_9, suvdriver_2_tobackground_10, suvdriver_2_tofront, suvdriver_2_tofront_2,
       suvdriver_2_tofront_3, suvdriver_2_tofront_4, suvdriver_2_tofront_5, suvdriver_2_tofront_6,
       suvdriver_2_tofront_7, suvdriver_2_tofront_8, suvdriver_2_tofront_9, suvdriver_2_tofront_10,
       suvdriver_3_tobackground, suvdriver_3_tobackground_2, suvdriver_3_tobackground_3,
       suvdriver_3_tobackground_4, suvdriver_3_tobackground_5, suvdriver_3_tobackground_6,
       suvdriver_3_tobackground_7, suvdriver_3_tobackground_8, suvdriver_3_tobackground_9,
       suvdriver_3_tobackground_10, suvdriver_3_tofront, suvdriver_3_tofront_2, suvdriver_3_tofront_3,
       suvdriver_3_tofront_4, suvdriver_3_tofront_5, suvdriver_3_tofront_6, suvdriver_3_tofront_7,
       suvdriver_3_tofront_8, suvdriver_3_tofront_9, suvdriver_3_tofront_10, suvdriver_4_tobackground,
       suvdriver_4_tobackground_2, suvdriver_4_tobackground_3, suvdriver_4_tobackground_4,
       suvdriver_4_tobackground_5, suvdriver_4_tobackground_6, suvdriver_4_tobackground_7,
       suvdriver_4_tobackground_8, suvdriver_4_tobackground_9, suvdriver_4_tobackground_10,
       suvdriver_4_tofront, suvdriver_4_tofront_2, suvdriver_4_tofront_3, suvdriver_4_tofront_4,
       suvdriver_4_tofront_5, suvdriver_4_tofront_6, suvdriver_4_tofront_7, suvdriver_4_tofront_8,
       suvdriver_4_tofront_9, suvdriver_4_tofront_10, swampdriver_1_p6, swampdriver_1_p7, swampdriver_1_p8,
       swampdriver_1_p9, swampdriver_1_p10, swampdriver_1_p11, swampdriver_1_p12, swampdriver_1_p13,
       swampdriver_1_p14, swampdriver_1_p15, swampdriver_1_p16, swampdriver_1_p17, swampdriver_1_p18,
       swampdriver_1_p19, swampdriver_1_p20, swampdriver_1_p21, swampdriver_1_p22, swampdriver_1_p23,
       swampdriver_1_p24, swampdriver_1_p25, swampdriver_2_p4, swampdriver_2_p5, swampdriver_2_p6,
       swampdriver_2_p7, swampdriver_2_p8, swampdriver_2_p9, swampdriver_2_p10, swampdriver_2_p11,
       swampdriver_2_p12, swampdriver_2_p13, swampdriver_2_p14, swampdriver_2_p15, swampdriver_2_p16,
       swampdriver_2_p17, swampdriver_2_p18, swampdriver_2_p19, swampdriver_2_p20, swampdriver_2_p21,
       swampdriver_2_p22, swampdriver_2_p23, swampdriver_3_p6, swampdriver_3_p7, swampdriver_3_p8,
       swampdriver_3_p9, swampdriver_3_p10, swampdriver_3_p11, swampdriver_3_p12, swampdriver_3_p13,
       swampdriver_3_p14, swampdriver_3_p15, swampdriver_3_p16, swampdriver_3_p17, swampdriver_3_p18,
       swampdriver_3_p19, swampdriver_3_p20, swampdriver_3_p21, swampdriver_3_p22, swampdriver_3_p23,
       swampdriver_3_p24, swampdriver_3_p25, swampdriver_4_p6, swampdriver_4_p7, swampdriver_4_p8,
       swampdriver_4_p9, swampdriver_4_p10, swampdriver_4_p11, swampdriver_4_p12, swampdriver_4_p13,
       swampdriver_4_p14, swampdriver_4_p15, swampdriver_4_p16, swampdriver_4_p17, swampdriver_4_p18,
       swampdriver_4_p19, swampdriver_4_p20, swampdriver_4_p21, swampdriver_4_p22, swampdriver_4_p23,
       swampdriver_4_p24, swampdriver_4_p25, swampdriver_5_p7, swampdriver_5_p8, swampdriver_5_p9,
       swampdriver_5_p10, swampdriver_5_p11, swampdriver_5_p12, swampdriver_5_p13, swampdriver_5_p14,
       swampdriver_5_p15, swampdriver_5_p16, swampdriver_5_p17, swampdriver_5_p18, swampdriver_5_p19,
       swampdriver_5_p20, swampdriver_5_p21, swampdriver_5_p22, swampdriver_5_p23, swampdriver_5_p24,
       swampdriver_5_p25, swampdriver_5_p26, swampdriver_6_p6, swampdriver_6_p7, swampdriver_6_p8,
       swampdriver_6_p9, swampdriver_6_p10, swampdriver_6_p11, swampdriver_6_p12, swampdriver_6_p13,
       swampdriver_6_p14, swampdriver_6_p15, swampdriver_6_p16, swampdriver_6_p17, swampdriver_6_p18,
       swampdriver_6_p19, swampdriver_6_p20, swampdriver_6_p21, swampdriver_6_p22, swampdriver_6_p23,
       swampdriver_6_p24, swampdriver_6_p25, swampdriver_7_p6, swampdriver_7_p7, swampdriver_7_p8,
       swampdriver_7_p9, swampdriver_7_p10, swampdriver_7_p11, swampdriver_7_p12, swampdriver_7_p13,
       swampdriver_7_p14, swampdriver_7_p15, swampdriver_7_p16, swampdriver_7_p17, swampdriver_7_p18,
       swampdriver_7_p19, swampdriver_7_p20, swampdriver_7_p21, swampdriver_7_p22, swampdriver_7_p23,
       swampdriver_7_p24, swampdriver_7_p25, swampdriver_8_p6, swampdriver_8_p7, swampdriver_8_p8,
       swampdriver_8_p9, swampdriver_8_p10, swampdriver_8_p11, swampdriver_8_p12, swampdriver_8_p13,
       swampdriver_8_p14, swampdriver_8_p15, swampdriver_8_p16, swampdriver_8_p17, swampdriver_8_p18,
       swampdriver_8_p19, swampdriver_8_p20, swampdriver_8_p21, swampdriver_8_p22, swampdriver_8_p23,
       swampdriver_8_p24, swampdriver_8_p25, truckdriver_1_tobackground, truckdriver_1_tobackground_2,
       truckdriver_1_tobackground_3, truckdriver_1_tobackground_4, truckdriver_1_tobackground_5,
       truckdriver_1_tobackground_6, truckdriver_1_tobackground_7, truckdriver_1_tobackground_8,
       truckdriver_1_tobackground_9, truckdriver_1_tobackground_10, truckdriver_1_tofront,
       truckdriver_1_tofront_2, truckdriver_1_tofront_3, truckdriver_1_tofront_4, truckdriver_1_tofront_5,
       truckdriver_1_tofront_6, truckdriver_1_tofront_7, truckdriver_1_tofront_8, truckdriver_1_tofront_9,
       truckdriver_1_tofront_10, truckdriver_2_tobackground, truckdriver_2_tobackground_2,
       truckdriver_2_tobackground_3, truckdriver_2_tobackground_4, truckdriver_2_tobackground_5,
       truckdriver_2_tobackground_6, truckdriver_2_tobackground_7, truckdriver_2_tobackground_8,
       truckdriver_2_tobackground_9, truckdriver_2_tobackground_10, truckdriver_2_tofront,
       truckdriver_2_tofront_2, truckdriver_2_tofront_3, truckdriver_2_tofront_4, truckdriver_2_tofront_5,
       truckdriver_2_tofront_6, truckdriver_2_tofront_7, truckdriver_2_tofront_8, truckdriver_2_tofront_9,
       truckdriver_2_tofront_10, truckdriver_3_tobackground, truckdriver_3_tobackground_2,
       truckdriver_3_tobackground_3, truckdriver_3_tobackground_4, truckdriver_3_tobackground_5,
       truckdriver_3_tobackground_6, truckdriver_3_tobackground_7, truckdriver_3_tobackground_8,
       truckdriver_3_tobackground_9, truckdriver_3_tobackground_10, truckdriver_3_tofront,
       truckdriver_3_tofront_2, truckdriver_3_tofront_3, truckdriver_3_tofront_4, truckdriver_3_tofront_5,
       truckdriver_3_tofront_6, truckdriver_3_tofront_7, truckdriver_3_tofront_8, truckdriver_3_tofront_9,
       truckdriver_3_tofront_10, truckdriver_4_tobackground, truckdriver_4_tobackground_2,
       truckdriver_4_tobackground_3, truckdriver_4_tobackground_4, truckdriver_4_tobackground_5,
       truckdriver_4_tobackground_6, truckdriver_4_tobackground_7, truckdriver_4_tobackground_8,
       truckdriver_4_tobackground_9, truckdriver_4_tobackground_10, truckdriver_4_tofront,
       truckdriver_4_tofront_2, truckdriver_4_tofront_3, truckdriver_4_tofront_4, truckdriver_4_tofront_5,
       truckdriver_4_tofront_6, truckdriver_4_tofront_7, truckdriver_4_tofront_8, truckdriver_4_tofront_9,
       truckdriver_4_tofront_10, truckdriver_5_tobackground, truckdriver_5_tobackground_2,
       truckdriver_5_tobackground_3, truckdriver_5_tobackground_4, truckdriver_5_tobackground_5,
       truckdriver_5_tobackground_6, truckdriver_5_tobackground_7, truckdriver_5_tobackground_8,
       truckdriver_5_tobackground_9, truckdriver_5_tobackground_10, truckdriver_5_tofront,
       truckdriver_5_tofront_2, truckdriver_5_tofront_3, truckdriver_5_tofront_4, truckdriver_5_tofront_5,
       truckdriver_5_tofront_6, truckdriver_5_tofront_7, truckdriver_5_tofront_8, truckdriver_5_tofront_9,
       truckdriver_5_tofront_10, truckdriver_6_tobackground, truckdriver_6_tobackground_2,
       truckdriver_6_tobackground_3, truckdriver_6_tobackground_4, truckdriver_6_tobackground_5,
       truckdriver_6_tobackground_6, truckdriver_6_tobackground_7, truckdriver_6_tobackground_8,
       truckdriver_6_tobackground_9, truckdriver_6_tobackground_10, truckdriver_6_tofront,
       truckdriver_6_tofront_2, truckdriver_6_tofront_3, truckdriver_6_tofront_4, truckdriver_6_tofront_5,
       truckdriver_6_tofront_6, truckdriver_6_tofront_7, truckdriver_6_tofront_8, truckdriver_6_tofront_9,
       truckdriver_6_tofront_10, truckdriver_7_tobackground, truckdriver_7_tobackground_2,
       truckdriver_7_tobackground_3, truckdriver_7_tobackground_4, truckdriver_7_tobackground_5,
       truckdriver_7_tobackground_6, truckdriver_7_tobackground_7, truckdriver_7_tobackground_8,
       truckdriver_7_tobackground_9, truckdriver_7_tobackground_10, truckdriver_7_tofront,
       truckdriver_7_tofront_2, truckdriver_7_tofront_3, truckdriver_7_tofront_4, truckdriver_7_tofront_5,
       truckdriver_7_tofront_6, truckdriver_7_tofront_7, truckdriver_7_tofront_8, truckdriver_7_tofront_9,
       truckdriver_7_tofront_10, truckdriver_8_tobackground, truckdriver_8_tobackground_2,
       truckdriver_8_tobackground_3, truckdriver_8_tobackground_4, truckdriver_8_tobackground_5,
       truckdriver_8_tobackground_6, truckdriver_8_tobackground_7, truckdriver_8_tobackground_8,
       truckdriver_8_tobackground_9, truckdriver_8_tobackground_10, truckdriver_8_tofront,
       truckdriver_8_tofront_2, truckdriver_8_tofront_3, truckdriver_8_tofront_4, truckdriver_8_tofront_5,
       truckdriver_8_tofront_6, truckdriver_8_tofront_7, truckdriver_8_tofront_8, truckdriver_8_tofront_9,
       truckdriver_8_tofront_10, turtle_2x1_1_tobackground, turtle_2x1_1_tobackground_2,
       turtle_2x1_1_tobackground_3, turtle_2x1_1_tobackground_4, turtle_2x1_1_tobackground_5,
       turtle_2x1_1_tobackground_6, turtle_2x1_1_tobackground_7, turtle_2x1_1_tobackground_8,
       turtle_2x1_1_tobackground_9, turtle_2x1_1_tobackground_10, turtle_2x1_1_tofront,
       turtle_2x1_1_tofront_2, turtle_2x1_1_tofront_3, turtle_2x1_1_tofront_4, turtle_2x1_1_tofront_5,
       turtle_2x1_1_tofront_6, turtle_2x1_1_tofront_7, turtle_2x1_1_tofront_8, turtle_2x1_1_tofront_9,
       turtle_2x1_1_tofront_10, turtle_2x1_2_tobackground, turtle_2x1_2_tobackground_2,
       turtle_2x1_2_tobackground_3, turtle_2x1_2_tobackground_4, turtle_2x1_2_tobackground_5,
       turtle_2x1_2_tobackground_6, turtle_2x1_2_tobackground_7, turtle_2x1_2_tobackground_8,
       turtle_2x1_2_tobackground_9, turtle_2x1_2_tobackground_10, turtle_2x1_2_tofront,
       turtle_2x1_2_tofront_2, turtle_2x1_2_tofront_3, turtle_2x1_2_tofront_4, turtle_2x1_2_tofront_5,
       turtle_2x1_2_tofront_6, turtle_2x1_2_tofront_7, turtle_2x1_2_tofront_8, turtle_2x1_2_tofront_9,
       turtle_2x1_2_tofront_10, turtle_2x1_3_tobackground, turtle_2x1_3_tobackground_2,
       turtle_2x1_3_tobackground_3, turtle_2x1_3_tobackground_4, turtle_2x1_3_tobackground_5,
       turtle_2x1_3_tobackground_6, turtle_2x1_3_tobackground_7, turtle_2x1_3_tobackground_8,
       turtle_2x1_3_tobackground_9, turtle_2x1_3_tobackground_10, turtle_2x1_3_tofront,
       turtle_2x1_3_tofront_2, turtle_2x1_3_tofront_3, turtle_2x1_3_tofront_4, turtle_2x1_3_tofront_5,
       turtle_2x1_3_tofront_6, turtle_2x1_3_tofront_7, turtle_2x1_3_tofront_8, turtle_2x1_3_tofront_9,
       turtle_2x1_3_tofront_10, turtle_2x1_4_tobackground, turtle_2x1_4_tobackground_2,
       turtle_2x1_4_tobackground_3, turtle_2x1_4_tobackground_4, turtle_2x1_4_tobackground_5,
       turtle_2x1_4_tobackground_6, turtle_2x1_4_tobackground_7, turtle_2x1_4_tobackground_8,
       turtle_2x1_4_tobackground_9, turtle_2x1_4_tobackground_10, turtle_2x1_4_tofront,
       turtle_2x1_4_tofront_2, turtle_2x1_4_tofront_3, turtle_2x1_4_tofront_4, turtle_2x1_4_tofront_5,
       turtle_2x1_4_tofront_6, turtle_2x1_4_tofront_7, turtle_2x1_4_tofront_8, turtle_2x1_4_tofront_9,
       turtle_2x1_4_tofront_10, turtle_3x1_1_tobackground, turtle_3x1_1_tobackground_2,
       turtle_3x1_1_tobackground_3, turtle_3x1_1_tobackground_4, turtle_3x1_1_tobackground_5,
       turtle_3x1_1_tobackground_6, turtle_3x1_1_tobackground_7, turtle_3x1_1_tobackground_8,
       turtle_3x1_1_tobackground_9, turtle_3x1_1_tobackground_10, turtle_3x1_1_tofront,
       turtle_3x1_1_tofront_2, turtle_3x1_1_tofront_3, turtle_3x1_1_tofront_4, turtle_3x1_1_tofront_5,
       turtle_3x1_1_tofront_6, turtle_3x1_1_tofront_7, turtle_3x1_1_tofront_8, turtle_3x1_1_tofront_9,
       turtle_3x1_1_tofront_10, turtle_3x1_2_tobackground, turtle_3x1_2_tobackground_2,
       turtle_3x1_2_tobackground_3, turtle_3x1_2_tobackground_4, turtle_3x1_2_tobackground_5,
       turtle_3x1_2_tobackground_6, turtle_3x1_2_tobackground_7, turtle_3x1_2_tobackground_8,
       turtle_3x1_2_tobackground_9, turtle_3x1_2_tobackground_10, turtle_3x1_2_tofront,
       turtle_3x1_2_tofront_2, turtle_3x1_2_tofront_3, turtle_3x1_2_tofront_4, turtle_3x1_2_tofront_5,
       turtle_3x1_2_tofront_6, turtle_3x1_2_tofront_7, turtle_3x1_2_tofront_8, turtle_3x1_2_tofront_9,
       turtle_3x1_2_tofront_10, turtle_3x1_3_tobackground, turtle_3x1_3_tobackground_2,
       turtle_3x1_3_tobackground_3, turtle_3x1_3_tobackground_4, turtle_3x1_3_tobackground_5,
       turtle_3x1_3_tobackground_6, turtle_3x1_3_tobackground_7, turtle_3x1_3_tobackground_8,
       turtle_3x1_3_tobackground_9, turtle_3x1_3_tobackground_10, turtle_3x1_3_tofront,
       turtle_3x1_3_tofront_2, turtle_3x1_3_tofront_3, turtle_3x1_3_tofront_4, turtle_3x1_3_tofront_5,
       turtle_3x1_3_tofront_6, turtle_3x1_3_tofront_7, turtle_3x1_3_tofront_8, turtle_3x1_3_tofront_9,
       turtle_3x1_3_tofront_10, turtle_3x1_4_tobackground, turtle_3x1_4_tobackground_2,
       turtle_3x1_4_tobackground_3, turtle_3x1_4_tobackground_4, turtle_3x1_4_tobackground_5,
       turtle_3x1_4_tobackground_6, turtle_3x1_4_tobackground_7, turtle_3x1_4_tobackground_8,
       turtle_3x1_4_tobackground_9, turtle_3x1_4_tobackground_10, turtle_3x1_4_tofront,
       turtle_3x1_4_tofront_2, turtle_3x1_4_tofront_3, turtle_3x1_4_tofront_4, turtle_3x1_4_tofront_5,
       turtle_3x1_4_tofront_6, turtle_3x1_4_tofront_7, turtle_3x1_4_tofront_8, turtle_3x1_4_tofront_9,
       turtle_3x1_4_tofront_10;
  wire [31:0] current_score_1_the_1_st_line_of_the_picture, current_score_1_the_1_st_line_of_the_picture_2,
       current_score_1_the_2_nd_line_of_the_picture, current_score_1_the_2_nd_line_of_the_picture_2,
       current_score_1_the_3_rd_line_of_the_picture, current_score_1_the_3_rd_line_of_the_picture_2,
       current_score_1_the_4_th_line_of_the_picture, current_score_1_the_4_th_line_of_the_picture_2,
       current_score_1_the_5_th_line_of_the_picture, current_score_1_the_5_th_line_of_the_picture_2,
       current_score_1_the_6_th_line_of_the_picture, current_score_1_the_6_th_line_of_the_picture_2,
       current_score_1_the_7_th_line_of_the_picture, current_score_1_the_7_th_line_of_the_picture_2,
       current_score_1_the_8_th_line_of_the_picture, current_score_1_the_8_th_line_of_the_picture_2,
       current_score_1_the_9_th_line_of_the_picture, current_score_1_the_9_th_line_of_the_picture_2,
       current_score_1_the_10_th_line_of_the_picture, current_score_1_the_10_th_line_of_the_picture_2,
       current_score_1_the_11_th_line_of_the_picture, current_score_1_the_11_th_line_of_the_picture_2,
       current_score_1_the_12_th_line_of_the_picture, current_score_1_the_12_th_line_of_the_picture_2,
       current_score_1_the_13_th_line_of_the_picture, current_score_1_the_13_th_line_of_the_picture_2,
       current_score_1_the_14_th_line_of_the_picture, current_score_1_the_14_th_line_of_the_picture_2,
       current_score_1_the_15_th_line_of_the_picture, current_score_1_the_15_th_line_of_the_picture_2,
       current_score_1_the_16_th_line_of_the_picture, current_score_1_the_16_th_line_of_the_picture_2,
       current_score_1_the_17_th_line_of_the_picture, current_score_1_the_17_th_line_of_the_picture_2,
       current_score_1_the_18_th_line_of_the_picture, current_score_1_the_18_th_line_of_the_picture_2,
       current_score_1_the_19_th_line_of_the_picture, current_score_1_the_19_th_line_of_the_picture_2,
       current_score_1_the_20_th_line_of_the_picture, current_score_1_the_20_th_line_of_the_picture_2,
       current_score_1_the_21_st_line_of_the_picture, current_score_1_the_21_st_line_of_the_picture_2,
       current_score_1_the_22_nd_line_of_the_picture, current_score_1_the_22_nd_line_of_the_picture_2,
       current_score_1_the_23_rd_line_of_the_picture, current_score_1_the_23_rd_line_of_the_picture_2,
       current_score_1_the_24_th_line_of_the_picture, current_score_1_the_24_th_line_of_the_picture_2,
       current_score_1_the_25_th_line_of_the_picture, current_score_1_the_25_th_line_of_the_picture_2,
       current_score_1_the_26_th_line_of_the_picture, current_score_1_the_26_th_line_of_the_picture_2,
       current_score_1_the_27_th_line_of_the_picture, current_score_1_the_27_th_line_of_the_picture_2,
       current_score_1_the_28_th_line_of_the_picture, current_score_1_the_28_th_line_of_the_picture_2,
       current_score_1_the_29_th_line_of_the_picture, current_score_1_the_29_th_line_of_the_picture_2,
       current_score_1_the_30_th_line_of_the_picture, current_score_1_the_30_th_line_of_the_picture_2,
       current_score_1_the_31_st_line_of_the_picture, current_score_1_the_31_st_line_of_the_picture_2,
       current_score_1_the_32_nd_line_of_the_picture, current_score_1_the_32_nd_line_of_the_picture_2,
       lives_1_the_1_st_line_of_the_picture_4, lives_1_the_2_nd_line_of_the_picture_4,
       lives_1_the_3_rd_line_of_the_picture_4, lives_1_the_4_th_line_of_the_picture_4,
       lives_1_the_5_th_line_of_the_picture_4, lives_1_the_6_th_line_of_the_picture_4,
       lives_1_the_7_th_line_of_the_picture_4, lives_1_the_8_th_line_of_the_picture_4,
       lives_1_the_9_th_line_of_the_picture_4, lives_1_the_10_th_line_of_the_picture_4,
       lives_1_the_11_th_line_of_the_picture_4, lives_1_the_12_th_line_of_the_picture_4,
       lives_1_the_13_th_line_of_the_picture_4, lives_1_the_14_th_line_of_the_picture_4,
       lives_1_the_15_th_line_of_the_picture_4, lives_1_the_16_th_line_of_the_picture,
       lives_1_the_17_th_line_of_the_picture, lives_1_the_18_th_line_of_the_picture,
       lives_1_the_19_th_line_of_the_picture, lives_1_the_20_th_line_of_the_picture,
       lives_1_the_21_st_line_of_the_picture, lives_1_the_22_nd_line_of_the_picture,
       lives_1_the_23_rd_line_of_the_picture, lives_1_the_24_th_line_of_the_picture,
       lives_1_the_25_th_line_of_the_picture, lives_1_the_26_th_line_of_the_picture,
       lives_1_the_27_th_line_of_the_picture, lives_1_the_28_th_line_of_the_picture,
       lives_1_the_29_th_line_of_the_picture, lives_1_the_30_th_line_of_the_picture,
       lives_1_the_31_st_line_of_the_picture, lives_1_the_32_nd_line_of_the_picture,
       record_score_1_the_1_st_line_of_the_picture, record_score_1_the_1_st_line_of_the_picture_2,
       record_score_1_the_2_nd_line_of_the_picture, record_score_1_the_2_nd_line_of_the_picture_2,
       record_score_1_the_3_rd_line_of_the_picture, record_score_1_the_3_rd_line_of_the_picture_2,
       record_score_1_the_4_th_line_of_the_picture, record_score_1_the_4_th_line_of_the_picture_2,
       record_score_1_the_5_th_line_of_the_picture, record_score_1_the_5_th_line_of_the_picture_2,
       record_score_1_the_6_th_line_of_the_picture, record_score_1_the_6_th_line_of_the_picture_2,
       record_score_1_the_7_th_line_of_the_picture, record_score_1_the_7_th_line_of_the_picture_2,
       record_score_1_the_8_th_line_of_the_picture, record_score_1_the_8_th_line_of_the_picture_2,
       record_score_1_the_9_th_line_of_the_picture, record_score_1_the_9_th_line_of_the_picture_2,
       record_score_1_the_10_th_line_of_the_picture, record_score_1_the_10_th_line_of_the_picture_2,
       record_score_1_the_11_th_line_of_the_picture, record_score_1_the_11_th_line_of_the_picture_2,
       record_score_1_the_12_th_line_of_the_picture, record_score_1_the_12_th_line_of_the_picture_2,
       record_score_1_the_13_th_line_of_the_picture, record_score_1_the_13_th_line_of_the_picture_2,
       record_score_1_the_14_th_line_of_the_picture, record_score_1_the_14_th_line_of_the_picture_2,
       record_score_1_the_15_th_line_of_the_picture, record_score_1_the_15_th_line_of_the_picture_2,
       record_score_1_the_16_th_line_of_the_picture, record_score_1_the_16_th_line_of_the_picture_2,
       record_score_1_the_17_th_line_of_the_picture, record_score_1_the_17_th_line_of_the_picture_2,
       record_score_1_the_18_th_line_of_the_picture, record_score_1_the_18_th_line_of_the_picture_2,
       record_score_1_the_19_th_line_of_the_picture, record_score_1_the_19_th_line_of_the_picture_2,
       record_score_1_the_20_th_line_of_the_picture, record_score_1_the_20_th_line_of_the_picture_2,
       record_score_1_the_21_st_line_of_the_picture, record_score_1_the_21_st_line_of_the_picture_2,
       record_score_1_the_22_nd_line_of_the_picture, record_score_1_the_22_nd_line_of_the_picture_2,
       record_score_1_the_23_rd_line_of_the_picture, record_score_1_the_23_rd_line_of_the_picture_2,
       record_score_1_the_24_th_line_of_the_picture, record_score_1_the_24_th_line_of_the_picture_2,
       record_score_1_the_25_th_line_of_the_picture, record_score_1_the_25_th_line_of_the_picture_2,
       record_score_1_the_26_th_line_of_the_picture, record_score_1_the_26_th_line_of_the_picture_2,
       record_score_1_the_27_th_line_of_the_picture, record_score_1_the_27_th_line_of_the_picture_2,
       record_score_1_the_28_th_line_of_the_picture, record_score_1_the_28_th_line_of_the_picture_2,
       record_score_1_the_29_th_line_of_the_picture, record_score_1_the_29_th_line_of_the_picture_2,
       record_score_1_the_30_th_line_of_the_picture, record_score_1_the_30_th_line_of_the_picture_2,
       record_score_1_the_31_st_line_of_the_picture, record_score_1_the_31_st_line_of_the_picture_2,
       record_score_1_the_32_nd_line_of_the_picture, record_score_1_the_32_nd_line_of_the_picture_2,
       timer_1_the_1_st_line_of_the_picture, timer_1_the_1_st_line_of_the_picture_2,
       timer_1_the_1_st_line_of_the_picture_3, timer_1_the_1_st_line_of_the_picture_4,
       timer_1_the_2_nd_line_of_the_picture, timer_1_the_2_nd_line_of_the_picture_2,
       timer_1_the_2_nd_line_of_the_picture_3, timer_1_the_2_nd_line_of_the_picture_4,
       timer_1_the_3_rd_line_of_the_picture, timer_1_the_3_rd_line_of_the_picture_2,
       timer_1_the_3_rd_line_of_the_picture_3, timer_1_the_3_rd_line_of_the_picture_4,
       timer_1_the_4_th_line_of_the_picture, timer_1_the_4_th_line_of_the_picture_2,
       timer_1_the_4_th_line_of_the_picture_3, timer_1_the_4_th_line_of_the_picture_4,
       timer_1_the_5_th_line_of_the_picture, timer_1_the_5_th_line_of_the_picture_2,
       timer_1_the_5_th_line_of_the_picture_3, timer_1_the_5_th_line_of_the_picture_4,
       timer_1_the_6_th_line_of_the_picture, timer_1_the_6_th_line_of_the_picture_2,
       timer_1_the_6_th_line_of_the_picture_3, timer_1_the_6_th_line_of_the_picture_4,
       timer_1_the_7_th_line_of_the_picture, timer_1_the_7_th_line_of_the_picture_2,
       timer_1_the_7_th_line_of_the_picture_3, timer_1_the_7_th_line_of_the_picture_4,
       timer_1_the_8_th_line_of_the_picture, timer_1_the_8_th_line_of_the_picture_2,
       timer_1_the_8_th_line_of_the_picture_3, timer_1_the_8_th_line_of_the_picture_4,
       timer_1_the_9_th_line_of_the_picture, timer_1_the_9_th_line_of_the_picture_2,
       timer_1_the_9_th_line_of_the_picture_3, timer_1_the_9_th_line_of_the_picture_4,
       timer_1_the_10_th_line_of_the_picture, timer_1_the_10_th_line_of_the_picture_2,
       timer_1_the_10_th_line_of_the_picture_3, timer_1_the_10_th_line_of_the_picture_4,
       timer_1_the_11_th_line_of_the_picture, timer_1_the_11_th_line_of_the_picture_2,
       timer_1_the_11_th_line_of_the_picture_3, timer_1_the_11_th_line_of_the_picture_4,
       timer_1_the_12_th_line_of_the_picture, timer_1_the_12_th_line_of_the_picture_2,
       timer_1_the_12_th_line_of_the_picture_3, timer_1_the_12_th_line_of_the_picture_4,
       timer_1_the_13_th_line_of_the_picture, timer_1_the_13_th_line_of_the_picture_2,
       timer_1_the_13_th_line_of_the_picture_3, timer_1_the_13_th_line_of_the_picture_4,
       timer_1_the_14_th_line_of_the_picture, timer_1_the_14_th_line_of_the_picture_2,
       timer_1_the_14_th_line_of_the_picture_3, timer_1_the_14_th_line_of_the_picture_4,
       timer_1_the_15_th_line_of_the_picture, timer_1_the_15_th_line_of_the_picture_2,
       timer_1_the_15_th_line_of_the_picture_3, timer_1_the_15_th_line_of_the_picture_4,
       timer_1_the_16_th_line_of_the_picture, timer_1_the_16_th_line_of_the_picture_2,
       timer_1_the_16_th_line_of_the_picture_3, timer_1_the_16_th_line_of_the_picture_4,
       timer_1_the_17_th_line_of_the_picture, timer_1_the_17_th_line_of_the_picture_2,
       timer_1_the_17_th_line_of_the_picture_3, timer_1_the_17_th_line_of_the_picture_4,
       timer_1_the_18_th_line_of_the_picture, timer_1_the_18_th_line_of_the_picture_2,
       timer_1_the_18_th_line_of_the_picture_3, timer_1_the_18_th_line_of_the_picture_4,
       timer_1_the_19_th_line_of_the_picture, timer_1_the_19_th_line_of_the_picture_2,
       timer_1_the_19_th_line_of_the_picture_3, timer_1_the_19_th_line_of_the_picture_4,
       timer_1_the_20_th_line_of_the_picture, timer_1_the_20_th_line_of_the_picture_2,
       timer_1_the_20_th_line_of_the_picture_3, timer_1_the_20_th_line_of_the_picture_4,
       timer_1_the_21_st_line_of_the_picture, timer_1_the_21_st_line_of_the_picture_2,
       timer_1_the_22_nd_line_of_the_picture, timer_1_the_22_nd_line_of_the_picture_2,
       timer_1_the_23_rd_line_of_the_picture, timer_1_the_23_rd_line_of_the_picture_2,
       timer_1_the_24_th_line_of_the_picture, timer_1_the_24_th_line_of_the_picture_2,
       timer_1_the_25_th_line_of_the_picture, timer_1_the_25_th_line_of_the_picture_2,
       timer_1_the_26_th_line_of_the_picture, timer_1_the_26_th_line_of_the_picture_2,
       timer_1_the_27_th_line_of_the_picture, timer_1_the_27_th_line_of_the_picture_2,
       timer_1_the_28_th_line_of_the_picture, timer_1_the_28_th_line_of_the_picture_2,
       timer_1_the_29_th_line_of_the_picture, timer_1_the_29_th_line_of_the_picture_2,
       timer_1_the_30_th_line_of_the_picture, timer_1_the_30_th_line_of_the_picture_2,
       timer_1_the_31_st_line_of_the_picture, timer_1_the_31_st_line_of_the_picture_2,
       timer_1_the_32_nd_line_of_the_picture, timer_1_the_32_nd_line_of_the_picture_2,
       timer_1_time_flow__time_shift____left, timer_1_time_flow__time_shift____right;

  assign rKB = rightshifter_1_rkb | rightshifter_2_rkb | rightshifter_3_p1;  // OR_Gate or_1, 3 bits wide
  assign lKB = leftshifter_1_keyborder | leftshifter_2_keyborder;  // OR_Gate or_2, 3 bits wide
  Pull_Resistor pull_resistor_1 (.node(pull_resistor_1_node));
  assign pull_resistor_1_node = not_1_out ? level_clock : 1'bz;  // Controlled_Buffer controlled_buffer_1
  tact_by_level tact_by_level_1 (.new_level(rescue), .tact(clock), .tact_by_level(level_clock), .clear(restartGame));
  Clock clock_1 (.out(clock));
  Keyboard keyboard_1 (.clk(clock), .re(s_r_ff_1_qn), .clr(or_3_out), .data(keyboard_1_data));  // open: avail
  or or_3 (or_3_out, s_r_ff_1_q, restartGame);
  S_R_Flip_Flop s_r_ff_1 (
    .clk(clock), .Q(s_r_ff_1_q), .Qn(s_r_ff_1_qn), .preset(stop), .reset(restartGame));  // open: S, R, en
  or or_4 (bump, keyboard_2_p2, time_is_gone, intersection);
  rightShifter rightshifter_1 (
    .shiftM(rightshifter_1_shiftm), .shiftD(rightshifter_1_shiftd), .shiftCounts(2'b01),
    .tactGen(pull_resistor_1_node), .reset(intersection), .startShift(2'b00), .rKB(rightshifter_1_rkb),
    .isSameLvl(_11));
  leftShifter leftshifter_1 (
    .shiftD(leftshifter_1_shiftd), .shiftCounts(3'b001), .shiftM(leftshifter_1_shiftm),
    .tactGen(pull_resistor_1_node), .reset(intersection), .startShift(2'b00),
    .keyBorder(leftshifter_1_keyborder), .isSameLvl(_10));
  rightShifter rightshifter_2 (
    .shiftM(rightshifter_2_shiftm), .shiftD(rightshifter_2_shiftd), .shiftCounts(2'b00),
    .tactGen(pull_resistor_1_node), .reset(intersection), .startShift(2'b00), .rKB(rightshifter_2_rkb),
    .isSameLvl(_9));
  // rightShifter rightshifter_3: pin names not known; wires that end beside it: rightshifter_3_p1, 2'b00, 2'b10, rightshifter_3_p4, {5{1'b0}}, pull_resistor_1_node, rightshifter_3_p7, intersection, _8
  leftShifter leftshifter_2 (
    .shiftD(leftshifter_2_shiftd), .shiftCounts(3'b000), .shiftM(leftshifter_2_shiftm),
    .tactGen(pull_resistor_1_node), .reset(intersection), .startShift(2'b00),
    .keyBorder(leftshifter_2_keyborder), .isSameLvl(_7));
  leftShifter leftshifter_3 (
    .shiftD(leftshifter_3_shiftd), .shiftCounts(3'b000), .shiftM(leftshifter_3_shiftm),
    .tactGen(pull_resistor_1_node), .reset(intersection), .startShift(2'b10), .isSameLvl(_5));  // open: keyBorder
  rightShifter rightshifter_4 (
    .shiftM(rightshifter_4_shiftm), .shiftD(rightshifter_4_shiftd), .shiftCounts(2'b00),
    .tactGen(pull_resistor_1_node), .reset(intersection), .startShift(2'b00), .isSameLvl(_4));  // open: rKB
  leftShifter leftshifter_4 (
    .shiftD(leftshifter_4_shiftd), .shiftCounts(3'b010), .shiftM(leftshifter_4_shiftm),
    .tactGen(pull_resistor_1_node), .reset(intersection), .startShift(2'b00), .isSameLvl(_3));  // open: keyBorder
  rightShifter rightshifter_5 (
    .shiftM(rightshifter_5_shiftm), .shiftD(rightshifter_5_shiftd), .shiftCounts(2'b00),
    .tactGen(pull_resistor_1_node), .reset(intersection), .startShift(2'b10), .isSameLvl(_2));  // open: rKB
  leftShifter leftshifter_5 (
    .shiftD(leftshifter_5_shiftd), .shiftCounts(3'b000), .shiftM(leftshifter_5_shiftm),
    .tactGen(pull_resistor_1_node), .reset(intersection), .startShift(2'b00), .isSameLvl(_1));  // open: keyBorder
  not not_1 (not_1_out, stop);
  stopGame stopgame_1 (.tact(level_clock), .\event (\event ), .stopper(stop), .restart(restartGame));
  Button u_stop (.out(stop_out));
  finishComputer finishcomputer_1 (
    .res(restartGame), .playerD(keyboard_2_p9), .isSameLvl(_12), .playerM(keyboard_2_p8), .win(win),
    .positions(finishcomputer_1_positions), .ok(rescue), .die(finishcomputer_1_die));
  waterIntersect waterintersect_1 (
    .backLen(5'b10001), .inBackM(rightshifter_1_shiftm), .inBackD(rightshifter_1_shiftd),
    .inFrogM(keyboard_2_p8), .inFrogD(keyboard_2_p9), .inIntersect(finishcomputer_1_die), .doIntersect(_11),
    .outIntersect(waterintersect_1_outintersect), .tact(pull_resistor_1_node), .\event (pull_resistor_1_node));  // open: A
  _2_1turtlesIntersector u_2_1turtlesintersector_1 (
    .backLen(5'b10000), .inBackM(leftshifter_1_shiftm), .inFrogM(keyboard_2_p8), .doIntersect(_10),
    .\event (pull_resistor_1_node), .tact(pull_resistor_1_node),
    .outIntersect(n2_1turtlesintersector_1_outintersect), .animState(n2_1turtlesintersector_1_animstate),
    .tic(pull_resistor_1_node), .res(res), .animState_2(_1bAnim), .inIntersect(waterintersect_1_outintersect));  // open: A
  waterIntersect waterintersect_2 (
    .backLen(5'b11001), .inBackM(rightshifter_2_shiftm), .inBackD(rightshifter_2_shiftd),
    .inFrogM(keyboard_2_p8), .inFrogD(keyboard_2_p9), .inIntersect(n2_1turtlesintersector_1_outintersect),
    .doIntersect(_9), .outIntersect(waterintersect_2_outintersect), .tact(pull_resistor_1_node),
    .\event (pull_resistor_1_node));  // open: A
  smallLogIntersect smalllogintersect_1 (
    .backLen(5'b00111), .inBackM(rightshifter_3_p4), .inFrogM(keyboard_2_p8),
    .inIntersect(waterintersect_2_outintersect), .doIntersect(_8),
    .outIntersect(smalllogintersect_1_outintersect));
  waterIntersect waterintersect_3 (
    .backLen(5'b11110), .inBackM(leftshifter_2_shiftm), .inBackD(leftshifter_2_shiftd),
    .inFrogM(keyboard_2_p8), .inFrogD(keyboard_2_p9), .inIntersect(smalllogintersect_1_outintersect),
    .doIntersect(_7), .outIntersect(waterintersect_3_outintersect), .tact(pull_resistor_1_node),
    .\event (pull_resistor_1_node));  // open: A
  computeIntresection computeintresection_1 (
    .backLen(5'b10100), .inBackM(leftshifter_3_shiftm), .inBackD(leftshifter_3_shiftd),
    .inFrogD(keyboard_2_p9), .outIntersect(computeintresection_1_outintersect), .inFrogM(keyboard_2_p8),
    .inIntersect(waterintersect_3_outintersect), .doCompute(_5));
  computeIntresection computeintresection_2 (
    .backLen(5'b01010), .inBackM(rightshifter_4_shiftm), .inBackD(rightshifter_4_shiftd),
    .inFrogD(keyboard_2_p9), .outIntersect(computeintresection_2_outintersect), .inFrogM(keyboard_2_p8),
    .inIntersect(computeintresection_1_outintersect), .doCompute(_4));
  // Probe on leftshifter_4_shiftd
  // Probe on leftshifter_4_shiftm
  computeIntresection computeintresection_3 (
    .backLen(5'b10001), .inBackM(leftshifter_4_shiftm), .inBackD(leftshifter_4_shiftd),
    .inFrogD(keyboard_2_p9), .outIntersect(computeintresection_3_outintersect), .inFrogM(keyboard_2_p8),
    .inIntersect(computeintresection_2_outintersect), .doCompute(_3));
  computeIntresection computeintresection_4 (
    .backLen(5'b01010), .inBackM(rightshifter_5_shiftm), .inBackD(rightshifter_5_shiftd),
    .inFrogD(keyboard_2_p9), .outIntersect(computeintresection_4_outintersect), .inFrogM(keyboard_2_p8),
    .inIntersect(computeintresection_3_outintersect), .doCompute(_2));
  computeIntresection computeintresection_5 (
    .backLen(5'b10100), .inBackM(leftshifter_5_shiftm), .inBackD(leftshifter_5_shiftd),
    .inFrogD(keyboard_2_p9), .outIntersect(intersection), .inFrogM(keyboard_2_p8),
    .inIntersect(computeintresection_4_outintersect), .doCompute(_1));
  Pull_Resistor pull_resistor_2 (.node(intersection));
  // Probe on Y
  // Probe on keyboard_2_p9
  // Probe on nothing
  // Probe on keyboard_2_p8
  // keyboard keyboard_2: pin names not known; wires that end beside it: keyboard_1_data, keyboard_2_p2, lKB, stop_out, res, rKB, Y, keyboard_2_p8, keyboard_2_p9
  heightFlag heightflag_1 (.height(4'b1100), .playerY(Y), .eqY(_12));
  heightFlag heightflag_2 (.height(4'b1011), .playerY(Y), .eqY(_11));
  heightFlag heightflag_3 (.height(4'b1010), .playerY(Y), .eqY(_10));
  heightFlag heightflag_4 (.height(4'b1001), .playerY(Y), .eqY(_9));
  heightFlag heightflag_5 (.height(4'b1000), .playerY(Y), .eqY(_8));
  heightFlag heightflag_6 (.height(4'b0111), .playerY(Y), .eqY(_7));
  // heightFlag heightflag_7: pin names not known; wires that end beside it: Y, 4'b0110, heightflag_7_p3, _6
  heightFlag heightflag_8 (.height(4'b0101), .playerY(Y), .eqY(_5));
  heightFlag heightflag_9 (.height(4'b0100), .playerY(Y), .eqY(_4));
  heightFlag heightflag_10 (.height(4'b0011), .playerY(Y), .eqY(_3));
  heightFlag heightflag_11 (.height(4'b0010), .playerY(Y), .eqY(_2));
  heightFlag heightflag_12 (.height(4'b0001), .playerY(Y), .eqY(_1));
  heightFlag heightflag_13 (.height(4'b0000), .playerY(Y), .eqY(_0));
  DotMatrix #(.inputtype("row"), .matrixcols(30), .matrixrows(12)) dotmatrix_1 (
    .row0(finishconnector_1_tobackground), .row1(finishconnector_1_tobackground_2),
    .row2(finishconnector_1_tobackground_3), .row3(finishconnector_1_tobackground_4),
    .row4(finishconnector_1_tobackground_5), .row5(finishconnector_1_tobackground_6),
    .row6(finishconnector_1_tobackground_7), .row7(finishconnector_1_tobackground_8),
    .row8(finishconnector_1_tobackground_9), .row9(finishconnector_1_tobackground_10),
    .row10(finishconnector_1_tobackground_11), .row11(finishconnector_1_tobackground_12));
  finishConnector finishconnector_1 (
    .toBackground_3(finishconnector_1_tobackground_3), .toBackground_4(finishconnector_1_tobackground_4),
    .toBackground_5(finishconnector_1_tobackground_5), .toBackground_6(finishconnector_1_tobackground_6),
    .toBackground_7(finishconnector_1_tobackground_7), .toBackground_8(finishconnector_1_tobackground_8),
    .toBackground_9(finishconnector_1_tobackground_9), .toBackground_10(finishconnector_1_tobackground_10),
    .toBackground_11(finishconnector_1_tobackground_11), .toBackground_12(finishconnector_1_tobackground_12),
    .toBackground_2(finishconnector_1_tobackground_2), .toBackground(finishconnector_1_tobackground),
    .positions_2(finishconnector_1_positions_2), .circNumber_2(finishconnector_1_circnumber_2),
    .positions(finishcomputer_1_positions), .circNumber(2'b00));
  log_2x1 log_2x1_1 (
    .inBackShiftD(rightshifter_1_shiftd), .outBackShiftD(log_2x1_1_outbackshiftd),
    .inputBackShiftM(rightshifter_1_shiftm), .outputBackShiftM(log_2x1_1_outputbackshiftm),
    .inPlayerShiftD(keyboard_2_p9), .outPlayerShiftD(log_2x1_1_outplayershiftd),
    .inPlayerShiftM(keyboard_2_p8), .outPlayerShiftM(log_2x1_1_outplayershiftm), .inFlag(_11),
    .outFlag(log_2x1_1_outflag), .toBackground(log_2x1_1_tobackground),
    .toBackground_2(log_2x1_1_tobackground_2), .toBackground_3(log_2x1_1_tobackground_3),
    .toBackground_4(log_2x1_1_tobackground_4), .toBackground_5(log_2x1_1_tobackground_5),
    .toBackground_6(log_2x1_1_tobackground_6), .toBackground_7(log_2x1_1_tobackground_7),
    .toBackground_8(log_2x1_1_tobackground_8), .toBackground_9(log_2x1_1_tobackground_9),
    .toBackground_10(log_2x1_1_tobackground_10), .toFront(log_2x1_1_tofront),
    .toFront_2(log_2x1_1_tofront_2), .toFront_3(log_2x1_1_tofront_3), .toFront_4(log_2x1_1_tofront_4),
    .toFront_5(log_2x1_1_tofront_5), .toFront_6(log_2x1_1_tofront_6), .toFront_7(log_2x1_1_tofront_7),
    .toFront_8(log_2x1_1_tofront_8), .toFront_9(log_2x1_1_tofront_9), .toFront_10(log_2x1_1_tofront_10));
  DotMatrix #(.inputtype("row"), .matrixcols(30), .matrixrows(10)) dotmatrix_2 (
    .row0(log_2x1_1_tofront), .row1(log_2x1_1_tofront_2), .row2(log_2x1_1_tofront_3),
    .row3(log_2x1_1_tofront_4), .row4(log_2x1_1_tofront_5), .row5(log_2x1_1_tofront_6),
    .row6(log_2x1_1_tofront_7), .row7(log_2x1_1_tofront_8), .row8(log_2x1_1_tofront_9),
    .row9(log_2x1_1_tofront_10));
  DotMatrix #(.inputtype("row"), .matrixcols(30), .matrixrows(3)) dotmatrix_3 (
    .row0(log_2x1_1_tobackground), .row1(log_2x1_1_tobackground_2), .row2(log_2x1_1_tobackground_3));
  DotMatrix #(.inputtype("row"), .matrixcols(30), .matrixrows(4)) dotmatrix_4 (
    .row0(log_2x1_1_tobackground_4), .row1(log_2x1_1_tobackground_5), .row2(log_2x1_1_tobackground_6),
    .row3(log_2x1_1_tobackground_7));
  DotMatrix #(.inputtype("row"), .matrixcols(30), .matrixrows(3)) dotmatrix_5 (
    .row0(log_2x1_1_tobackground_8), .row1(log_2x1_1_tobackground_9), .row2(log_2x1_1_tobackground_10));
  DotMatrix #(.inputtype("row"), .matrixcols(30), .matrixrows(10)) dotmatrix_6 (
    .row0(turtle_2x1_1_tofront), .row1(turtle_2x1_1_tofront_2), .row2(turtle_2x1_1_tofront_3),
    .row3(turtle_2x1_1_tofront_4), .row4(turtle_2x1_1_tofront_5), .row5(turtle_2x1_1_tofront_6),
    .row6(turtle_2x1_1_tofront_7), .row7(turtle_2x1_1_tofront_8), .row8(turtle_2x1_1_tofront_9),
    .row9(turtle_2x1_1_tofront_10));
  DotMatrix #(.inputtype("row"), .matrixcols(30), .matrixrows(2)) dotmatrix_7 (
    .row0(turtle_2x1_1_tobackground), .row1(turtle_2x1_1_tobackground_2));
  turtle_2x1 turtle_2x1_1 (
    .inPlayerShiftD(keyboard_2_p9), .outPlayerShiftD(turtle_2x1_1_outplayershiftd),
    .inPlayerShiftM(keyboard_2_p8), .outPlayerShiftM(turtle_2x1_1_outplayershiftm), .inFlag(_10),
    .outFlag(turtle_2x1_1_outflag), .toBackground(turtle_2x1_1_tobackground),
    .toBackground_2(turtle_2x1_1_tobackground_2), .toBackground_3(turtle_2x1_1_tobackground_3),
    .toBackground_4(turtle_2x1_1_tobackground_4), .toBackground_5(turtle_2x1_1_tobackground_5),
    .toBackground_6(turtle_2x1_1_tobackground_6), .toBackground_7(turtle_2x1_1_tobackground_7),
    .toBackground_8(turtle_2x1_1_tobackground_8), .toBackground_9(turtle_2x1_1_tobackground_9),
    .toBackground_10(turtle_2x1_1_tobackground_10), .toFront(turtle_2x1_1_tofront),
    .toFront_2(turtle_2x1_1_tofront_2), .toFront_3(turtle_2x1_1_tofront_3),
    .toFront_4(turtle_2x1_1_tofront_4), .toFront_5(turtle_2x1_1_tofront_5),
    .toFront_6(turtle_2x1_1_tofront_6), .toFront_7(turtle_2x1_1_tofront_7),
    .toFront_8(turtle_2x1_1_tofront_8), .toFront_9(turtle_2x1_1_tofront_9),
    .toFront_10(turtle_2x1_1_tofront_10), .inBackShiftD(leftshifter_1_shiftd),
    .outBackShiftD(turtle_2x1_1_outbackshiftd), .inputBackShiftM(leftshifter_1_shiftm),
    .outputBackShiftM(turtle_2x1_1_outputbackshiftm), .animState(n2_1turtlesintersector_1_animstate),
    .animState_2(turtle_2x1_1_animstate_2));
  DotMatrix #(.inputtype("row"), .matrixcols(30), .matrixrows(6)) dotmatrix_8 (
    .row0(turtle_2x1_1_tobackground_3), .row1(turtle_2x1_1_tobackground_4),
    .row2(turtle_2x1_1_tobackground_5), .row3(turtle_2x1_1_tobackground_6),
    .row4(turtle_2x1_1_tobackground_7), .row5(turtle_2x1_1_tobackground_8));
  DotMatrix #(.inputtype("row"), .matrixcols(30), .matrixrows(2)) dotmatrix_9 (
    .row0(turtle_2x1_1_tobackground_9), .row1(turtle_2x1_1_tobackground_10));
  log_3x2 log_3x2_1 (
    .inBackShiftD(rightshifter_2_shiftd), .outBackShiftD(log_3x2_1_outbackshiftd),
    .inputBackShiftM(rightshifter_2_shiftm), .outputBackShiftM(log_3x2_1_outputbackshiftm),
    .inPlayerShiftD(keyboard_2_p9), .outPlayerShiftD(log_3x2_1_outplayershiftd),
    .inPlayerShiftM(keyboard_2_p8), .outPlayerShiftM(log_3x2_1_outplayershiftm), .inFlag(_9),
    .outFlag(log_3x2_1_outflag), .toBackground(log_3x2_1_tobackground),
    .toBackground_2(log_3x2_1_tobackground_2), .toBackground_3(log_3x2_1_tobackground_3),
    .toBackground_4(log_3x2_1_tobackground_4), .toBackground_5(log_3x2_1_tobackground_5),
    .toBackground_6(log_3x2_1_tobackground_6), .toBackground_7(log_3x2_1_tobackground_7),
    .toBackground_8(log_3x2_1_tobackground_8), .toBackground_9(log_3x2_1_tobackground_9),
    .toBackground_10(log_3x2_1_tobackground_10), .toFront(log_3x2_1_tofront),
    .toFront_2(log_3x2_1_tofront_2), .toFront_3(log_3x2_1_tofront_3), .toFront_4(log_3x2_1_tofront_4),
    .toFront_5(log_3x2_1_tofront_5), .toFront_6(log_3x2_1_tofront_6), .toFront_7(log_3x2_1_tofront_7),
    .toFront_8(log_3x2_1_tofront_8), .toFront_9(log_3x2_1_tofront_9), .toFront_10(log_3x2_1_tofront_10));
  DotMatrix #(.inputtype("row"), .matrixcols(30), .matrixrows(10)) dotmatrix_10 (
    .row0(log_3x2_1_tofront), .row1(log_3x2_1_tofront_2), .row2(log_3x2_1_tofront_3),
    .row3(log_3x2_1_tofront_4), .row4(log_3x2_1_tofront_5), .row5(log_3x2_1_tofront_6),
    .row6(log_3x2_1_tofront_7), .row7(log_3x2_1_tofront_8), .row8(log_3x2_1_tofront_9),
    .row9(log_3x2_1_tofront_10));
  DotMatrix #(.inputtype("row"), .matrixcols(30), .matrixrows(3)) dotmatrix_11 (
    .row0(log_3x2_1_tobackground), .row1(log_3x2_1_tobackground_2), .row2(log_3x2_1_tobackground_3));
  DotMatrix #(.inputtype("row"), .matrixcols(30), .matrixrows(4)) dotmatrix_12 (
    .row0(log_3x2_1_tobackground_4), .row1(log_3x2_1_tobackground_5), .row2(log_3x2_1_tobackground_6),
    .row3(log_3x2_1_tobackground_7));
  DotMatrix #(.inputtype("row"), .matrixcols(30), .matrixrows(3)) dotmatrix_13 (
    .row0(log_3x2_1_tobackground_8), .row1(log_3x2_1_tobackground_9), .row2(log_3x2_1_tobackground_10));
  DotMatrix #(.inputtype("row"), .matrixcols(30), .matrixrows(3)) dotmatrix_14 (
    .row0(log_1x1_1_tobackground), .row1(log_1x1_1_tobackground_2), .row2(log_1x1_1_tobackground_3));
  log_1x1 log_1x1_1 (
    .inBackShiftD(rightshifter_3_p7), .outBackShiftD(log_1x1_1_outbackshiftd),
    .inputBackShiftM(rightshifter_3_p4), .outputBackShiftM(log_1x1_1_outputbackshiftm),
    .inPlayerShiftD(keyboard_2_p9), .outPlayerShiftD(log_1x1_1_outplayershiftd),
    .inPlayerShiftM(keyboard_2_p8), .outPlayerShiftM(log_1x1_1_outplayershiftm), .inFlag(_8),
    .outFlag(log_1x1_1_outflag), .toBackground(log_1x1_1_tobackground),
    .toBackground_2(log_1x1_1_tobackground_2), .toBackground_3(log_1x1_1_tobackground_3),
    .toBackground_4(log_1x1_1_tobackground_4), .toBackground_5(log_1x1_1_tobackground_5),
    .toBackground_6(log_1x1_1_tobackground_6), .toBackground_7(log_1x1_1_tobackground_7),
    .toBackground_8(log_1x1_1_tobackground_8), .toBackground_9(log_1x1_1_tobackground_9),
    .toBackground_10(log_1x1_1_tobackground_10), .toFront(log_1x1_1_tofront),
    .toFront_2(log_1x1_1_tofront_2), .toFront_3(log_1x1_1_tofront_3), .toFront_4(log_1x1_1_tofront_4),
    .toFront_5(log_1x1_1_tofront_5), .toFront_6(log_1x1_1_tofront_6), .toFront_7(log_1x1_1_tofront_7),
    .toFront_8(log_1x1_1_tofront_8), .toFront_9(log_1x1_1_tofront_9), .toFront_10(log_1x1_1_tofront_10));
  DotMatrix #(.inputtype("row"), .matrixcols(30), .matrixrows(10)) dotmatrix_15 (
    .row0(log_1x1_1_tofront), .row1(log_1x1_1_tofront_2), .row2(log_1x1_1_tofront_3),
    .row3(log_1x1_1_tofront_4), .row4(log_1x1_1_tofront_5), .row5(log_1x1_1_tofront_6),
    .row6(log_1x1_1_tofront_7), .row7(log_1x1_1_tofront_8), .row8(log_1x1_1_tofront_9),
    .row9(log_1x1_1_tofront_10));
  DotMatrix #(.inputtype("row"), .matrixcols(30), .matrixrows(4)) dotmatrix_16 (
    .row0(log_1x1_1_tobackground_4), .row1(log_1x1_1_tobackground_5), .row2(log_1x1_1_tobackground_6),
    .row3(log_1x1_1_tobackground_7));
  DotMatrix #(.inputtype("row"), .matrixcols(30), .matrixrows(3)) dotmatrix_17 (
    .row0(log_1x1_1_tobackground_8), .row1(log_1x1_1_tobackground_9), .row2(log_1x1_1_tobackground_10));
  DotMatrix #(.inputtype("row"), .matrixcols(30), .matrixrows(10)) dotmatrix_18 (
    .row0(turtle_3x1_1_tofront), .row1(turtle_3x1_1_tofront_2), .row2(turtle_3x1_1_tofront_3),
    .row3(turtle_3x1_1_tofront_4), .row4(turtle_3x1_1_tofront_5), .row5(turtle_3x1_1_tofront_6),
    .row6(turtle_3x1_1_tofront_7), .row7(turtle_3x1_1_tofront_8), .row8(turtle_3x1_1_tofront_9),
    .row9(turtle_3x1_1_tofront_10));
  turtle_3x1 turtle_3x1_1 (
    .inBackShiftD(leftshifter_2_shiftd), .outBackShiftD(turtle_3x1_1_outbackshiftd),
    .inputBackShiftM(leftshifter_2_shiftm), .outputBackShiftM(turtle_3x1_1_outputbackshiftm),
    .inPlayerShiftD(keyboard_2_p9), .outPlayerShiftD(turtle_3x1_1_outplayershiftd),
    .inPlayerShiftM(keyboard_2_p8), .outPlayerShiftM(turtle_3x1_1_outplayershiftm), .inFlag(_7),
    .outFlag(turtle_3x1_1_outflag), .toBackground(turtle_3x1_1_tobackground),
    .toBackground_2(turtle_3x1_1_tobackground_2), .toBackground_3(turtle_3x1_1_tobackground_3),
    .toBackground_4(turtle_3x1_1_tobackground_4), .toBackground_5(turtle_3x1_1_tobackground_5),
    .toBackground_6(turtle_3x1_1_tobackground_6), .toBackground_7(turtle_3x1_1_tobackground_7),
    .toBackground_8(turtle_3x1_1_tobackground_8), .toBackground_9(turtle_3x1_1_tobackground_9),
    .toBackground_10(turtle_3x1_1_tobackground_10), .toFront(turtle_3x1_1_tofront),
    .toFront_2(turtle_3x1_1_tofront_2), .toFront_3(turtle_3x1_1_tofront_3),
    .toFront_4(turtle_3x1_1_tofront_4), .toFront_5(turtle_3x1_1_tofront_5),
    .toFront_6(turtle_3x1_1_tofront_6), .toFront_7(turtle_3x1_1_tofront_7),
    .toFront_8(turtle_3x1_1_tofront_8), .toFront_9(turtle_3x1_1_tofront_9),
    .toFront_10(turtle_3x1_1_tofront_10), .animState(_1bAnim), .animState_2(turtle_3x1_1_animstate_2));
  DotMatrix #(.inputtype("row"), .matrixcols(30), .matrixrows(2)) dotmatrix_19 (
    .row0(turtle_3x1_1_tobackground), .row1(turtle_3x1_1_tobackground_2));
  DotMatrix #(.inputtype("row"), .matrixcols(30), .matrixrows(6)) dotmatrix_20 (
    .row0(turtle_3x1_1_tobackground_3), .row1(turtle_3x1_1_tobackground_4),
    .row2(turtle_3x1_1_tobackground_5), .row3(turtle_3x1_1_tobackground_6),
    .row4(turtle_3x1_1_tobackground_7), .row5(turtle_3x1_1_tobackground_8));
  DotMatrix #(.inputtype("row"), .matrixcols(30), .matrixrows(2)) dotmatrix_21 (
    .row0(turtle_3x1_1_tobackground_9), .row1(turtle_3x1_1_tobackground_10));
  // swampDriver swampdriver_1: pin names not known; wires that end beside it: Y, keyboard_2_p8, keyboard_2_p9, heightflag_7_p3, _6, swampdriver_1_p6, swampdriver_1_p7, swampdriver_1_p8, swampdriver_1_p9, swampdriver_1_p10, swampdriver_1_p11, swampdriver_1_p12, swampdriver_1_p13, swampdriver_1_p14, swampdriver_1_p15, swampdriver_1_p16, swampdriver_1_p17, swampdriver_1_p18, swampdriver_1_p19, swampdriver_1_p20, swampdriver_1_p21, swampdriver_1_p22, swampdriver_1_p23, swampdriver_1_p24, swampdriver_1_p25, swampdriver_1_p26, swampdriver_1_p27, swampdriver_1_p28, swampdriver_1_p29, swampdriver_1_p30
  DotMatrix #(.inputtype("row"), .matrixcols(30), .matrixrows(10)) dotmatrix_22 (
    .row0(swampdriver_1_p16), .row1(swampdriver_1_p17), .row2(swampdriver_1_p18), .row3(swampdriver_1_p19),
    .row4(swampdriver_1_p20), .row5(swampdriver_1_p21), .row6(swampdriver_1_p22), .row7(swampdriver_1_p23),
    .row8(swampdriver_1_p24), .row9(swampdriver_1_p25));
  DotMatrix #(.inputtype("row"), .matrixcols(30), .matrixrows(3)) dotmatrix_23 (
    .row0(swampdriver_1_p6), .row1(swampdriver_1_p7), .row2(swampdriver_1_p8));
  DotMatrix #(.inputtype("row"), .matrixcols(30), .matrixrows(4)) dotmatrix_24 (
    .row0(swampdriver_1_p9), .row1(swampdriver_1_p10), .row2(swampdriver_1_p11), .row3(swampdriver_1_p12));
  DotMatrix #(.inputtype("row"), .matrixcols(30), .matrixrows(3)) dotmatrix_25 (
    .row0(swampdriver_1_p13), .row1(swampdriver_1_p14), .row2(swampdriver_1_p15));
  truckDriver truckdriver_1 (
    .inBackShiftD(leftshifter_3_shiftd), .outBackShiftD(truckdriver_1_outbackshiftd),
    .inputBackShiftM(leftshifter_3_shiftm), .outputBackShiftM(truckdriver_1_outputbackshiftm),
    .inPlayerShiftD(keyboard_2_p9), .outPlayerShiftD(truckdriver_1_outplayershiftd),
    .inPlayerShiftM(keyboard_2_p8), .outPlayerShiftM(truckdriver_1_outplayershiftm), .inFlag(_5),
    .outFlag(truckdriver_1_outflag), .toBackground(truckdriver_1_tobackground),
    .toBackground_2(truckdriver_1_tobackground_2), .toBackground_3(truckdriver_1_tobackground_3),
    .toBackground_4(truckdriver_1_tobackground_4), .toBackground_5(truckdriver_1_tobackground_5),
    .toBackground_6(truckdriver_1_tobackground_6), .toBackground_7(truckdriver_1_tobackground_7),
    .toBackground_8(truckdriver_1_tobackground_8), .toBackground_9(truckdriver_1_tobackground_9),
    .toBackground_10(truckdriver_1_tobackground_10), .toFront(truckdriver_1_tofront),
    .toFront_2(truckdriver_1_tofront_2), .toFront_3(truckdriver_1_tofront_3),
    .toFront_4(truckdriver_1_tofront_4), .toFront_5(truckdriver_1_tofront_5),
    .toFront_6(truckdriver_1_tofront_6), .toFront_7(truckdriver_1_tofront_7),
    .toFront_8(truckdriver_1_tofront_8), .toFront_9(truckdriver_1_tofront_9),
    .toFront_10(truckdriver_1_tofront_10));
  DotMatrix #(.inputtype("row"), .matrixcols(30), .matrixrows(10)) dotmatrix_26 (
    .row0(truckdriver_1_tofront), .row1(truckdriver_1_tofront_2), .row2(truckdriver_1_tofront_3),
    .row3(truckdriver_1_tofront_4), .row4(truckdriver_1_tofront_5), .row5(truckdriver_1_tofront_6),
    .row6(truckdriver_1_tofront_7), .row7(truckdriver_1_tofront_8), .row8(truckdriver_1_tofront_9),
    .row9(truckdriver_1_tofront_10));
  DotMatrix #(.inputtype("row"), .matrixcols(30), .matrixrows(2)) dotmatrix_27 (
    .row0(truckdriver_1_tobackground), .row1(truckdriver_1_tobackground_2));
  DotMatrix #(.inputtype("row"), .matrixcols(30), .matrixrows(6)) dotmatrix_28 (
    .row0(truckdriver_1_tobackground_3), .row1(truckdriver_1_tobackground_4),
    .row2(truckdriver_1_tobackground_5), .row3(truckdriver_1_tobackground_6),
    .row4(truckdriver_1_tobackground_7), .row5(truckdriver_1_tobackground_8));
  DotMatrix #(.inputtype("row"), .matrixcols(30), .matrixrows(2)) dotmatrix_29 (
    .row0(truckdriver_1_tobackground_9), .row1(truckdriver_1_tobackground_10));
  DotMatrix #(.inputtype("row"), .matrixcols(30), .matrixrows(2)) dotmatrix_30 (
    .row0(carconnectorv2_1_tobackground), .row1(carconnectorv2_1_tobackground_2));
  DotMatrix #(.inputtype("row"), .matrixcols(30), .matrixrows(10)) dotmatrix_31 (
    .row0(carconnectorv2_1_tofront), .row1(carconnectorv2_1_tofront_2), .row2(carconnectorv2_1_tofront_3),
    .row3(carconnectorv2_1_tofront_4), .row4(carconnectorv2_1_tofront_5), .row5(carconnectorv2_1_tofront_6),
    .row6(carconnectorv2_1_tofront_7), .row7(carconnectorv2_1_tofront_8), .row8(carconnectorv2_1_tofront_9),
    .row9(carconnectorv2_1_tofront_10));
  carConnectorV2 carconnectorv2_1 (
    .inBackShiftD(rightshifter_4_shiftd), .outBackShiftD(carconnectorv2_1_outbackshiftd),
    .inputBackShiftM(rightshifter_4_shiftm), .outputBackShiftM(carconnectorv2_1_outputbackshiftm),
    .outPlayerShiftD(carconnectorv2_1_outplayershiftd), .inPlayerShiftM(keyboard_2_p8),
    .outPlayerShiftM(carconnectorv2_1_outplayershiftm), .inFlag(_4), .outFlag(carconnectorv2_1_outflag),
    .toBackground(carconnectorv2_1_tobackground), .toBackground_2(carconnectorv2_1_tobackground_2),
    .toBackground_3(carconnectorv2_1_tobackground_3), .toBackground_4(carconnectorv2_1_tobackground_4),
    .toBackground_5(carconnectorv2_1_tobackground_5), .toBackground_6(carconnectorv2_1_tobackground_6),
    .toBackground_7(carconnectorv2_1_tobackground_7), .toBackground_8(carconnectorv2_1_tobackground_8),
    .toBackground_9(carconnectorv2_1_tobackground_9), .toBackground_10(carconnectorv2_1_tobackground_10),
    .toFront(carconnectorv2_1_tofront), .toFront_2(carconnectorv2_1_tofront_2),
    .toFront_3(carconnectorv2_1_tofront_3), .toFront_4(carconnectorv2_1_tofront_4),
    .toFront_5(carconnectorv2_1_tofront_5), .toFront_6(carconnectorv2_1_tofront_6),
    .toFront_7(carconnectorv2_1_tofront_7), .toFront_8(carconnectorv2_1_tofront_8),
    .toFront_9(carconnectorv2_1_tofront_9), .toFront_10(carconnectorv2_1_tofront_10),
    .inPlayerShiftD(keyboard_2_p9));
  DotMatrix #(.inputtype("row"), .matrixcols(30), .matrixrows(6)) dotmatrix_32 (
    .row0(carconnectorv2_1_tobackground_3), .row1(carconnectorv2_1_tobackground_4),
    .row2(carconnectorv2_1_tobackground_5), .row3(carconnectorv2_1_tobackground_6),
    .row4(carconnectorv2_1_tobackground_7), .row5(carconnectorv2_1_tobackground_8));
  DotMatrix #(.inputtype("row"), .matrixcols(30), .matrixrows(2)) dotmatrix_33 (
    .row0(carconnectorv2_1_tobackground_9), .row1(carconnectorv2_1_tobackground_10));
  DotMatrix #(.inputtype("row"), .matrixcols(30), .matrixrows(10)) dotmatrix_34 (
    .row0(boliddriver_1_tofront), .row1(boliddriver_1_tofront_2), .row2(boliddriver_1_tofront_3),
    .row3(boliddriver_1_tofront_4), .row4(boliddriver_1_tofront_5), .row5(boliddriver_1_tofront_6),
    .row6(boliddriver_1_tofront_7), .row7(boliddriver_1_tofront_8), .row8(boliddriver_1_tofront_9),
    .row9(boliddriver_1_tofront_10));
  DotMatrix #(.inputtype("row"), .matrixcols(30), .matrixrows(2)) dotmatrix_35 (
    .row0(boliddriver_1_tobackground), .row1(boliddriver_1_tobackground_2));
  bolidDriver boliddriver_1 (
    .inBackShiftD(leftshifter_4_shiftd), .outBackShiftD(boliddriver_1_outbackshiftd),
    .inputBackShiftM(leftshifter_4_shiftm), .outputBackShiftM(boliddriver_1_outputbackshiftm),
    .inPlayerShiftD(keyboard_2_p9), .outPlayerShiftD(boliddriver_1_outplayershiftd),
    .inPlayerShiftM(keyboard_2_p8), .outPlayerShiftM(boliddriver_1_outplayershiftm), .inFlag(_3),
    .outFlag(boliddriver_1_outflag), .toBackground(boliddriver_1_tobackground),
    .toBackground_2(boliddriver_1_tobackground_2), .toBackground_3(boliddriver_1_tobackground_3),
    .toBackground_4(boliddriver_1_tobackground_4), .toBackground_5(boliddriver_1_tobackground_5),
    .toBackground_6(boliddriver_1_tobackground_6), .toBackground_7(boliddriver_1_tobackground_7),
    .toBackground_8(boliddriver_1_tobackground_8), .toBackground_9(boliddriver_1_tobackground_9),
    .toBackground_10(boliddriver_1_tobackground_10), .toFront(boliddriver_1_tofront),
    .toFront_2(boliddriver_1_tofront_2), .toFront_3(boliddriver_1_tofront_3),
    .toFront_4(boliddriver_1_tofront_4), .toFront_5(boliddriver_1_tofront_5),
    .toFront_6(boliddriver_1_tofront_6), .toFront_7(boliddriver_1_tofront_7),
    .toFront_8(boliddriver_1_tofront_8), .toFront_9(boliddriver_1_tofront_9),
    .toFront_10(boliddriver_1_tofront_10));
  DotMatrix #(.inputtype("row"), .matrixcols(30), .matrixrows(6)) dotmatrix_36 (
    .row0(boliddriver_1_tobackground_3), .row1(boliddriver_1_tobackground_4),
    .row2(boliddriver_1_tobackground_5), .row3(boliddriver_1_tobackground_6),
    .row4(boliddriver_1_tobackground_7), .row5(boliddriver_1_tobackground_8));
  DotMatrix #(.inputtype("row"), .matrixcols(30), .matrixrows(2)) dotmatrix_37 (
    .row0(boliddriver_1_tobackground_9), .row1(boliddriver_1_tobackground_10));
  SUVDriver suvdriver_1 (
    .inBackShiftD(rightshifter_5_shiftd), .outBackShiftD(suvdriver_1_outbackshiftd),
    .inputBackShiftM(rightshifter_5_shiftm), .outputBackShiftM(suvdriver_1_outputbackshiftm),
    .inPlayerShiftD(keyboard_2_p9), .outPlayerShiftD(suvdriver_1_outplayershiftd),
    .inPlayerShiftM(keyboard_2_p8), .outPlayerShiftM(suvdriver_1_outplayershiftm), .inFlag(_2),
    .outFlag(suvdriver_1_outflag), .toBackground(suvdriver_1_tobackground),
    .toBackground_2(suvdriver_1_tobackground_2), .toBackground_3(suvdriver_1_tobackground_3),
    .toBackground_4(suvdriver_1_tobackground_4), .toBackground_5(suvdriver_1_tobackground_5),
    .toBackground_6(suvdriver_1_tobackground_6), .toBackground_7(suvdriver_1_tobackground_7),
    .toBackground_8(suvdriver_1_tobackground_8), .toBackground_9(suvdriver_1_tobackground_9),
    .toBackground_10(suvdriver_1_tobackground_10), .toFront(suvdriver_1_tofront),
    .toFront_2(suvdriver_1_tofront_2), .toFront_3(suvdriver_1_tofront_3), .toFront_4(suvdriver_1_tofront_4),
    .toFront_5(suvdriver_1_tofront_5), .toFront_6(suvdriver_1_tofront_6), .toFront_7(suvdriver_1_tofront_7),
    .toFront_8(suvdriver_1_tofront_8), .toFront_9(suvdriver_1_tofront_9), .toFront_10(suvdriver_1_tofront_10));
  DotMatrix #(.inputtype("row"), .matrixcols(30), .matrixrows(10)) dotmatrix_38 (
    .row0(suvdriver_1_tofront), .row1(suvdriver_1_tofront_2), .row2(suvdriver_1_tofront_3),
    .row3(suvdriver_1_tofront_4), .row4(suvdriver_1_tofront_5), .row5(suvdriver_1_tofront_6),
    .row6(suvdriver_1_tofront_7), .row7(suvdriver_1_tofront_8), .row8(suvdriver_1_tofront_9),
    .row9(suvdriver_1_tofront_10));
  DotMatrix #(.inputtype("row"), .matrixcols(30), .matrixrows(2)) dotmatrix_39 (
    .row0(suvdriver_1_tobackground), .row1(suvdriver_1_tobackground_2));
  DotMatrix #(.inputtype("row"), .matrixcols(30), .matrixrows(6)) dotmatrix_40 (
    .row0(suvdriver_1_tobackground_3), .row1(suvdriver_1_tobackground_4), .row2(suvdriver_1_tobackground_5),
    .row3(suvdriver_1_tobackground_6), .row4(suvdriver_1_tobackground_7), .row5(suvdriver_1_tobackground_8));
  DotMatrix #(.inputtype("row"), .matrixcols(30), .matrixrows(2)) dotmatrix_41 (
    .row0(suvdriver_1_tobackground_9), .row1(suvdriver_1_tobackground_10));
  DotMatrix #(.inputtype("row"), .matrixcols(30), .matrixrows(2)) dotmatrix_42 (
    .row0(truckdriver_2_tobackground), .row1(truckdriver_2_tobackground_2));
  truckDriver truckdriver_2 (
    .inBackShiftD(leftshifter_5_shiftd), .outBackShiftD(truckdriver_2_outbackshiftd),
    .inputBackShiftM(leftshifter_5_shiftm), .outputBackShiftM(truckdriver_2_outputbackshiftm),
    .inPlayerShiftD(keyboard_2_p9), .outPlayerShiftD(truckdriver_2_outplayershiftd),
    .inPlayerShiftM(keyboard_2_p8), .outPlayerShiftM(truckdriver_2_outplayershiftm), .inFlag(_1),
    .outFlag(truckdriver_2_outflag), .toBackground(truckdriver_2_tobackground),
    .toBackground_2(truckdriver_2_tobackground_2), .toBackground_3(truckdriver_2_tobackground_3),
    .toBackground_4(truckdriver_2_tobackground_4), .toBackground_5(truckdriver_2_tobackground_5),
    .toBackground_6(truckdriver_2_tobackground_6), .toBackground_7(truckdriver_2_tobackground_7),
    .toBackground_8(truckdriver_2_tobackground_8), .toBackground_9(truckdriver_2_tobackground_9),
    .toBackground_10(truckdriver_2_tobackground_10), .toFront(truckdriver_2_tofront),
    .toFront_2(truckdriver_2_tofront_2), .toFront_3(truckdriver_2_tofront_3),
    .toFront_4(truckdriver_2_tofront_4), .toFront_5(truckdriver_2_tofront_5),
    .toFront_6(truckdriver_2_tofront_6), .toFront_7(truckdriver_2_tofront_7),
    .toFront_8(truckdriver_2_tofront_8), .toFront_9(truckdriver_2_tofront_9),
    .toFront_10(truckdriver_2_tofront_10));
  DotMatrix #(.inputtype("row"), .matrixcols(30), .matrixrows(10)) dotmatrix_43 (
    .row0(truckdriver_2_tofront), .row1(truckdriver_2_tofront_2), .row2(truckdriver_2_tofront_3),
    .row3(truckdriver_2_tofront_4), .row4(truckdriver_2_tofront_5), .row5(truckdriver_2_tofront_6),
    .row6(truckdriver_2_tofront_7), .row7(truckdriver_2_tofront_8), .row8(truckdriver_2_tofront_9),
    .row9(truckdriver_2_tofront_10));
  DotMatrix #(.inputtype("row"), .matrixcols(30), .matrixrows(6)) dotmatrix_44 (
    .row0(truckdriver_2_tobackground_3), .row1(truckdriver_2_tobackground_4),
    .row2(truckdriver_2_tobackground_5), .row3(truckdriver_2_tobackground_6),
    .row4(truckdriver_2_tobackground_7), .row5(truckdriver_2_tobackground_8));
  DotMatrix #(.inputtype("row"), .matrixcols(30), .matrixrows(2)) dotmatrix_45 (
    .row0(truckdriver_2_tobackground_9), .row1(truckdriver_2_tobackground_10));
  DotMatrix #(.inputtype("row"), .matrixcols(30), .matrixrows(3)) dotmatrix_46 (
    .row0(swampdriver_2_p4), .row1(swampdriver_2_p5), .row2(swampdriver_2_p6));
  // swampDriver swampdriver_2: pin names not known; wires that end beside it: keyboard_2_p8, keyboard_2_p9, _0, swampdriver_2_p4, swampdriver_2_p5, swampdriver_2_p6, swampdriver_2_p7, swampdriver_2_p8, swampdriver_2_p9, swampdriver_2_p10, swampdriver_2_p11, swampdriver_2_p12, swampdriver_2_p13, swampdriver_2_p14, swampdriver_2_p15, swampdriver_2_p16, swampdriver_2_p17, swampdriver_2_p18, swampdriver_2_p19, swampdriver_2_p20, swampdriver_2_p21, swampdriver_2_p22, swampdriver_2_p23, swampdriver_2_p24, swampdriver_2_p25, swampdriver_2_p26, swampdriver_2_p27, swampdriver_2_p28
  DotMatrix #(.inputtype("row"), .matrixcols(30), .matrixrows(10)) dotmatrix_47 (
    .row0(swampdriver_2_p14), .row1(swampdriver_2_p15), .row2(swampdriver_2_p16), .row3(swampdriver_2_p17),
    .row4(swampdriver_2_p18), .row5(swampdriver_2_p19), .row6(swampdriver_2_p20), .row7(swampdriver_2_p21),
    .row8(swampdriver_2_p22), .row9(swampdriver_2_p23));
  DotMatrix #(.inputtype("row"), .matrixcols(30), .matrixrows(4)) dotmatrix_48 (
    .row0(swampdriver_2_p7), .row1(swampdriver_2_p8), .row2(swampdriver_2_p9), .row3(swampdriver_2_p10));
  DotMatrix #(.inputtype("row"), .matrixcols(30), .matrixrows(3)) dotmatrix_49 (
    .row0(swampdriver_2_p11), .row1(swampdriver_2_p12), .row2(swampdriver_2_p13));
  Button u_res (.out(restartGame));
  CdM_8 cdm_8_1 (
    .IRQ(IRQ), .vector(vector), .lAck(IAck), .in_out(in_out), .I_Oadr(I_Oadr), .I_Osel(I_Osel),
    .I_Odat(I_Odat), .clear(restartGame), .clock(clock));
  DotMatrix #(.inputtype("row"), .matrixcols(30), .matrixrows(12)) dotmatrix_50 (
    .row0(finishconnector_2_tobackground), .row1(finishconnector_2_tobackground_2),
    .row2(finishconnector_2_tobackground_3), .row3(finishconnector_2_tobackground_4),
    .row4(finishconnector_2_tobackground_5), .row5(finishconnector_2_tobackground_6),
    .row6(finishconnector_2_tobackground_7), .row7(finishconnector_2_tobackground_8),
    .row8(finishconnector_2_tobackground_9), .row9(finishconnector_2_tobackground_10),
    .row10(finishconnector_2_tobackground_11), .row11(finishconnector_2_tobackground_12));
  finishConnector finishconnector_2 (
    .toBackground_3(finishconnector_2_tobackground_3), .toBackground_4(finishconnector_2_tobackground_4),
    .toBackground_5(finishconnector_2_tobackground_5), .toBackground_6(finishconnector_2_tobackground_6),
    .toBackground_7(finishconnector_2_tobackground_7), .toBackground_8(finishconnector_2_tobackground_8),
    .toBackground_9(finishconnector_2_tobackground_9), .toBackground_10(finishconnector_2_tobackground_10),
    .toBackground_11(finishconnector_2_tobackground_11), .toBackground_12(finishconnector_2_tobackground_12),
    .toBackground_2(finishconnector_2_tobackground_2), .toBackground(finishconnector_2_tobackground),
    .positions_2(finishconnector_2_positions_2), .circNumber_2(finishconnector_2_circnumber_2),
    .positions(finishconnector_1_positions_2), .circNumber(finishconnector_1_circnumber_2));
  DotMatrix #(.inputtype("row"), .matrixcols(30), .matrixrows(10)) dotmatrix_51 (
    .row0(log_2x1_2_tofront), .row1(log_2x1_2_tofront_2), .row2(log_2x1_2_tofront_3),
    .row3(log_2x1_2_tofront_4), .row4(log_2x1_2_tofront_5), .row5(log_2x1_2_tofront_6),
    .row6(log_2x1_2_tofront_7), .row7(log_2x1_2_tofront_8), .row8(log_2x1_2_tofront_9),
    .row9(log_2x1_2_tofront_10));
  log_2x1 log_2x1_2 (
    .inBackShiftD(log_2x1_1_outbackshiftd), .outBackShiftD(log_2x1_2_outbackshiftd),
    .inputBackShiftM(log_2x1_1_outputbackshiftm), .outputBackShiftM(log_2x1_2_outputbackshiftm),
    .inPlayerShiftD(log_2x1_1_outplayershiftd), .outPlayerShiftD(log_2x1_2_outplayershiftd),
    .inPlayerShiftM(log_2x1_1_outplayershiftm), .outPlayerShiftM(log_2x1_2_outplayershiftm),
    .inFlag(log_2x1_1_outflag), .outFlag(log_2x1_2_outflag), .toBackground(log_2x1_2_tobackground),
    .toBackground_2(log_2x1_2_tobackground_2), .toBackground_3(log_2x1_2_tobackground_3),
    .toBackground_4(log_2x1_2_tobackground_4), .toBackground_5(log_2x1_2_tobackground_5),
    .toBackground_6(log_2x1_2_tobackground_6), .toBackground_7(log_2x1_2_tobackground_7),
    .toBackground_8(log_2x1_2_tobackground_8), .toBackground_9(log_2x1_2_tobackground_9),
    .toBackground_10(log_2x1_2_tobackground_10), .toFront(log_2x1_2_tofront),
    .toFront_2(log_2x1_2_tofront_2), .toFront_3(log_2x1_2_tofront_3), .toFront_4(log_2x1_2_tofront_4),
    .toFront_5(log_2x1_2_tofront_5), .toFront_6(log_2x1_2_tofront_6), .toFront_7(log_2x1_2_tofront_7),
    .toFront_8(log_2x1_2_tofront_8), .toFront_9(log_2x1_2_tofront_9), .toFront_10(log_2x1_2_tofront_10));
  DotMatrix #(.inputtype("row"), .matrixcols(30), .matrixrows(3)) dotmatrix_52 (
    .row0(log_2x1_2_tobackground), .row1(log_2x1_2_tobackground_2), .row2(log_2x1_2_tobackground_3));
  DotMatrix #(.inputtype("row"), .matrixcols(30), .matrixrows(4)) dotmatrix_53 (
    .row0(log_2x1_2_tobackground_4), .row1(log_2x1_2_tobackground_5), .row2(log_2x1_2_tobackground_6),
    .row3(log_2x1_2_tobackground_7));
  DotMatrix #(.inputtype("row"), .matrixcols(30), .matrixrows(3)) dotmatrix_54 (
    .row0(log_2x1_2_tobackground_8), .row1(log_2x1_2_tobackground_9), .row2(log_2x1_2_tobackground_10));
  DotMatrix #(.inputtype("row"), .matrixcols(30), .matrixrows(2)) dotmatrix_55 (
    .row0(turtle_2x1_2_tobackground), .row1(turtle_2x1_2_tobackground_2));
  DotMatrix #(.inputtype("row"), .matrixcols(30), .matrixrows(10)) dotmatrix_56 (
    .row0(turtle_2x1_2_tofront), .row1(turtle_2x1_2_tofront_2), .row2(turtle_2x1_2_tofront_3),
    .row3(turtle_2x1_2_tofront_4), .row4(turtle_2x1_2_tofront_5), .row5(turtle_2x1_2_tofront_6),
    .row6(turtle_2x1_2_tofront_7), .row7(turtle_2x1_2_tofront_8), .row8(turtle_2x1_2_tofront_9),
    .row9(turtle_2x1_2_tofront_10));
  turtle_2x1 turtle_2x1_2 (
    .inPlayerShiftD(turtle_2x1_1_outplayershiftd), .outPlayerShiftD(turtle_2x1_2_outplayershiftd),
    .inPlayerShiftM(turtle_2x1_1_outplayershiftm), .outPlayerShiftM(turtle_2x1_2_outplayershiftm),
    .inFlag(turtle_2x1_1_outflag), .outFlag(turtle_2x1_2_outflag), .toBackground(turtle_2x1_2_tobackground),
    .toBackground_2(turtle_2x1_2_tobackground_2), .toBackground_3(turtle_2x1_2_tobackground_3),
    .toBackground_4(turtle_2x1_2_tobackground_4), .toBackground_5(turtle_2x1_2_tobackground_5),
    .toBackground_6(turtle_2x1_2_tobackground_6), .toBackground_7(turtle_2x1_2_tobackground_7),
    .toBackground_8(turtle_2x1_2_tobackground_8), .toBackground_9(turtle_2x1_2_tobackground_9),
    .toBackground_10(turtle_2x1_2_tobackground_10), .toFront(turtle_2x1_2_tofront),
    .toFront_2(turtle_2x1_2_tofront_2), .toFront_3(turtle_2x1_2_tofront_3),
    .toFront_4(turtle_2x1_2_tofront_4), .toFront_5(turtle_2x1_2_tofront_5),
    .toFront_6(turtle_2x1_2_tofront_6), .toFront_7(turtle_2x1_2_tofront_7),
    .toFront_8(turtle_2x1_2_tofront_8), .toFront_9(turtle_2x1_2_tofront_9),
    .toFront_10(turtle_2x1_2_tofront_10), .inBackShiftD(turtle_2x1_1_outbackshiftd),
    .outBackShiftD(turtle_2x1_2_outbackshiftd), .inputBackShiftM(turtle_2x1_1_outputbackshiftm),
    .outputBackShiftM(turtle_2x1_2_outputbackshiftm), .animState(turtle_2x1_1_animstate_2),
    .animState_2(turtle_2x1_2_animstate_2));
  DotMatrix #(.inputtype("row"), .matrixcols(30), .matrixrows(6)) dotmatrix_57 (
    .row0(turtle_2x1_2_tobackground_3), .row1(turtle_2x1_2_tobackground_4),
    .row2(turtle_2x1_2_tobackground_5), .row3(turtle_2x1_2_tobackground_6),
    .row4(turtle_2x1_2_tobackground_7), .row5(turtle_2x1_2_tobackground_8));
  DotMatrix #(.inputtype("row"), .matrixcols(30), .matrixrows(2)) dotmatrix_58 (
    .row0(turtle_2x1_2_tobackground_9), .row1(turtle_2x1_2_tobackground_10));
  DotMatrix #(.inputtype("row"), .matrixcols(30), .matrixrows(10)) dotmatrix_59 (
    .row0(log_3x2_2_tofront), .row1(log_3x2_2_tofront_2), .row2(log_3x2_2_tofront_3),
    .row3(log_3x2_2_tofront_4), .row4(log_3x2_2_tofront_5), .row5(log_3x2_2_tofront_6),
    .row6(log_3x2_2_tofront_7), .row7(log_3x2_2_tofront_8), .row8(log_3x2_2_tofront_9),
    .row9(log_3x2_2_tofront_10));
  log_3x2 log_3x2_2 (
    .inBackShiftD(log_3x2_1_outbackshiftd), .outBackShiftD(log_3x2_2_outbackshiftd),
    .inputBackShiftM(log_3x2_1_outputbackshiftm), .outputBackShiftM(log_3x2_2_outputbackshiftm),
    .inPlayerShiftD(log_3x2_1_outplayershiftd), .outPlayerShiftD(log_3x2_2_outplayershiftd),
    .inPlayerShiftM(log_3x2_1_outplayershiftm), .outPlayerShiftM(log_3x2_2_outplayershiftm),
    .inFlag(log_3x2_1_outflag), .outFlag(log_3x2_2_outflag), .toBackground(log_3x2_2_tobackground),
    .toBackground_2(log_3x2_2_tobackground_2), .toBackground_3(log_3x2_2_tobackground_3),
    .toBackground_4(log_3x2_2_tobackground_4), .toBackground_5(log_3x2_2_tobackground_5),
    .toBackground_6(log_3x2_2_tobackground_6), .toBackground_7(log_3x2_2_tobackground_7),
    .toBackground_8(log_3x2_2_tobackground_8), .toBackground_9(log_3x2_2_tobackground_9),
    .toBackground_10(log_3x2_2_tobackground_10), .toFront(log_3x2_2_tofront),
    .toFront_2(log_3x2_2_tofront_2), .toFront_3(log_3x2_2_tofront_3), .toFront_4(log_3x2_2_tofront_4),
    .toFront_5(log_3x2_2_tofront_5), .toFront_6(log_3x2_2_tofront_6), .toFront_7(log_3x2_2_tofront_7),
    .toFront_8(log_3x2_2_tofront_8), .toFront_9(log_3x2_2_tofront_9), .toFront_10(log_3x2_2_tofront_10));
  DotMatrix #(.inputtype("row"), .matrixcols(30), .matrixrows(3)) dotmatrix_60 (
    .row0(log_3x2_2_tobackground), .row1(log_3x2_2_tobackground_2), .row2(log_3x2_2_tobackground_3));
  DotMatrix #(.inputtype("row"), .matrixcols(30), .matrixrows(4)) dotmatrix_61 (
    .row0(log_3x2_2_tobackground_4), .row1(log_3x2_2_tobackground_5), .row2(log_3x2_2_tobackground_6),
    .row3(log_3x2_2_tobackground_7));
  DotMatrix #(.inputtype("row"), .matrixcols(30), .matrixrows(3)) dotmatrix_62 (
    .row0(log_3x2_2_tobackground_8), .row1(log_3x2_2_tobackground_9), .row2(log_3x2_2_tobackground_10));
  DotMatrix #(.inputtype("row"), .matrixcols(30), .matrixrows(3)) dotmatrix_63 (
    .row0(log_1x1_2_tobackground), .row1(log_1x1_2_tobackground_2), .row2(log_1x1_2_tobackground_3));
  DotMatrix #(.inputtype("row"), .matrixcols(30), .matrixrows(10)) dotmatrix_64 (
    .row0(log_1x1_2_tofront), .row1(log_1x1_2_tofront_2), .row2(log_1x1_2_tofront_3),
    .row3(log_1x1_2_tofront_4), .row4(log_1x1_2_tofront_5), .row5(log_1x1_2_tofront_6),
    .row6(log_1x1_2_tofront_7), .row7(log_1x1_2_tofront_8), .row8(log_1x1_2_tofront_9),
    .row9(log_1x1_2_tofront_10));
  log_1x1 log_1x1_2 (
    .inBackShiftD(log_1x1_1_outbackshiftd), .outBackShiftD(log_1x1_2_outbackshiftd),
    .inputBackShiftM(log_1x1_1_outputbackshiftm), .outputBackShiftM(log_1x1_2_outputbackshiftm),
    .inPlayerShiftD(log_1x1_1_outplayershiftd), .outPlayerShiftD(log_1x1_2_outplayershiftd),
    .inPlayerShiftM(log_1x1_1_outplayershiftm), .outPlayerShiftM(log_1x1_2_outplayershiftm),
    .inFlag(log_1x1_1_outflag), .outFlag(log_1x1_2_outflag), .toBackground(log_1x1_2_tobackground),
    .toBackground_2(log_1x1_2_tobackground_2), .toBackground_3(log_1x1_2_tobackground_3),
    .toBackground_4(log_1x1_2_tobackground_4), .toBackground_5(log_1x1_2_tobackground_5),
    .toBackground_6(log_1x1_2_tobackground_6), .toBackground_7(log_1x1_2_tobackground_7),
    .toBackground_8(log_1x1_2_tobackground_8), .toBackground_9(log_1x1_2_tobackground_9),
    .toBackground_10(log_1x1_2_tobackground_10), .toFront(log_1x1_2_tofront),
    .toFront_2(log_1x1_2_tofront_2), .toFront_3(log_1x1_2_tofront_3), .toFront_4(log_1x1_2_tofront_4),
    .toFront_5(log_1x1_2_tofront_5), .toFront_6(log_1x1_2_tofront_6), .toFront_7(log_1x1_2_tofront_7),
    .toFront_8(log_1x1_2_tofront_8), .toFront_9(log_1x1_2_tofront_9), .toFront_10(log_1x1_2_tofront_10));
  DotMatrix #(.inputtype("row"), .matrixcols(30), .matrixrows(4)) dotmatrix_65 (
    .row0(log_1x1_2_tobackground_4), .row1(log_1x1_2_tobackground_5), .row2(log_1x1_2_tobackground_6),
    .row3(log_1x1_2_tobackground_7));
  DotMatrix #(.inputtype("row"), .matrixcols(30), .matrixrows(3)) dotmatrix_66 (
    .row0(log_1x1_2_tobackground_8), .row1(log_1x1_2_tobackground_9), .row2(log_1x1_2_tobackground_10));
  turtle_3x1 turtle_3x1_2 (
    .inBackShiftD(turtle_3x1_1_outbackshiftd), .outBackShiftD(turtle_3x1_2_outbackshiftd),
    .inputBackShiftM(turtle_3x1_1_outputbackshiftm), .outputBackShiftM(turtle_3x1_2_outputbackshiftm),
    .inPlayerShiftD(turtle_3x1_1_outplayershiftd), .outPlayerShiftD(turtle_3x1_2_outplayershiftd),
    .inPlayerShiftM(turtle_3x1_1_outplayershiftm), .outPlayerShiftM(turtle_3x1_2_outplayershiftm),
    .inFlag(turtle_3x1_1_outflag), .outFlag(turtle_3x1_2_outflag), .toBackground(turtle_3x1_2_tobackground),
    .toBackground_2(turtle_3x1_2_tobackground_2), .toBackground_3(turtle_3x1_2_tobackground_3),
    .toBackground_4(turtle_3x1_2_tobackground_4), .toBackground_5(turtle_3x1_2_tobackground_5),
    .toBackground_6(turtle_3x1_2_tobackground_6), .toBackground_7(turtle_3x1_2_tobackground_7),
    .toBackground_8(turtle_3x1_2_tobackground_8), .toBackground_9(turtle_3x1_2_tobackground_9),
    .toBackground_10(turtle_3x1_2_tobackground_10), .toFront(turtle_3x1_2_tofront),
    .toFront_2(turtle_3x1_2_tofront_2), .toFront_3(turtle_3x1_2_tofront_3),
    .toFront_4(turtle_3x1_2_tofront_4), .toFront_5(turtle_3x1_2_tofront_5),
    .toFront_6(turtle_3x1_2_tofront_6), .toFront_7(turtle_3x1_2_tofront_7),
    .toFront_8(turtle_3x1_2_tofront_8), .toFront_9(turtle_3x1_2_tofront_9),
    .toFront_10(turtle_3x1_2_tofront_10), .animState(turtle_3x1_1_animstate_2),
    .animState_2(turtle_3x1_2_animstate_2));
  DotMatrix #(.inputtype("row"), .matrixcols(30), .matrixrows(10)) dotmatrix_67 (
    .row0(turtle_3x1_2_tofront), .row1(turtle_3x1_2_tofront_2), .row2(turtle_3x1_2_tofront_3),
    .row3(turtle_3x1_2_tofront_4), .row4(turtle_3x1_2_tofront_5), .row5(turtle_3x1_2_tofront_6),
    .row6(turtle_3x1_2_tofront_7), .row7(turtle_3x1_2_tofront_8), .row8(turtle_3x1_2_tofront_9),
    .row9(turtle_3x1_2_tofront_10));
  DotMatrix #(.inputtype("row"), .matrixcols(30), .matrixrows(2)) dotmatrix_68 (
    .row0(turtle_3x1_2_tobackground), .row1(turtle_3x1_2_tobackground_2));
  DotMatrix #(.inputtype("row"), .matrixcols(30), .matrixrows(6)) dotmatrix_69 (
    .row0(turtle_3x1_2_tobackground_3), .row1(turtle_3x1_2_tobackground_4),
    .row2(turtle_3x1_2_tobackground_5), .row3(turtle_3x1_2_tobackground_6),
    .row4(turtle_3x1_2_tobackground_7), .row5(turtle_3x1_2_tobackground_8));
  DotMatrix #(.inputtype("row"), .matrixcols(30), .matrixrows(2)) dotmatrix_70 (
    .row0(turtle_3x1_2_tobackground_9), .row1(turtle_3x1_2_tobackground_10));
  DotMatrix #(.inputtype("row"), .matrixcols(30), .matrixrows(10)) dotmatrix_71 (
    .row0(swampdriver_3_p16), .row1(swampdriver_3_p17), .row2(swampdriver_3_p18), .row3(swampdriver_3_p19),
    .row4(swampdriver_3_p20), .row5(swampdriver_3_p21), .row6(swampdriver_3_p22), .row7(swampdriver_3_p23),
    .row8(swampdriver_3_p24), .row9(swampdriver_3_p25));
  // swampDriver swampdriver_3: pin names not known; wires that end beside it: swampdriver_1_p26, swampdriver_1_p27, swampdriver_1_p28, swampdriver_1_p29, swampdriver_1_p30, swampdriver_3_p6, swampdriver_3_p7, swampdriver_3_p8, swampdriver_3_p9, swampdriver_3_p10, swampdriver_3_p11, swampdriver_3_p12, swampdriver_3_p13, swampdriver_3_p14, swampdriver_3_p15, swampdriver_3_p16, swampdriver_3_p17, swampdriver_3_p18, swampdriver_3_p19, swampdriver_3_p20, swampdriver_3_p21, swampdriver_3_p22, swampdriver_3_p23, swampdriver_3_p24, swampdriver_3_p25, swampdriver_3_p26, swampdriver_3_p27, swampdriver_3_p28, swampdriver_3_p29, swampdriver_3_p30
  DotMatrix #(.inputtype("row"), .matrixcols(30), .matrixrows(3)) dotmatrix_72 (
    .row0(swampdriver_3_p6), .row1(swampdriver_3_p7), .row2(swampdriver_3_p8));
  DotMatrix #(.inputtype("row"), .matrixcols(30), .matrixrows(4)) dotmatrix_73 (
    .row0(swampdriver_3_p9), .row1(swampdriver_3_p10), .row2(swampdriver_3_p11), .row3(swampdriver_3_p12));
  DotMatrix #(.inputtype("row"), .matrixcols(30), .matrixrows(3)) dotmatrix_74 (
    .row0(swampdriver_3_p13), .row1(swampdriver_3_p14), .row2(swampdriver_3_p15));
  DotMatrix #(.inputtype("row"), .matrixcols(30), .matrixrows(2)) dotmatrix_75 (
    .row0(truckdriver_3_tobackground), .row1(truckdriver_3_tobackground_2));
  DotMatrix #(.inputtype("row"), .matrixcols(30), .matrixrows(10)) dotmatrix_76 (
    .row0(truckdriver_3_tofront), .row1(truckdriver_3_tofront_2), .row2(truckdriver_3_tofront_3),
    .row3(truckdriver_3_tofront_4), .row4(truckdriver_3_tofront_5), .row5(truckdriver_3_tofront_6),
    .row6(truckdriver_3_tofront_7), .row7(truckdriver_3_tofront_8), .row8(truckdriver_3_tofront_9),
    .row9(truckdriver_3_tofront_10));
  truckDriver truckdriver_3 (
    .inBackShiftD(truckdriver_1_outbackshiftd), .outBackShiftD(truckdriver_3_outbackshiftd),
    .inputBackShiftM(truckdriver_1_outputbackshiftm), .outputBackShiftM(truckdriver_3_outputbackshiftm),
    .inPlayerShiftD(truckdriver_1_outplayershiftd), .outPlayerShiftD(truckdriver_3_outplayershiftd),
    .inPlayerShiftM(truckdriver_1_outplayershiftm), .outPlayerShiftM(truckdriver_3_outplayershiftm),
    .inFlag(truckdriver_1_outflag), .outFlag(truckdriver_3_outflag),
    .toBackground(truckdriver_3_tobackground), .toBackground_2(truckdriver_3_tobackground_2),
    .toBackground_3(truckdriver_3_tobackground_3), .toBackground_4(truckdriver_3_tobackground_4),
    .toBackground_5(truckdriver_3_tobackground_5), .toBackground_6(truckdriver_3_tobackground_6),
    .toBackground_7(truckdriver_3_tobackground_7), .toBackground_8(truckdriver_3_tobackground_8),
    .toBackground_9(truckdriver_3_tobackground_9), .toBackground_10(truckdriver_3_tobackground_10),
    .toFront(truckdriver_3_tofront), .toFront_2(truckdriver_3_tofront_2),
    .toFront_3(truckdriver_3_tofront_3), .toFront_4(truckdriver_3_tofront_4),
    .toFront_5(truckdriver_3_tofront_5), .toFront_6(truckdriver_3_tofront_6),
    .toFront_7(truckdriver_3_tofront_7), .toFront_8(truckdriver_3_tofront_8),
    .toFront_9(truckdriver_3_tofront_9), .toFront_10(truckdriver_3_tofront_10));
  DotMatrix #(.inputtype("row"), .matrixcols(30), .matrixrows(6)) dotmatrix_77 (
    .row0(truckdriver_3_tobackground_3), .row1(truckdriver_3_tobackground_4),
    .row2(truckdriver_3_tobackground_5), .row3(truckdriver_3_tobackground_6),
    .row4(truckdriver_3_tobackground_7), .row5(truckdriver_3_tobackground_8));
  DotMatrix #(.inputtype("row"), .matrixcols(30), .matrixrows(2)) dotmatrix_78 (
    .row0(truckdriver_3_tobackground_9), .row1(truckdriver_3_tobackground_10));
  DotMatrix #(.inputtype("row"), .matrixcols(30), .matrixrows(2)) dotmatrix_79 (
    .row0(carconnectorv2_2_tobackground), .row1(carconnectorv2_2_tobackground_2));
  DotMatrix #(.inputtype("row"), .matrixcols(30), .matrixrows(10)) dotmatrix_80 (
    .row0(carconnectorv2_2_tofront), .row1(carconnectorv2_2_tofront_2), .row2(carconnectorv2_2_tofront_3),
    .row3(carconnectorv2_2_tofront_4), .row4(carconnectorv2_2_tofront_5), .row5(carconnectorv2_2_tofront_6),
    .row6(carconnectorv2_2_tofront_7), .row7(carconnectorv2_2_tofront_8), .row8(carconnectorv2_2_tofront_9),
    .row9(carconnectorv2_2_tofront_10));
  carConnectorV2 carconnectorv2_2 (
    .inBackShiftD(carconnectorv2_1_outbackshiftd), .outBackShiftD(carconnectorv2_2_outbackshiftd),
    .inputBackShiftM(carconnectorv2_1_outputbackshiftm),
    .outputBackShiftM(carconnectorv2_2_outputbackshiftm), .outPlayerShiftD(carconnectorv2_2_outplayershiftd),
    .inPlayerShiftM(carconnectorv2_1_outplayershiftm), .outPlayerShiftM(carconnectorv2_2_outplayershiftm),
    .inFlag(carconnectorv2_1_outflag), .outFlag(carconnectorv2_2_outflag),
    .toBackground(carconnectorv2_2_tobackground), .toBackground_2(carconnectorv2_2_tobackground_2),
    .toBackground_3(carconnectorv2_2_tobackground_3), .toBackground_4(carconnectorv2_2_tobackground_4),
    .toBackground_5(carconnectorv2_2_tobackground_5), .toBackground_6(carconnectorv2_2_tobackground_6),
    .toBackground_7(carconnectorv2_2_tobackground_7), .toBackground_8(carconnectorv2_2_tobackground_8),
    .toBackground_9(carconnectorv2_2_tobackground_9), .toBackground_10(carconnectorv2_2_tobackground_10),
    .toFront(carconnectorv2_2_tofront), .toFront_2(carconnectorv2_2_tofront_2),
    .toFront_3(carconnectorv2_2_tofront_3), .toFront_4(carconnectorv2_2_tofront_4),
    .toFront_5(carconnectorv2_2_tofront_5), .toFront_6(carconnectorv2_2_tofront_6),
    .toFront_7(carconnectorv2_2_tofront_7), .toFront_8(carconnectorv2_2_tofront_8),
    .toFront_9(carconnectorv2_2_tofront_9), .toFront_10(carconnectorv2_2_tofront_10),
    .inPlayerShiftD(carconnectorv2_1_outplayershiftd));
  DotMatrix #(.inputtype("row"), .matrixcols(30), .matrixrows(6)) dotmatrix_81 (
    .row0(carconnectorv2_2_tobackground_3), .row1(carconnectorv2_2_tobackground_4),
    .row2(carconnectorv2_2_tobackground_5), .row3(carconnectorv2_2_tobackground_6),
    .row4(carconnectorv2_2_tobackground_7), .row5(carconnectorv2_2_tobackground_8));
  DotMatrix #(.inputtype("row"), .matrixcols(30), .matrixrows(2)) dotmatrix_82 (
    .row0(carconnectorv2_2_tobackground_9), .row1(carconnectorv2_2_tobackground_10));
  bolidDriver boliddriver_2 (
    .inBackShiftD(boliddriver_1_outbackshiftd), .outBackShiftD(boliddriver_2_outbackshiftd),
    .inputBackShiftM(boliddriver_1_outputbackshiftm), .outputBackShiftM(boliddriver_2_outputbackshiftm),
    .inPlayerShiftD(boliddriver_1_outplayershiftd), .outPlayerShiftD(boliddriver_2_outplayershiftd),
    .inPlayerShiftM(boliddriver_1_outplayershiftm), .outPlayerShiftM(boliddriver_2_outplayershiftm),
    .inFlag(boliddriver_1_outflag), .outFlag(boliddriver_2_outflag),
    .toBackground(boliddriver_2_tobackground), .toBackground_2(boliddriver_2_tobackground_2),
    .toBackground_3(boliddriver_2_tobackground_3), .toBackground_4(boliddriver_2_tobackground_4),
    .toBackground_5(boliddriver_2_tobackground_5), .toBackground_6(boliddriver_2_tobackground_6),
    .toBackground_7(boliddriver_2_tobackground_7), .toBackground_8(boliddriver_2_tobackground_8),
    .toBackground_9(boliddriver_2_tobackground_9), .toBackground_10(boliddriver_2_tobackground_10),
    .toFront(boliddriver_2_tofront), .toFront_2(boliddriver_2_tofront_2),
    .toFront_3(boliddriver_2_tofront_3), .toFront_4(boliddriver_2_tofront_4),
    .toFront_5(boliddriver_2_tofront_5), .toFront_6(boliddriver_2_tofront_6),
    .toFront_7(boliddriver_2_tofront_7), .toFront_8(boliddriver_2_tofront_8),
    .toFront_9(boliddriver_2_tofront_9), .toFront_10(boliddriver_2_tofront_10));
  DotMatrix #(.inputtype("row"), .matrixcols(30), .matrixrows(2)) dotmatrix_83 (
    .row0(boliddriver_2_tobackground), .row1(boliddriver_2_tobackground_2));
  DotMatrix #(.inputtype("row"), .matrixcols(30), .matrixrows(10)) dotmatrix_84 (
    .row0(boliddriver_2_tofront), .row1(boliddriver_2_tofront_2), .row2(boliddriver_2_tofront_3),
    .row3(boliddriver_2_tofront_4), .row4(boliddriver_2_tofront_5), .row5(boliddriver_2_tofront_6),
    .row6(boliddriver_2_tofront_7), .row7(boliddriver_2_tofront_8), .row8(boliddriver_2_tofront_9),
    .row9(boliddriver_2_tofront_10));
  DotMatrix #(.inputtype("row"), .matrixcols(30), .matrixrows(6)) dotmatrix_85 (
    .row0(boliddriver_2_tobackground_3), .row1(boliddriver_2_tobackground_4),
    .row2(boliddriver_2_tobackground_5), .row3(boliddriver_2_tobackground_6),
    .row4(boliddriver_2_tobackground_7), .row5(boliddriver_2_tobackground_8));
  DotMatrix #(.inputtype("row"), .matrixcols(30), .matrixrows(2)) dotmatrix_86 (
    .row0(boliddriver_2_tobackground_9), .row1(boliddriver_2_tobackground_10));
  SUVDriver suvdriver_2 (
    .inBackShiftD(suvdriver_1_outbackshiftd), .outBackShiftD(suvdriver_2_outbackshiftd),
    .inputBackShiftM(suvdriver_1_outputbackshiftm), .outputBackShiftM(suvdriver_2_outputbackshiftm),
    .inPlayerShiftD(suvdriver_1_outplayershiftd), .outPlayerShiftD(suvdriver_2_outplayershiftd),
    .inPlayerShiftM(suvdriver_1_outplayershiftm), .outPlayerShiftM(suvdriver_2_outplayershiftm),
    .inFlag(suvdriver_1_outflag), .outFlag(suvdriver_2_outflag), .toBackground(suvdriver_2_tobackground),
    .toBackground_2(suvdriver_2_tobackground_2), .toBackground_3(suvdriver_2_tobackground_3),
    .toBackground_4(suvdriver_2_tobackground_4), .toBackground_5(suvdriver_2_tobackground_5),
    .toBackground_6(suvdriver_2_tobackground_6), .toBackground_7(suvdriver_2_tobackground_7),
    .toBackground_8(suvdriver_2_tobackground_8), .toBackground_9(suvdriver_2_tobackground_9),
    .toBackground_10(suvdriver_2_tobackground_10), .toFront(suvdriver_2_tofront),
    .toFront_2(suvdriver_2_tofront_2), .toFront_3(suvdriver_2_tofront_3), .toFront_4(suvdriver_2_tofront_4),
    .toFront_5(suvdriver_2_tofront_5), .toFront_6(suvdriver_2_tofront_6), .toFront_7(suvdriver_2_tofront_7),
    .toFront_8(suvdriver_2_tofront_8), .toFront_9(suvdriver_2_tofront_9), .toFront_10(suvdriver_2_tofront_10));
  DotMatrix #(.inputtype("row"), .matrixcols(30), .matrixrows(2)) dotmatrix_87 (
    .row0(suvdriver_2_tobackground), .row1(suvdriver_2_tobackground_2));
  DotMatrix #(.inputtype("row"), .matrixcols(30), .matrixrows(10)) dotmatrix_88 (
    .row0(suvdriver_2_tofront), .row1(suvdriver_2_tofront_2), .row2(suvdriver_2_tofront_3),
    .row3(suvdriver_2_tofront_4), .row4(suvdriver_2_tofront_5), .row5(suvdriver_2_tofront_6),
    .row6(suvdriver_2_tofront_7), .row7(suvdriver_2_tofront_8), .row8(suvdriver_2_tofront_9),
    .row9(suvdriver_2_tofront_10));
  DotMatrix #(.inputtype("row"), .matrixcols(30), .matrixrows(6)) dotmatrix_89 (
    .row0(suvdriver_2_tobackground_3), .row1(suvdriver_2_tobackground_4), .row2(suvdriver_2_tobackground_5),
    .row3(suvdriver_2_tobackground_6), .row4(suvdriver_2_tobackground_7), .row5(suvdriver_2_tobackground_8));
  DotMatrix #(.inputtype("row"), .matrixcols(30), .matrixrows(2)) dotmatrix_90 (
    .row0(suvdriver_2_tobackground_9), .row1(suvdriver_2_tobackground_10));
  DotMatrix #(.inputtype("row"), .matrixcols(30), .matrixrows(2)) dotmatrix_91 (
    .row0(truckdriver_4_tobackground), .row1(truckdriver_4_tobackground_2));
  DotMatrix #(.inputtype("row"), .matrixcols(30), .matrixrows(10)) dotmatrix_92 (
    .row0(truckdriver_4_tofront), .row1(truckdriver_4_tofront_2), .row2(truckdriver_4_tofront_3),
    .row3(truckdriver_4_tofront_4), .row4(truckdriver_4_tofront_5), .row5(truckdriver_4_tofront_6),
    .row6(truckdriver_4_tofront_7), .row7(truckdriver_4_tofront_8), .row8(truckdriver_4_tofront_9),
    .row9(truckdriver_4_tofront_10));
  truckDriver truckdriver_4 (
    .inBackShiftD(truckdriver_2_outbackshiftd), .outBackShiftD(truckdriver_4_outbackshiftd),
    .inputBackShiftM(truckdriver_2_outputbackshiftm), .outputBackShiftM(truckdriver_4_outputbackshiftm),
    .inPlayerShiftD(truckdriver_2_outplayershiftd), .outPlayerShiftD(truckdriver_4_outplayershiftd),
    .inPlayerShiftM(truckdriver_2_outplayershiftm), .outPlayerShiftM(truckdriver_4_outplayershiftm),
    .inFlag(truckdriver_2_outflag), .outFlag(truckdriver_4_outflag),
    .toBackground(truckdriver_4_tobackground), .toBackground_2(truckdriver_4_tobackground_2),
    .toBackground_3(truckdriver_4_tobackground_3), .toBackground_4(truckdriver_4_tobackground_4),
    .toBackground_5(truckdriver_4_tobackground_5), .toBackground_6(truckdriver_4_tobackground_6),
    .toBackground_7(truckdriver_4_tobackground_7), .toBackground_8(truckdriver_4_tobackground_8),
    .toBackground_9(truckdriver_4_tobackground_9), .toBackground_10(truckdriver_4_tobackground_10),
    .toFront(truckdriver_4_tofront), .toFront_2(truckdriver_4_tofront_2),
    .toFront_3(truckdriver_4_tofront_3), .toFront_4(truckdriver_4_tofront_4),
    .toFront_5(truckdriver_4_tofront_5), .toFront_6(truckdriver_4_tofront_6),
    .toFront_7(truckdriver_4_tofront_7), .toFront_8(truckdriver_4_tofront_8),
    .toFront_9(truckdriver_4_tofront_9), .toFront_10(truckdriver_4_tofront_10));
  DotMatrix #(.inputtype("row"), .matrixcols(30), .matrixrows(6)) dotmatrix_93 (
    .row0(truckdriver_4_tobackground_3), .row1(truckdriver_4_tobackground_4),
    .row2(truckdriver_4_tobackground_5), .row3(truckdriver_4_tobackground_6),
    .row4(truckdriver_4_tobackground_7), .row5(truckdriver_4_tobackground_8));
  DotMatrix #(.inputtype("row"), .matrixcols(30), .matrixrows(2)) dotmatrix_94 (
    .row0(truckdriver_4_tobackground_9), .row1(truckdriver_4_tobackground_10));
  DotMatrix #(.inputtype("row"), .matrixcols(30), .matrixrows(3)) dotmatrix_95 (
    .row0(swampdriver_4_p6), .row1(swampdriver_4_p7), .row2(swampdriver_4_p8));
  // swampDriver swampdriver_4: pin names not known; wires that end beside it: swampdriver_2_p24, swampdriver_2_p25, swampdriver_2_p26, swampdriver_2_p27, swampdriver_2_p28, swampdriver_4_p6, swampdriver_4_p7, swampdriver_4_p8, swampdriver_4_p9, swampdriver_4_p10, swampdriver_4_p11, swampdriver_4_p12, swampdriver_4_p13, swampdriver_4_p14, swampdriver_4_p15, swampdriver_4_p16, swampdriver_4_p17, swampdriver_4_p18, swampdriver_4_p19, swampdriver_4_p20, swampdriver_4_p21, swampdriver_4_p22, swampdriver_4_p23, swampdriver_4_p24, swampdriver_4_p25, swampdriver_4_p26, swampdriver_4_p27, swampdriver_4_p28, swampdriver_4_p29, swampdriver_4_p30
  DotMatrix #(.inputtype("row"), .matrixcols(30), .matrixrows(10)) dotmatrix_96 (
    .row0(swampdriver_4_p16), .row1(swampdriver_4_p17), .row2(swampdriver_4_p18), .row3(swampdriver_4_p19),
    .row4(swampdriver_4_p20), .row5(swampdriver_4_p21), .row6(swampdriver_4_p22), .row7(swampdriver_4_p23),
    .row8(swampdriver_4_p24), .row9(swampdriver_4_p25));
  DotMatrix #(.inputtype("row"), .matrixcols(30), .matrixrows(4)) dotmatrix_97 (
    .row0(swampdriver_4_p9), .row1(swampdriver_4_p10), .row2(swampdriver_4_p11), .row3(swampdriver_4_p12));
  DotMatrix #(.inputtype("row"), .matrixcols(30), .matrixrows(3)) dotmatrix_98 (
    .row0(swampdriver_4_p13), .row1(swampdriver_4_p14), .row2(swampdriver_4_p15));
  set_interrupts set_interrupts_1 (
    .bump(bump), .rescue(rescue), .good_jump(good_jump), .IRQ(IRQ), .vector(vector), .clock(clock),
    .reset(restartGame), .IAck(IAck));
  or or_5 (res, restartGame, rescue, bump);
  DotMatrix #(.inputtype("row"), .matrixcols(30), .matrixrows(12)) dotmatrix_99 (
    .row0(finishconnector_3_tobackground), .row1(finishconnector_3_tobackground_2),
    .row2(finishconnector_3_tobackground_3), .row3(finishconnector_3_tobackground_4),
    .row4(finishconnector_3_tobackground_5), .row5(finishconnector_3_tobackground_6),
    .row6(finishconnector_3_tobackground_7), .row7(finishconnector_3_tobackground_8),
    .row8(finishconnector_3_tobackground_9), .row9(finishconnector_3_tobackground_10),
    .row10(finishconnector_3_tobackground_11), .row11(finishconnector_3_tobackground_12));
  finishConnector finishconnector_3 (
    .toBackground_3(finishconnector_3_tobackground_3), .toBackground_4(finishconnector_3_tobackground_4),
    .toBackground_5(finishconnector_3_tobackground_5), .toBackground_6(finishconnector_3_tobackground_6),
    .toBackground_7(finishconnector_3_tobackground_7), .toBackground_8(finishconnector_3_tobackground_8),
    .toBackground_9(finishconnector_3_tobackground_9), .toBackground_10(finishconnector_3_tobackground_10),
    .toBackground_11(finishconnector_3_tobackground_11), .toBackground_12(finishconnector_3_tobackground_12),
    .toBackground_2(finishconnector_3_tobackground_2), .toBackground(finishconnector_3_tobackground),
    .positions_2(finishconnector_3_positions_2), .circNumber_2(finishconnector_3_circnumber_2),
    .positions(finishconnector_2_positions_2), .circNumber(finishconnector_2_circnumber_2));
  log_2x1 log_2x1_3 (
    .inBackShiftD(log_2x1_2_outbackshiftd), .outBackShiftD(log_2x1_3_outbackshiftd),
    .inputBackShiftM(log_2x1_2_outputbackshiftm), .outputBackShiftM(log_2x1_3_outputbackshiftm),
    .inPlayerShiftD(log_2x1_2_outplayershiftd), .outPlayerShiftD(log_2x1_3_outplayershiftd),
    .inPlayerShiftM(log_2x1_2_outplayershiftm), .outPlayerShiftM(log_2x1_3_outplayershiftm),
    .inFlag(log_2x1_2_outflag), .outFlag(log_2x1_3_outflag), .toBackground(log_2x1_3_tobackground),
    .toBackground_2(log_2x1_3_tobackground_2), .toBackground_3(log_2x1_3_tobackground_3),
    .toBackground_4(log_2x1_3_tobackground_4), .toBackground_5(log_2x1_3_tobackground_5),
    .toBackground_6(log_2x1_3_tobackground_6), .toBackground_7(log_2x1_3_tobackground_7),
    .toBackground_8(log_2x1_3_tobackground_8), .toBackground_9(log_2x1_3_tobackground_9),
    .toBackground_10(log_2x1_3_tobackground_10), .toFront(log_2x1_3_tofront),
    .toFront_2(log_2x1_3_tofront_2), .toFront_3(log_2x1_3_tofront_3), .toFront_4(log_2x1_3_tofront_4),
    .toFront_5(log_2x1_3_tofront_5), .toFront_6(log_2x1_3_tofront_6), .toFront_7(log_2x1_3_tofront_7),
    .toFront_8(log_2x1_3_tofront_8), .toFront_9(log_2x1_3_tofront_9), .toFront_10(log_2x1_3_tofront_10));
  DotMatrix #(.inputtype("row"), .matrixcols(30), .matrixrows(10)) dotmatrix_100 (
    .row0(log_2x1_3_tofront), .row1(log_2x1_3_tofront_2), .row2(log_2x1_3_tofront_3),
    .row3(log_2x1_3_tofront_4), .row4(log_2x1_3_tofront_5), .row5(log_2x1_3_tofront_6),
    .row6(log_2x1_3_tofront_7), .row7(log_2x1_3_tofront_8), .row8(log_2x1_3_tofront_9),
    .row9(log_2x1_3_tofront_10));
  DotMatrix #(.inputtype("row"), .matrixcols(30), .matrixrows(3)) dotmatrix_101 (
    .row0(log_2x1_3_tobackground), .row1(log_2x1_3_tobackground_2), .row2(log_2x1_3_tobackground_3));
  DotMatrix #(.inputtype("row"), .matrixcols(30), .matrixrows(4)) dotmatrix_102 (
    .row0(log_2x1_3_tobackground_4), .row1(log_2x1_3_tobackground_5), .row2(log_2x1_3_tobackground_6),
    .row3(log_2x1_3_tobackground_7));
  DotMatrix #(.inputtype("row"), .matrixcols(30), .matrixrows(3)) dotmatrix_103 (
    .row0(log_2x1_3_tobackground_8), .row1(log_2x1_3_tobackground_9), .row2(log_2x1_3_tobackground_10));
  DotMatrix #(.inputtype("row"), .matrixcols(30), .matrixrows(10)) dotmatrix_104 (
    .row0(turtle_2x1_3_tofront), .row1(turtle_2x1_3_tofront_2), .row2(turtle_2x1_3_tofront_3),
    .row3(turtle_2x1_3_tofront_4), .row4(turtle_2x1_3_tofront_5), .row5(turtle_2x1_3_tofront_6),
    .row6(turtle_2x1_3_tofront_7), .row7(turtle_2x1_3_tofront_8), .row8(turtle_2x1_3_tofront_9),
    .row9(turtle_2x1_3_tofront_10));
  turtle_2x1 turtle_2x1_3 (
    .inPlayerShiftD(turtle_2x1_2_outplayershiftd), .outPlayerShiftD(turtle_2x1_3_outplayershiftd),
    .inPlayerShiftM(turtle_2x1_2_outplayershiftm), .outPlayerShiftM(turtle_2x1_3_outplayershiftm),
    .inFlag(turtle_2x1_2_outflag), .outFlag(turtle_2x1_3_outflag), .toBackground(turtle_2x1_3_tobackground),
    .toBackground_2(turtle_2x1_3_tobackground_2), .toBackground_3(turtle_2x1_3_tobackground_3),
    .toBackground_4(turtle_2x1_3_tobackground_4), .toBackground_5(turtle_2x1_3_tobackground_5),
    .toBackground_6(turtle_2x1_3_tobackground_6), .toBackground_7(turtle_2x1_3_tobackground_7),
    .toBackground_8(turtle_2x1_3_tobackground_8), .toBackground_9(turtle_2x1_3_tobackground_9),
    .toBackground_10(turtle_2x1_3_tobackground_10), .toFront(turtle_2x1_3_tofront),
    .toFront_2(turtle_2x1_3_tofront_2), .toFront_3(turtle_2x1_3_tofront_3),
    .toFront_4(turtle_2x1_3_tofront_4), .toFront_5(turtle_2x1_3_tofront_5),
    .toFront_6(turtle_2x1_3_tofront_6), .toFront_7(turtle_2x1_3_tofront_7),
    .toFront_8(turtle_2x1_3_tofront_8), .toFront_9(turtle_2x1_3_tofront_9),
    .toFront_10(turtle_2x1_3_tofront_10), .inBackShiftD(turtle_2x1_2_outbackshiftd),
    .outBackShiftD(turtle_2x1_3_outbackshiftd), .inputBackShiftM(turtle_2x1_2_outputbackshiftm),
    .outputBackShiftM(turtle_2x1_3_outputbackshiftm), .animState(turtle_2x1_2_animstate_2),
    .animState_2(turtle_2x1_3_animstate_2));
  DotMatrix #(.inputtype("row"), .matrixcols(30), .matrixrows(2)) dotmatrix_105 (
    .row0(turtle_2x1_3_tobackground), .row1(turtle_2x1_3_tobackground_2));
  DotMatrix #(.inputtype("row"), .matrixcols(30), .matrixrows(6)) dotmatrix_106 (
    .row0(turtle_2x1_3_tobackground_3), .row1(turtle_2x1_3_tobackground_4),
    .row2(turtle_2x1_3_tobackground_5), .row3(turtle_2x1_3_tobackground_6),
    .row4(turtle_2x1_3_tobackground_7), .row5(turtle_2x1_3_tobackground_8));
  DotMatrix #(.inputtype("row"), .matrixcols(30), .matrixrows(2)) dotmatrix_107 (
    .row0(turtle_2x1_3_tobackground_9), .row1(turtle_2x1_3_tobackground_10));
  log_3x2 log_3x2_3 (
    .inBackShiftD(log_3x2_2_outbackshiftd), .outBackShiftD(log_3x2_3_outbackshiftd),
    .inputBackShiftM(log_3x2_2_outputbackshiftm), .outputBackShiftM(log_3x2_3_outputbackshiftm),
    .inPlayerShiftD(log_3x2_2_outplayershiftd), .outPlayerShiftD(log_3x2_3_outplayershiftd),
    .inPlayerShiftM(log_3x2_2_outplayershiftm), .outPlayerShiftM(log_3x2_3_outplayershiftm),
    .inFlag(log_3x2_2_outflag), .outFlag(log_3x2_3_outflag), .toBackground(log_3x2_3_tobackground),
    .toBackground_2(log_3x2_3_tobackground_2), .toBackground_3(log_3x2_3_tobackground_3),
    .toBackground_4(log_3x2_3_tobackground_4), .toBackground_5(log_3x2_3_tobackground_5),
    .toBackground_6(log_3x2_3_tobackground_6), .toBackground_7(log_3x2_3_tobackground_7),
    .toBackground_8(log_3x2_3_tobackground_8), .toBackground_9(log_3x2_3_tobackground_9),
    .toBackground_10(log_3x2_3_tobackground_10), .toFront(log_3x2_3_tofront),
    .toFront_2(log_3x2_3_tofront_2), .toFront_3(log_3x2_3_tofront_3), .toFront_4(log_3x2_3_tofront_4),
    .toFront_5(log_3x2_3_tofront_5), .toFront_6(log_3x2_3_tofront_6), .toFront_7(log_3x2_3_tofront_7),
    .toFront_8(log_3x2_3_tofront_8), .toFront_9(log_3x2_3_tofront_9), .toFront_10(log_3x2_3_tofront_10));
  DotMatrix #(.inputtype("row"), .matrixcols(30), .matrixrows(10)) dotmatrix_108 (
    .row0(log_3x2_3_tofront), .row1(log_3x2_3_tofront_2), .row2(log_3x2_3_tofront_3),
    .row3(log_3x2_3_tofront_4), .row4(log_3x2_3_tofront_5), .row5(log_3x2_3_tofront_6),
    .row6(log_3x2_3_tofront_7), .row7(log_3x2_3_tofront_8), .row8(log_3x2_3_tofront_9),
    .row9(log_3x2_3_tofront_10));
  DotMatrix #(.inputtype("row"), .matrixcols(30), .matrixrows(3)) dotmatrix_109 (
    .row0(log_3x2_3_tobackground), .row1(log_3x2_3_tobackground_2), .row2(log_3x2_3_tobackground_3));
  DotMatrix #(.inputtype("row"), .matrixcols(30), .matrixrows(4)) dotmatrix_110 (
    .row0(log_3x2_3_tobackground_4), .row1(log_3x2_3_tobackground_5), .row2(log_3x2_3_tobackground_6),
    .row3(log_3x2_3_tobackground_7));
  DotMatrix #(.inputtype("row"), .matrixcols(30), .matrixrows(3)) dotmatrix_111 (
    .row0(log_3x2_3_tobackground_8), .row1(log_3x2_3_tobackground_9), .row2(log_3x2_3_tobackground_10));
  log_1x1 log_1x1_3 (
    .inBackShiftD(log_1x1_2_outbackshiftd), .outBackShiftD(log_1x1_3_outbackshiftd),
    .inputBackShiftM(log_1x1_2_outputbackshiftm), .outputBackShiftM(log_1x1_3_outputbackshiftm),
    .inPlayerShiftD(log_1x1_2_outplayershiftd), .outPlayerShiftD(log_1x1_3_outplayershiftd),
    .inPlayerShiftM(log_1x1_2_outplayershiftm), .outPlayerShiftM(log_1x1_3_outplayershiftm),
    .inFlag(log_1x1_2_outflag), .outFlag(log_1x1_3_outflag), .toBackground(log_1x1_3_tobackground),
    .toBackground_2(log_1x1_3_tobackground_2), .toBackground_3(log_1x1_3_tobackground_3),
    .toBackground_4(log_1x1_3_tobackground_4), .toBackground_5(log_1x1_3_tobackground_5),
    .toBackground_6(log_1x1_3_tobackground_6), .toBackground_7(log_1x1_3_tobackground_7),
    .toBackground_8(log_1x1_3_tobackground_8), .toBackground_9(log_1x1_3_tobackground_9),
    .toBackground_10(log_1x1_3_tobackground_10), .toFront(log_1x1_3_tofront),
    .toFront_2(log_1x1_3_tofront_2), .toFront_3(log_1x1_3_tofront_3), .toFront_4(log_1x1_3_tofront_4),
    .toFront_5(log_1x1_3_tofront_5), .toFront_6(log_1x1_3_tofront_6), .toFront_7(log_1x1_3_tofront_7),
    .toFront_8(log_1x1_3_tofront_8), .toFront_9(log_1x1_3_tofront_9), .toFront_10(log_1x1_3_tofront_10));
  DotMatrix #(.inputtype("row"), .matrixcols(30), .matrixrows(3)) dotmatrix_112 (
    .row0(log_1x1_3_tobackground), .row1(log_1x1_3_tobackground_2), .row2(log_1x1_3_tobackground_3));
  DotMatrix #(.inputtype("row"), .matrixcols(30), .matrixrows(10)) dotmatrix_113 (
    .row0(log_1x1_3_tofront), .row1(log_1x1_3_tofront_2), .row2(log_1x1_3_tofront_3),
    .row3(log_1x1_3_tofront_4), .row4(log_1x1_3_tofront_5), .row5(log_1x1_3_tofront_6),
    .row6(log_1x1_3_tofront_7), .row7(log_1x1_3_tofront_8), .row8(log_1x1_3_tofront_9),
    .row9(log_1x1_3_tofront_10));
  DotMatrix #(.inputtype("row"), .matrixcols(30), .matrixrows(4)) dotmatrix_114 (
    .row0(log_1x1_3_tobackground_4), .row1(log_1x1_3_tobackground_5), .row2(log_1x1_3_tobackground_6),
    .row3(log_1x1_3_tobackground_7));
  DotMatrix #(.inputtype("row"), .matrixcols(30), .matrixrows(3)) dotmatrix_115 (
    .row0(log_1x1_3_tobackground_8), .row1(log_1x1_3_tobackground_9), .row2(log_1x1_3_tobackground_10));
  DotMatrix #(.inputtype("row"), .matrixcols(30), .matrixrows(2)) dotmatrix_116 (
    .row0(turtle_3x1_3_tobackground), .row1(turtle_3x1_3_tobackground_2));
  DotMatrix #(.inputtype("row"), .matrixcols(30), .matrixrows(10)) dotmatrix_117 (
    .row0(turtle_3x1_3_tofront), .row1(turtle_3x1_3_tofront_2), .row2(turtle_3x1_3_tofront_3),
    .row3(turtle_3x1_3_tofront_4), .row4(turtle_3x1_3_tofront_5), .row5(turtle_3x1_3_tofront_6),
    .row6(turtle_3x1_3_tofront_7), .row7(turtle_3x1_3_tofront_8), .row8(turtle_3x1_3_tofront_9),
    .row9(turtle_3x1_3_tofront_10));
  turtle_3x1 turtle_3x1_3 (
    .inBackShiftD(turtle_3x1_2_outbackshiftd), .outBackShiftD(turtle_3x1_3_outbackshiftd),
    .inputBackShiftM(turtle_3x1_2_outputbackshiftm), .outputBackShiftM(turtle_3x1_3_outputbackshiftm),
    .inPlayerShiftD(turtle_3x1_2_outplayershiftd), .outPlayerShiftD(turtle_3x1_3_outplayershiftd),
    .inPlayerShiftM(turtle_3x1_2_outplayershiftm), .outPlayerShiftM(turtle_3x1_3_outplayershiftm),
    .inFlag(turtle_3x1_2_outflag), .outFlag(turtle_3x1_3_outflag), .toBackground(turtle_3x1_3_tobackground),
    .toBackground_2(turtle_3x1_3_tobackground_2), .toBackground_3(turtle_3x1_3_tobackground_3),
    .toBackground_4(turtle_3x1_3_tobackground_4), .toBackground_5(turtle_3x1_3_tobackground_5),
    .toBackground_6(turtle_3x1_3_tobackground_6), .toBackground_7(turtle_3x1_3_tobackground_7),
    .toBackground_8(turtle_3x1_3_tobackground_8), .toBackground_9(turtle_3x1_3_tobackground_9),
    .toBackground_10(turtle_3x1_3_tobackground_10), .toFront(turtle_3x1_3_tofront),
    .toFront_2(turtle_3x1_3_tofront_2), .toFront_3(turtle_3x1_3_tofront_3),
    .toFront_4(turtle_3x1_3_tofront_4), .toFront_5(turtle_3x1_3_tofront_5),
    .toFront_6(turtle_3x1_3_tofront_6), .toFront_7(turtle_3x1_3_tofront_7),
    .toFront_8(turtle_3x1_3_tofront_8), .toFront_9(turtle_3x1_3_tofront_9),
    .toFront_10(turtle_3x1_3_tofront_10), .animState(turtle_3x1_2_animstate_2),
    .animState_2(turtle_3x1_3_animstate_2));
  DotMatrix #(.inputtype("row"), .matrixcols(30), .matrixrows(6)) dotmatrix_118 (
    .row0(turtle_3x1_3_tobackground_3), .row1(turtle_3x1_3_tobackground_4),
    .row2(turtle_3x1_3_tobackground_5), .row3(turtle_3x1_3_tobackground_6),
    .row4(turtle_3x1_3_tobackground_7), .row5(turtle_3x1_3_tobackground_8));
  DotMatrix #(.inputtype("row"), .matrixcols(30), .matrixrows(2)) dotmatrix_119 (
    .row0(turtle_3x1_3_tobackground_9), .row1(turtle_3x1_3_tobackground_10));
  DotMatrix #(.inputtype("row"), .matrixcols(30), .matrixrows(10)) dotmatrix_120 (
    .row0(swampdriver_5_p17), .row1(swampdriver_5_p18), .row2(swampdriver_5_p19), .row3(swampdriver_5_p20),
    .row4(swampdriver_5_p21), .row5(swampdriver_5_p22), .row6(swampdriver_5_p23), .row7(swampdriver_5_p24),
    .row8(swampdriver_5_p25), .row9(swampdriver_5_p26));
  DotMatrix #(.inputtype("row"), .matrixcols(30), .matrixrows(3)) dotmatrix_121 (
    .row0(swampdriver_5_p7), .row1(swampdriver_5_p8), .row2(swampdriver_5_p9));
  // swampDriver swampdriver_5: pin names not known; wires that end beside it: swampdriver_3_p26, swampdriver_3_p27, swampdriver_3_p28, swampdriver_3_p29, swampdriver_3_p30, turtle_3x1_2_outflag, swampdriver_5_p7, swampdriver_5_p8, swampdriver_5_p9, swampdriver_5_p10, swampdriver_5_p11, swampdriver_5_p12, swampdriver_5_p13, swampdriver_5_p14, swampdriver_5_p15, swampdriver_5_p16, swampdriver_5_p17, swampdriver_5_p18, swampdriver_5_p19, swampdriver_5_p20, swampdriver_5_p21, swampdriver_5_p22, swampdriver_5_p23, swampdriver_5_p24, swampdriver_5_p25, swampdriver_5_p26, swampdriver_5_p27, swampdriver_5_p28, swampdriver_5_p29, swampdriver_5_p30, swampdriver_5_p31
  DotMatrix #(.inputtype("row"), .matrixcols(30), .matrixrows(4)) dotmatrix_122 (
    .row0(swampdriver_5_p10), .row1(swampdriver_5_p11), .row2(swampdriver_5_p12), .row3(swampdriver_5_p13));
  DotMatrix #(.inputtype("row"), .matrixcols(30), .matrixrows(3)) dotmatrix_123 (
    .row0(swampdriver_5_p14), .row1(swampdriver_5_p15), .row2(swampdriver_5_p16));
  DotMatrix #(.inputtype("row"), .matrixcols(30), .matrixrows(10)) dotmatrix_124 (
    .row0(truckdriver_5_tofront), .row1(truckdriver_5_tofront_2), .row2(truckdriver_5_tofront_3),
    .row3(truckdriver_5_tofront_4), .row4(truckdriver_5_tofront_5), .row5(truckdriver_5_tofront_6),
    .row6(truckdriver_5_tofront_7), .row7(truckdriver_5_tofront_8), .row8(truckdriver_5_tofront_9),
    .row9(truckdriver_5_tofront_10));
  truckDriver truckdriver_5 (
    .inBackShiftD(truckdriver_3_outbackshiftd), .outBackShiftD(truckdriver_5_outbackshiftd),
    .inputBackShiftM(truckdriver_3_outputbackshiftm), .outputBackShiftM(truckdriver_5_outputbackshiftm),
    .inPlayerShiftD(truckdriver_3_outplayershiftd), .outPlayerShiftD(truckdriver_5_outplayershiftd),
    .inPlayerShiftM(truckdriver_3_outplayershiftm), .outPlayerShiftM(truckdriver_5_outplayershiftm),
    .inFlag(truckdriver_3_outflag), .outFlag(truckdriver_5_outflag),
    .toBackground(truckdriver_5_tobackground), .toBackground_2(truckdriver_5_tobackground_2),
    .toBackground_3(truckdriver_5_tobackground_3), .toBackground_4(truckdriver_5_tobackground_4),
    .toBackground_5(truckdriver_5_tobackground_5), .toBackground_6(truckdriver_5_tobackground_6),
    .toBackground_7(truckdriver_5_tobackground_7), .toBackground_8(truckdriver_5_tobackground_8),
    .toBackground_9(truckdriver_5_tobackground_9), .toBackground_10(truckdriver_5_tobackground_10),
    .toFront(truckdriver_5_tofront), .toFront_2(truckdriver_5_tofront_2),
    .toFront_3(truckdriver_5_tofront_3), .toFront_4(truckdriver_5_tofront_4),
    .toFront_5(truckdriver_5_tofront_5), .toFront_6(truckdriver_5_tofront_6),
    .toFront_7(truckdriver_5_tofront_7), .toFront_8(truckdriver_5_tofront_8),
    .toFront_9(truckdriver_5_tofront_9), .toFront_10(truckdriver_5_tofront_10));
  DotMatrix #(.inputtype("row"), .matrixcols(30), .matrixrows(2)) dotmatrix_125 (
    .row0(truckdriver_5_tobackground), .row1(truckdriver_5_tobackground_2));
  DotMatrix #(.inputtype("row"), .matrixcols(30), .matrixrows(6)) dotmatrix_126 (
    .row0(truckdriver_5_tobackground_3), .row1(truckdriver_5_tobackground_4),
    .row2(truckdriver_5_tobackground_5), .row3(truckdriver_5_tobackground_6),
    .row4(truckdriver_5_tobackground_7), .row5(truckdriver_5_tobackground_8));
  DotMatrix #(.inputtype("row"), .matrixcols(30), .matrixrows(2)) dotmatrix_127 (
    .row0(truckdriver_5_tobackground_9), .row1(truckdriver_5_tobackground_10));
  DotMatrix #(.inputtype("row"), .matrixcols(30), .matrixrows(2)) dotmatrix_128 (
    .row0(carconnectorv2_3_tobackground), .row1(carconnectorv2_3_tobackground_2));
  DotMatrix #(.inputtype("row"), .matrixcols(30), .matrixrows(10)) dotmatrix_129 (
    .row0(carconnectorv2_3_tofront), .row1(carconnectorv2_3_tofront_2), .row2(carconnectorv2_3_tofront_3),
    .row3(carconnectorv2_3_tofront_4), .row4(carconnectorv2_3_tofront_5), .row5(carconnectorv2_3_tofront_6),
    .row6(carconnectorv2_3_tofront_7), .row7(carconnectorv2_3_tofront_8), .row8(carconnectorv2_3_tofront_9),
    .row9(carconnectorv2_3_tofront_10));
  carConnectorV2 carconnectorv2_3 (
    .inBackShiftD(carconnectorv2_2_outbackshiftd), .outBackShiftD(carconnectorv2_3_outbackshiftd),
    .inputBackShiftM(carconnectorv2_2_outputbackshiftm),
    .outputBackShiftM(carconnectorv2_3_outputbackshiftm), .outPlayerShiftD(carconnectorv2_3_outplayershiftd),
    .inPlayerShiftM(carconnectorv2_2_outplayershiftm), .outPlayerShiftM(carconnectorv2_3_outplayershiftm),
    .inFlag(carconnectorv2_2_outflag), .outFlag(carconnectorv2_3_outflag),
    .toBackground(carconnectorv2_3_tobackground), .toBackground_2(carconnectorv2_3_tobackground_2),
    .toBackground_3(carconnectorv2_3_tobackground_3), .toBackground_4(carconnectorv2_3_tobackground_4),
    .toBackground_5(carconnectorv2_3_tobackground_5), .toBackground_6(carconnectorv2_3_tobackground_6),
    .toBackground_7(carconnectorv2_3_tobackground_7), .toBackground_8(carconnectorv2_3_tobackground_8),
    .toBackground_9(carconnectorv2_3_tobackground_9), .toBackground_10(carconnectorv2_3_tobackground_10),
    .toFront(carconnectorv2_3_tofront), .toFront_2(carconnectorv2_3_tofront_2),
    .toFront_3(carconnectorv2_3_tofront_3), .toFront_4(carconnectorv2_3_tofront_4),
    .toFront_5(carconnectorv2_3_tofront_5), .toFront_6(carconnectorv2_3_tofront_6),
    .toFront_7(carconnectorv2_3_tofront_7), .toFront_8(carconnectorv2_3_tofront_8),
    .toFront_9(carconnectorv2_3_tofront_9), .toFront_10(carconnectorv2_3_tofront_10),
    .inPlayerShiftD(carconnectorv2_2_outplayershiftd));
  DotMatrix #(.inputtype("row"), .matrixcols(30), .matrixrows(6)) dotmatrix_130 (
    .row0(carconnectorv2_3_tobackground_3), .row1(carconnectorv2_3_tobackground_4),
    .row2(carconnectorv2_3_tobackground_5), .row3(carconnectorv2_3_tobackground_6),
    .row4(carconnectorv2_3_tobackground_7), .row5(carconnectorv2_3_tobackground_8));
  DotMatrix #(.inputtype("row"), .matrixcols(30), .matrixrows(2)) dotmatrix_131 (
    .row0(carconnectorv2_3_tobackground_9), .row1(carconnectorv2_3_tobackground_10));
  DotMatrix #(.inputtype("row"), .matrixcols(30), .matrixrows(10)) dotmatrix_132 (
    .row0(boliddriver_3_tofront), .row1(boliddriver_3_tofront_2), .row2(boliddriver_3_tofront_3),
    .row3(boliddriver_3_tofront_4), .row4(boliddriver_3_tofront_5), .row5(boliddriver_3_tofront_6),
    .row6(boliddriver_3_tofront_7), .row7(boliddriver_3_tofront_8), .row8(boliddriver_3_tofront_9),
    .row9(boliddriver_3_tofront_10));
  bolidDriver boliddriver_3 (
    .inBackShiftD(boliddriver_2_outbackshiftd), .outBackShiftD(boliddriver_3_outbackshiftd),
    .inputBackShiftM(boliddriver_2_outputbackshiftm), .outputBackShiftM(boliddriver_3_outputbackshiftm),
    .inPlayerShiftD(boliddriver_2_outplayershiftd), .outPlayerShiftD(boliddriver_3_outplayershiftd),
    .inPlayerShiftM(boliddriver_2_outplayershiftm), .outPlayerShiftM(boliddriver_3_outplayershiftm),
    .inFlag(boliddriver_2_outflag), .outFlag(boliddriver_3_outflag),
    .toBackground(boliddriver_3_tobackground), .toBackground_2(boliddriver_3_tobackground_2),
    .toBackground_3(boliddriver_3_tobackground_3), .toBackground_4(boliddriver_3_tobackground_4),
    .toBackground_5(boliddriver_3_tobackground_5), .toBackground_6(boliddriver_3_tobackground_6),
    .toBackground_7(boliddriver_3_tobackground_7), .toBackground_8(boliddriver_3_tobackground_8),
    .toBackground_9(boliddriver_3_tobackground_9), .toBackground_10(boliddriver_3_tobackground_10),
    .toFront(boliddriver_3_tofront), .toFront_2(boliddriver_3_tofront_2),
    .toFront_3(boliddriver_3_tofront_3), .toFront_4(boliddriver_3_tofront_4),
    .toFront_5(boliddriver_3_tofront_5), .toFront_6(boliddriver_3_tofront_6),
    .toFront_7(boliddriver_3_tofront_7), .toFront_8(boliddriver_3_tofront_8),
    .toFront_9(boliddriver_3_tofront_9), .toFront_10(boliddriver_3_tofront_10));
  DotMatrix #(.inputtype("row"), .matrixcols(30), .matrixrows(2)) dotmatrix_133 (
    .row0(boliddriver_3_tobackground), .row1(boliddriver_3_tobackground_2));
  DotMatrix #(.inputtype("row"), .matrixcols(30), .matrixrows(6)) dotmatrix_134 (
    .row0(boliddriver_3_tobackground_3), .row1(boliddriver_3_tobackground_4),
    .row2(boliddriver_3_tobackground_5), .row3(boliddriver_3_tobackground_6),
    .row4(boliddriver_3_tobackground_7), .row5(boliddriver_3_tobackground_8));
  DotMatrix #(.inputtype("row"), .matrixcols(30), .matrixrows(2)) dotmatrix_135 (
    .row0(boliddriver_3_tobackground_9), .row1(boliddriver_3_tobackground_10));
  DotMatrix #(.inputtype("row"), .matrixcols(30), .matrixrows(10)) dotmatrix_136 (
    .row0(suvdriver_3_tofront), .row1(suvdriver_3_tofront_2), .row2(suvdriver_3_tofront_3),
    .row3(suvdriver_3_tofront_4), .row4(suvdriver_3_tofront_5), .row5(suvdriver_3_tofront_6),
    .row6(suvdriver_3_tofront_7), .row7(suvdriver_3_tofront_8), .row8(suvdriver_3_tofront_9),
    .row9(suvdriver_3_tofront_10));
  DotMatrix #(.inputtype("row"), .matrixcols(30), .matrixrows(2)) dotmatrix_137 (
    .row0(suvdriver_3_tobackground), .row1(suvdriver_3_tobackground_2));
  SUVDriver suvdriver_3 (
    .inBackShiftD(suvdriver_2_outbackshiftd), .outBackShiftD(suvdriver_3_outbackshiftd),
    .inputBackShiftM(suvdriver_2_outputbackshiftm), .outputBackShiftM(suvdriver_3_outputbackshiftm),
    .inPlayerShiftD(suvdriver_2_outplayershiftd), .outPlayerShiftD(suvdriver_3_outplayershiftd),
    .inPlayerShiftM(suvdriver_2_outplayershiftm), .outPlayerShiftM(suvdriver_3_outplayershiftm),
    .inFlag(suvdriver_2_outflag), .outFlag(suvdriver_3_outflag), .toBackground(suvdriver_3_tobackground),
    .toBackground_2(suvdriver_3_tobackground_2), .toBackground_3(suvdriver_3_tobackground_3),
    .toBackground_4(suvdriver_3_tobackground_4), .toBackground_5(suvdriver_3_tobackground_5),
    .toBackground_6(suvdriver_3_tobackground_6), .toBackground_7(suvdriver_3_tobackground_7),
    .toBackground_8(suvdriver_3_tobackground_8), .toBackground_9(suvdriver_3_tobackground_9),
    .toBackground_10(suvdriver_3_tobackground_10), .toFront(suvdriver_3_tofront),
    .toFront_2(suvdriver_3_tofront_2), .toFront_3(suvdriver_3_tofront_3), .toFront_4(suvdriver_3_tofront_4),
    .toFront_5(suvdriver_3_tofront_5), .toFront_6(suvdriver_3_tofront_6), .toFront_7(suvdriver_3_tofront_7),
    .toFront_8(suvdriver_3_tofront_8), .toFront_9(suvdriver_3_tofront_9), .toFront_10(suvdriver_3_tofront_10));
  DotMatrix #(.inputtype("row"), .matrixcols(30), .matrixrows(6)) dotmatrix_138 (
    .row0(suvdriver_3_tobackground_3), .row1(suvdriver_3_tobackground_4), .row2(suvdriver_3_tobackground_5),
    .row3(suvdriver_3_tobackground_6), .row4(suvdriver_3_tobackground_7), .row5(suvdriver_3_tobackground_8));
  DotMatrix #(.inputtype("row"), .matrixcols(30), .matrixrows(2)) dotmatrix_139 (
    .row0(suvdriver_3_tobackground_9), .row1(suvdriver_3_tobackground_10));
  DotMatrix #(.inputtype("row"), .matrixcols(30), .matrixrows(10)) dotmatrix_140 (
    .row0(truckdriver_6_tofront), .row1(truckdriver_6_tofront_2), .row2(truckdriver_6_tofront_3),
    .row3(truckdriver_6_tofront_4), .row4(truckdriver_6_tofront_5), .row5(truckdriver_6_tofront_6),
    .row6(truckdriver_6_tofront_7), .row7(truckdriver_6_tofront_8), .row8(truckdriver_6_tofront_9),
    .row9(truckdriver_6_tofront_10));
  DotMatrix #(.inputtype("row"), .matrixcols(30), .matrixrows(2)) dotmatrix_141 (
    .row0(truckdriver_6_tobackground), .row1(truckdriver_6_tobackground_2));
  truckDriver truckdriver_6 (
    .inBackShiftD(truckdriver_4_outbackshiftd), .outBackShiftD(truckdriver_6_outbackshiftd),
    .inputBackShiftM(truckdriver_4_outputbackshiftm), .outputBackShiftM(truckdriver_6_outputbackshiftm),
    .inPlayerShiftD(truckdriver_4_outplayershiftd), .outPlayerShiftD(truckdriver_6_outplayershiftd),
    .inPlayerShiftM(truckdriver_4_outplayershiftm), .outPlayerShiftM(truckdriver_6_outplayershiftm),
    .inFlag(truckdriver_4_outflag), .outFlag(truckdriver_6_outflag),
    .toBackground(truckdriver_6_tobackground), .toBackground_2(truckdriver_6_tobackground_2),
    .toBackground_3(truckdriver_6_tobackground_3), .toBackground_4(truckdriver_6_tobackground_4),
    .toBackground_5(truckdriver_6_tobackground_5), .toBackground_6(truckdriver_6_tobackground_6),
    .toBackground_7(truckdriver_6_tobackground_7), .toBackground_8(truckdriver_6_tobackground_8),
    .toBackground_9(truckdriver_6_tobackground_9), .toBackground_10(truckdriver_6_tobackground_10),
    .toFront(truckdriver_6_tofront), .toFront_2(truckdriver_6_tofront_2),
    .toFront_3(truckdriver_6_tofront_3), .toFront_4(truckdriver_6_tofront_4),
    .toFront_5(truckdriver_6_tofront_5), .toFront_6(truckdriver_6_tofront_6),
    .toFront_7(truckdriver_6_tofront_7), .toFront_8(truckdriver_6_tofront_8),
    .toFront_9(truckdriver_6_tofront_9), .toFront_10(truckdriver_6_tofront_10));
  DotMatrix #(.inputtype("row"), .matrixcols(30), .matrixrows(6)) dotmatrix_142 (
    .row0(truckdriver_6_tobackground_3), .row1(truckdriver_6_tobackground_4),
    .row2(truckdriver_6_tobackground_5), .row3(truckdriver_6_tobackground_6),
    .row4(truckdriver_6_tobackground_7), .row5(truckdriver_6_tobackground_8));
  DotMatrix #(.inputtype("row"), .matrixcols(30), .matrixrows(2)) dotmatrix_143 (
    .row0(truckdriver_6_tobackground_9), .row1(truckdriver_6_tobackground_10));
  DotMatrix #(.inputtype("row"), .matrixcols(30), .matrixrows(10)) dotmatrix_144 (
    .row0(swampdriver_6_p16), .row1(swampdriver_6_p17), .row2(swampdriver_6_p18), .row3(swampdriver_6_p19),
    .row4(swampdriver_6_p20), .row5(swampdriver_6_p21), .row6(swampdriver_6_p22), .row7(swampdriver_6_p23),
    .row8(swampdriver_6_p24), .row9(swampdriver_6_p25));
  DotMatrix #(.inputtype("row"), .matrixcols(30), .matrixrows(3)) dotmatrix_145 (
    .row0(swampdriver_6_p6), .row1(swampdriver_6_p7), .row2(swampdriver_6_p8));
  // swampDriver swampdriver_6: pin names not known; wires that end beside it: swampdriver_4_p26, swampdriver_4_p27, swampdriver_4_p28, swampdriver_4_p29, swampdriver_4_p30, swampdriver_6_p6, swampdriver_6_p7, swampdriver_6_p8, swampdriver_6_p9, swampdriver_6_p10, swampdriver_6_p11, swampdriver_6_p12, swampdriver_6_p13, swampdriver_6_p14, swampdriver_6_p15, swampdriver_6_p16, swampdriver_6_p17, swampdriver_6_p18, swampdriver_6_p19, swampdriver_6_p20, swampdriver_6_p21, swampdriver_6_p22, swampdriver_6_p23, swampdriver_6_p24, swampdriver_6_p25, swampdriver_6_p26, swampdriver_6_p27, swampdriver_6_p28, swampdriver_6_p29, swampdriver_6_p30
  DotMatrix #(.inputtype("row"), .matrixcols(30), .matrixrows(4)) dotmatrix_146 (
    .row0(swampdriver_6_p9), .row1(swampdriver_6_p10), .row2(swampdriver_6_p11), .row3(swampdriver_6_p12));
  DotMatrix #(.inputtype("row"), .matrixcols(30), .matrixrows(3)) dotmatrix_147 (
    .row0(swampdriver_6_p13), .row1(swampdriver_6_p14), .row2(swampdriver_6_p15));
  max_height max_height_1 (.clock(clock), .reset(res), .max_height(max_height_1_max_height), .current_height(Y));
  good_jump good_jump_1 (
    .current_max_height(max_height_1_max_height), .clock(clock), .clear(res), .good_jump(good_jump));
  DotMatrix #(.inputtype("row"), .matrixcols(30), .matrixrows(12)) dotmatrix_148 (
    .row0(finishconnector_4_tobackground), .row1(finishconnector_4_tobackground_2),
    .row2(finishconnector_4_tobackground_3), .row3(finishconnector_4_tobackground_4),
    .row4(finishconnector_4_tobackground_5), .row5(finishconnector_4_tobackground_6),
    .row6(finishconnector_4_tobackground_7), .row7(finishconnector_4_tobackground_8),
    .row8(finishconnector_4_tobackground_9), .row9(finishconnector_4_tobackground_10),
    .row10(finishconnector_4_tobackground_11), .row11(finishconnector_4_tobackground_12));
  finishConnector finishconnector_4 (
    .toBackground_3(finishconnector_4_tobackground_3), .toBackground_4(finishconnector_4_tobackground_4),
    .toBackground_5(finishconnector_4_tobackground_5), .toBackground_6(finishconnector_4_tobackground_6),
    .toBackground_7(finishconnector_4_tobackground_7), .toBackground_8(finishconnector_4_tobackground_8),
    .toBackground_9(finishconnector_4_tobackground_9), .toBackground_10(finishconnector_4_tobackground_10),
    .toBackground_11(finishconnector_4_tobackground_11), .toBackground_12(finishconnector_4_tobackground_12),
    .toBackground_2(finishconnector_4_tobackground_2), .toBackground(finishconnector_4_tobackground),
    .positions_2(finishconnector_4_positions_2), .circNumber_2(finishconnector_4_circnumber_2),
    .positions(finishconnector_3_positions_2), .circNumber(finishconnector_3_circnumber_2));
  DotMatrix #(.inputtype("row"), .matrixcols(30), .matrixrows(10)) dotmatrix_149 (
    .row0(log_2x1_4_tofront), .row1(log_2x1_4_tofront_2), .row2(log_2x1_4_tofront_3),
    .row3(log_2x1_4_tofront_4), .row4(log_2x1_4_tofront_5), .row5(log_2x1_4_tofront_6),
    .row6(log_2x1_4_tofront_7), .row7(log_2x1_4_tofront_8), .row8(log_2x1_4_tofront_9),
    .row9(log_2x1_4_tofront_10));
  log_2x1 log_2x1_4 (
    .inBackShiftD(log_2x1_3_outbackshiftd), .outBackShiftD(log_2x1_4_outbackshiftd),
    .inputBackShiftM(log_2x1_3_outputbackshiftm), .outputBackShiftM(log_2x1_4_outputbackshiftm),
    .inPlayerShiftD(log_2x1_3_outplayershiftd), .outPlayerShiftD(log_2x1_4_outplayershiftd),
    .inPlayerShiftM(log_2x1_3_outplayershiftm), .outPlayerShiftM(log_2x1_4_outplayershiftm),
    .inFlag(log_2x1_3_outflag), .outFlag(log_2x1_4_outflag), .toBackground(log_2x1_4_tobackground),
    .toBackground_2(log_2x1_4_tobackground_2), .toBackground_3(log_2x1_4_tobackground_3),
    .toBackground_4(log_2x1_4_tobackground_4), .toBackground_5(log_2x1_4_tobackground_5),
    .toBackground_6(log_2x1_4_tobackground_6), .toBackground_7(log_2x1_4_tobackground_7),
    .toBackground_8(log_2x1_4_tobackground_8), .toBackground_9(log_2x1_4_tobackground_9),
    .toBackground_10(log_2x1_4_tobackground_10), .toFront(log_2x1_4_tofront),
    .toFront_2(log_2x1_4_tofront_2), .toFront_3(log_2x1_4_tofront_3), .toFront_4(log_2x1_4_tofront_4),
    .toFront_5(log_2x1_4_tofront_5), .toFront_6(log_2x1_4_tofront_6), .toFront_7(log_2x1_4_tofront_7),
    .toFront_8(log_2x1_4_tofront_8), .toFront_9(log_2x1_4_tofront_9), .toFront_10(log_2x1_4_tofront_10));
  DotMatrix #(.inputtype("row"), .matrixcols(30), .matrixrows(3)) dotmatrix_150 (
    .row0(log_2x1_4_tobackground), .row1(log_2x1_4_tobackground_2), .row2(log_2x1_4_tobackground_3));
  DotMatrix #(.inputtype("row"), .matrixcols(30), .matrixrows(4)) dotmatrix_151 (
    .row0(log_2x1_4_tobackground_4), .row1(log_2x1_4_tobackground_5), .row2(log_2x1_4_tobackground_6),
    .row3(log_2x1_4_tobackground_7));
  DotMatrix #(.inputtype("row"), .matrixcols(30), .matrixrows(3)) dotmatrix_152 (
    .row0(log_2x1_4_tobackground_8), .row1(log_2x1_4_tobackground_9), .row2(log_2x1_4_tobackground_10));
  turtle_2x1 turtle_2x1_4 (
    .inPlayerShiftD(turtle_2x1_3_outplayershiftd), .outPlayerShiftD(turtle_2x1_4_outplayershiftd),
    .inPlayerShiftM(turtle_2x1_3_outplayershiftm), .outPlayerShiftM(turtle_2x1_4_outplayershiftm),
    .inFlag(turtle_2x1_3_outflag), .outFlag(turtle_2x1_4_outflag), .toBackground(turtle_2x1_4_tobackground),
    .toBackground_2(turtle_2x1_4_tobackground_2), .toBackground_3(turtle_2x1_4_tobackground_3),
    .toBackground_4(turtle_2x1_4_tobackground_4), .toBackground_5(turtle_2x1_4_tobackground_5),
    .toBackground_6(turtle_2x1_4_tobackground_6), .toBackground_7(turtle_2x1_4_tobackground_7),
    .toBackground_8(turtle_2x1_4_tobackground_8), .toBackground_9(turtle_2x1_4_tobackground_9),
    .toBackground_10(turtle_2x1_4_tobackground_10), .toFront(turtle_2x1_4_tofront),
    .toFront_2(turtle_2x1_4_tofront_2), .toFront_3(turtle_2x1_4_tofront_3),
    .toFront_4(turtle_2x1_4_tofront_4), .toFront_5(turtle_2x1_4_tofront_5),
    .toFront_6(turtle_2x1_4_tofront_6), .toFront_7(turtle_2x1_4_tofront_7),
    .toFront_8(turtle_2x1_4_tofront_8), .toFront_9(turtle_2x1_4_tofront_9),
    .toFront_10(turtle_2x1_4_tofront_10), .inBackShiftD(turtle_2x1_3_outbackshiftd),
    .outBackShiftD(turtle_2x1_4_outbackshiftd), .inputBackShiftM(turtle_2x1_3_outputbackshiftm),
    .outputBackShiftM(turtle_2x1_4_outputbackshiftm), .animState(turtle_2x1_3_animstate_2));  // open: animState_2
  DotMatrix #(.inputtype("row"), .matrixcols(30), .matrixrows(2)) dotmatrix_153 (
    .row0(turtle_2x1_4_tobackground), .row1(turtle_2x1_4_tobackground_2));
  DotMatrix #(.inputtype("row"), .matrixcols(30), .matrixrows(10)) dotmatrix_154 (
    .row0(turtle_2x1_4_tofront), .row1(turtle_2x1_4_tofront_2), .row2(turtle_2x1_4_tofront_3),
    .row3(turtle_2x1_4_tofront_4), .row4(turtle_2x1_4_tofront_5), .row5(turtle_2x1_4_tofront_6),
    .row6(turtle_2x1_4_tofront_7), .row7(turtle_2x1_4_tofront_8), .row8(turtle_2x1_4_tofront_9),
    .row9(turtle_2x1_4_tofront_10));
  DotMatrix #(.inputtype("row"), .matrixcols(30), .matrixrows(6)) dotmatrix_155 (
    .row0(turtle_2x1_4_tobackground_3), .row1(turtle_2x1_4_tobackground_4),
    .row2(turtle_2x1_4_tobackground_5), .row3(turtle_2x1_4_tobackground_6),
    .row4(turtle_2x1_4_tobackground_7), .row5(turtle_2x1_4_tobackground_8));
  DotMatrix #(.inputtype("row"), .matrixcols(30), .matrixrows(2)) dotmatrix_156 (
    .row0(turtle_2x1_4_tobackground_9), .row1(turtle_2x1_4_tobackground_10));
  DotMatrix #(.inputtype("row"), .matrixcols(30), .matrixrows(10)) dotmatrix_157 (
    .row0(log_3x2_4_tofront), .row1(log_3x2_4_tofront_2), .row2(log_3x2_4_tofront_3),
    .row3(log_3x2_4_tofront_4), .row4(log_3x2_4_tofront_5), .row5(log_3x2_4_tofront_6),
    .row6(log_3x2_4_tofront_7), .row7(log_3x2_4_tofront_8), .row8(log_3x2_4_tofront_9),
    .row9(log_3x2_4_tofront_10));
  DotMatrix #(.inputtype("row"), .matrixcols(30), .matrixrows(3)) dotmatrix_158 (
    .row0(log_3x2_4_tobackground), .row1(log_3x2_4_tobackground_2), .row2(log_3x2_4_tobackground_3));
  log_3x2 log_3x2_4 (
    .inBackShiftD(log_3x2_3_outbackshiftd), .outBackShiftD(log_3x2_4_outbackshiftd),
    .inputBackShiftM(log_3x2_3_outputbackshiftm), .outputBackShiftM(log_3x2_4_outputbackshiftm),
    .inPlayerShiftD(log_3x2_3_outplayershiftd), .outPlayerShiftD(log_3x2_4_outplayershiftd),
    .inPlayerShiftM(log_3x2_3_outplayershiftm), .outPlayerShiftM(log_3x2_4_outplayershiftm),
    .inFlag(log_3x2_3_outflag), .outFlag(log_3x2_4_outflag), .toBackground(log_3x2_4_tobackground),
    .toBackground_2(log_3x2_4_tobackground_2), .toBackground_3(log_3x2_4_tobackground_3),
    .toBackground_4(log_3x2_4_tobackground_4), .toBackground_5(log_3x2_4_tobackground_5),
    .toBackground_6(log_3x2_4_tobackground_6), .toBackground_7(log_3x2_4_tobackground_7),
    .toBackground_8(log_3x2_4_tobackground_8), .toBackground_9(log_3x2_4_tobackground_9),
    .toBackground_10(log_3x2_4_tobackground_10), .toFront(log_3x2_4_tofront),
    .toFront_2(log_3x2_4_tofront_2), .toFront_3(log_3x2_4_tofront_3), .toFront_4(log_3x2_4_tofront_4),
    .toFront_5(log_3x2_4_tofront_5), .toFront_6(log_3x2_4_tofront_6), .toFront_7(log_3x2_4_tofront_7),
    .toFront_8(log_3x2_4_tofront_8), .toFront_9(log_3x2_4_tofront_9), .toFront_10(log_3x2_4_tofront_10));
  DotMatrix #(.inputtype("row"), .matrixcols(30), .matrixrows(4)) dotmatrix_159 (
    .row0(log_3x2_4_tobackground_4), .row1(log_3x2_4_tobackground_5), .row2(log_3x2_4_tobackground_6),
    .row3(log_3x2_4_tobackground_7));
  DotMatrix #(.inputtype("row"), .matrixcols(30), .matrixrows(3)) dotmatrix_160 (
    .row0(log_3x2_4_tobackground_8), .row1(log_3x2_4_tobackground_9), .row2(log_3x2_4_tobackground_10));
  DotMatrix #(.inputtype("row"), .matrixcols(30), .matrixrows(10)) dotmatrix_161 (
    .row0(log_1x1_4_tofront), .row1(log_1x1_4_tofront_2), .row2(log_1x1_4_tofront_3),
    .row3(log_1x1_4_tofront_4), .row4(log_1x1_4_tofront_5), .row5(log_1x1_4_tofront_6),
    .row6(log_1x1_4_tofront_7), .row7(log_1x1_4_tofront_8), .row8(log_1x1_4_tofront_9),
    .row9(log_1x1_4_tofront_10));
  log_1x1 log_1x1_4 (
    .inBackShiftD(log_1x1_3_outbackshiftd), .outBackShiftD(log_1x1_4_outbackshiftd),
    .inputBackShiftM(log_1x1_3_outputbackshiftm), .outputBackShiftM(log_1x1_4_outputbackshiftm),
    .inPlayerShiftD(log_1x1_3_outplayershiftd), .outPlayerShiftD(log_1x1_4_outplayershiftd),
    .inPlayerShiftM(log_1x1_3_outplayershiftm), .outPlayerShiftM(log_1x1_4_outplayershiftm),
    .inFlag(log_1x1_3_outflag), .outFlag(log_1x1_4_outflag), .toBackground(log_1x1_4_tobackground),
    .toBackground_2(log_1x1_4_tobackground_2), .toBackground_3(log_1x1_4_tobackground_3),
    .toBackground_4(log_1x1_4_tobackground_4), .toBackground_5(log_1x1_4_tobackground_5),
    .toBackground_6(log_1x1_4_tobackground_6), .toBackground_7(log_1x1_4_tobackground_7),
    .toBackground_8(log_1x1_4_tobackground_8), .toBackground_9(log_1x1_4_tobackground_9),
    .toBackground_10(log_1x1_4_tobackground_10), .toFront(log_1x1_4_tofront),
    .toFront_2(log_1x1_4_tofront_2), .toFront_3(log_1x1_4_tofront_3), .toFront_4(log_1x1_4_tofront_4),
    .toFront_5(log_1x1_4_tofront_5), .toFront_6(log_1x1_4_tofront_6), .toFront_7(log_1x1_4_tofront_7),
    .toFront_8(log_1x1_4_tofront_8), .toFront_9(log_1x1_4_tofront_9), .toFront_10(log_1x1_4_tofront_10));
  DotMatrix #(.inputtype("row"), .matrixcols(30), .matrixrows(3)) dotmatrix_162 (
    .row0(log_1x1_4_tobackground), .row1(log_1x1_4_tobackground_2), .row2(log_1x1_4_tobackground_3));
  DotMatrix #(.inputtype("row"), .matrixcols(30), .matrixrows(4)) dotmatrix_163 (
    .row0(log_1x1_4_tobackground_4), .row1(log_1x1_4_tobackground_5), .row2(log_1x1_4_tobackground_6),
    .row3(log_1x1_4_tobackground_7));
  DotMatrix #(.inputtype("row"), .matrixcols(30), .matrixrows(3)) dotmatrix_164 (
    .row0(log_1x1_4_tobackground_8), .row1(log_1x1_4_tobackground_9), .row2(log_1x1_4_tobackground_10));
  DotMatrix #(.inputtype("row"), .matrixcols(30), .matrixrows(10)) dotmatrix_165 (
    .row0(turtle_3x1_4_tofront), .row1(turtle_3x1_4_tofront_2), .row2(turtle_3x1_4_tofront_3),
    .row3(turtle_3x1_4_tofront_4), .row4(turtle_3x1_4_tofront_5), .row5(turtle_3x1_4_tofront_6),
    .row6(turtle_3x1_4_tofront_7), .row7(turtle_3x1_4_tofront_8), .row8(turtle_3x1_4_tofront_9),
    .row9(turtle_3x1_4_tofront_10));
  DotMatrix #(.inputtype("row"), .matrixcols(30), .matrixrows(2)) dotmatrix_166 (
    .row0(turtle_3x1_4_tobackground), .row1(turtle_3x1_4_tobackground_2));
  turtle_3x1 turtle_3x1_4 (
    .inBackShiftD(turtle_3x1_3_outbackshiftd), .outBackShiftD(turtle_3x1_4_outbackshiftd),
    .inputBackShiftM(turtle_3x1_3_outputbackshiftm), .outputBackShiftM(turtle_3x1_4_outputbackshiftm),
    .inPlayerShiftD(turtle_3x1_3_outplayershiftd), .outPlayerShiftD(turtle_3x1_4_outplayershiftd),
    .inPlayerShiftM(turtle_3x1_3_outplayershiftm), .outPlayerShiftM(turtle_3x1_4_outplayershiftm),
    .inFlag(turtle_3x1_3_outflag), .outFlag(turtle_3x1_4_outflag), .toBackground(turtle_3x1_4_tobackground),
    .toBackground_2(turtle_3x1_4_tobackground_2), .toBackground_3(turtle_3x1_4_tobackground_3),
    .toBackground_4(turtle_3x1_4_tobackground_4), .toBackground_5(turtle_3x1_4_tobackground_5),
    .toBackground_6(turtle_3x1_4_tobackground_6), .toBackground_7(turtle_3x1_4_tobackground_7),
    .toBackground_8(turtle_3x1_4_tobackground_8), .toBackground_9(turtle_3x1_4_tobackground_9),
    .toBackground_10(turtle_3x1_4_tobackground_10), .toFront(turtle_3x1_4_tofront),
    .toFront_2(turtle_3x1_4_tofront_2), .toFront_3(turtle_3x1_4_tofront_3),
    .toFront_4(turtle_3x1_4_tofront_4), .toFront_5(turtle_3x1_4_tofront_5),
    .toFront_6(turtle_3x1_4_tofront_6), .toFront_7(turtle_3x1_4_tofront_7),
    .toFront_8(turtle_3x1_4_tofront_8), .toFront_9(turtle_3x1_4_tofront_9),
    .toFront_10(turtle_3x1_4_tofront_10), .animState(turtle_3x1_3_animstate_2));  // open: animState_2
  DotMatrix #(.inputtype("row"), .matrixcols(30), .matrixrows(6)) dotmatrix_167 (
    .row0(turtle_3x1_4_tobackground_3), .row1(turtle_3x1_4_tobackground_4),
    .row2(turtle_3x1_4_tobackground_5), .row3(turtle_3x1_4_tobackground_6),
    .row4(turtle_3x1_4_tobackground_7), .row5(turtle_3x1_4_tobackground_8));
  DotMatrix #(.inputtype("row"), .matrixcols(30), .matrixrows(2)) dotmatrix_168 (
    .row0(turtle_3x1_4_tobackground_9), .row1(turtle_3x1_4_tobackground_10));
  DotMatrix #(.inputtype("row"), .matrixcols(30), .matrixrows(10)) dotmatrix_169 (
    .row0(swampdriver_7_p16), .row1(swampdriver_7_p17), .row2(swampdriver_7_p18), .row3(swampdriver_7_p19),
    .row4(swampdriver_7_p20), .row5(swampdriver_7_p21), .row6(swampdriver_7_p22), .row7(swampdriver_7_p23),
    .row8(swampdriver_7_p24), .row9(swampdriver_7_p25));
  DotMatrix #(.inputtype("row"), .matrixcols(30), .matrixrows(3)) dotmatrix_170 (
    .row0(swampdriver_7_p6), .row1(swampdriver_7_p7), .row2(swampdriver_7_p8));
  // swampDriver swampdriver_7: pin names not known; wires that end beside it: swampdriver_5_p27, swampdriver_5_p28, swampdriver_5_p29, swampdriver_5_p30, swampdriver_5_p31, swampdriver_7_p6, swampdriver_7_p7, swampdriver_7_p8, swampdriver_7_p9, swampdriver_7_p10, swampdriver_7_p11, swampdriver_7_p12, swampdriver_7_p13, swampdriver_7_p14, swampdriver_7_p15, swampdriver_7_p16, swampdriver_7_p17, swampdriver_7_p18, swampdriver_7_p19, swampdriver_7_p20, swampdriver_7_p21, swampdriver_7_p22, swampdriver_7_p23, swampdriver_7_p24, swampdriver_7_p25
  DotMatrix #(.inputtype("row"), .matrixcols(30), .matrixrows(4)) dotmatrix_171 (
    .row0(swampdriver_7_p9), .row1(swampdriver_7_p10), .row2(swampdriver_7_p11), .row3(swampdriver_7_p12));
  DotMatrix #(.inputtype("row"), .matrixcols(30), .matrixrows(3)) dotmatrix_172 (
    .row0(swampdriver_7_p13), .row1(swampdriver_7_p14), .row2(swampdriver_7_p15));
  DotMatrix #(.inputtype("row"), .matrixcols(30), .matrixrows(2)) dotmatrix_173 (
    .row0(truckdriver_7_tobackground), .row1(truckdriver_7_tobackground_2));
  DotMatrix #(.inputtype("row"), .matrixcols(30), .matrixrows(10)) dotmatrix_174 (
    .row0(truckdriver_7_tofront), .row1(truckdriver_7_tofront_2), .row2(truckdriver_7_tofront_3),
    .row3(truckdriver_7_tofront_4), .row4(truckdriver_7_tofront_5), .row5(truckdriver_7_tofront_6),
    .row6(truckdriver_7_tofront_7), .row7(truckdriver_7_tofront_8), .row8(truckdriver_7_tofront_9),
    .row9(truckdriver_7_tofront_10));
  truckDriver truckdriver_7 (
    .inBackShiftD(truckdriver_5_outbackshiftd), .inputBackShiftM(truckdriver_5_outputbackshiftm),
    .inPlayerShiftD(truckdriver_5_outplayershiftd), .inPlayerShiftM(truckdriver_5_outplayershiftm),
    .inFlag(truckdriver_5_outflag), .toBackground(truckdriver_7_tobackground),
    .toBackground_2(truckdriver_7_tobackground_2), .toBackground_3(truckdriver_7_tobackground_3),
    .toBackground_4(truckdriver_7_tobackground_4), .toBackground_5(truckdriver_7_tobackground_5),
    .toBackground_6(truckdriver_7_tobackground_6), .toBackground_7(truckdriver_7_tobackground_7),
    .toBackground_8(truckdriver_7_tobackground_8), .toBackground_9(truckdriver_7_tobackground_9),
    .toBackground_10(truckdriver_7_tobackground_10), .toFront(truckdriver_7_tofront),
    .toFront_2(truckdriver_7_tofront_2), .toFront_3(truckdriver_7_tofront_3),
    .toFront_4(truckdriver_7_tofront_4), .toFront_5(truckdriver_7_tofront_5),
    .toFront_6(truckdriver_7_tofront_6), .toFront_7(truckdriver_7_tofront_7),
    .toFront_8(truckdriver_7_tofront_8), .toFront_9(truckdriver_7_tofront_9),
    .toFront_10(truckdriver_7_tofront_10));  // open: outBackShiftD, outputBackShiftM, outPlayerShiftD, outPlayerShiftM, outFlag
  DotMatrix #(.inputtype("row"), .matrixcols(30), .matrixrows(6)) dotmatrix_175 (
    .row0(truckdriver_7_tobackground_3), .row1(truckdriver_7_tobackground_4),
    .row2(truckdriver_7_tobackground_5), .row3(truckdriver_7_tobackground_6),
    .row4(truckdriver_7_tobackground_7), .row5(truckdriver_7_tobackground_8));
  DotMatrix #(.inputtype("row"), .matrixcols(30), .matrixrows(2)) dotmatrix_176 (
    .row0(truckdriver_7_tobackground_9), .row1(truckdriver_7_tobackground_10));
  DotMatrix #(.inputtype("row"), .matrixcols(30), .matrixrows(2)) dotmatrix_177 (
    .row0(carconnectorv2_4_tobackground), .row1(carconnectorv2_4_tobackground_2));
  carConnectorV2 carconnectorv2_4 (
    .inBackShiftD(carconnectorv2_3_outbackshiftd), .inputBackShiftM(carconnectorv2_3_outputbackshiftm),
    .inPlayerShiftM(carconnectorv2_3_outplayershiftm), .inFlag(carconnectorv2_3_outflag),
    .toBackground(carconnectorv2_4_tobackground), .toBackground_2(carconnectorv2_4_tobackground_2),
    .toBackground_3(carconnectorv2_4_tobackground_3), .toBackground_4(carconnectorv2_4_tobackground_4),
    .toBackground_5(carconnectorv2_4_tobackground_5), .toBackground_6(carconnectorv2_4_tobackground_6),
    .toBackground_7(carconnectorv2_4_tobackground_7), .toBackground_8(carconnectorv2_4_tobackground_8),
    .toBackground_9(carconnectorv2_4_tobackground_9), .toBackground_10(carconnectorv2_4_tobackground_10),
    .toFront(carconnectorv2_4_tofront), .toFront_2(carconnectorv2_4_tofront_2),
    .toFront_3(carconnectorv2_4_tofront_3), .toFront_4(carconnectorv2_4_tofront_4),
    .toFront_5(carconnectorv2_4_tofront_5), .toFront_6(carconnectorv2_4_tofront_6),
    .toFront_7(carconnectorv2_4_tofront_7), .toFront_8(carconnectorv2_4_tofront_8),
    .toFront_9(carconnectorv2_4_tofront_9), .toFront_10(carconnectorv2_4_tofront_10),
    .inPlayerShiftD(carconnectorv2_3_outplayershiftd));  // open: outBackShiftD, outputBackShiftM, outPlayerShiftD, outPlayerShiftM, outFlag
  DotMatrix #(.inputtype("row"), .matrixcols(30), .matrixrows(10)) dotmatrix_178 (
    .row0(carconnectorv2_4_tofront), .row1(carconnectorv2_4_tofront_2), .row2(carconnectorv2_4_tofront_3),
    .row3(carconnectorv2_4_tofront_4), .row4(carconnectorv2_4_tofront_5), .row5(carconnectorv2_4_tofront_6),
    .row6(carconnectorv2_4_tofront_7), .row7(carconnectorv2_4_tofront_8), .row8(carconnectorv2_4_tofront_9),
    .row9(carconnectorv2_4_tofront_10));
  DotMatrix #(.inputtype("row"), .matrixcols(30), .matrixrows(6)) dotmatrix_179 (
    .row0(carconnectorv2_4_tobackground_3), .row1(carconnectorv2_4_tobackground_4),
    .row2(carconnectorv2_4_tobackground_5), .row3(carconnectorv2_4_tobackground_6),
    .row4(carconnectorv2_4_tobackground_7), .row5(carconnectorv2_4_tobackground_8));
  DotMatrix #(.inputtype("row"), .matrixcols(30), .matrixrows(2)) dotmatrix_180 (
    .row0(carconnectorv2_4_tobackground_9), .row1(carconnectorv2_4_tobackground_10));
  DotMatrix #(.inputtype("row"), .matrixcols(30), .matrixrows(2)) dotmatrix_181 (
    .row0(boliddriver_4_tobackground), .row1(boliddriver_4_tobackground_2));
  bolidDriver boliddriver_4 (
    .inBackShiftD(boliddriver_3_outbackshiftd), .inputBackShiftM(boliddriver_3_outputbackshiftm),
    .inPlayerShiftD(boliddriver_3_outplayershiftd), .inPlayerShiftM(boliddriver_3_outplayershiftm),
    .inFlag(boliddriver_3_outflag), .toBackground(boliddriver_4_tobackground),
    .toBackground_2(boliddriver_4_tobackground_2), .toBackground_3(boliddriver_4_tobackground_3),
    .toBackground_4(boliddriver_4_tobackground_4), .toBackground_5(boliddriver_4_tobackground_5),
    .toBackground_6(boliddriver_4_tobackground_6), .toBackground_7(boliddriver_4_tobackground_7),
    .toBackground_8(boliddriver_4_tobackground_8), .toBackground_9(boliddriver_4_tobackground_9),
    .toBackground_10(boliddriver_4_tobackground_10), .toFront(boliddriver_4_tofront),
    .toFront_2(boliddriver_4_tofront_2), .toFront_3(boliddriver_4_tofront_3),
    .toFront_4(boliddriver_4_tofront_4), .toFront_5(boliddriver_4_tofront_5),
    .toFront_6(boliddriver_4_tofront_6), .toFront_7(boliddriver_4_tofront_7),
    .toFront_8(boliddriver_4_tofront_8), .toFront_9(boliddriver_4_tofront_9),
    .toFront_10(boliddriver_4_tofront_10));  // open: outBackShiftD, outputBackShiftM, outPlayerShiftD, outPlayerShiftM, outFlag
  DotMatrix #(.inputtype("row"), .matrixcols(30), .matrixrows(10)) dotmatrix_182 (
    .row0(boliddriver_4_tofront), .row1(boliddriver_4_tofront_2), .row2(boliddriver_4_tofront_3),
    .row3(boliddriver_4_tofront_4), .row4(boliddriver_4_tofront_5), .row5(boliddriver_4_tofront_6),
    .row6(boliddriver_4_tofront_7), .row7(boliddriver_4_tofront_8), .row8(boliddriver_4_tofront_9),
    .row9(boliddriver_4_tofront_10));
  DotMatrix #(.inputtype("row"), .matrixcols(30), .matrixrows(6)) dotmatrix_183 (
    .row0(boliddriver_4_tobackground_3), .row1(boliddriver_4_tobackground_4),
    .row2(boliddriver_4_tobackground_5), .row3(boliddriver_4_tobackground_6),
    .row4(boliddriver_4_tobackground_7), .row5(boliddriver_4_tobackground_8));
  DotMatrix #(.inputtype("row"), .matrixcols(30), .matrixrows(2)) dotmatrix_184 (
    .row0(boliddriver_4_tobackground_9), .row1(boliddriver_4_tobackground_10));
  DotMatrix #(.inputtype("row"), .matrixcols(30), .matrixrows(10)) dotmatrix_185 (
    .row0(suvdriver_4_tofront), .row1(suvdriver_4_tofront_2), .row2(suvdriver_4_tofront_3),
    .row3(suvdriver_4_tofront_4), .row4(suvdriver_4_tofront_5), .row5(suvdriver_4_tofront_6),
    .row6(suvdriver_4_tofront_7), .row7(suvdriver_4_tofront_8), .row8(suvdriver_4_tofront_9),
    .row9(suvdriver_4_tofront_10));
  SUVDriver suvdriver_4 (
    .inBackShiftD(suvdriver_3_outbackshiftd), .inputBackShiftM(suvdriver_3_outputbackshiftm),
    .inPlayerShiftD(suvdriver_3_outplayershiftd), .inPlayerShiftM(suvdriver_3_outplayershiftm),
    .inFlag(suvdriver_3_outflag), .toBackground(suvdriver_4_tobackground),
    .toBackground_2(suvdriver_4_tobackground_2), .toBackground_3(suvdriver_4_tobackground_3),
    .toBackground_4(suvdriver_4_tobackground_4), .toBackground_5(suvdriver_4_tobackground_5),
    .toBackground_6(suvdriver_4_tobackground_6), .toBackground_7(suvdriver_4_tobackground_7),
    .toBackground_8(suvdriver_4_tobackground_8), .toBackground_9(suvdriver_4_tobackground_9),
    .toBackground_10(suvdriver_4_tobackground_10), .toFront(suvdriver_4_tofront),
    .toFront_2(suvdriver_4_tofront_2), .toFront_3(suvdriver_4_tofront_3), .toFront_4(suvdriver_4_tofront_4),
    .toFront_5(suvdriver_4_tofront_5), .toFront_6(suvdriver_4_tofront_6), .toFront_7(suvdriver_4_tofront_7),
    .toFront_8(suvdriver_4_tofront_8), .toFront_9(suvdriver_4_tofront_9), .toFront_10(suvdriver_4_tofront_10));  // open: outBackShiftD, outputBackShiftM, outPlayerShiftD, outPlayerShiftM, outFlag
  DotMatrix #(.inputtype("row"), .matrixcols(30), .matrixrows(2)) dotmatrix_186 (
    .row0(suvdriver_4_tobackground), .row1(suvdriver_4_tobackground_2));
  DotMatrix #(.inputtype("row"), .matrixcols(30), .matrixrows(6)) dotmatrix_187 (
    .row0(suvdriver_4_tobackground_3), .row1(suvdriver_4_tobackground_4), .row2(suvdriver_4_tobackground_5),
    .row3(suvdriver_4_tobackground_6), .row4(suvdriver_4_tobackground_7), .row5(suvdriver_4_tobackground_8));
  DotMatrix #(.inputtype("row"), .matrixcols(30), .matrixrows(2)) dotmatrix_188 (
    .row0(suvdriver_4_tobackground_9), .row1(suvdriver_4_tobackground_10));
  DotMatrix #(.inputtype("row"), .matrixcols(30), .matrixrows(10)) dotmatrix_189 (
    .row0(truckdriver_8_tofront), .row1(truckdriver_8_tofront_2), .row2(truckdriver_8_tofront_3),
    .row3(truckdriver_8_tofront_4), .row4(truckdriver_8_tofront_5), .row5(truckdriver_8_tofront_6),
    .row6(truckdriver_8_tofront_7), .row7(truckdriver_8_tofront_8), .row8(truckdriver_8_tofront_9),
    .row9(truckdriver_8_tofront_10));
  DotMatrix #(.inputtype("row"), .matrixcols(30), .matrixrows(2)) dotmatrix_190 (
    .row0(truckdriver_8_tobackground), .row1(truckdriver_8_tobackground_2));
  truckDriver truckdriver_8 (
    .inBackShiftD(truckdriver_6_outbackshiftd), .inputBackShiftM(truckdriver_6_outputbackshiftm),
    .inPlayerShiftD(truckdriver_6_outplayershiftd), .inPlayerShiftM(truckdriver_6_outplayershiftm),
    .inFlag(truckdriver_6_outflag), .toBackground(truckdriver_8_tobackground),
    .toBackground_2(truckdriver_8_tobackground_2), .toBackground_3(truckdriver_8_tobackground_3),
    .toBackground_4(truckdriver_8_tobackground_4), .toBackground_5(truckdriver_8_tobackground_5),
    .toBackground_6(truckdriver_8_tobackground_6), .toBackground_7(truckdriver_8_tobackground_7),
    .toBackground_8(truckdriver_8_tobackground_8), .toBackground_9(truckdriver_8_tobackground_9),
    .toBackground_10(truckdriver_8_tobackground_10), .toFront(truckdriver_8_tofront),
    .toFront_2(truckdriver_8_tofront_2), .toFront_3(truckdriver_8_tofront_3),
    .toFront_4(truckdriver_8_tofront_4), .toFront_5(truckdriver_8_tofront_5),
    .toFront_6(truckdriver_8_tofront_6), .toFront_7(truckdriver_8_tofront_7),
    .toFront_8(truckdriver_8_tofront_8), .toFront_9(truckdriver_8_tofront_9),
    .toFront_10(truckdriver_8_tofront_10));  // open: outBackShiftD, outputBackShiftM, outPlayerShiftD, outPlayerShiftM, outFlag
  DotMatrix #(.inputtype("row"), .matrixcols(30), .matrixrows(6)) dotmatrix_191 (
    .row0(truckdriver_8_tobackground_3), .row1(truckdriver_8_tobackground_4),
    .row2(truckdriver_8_tobackground_5), .row3(truckdriver_8_tobackground_6),
    .row4(truckdriver_8_tobackground_7), .row5(truckdriver_8_tobackground_8));
  DotMatrix #(.inputtype("row"), .matrixcols(30), .matrixrows(2)) dotmatrix_192 (
    .row0(truckdriver_8_tobackground_9), .row1(truckdriver_8_tobackground_10));
  DotMatrix #(.inputtype("row"), .matrixcols(30), .matrixrows(10)) dotmatrix_193 (
    .row0(swampdriver_8_p16), .row1(swampdriver_8_p17), .row2(swampdriver_8_p18), .row3(swampdriver_8_p19),
    .row4(swampdriver_8_p20), .row5(swampdriver_8_p21), .row6(swampdriver_8_p22), .row7(swampdriver_8_p23),
    .row8(swampdriver_8_p24), .row9(swampdriver_8_p25));
  // swampDriver swampdriver_8: pin names not known; wires that end beside it: swampdriver_6_p26, swampdriver_6_p27, swampdriver_6_p28, swampdriver_6_p29, swampdriver_6_p30, swampdriver_8_p6, swampdriver_8_p7, swampdriver_8_p8, swampdriver_8_p9, swampdriver_8_p10, swampdriver_8_p11, swampdriver_8_p12, swampdriver_8_p13, swampdriver_8_p14, swampdriver_8_p15, swampdriver_8_p16, swampdriver_8_p17, swampdriver_8_p18, swampdriver_8_p19, swampdriver_8_p20, swampdriver_8_p21, swampdriver_8_p22, swampdriver_8_p23, swampdriver_8_p24, swampdriver_8_p25
  DotMatrix #(.inputtype("row"), .matrixcols(30), .matrixrows(3)) dotmatrix_194 (
    .row0(swampdriver_8_p6), .row1(swampdriver_8_p7), .row2(swampdriver_8_p8));
  DotMatrix #(.inputtype("row"), .matrixcols(30), .matrixrows(4)) dotmatrix_195 (
    .row0(swampdriver_8_p9), .row1(swampdriver_8_p10), .row2(swampdriver_8_p11), .row3(swampdriver_8_p12));
  DotMatrix #(.inputtype("row"), .matrixcols(30), .matrixrows(3)) dotmatrix_196 (
    .row0(swampdriver_8_p13), .row1(swampdriver_8_p14), .row2(swampdriver_8_p15));
  lives lives_1 (
    .in_out(in_out), .I_Oadr(I_Oadr), .I_Osel(I_Osel), .I_Odat(I_Odat), .clock(clock), .clear(restartGame),
    .the_1_st_line_of_the_picture_4(lives_1_the_1_st_line_of_the_picture_4),
    .the_14_th_line_of_the_picture_4(lives_1_the_14_th_line_of_the_picture_4),
    .the_2_nd_line_of_the_picture_4(lives_1_the_2_nd_line_of_the_picture_4),
    .the_15_th_line_of_the_picture_4(lives_1_the_15_th_line_of_the_picture_4),
    .the_3_rd_line_of_the_picture_4(lives_1_the_3_rd_line_of_the_picture_4),
    .the_16_th_line_of_the_picture(lives_1_the_16_th_line_of_the_picture),
    .the_4_th_line_of_the_picture_4(lives_1_the_4_th_line_of_the_picture_4),
    .the_17_th_line_of_the_picture(lives_1_the_17_th_line_of_the_picture),
    .the_5_th_line_of_the_picture_4(lives_1_the_5_th_line_of_the_picture_4),
    .the_18_th_line_of_the_picture(lives_1_the_18_th_line_of_the_picture),
    .the_6_th_line_of_the_picture_4(lives_1_the_6_th_line_of_the_picture_4),
    .the_19_th_line_of_the_picture(lives_1_the_19_th_line_of_the_picture),
    .the_7_th_line_of_the_picture_4(lives_1_the_7_th_line_of_the_picture_4),
    .the_20_th_line_of_the_picture(lives_1_the_20_th_line_of_the_picture),
    .the_1_st_line_of_the_picture(lives_1_the_1_st_line_of_the_picture),
    .the_8_th_line_of_the_picture_4(lives_1_the_8_th_line_of_the_picture_4),
    .the_21_st_line_of_the_picture(lives_1_the_21_st_line_of_the_picture),
    .the_2_nd_line_of_the_picture(lives_1_the_2_nd_line_of_the_picture),
    .the_9_th_line_of_the_picture_4(lives_1_the_9_th_line_of_the_picture_4),
    .the_22_nd_line_of_the_picture(lives_1_the_22_nd_line_of_the_picture),
    .the_3_rd_line_of_the_picture(lives_1_the_3_rd_line_of_the_picture),
    .the_4_th_line_of_the_picture(lives_1_the_4_th_line_of_the_picture),
    .the_10_th_line_of_the_picture_4(lives_1_the_10_th_line_of_the_picture_4),
    .the_23_rd_line_of_the_picture(lives_1_the_23_rd_line_of_the_picture),
    .the_5_th_line_of_the_picture(lives_1_the_5_th_line_of_the_picture),
    .the_11_th_line_of_the_picture_4(lives_1_the_11_th_line_of_the_picture_4),
    .the_24_th_line_of_the_picture(lives_1_the_24_th_line_of_the_picture),
    .the_6_th_line_of_the_picture(lives_1_the_6_th_line_of_the_picture),
    .the_12_th_line_of_the_picture_4(lives_1_the_12_th_line_of_the_picture_4),
    .the_25_th_line_of_the_picture(lives_1_the_25_th_line_of_the_picture),
    .the_7_th_line_of_the_picture(lives_1_the_7_th_line_of_the_picture),
    .the_13_th_line_of_the_picture_4(lives_1_the_13_th_line_of_the_picture_4),
    .number_of_lives(lives_1_number_of_lives),
    .the_26_th_line_of_the_picture(lives_1_the_26_th_line_of_the_picture),
    .the_27_th_line_of_the_picture(lives_1_the_27_th_line_of_the_picture),
    .the_28_th_line_of_the_picture(lives_1_the_28_th_line_of_the_picture),
    .the_29_th_line_of_the_picture(lives_1_the_29_th_line_of_the_picture),
    .the_30_th_line_of_the_picture(lives_1_the_30_th_line_of_the_picture),
    .the_31_st_line_of_the_picture(lives_1_the_31_st_line_of_the_picture),
    .the_32_nd_line_of_the_picture(lives_1_the_32_nd_line_of_the_picture),
    .the_8_th_line_of_the_picture(lives_1_the_8_th_line_of_the_picture),
    .the_9_th_line_of_the_picture(lives_1_the_9_th_line_of_the_picture),
    .the_10_th_line_of_the_picture(lives_1_the_10_th_line_of_the_picture),
    .the_11_th_line_of_the_picture(lives_1_the_11_th_line_of_the_picture),
    .the_12_th_line_of_the_picture(lives_1_the_12_th_line_of_the_picture),
    .the_13_th_line_of_the_picture(lives_1_the_13_th_line_of_the_picture),
    .the_14_th_line_of_the_picture(lives_1_the_14_th_line_of_the_picture),
    .the_15_th_line_of_the_picture(lives_1_the_15_th_line_of_the_picture),
    .the_1_st_line_of_the_picture_2(lives_1_the_1_st_line_of_the_picture_2),
    .the_2_nd_line_of_the_picture_2(lives_1_the_2_nd_line_of_the_picture_2),
    .the_3_rd_line_of_the_picture_2(lives_1_the_3_rd_line_of_the_picture_2),
    .the_4_th_line_of_the_picture_2(lives_1_the_4_th_line_of_the_picture_2),
    .the_5_th_line_of_the_picture_2(lives_1_the_5_th_line_of_the_picture_2),
    .the_6_th_line_of_the_picture_2(lives_1_the_6_th_line_of_the_picture_2),
    .the_7_th_line_of_the_picture_2(lives_1_the_7_th_line_of_the_picture_2),
    .the_8_th_line_of_the_picture_2(lives_1_the_8_th_line_of_the_picture_2),
    .the_9_th_line_of_the_picture_2(lives_1_the_9_th_line_of_the_picture_2),
    .the_10_th_line_of_the_picture_2(lives_1_the_10_th_line_of_the_picture_2),
    .the_11_th_line_of_the_picture_2(lives_1_the_11_th_line_of_the_picture_2),
    .the_12_th_line_of_the_picture_2(lives_1_the_12_th_line_of_the_picture_2),
    .the_13_th_line_of_the_picture_2(lives_1_the_13_th_line_of_the_picture_2),
    .the_14_th_line_of_the_picture_2(lives_1_the_14_th_line_of_the_picture_2),
    .the_15_th_line_of_the_picture_2(lives_1_the_15_th_line_of_the_picture_2),
    .the_1_st_line_of_the_picture_3(lives_1_the_1_st_line_of_the_picture_3),
    .the_2_nd_line_of_the_picture_3(lives_1_the_2_nd_line_of_the_picture_3),
    .the_3_rd_line_of_the_picture_3(lives_1_the_3_rd_line_of_the_picture_3),
    .the_4_th_line_of_the_picture_3(lives_1_the_4_th_line_of_the_picture_3),
    .the_5_th_line_of_the_picture_3(lives_1_the_5_th_line_of_the_picture_3),
    .the_6_th_line_of_the_picture_3(lives_1_the_6_th_line_of_the_picture_3),
    .the_7_th_line_of_the_picture_3(lives_1_the_7_th_line_of_the_picture_3),
    .the_8_th_line_of_the_picture_3(lives_1_the_8_th_line_of_the_picture_3),
    .the_9_th_line_of_the_picture_3(lives_1_the_9_th_line_of_the_picture_3),
    .the_10_th_line_of_the_picture_3(lives_1_the_10_th_line_of_the_picture_3),
    .the_11_th_line_of_the_picture_3(lives_1_the_11_th_line_of_the_picture_3),
    .the_12_th_line_of_the_picture_3(lives_1_the_12_th_line_of_the_picture_3),
    .the_13_th_line_of_the_picture_3(lives_1_the_13_th_line_of_the_picture_3),
    .the_14_th_line_of_the_picture_3(lives_1_the_14_th_line_of_the_picture_3),
    .the_15_th_line_of_the_picture_3(lives_1_the_15_th_line_of_the_picture_3));
  DotMatrix #(.inputtype("row"), .matrixcols(32), .matrixrows(32)) dotmatrix_197 (
    .row0(lives_1_the_1_st_line_of_the_picture_4), .row1(lives_1_the_2_nd_line_of_the_picture_4),
    .row2(lives_1_the_3_rd_line_of_the_picture_4), .row3(lives_1_the_4_th_line_of_the_picture_4),
    .row4(lives_1_the_5_th_line_of_the_picture_4), .row5(lives_1_the_6_th_line_of_the_picture_4),
    .row6(lives_1_the_7_th_line_of_the_picture_4), .row7(lives_1_the_8_th_line_of_the_picture_4),
    .row8(lives_1_the_9_th_line_of_the_picture_4), .row9(lives_1_the_10_th_line_of_the_picture_4),
    .row10(lives_1_the_11_th_line_of_the_picture_4), .row11(lives_1_the_12_th_line_of_the_picture_4),
    .row12(lives_1_the_13_th_line_of_the_picture_4), .row13(lives_1_the_14_th_line_of_the_picture_4),
    .row14(lives_1_the_15_th_line_of_the_picture_4), .row15(lives_1_the_16_th_line_of_the_picture),
    .row16(lives_1_the_17_th_line_of_the_picture), .row17(lives_1_the_18_th_line_of_the_picture),
    .row18(lives_1_the_19_th_line_of_the_picture), .row19(lives_1_the_20_th_line_of_the_picture),
    .row20(lives_1_the_21_st_line_of_the_picture), .row21(lives_1_the_22_nd_line_of_the_picture),
    .row22(lives_1_the_23_rd_line_of_the_picture), .row23(lives_1_the_24_th_line_of_the_picture),
    .row24(lives_1_the_25_th_line_of_the_picture), .row25(lives_1_the_26_th_line_of_the_picture),
    .row26(lives_1_the_27_th_line_of_the_picture), .row27(lives_1_the_28_th_line_of_the_picture),
    .row28(lives_1_the_29_th_line_of_the_picture), .row29(lives_1_the_30_th_line_of_the_picture),
    .row30(lives_1_the_31_st_line_of_the_picture), .row31(lives_1_the_32_nd_line_of_the_picture));
  DotMatrix #(.inputtype("row"), .matrixcols(15), .matrixrows(15)) dotmatrix_198 (
    .row0(lives_1_the_1_st_line_of_the_picture), .row1(lives_1_the_2_nd_line_of_the_picture),
    .row2(lives_1_the_3_rd_line_of_the_picture), .row3(lives_1_the_4_th_line_of_the_picture),
    .row4(lives_1_the_5_th_line_of_the_picture), .row5(lives_1_the_6_th_line_of_the_picture),
    .row6(lives_1_the_7_th_line_of_the_picture), .row7(lives_1_the_8_th_line_of_the_picture),
    .row8(lives_1_the_9_th_line_of_the_picture), .row9(lives_1_the_10_th_line_of_the_picture),
    .row10(lives_1_the_11_th_line_of_the_picture), .row11(lives_1_the_12_th_line_of_the_picture),
    .row12(lives_1_the_13_th_line_of_the_picture), .row13(lives_1_the_14_th_line_of_the_picture),
    .row14(lives_1_the_15_th_line_of_the_picture));
  DotMatrix #(.inputtype("row"), .matrixcols(32), .matrixrows(32)) dotmatrix_199 (
    .row0(record_score_1_the_1_st_line_of_the_picture), .row1(record_score_1_the_2_nd_line_of_the_picture),
    .row2(record_score_1_the_3_rd_line_of_the_picture), .row3(record_score_1_the_4_th_line_of_the_picture),
    .row4(record_score_1_the_5_th_line_of_the_picture), .row5(record_score_1_the_6_th_line_of_the_picture),
    .row6(record_score_1_the_7_th_line_of_the_picture), .row7(record_score_1_the_8_th_line_of_the_picture),
    .row8(record_score_1_the_9_th_line_of_the_picture), .row9(record_score_1_the_10_th_line_of_the_picture),
    .row10(record_score_1_the_11_th_line_of_the_picture),
    .row11(record_score_1_the_12_th_line_of_the_picture),
    .row12(record_score_1_the_13_th_line_of_the_picture),
    .row13(record_score_1_the_14_th_line_of_the_picture),
    .row14(record_score_1_the_15_th_line_of_the_picture),
    .row15(record_score_1_the_16_th_line_of_the_picture),
    .row16(record_score_1_the_17_th_line_of_the_picture),
    .row17(record_score_1_the_18_th_line_of_the_picture),
    .row18(record_score_1_the_19_th_line_of_the_picture),
    .row19(record_score_1_the_20_th_line_of_the_picture),
    .row20(record_score_1_the_21_st_line_of_the_picture),
    .row21(record_score_1_the_22_nd_line_of_the_picture),
    .row22(record_score_1_the_23_rd_line_of_the_picture),
    .row23(record_score_1_the_24_th_line_of_the_picture),
    .row24(record_score_1_the_25_th_line_of_the_picture),
    .row25(record_score_1_the_26_th_line_of_the_picture),
    .row26(record_score_1_the_27_th_line_of_the_picture),
    .row27(record_score_1_the_28_th_line_of_the_picture),
    .row28(record_score_1_the_29_th_line_of_the_picture),
    .row29(record_score_1_the_30_th_line_of_the_picture),
    .row30(record_score_1_the_31_st_line_of_the_picture), .row31(record_score_1_the_32_nd_line_of_the_picture));
  record_score record_score_1 (
    .the_1_st_line_of_the_picture(record_score_1_the_1_st_line_of_the_picture),
    .the_11_th_line_of_the_picture(record_score_1_the_11_th_line_of_the_picture),
    .the_2_nd_line_of_the_picture(record_score_1_the_2_nd_line_of_the_picture),
    .the_12_th_line_of_the_picture(record_score_1_the_12_th_line_of_the_picture),
    .the_3_rd_line_of_the_picture(record_score_1_the_3_rd_line_of_the_picture),
    .the_13_th_line_of_the_picture(record_score_1_the_13_th_line_of_the_picture),
    .the_4_th_line_of_the_picture(record_score_1_the_4_th_line_of_the_picture),
    .the_14_th_line_of_the_picture(record_score_1_the_14_th_line_of_the_picture),
    .the_5_th_line_of_the_picture(record_score_1_the_5_th_line_of_the_picture),
    .the_15_th_line_of_the_picture(record_score_1_the_15_th_line_of_the_picture),
    .the_6_th_line_of_the_picture(record_score_1_the_6_th_line_of_the_picture),
    .the_16_th_line_of_the_picture(record_score_1_the_16_th_line_of_the_picture),
    .the_7_th_line_of_the_picture(record_score_1_the_7_th_line_of_the_picture),
    .the_17_th_line_of_the_picture(record_score_1_the_17_th_line_of_the_picture),
    .the_8_th_line_of_the_picture(record_score_1_the_8_th_line_of_the_picture),
    .the_18_th_line_of_the_picture(record_score_1_the_18_th_line_of_the_picture),
    .the_9_th_line_of_the_picture(record_score_1_the_9_th_line_of_the_picture),
    .the_19_th_line_of_the_picture(record_score_1_the_19_th_line_of_the_picture),
    .the_10_th_line_of_the_picture(record_score_1_the_10_th_line_of_the_picture),
    .the_20_th_line_of_the_picture(record_score_1_the_20_th_line_of_the_picture), .in_out(in_out),
    .I_Oadr(I_Oadr), .I_Osel(I_Osel), .I_Odat(I_Odat), .clock(clock), .clear(restartGame),
    .the_first_digit(record_score_1_the_first_digit), .the_second_digit(record_score_1_the_second_digit),
    .the_third_digit(record_score_1_the_third_digit),
    .the_21_st_line_of_the_picture(record_score_1_the_21_st_line_of_the_picture),
    .the_22_nd_line_of_the_picture(record_score_1_the_22_nd_line_of_the_picture),
    .the_23_rd_line_of_the_picture(record_score_1_the_23_rd_line_of_the_picture),
    .the_24_th_line_of_the_picture(record_score_1_the_24_th_line_of_the_picture),
    .the_25_th_line_of_the_picture(record_score_1_the_25_th_line_of_the_picture),
    .the_26_th_line_of_the_picture(record_score_1_the_26_th_line_of_the_picture),
    .the_27_th_line_of_the_picture(record_score_1_the_27_th_line_of_the_picture),
    .the_28_th_line_of_the_picture(record_score_1_the_28_th_line_of_the_picture),
    .the_29_th_line_of_the_picture(record_score_1_the_29_th_line_of_the_picture),
    .the_30_th_line_of_the_picture(record_score_1_the_30_th_line_of_the_picture),
    .the_31_st_line_of_the_picture(record_score_1_the_31_st_line_of_the_picture),
    .the_32_nd_line_of_the_picture(record_score_1_the_32_nd_line_of_the_picture),
    .the_1_st_line_of_the_picture_2(record_score_1_the_1_st_line_of_the_picture_2),
    .the_17_th_line_of_the_picture_2(record_score_1_the_17_th_line_of_the_picture_2),
    .the_2_nd_line_of_the_picture_2(record_score_1_the_2_nd_line_of_the_picture_2),
    .the_18_th_line_of_the_picture_2(record_score_1_the_18_th_line_of_the_picture_2),
    .the_3_rd_line_of_the_picture_2(record_score_1_the_3_rd_line_of_the_picture_2),
    .the_19_th_line_of_the_picture_2(record_score_1_the_19_th_line_of_the_picture_2),
    .the_4_th_line_of_the_picture_2(record_score_1_the_4_th_line_of_the_picture_2),
    .the_20_th_line_of_the_picture_2(record_score_1_the_20_th_line_of_the_picture_2),
    .the_5_th_line_of_the_picture_2(record_score_1_the_5_th_line_of_the_picture_2),
    .the_21_st_line_of_the_picture_2(record_score_1_the_21_st_line_of_the_picture_2),
    .the_6_th_line_of_the_picture_2(record_score_1_the_6_th_line_of_the_picture_2),
    .the_22_nd_line_of_the_picture_2(record_score_1_the_22_nd_line_of_the_picture_2),
    .the_7_th_line_of_the_picture_2(record_score_1_the_7_th_line_of_the_picture_2),
    .the_23_rd_line_of_the_picture_2(record_score_1_the_23_rd_line_of_the_picture_2),
    .the_8_th_line_of_the_picture_2(record_score_1_the_8_th_line_of_the_picture_2),
    .the_24_th_line_of_the_picture_2(record_score_1_the_24_th_line_of_the_picture_2),
    .the_9_th_line_of_the_picture_2(record_score_1_the_9_th_line_of_the_picture_2),
    .the_10_th_line_of_the_picture_2(record_score_1_the_10_th_line_of_the_picture_2),
    .the_11_th_line_of_the_picture_2(record_score_1_the_11_th_line_of_the_picture_2),
    .the_12_th_line_of_the_picture_2(record_score_1_the_12_th_line_of_the_picture_2),
    .the_13_th_line_of_the_picture_2(record_score_1_the_13_th_line_of_the_picture_2),
    .the_14_th_line_of_the_picture_2(record_score_1_the_14_th_line_of_the_picture_2),
    .the_15_th_line_of_the_picture_2(record_score_1_the_15_th_line_of_the_picture_2),
    .the_16_th_line_of_the_picture_2(record_score_1_the_16_th_line_of_the_picture_2),
    .the_25_th_line_of_the_picture_2(record_score_1_the_25_th_line_of_the_picture_2),
    .the_26_th_line_of_the_picture_2(record_score_1_the_26_th_line_of_the_picture_2),
    .the_27_th_line_of_the_picture_2(record_score_1_the_27_th_line_of_the_picture_2),
    .the_28_th_line_of_the_picture_2(record_score_1_the_28_th_line_of_the_picture_2),
    .the_29_th_line_of_the_picture_2(record_score_1_the_29_th_line_of_the_picture_2),
    .the_30_th_line_of_the_picture_2(record_score_1_the_30_th_line_of_the_picture_2),
    .the_31_st_line_of_the_picture_2(record_score_1_the_31_st_line_of_the_picture_2),
    .the_32_nd_line_of_the_picture_2(record_score_1_the_32_nd_line_of_the_picture_2));
  DotMatrix #(.inputtype("row"), .matrixcols(20), .matrixrows(30)) dotmatrix_200 (
    .row0(digits_1_the_1_st_line_of_the_picture), .row1(digits_1_the_2_nd_line_of_the_picture),
    .row2(digits_1_the_3_rd_line_of_the_picture), .row3(digits_1_the_4_th_line_of_the_picture),
    .row4(digits_1_the_5_th_line_of_the_picture), .row5(digits_1_the_6_th_line_of_the_picture),
    .row6(digits_1_the_7_th_line_of_the_picture), .row7(digits_1_the_8_th_line_of_the_picture),
    .row8(digits_1_the_9_th_line_of_the_picture), .row9(digits_1_the_10_th_line_of_the_picture),
    .row10(digits_1_the_11_th_line_of_the_picture), .row11(digits_1_the_12_th_line_of_the_picture),
    .row12(digits_1_the_13_th_line_of_the_picture), .row13(digits_1_the_14_th_line_of_the_picture),
    .row14(digits_1_the_15_th_line_of_the_picture), .row15(digits_1_the_16_th_line_of_the_picture),
    .row16(digits_1_the_17_th_line_of_the_picture), .row17(digits_1_the_18_th_line_of_the_picture),
    .row18(digits_1_the_19_th_line_of_the_picture), .row19(digits_1_the_20_th_line_of_the_picture),
    .row20(digits_1_the_21_st_line_of_the_picture), .row21(digits_1_the_22_nd_line_of_the_picture),
    .row22(digits_1_the_23_rd_line_of_the_picture), .row23(digits_1_the_24_th_line_of_the_picture),
    .row24(digits_1_the_25_th_line_of_the_picture), .row25(digits_1_the_26_th_line_of_the_picture),
    .row26(digits_1_the_27_th_line_of_the_picture), .row27(digits_1_the_28_th_line_of_the_picture),
    .row28(digits_1_the_29_th_line_of_the_picture), .row29(digits_1_the_30_th_line_of_the_picture));
  digits digits_1 (
    .the_1_st_line_of_the_picture(digits_1_the_1_st_line_of_the_picture),
    .the_2_nd_line_of_the_picture(digits_1_the_2_nd_line_of_the_picture),
    .the_3_rd_line_of_the_picture(digits_1_the_3_rd_line_of_the_picture),
    .the_4_th_line_of_the_picture(digits_1_the_4_th_line_of_the_picture),
    .the_5_th_line_of_the_picture(digits_1_the_5_th_line_of_the_picture),
    .the_6_th_line_of_the_picture(digits_1_the_6_th_line_of_the_picture),
    .the_7_th_line_of_the_picture(digits_1_the_7_th_line_of_the_picture),
    .the_8_th_line_of_the_picture(digits_1_the_8_th_line_of_the_picture),
    .the_9_th_line_of_the_picture(digits_1_the_9_th_line_of_the_picture),
    .the_10_th_line_of_the_picture(digits_1_the_10_th_line_of_the_picture),
    .the_11_th_line_of_the_picture(digits_1_the_11_th_line_of_the_picture),
    .the_12_th_line_of_the_picture(digits_1_the_12_th_line_of_the_picture),
    .the_13_th_line_of_the_picture(digits_1_the_13_th_line_of_the_picture),
    .the_14_th_line_of_the_picture(digits_1_the_14_th_line_of_the_picture),
    .the_15_th_line_of_the_picture(digits_1_the_15_th_line_of_the_picture),
    .digit(record_score_1_the_first_digit),
    .the_16_th_line_of_the_picture(digits_1_the_16_th_line_of_the_picture),
    .the_17_th_line_of_the_picture(digits_1_the_17_th_line_of_the_picture),
    .the_18_th_line_of_the_picture(digits_1_the_18_th_line_of_the_picture),
    .the_19_th_line_of_the_picture(digits_1_the_19_th_line_of_the_picture),
    .the_20_th_line_of_the_picture(digits_1_the_20_th_line_of_the_picture),
    .the_21_st_line_of_the_picture(digits_1_the_21_st_line_of_the_picture),
    .the_22_nd_line_of_the_picture(digits_1_the_22_nd_line_of_the_picture),
    .the_23_rd_line_of_the_picture(digits_1_the_23_rd_line_of_the_picture),
    .the_24_th_line_of_the_picture(digits_1_the_24_th_line_of_the_picture),
    .the_25_th_line_of_the_picture(digits_1_the_25_th_line_of_the_picture),
    .the_26_th_line_of_the_picture(digits_1_the_26_th_line_of_the_picture),
    .the_27_th_line_of_the_picture(digits_1_the_27_th_line_of_the_picture),
    .the_28_th_line_of_the_picture(digits_1_the_28_th_line_of_the_picture),
    .the_29_th_line_of_the_picture(digits_1_the_29_th_line_of_the_picture),
    .the_30_th_line_of_the_picture(digits_1_the_30_th_line_of_the_picture));
  digits digits_2 (
    .the_1_st_line_of_the_picture(digits_2_the_1_st_line_of_the_picture),
    .the_2_nd_line_of_the_picture(digits_2_the_2_nd_line_of_the_picture),
    .the_3_rd_line_of_the_picture(digits_2_the_3_rd_line_of_the_picture),
    .the_4_th_line_of_the_picture(digits_2_the_4_th_line_of_the_picture),
    .the_5_th_line_of_the_picture(digits_2_the_5_th_line_of_the_picture),
    .the_6_th_line_of_the_picture(digits_2_the_6_th_line_of_the_picture),
    .the_7_th_line_of_the_picture(digits_2_the_7_th_line_of_the_picture),
    .the_8_th_line_of_the_picture(digits_2_the_8_th_line_of_the_picture),
    .the_9_th_line_of_the_picture(digits_2_the_9_th_line_of_the_picture),
    .the_10_th_line_of_the_picture(digits_2_the_10_th_line_of_the_picture),
    .the_11_th_line_of_the_picture(digits_2_the_11_th_line_of_the_picture),
    .the_12_th_line_of_the_picture(digits_2_the_12_th_line_of_the_picture),
    .the_13_th_line_of_the_picture(digits_2_the_13_th_line_of_the_picture),
    .the_14_th_line_of_the_picture(digits_2_the_14_th_line_of_the_picture),
    .the_15_th_line_of_the_picture(digits_2_the_15_th_line_of_the_picture), .digit(timer_1_the_first_digit),
    .the_16_th_line_of_the_picture(digits_2_the_16_th_line_of_the_picture),
    .the_17_th_line_of_the_picture(digits_2_the_17_th_line_of_the_picture),
    .the_18_th_line_of_the_picture(digits_2_the_18_th_line_of_the_picture),
    .the_19_th_line_of_the_picture(digits_2_the_19_th_line_of_the_picture),
    .the_20_th_line_of_the_picture(digits_2_the_20_th_line_of_the_picture),
    .the_21_st_line_of_the_picture(digits_2_the_21_st_line_of_the_picture),
    .the_22_nd_line_of_the_picture(digits_2_the_22_nd_line_of_the_picture),
    .the_23_rd_line_of_the_picture(digits_2_the_23_rd_line_of_the_picture),
    .the_24_th_line_of_the_picture(digits_2_the_24_th_line_of_the_picture),
    .the_25_th_line_of_the_picture(digits_2_the_25_th_line_of_the_picture),
    .the_26_th_line_of_the_picture(digits_2_the_26_th_line_of_the_picture),
    .the_27_th_line_of_the_picture(digits_2_the_27_th_line_of_the_picture),
    .the_28_th_line_of_the_picture(digits_2_the_28_th_line_of_the_picture),
    .the_29_th_line_of_the_picture(digits_2_the_29_th_line_of_the_picture),
    .the_30_th_line_of_the_picture(digits_2_the_30_th_line_of_the_picture));
  DotMatrix #(.inputtype("row"), .matrixcols(20), .matrixrows(30)) dotmatrix_201 (
    .row0(digits_2_the_1_st_line_of_the_picture), .row1(digits_2_the_2_nd_line_of_the_picture),
    .row2(digits_2_the_3_rd_line_of_the_picture), .row3(digits_2_the_4_th_line_of_the_picture),
    .row4(digits_2_the_5_th_line_of_the_picture), .row5(digits_2_the_6_th_line_of_the_picture),
    .row6(digits_2_the_7_th_line_of_the_picture), .row7(digits_2_the_8_th_line_of_the_picture),
    .row8(digits_2_the_9_th_line_of_the_picture), .row9(digits_2_the_10_th_line_of_the_picture),
    .row10(digits_2_the_11_th_line_of_the_picture), .row11(digits_2_the_12_th_line_of_the_picture),
    .row12(digits_2_the_13_th_line_of_the_picture), .row13(digits_2_the_14_th_line_of_the_picture),
    .row14(digits_2_the_15_th_line_of_the_picture), .row15(digits_2_the_16_th_line_of_the_picture),
    .row16(digits_2_the_17_th_line_of_the_picture), .row17(digits_2_the_18_th_line_of_the_picture),
    .row18(digits_2_the_19_th_line_of_the_picture), .row19(digits_2_the_20_th_line_of_the_picture),
    .row20(digits_2_the_21_st_line_of_the_picture), .row21(digits_2_the_22_nd_line_of_the_picture),
    .row22(digits_2_the_23_rd_line_of_the_picture), .row23(digits_2_the_24_th_line_of_the_picture),
    .row24(digits_2_the_25_th_line_of_the_picture), .row25(digits_2_the_26_th_line_of_the_picture),
    .row26(digits_2_the_27_th_line_of_the_picture), .row27(digits_2_the_28_th_line_of_the_picture),
    .row28(digits_2_the_29_th_line_of_the_picture), .row29(digits_2_the_30_th_line_of_the_picture));
  DotMatrix #(.inputtype("row"), .matrixcols(20), .matrixrows(30)) dotmatrix_202 (
    .row0(digits_3_the_1_st_line_of_the_picture), .row1(digits_3_the_2_nd_line_of_the_picture),
    .row2(digits_3_the_3_rd_line_of_the_picture), .row3(digits_3_the_4_th_line_of_the_picture),
    .row4(digits_3_the_5_th_line_of_the_picture), .row5(digits_3_the_6_th_line_of_the_picture),
    .row6(digits_3_the_7_th_line_of_the_picture), .row7(digits_3_the_8_th_line_of_the_picture),
    .row8(digits_3_the_9_th_line_of_the_picture), .row9(digits_3_the_10_th_line_of_the_picture),
    .row10(digits_3_the_11_th_line_of_the_picture), .row11(digits_3_the_12_th_line_of_the_picture),
    .row12(digits_3_the_13_th_line_of_the_picture), .row13(digits_3_the_14_th_line_of_the_picture),
    .row14(digits_3_the_15_th_line_of_the_picture), .row15(digits_3_the_16_th_line_of_the_picture),
    .row16(digits_3_the_17_th_line_of_the_picture), .row17(digits_3_the_18_th_line_of_the_picture),
    .row18(digits_3_the_19_th_line_of_the_picture), .row19(digits_3_the_20_th_line_of_the_picture),
    .row20(digits_3_the_21_st_line_of_the_picture), .row21(digits_3_the_22_nd_line_of_the_picture),
    .row22(digits_3_the_23_rd_line_of_the_picture), .row23(digits_3_the_24_th_line_of_the_picture),
    .row24(digits_3_the_25_th_line_of_the_picture), .row25(digits_3_the_26_th_line_of_the_picture),
    .row26(digits_3_the_27_th_line_of_the_picture), .row27(digits_3_the_28_th_line_of_the_picture),
    .row28(digits_3_the_29_th_line_of_the_picture), .row29(digits_3_the_30_th_line_of_the_picture));
  digits digits_3 (
    .the_1_st_line_of_the_picture(digits_3_the_1_st_line_of_the_picture),
    .the_2_nd_line_of_the_picture(digits_3_the_2_nd_line_of_the_picture),
    .the_3_rd_line_of_the_picture(digits_3_the_3_rd_line_of_the_picture),
    .the_4_th_line_of_the_picture(digits_3_the_4_th_line_of_the_picture),
    .the_5_th_line_of_the_picture(digits_3_the_5_th_line_of_the_picture),
    .the_6_th_line_of_the_picture(digits_3_the_6_th_line_of_the_picture),
    .the_7_th_line_of_the_picture(digits_3_the_7_th_line_of_the_picture),
    .the_8_th_line_of_the_picture(digits_3_the_8_th_line_of_the_picture),
    .the_9_th_line_of_the_picture(digits_3_the_9_th_line_of_the_picture),
    .the_10_th_line_of_the_picture(digits_3_the_10_th_line_of_the_picture),
    .the_11_th_line_of_the_picture(digits_3_the_11_th_line_of_the_picture),
    .the_12_th_line_of_the_picture(digits_3_the_12_th_line_of_the_picture),
    .the_13_th_line_of_the_picture(digits_3_the_13_th_line_of_the_picture),
    .the_14_th_line_of_the_picture(digits_3_the_14_th_line_of_the_picture),
    .the_15_th_line_of_the_picture(digits_3_the_15_th_line_of_the_picture), .digit(timer_1_the_second_digit),
    .the_16_th_line_of_the_picture(digits_3_the_16_th_line_of_the_picture),
    .the_17_th_line_of_the_picture(digits_3_the_17_th_line_of_the_picture),
    .the_18_th_line_of_the_picture(digits_3_the_18_th_line_of_the_picture),
    .the_19_th_line_of_the_picture(digits_3_the_19_th_line_of_the_picture),
    .the_20_th_line_of_the_picture(digits_3_the_20_th_line_of_the_picture),
    .the_21_st_line_of_the_picture(digits_3_the_21_st_line_of_the_picture),
    .the_22_nd_line_of_the_picture(digits_3_the_22_nd_line_of_the_picture),
    .the_23_rd_line_of_the_picture(digits_3_the_23_rd_line_of_the_picture),
    .the_24_th_line_of_the_picture(digits_3_the_24_th_line_of_the_picture),
    .the_25_th_line_of_the_picture(digits_3_the_25_th_line_of_the_picture),
    .the_26_th_line_of_the_picture(digits_3_the_26_th_line_of_the_picture),
    .the_27_th_line_of_the_picture(digits_3_the_27_th_line_of_the_picture),
    .the_28_th_line_of_the_picture(digits_3_the_28_th_line_of_the_picture),
    .the_29_th_line_of_the_picture(digits_3_the_29_th_line_of_the_picture),
    .the_30_th_line_of_the_picture(digits_3_the_30_th_line_of_the_picture));
  DotMatrix #(.inputtype("row"), .matrixcols(15), .matrixrows(15)) dotmatrix_203 (
    .row0(lives_1_the_1_st_line_of_the_picture_2), .row1(lives_1_the_2_nd_line_of_the_picture_2),
    .row2(lives_1_the_3_rd_line_of_the_picture_2), .row3(lives_1_the_4_th_line_of_the_picture_2),
    .row4(lives_1_the_5_th_line_of_the_picture_2), .row5(lives_1_the_6_th_line_of_the_picture_2),
    .row6(lives_1_the_7_th_line_of_the_picture_2), .row7(lives_1_the_8_th_line_of_the_picture_2),
    .row8(lives_1_the_9_th_line_of_the_picture_2), .row9(lives_1_the_10_th_line_of_the_picture_2),
    .row10(lives_1_the_11_th_line_of_the_picture_2), .row11(lives_1_the_12_th_line_of_the_picture_2),
    .row12(lives_1_the_13_th_line_of_the_picture_2), .row13(lives_1_the_14_th_line_of_the_picture_2),
    .row14(lives_1_the_15_th_line_of_the_picture_2));
  DotMatrix #(.inputtype("row"), .matrixcols(20), .matrixrows(30)) dotmatrix_204 (
    .row0(digits_4_the_1_st_line_of_the_picture), .row1(digits_4_the_2_nd_line_of_the_picture),
    .row2(digits_4_the_3_rd_line_of_the_picture), .row3(digits_4_the_4_th_line_of_the_picture),
    .row4(digits_4_the_5_th_line_of_the_picture), .row5(digits_4_the_6_th_line_of_the_picture),
    .row6(digits_4_the_7_th_line_of_the_picture), .row7(digits_4_the_8_th_line_of_the_picture),
    .row8(digits_4_the_9_th_line_of_the_picture), .row9(digits_4_the_10_th_line_of_the_picture),
    .row10(digits_4_the_11_th_line_of_the_picture), .row11(digits_4_the_12_th_line_of_the_picture),
    .row12(digits_4_the_13_th_line_of_the_picture), .row13(digits_4_the_14_th_line_of_the_picture),
    .row14(digits_4_the_15_th_line_of_the_picture), .row15(digits_4_the_16_th_line_of_the_picture),
    .row16(digits_4_the_17_th_line_of_the_picture), .row17(digits_4_the_18_th_line_of_the_picture),
    .row18(digits_4_the_19_th_line_of_the_picture), .row19(digits_4_the_20_th_line_of_the_picture),
    .row20(digits_4_the_21_st_line_of_the_picture), .row21(digits_4_the_22_nd_line_of_the_picture),
    .row22(digits_4_the_23_rd_line_of_the_picture), .row23(digits_4_the_24_th_line_of_the_picture),
    .row24(digits_4_the_25_th_line_of_the_picture), .row25(digits_4_the_26_th_line_of_the_picture),
    .row26(digits_4_the_27_th_line_of_the_picture), .row27(digits_4_the_28_th_line_of_the_picture),
    .row28(digits_4_the_29_th_line_of_the_picture), .row29(digits_4_the_30_th_line_of_the_picture));
  digits digits_4 (
    .the_1_st_line_of_the_picture(digits_4_the_1_st_line_of_the_picture),
    .the_2_nd_line_of_the_picture(digits_4_the_2_nd_line_of_the_picture),
    .the_3_rd_line_of_the_picture(digits_4_the_3_rd_line_of_the_picture),
    .the_4_th_line_of_the_picture(digits_4_the_4_th_line_of_the_picture),
    .the_5_th_line_of_the_picture(digits_4_the_5_th_line_of_the_picture),
    .the_6_th_line_of_the_picture(digits_4_the_6_th_line_of_the_picture),
    .the_7_th_line_of_the_picture(digits_4_the_7_th_line_of_the_picture),
    .the_8_th_line_of_the_picture(digits_4_the_8_th_line_of_the_picture),
    .the_9_th_line_of_the_picture(digits_4_the_9_th_line_of_the_picture),
    .the_10_th_line_of_the_picture(digits_4_the_10_th_line_of_the_picture),
    .the_11_th_line_of_the_picture(digits_4_the_11_th_line_of_the_picture),
    .the_12_th_line_of_the_picture(digits_4_the_12_th_line_of_the_picture),
    .the_13_th_line_of_the_picture(digits_4_the_13_th_line_of_the_picture),
    .the_14_th_line_of_the_picture(digits_4_the_14_th_line_of_the_picture),
    .the_15_th_line_of_the_picture(digits_4_the_15_th_line_of_the_picture),
    .digit(record_score_1_the_second_digit),
    .the_16_th_line_of_the_picture(digits_4_the_16_th_line_of_the_picture),
    .the_17_th_line_of_the_picture(digits_4_the_17_th_line_of_the_picture),
    .the_18_th_line_of_the_picture(digits_4_the_18_th_line_of_the_picture),
    .the_19_th_line_of_the_picture(digits_4_the_19_th_line_of_the_picture),
    .the_20_th_line_of_the_picture(digits_4_the_20_th_line_of_the_picture),
    .the_21_st_line_of_the_picture(digits_4_the_21_st_line_of_the_picture),
    .the_22_nd_line_of_the_picture(digits_4_the_22_nd_line_of_the_picture),
    .the_23_rd_line_of_the_picture(digits_4_the_23_rd_line_of_the_picture),
    .the_24_th_line_of_the_picture(digits_4_the_24_th_line_of_the_picture),
    .the_25_th_line_of_the_picture(digits_4_the_25_th_line_of_the_picture),
    .the_26_th_line_of_the_picture(digits_4_the_26_th_line_of_the_picture),
    .the_27_th_line_of_the_picture(digits_4_the_27_th_line_of_the_picture),
    .the_28_th_line_of_the_picture(digits_4_the_28_th_line_of_the_picture),
    .the_29_th_line_of_the_picture(digits_4_the_29_th_line_of_the_picture),
    .the_30_th_line_of_the_picture(digits_4_the_30_th_line_of_the_picture));
  DotMatrix #(.inputtype("row"), .matrixcols(20), .matrixrows(30)) dotmatrix_205 (
    .row0(digits_5_the_1_st_line_of_the_picture), .row1(digits_5_the_2_nd_line_of_the_picture),
    .row2(digits_5_the_3_rd_line_of_the_picture), .row3(digits_5_the_4_th_line_of_the_picture),
    .row4(digits_5_the_5_th_line_of_the_picture), .row5(digits_5_the_6_th_line_of_the_picture),
    .row6(digits_5_the_7_th_line_of_the_picture), .row7(digits_5_the_8_th_line_of_the_picture),
    .row8(digits_5_the_9_th_line_of_the_picture), .row9(digits_5_the_10_th_line_of_the_picture),
    .row10(digits_5_the_11_th_line_of_the_picture), .row11(digits_5_the_12_th_line_of_the_picture),
    .row12(digits_5_the_13_th_line_of_the_picture), .row13(digits_5_the_14_th_line_of_the_picture),
    .row14(digits_5_the_15_th_line_of_the_picture), .row15(digits_5_the_16_th_line_of_the_picture),
    .row16(digits_5_the_17_th_line_of_the_picture), .row17(digits_5_the_18_th_line_of_the_picture),
    .row18(digits_5_the_19_th_line_of_the_picture), .row19(digits_5_the_20_th_line_of_the_picture),
    .row20(digits_5_the_21_st_line_of_the_picture), .row21(digits_5_the_22_nd_line_of_the_picture),
    .row22(digits_5_the_23_rd_line_of_the_picture), .row23(digits_5_the_24_th_line_of_the_picture),
    .row24(digits_5_the_25_th_line_of_the_picture), .row25(digits_5_the_26_th_line_of_the_picture),
    .row26(digits_5_the_27_th_line_of_the_picture), .row27(digits_5_the_28_th_line_of_the_picture),
    .row28(digits_5_the_29_th_line_of_the_picture), .row29(digits_5_the_30_th_line_of_the_picture));
  digits digits_5 (
    .the_1_st_line_of_the_picture(digits_5_the_1_st_line_of_the_picture),
    .the_2_nd_line_of_the_picture(digits_5_the_2_nd_line_of_the_picture),
    .the_3_rd_line_of_the_picture(digits_5_the_3_rd_line_of_the_picture),
    .the_4_th_line_of_the_picture(digits_5_the_4_th_line_of_the_picture),
    .the_5_th_line_of_the_picture(digits_5_the_5_th_line_of_the_picture),
    .the_6_th_line_of_the_picture(digits_5_the_6_th_line_of_the_picture),
    .the_7_th_line_of_the_picture(digits_5_the_7_th_line_of_the_picture),
    .the_8_th_line_of_the_picture(digits_5_the_8_th_line_of_the_picture),
    .the_9_th_line_of_the_picture(digits_5_the_9_th_line_of_the_picture),
    .the_10_th_line_of_the_picture(digits_5_the_10_th_line_of_the_picture),
    .the_11_th_line_of_the_picture(digits_5_the_11_th_line_of_the_picture),
    .the_12_th_line_of_the_picture(digits_5_the_12_th_line_of_the_picture),
    .the_13_th_line_of_the_picture(digits_5_the_13_th_line_of_the_picture),
    .the_14_th_line_of_the_picture(digits_5_the_14_th_line_of_the_picture),
    .the_15_th_line_of_the_picture(digits_5_the_15_th_line_of_the_picture), .digit(lives_1_number_of_lives),
    .the_16_th_line_of_the_picture(digits_5_the_16_th_line_of_the_picture),
    .the_17_th_line_of_the_picture(digits_5_the_17_th_line_of_the_picture),
    .the_18_th_line_of_the_picture(digits_5_the_18_th_line_of_the_picture),
    .the_19_th_line_of_the_picture(digits_5_the_19_th_line_of_the_picture),
    .the_20_th_line_of_the_picture(digits_5_the_20_th_line_of_the_picture),
    .the_21_st_line_of_the_picture(digits_5_the_21_st_line_of_the_picture),
    .the_22_nd_line_of_the_picture(digits_5_the_22_nd_line_of_the_picture),
    .the_23_rd_line_of_the_picture(digits_5_the_23_rd_line_of_the_picture),
    .the_24_th_line_of_the_picture(digits_5_the_24_th_line_of_the_picture),
    .the_25_th_line_of_the_picture(digits_5_the_25_th_line_of_the_picture),
    .the_26_th_line_of_the_picture(digits_5_the_26_th_line_of_the_picture),
    .the_27_th_line_of_the_picture(digits_5_the_27_th_line_of_the_picture),
    .the_28_th_line_of_the_picture(digits_5_the_28_th_line_of_the_picture),
    .the_29_th_line_of_the_picture(digits_5_the_29_th_line_of_the_picture),
    .the_30_th_line_of_the_picture(digits_5_the_30_th_line_of_the_picture));
  DotMatrix #(.inputtype("row"), .matrixcols(32), .matrixrows(32)) dotmatrix_206 (
    .row0(record_score_1_the_1_st_line_of_the_picture_2),
    .row1(record_score_1_the_2_nd_line_of_the_picture_2),
    .row2(record_score_1_the_3_rd_line_of_the_picture_2),
    .row3(record_score_1_the_4_th_line_of_the_picture_2),
    .row4(record_score_1_the_5_th_line_of_the_picture_2),
    .row5(record_score_1_the_6_th_line_of_the_picture_2),
    .row6(record_score_1_the_7_th_line_of_the_picture_2),
    .row7(record_score_1_the_8_th_line_of_the_picture_2),
    .row8(record_score_1_the_9_th_line_of_the_picture_2),
    .row9(record_score_1_the_10_th_line_of_the_picture_2),
    .row10(record_score_1_the_11_th_line_of_the_picture_2),
    .row11(record_score_1_the_12_th_line_of_the_picture_2),
    .row12(record_score_1_the_13_th_line_of_the_picture_2),
    .row13(record_score_1_the_14_th_line_of_the_picture_2),
    .row14(record_score_1_the_15_th_line_of_the_picture_2),
    .row15(record_score_1_the_16_th_line_of_the_picture_2),
    .row16(record_score_1_the_17_th_line_of_the_picture_2),
    .row17(record_score_1_the_18_th_line_of_the_picture_2),
    .row18(record_score_1_the_19_th_line_of_the_picture_2),
    .row19(record_score_1_the_20_th_line_of_the_picture_2),
    .row20(record_score_1_the_21_st_line_of_the_picture_2),
    .row21(record_score_1_the_22_nd_line_of_the_picture_2),
    .row22(record_score_1_the_23_rd_line_of_the_picture_2),
    .row23(record_score_1_the_24_th_line_of_the_picture_2),
    .row24(record_score_1_the_25_th_line_of_the_picture_2),
    .row25(record_score_1_the_26_th_line_of_the_picture_2),
    .row26(record_score_1_the_27_th_line_of_the_picture_2),
    .row27(record_score_1_the_28_th_line_of_the_picture_2),
    .row28(record_score_1_the_29_th_line_of_the_picture_2),
    .row29(record_score_1_the_30_th_line_of_the_picture_2),
    .row30(record_score_1_the_31_st_line_of_the_picture_2),
    .row31(record_score_1_the_32_nd_line_of_the_picture_2));
  DotMatrix #(.inputtype("row"), .matrixcols(15), .matrixrows(15)) dotmatrix_207 (
    .row0(lives_1_the_1_st_line_of_the_picture_3), .row1(lives_1_the_2_nd_line_of_the_picture_3),
    .row2(lives_1_the_3_rd_line_of_the_picture_3), .row3(lives_1_the_4_th_line_of_the_picture_3),
    .row4(lives_1_the_5_th_line_of_the_picture_3), .row5(lives_1_the_6_th_line_of_the_picture_3),
    .row6(lives_1_the_8_th_line_of_the_picture_3), .row7(lives_1_the_7_th_line_of_the_picture_3),
    .row8(lives_1_the_9_th_line_of_the_picture_3), .row9(lives_1_the_10_th_line_of_the_picture_3),
    .row10(lives_1_the_11_th_line_of_the_picture_3), .row11(lives_1_the_12_th_line_of_the_picture_3),
    .row12(lives_1_the_13_th_line_of_the_picture_3), .row13(lives_1_the_14_th_line_of_the_picture_3),
    .row14(lives_1_the_15_th_line_of_the_picture_3));
  timer timer_1 (
    .the_1_st_line_of_the_picture_3(timer_1_the_1_st_line_of_the_picture_3),
    .the_6_th_line_of_the_picture_3(timer_1_the_6_th_line_of_the_picture_3),
    .the_2_nd_line_of_the_picture_3(timer_1_the_2_nd_line_of_the_picture_3),
    .the_7_th_line_of_the_picture_3(timer_1_the_7_th_line_of_the_picture_3),
    .the_3_rd_line_of_the_picture_3(timer_1_the_3_rd_line_of_the_picture_3),
    .the_8_th_line_of_the_picture_3(timer_1_the_8_th_line_of_the_picture_3),
    .the_4_th_line_of_the_picture_3(timer_1_the_4_th_line_of_the_picture_3),
    .the_9_th_line_of_the_picture_3(timer_1_the_9_th_line_of_the_picture_3),
    .the_5_th_line_of_the_picture_3(timer_1_the_5_th_line_of_the_picture_3),
    .the_10_th_line_of_the_picture_3(timer_1_the_10_th_line_of_the_picture_3),
    .the_1_st_line_of_the_picture(timer_1_the_1_st_line_of_the_picture),
    .the_6_th_line_of_the_picture(timer_1_the_6_th_line_of_the_picture),
    .the_2_nd_line_of_the_picture(timer_1_the_2_nd_line_of_the_picture),
    .the_7_th_line_of_the_picture(timer_1_the_7_th_line_of_the_picture),
    .the_3_rd_line_of_the_picture(timer_1_the_3_rd_line_of_the_picture),
    .the_8_th_line_of_the_picture(timer_1_the_8_th_line_of_the_picture),
    .the_4_th_line_of_the_picture(timer_1_the_4_th_line_of_the_picture),
    .the_9_th_line_of_the_picture(timer_1_the_9_th_line_of_the_picture),
    .the_5_th_line_of_the_picture(timer_1_the_5_th_line_of_the_picture),
    .the_10_th_line_of_the_picture(timer_1_the_10_th_line_of_the_picture),
    .the_first_digit(timer_1_the_first_digit), .the_second_digit(timer_1_the_second_digit),
    .time_flow__time_shift____left(timer_1_time_flow__time_shift____left), .clock(controlled_buffer_2_out),
    .clear(res), .time_is_gone(time_is_gone),
    .the_11_th_line_of_the_picture_3(timer_1_the_11_th_line_of_the_picture_3),
    .the_12_th_line_of_the_picture_3(timer_1_the_12_th_line_of_the_picture_3),
    .the_13_th_line_of_the_picture_3(timer_1_the_13_th_line_of_the_picture_3),
    .the_14_th_line_of_the_picture_3(timer_1_the_14_th_line_of_the_picture_3),
    .the_15_th_line_of_the_picture_3(timer_1_the_15_th_line_of_the_picture_3),
    .the_16_th_line_of_the_picture_3(timer_1_the_16_th_line_of_the_picture_3),
    .the_17_th_line_of_the_picture(timer_1_the_17_th_line_of_the_picture),
    .the_18_th_line_of_the_picture(timer_1_the_18_th_line_of_the_picture),
    .the_19_th_line_of_the_picture(timer_1_the_19_th_line_of_the_picture),
    .the_20_th_line_of_the_picture(timer_1_the_20_th_line_of_the_picture),
    .the_21_st_line_of_the_picture(timer_1_the_21_st_line_of_the_picture),
    .the_22_nd_line_of_the_picture(timer_1_the_22_nd_line_of_the_picture),
    .the_23_rd_line_of_the_picture(timer_1_the_23_rd_line_of_the_picture),
    .the_24_th_line_of_the_picture(timer_1_the_24_th_line_of_the_picture),
    .the_25_th_line_of_the_picture(timer_1_the_25_th_line_of_the_picture),
    .the_26_th_line_of_the_picture(timer_1_the_26_th_line_of_the_picture),
    .the_27_th_line_of_the_picture(timer_1_the_27_th_line_of_the_picture),
    .the_28_th_line_of_the_picture(timer_1_the_28_th_line_of_the_picture),
    .the_29_th_line_of_the_picture(timer_1_the_29_th_line_of_the_picture),
    .the_30_th_line_of_the_picture(timer_1_the_30_th_line_of_the_picture),
    .the_31_st_line_of_the_picture(timer_1_the_31_st_line_of_the_picture),
    .the_32_nd_line_of_the_picture(timer_1_the_32_nd_line_of_the_picture),
    .the_1_st_line_of_the_picture_4(timer_1_the_1_st_line_of_the_picture_4),
    .the_17_th_line_of_the_picture_2(timer_1_the_17_th_line_of_the_picture_2),
    .the_2_nd_line_of_the_picture_4(timer_1_the_2_nd_line_of_the_picture_4),
    .the_18_th_line_of_the_picture_2(timer_1_the_18_th_line_of_the_picture_2),
    .the_3_rd_line_of_the_picture_4(timer_1_the_3_rd_line_of_the_picture_4),
    .the_19_th_line_of_the_picture_2(timer_1_the_19_th_line_of_the_picture_2),
    .the_4_th_line_of_the_picture_4(timer_1_the_4_th_line_of_the_picture_4),
    .the_20_th_line_of_the_picture_2(timer_1_the_20_th_line_of_the_picture_2),
    .the_5_th_line_of_the_picture_4(timer_1_the_5_th_line_of_the_picture_4),
    .the_21_st_line_of_the_picture_2(timer_1_the_21_st_line_of_the_picture_2),
    .the_6_th_line_of_the_picture_4(timer_1_the_6_th_line_of_the_picture_4),
    .the_22_nd_line_of_the_picture_2(timer_1_the_22_nd_line_of_the_picture_2),
    .the_7_th_line_of_the_picture_4(timer_1_the_7_th_line_of_the_picture_4),
    .the_23_rd_line_of_the_picture_2(timer_1_the_23_rd_line_of_the_picture_2),
    .the_8_th_line_of_the_picture_4(timer_1_the_8_th_line_of_the_picture_4),
    .the_24_th_line_of_the_picture_2(timer_1_the_24_th_line_of_the_picture_2),
    .the_9_th_line_of_the_picture_4(timer_1_the_9_th_line_of_the_picture_4),
    .the_25_th_line_of_the_picture_2(timer_1_the_25_th_line_of_the_picture_2),
    .the_10_th_line_of_the_picture_4(timer_1_the_10_th_line_of_the_picture_4),
    .the_26_th_line_of_the_picture_2(timer_1_the_26_th_line_of_the_picture_2),
    .the_11_th_line_of_the_picture_4(timer_1_the_11_th_line_of_the_picture_4),
    .the_27_th_line_of_the_picture_2(timer_1_the_27_th_line_of_the_picture_2),
    .the_12_th_line_of_the_picture_4(timer_1_the_12_th_line_of_the_picture_4),
    .the_28_th_line_of_the_picture_2(timer_1_the_28_th_line_of_the_picture_2),
    .the_13_th_line_of_the_picture_4(timer_1_the_13_th_line_of_the_picture_4),
    .the_29_th_line_of_the_picture_2(timer_1_the_29_th_line_of_the_picture_2),
    .the_14_th_line_of_the_picture_4(timer_1_the_14_th_line_of_the_picture_4),
    .the_30_th_line_of_the_picture_2(timer_1_the_30_th_line_of_the_picture_2),
    .the_15_th_line_of_the_picture_4(timer_1_the_15_th_line_of_the_picture_4),
    .the_31_st_line_of_the_picture_2(timer_1_the_31_st_line_of_the_picture_2),
    .the_16_th_line_of_the_picture_4(timer_1_the_16_th_line_of_the_picture_4),
    .the_32_nd_line_of_the_picture_2(timer_1_the_32_nd_line_of_the_picture_2),
    .the_11_th_line_of_the_picture(timer_1_the_11_th_line_of_the_picture),
    .the_12_th_line_of_the_picture(timer_1_the_12_th_line_of_the_picture),
    .the_13_th_line_of_the_picture(timer_1_the_13_th_line_of_the_picture),
    .the_14_th_line_of_the_picture(timer_1_the_14_th_line_of_the_picture),
    .the_15_th_line_of_the_picture(timer_1_the_15_th_line_of_the_picture),
    .the_16_th_line_of_the_picture(timer_1_the_16_th_line_of_the_picture),
    .the_17_th_line_of_the_picture_3(timer_1_the_17_th_line_of_the_picture_3),
    .the_18_th_line_of_the_picture_3(timer_1_the_18_th_line_of_the_picture_3),
    .the_19_th_line_of_the_picture_3(timer_1_the_19_th_line_of_the_picture_3),
    .the_20_th_line_of_the_picture_3(timer_1_the_20_th_line_of_the_picture_3),
    .the_1_st_line_of_the_picture_2(timer_1_the_1_st_line_of_the_picture_2),
    .the_11_th_line_of_the_picture_2(timer_1_the_11_th_line_of_the_picture_2),
    .the_12_th_line_of_the_picture_2(timer_1_the_12_th_line_of_the_picture_2),
    .the_3_rd_line_of_the_picture_2(timer_1_the_3_rd_line_of_the_picture_2),
    .the_13_th_line_of_the_picture_2(timer_1_the_13_th_line_of_the_picture_2),
    .the_4_th_line_of_the_picture_2(timer_1_the_4_th_line_of_the_picture_2),
    .the_14_th_line_of_the_picture_2(timer_1_the_14_th_line_of_the_picture_2),
    .the_5_th_line_of_the_picture_2(timer_1_the_5_th_line_of_the_picture_2),
    .the_15_th_line_of_the_picture_2(timer_1_the_15_th_line_of_the_picture_2),
    .the_6_th_line_of_the_picture_2(timer_1_the_6_th_line_of_the_picture_2),
    .the_16_th_line_of_the_picture_2(timer_1_the_16_th_line_of_the_picture_2),
    .the_7_th_line_of_the_picture_2(timer_1_the_7_th_line_of_the_picture_2),
    .the_17_th_line_of_the_picture_4(timer_1_the_17_th_line_of_the_picture_4),
    .the_8_th_line_of_the_picture_2(timer_1_the_8_th_line_of_the_picture_2),
    .the_18_th_line_of_the_picture_4(timer_1_the_18_th_line_of_the_picture_4),
    .the_9_th_line_of_the_picture_2(timer_1_the_9_th_line_of_the_picture_2),
    .the_19_th_line_of_the_picture_4(timer_1_the_19_th_line_of_the_picture_4),
    .the_20_th_line_of_the_picture_4(timer_1_the_20_th_line_of_the_picture_4),
    .the_10_th_line_of_the_picture_2(timer_1_the_10_th_line_of_the_picture_2),
    .the_2_nd_line_of_the_picture_2(timer_1_the_2_nd_line_of_the_picture_2),
    .time_flow__time_shift____right(timer_1_time_flow__time_shift____right));
  DotMatrix #(.inputtype("row"), .matrixcols(32), .matrixrows(20)) dotmatrix_208 (
    .row0(timer_1_time_flow__time_shift____left), .row1(timer_1_time_flow__time_shift____left),
    .row2(timer_1_time_flow__time_shift____left), .row3(timer_1_time_flow__time_shift____left),
    .row4(timer_1_time_flow__time_shift____left), .row5(timer_1_time_flow__time_shift____left),
    .row6(timer_1_time_flow__time_shift____left), .row7(timer_1_time_flow__time_shift____left),
    .row8(timer_1_time_flow__time_shift____left), .row9(timer_1_time_flow__time_shift____left),
    .row10(timer_1_time_flow__time_shift____left), .row11(timer_1_time_flow__time_shift____left),
    .row12(timer_1_time_flow__time_shift____left), .row13(timer_1_time_flow__time_shift____left),
    .row14(timer_1_time_flow__time_shift____left), .row15(timer_1_time_flow__time_shift____left),
    .row16(timer_1_time_flow__time_shift____left), .row17(timer_1_time_flow__time_shift____left),
    .row18(timer_1_time_flow__time_shift____left), .row19(timer_1_time_flow__time_shift____left));
  digits digits_6 (
    .the_1_st_line_of_the_picture(digits_6_the_1_st_line_of_the_picture),
    .the_2_nd_line_of_the_picture(digits_6_the_2_nd_line_of_the_picture),
    .the_3_rd_line_of_the_picture(digits_6_the_3_rd_line_of_the_picture),
    .the_4_th_line_of_the_picture(digits_6_the_4_th_line_of_the_picture),
    .the_5_th_line_of_the_picture(digits_6_the_5_th_line_of_the_picture),
    .the_6_th_line_of_the_picture(digits_6_the_6_th_line_of_the_picture),
    .the_7_th_line_of_the_picture(digits_6_the_7_th_line_of_the_picture),
    .the_8_th_line_of_the_picture(digits_6_the_8_th_line_of_the_picture),
    .the_9_th_line_of_the_picture(digits_6_the_9_th_line_of_the_picture),
    .the_10_th_line_of_the_picture(digits_6_the_10_th_line_of_the_picture),
    .the_11_th_line_of_the_picture(digits_6_the_11_th_line_of_the_picture),
    .the_12_th_line_of_the_picture(digits_6_the_12_th_line_of_the_picture),
    .the_13_th_line_of_the_picture(digits_6_the_13_th_line_of_the_picture),
    .the_14_th_line_of_the_picture(digits_6_the_14_th_line_of_the_picture),
    .the_15_th_line_of_the_picture(digits_6_the_15_th_line_of_the_picture),
    .digit(record_score_1_the_third_digit),
    .the_16_th_line_of_the_picture(digits_6_the_16_th_line_of_the_picture),
    .the_17_th_line_of_the_picture(digits_6_the_17_th_line_of_the_picture),
    .the_18_th_line_of_the_picture(digits_6_the_18_th_line_of_the_picture),
    .the_19_th_line_of_the_picture(digits_6_the_19_th_line_of_the_picture),
    .the_20_th_line_of_the_picture(digits_6_the_20_th_line_of_the_picture),
    .the_21_st_line_of_the_picture(digits_6_the_21_st_line_of_the_picture),
    .the_22_nd_line_of_the_picture(digits_6_the_22_nd_line_of_the_picture),
    .the_23_rd_line_of_the_picture(digits_6_the_23_rd_line_of_the_picture),
    .the_24_th_line_of_the_picture(digits_6_the_24_th_line_of_the_picture),
    .the_25_th_line_of_the_picture(digits_6_the_25_th_line_of_the_picture),
    .the_26_th_line_of_the_picture(digits_6_the_26_th_line_of_the_picture),
    .the_27_th_line_of_the_picture(digits_6_the_27_th_line_of_the_picture),
    .the_28_th_line_of_the_picture(digits_6_the_28_th_line_of_the_picture),
    .the_29_th_line_of_the_picture(digits_6_the_29_th_line_of_the_picture),
    .the_30_th_line_of_the_picture(digits_6_the_30_th_line_of_the_picture));
  DotMatrix #(.inputtype("row"), .matrixcols(20), .matrixrows(30)) dotmatrix_209 (
    .row0(digits_6_the_1_st_line_of_the_picture), .row1(digits_6_the_2_nd_line_of_the_picture),
    .row2(digits_6_the_3_rd_line_of_the_picture), .row3(digits_6_the_4_th_line_of_the_picture),
    .row4(digits_6_the_5_th_line_of_the_picture), .row5(digits_6_the_6_th_line_of_the_picture),
    .row6(digits_6_the_7_th_line_of_the_picture), .row7(digits_6_the_8_th_line_of_the_picture),
    .row8(digits_6_the_9_th_line_of_the_picture), .row9(digits_6_the_10_th_line_of_the_picture),
    .row10(digits_6_the_11_th_line_of_the_picture), .row11(digits_6_the_12_th_line_of_the_picture),
    .row12(digits_6_the_13_th_line_of_the_picture), .row13(digits_6_the_14_th_line_of_the_picture),
    .row14(digits_6_the_15_th_line_of_the_picture), .row15(digits_6_the_16_th_line_of_the_picture),
    .row16(digits_6_the_17_th_line_of_the_picture), .row17(digits_6_the_18_th_line_of_the_picture),
    .row18(digits_6_the_19_th_line_of_the_picture), .row19(digits_6_the_20_th_line_of_the_picture),
    .row20(digits_6_the_21_st_line_of_the_picture), .row21(digits_6_the_22_nd_line_of_the_picture),
    .row22(digits_6_the_23_rd_line_of_the_picture), .row23(digits_6_the_24_th_line_of_the_picture),
    .row24(digits_6_the_25_th_line_of_the_picture), .row25(digits_6_the_26_th_line_of_the_picture),
    .row26(digits_6_the_27_th_line_of_the_picture), .row27(digits_6_the_28_th_line_of_the_picture),
    .row28(digits_6_the_29_th_line_of_the_picture), .row29(digits_6_the_30_th_line_of_the_picture));
  DotMatrix #(.inputtype("row"), .matrixcols(32), .matrixrows(32)) dotmatrix_210 (
    .row0(timer_1_the_1_st_line_of_the_picture_3), .row1(timer_1_the_2_nd_line_of_the_picture_3),
    .row2(timer_1_the_3_rd_line_of_the_picture_3), .row3(timer_1_the_4_th_line_of_the_picture_3),
    .row4(timer_1_the_5_th_line_of_the_picture_3), .row5(timer_1_the_6_th_line_of_the_picture_3),
    .row6(timer_1_the_7_th_line_of_the_picture_3), .row7(timer_1_the_8_th_line_of_the_picture_3),
    .row8(timer_1_the_9_th_line_of_the_picture_3), .row9(timer_1_the_10_th_line_of_the_picture_3),
    .row10(timer_1_the_11_th_line_of_the_picture_3), .row11(timer_1_the_12_th_line_of_the_picture_3),
    .row12(timer_1_the_13_th_line_of_the_picture_3), .row13(timer_1_the_14_th_line_of_the_picture_3),
    .row14(timer_1_the_15_th_line_of_the_picture_3), .row15(timer_1_the_16_th_line_of_the_picture_3),
    .row16(timer_1_the_17_th_line_of_the_picture), .row17(timer_1_the_18_th_line_of_the_picture),
    .row18(timer_1_the_19_th_line_of_the_picture), .row19(timer_1_the_20_th_line_of_the_picture),
    .row20(timer_1_the_21_st_line_of_the_picture), .row21(timer_1_the_22_nd_line_of_the_picture),
    .row22(timer_1_the_23_rd_line_of_the_picture), .row23(timer_1_the_24_th_line_of_the_picture),
    .row24(timer_1_the_25_th_line_of_the_picture), .row25(timer_1_the_26_th_line_of_the_picture),
    .row26(timer_1_the_27_th_line_of_the_picture), .row27(timer_1_the_28_th_line_of_the_picture),
    .row28(timer_1_the_29_th_line_of_the_picture), .row29(timer_1_the_30_th_line_of_the_picture),
    .row30(timer_1_the_31_st_line_of_the_picture), .row31(timer_1_the_32_nd_line_of_the_picture));
  DotMatrix #(.inputtype("row"), .matrixcols(32), .matrixrows(20)) dotmatrix_211 (
    .row0(timer_1_the_1_st_line_of_the_picture), .row1(timer_1_the_2_nd_line_of_the_picture),
    .row2(timer_1_the_3_rd_line_of_the_picture), .row3(timer_1_the_4_th_line_of_the_picture),
    .row4(timer_1_the_5_th_line_of_the_picture), .row5(timer_1_the_6_th_line_of_the_picture),
    .row6(timer_1_the_7_th_line_of_the_picture), .row7(timer_1_the_8_th_line_of_the_picture),
    .row8(timer_1_the_9_th_line_of_the_picture), .row9(timer_1_the_10_th_line_of_the_picture),
    .row10(timer_1_the_11_th_line_of_the_picture), .row11(timer_1_the_12_th_line_of_the_picture),
    .row12(timer_1_the_13_th_line_of_the_picture), .row13(timer_1_the_14_th_line_of_the_picture),
    .row14(timer_1_the_15_th_line_of_the_picture), .row15(timer_1_the_16_th_line_of_the_picture),
    .row16(timer_1_the_17_th_line_of_the_picture_3), .row17(timer_1_the_18_th_line_of_the_picture_3),
    .row18(timer_1_the_19_th_line_of_the_picture_3), .row19(timer_1_the_20_th_line_of_the_picture_3));
  not not_2 (not_2_out, stop);
  assign controlled_buffer_2_out = not_2_out ? level_clock : 1'bz;  // Controlled_Buffer controlled_buffer_2
  DotMatrix #(.inputtype("row"), .matrixcols(27), .matrixrows(23)) dotmatrix_212 (
    .row0(number_of_saved_frogs_victory_lose_1_the_1_st_line_of_the_picture),
    .row1(number_of_saved_frogs_victory_lose_1_the_2_nd_line_of_the_picture),
    .row2(number_of_saved_frogs_victory_lose_1_the_3_rd_line_of_the_picture),
    .row3(number_of_saved_frogs_victory_lose_1_the_4_th_line_of_the_picture),
    .row4(number_of_saved_frogs_victory_lose_1_the_5_th_line_of_the_picture),
    .row5(number_of_saved_frogs_victory_lose_1_the_6_th_line_of_the_picture),
    .row6(number_of_saved_frogs_victory_lose_1_the_7_th_line_of_the_picture),
    .row7(number_of_saved_frogs_victory_lose_1_the_8_th_line_of_the_picture),
    .row8(number_of_saved_frogs_victory_lose_1_the_9_th_line_of_the_picture),
    .row9(number_of_saved_frogs_victory_lose_1_the_10_th_line_of_the_picture),
    .row10(number_of_saved_frogs_victory_lose_1_the_11_th_line_of_the_picture),
    .row11(number_of_saved_frogs_victory_lose_1_the_12_th_line_of_the_picture),
    .row12(number_of_saved_frogs_victory_lose_1_the_13_th_line_of_the_picture),
    .row13(number_of_saved_frogs_victory_lose_1_the_14_th_line_of_the_picture),
    .row14(number_of_saved_frogs_victory_lose_1_the_15_th_line_of_the_picture),
    .row15(number_of_saved_frogs_victory_lose_1_the_16_th_line_of_the_picture),
    .row16(number_of_saved_frogs_victory_lose_1_the_17_th_line_of_the_picture),
    .row17(number_of_saved_frogs_victory_lose_1_the_18_th_line_of_the_picture),
    .row18(number_of_saved_frogs_victory_lose_1_the_19_th_line_of_the_picture),
    .row19(number_of_saved_frogs_victory_lose_1_the_20_th_line_of_the_picture),
    .row20(number_of_saved_frogs_victory_lose_1_the_21_st_line_of_the_picture),
    .row21(number_of_saved_frogs_victory_lose_1_the_22_nd_line_of_the_picture),
    .row22(number_of_saved_frogs_victory_lose_1_the_23_rd_line_of_the_picture));
  number_of_saved_frogs___victory___lose number_of_saved_frogs_victory_lose_1 (
    .the_17_th_line_of_the_picture(number_of_saved_frogs_victory_lose_1_the_17_th_line_of_the_picture),
    .the_1_st_line_of_the_picture(number_of_saved_frogs_victory_lose_1_the_1_st_line_of_the_picture),
    .the_9_th_line_of_the_picture(number_of_saved_frogs_victory_lose_1_the_9_th_line_of_the_picture),
    .the_18_th_line_of_the_picture(number_of_saved_frogs_victory_lose_1_the_18_th_line_of_the_picture),
    .the_2_nd_line_of_the_picture(number_of_saved_frogs_victory_lose_1_the_2_nd_line_of_the_picture),
    .the_10_th_line_of_the_picture(number_of_saved_frogs_victory_lose_1_the_10_th_line_of_the_picture),
    .the_19_th_line_of_the_picture(number_of_saved_frogs_victory_lose_1_the_19_th_line_of_the_picture),
    .the_3_rd_line_of_the_picture(number_of_saved_frogs_victory_lose_1_the_3_rd_line_of_the_picture),
    .the_11_th_line_of_the_picture(number_of_saved_frogs_victory_lose_1_the_11_th_line_of_the_picture),
    .the_20_th_line_of_the_picture(number_of_saved_frogs_victory_lose_1_the_20_th_line_of_the_picture),
    .the_4_th_line_of_the_picture(number_of_saved_frogs_victory_lose_1_the_4_th_line_of_the_picture),
    .the_12_th_line_of_the_picture(number_of_saved_frogs_victory_lose_1_the_12_th_line_of_the_picture),
    .the_21_st_line_of_the_picture(number_of_saved_frogs_victory_lose_1_the_21_st_line_of_the_picture),
    .the_5_th_line_of_the_picture(number_of_saved_frogs_victory_lose_1_the_5_th_line_of_the_picture),
    .the_13_th_line_of_the_picture(number_of_saved_frogs_victory_lose_1_the_13_th_line_of_the_picture),
    .the_22_nd_line_of_the_picture(number_of_saved_frogs_victory_lose_1_the_22_nd_line_of_the_picture),
    .the_6_th_line_of_the_picture(number_of_saved_frogs_victory_lose_1_the_6_th_line_of_the_picture),
    .the_14_th_line_of_the_picture(number_of_saved_frogs_victory_lose_1_the_14_th_line_of_the_picture),
    .the_23_rd_line_of_the_picture(number_of_saved_frogs_victory_lose_1_the_23_rd_line_of_the_picture),
    .the_7_th_line_of_the_picture(number_of_saved_frogs_victory_lose_1_the_7_th_line_of_the_picture),
    .the_15_th_line_of_the_picture(number_of_saved_frogs_victory_lose_1_the_15_th_line_of_the_picture),
    .the_8_th_line_of_the_picture(number_of_saved_frogs_victory_lose_1_the_8_th_line_of_the_picture),
    .the_16_th_line_of_the_picture(number_of_saved_frogs_victory_lose_1_the_16_th_line_of_the_picture),
    .in_out(in_out), .I_Oadr(I_Oadr), .I_Osel(I_Osel), .I_Odat(I_Odat), .clock(clock), .clear(restartGame),
    .number_of_survivors(number_of_saved_frogs_victory_lose_1_number_of_survivors),
    .\event (number_of_saved_frogs_victory_lose_1_event));
  current_score current_score_1 (
    .the_first_digit(current_score_1_the_first_digit), .the_second_digit(current_score_1_the_second_digit),
    .the_third_digit(current_score_1_the_third_digit), .in_out(in_out), .I_Oadr(I_Oadr), .I_Osel(I_Osel),
    .I_Odat(I_Odat), .clock(clock), .clear(restartGame),
    .the_1_st_line_of_the_picture(current_score_1_the_1_st_line_of_the_picture),
    .the_17_th_line_of_the_picture(current_score_1_the_17_th_line_of_the_picture),
    .the_1_st_line_of_the_picture_2(current_score_1_the_1_st_line_of_the_picture_2),
    .the_17_th_line_of_the_picture_2(current_score_1_the_17_th_line_of_the_picture_2),
    .the_2_nd_line_of_the_picture(current_score_1_the_2_nd_line_of_the_picture),
    .the_18_th_line_of_the_picture(current_score_1_the_18_th_line_of_the_picture),
    .the_2_nd_line_of_the_picture_2(current_score_1_the_2_nd_line_of_the_picture_2),
    .the_18_th_line_of_the_picture_2(current_score_1_the_18_th_line_of_the_picture_2),
    .the_3_rd_line_of_the_picture(current_score_1_the_3_rd_line_of_the_picture),
    .the_19_th_line_of_the_picture(current_score_1_the_19_th_line_of_the_picture),
    .the_3_rd_line_of_the_picture_2(current_score_1_the_3_rd_line_of_the_picture_2),
    .the_19_th_line_of_the_picture_2(current_score_1_the_19_th_line_of_the_picture_2),
    .the_4_th_line_of_the_picture(current_score_1_the_4_th_line_of_the_picture),
    .the_20_th_line_of_the_picture(current_score_1_the_20_th_line_of_the_picture),
    .the_4_th_line_of_the_picture_2(current_score_1_the_4_th_line_of_the_picture_2),
    .the_20_th_line_of_the_picture_2(current_score_1_the_20_th_line_of_the_picture_2),
    .the_5_th_line_of_the_picture(current_score_1_the_5_th_line_of_the_picture),
    .the_21_st_line_of_the_picture(current_score_1_the_21_st_line_of_the_picture),
    .the_5_th_line_of_the_picture_2(current_score_1_the_5_th_line_of_the_picture_2),
    .the_21_st_line_of_the_picture_2(current_score_1_the_21_st_line_of_the_picture_2),
    .the_6_th_line_of_the_picture(current_score_1_the_6_th_line_of_the_picture),
    .the_22_nd_line_of_the_picture(current_score_1_the_22_nd_line_of_the_picture),
    .the_6_th_line_of_the_picture_2(current_score_1_the_6_th_line_of_the_picture_2),
    .the_22_nd_line_of_the_picture_2(current_score_1_the_22_nd_line_of_the_picture_2),
    .the_7_th_line_of_the_picture(current_score_1_the_7_th_line_of_the_picture),
    .the_23_rd_line_of_the_picture(current_score_1_the_23_rd_line_of_the_picture),
    .the_7_th_line_of_the_picture_2(current_score_1_the_7_th_line_of_the_picture_2),
    .the_23_rd_line_of_the_picture_2(current_score_1_the_23_rd_line_of_the_picture_2),
    .the_8_th_line_of_the_picture(current_score_1_the_8_th_line_of_the_picture),
    .the_24_th_line_of_the_picture(current_score_1_the_24_th_line_of_the_picture),
    .the_8_th_line_of_the_picture_2(current_score_1_the_8_th_line_of_the_picture_2),
    .the_24_th_line_of_the_picture_2(current_score_1_the_24_th_line_of_the_picture_2),
    .the_9_th_line_of_the_picture(current_score_1_the_9_th_line_of_the_picture),
    .the_25_th_line_of_the_picture(current_score_1_the_25_th_line_of_the_picture),
    .the_9_th_line_of_the_picture_2(current_score_1_the_9_th_line_of_the_picture_2),
    .the_25_th_line_of_the_picture_2(current_score_1_the_25_th_line_of_the_picture_2),
    .the_10_th_line_of_the_picture(current_score_1_the_10_th_line_of_the_picture),
    .the_26_th_line_of_the_picture(current_score_1_the_26_th_line_of_the_picture),
    .the_10_th_line_of_the_picture_2(current_score_1_the_10_th_line_of_the_picture_2),
    .the_26_th_line_of_the_picture_2(current_score_1_the_26_th_line_of_the_picture_2),
    .the_11_th_line_of_the_picture(current_score_1_the_11_th_line_of_the_picture),
    .the_27_th_line_of_the_picture(current_score_1_the_27_th_line_of_the_picture),
    .the_11_th_line_of_the_picture_2(current_score_1_the_11_th_line_of_the_picture_2),
    .the_27_th_line_of_the_picture_2(current_score_1_the_27_th_line_of_the_picture_2),
    .the_12_th_line_of_the_picture(current_score_1_the_12_th_line_of_the_picture),
    .the_28_th_line_of_the_picture(current_score_1_the_28_th_line_of_the_picture),
    .the_12_th_line_of_the_picture_2(current_score_1_the_12_th_line_of_the_picture_2),
    .the_28_th_line_of_the_picture_2(current_score_1_the_28_th_line_of_the_picture_2),
    .the_13_th_line_of_the_picture(current_score_1_the_13_th_line_of_the_picture),
    .the_29_th_line_of_the_picture(current_score_1_the_29_th_line_of_the_picture),
    .the_13_th_line_of_the_picture_2(current_score_1_the_13_th_line_of_the_picture_2),
    .the_29_th_line_of_the_picture_2(current_score_1_the_29_th_line_of_the_picture_2),
    .the_14_th_line_of_the_picture(current_score_1_the_14_th_line_of_the_picture),
    .the_30_th_line_of_the_picture(current_score_1_the_30_th_line_of_the_picture),
    .the_14_th_line_of_the_picture_2(current_score_1_the_14_th_line_of_the_picture_2),
    .the_30_th_line_of_the_picture_2(current_score_1_the_30_th_line_of_the_picture_2),
    .the_15_th_line_of_the_picture(current_score_1_the_15_th_line_of_the_picture),
    .the_31_st_line_of_the_picture(current_score_1_the_31_st_line_of_the_picture),
    .the_15_th_line_of_the_picture_2(current_score_1_the_15_th_line_of_the_picture_2),
    .the_31_st_line_of_the_picture_2(current_score_1_the_31_st_line_of_the_picture_2),
    .the_16_th_line_of_the_picture(current_score_1_the_16_th_line_of_the_picture),
    .the_32_nd_line_of_the_picture(current_score_1_the_32_nd_line_of_the_picture),
    .the_16_th_line_of_the_picture_2(current_score_1_the_16_th_line_of_the_picture_2),
    .the_32_nd_line_of_the_picture_2(current_score_1_the_32_nd_line_of_the_picture_2));
  DotMatrix #(.inputtype("row"), .matrixcols(32), .matrixrows(32)) dotmatrix_213 (
    .row0(current_score_1_the_1_st_line_of_the_picture), .row1(current_score_1_the_2_nd_line_of_the_picture),
    .row2(current_score_1_the_3_rd_line_of_the_picture), .row3(current_score_1_the_4_th_line_of_the_picture),
    .row4(current_score_1_the_5_th_line_of_the_picture), .row5(current_score_1_the_6_th_line_of_the_picture),
    .row6(current_score_1_the_7_th_line_of_the_picture), .row7(current_score_1_the_8_th_line_of_the_picture),
    .row8(current_score_1_the_9_th_line_of_the_picture),
    .row9(current_score_1_the_10_th_line_of_the_picture),
    .row10(current_score_1_the_11_th_line_of_the_picture),
    .row11(current_score_1_the_12_th_line_of_the_picture),
    .row12(current_score_1_the_13_th_line_of_the_picture),
    .row13(current_score_1_the_14_th_line_of_the_picture),
    .row14(current_score_1_the_15_th_line_of_the_picture),
    .row15(current_score_1_the_16_th_line_of_the_picture),
    .row16(current_score_1_the_17_th_line_of_the_picture),
    .row17(current_score_1_the_18_th_line_of_the_picture),
    .row18(current_score_1_the_19_th_line_of_the_picture),
    .row19(current_score_1_the_20_th_line_of_the_picture),
    .row20(current_score_1_the_21_st_line_of_the_picture),
    .row21(current_score_1_the_22_nd_line_of_the_picture),
    .row22(current_score_1_the_23_rd_line_of_the_picture),
    .row23(current_score_1_the_24_th_line_of_the_picture),
    .row24(current_score_1_the_25_th_line_of_the_picture),
    .row25(current_score_1_the_26_th_line_of_the_picture),
    .row26(current_score_1_the_27_th_line_of_the_picture),
    .row27(current_score_1_the_28_th_line_of_the_picture),
    .row28(current_score_1_the_29_th_line_of_the_picture),
    .row29(current_score_1_the_30_th_line_of_the_picture),
    .row30(current_score_1_the_31_st_line_of_the_picture),
    .row31(current_score_1_the_32_nd_line_of_the_picture));
  DotMatrix #(.inputtype("row"), .matrixcols(20), .matrixrows(30)) dotmatrix_214 (
    .row0(digits_7_the_1_st_line_of_the_picture), .row1(digits_7_the_2_nd_line_of_the_picture),
    .row2(digits_7_the_3_rd_line_of_the_picture), .row3(digits_7_the_4_th_line_of_the_picture),
    .row4(digits_7_the_5_th_line_of_the_picture), .row5(digits_7_the_6_th_line_of_the_picture),
    .row6(digits_7_the_7_th_line_of_the_picture), .row7(digits_7_the_8_th_line_of_the_picture),
    .row8(digits_7_the_9_th_line_of_the_picture), .row9(digits_7_the_10_th_line_of_the_picture),
    .row10(digits_7_the_11_th_line_of_the_picture), .row11(digits_7_the_12_th_line_of_the_picture),
    .row12(digits_7_the_13_th_line_of_the_picture), .row13(digits_7_the_14_th_line_of_the_picture),
    .row14(digits_7_the_15_th_line_of_the_picture), .row15(digits_7_the_16_th_line_of_the_picture),
    .row16(digits_7_the_17_th_line_of_the_picture), .row17(digits_7_the_18_th_line_of_the_picture),
    .row18(digits_7_the_19_th_line_of_the_picture), .row19(digits_7_the_20_th_line_of_the_picture),
    .row20(digits_7_the_21_st_line_of_the_picture), .row21(digits_7_the_22_nd_line_of_the_picture),
    .row22(digits_7_the_23_rd_line_of_the_picture), .row23(digits_7_the_24_th_line_of_the_picture),
    .row24(digits_7_the_25_th_line_of_the_picture), .row25(digits_7_the_26_th_line_of_the_picture),
    .row26(digits_7_the_27_th_line_of_the_picture), .row27(digits_7_the_28_th_line_of_the_picture),
    .row28(digits_7_the_29_th_line_of_the_picture), .row29(digits_7_the_30_th_line_of_the_picture));
  digits digits_7 (
    .the_1_st_line_of_the_picture(digits_7_the_1_st_line_of_the_picture),
    .the_2_nd_line_of_the_picture(digits_7_the_2_nd_line_of_the_picture),
    .the_3_rd_line_of_the_picture(digits_7_the_3_rd_line_of_the_picture),
    .the_4_th_line_of_the_picture(digits_7_the_4_th_line_of_the_picture),
    .the_5_th_line_of_the_picture(digits_7_the_5_th_line_of_the_picture),
    .the_6_th_line_of_the_picture(digits_7_the_6_th_line_of_the_picture),
    .the_7_th_line_of_the_picture(digits_7_the_7_th_line_of_the_picture),
    .the_8_th_line_of_the_picture(digits_7_the_8_th_line_of_the_picture),
    .the_9_th_line_of_the_picture(digits_7_the_9_th_line_of_the_picture),
    .the_10_th_line_of_the_picture(digits_7_the_10_th_line_of_the_picture),
    .the_11_th_line_of_the_picture(digits_7_the_11_th_line_of_the_picture),
    .the_12_th_line_of_the_picture(digits_7_the_12_th_line_of_the_picture),
    .the_13_th_line_of_the_picture(digits_7_the_13_th_line_of_the_picture),
    .the_14_th_line_of_the_picture(digits_7_the_14_th_line_of_the_picture),
    .the_15_th_line_of_the_picture(digits_7_the_15_th_line_of_the_picture),
    .digit(current_score_1_the_first_digit),
    .the_16_th_line_of_the_picture(digits_7_the_16_th_line_of_the_picture),
    .the_17_th_line_of_the_picture(digits_7_the_17_th_line_of_the_picture),
    .the_18_th_line_of_the_picture(digits_7_the_18_th_line_of_the_picture),
    .the_19_th_line_of_the_picture(digits_7_the_19_th_line_of_the_picture),
    .the_20_th_line_of_the_picture(digits_7_the_20_th_line_of_the_picture),
    .the_21_st_line_of_the_picture(digits_7_the_21_st_line_of_the_picture),
    .the_22_nd_line_of_the_picture(digits_7_the_22_nd_line_of_the_picture),
    .the_23_rd_line_of_the_picture(digits_7_the_23_rd_line_of_the_picture),
    .the_24_th_line_of_the_picture(digits_7_the_24_th_line_of_the_picture),
    .the_25_th_line_of_the_picture(digits_7_the_25_th_line_of_the_picture),
    .the_26_th_line_of_the_picture(digits_7_the_26_th_line_of_the_picture),
    .the_27_th_line_of_the_picture(digits_7_the_27_th_line_of_the_picture),
    .the_28_th_line_of_the_picture(digits_7_the_28_th_line_of_the_picture),
    .the_29_th_line_of_the_picture(digits_7_the_29_th_line_of_the_picture),
    .the_30_th_line_of_the_picture(digits_7_the_30_th_line_of_the_picture));
  DotMatrix #(.inputtype("row"), .matrixcols(32), .matrixrows(20)) dotmatrix_215 (
    .row0(timer_1_time_flow__time_shift____right), .row1(timer_1_time_flow__time_shift____right),
    .row2(timer_1_time_flow__time_shift____right), .row3(timer_1_time_flow__time_shift____right),
    .row4(timer_1_time_flow__time_shift____right), .row5(timer_1_time_flow__time_shift____right),
    .row6(timer_1_time_flow__time_shift____right), .row7(timer_1_time_flow__time_shift____right),
    .row8(timer_1_time_flow__time_shift____right), .row9(timer_1_time_flow__time_shift____right),
    .row10(timer_1_time_flow__time_shift____right), .row11(timer_1_time_flow__time_shift____right),
    .row12(timer_1_time_flow__time_shift____right), .row13(timer_1_time_flow__time_shift____right),
    .row14(timer_1_time_flow__time_shift____right), .row15(timer_1_time_flow__time_shift____right),
    .row16(timer_1_time_flow__time_shift____right), .row17(timer_1_time_flow__time_shift____right),
    .row18(timer_1_time_flow__time_shift____right), .row19(timer_1_time_flow__time_shift____right));
  DotMatrix #(.inputtype("row"), .matrixcols(32), .matrixrows(32)) dotmatrix_216 (
    .row0(timer_1_the_1_st_line_of_the_picture_4), .row1(timer_1_the_2_nd_line_of_the_picture_4),
    .row2(timer_1_the_3_rd_line_of_the_picture_4), .row3(timer_1_the_4_th_line_of_the_picture_4),
    .row4(timer_1_the_5_th_line_of_the_picture_4), .row5(timer_1_the_6_th_line_of_the_picture_4),
    .row6(timer_1_the_7_th_line_of_the_picture_4), .row7(timer_1_the_8_th_line_of_the_picture_4),
    .row8(timer_1_the_9_th_line_of_the_picture_4), .row9(timer_1_the_10_th_line_of_the_picture_4),
    .row10(timer_1_the_11_th_line_of_the_picture_4), .row11(timer_1_the_12_th_line_of_the_picture_4),
    .row12(timer_1_the_13_th_line_of_the_picture_4), .row13(timer_1_the_14_th_line_of_the_picture_4),
    .row14(timer_1_the_15_th_line_of_the_picture_4), .row15(timer_1_the_16_th_line_of_the_picture_4),
    .row16(timer_1_the_17_th_line_of_the_picture_2), .row17(timer_1_the_18_th_line_of_the_picture_2),
    .row18(timer_1_the_19_th_line_of_the_picture_2), .row19(timer_1_the_20_th_line_of_the_picture_2),
    .row20(timer_1_the_21_st_line_of_the_picture_2), .row21(timer_1_the_22_nd_line_of_the_picture_2),
    .row22(timer_1_the_23_rd_line_of_the_picture_2), .row23(timer_1_the_24_th_line_of_the_picture_2),
    .row24(timer_1_the_25_th_line_of_the_picture_2), .row25(timer_1_the_26_th_line_of_the_picture_2),
    .row26(timer_1_the_27_th_line_of_the_picture_2), .row27(timer_1_the_28_th_line_of_the_picture_2),
    .row28(timer_1_the_29_th_line_of_the_picture_2), .row29(timer_1_the_30_th_line_of_the_picture_2),
    .row30(timer_1_the_31_st_line_of_the_picture_2), .row31(timer_1_the_32_nd_line_of_the_picture_2));
  DotMatrix #(.inputtype("row"), .matrixcols(32), .matrixrows(20)) dotmatrix_217 (
    .row0(timer_1_the_1_st_line_of_the_picture_2), .row1(timer_1_the_2_nd_line_of_the_picture_2),
    .row2(timer_1_the_3_rd_line_of_the_picture_2), .row3(timer_1_the_4_th_line_of_the_picture_2),
    .row4(timer_1_the_5_th_line_of_the_picture_2), .row5(timer_1_the_6_th_line_of_the_picture_2),
    .row6(timer_1_the_7_th_line_of_the_picture_2), .row7(timer_1_the_8_th_line_of_the_picture_2),
    .row8(timer_1_the_9_th_line_of_the_picture_2), .row9(timer_1_the_10_th_line_of_the_picture_2),
    .row10(timer_1_the_11_th_line_of_the_picture_2), .row11(timer_1_the_12_th_line_of_the_picture_2),
    .row12(timer_1_the_13_th_line_of_the_picture_2), .row13(timer_1_the_14_th_line_of_the_picture_2),
    .row14(timer_1_the_15_th_line_of_the_picture_2), .row15(timer_1_the_16_th_line_of_the_picture_2),
    .row16(timer_1_the_17_th_line_of_the_picture_4), .row17(timer_1_the_18_th_line_of_the_picture_4),
    .row18(timer_1_the_19_th_line_of_the_picture_4), .row19(timer_1_the_20_th_line_of_the_picture_4));
  digits digits_8 (
    .the_1_st_line_of_the_picture(digits_8_the_1_st_line_of_the_picture),
    .the_2_nd_line_of_the_picture(digits_8_the_2_nd_line_of_the_picture),
    .the_3_rd_line_of_the_picture(digits_8_the_3_rd_line_of_the_picture),
    .the_4_th_line_of_the_picture(digits_8_the_4_th_line_of_the_picture),
    .the_5_th_line_of_the_picture(digits_8_the_5_th_line_of_the_picture),
    .the_6_th_line_of_the_picture(digits_8_the_6_th_line_of_the_picture),
    .the_7_th_line_of_the_picture(digits_8_the_7_th_line_of_the_picture),
    .the_8_th_line_of_the_picture(digits_8_the_8_th_line_of_the_picture),
    .the_9_th_line_of_the_picture(digits_8_the_9_th_line_of_the_picture),
    .the_10_th_line_of_the_picture(digits_8_the_10_th_line_of_the_picture),
    .the_11_th_line_of_the_picture(digits_8_the_11_th_line_of_the_picture),
    .the_12_th_line_of_the_picture(digits_8_the_12_th_line_of_the_picture),
    .the_13_th_line_of_the_picture(digits_8_the_13_th_line_of_the_picture),
    .the_14_th_line_of_the_picture(digits_8_the_14_th_line_of_the_picture),
    .the_15_th_line_of_the_picture(digits_8_the_15_th_line_of_the_picture),
    .digit(number_of_saved_frogs_victory_lose_1_number_of_survivors),
    .the_16_th_line_of_the_picture(digits_8_the_16_th_line_of_the_picture),
    .the_17_th_line_of_the_picture(digits_8_the_17_th_line_of_the_picture),
    .the_18_th_line_of_the_picture(digits_8_the_18_th_line_of_the_picture),
    .the_19_th_line_of_the_picture(digits_8_the_19_th_line_of_the_picture),
    .the_20_th_line_of_the_picture(digits_8_the_20_th_line_of_the_picture),
    .the_21_st_line_of_the_picture(digits_8_the_21_st_line_of_the_picture),
    .the_22_nd_line_of_the_picture(digits_8_the_22_nd_line_of_the_picture),
    .the_23_rd_line_of_the_picture(digits_8_the_23_rd_line_of_the_picture),
    .the_24_th_line_of_the_picture(digits_8_the_24_th_line_of_the_picture),
    .the_25_th_line_of_the_picture(digits_8_the_25_th_line_of_the_picture),
    .the_26_th_line_of_the_picture(digits_8_the_26_th_line_of_the_picture),
    .the_27_th_line_of_the_picture(digits_8_the_27_th_line_of_the_picture),
    .the_28_th_line_of_the_picture(digits_8_the_28_th_line_of_the_picture),
    .the_29_th_line_of_the_picture(digits_8_the_29_th_line_of_the_picture),
    .the_30_th_line_of_the_picture(digits_8_the_30_th_line_of_the_picture));
  DotMatrix #(.inputtype("row"), .matrixcols(20), .matrixrows(30)) dotmatrix_218 (
    .row0(digits_8_the_1_st_line_of_the_picture), .row1(digits_8_the_2_nd_line_of_the_picture),
    .row2(digits_8_the_3_rd_line_of_the_picture), .row3(digits_8_the_4_th_line_of_the_picture),
    .row4(digits_8_the_5_th_line_of_the_picture), .row5(digits_8_the_6_th_line_of_the_picture),
    .row6(digits_8_the_7_th_line_of_the_picture), .row7(digits_8_the_8_th_line_of_the_picture),
    .row8(digits_8_the_9_th_line_of_the_picture), .row9(digits_8_the_10_th_line_of_the_picture),
    .row10(digits_8_the_11_th_line_of_the_picture), .row11(digits_8_the_12_th_line_of_the_picture),
    .row12(digits_8_the_13_th_line_of_the_picture), .row13(digits_8_the_14_th_line_of_the_picture),
    .row14(digits_8_the_15_th_line_of_the_picture), .row15(digits_8_the_16_th_line_of_the_picture),
    .row16(digits_8_the_17_th_line_of_the_picture), .row17(digits_8_the_18_th_line_of_the_picture),
    .row18(digits_8_the_19_th_line_of_the_picture), .row19(digits_8_the_20_th_line_of_the_picture),
    .row20(digits_8_the_21_st_line_of_the_picture), .row21(digits_8_the_22_nd_line_of_the_picture),
    .row22(digits_8_the_23_rd_line_of_the_picture), .row23(digits_8_the_24_th_line_of_the_picture),
    .row24(digits_8_the_25_th_line_of_the_picture), .row25(digits_8_the_26_th_line_of_the_picture),
    .row26(digits_8_the_27_th_line_of_the_picture), .row27(digits_8_the_28_th_line_of_the_picture),
    .row28(digits_8_the_29_th_line_of_the_picture), .row29(digits_8_the_30_th_line_of_the_picture));
  DotMatrix #(.inputtype("row"), .matrixcols(20), .matrixrows(30)) dotmatrix_219 (
    .row0(digits_9_the_1_st_line_of_the_picture), .row1(digits_9_the_2_nd_line_of_the_picture),
    .row2(digits_9_the_3_rd_line_of_the_picture), .row3(digits_9_the_4_th_line_of_the_picture),
    .row4(digits_9_the_5_th_line_of_the_picture), .row5(digits_9_the_6_th_line_of_the_picture),
    .row6(digits_9_the_7_th_line_of_the_picture), .row7(digits_9_the_8_th_line_of_the_picture),
    .row8(digits_9_the_9_th_line_of_the_picture), .row9(digits_9_the_10_th_line_of_the_picture),
    .row10(digits_9_the_11_th_line_of_the_picture), .row11(digits_9_the_12_th_line_of_the_picture),
    .row12(digits_9_the_13_th_line_of_the_picture), .row13(digits_9_the_14_th_line_of_the_picture),
    .row14(digits_9_the_15_th_line_of_the_picture), .row15(digits_9_the_16_th_line_of_the_picture),
    .row16(digits_9_the_17_th_line_of_the_picture), .row17(digits_9_the_18_th_line_of_the_picture),
    .row18(digits_9_the_19_th_line_of_the_picture), .row19(digits_9_the_20_th_line_of_the_picture),
    .row20(digits_9_the_21_st_line_of_the_picture), .row21(digits_9_the_22_nd_line_of_the_picture),
    .row22(digits_9_the_23_rd_line_of_the_picture), .row23(digits_9_the_24_th_line_of_the_picture),
    .row24(digits_9_the_25_th_line_of_the_picture), .row25(digits_9_the_26_th_line_of_the_picture),
    .row26(digits_9_the_27_th_line_of_the_picture), .row27(digits_9_the_28_th_line_of_the_picture),
    .row28(digits_9_the_29_th_line_of_the_picture), .row29(digits_9_the_30_th_line_of_the_picture));
  digits digits_9 (
    .the_1_st_line_of_the_picture(digits_9_the_1_st_line_of_the_picture),
    .the_2_nd_line_of_the_picture(digits_9_the_2_nd_line_of_the_picture),
    .the_3_rd_line_of_the_picture(digits_9_the_3_rd_line_of_the_picture),
    .the_4_th_line_of_the_picture(digits_9_the_4_th_line_of_the_picture),
    .the_5_th_line_of_the_picture(digits_9_the_5_th_line_of_the_picture),
    .the_6_th_line_of_the_picture(digits_9_the_6_th_line_of_the_picture),
    .the_7_th_line_of_the_picture(digits_9_the_7_th_line_of_the_picture),
    .the_8_th_line_of_the_picture(digits_9_the_8_th_line_of_the_picture),
    .the_9_th_line_of_the_picture(digits_9_the_9_th_line_of_the_picture),
    .the_10_th_line_of_the_picture(digits_9_the_10_th_line_of_the_picture),
    .the_11_th_line_of_the_picture(digits_9_the_11_th_line_of_the_picture),
    .the_12_th_line_of_the_picture(digits_9_the_12_th_line_of_the_picture),
    .the_13_th_line_of_the_picture(digits_9_the_13_th_line_of_the_picture),
    .the_14_th_line_of_the_picture(digits_9_the_14_th_line_of_the_picture),
    .the_15_th_line_of_the_picture(digits_9_the_15_th_line_of_the_picture),
    .digit(current_score_1_the_second_digit),
    .the_16_th_line_of_the_picture(digits_9_the_16_th_line_of_the_picture),
    .the_17_th_line_of_the_picture(digits_9_the_17_th_line_of_the_picture),
    .the_18_th_line_of_the_picture(digits_9_the_18_th_line_of_the_picture),
    .the_19_th_line_of_the_picture(digits_9_the_19_th_line_of_the_picture),
    .the_20_th_line_of_the_picture(digits_9_the_20_th_line_of_the_picture),
    .the_21_st_line_of_the_picture(digits_9_the_21_st_line_of_the_picture),
    .the_22_nd_line_of_the_picture(digits_9_the_22_nd_line_of_the_picture),
    .the_23_rd_line_of_the_picture(digits_9_the_23_rd_line_of_the_picture),
    .the_24_th_line_of_the_picture(digits_9_the_24_th_line_of_the_picture),
    .the_25_th_line_of_the_picture(digits_9_the_25_th_line_of_the_picture),
    .the_26_th_line_of_the_picture(digits_9_the_26_th_line_of_the_picture),
    .the_27_th_line_of_the_picture(digits_9_the_27_th_line_of_the_picture),
    .the_28_th_line_of_the_picture(digits_9_the_28_th_line_of_the_picture),
    .the_29_th_line_of_the_picture(digits_9_the_29_th_line_of_the_picture),
    .the_30_th_line_of_the_picture(digits_9_the_30_th_line_of_the_picture));
  or or_6 (\event , win, number_of_saved_frogs_victory_lose_1_event);
  DotMatrix #(.inputtype("row"), .matrixcols(32), .matrixrows(32)) dotmatrix_220 (
    .row0(current_score_1_the_1_st_line_of_the_picture_2),
    .row1(current_score_1_the_2_nd_line_of_the_picture_2),
    .row2(current_score_1_the_3_rd_line_of_the_picture_2),
    .row3(current_score_1_the_4_th_line_of_the_picture_2),
    .row4(current_score_1_the_5_th_line_of_the_picture_2),
    .row5(current_score_1_the_6_th_line_of_the_picture_2),
    .row6(current_score_1_the_7_th_line_of_the_picture_2),
    .row7(current_score_1_the_8_th_line_of_the_picture_2),
    .row8(current_score_1_the_9_th_line_of_the_picture_2),
    .row9(current_score_1_the_10_th_line_of_the_picture_2),
    .row10(current_score_1_the_11_th_line_of_the_picture_2),
    .row11(current_score_1_the_12_th_line_of_the_picture_2),
    .row12(current_score_1_the_13_th_line_of_the_picture_2),
    .row13(current_score_1_the_14_th_line_of_the_picture_2),
    .row14(current_score_1_the_15_th_line_of_the_picture_2),
    .row15(current_score_1_the_16_th_line_of_the_picture_2),
    .row16(current_score_1_the_17_th_line_of_the_picture_2),
    .row17(current_score_1_the_18_th_line_of_the_picture_2),
    .row18(current_score_1_the_19_th_line_of_the_picture_2),
    .row19(current_score_1_the_20_th_line_of_the_picture_2),
    .row20(current_score_1_the_21_st_line_of_the_picture_2),
    .row21(current_score_1_the_22_nd_line_of_the_picture_2),
    .row22(current_score_1_the_23_rd_line_of_the_picture_2),
    .row23(current_score_1_the_24_th_line_of_the_picture_2),
    .row24(current_score_1_the_25_th_line_of_the_picture_2),
    .row25(current_score_1_the_26_th_line_of_the_picture_2),
    .row26(current_score_1_the_27_th_line_of_the_picture_2),
    .row27(current_score_1_the_28_th_line_of_the_picture_2),
    .row28(current_score_1_the_29_th_line_of_the_picture_2),
    .row29(current_score_1_the_30_th_line_of_the_picture_2),
    .row30(current_score_1_the_31_st_line_of_the_picture_2),
    .row31(current_score_1_the_32_nd_line_of_the_picture_2));
  digits digits_10 (
    .the_1_st_line_of_the_picture(digits_10_the_1_st_line_of_the_picture),
    .the_2_nd_line_of_the_picture(digits_10_the_2_nd_line_of_the_picture),
    .the_3_rd_line_of_the_picture(digits_10_the_3_rd_line_of_the_picture),
    .the_4_th_line_of_the_picture(digits_10_the_4_th_line_of_the_picture),
    .the_5_th_line_of_the_picture(digits_10_the_5_th_line_of_the_picture),
    .the_6_th_line_of_the_picture(digits_10_the_6_th_line_of_the_picture),
    .the_7_th_line_of_the_picture(digits_10_the_7_th_line_of_the_picture),
    .the_8_th_line_of_the_picture(digits_10_the_8_th_line_of_the_picture),
    .the_9_th_line_of_the_picture(digits_10_the_9_th_line_of_the_picture),
    .the_10_th_line_of_the_picture(digits_10_the_10_th_line_of_the_picture),
    .the_11_th_line_of_the_picture(digits_10_the_11_th_line_of_the_picture),
    .the_12_th_line_of_the_picture(digits_10_the_12_th_line_of_the_picture),
    .the_13_th_line_of_the_picture(digits_10_the_13_th_line_of_the_picture),
    .the_14_th_line_of_the_picture(digits_10_the_14_th_line_of_the_picture),
    .the_15_th_line_of_the_picture(digits_10_the_15_th_line_of_the_picture),
    .digit(current_score_1_the_third_digit),
    .the_16_th_line_of_the_picture(digits_10_the_16_th_line_of_the_picture),
    .the_17_th_line_of_the_picture(digits_10_the_17_th_line_of_the_picture),
    .the_18_th_line_of_the_picture(digits_10_the_18_th_line_of_the_picture),
    .the_19_th_line_of_the_picture(digits_10_the_19_th_line_of_the_picture),
    .the_20_th_line_of_the_picture(digits_10_the_20_th_line_of_the_picture),
    .the_21_st_line_of_the_picture(digits_10_the_21_st_line_of_the_picture),
    .the_22_nd_line_of_the_picture(digits_10_the_22_nd_line_of_the_picture),
    .the_23_rd_line_of_the_picture(digits_10_the_23_rd_line_of_the_picture),
    .the_24_th_line_of_the_picture(digits_10_the_24_th_line_of_the_picture),
    .the_25_th_line_of_the_picture(digits_10_the_25_th_line_of_the_picture),
    .the_26_th_line_of_the_picture(digits_10_the_26_th_line_of_the_picture),
    .the_27_th_line_of_the_picture(digits_10_the_27_th_line_of_the_picture),
    .the_28_th_line_of_the_picture(digits_10_the_28_th_line_of_the_picture),
    .the_29_th_line_of_the_picture(digits_10_the_29_th_line_of_the_picture),
    .the_30_th_line_of_the_picture(digits_10_the_30_th_line_of_the_picture));
  DotMatrix #(.inputtype("row"), .matrixcols(20), .matrixrows(30)) dotmatrix_221 (
    .row0(digits_10_the_1_st_line_of_the_picture), .row1(digits_10_the_2_nd_line_of_the_picture),
    .row2(digits_10_the_3_rd_line_of_the_picture), .row3(digits_10_the_4_th_line_of_the_picture),
    .row4(digits_10_the_5_th_line_of_the_picture), .row5(digits_10_the_6_th_line_of_the_picture),
    .row6(digits_10_the_7_th_line_of_the_picture), .row7(digits_10_the_8_th_line_of_the_picture),
    .row8(digits_10_the_9_th_line_of_the_picture), .row9(digits_10_the_10_th_line_of_the_picture),
    .row10(digits_10_the_11_th_line_of_the_picture), .row11(digits_10_the_12_th_line_of_the_picture),
    .row12(digits_10_the_13_th_line_of_the_picture), .row13(digits_10_the_14_th_line_of_the_picture),
    .row14(digits_10_the_15_th_line_of_the_picture), .row15(digits_10_the_16_th_line_of_the_picture),
    .row16(digits_10_the_17_th_line_of_the_picture), .row17(digits_10_the_18_th_line_of_the_picture),
    .row18(digits_10_the_19_th_line_of_the_picture), .row19(digits_10_the_20_th_line_of_the_picture),
    .row20(digits_10_the_21_st_line_of_the_picture), .row21(digits_10_the_22_nd_line_of_the_picture),
    .row22(digits_10_the_23_rd_line_of_the_picture), .row23(digits_10_the_24_th_line_of_the_picture),
    .row24(digits_10_the_25_th_line_of_the_picture), .row25(digits_10_the_26_th_line_of_the_picture),
    .row26(digits_10_the_27_th_line_of_the_picture), .row27(digits_10_the_28_th_line_of_the_picture),
    .row28(digits_10_the_29_th_line_of_the_picture), .row29(digits_10_the_30_th_line_of_the_picture));

  // Other names for the same wires on the sheet: resPlOk = rescue
endmodule

// stop
module stopGame (
  input  restart,
  input  tact,
  input  \event ,
  output stopper
);

  wire and_1_out, comparator_1_eq, controlled_buffer_1_out, not_1_out, not_2_out, or_1_out;
  wire [4:0] counter_1_q;

  assign controlled_buffer_1_out = not_1_out ? and_1_out : 1'bz;  // Controlled_Buffer controlled_buffer_1
  not not_1 (not_1_out, or_1_out);
  Counter #(.width(5), .max('h1f)) counter_1 (
    .Q(counter_1_q), .clk(and_1_out), .clr(not_2_out));  // open: load, D, count, carry
  not not_2 (not_2_out, \event );
  and and_1 (and_1_out, tact, \event );
  D_Flip_Flop d_ff_1 (.Q(stopper), .preset(controlled_buffer_1_out), .reset(or_1_out));  // open: clk, D, Qn, en
  or or_1 (or_1_out, comparator_1_eq, restart);
  Comparator #(.width(5), .mode("unsigned")) comparator_1 (
    .a(counter_1_q), .b(5'b11101), .eq(comparator_1_eq));  // open: gt, lt
endmodule

module latency (
  input  in,
  output out
);

  wire not_1_out, not_2_out, not_3_out, not_4_out, not_5_out, not_6_out, not_7_out, not_8_out, not_9_out,
       not_10_out, not_11_out, not_12_out, not_13_out, not_14_out, not_15_out, not_16_out, not_17_out,
       not_18_out, not_19_out, not_20_out, not_21_out, not_22_out, not_23_out, not_24_out, not_25_out,
       not_26_out, not_27_out, not_28_out, not_29_out, not_30_out, not_31_out, not_32_out, not_33_out,
       not_34_out, not_35_out, not_36_out, not_37_out, not_38_out, not_39_out, not_40_out, not_41_out,
       not_42_out, not_43_out, not_44_out, not_45_out, not_46_out, not_47_out, not_48_out, not_49_out,
       not_50_out, not_51_out, not_52_out, not_54_out;

  not not_1 (not_1_out, not_2_out);
  not not_2 (not_2_out, in);
  not not_3 (not_3_out, not_6_out);
  not not_4 (not_4_out, not_1_out);
  not not_5 (not_5_out, not_4_out);
  not not_6 (not_6_out, not_5_out);
  not not_7 (not_7_out, not_3_out);
  not not_8 (not_8_out, not_9_out);
  not not_9 (not_9_out, not_10_out);
  not not_10 (not_10_out, not_7_out);
  not not_11 (not_11_out, not_12_out);
  not not_12 (not_12_out, not_8_out);
  not not_13 (not_13_out, not_11_out);
  not not_14 (not_14_out, not_13_out);
  not not_15 (not_15_out, not_17_out);
  not not_16 (not_16_out, not_18_out);
  not not_17 (not_17_out, not_14_out);
  not not_18 (not_18_out, not_15_out);
  not not_19 (not_19_out, not_22_out);
  not not_20 (not_20_out, not_16_out);
  not not_21 (not_21_out, not_19_out);
  not not_22 (not_22_out, not_20_out);
  not not_23 (not_23_out, not_26_out);
  not not_24 (not_24_out, not_23_out);
  not not_25 (not_25_out, not_21_out);
  not not_26 (not_26_out, not_25_out);
  not not_27 (not_27_out, not_30_out);
  not not_28 (not_28_out, not_24_out);
  not not_29 (not_29_out, not_27_out);
  not not_30 (not_30_out, not_28_out);
  not not_31 (not_31_out, not_33_out);
  not not_32 (not_32_out, not_29_out);
  not not_33 (not_33_out, not_34_out);
  not not_34 (not_34_out, not_32_out);
  not not_35 (not_35_out, not_37_out);
  not not_36 (not_36_out, not_35_out);
  not not_37 (not_37_out, not_31_out);
  not not_38 (not_38_out, not_36_out);
  not not_39 (not_39_out, not_40_out);
  not not_40 (not_40_out, not_41_out);
  not not_41 (not_41_out, not_38_out);
  not not_42 (not_42_out, not_39_out);
  not not_43 (not_43_out, not_45_out);
  not not_44 (not_44_out, not_42_out);
  not not_45 (not_45_out, not_46_out);
  not not_46 (not_46_out, not_44_out);
  not not_47 (not_47_out, not_43_out);
  not not_48 (not_48_out, not_47_out);
  not not_49 (not_49_out, not_50_out);
  not not_50 (not_50_out, not_48_out);
  not not_51 (not_51_out, not_52_out);
  not not_52 (not_52_out, not_49_out);
  not not_53 (out, not_54_out);
  not not_54 (not_54_out, not_51_out);
endmodule
