// Logisim project drivers.circ as structural Verilog: 11 circuits, main circuit carConnectorV2
// carConnector
module carConnectorV2 (
  input  [1:0] inBackShiftD,
  input  [4:0] inputBackShiftM,
  input  [1:0] inPlayerShiftD,
  input  [4:0] inPlayerShiftM,
  input  inFlag,
  output [29:0] toBackground,
  output [29:0] toBackground_2,
  output [29:0] toBackground_3,
  output [29:0] toBackground_4,
  output [29:0] toBackground_5,
  output [1:0] outBackShiftD,
  output [29:0] toBackground_6,
  output [4:0] outputBackShiftM,
  output [29:0] toBackground_7,
  output [29:0] toBackground_8,
  output [29:0] toBackground_9,
  output [29:0] toBackground_10,
  output [1:0] outPlayerShiftD,
  output [4:0] outPlayerShiftM,
  output outFlag,
  output [29:0] toFront,
  output [29:0] toFront_2,
  output [29:0] toFront_3,
  output [29:0] toFront_4,
  output [29:0] toFront_5,
  output [29:0] toFront_6,
  output [29:0] toFront_7,
  output [29:0] toFront_8,
  output [29:0] toFront_9,
  output [29:0] toFront_10
);

  wire comparator_1_eq, comparator_2_eq, comparator_3_eq, comparator_4_eq, comparator_5_eq,
       controlled_buffer_21_out, controlled_buffer_22_out;
  wire [1:0] adder_5_out, multiplexer_1_out;
  wire [4:0] adder_3_out, adder_4_out, adder_6_out, adder_7_out, adder_8_out, not_1_out, not_2_out;
  wire [29:0] controlled_buffer_1_out, controlled_buffer_2_out, controlled_buffer_4_out,
       controlled_buffer_5_out, controlled_buffer_6_out, controlled_buffer_10_out, controlled_buffer_13_out,
       controlled_buffer_15_out, controlled_buffer_16_out, controlled_buffer_19_out,
       controlled_buffer_23_out, controlled_buffer_24_out, controlled_buffer_25_out,
       controlled_buffer_27_out, controlled_buffer_29_out, controlled_buffer_30_out,
       controlled_buffer_32_out, controlled_buffer_34_out, controlled_buffer_37_out, or_1_out, or_2_out,
       or_3_out, or_4_out, or_5_out, or_6_out, or_7_out, or_8_out, or_9_out, or_10_out, pull_resistor_6_node,
       pull_resistor_10_node, pull_resistor_11_node, pull_resistor_12_node, pull_resistor_14_node,
       pull_resistor_15_node, pull_resistor_17_node, pull_resistor_20_node, pull_resistor_21_node,
       pull_resistor_23_node, pull_resistor_29_node, pull_resistor_31_node, pull_resistor_34_node,
       pull_resistor_37_node, pull_resistor_39_node, pull_resistor_40_node, pull_resistor_42_node,
       pull_resistor_43_node, pull_resistor_44_node, pull_resistor_45_node, pull_resistor_46_node,
       shifter_1_out, shifter_2_out, shifter_3_out, shifter_4_out, shifter_5_out, shifter_6_out,
       shifter_7_out, shifter_8_out, shifter_9_out, shifter_10_out, shifter_11_out, shifter_12_out,
       shifter_13_out, shifter_14_out, shifter_15_out, shifter_16_out, shifter_17_out, shifter_18_out,
       shifter_19_out, shifter_20_out, shifter_21_out, shifter_22_out, shifter_23_out, shifter_24_out,
       shifter_25_out, shifter_26_out, shifter_27_out, shifter_28_out, shifter_29_out, shifter_30_out,
       shifter_31_out, shifter_32_out, shifter_33_out, shifter_34_out, shifter_35_out, shifter_36_out,
       shifter_37_out, shifter_38_out, shifter_39_out, shifter_40_out, shifter_41_out, shifter_42_out,
       shifter_43_out, shifter_44_out, shifter_45_out, shifter_46_out, shifter_47_out, shifter_48_out,
       shifter_49_out, shifter_50_out;

  Pull_Resistor pull_resistor_1 (.node(inputBackShiftM));
  Comparator #(.width(2)) comparator_1 (.a(2'b00), .b(inBackShiftD), .eq(comparator_1_eq));  // open: gt, lt
  Adder #(.width(2)) adder_1 (.a(inBackShiftD), .b(2'b01), .out(outBackShiftD));  // open: cin, cout
  // Probe on outBackShiftD
  // Probe on outBackShiftD
  // Probe on 2'b00
  Comparator #(.width(2)) comparator_2 (.a(outBackShiftD), .b(2'b00), .eq(comparator_2_eq));  // open: gt, lt
  Adder #(.width(2)) adder_2 (.a(inPlayerShiftD), .b(2'b01), .out(outPlayerShiftD));  // open: cin, cout
  Pull_Resistor pull_resistor_2 (.node(inPlayerShiftM));
  Adder #(.width(5)) adder_3 (.a(inPlayerShiftM), .b(5'b00001), .out(adder_3_out));  // open: cin, cout
  Comparator #(.width(5), .mode("unsigned")) comparator_3 (
    .a(inPlayerShiftM), .b(5'b11110), .eq(comparator_3_eq));  // open: gt, lt
  Pull_Resistor pull_resistor_3 (.node(comparator_1_eq));
  assign controlled_buffer_1_out = comparator_1_eq ? {30{1'b0}} : 30'bz;  // Controlled_Buffer controlled_buffer_1
  Pull_Resistor pull_resistor_4 (.node(controlled_buffer_1_out));
  assign controlled_buffer_2_out = comparator_1_eq ? 30'h84 : 30'bz;  // Controlled_Buffer controlled_buffer_2
  Pull_Resistor pull_resistor_5 (.node(controlled_buffer_2_out));
  Pull_Resistor pull_resistor_6 (.node(pull_resistor_6_node));
  assign pull_resistor_6_node = comparator_1_eq ? 30'h1fe : 30'bz;  // Controlled_Buffer controlled_buffer_3
  assign controlled_buffer_4_out = comparator_1_eq ? 30'h343 : 30'bz;  // Controlled_Buffer controlled_buffer_4
  Pull_Resistor pull_resistor_7 (.node(controlled_buffer_4_out));
  assign controlled_buffer_5_out = comparator_1_eq ? 30'h243 : 30'bz;  // Controlled_Buffer controlled_buffer_5
  Pull_Resistor pull_resistor_8 (.node(controlled_buffer_5_out));
  assign controlled_buffer_6_out = comparator_1_eq ? 30'h243 : 30'bz;  // Controlled_Buffer controlled_buffer_6
  Pull_Resistor pull_resistor_9 (.node(controlled_buffer_6_out));
  Pull_Resistor pull_resistor_10 (.node(pull_resistor_10_node));
  assign pull_resistor_10_node = comparator_1_eq ? 30'h343 : 30'bz;  // Controlled_Buffer controlled_buffer_7
  Pull_Resistor pull_resistor_11 (.node(pull_resistor_11_node));
  assign pull_resistor_11_node = comparator_1_eq ? 30'h1fe : 30'bz;  // Controlled_Buffer controlled_buffer_8
  Pull_Resistor pull_resistor_12 (.node(pull_resistor_12_node));
  assign pull_resistor_12_node = comparator_1_eq ? 30'h84 : 30'bz;  // Controlled_Buffer controlled_buffer_9
  assign controlled_buffer_10_out = comparator_1_eq ? {30{1'b0}} : 30'bz;  // Controlled_Buffer controlled_buffer_10
  Pull_Resistor pull_resistor_13 (.node(controlled_buffer_10_out));
  assign not_1_out = ~inputBackShiftM;  // NOT_Gate not_1, 5 bits wide
  Multiplexer #(.width(2), .disabled(0), .enable("false")) multiplexer_1 (
    .in0(inPlayerShiftD), .in1(outPlayerShiftD), .out(multiplexer_1_out), .sel(comparator_3_eq));
  Shifter #(.width(30)) shifter_1 (.in(controlled_buffer_1_out), .\dist (inputBackShiftM), .out(shifter_1_out));
  Shifter #(.width(30)) shifter_2 (.in(controlled_buffer_2_out), .\dist (inputBackShiftM), .out(shifter_2_out));
  Shifter #(.width(30)) shifter_3 (.in(pull_resistor_6_node), .\dist (inputBackShiftM), .out(shifter_3_out));
  Shifter #(.width(30)) shifter_4 (.in(controlled_buffer_4_out), .\dist (inputBackShiftM), .out(shifter_4_out));
  Shifter #(.width(30)) shifter_5 (.in(controlled_buffer_5_out), .\dist (inputBackShiftM), .out(shifter_5_out));
  Shifter #(.width(30)) shifter_6 (.in(controlled_buffer_6_out), .\dist (inputBackShiftM), .out(shifter_6_out));
  Shifter #(.width(30)) shifter_7 (.in(pull_resistor_10_node), .\dist (inputBackShiftM), .out(shifter_7_out));
  Shifter #(.width(30)) shifter_8 (.in(pull_resistor_11_node), .\dist (inputBackShiftM), .out(shifter_8_out));
  Shifter #(.width(30)) shifter_9 (.in(pull_resistor_12_node), .\dist (inputBackShiftM), .out(shifter_9_out));
  Shifter #(.width(30)) shifter_10 (.in(controlled_buffer_10_out), .\dist (inputBackShiftM), .out(shifter_10_out));
  Adder #(.width(5)) adder_4 (.a(not_1_out), .b(5'b00001), .out(adder_4_out));  // open: cin, cout
  Pull_Resistor pull_resistor_14 (.node(pull_resistor_14_node));
  assign pull_resistor_14_node = comparator_2_eq ? {30{1'b0}} : 30'bz;  // Controlled_Buffer controlled_buffer_11
  Pull_Resistor pull_resistor_15 (.node(pull_resistor_15_node));
  assign pull_resistor_15_node = comparator_2_eq ? 30'h84 : 30'bz;  // Controlled_Buffer controlled_buffer_12
  assign controlled_buffer_13_out = comparator_2_eq ? 30'h1fe : 30'bz;  // Controlled_Buffer controlled_buffer_13
  Pull_Resistor pull_resistor_16 (.node(controlled_buffer_13_out));
  Pull_Resistor pull_resistor_17 (.node(pull_resistor_17_node));
  assign pull_resistor_17_node = comparator_2_eq ? 30'h343 : 30'bz;  // Controlled_Buffer controlled_buffer_14
  assign controlled_buffer_15_out = comparator_2_eq ? 30'h243 : 30'bz;  // Controlled_Buffer controlled_buffer_15
  Pull_Resistor pull_resistor_18 (.node(controlled_buffer_15_out));
  assign controlled_buffer_16_out = comparator_2_eq ? 30'h243 : 30'bz;  // Controlled_Buffer controlled_buffer_16
  Pull_Resistor pull_resistor_19 (.node(controlled_buffer_16_out));
  Pull_Resistor pull_resistor_20 (.node(pull_resistor_20_node));
  assign pull_resistor_20_node = comparator_2_eq ? 30'h343 : 30'bz;  // Controlled_Buffer controlled_buffer_17
  Pull_Resistor pull_resistor_21 (.node(pull_resistor_21_node));
  assign pull_resistor_21_node = comparator_2_eq ? 30'h1fe : 30'bz;  // Controlled_Buffer controlled_buffer_18
  assign controlled_buffer_19_out = comparator_2_eq ? 30'h84 : 30'bz;  // Controlled_Buffer controlled_buffer_19
  Pull_Resistor pull_resistor_22 (.node(controlled_buffer_19_out));
  Pull_Resistor pull_resistor_23 (.node(pull_resistor_23_node));
  assign pull_resistor_23_node = comparator_2_eq ? {30{1'b0}} : 30'bz;  // Controlled_Buffer controlled_buffer_20
  Pull_Resistor pull_resistor_24 (.node(comparator_2_eq));
  Comparator #(.width(2)) comparator_4 (.a(2'b00), .b(multiplexer_1_out), .eq(comparator_4_eq));  // open: gt, lt
  assign controlled_buffer_21_out = inFlag ? comparator_4_eq : 1'bz;  // Controlled_Buffer controlled_buffer_21
  Comparator #(.width(2)) comparator_5 (.a(2'b00), .b(adder_5_out), .eq(comparator_5_eq));  // open: gt, lt
  Adder #(.width(2)) adder_5 (.a(multiplexer_1_out), .b(2'b01), .out(adder_5_out));  // open: cin, cout
  assign or_1_out = shifter_1_out | shifter_11_out;  // OR_Gate or_1, 30 bits wide
  Adder #(.width(5)) adder_6 (.a(5'b11110), .b(adder_4_out), .out(adder_6_out));  // open: cin, cout
  Shifter #(.width(30), .shift("lr")) shifter_11 (
    .in(pull_resistor_14_node), .\dist (adder_6_out), .out(shifter_11_out));
  Shifter #(.width(30), .shift("lr")) shifter_12 (
    .in(pull_resistor_15_node), .\dist (adder_6_out), .out(shifter_12_out));
  Shifter #(.width(30), .shift("lr")) shifter_13 (
    .in(controlled_buffer_13_out), .\dist (adder_6_out), .out(shifter_13_out));
  Shifter #(.width(30), .shift("lr")) shifter_14 (
    .in(pull_resistor_17_node), .\dist (adder_6_out), .out(shifter_14_out));
  Shifter #(.width(30), .shift("lr")) shifter_15 (
    .in(controlled_buffer_15_out), .\dist (adder_6_out), .out(shifter_15_out));
  Shifter #(.width(30), .shift("lr")) shifter_16 (
    .in(controlled_buffer_16_out), .\dist (adder_6_out), .out(shifter_16_out));
  Shifter #(.width(30), .shift("lr")) shifter_17 (
    .in(pull_resistor_20_node), .\dist (adder_6_out), .out(shifter_17_out));
  Shifter #(.width(30), .shift("lr")) shifter_18 (
    .in(pull_resistor_21_node), .\dist (adder_6_out), .out(shifter_18_out));
  Shifter #(.width(30), .shift("lr")) shifter_19 (
    .in(controlled_buffer_19_out), .\dist (adder_6_out), .out(shifter_19_out));
  Shifter #(.width(30), .shift("lr")) shifter_20 (
    .in(pull_resistor_23_node), .\dist (adder_6_out), .out(shifter_20_out));
  assign or_2_out = shifter_2_out | shifter_12_out;  // OR_Gate or_2, 30 bits wide
  assign or_3_out = shifter_3_out | shifter_13_out;  // OR_Gate or_3, 30 bits wide
  assign or_4_out = shifter_4_out | shifter_14_out;  // OR_Gate or_4, 30 bits wide
  assign or_5_out = shifter_5_out | shifter_15_out;  // OR_Gate or_5, 30 bits wide
  assign or_6_out = shifter_6_out | shifter_16_out;  // OR_Gate or_6, 30 bits wide
  assign or_7_out = shifter_7_out | shifter_17_out;  // OR_Gate or_7, 30 bits wide
  assign or_8_out = shifter_8_out | shifter_18_out;  // OR_Gate or_8, 30 bits wide
  assign or_9_out = shifter_9_out | shifter_19_out;  // OR_Gate or_9, 30 bits wide
  assign controlled_buffer_22_out = inFlag ? comparator_5_eq : 1'bz;  // Controlled_Buffer controlled_buffer_22
  assign or_10_out = shifter_10_out | shifter_20_out;  // OR_Gate or_10, 30 bits wide
  assign controlled_buffer_23_out = controlled_buffer_21_out ? 30'h279 : 30'bz;  // Controlled_Buffer controlled_buffer_23
  Pull_Resistor pull_resistor_25 (.node(controlled_buffer_21_out));
  Pull_Resistor pull_resistor_26 (.node(controlled_buffer_23_out));
  assign controlled_buffer_24_out = controlled_buffer_21_out ? 30'h231 : 30'bz;  // Controlled_Buffer controlled_buffer_24
  Pull_Resistor pull_resistor_27 (.node(controlled_buffer_24_out));
  assign controlled_buffer_25_out = controlled_buffer_21_out ? 30'h279 : 30'bz;  // Controlled_Buffer controlled_buffer_25
  Pull_Resistor pull_resistor_28 (.node(controlled_buffer_25_out));
  Pull_Resistor pull_resistor_29 (.node(pull_resistor_29_node));
  assign pull_resistor_29_node = controlled_buffer_21_out ? 30'h3ff : 30'bz;  // Controlled_Buffer controlled_buffer_26
  assign controlled_buffer_27_out = controlled_buffer_21_out ? 30'hfc : 30'bz;  // Controlled_Buffer controlled_buffer_27
  Pull_Resistor pull_resistor_30 (.node(controlled_buffer_27_out));
  Pull_Resistor pull_resistor_31 (.node(pull_resistor_31_node));
  assign pull_resistor_31_node = controlled_buffer_21_out ? 30'hfc : 30'bz;  // Controlled_Buffer controlled_buffer_28
  assign controlled_buffer_29_out = controlled_buffer_21_out ? 30'h3ff : 30'bz;  // Controlled_Buffer controlled_buffer_29
  Pull_Resistor pull_resistor_32 (.node(controlled_buffer_29_out));
  assign controlled_buffer_30_out = controlled_buffer_21_out ? 30'h279 : 30'bz;  // Controlled_Buffer controlled_buffer_30
  Pull_Resistor pull_resistor_33 (.node(controlled_buffer_30_out));
  Pull_Resistor pull_resistor_34 (.node(pull_resistor_34_node));
  assign pull_resistor_34_node = controlled_buffer_21_out ? 30'h231 : 30'bz;  // Controlled_Buffer controlled_buffer_31
  assign controlled_buffer_32_out = controlled_buffer_21_out ? 30'h201 : 30'bz;  // Controlled_Buffer controlled_buffer_32
  Pull_Resistor pull_resistor_35 (.node(controlled_buffer_32_out));
  Shifter #(.width(30)) shifter_21 (.in(controlled_buffer_23_out), .\dist (adder_3_out), .out(shifter_21_out));
  Shifter #(.width(30)) shifter_22 (.in(controlled_buffer_24_out), .\dist (adder_3_out), .out(shifter_22_out));
  Shifter #(.width(30)) shifter_23 (.in(controlled_buffer_25_out), .\dist (adder_3_out), .out(shifter_23_out));
  Shifter #(.width(30)) shifter_24 (.in(pull_resistor_29_node), .\dist (adder_3_out), .out(shifter_24_out));
  Shifter #(.width(30)) shifter_25 (.in(controlled_buffer_27_out), .\dist (adder_3_out), .out(shifter_25_out));
  Shifter #(.width(30)) shifter_26 (.in(pull_resistor_31_node), .\dist (adder_3_out), .out(shifter_26_out));
  Shifter #(.width(30)) shifter_27 (.in(controlled_buffer_29_out), .\dist (adder_3_out), .out(shifter_27_out));
  Shifter #(.width(30)) shifter_28 (.in(controlled_buffer_30_out), .\dist (adder_3_out), .out(shifter_28_out));
  Shifter #(.width(30)) shifter_29 (.in(pull_resistor_34_node), .\dist (adder_3_out), .out(shifter_29_out));
  Shifter #(.width(30)) shifter_30 (.in(controlled_buffer_32_out), .\dist (adder_3_out), .out(shifter_30_out));
  assign not_2_out = ~adder_3_out;  // NOT_Gate not_2, 5 bits wide
  Adder #(.width(5)) adder_7 (.a(not_2_out), .b(5'b00001), .out(adder_7_out));  // open: cin, cout
  Pull_Resistor pull_resistor_36 (.node(controlled_buffer_22_out));
  Adder #(.width(5)) adder_8 (.a(5'b11110), .b(adder_7_out), .out(adder_8_out));  // open: cin, cout
  Pull_Resistor pull_resistor_37 (.node(pull_resistor_37_node));
  assign pull_resistor_37_node = controlled_buffer_22_out ? 30'h279 : 30'bz;  // Controlled_Buffer controlled_buffer_33
  Shifter #(.width(30), .shift("lr")) shifter_31 (
    .in(pull_resistor_37_node), .\dist (adder_8_out), .out(shifter_31_out));
  assign controlled_buffer_34_out = controlled_buffer_22_out ? 30'h231 : 30'bz;  // Controlled_Buffer controlled_buffer_34
  Pull_Resistor pull_resistor_38 (.node(controlled_buffer_34_out));
  Shifter #(.width(30), .shift("lr")) shifter_32 (
    .in(controlled_buffer_34_out), .\dist (adder_8_out), .out(shifter_32_out));
  Pull_Resistor pull_resistor_39 (.node(pull_resistor_39_node));
  assign pull_resistor_39_node = controlled_buffer_22_out ? 30'h279 : 30'bz;  // Controlled_Buffer controlled_buffer_35
  Shifter #(.width(30), .shift("lr")) shifter_33 (
    .in(pull_resistor_39_node), .\dist (adder_8_out), .out(shifter_33_out));
  Pull_Resistor pull_resistor_40 (.node(pull_resistor_40_node));
  assign pull_resistor_40_node = controlled_buffer_22_out ? 30'h3ff : 30'bz;  // Controlled_Buffer controlled_buffer_36
  Shifter #(.width(30), .shift("lr")) shifter_34 (
    .in(pull_resistor_40_node), .\dist (adder_8_out), .out(shifter_34_out));
  assign controlled_buffer_37_out = controlled_buffer_22_out ? 30'hfc : 30'bz;  // Controlled_Buffer controlled_buffer_37
  Pull_Resistor pull_resistor_41 (.node(controlled_buffer_37_out));
  Shifter #(.width(30), .shift("lr")) shifter_35 (
    .in(controlled_buffer_37_out), .\dist (adder_8_out), .out(shifter_35_out));
  Pull_Resistor pull_resistor_42 (.node(pull_resistor_42_node));
  assign pull_resistor_42_node = controlled_buffer_22_out ? 30'hfc : 30'bz;  // Controlled_Buffer controlled_buffer_38
  Shifter #(.width(30), .shift("lr")) shifter_36 (
    .in(pull_resistor_42_node), .\dist (adder_8_out), .out(shifter_36_out));
  Pull_Resistor pull_resistor_43 (.node(pull_resistor_43_node));
  assign pull_resistor_43_node = controlled_buffer_22_out ? 30'h3ff : 30'bz;  // Controlled_Buffer controlled_buffer_39
  Shifter #(.width(30), .shift("lr")) shifter_37 (
    .in(pull_resistor_43_node), .\dist (adder_8_out), .out(shifter_37_out));
  Pull_Resistor pull_resistor_44 (.node(pull_resistor_44_node));
  assign pull_resistor_44_node = controlled_buffer_22_out ? 30'h279 : 30'bz;  // Controlled_Buffer controlled_buffer_40
  Shifter #(.width(30), .shift("lr")) shifter_38 (
    .in(pull_resistor_44_node), .\dist (adder_8_out), .out(shifter_38_out));
  Pull_Resistor pull_resistor_45 (.node(pull_resistor_45_node));
  assign pull_resistor_45_node = controlled_buffer_22_out ? 30'h231 : 30'bz;  // Controlled_Buffer controlled_buffer_41
  Shifter #(.width(30), .shift("lr")) shifter_39 (
    .in(pull_resistor_45_node), .\dist (adder_8_out), .out(shifter_39_out));
  Pull_Resistor pull_resistor_46 (.node(pull_resistor_46_node));
  assign pull_resistor_46_node = controlled_buffer_22_out ? 30'h201 : 30'bz;  // Controlled_Buffer controlled_buffer_42
  Shifter #(.width(30), .shift("lr")) shifter_40 (
    .in(pull_resistor_46_node), .\dist (adder_8_out), .out(shifter_40_out));
  assign toFront = shifter_21_out | shifter_31_out;  // OR_Gate or_11, 30 bits wide
  assign toFront_2 = shifter_22_out | shifter_32_out;  // OR_Gate or_12, 30 bits wide
  assign toFront_3 = shifter_23_out | shifter_33_out;  // OR_Gate or_13, 30 bits wide
  assign toFront_4 = shifter_24_out | shifter_34_out;  // OR_Gate or_14, 30 bits wide
  assign toFront_5 = shifter_25_out | shifter_35_out;  // OR_Gate or_15, 30 bits wide
  assign toFront_6 = shifter_26_out | shifter_36_out;  // OR_Gate or_16, 30 bits wide
  assign toFront_7 = shifter_27_out | shifter_37_out;  // OR_Gate or_17, 30 bits wide
  assign toFront_8 = shifter_28_out | shifter_38_out;  // OR_Gate or_18, 30 bits wide
  assign toBackground = or_1_out | shifter_41_out;  // OR_Gate or_19, 30 bits wide
  Shifter #(.width(30), .shift("lr")) shifter_41 (.in(toFront), .\dist (5'b00001), .out(shifter_41_out));
  Shifter #(.width(30), .shift("lr")) shifter_42 (.in(toFront_2), .\dist (5'b00001), .out(shifter_42_out));
  Shifter #(.width(30), .shift("lr")) shifter_43 (.in(toFront_3), .\dist (5'b00001), .out(shifter_43_out));
  Shifter #(.width(30), .shift("lr")) shifter_44 (.in(toFront_4), .\dist (5'b00001), .out(shifter_44_out));
  Shifter #(.width(30), .shift("lr")) shifter_45 (.in(toFront_5), .\dist (5'b00001), .out(shifter_45_out));
  Shifter #(.width(30), .shift("lr")) shifter_46 (.in(toFront_6), .\dist (5'b00001), .out(shifter_46_out));
  Shifter #(.width(30), .shift("lr")) shifter_47 (.in(toFront_7), .\dist (5'b00001), .out(shifter_47_out));
  assign toFront_9 = shifter_29_out | shifter_39_out;  // OR_Gate or_20, 30 bits wide
  assign toFront_10 = shifter_30_out | shifter_40_out;  // OR_Gate or_21, 30 bits wide
  assign toBackground_2 = or_2_out | shifter_42_out;  // OR_Gate or_22, 30 bits wide
  assign toBackground_3 = or_3_out | shifter_43_out;  // OR_Gate or_23, 30 bits wide
  assign toBackground_4 = or_4_out | shifter_44_out;  // OR_Gate or_24, 30 bits wide
  assign toBackground_5 = or_5_out | shifter_45_out;  // OR_Gate or_25, 30 bits wide
  assign toBackground_6 = or_6_out | shifter_46_out;  // OR_Gate or_26, 30 bits wide
  assign toBackground_7 = or_7_out | shifter_47_out;  // OR_Gate or_27, 30 bits wide
  assign toBackground_8 = or_8_out | shifter_48_out;  // OR_Gate or_28, 30 bits wide
  assign toBackground_9 = or_9_out | shifter_49_out;  // OR_Gate or_29, 30 bits wide
  Shifter #(.width(30), .shift("lr")) shifter_48 (.in(toFront_8), .\dist (5'b00001), .out(shifter_48_out));
  Shifter #(.width(30), .shift("lr")) shifter_49 (.in(toFront_9), .\dist (5'b00001), .out(shifter_49_out));
  Shifter #(.width(30), .shift("lr")) shifter_50 (.in(toFront_10), .\dist (5'b00001), .out(shifter_50_out));
  assign toBackground_10 = or_10_out | shifter_50_out;  // OR_Gate or_30, 30 bits wide

  assign outFlag = inFlag;
  assign outPlayerShiftM = inPlayerShiftM;
  assign outputBackShiftM = inputBackShiftM;

  // Notes on the sheet:
  //   MAKE SHIFT BY NEXT MATRICE
  //   MAKE SHIFT IN CURRENT MATRICE
  //   MAKE SHIFT IN CURRENT MATRICE
  //   MAKE SHIFT BY NEXT MATRICE
endmodule

module log_3x2 (
  input  [1:0] inBackShiftD,
  input  [4:0] inputBackShiftM,
  input  [1:0] inPlayerShiftD,
  input  [4:0] inPlayerShiftM,
  input  inFlag,
  output [29:0] toBackground,
  output [29:0] toBackground_2,
  output [29:0] toBackground_3,
  output [29:0] toBackground_4,
  output [29:0] toBackground_5,
  output [1:0] outBackShiftD,
  output [29:0] toBackground_6,
  output [4:0] outputBackShiftM,
  output [29:0] toBackground_7,
  output [29:0] toBackground_8,
  output [29:0] toBackground_9,
  output [29:0] toBackground_10,
  output [29:0] toFront,
  output [29:0] toFront_2,
  output [1:0] outPlayerShiftD,
  output [29:0] toFront_3,
  output [4:0] outPlayerShiftM,
  output outFlag,
  output [29:0] toFront_4,
  output [29:0] toFront_5,
  output [29:0] toFront_6,
  output [29:0] toFront_7,
  output [29:0] toFront_8,
  output [29:0] toFront_9,
  output [29:0] toFront_10
);

  wire comparator_1_eq, comparator_2_eq, comparator_3_eq, comparator_4_eq, comparator_5_eq, comparator_6_eq,
       comparator_7_eq, controlled_buffer_21_out, controlled_buffer_22_out, or_1_out, or_2_out;
  wire [1:0] adder_6_out, multiplexer_1_out;
  wire [4:0] adder_2_out, adder_3_out, adder_5_out, adder_7_out, adder_8_out, not_1_out, not_2_out;
  wire [29:0] controlled_buffer_1_out, controlled_buffer_5_out, controlled_buffer_9_out,
       controlled_buffer_10_out, controlled_buffer_12_out, controlled_buffer_13_out,
       controlled_buffer_15_out, controlled_buffer_16_out, controlled_buffer_17_out,
       controlled_buffer_18_out, controlled_buffer_20_out, controlled_buffer_23_out,
       controlled_buffer_26_out, controlled_buffer_28_out, controlled_buffer_29_out,
       controlled_buffer_31_out, controlled_buffer_32_out, controlled_buffer_34_out,
       controlled_buffer_35_out, controlled_buffer_37_out, controlled_buffer_38_out,
       controlled_buffer_39_out, controlled_buffer_40_out, controlled_buffer_42_out, or_3_out, or_4_out,
       or_5_out, or_6_out, or_7_out, or_8_out, or_9_out, or_10_out, or_11_out, or_12_out,
       pull_resistor_4_node, pull_resistor_5_node, pull_resistor_6_node, pull_resistor_8_node,
       pull_resistor_9_node, pull_resistor_10_node, pull_resistor_13_node, pull_resistor_16_node,
       pull_resistor_21_node, pull_resistor_27_node, pull_resistor_28_node, pull_resistor_30_node,
       pull_resistor_33_node, pull_resistor_36_node, pull_resistor_39_node, pull_resistor_44_node,
       shifter_1_out, shifter_2_out, shifter_3_out, shifter_4_out, shifter_5_out, shifter_6_out,
       shifter_7_out, shifter_8_out, shifter_9_out, shifter_10_out, shifter_11_out, shifter_12_out,
       shifter_13_out, shifter_14_out, shifter_15_out, shifter_16_out, shifter_17_out, shifter_18_out,
       shifter_19_out, shifter_20_out, shifter_21_out, shifter_22_out, shifter_23_out, shifter_24_out,
       shifter_25_out, shifter_26_out, shifter_27_out, shifter_28_out, shifter_29_out, shifter_30_out,
       shifter_31_out, shifter_32_out, shifter_33_out, shifter_34_out, shifter_35_out, shifter_36_out,
       shifter_37_out, shifter_38_out, shifter_39_out, shifter_40_out, shifter_41_out, shifter_42_out,
       shifter_43_out, shifter_44_out, shifter_45_out, shifter_46_out, shifter_47_out, shifter_48_out,
       shifter_49_out, shifter_50_out;

  Pull_Resistor pull_resistor_1 (.node(inputBackShiftM));
  Comparator #(.width(2)) comparator_1 (.a(inBackShiftD), .b(2'b10), .eq(comparator_1_eq));  // open: gt, lt
  Comparator #(.width(2)) comparator_2 (.a(2'b00), .b(inBackShiftD), .eq(comparator_2_eq));  // open: gt, lt
  // Probe on outBackShiftD
  Adder #(.width(2)) adder_1 (.a(inBackShiftD), .b(2'b01), .out(outBackShiftD));  // open: cin, cout
  or or_1 (or_1_out, comparator_1_eq, comparator_2_eq);
  Comparator #(.width(2)) comparator_3 (.a(outBackShiftD), .b(2'b10), .eq(comparator_3_eq));  // open: gt, lt
  or or_2 (or_2_out, comparator_3_eq, comparator_4_eq);
  Comparator #(.width(2)) comparator_4 (.a(2'b00), .b(outBackShiftD), .eq(comparator_4_eq));  // open: gt, lt
  Pull_Resistor pull_resistor_2 (.node(or_1_out));
  assign controlled_buffer_1_out = or_1_out ? {30{1'b0}} : 30'bz;  // Controlled_Buffer controlled_buffer_1
  Pull_Resistor pull_resistor_3 (.node(controlled_buffer_1_out));
  Pull_Resistor pull_resistor_4 (.node(pull_resistor_4_node));
  assign pull_resistor_4_node = or_1_out ? {30{1'b1}} : 30'bz;  // Controlled_Buffer controlled_buffer_2
  Pull_Resistor pull_resistor_5 (.node(pull_resistor_5_node));
  assign pull_resistor_5_node = or_1_out ? 30'h2fbfcfef : 30'bz;  // Controlled_Buffer controlled_buffer_3
  Pull_Resistor pull_resistor_6 (.node(pull_resistor_6_node));
  assign pull_resistor_6_node = or_1_out ? 30'h3fafafaf : 30'bz;  // Controlled_Buffer controlled_buffer_4
  assign controlled_buffer_5_out = or_1_out ? 30'h3eeeeeee : 30'bz;  // Controlled_Buffer controlled_buffer_5
  Pull_Resistor pull_resistor_7 (.node(controlled_buffer_5_out));
  Pull_Resistor pull_resistor_8 (.node(pull_resistor_8_node));
  assign pull_resistor_8_node = or_1_out ? 30'h2edfbafa : 30'bz;  // Controlled_Buffer controlled_buffer_6
  Pull_Resistor pull_resistor_9 (.node(pull_resistor_9_node));
  assign pull_resistor_9_node = or_1_out ? {30{1'b1}} : 30'bz;  // Controlled_Buffer controlled_buffer_7
  Pull_Resistor pull_resistor_10 (.node(pull_resistor_10_node));
  assign pull_resistor_10_node = or_1_out ? 30'h3f7ba9f : 30'bz;  // Controlled_Buffer controlled_buffer_8
  assign controlled_buffer_9_out = or_1_out ? {30{1'b1}} : 30'bz;  // Controlled_Buffer controlled_buffer_9
  Pull_Resistor pull_resistor_11 (.node(controlled_buffer_9_out));
  assign controlled_buffer_10_out = or_1_out ? {30{1'b0}} : 30'bz;  // Controlled_Buffer controlled_buffer_10
  Pull_Resistor pull_resistor_12 (.node(controlled_buffer_10_out));
  Shifter #(.width(30)) shifter_1 (.in(controlled_buffer_1_out), .\dist (inputBackShiftM), .out(shifter_1_out));
  Shifter #(.width(30)) shifter_2 (.in(pull_resistor_4_node), .\dist (inputBackShiftM), .out(shifter_2_out));
  Shifter #(.width(30)) shifter_3 (.in(pull_resistor_5_node), .\dist (inputBackShiftM), .out(shifter_3_out));
  Shifter #(.width(30)) shifter_4 (.in(pull_resistor_6_node), .\dist (inputBackShiftM), .out(shifter_4_out));
  Shifter #(.width(30)) shifter_5 (.in(controlled_buffer_5_out), .\dist (inputBackShiftM), .out(shifter_5_out));
  Shifter #(.width(30)) shifter_6 (.in(pull_resistor_8_node), .\dist (inputBackShiftM), .out(shifter_6_out));
  Shifter #(.width(30)) shifter_7 (.in(pull_resistor_9_node), .\dist (inputBackShiftM), .out(shifter_7_out));
  Shifter #(.width(30)) shifter_8 (.in(pull_resistor_10_node), .\dist (inputBackShiftM), .out(shifter_8_out));
  Shifter #(.width(30)) shifter_9 (.in(controlled_buffer_9_out), .\dist (inputBackShiftM), .out(shifter_9_out));
  Shifter #(.width(30)) shifter_10 (.in(controlled_buffer_10_out), .\dist (inputBackShiftM), .out(shifter_10_out));
  assign not_1_out = ~inputBackShiftM;  // NOT_Gate not_1, 5 bits wide
  Adder #(.width(5)) adder_2 (.a(not_1_out), .b(5'b00001), .out(adder_2_out));  // open: cin, cout
  Adder #(.width(5)) adder_3 (.a(5'b11110), .b(adder_2_out), .out(adder_3_out));  // open: cin, cout
  Pull_Resistor pull_resistor_13 (.node(pull_resistor_13_node));
  assign pull_resistor_13_node = or_2_out ? {30{1'b0}} : 30'bz;  // Controlled_Buffer controlled_buffer_11
  assign controlled_buffer_12_out = or_2_out ? {30{1'b1}} : 30'bz;  // Controlled_Buffer controlled_buffer_12
  Pull_Resistor pull_resistor_14 (.node(controlled_buffer_12_out));
  assign controlled_buffer_13_out = or_2_out ? 30'h2fbfcfef : 30'bz;  // Controlled_Buffer controlled_buffer_13
  Pull_Resistor pull_resistor_15 (.node(controlled_buffer_13_out));
  Pull_Resistor pull_resistor_16 (.node(pull_resistor_16_node));
  assign pull_resistor_16_node = or_2_out ? 30'h3fafafaf : 30'bz;  // Controlled_Buffer controlled_buffer_14
  assign controlled_buffer_15_out = or_2_out ? 30'h3eeeeeee : 30'bz;  // Controlled_Buffer controlled_buffer_15
  Pull_Resistor pull_resistor_17 (.node(controlled_buffer_15_out));
  assign controlled_buffer_16_out = or_2_out ? 30'h2edfbafa : 30'bz;  // Controlled_Buffer controlled_buffer_16
  Pull_Resistor pull_resistor_18 (.node(controlled_buffer_16_out));
  assign controlled_buffer_17_out = or_2_out ? {30{1'b1}} : 30'bz;  // Controlled_Buffer controlled_buffer_17
  Pull_Resistor pull_resistor_19 (.node(controlled_buffer_17_out));
  assign controlled_buffer_18_out = or_2_out ? 30'h3f7ba9f : 30'bz;  // Controlled_Buffer controlled_buffer_18
  Pull_Resistor pull_resistor_20 (.node(controlled_buffer_18_out));
  Pull_Resistor pull_resistor_21 (.node(pull_resistor_21_node));
  assign pull_resistor_21_node = or_2_out ? {30{1'b1}} : 30'bz;  // Controlled_Buffer controlled_buffer_19
  assign controlled_buffer_20_out = or_2_out ? {30{1'b0}} : 30'bz;  // Controlled_Buffer controlled_buffer_20
  Pull_Resistor pull_resistor_22 (.node(controlled_buffer_20_out));
  Pull_Resistor pull_resistor_23 (.node(or_2_out));
  assign or_3_out = shifter_1_out | shifter_11_out;  // OR_Gate or_3, 30 bits wide
  assign or_4_out = shifter_2_out | shifter_12_out;  // OR_Gate or_4, 30 bits wide
  assign or_5_out = shifter_3_out | shifter_13_out;  // OR_Gate or_5, 30 bits wide
  assign or_6_out = shifter_4_out | shifter_14_out;  // OR_Gate or_6, 30 bits wide
  assign or_7_out = shifter_5_out | shifter_15_out;  // OR_Gate or_7, 30 bits wide
  Shifter #(.width(30), .shift("lr")) shifter_11 (
    .in(pull_resistor_13_node), .\dist (adder_3_out), .out(shifter_11_out));
  Shifter #(.width(30), .shift("lr")) shifter_12 (
    .in(controlled_buffer_12_out), .\dist (adder_3_out), .out(shifter_12_out));
  Shifter #(.width(30), .shift("lr")) shifter_13 (
    .in(controlled_buffer_13_out), .\dist (adder_3_out), .out(shifter_13_out));
  Shifter #(.width(30), .shift("lr")) shifter_14 (
    .in(pull_resistor_16_node), .\dist (adder_3_out), .out(shifter_14_out));
  Shifter #(.width(30), .shift("lr")) shifter_15 (
    .in(controlled_buffer_15_out), .\dist (adder_3_out), .out(shifter_15_out));
  Shifter #(.width(30), .shift("lr")) shifter_16 (
    .in(controlled_buffer_16_out), .\dist (adder_3_out), .out(shifter_16_out));
  Shifter #(.width(30), .shift("lr")) shifter_17 (
    .in(controlled_buffer_17_out), .\dist (adder_3_out), .out(shifter_17_out));
  Shifter #(.width(30), .shift("lr")) shifter_18 (
    .in(controlled_buffer_18_out), .\dist (adder_3_out), .out(shifter_18_out));
  Shifter #(.width(30), .shift("lr")) shifter_19 (
    .in(pull_resistor_21_node), .\dist (adder_3_out), .out(shifter_19_out));
  Shifter #(.width(30), .shift("lr")) shifter_20 (
    .in(controlled_buffer_20_out), .\dist (adder_3_out), .out(shifter_20_out));
  assign or_8_out = shifter_6_out | shifter_16_out;  // OR_Gate or_8, 30 bits wide
  assign or_9_out = shifter_7_out | shifter_17_out;  // OR_Gate or_9, 30 bits wide
  assign or_10_out = shifter_8_out | shifter_18_out;  // OR_Gate or_10, 30 bits wide
  assign or_11_out = shifter_9_out | shifter_19_out;  // OR_Gate or_11, 30 bits wide
  assign or_12_out = shifter_10_out | shifter_20_out;  // OR_Gate or_12, 30 bits wide
  Adder #(.width(2)) adder_4 (.a(inPlayerShiftD), .b(2'b01), .out(outPlayerShiftD));  // open: cin, cout
  Pull_Resistor pull_resistor_24 (.node(inPlayerShiftM));
  // Probe on adder_5_out
  Adder #(.width(5)) adder_5 (.a(inPlayerShiftM), .b(5'b00001), .out(adder_5_out));  // open: cin, cout
  Multiplexer #(.width(2), .disabled(0), .enable("false")) multiplexer_1 (
    .in0(inPlayerShiftD), .in1(outPlayerShiftD), .out(multiplexer_1_out), .sel(comparator_5_eq));
  Comparator #(.width(5), .mode("unsigned")) comparator_5 (
    .a(inPlayerShiftM), .b(5'b11110), .eq(comparator_5_eq));  // open: gt, lt
  // Probe on multiplexer_1_out
  assign controlled_buffer_21_out = inFlag ? comparator_6_eq : 1'bz;  // Controlled_Buffer controlled_buffer_21
  Comparator #(.width(2)) comparator_6 (.a(2'b00), .b(multiplexer_1_out), .eq(comparator_6_eq));  // open: gt, lt
  Adder #(.width(2)) adder_6 (.a(multiplexer_1_out), .b(2'b01), .out(adder_6_out));  // open: cin, cout
  assign controlled_buffer_22_out = inFlag ? comparator_7_eq : 1'bz;  // Controlled_Buffer controlled_buffer_22
  Comparator #(.width(2)) comparator_7 (.a(2'b00), .b(adder_6_out), .eq(comparator_7_eq));  // open: gt, lt
  Pull_Resistor pull_resistor_25 (.node(controlled_buffer_21_out));
  assign controlled_buffer_23_out = controlled_buffer_21_out ? 30'h279 : 30'bz;  // Controlled_Buffer controlled_buffer_23
  Pull_Resistor pull_resistor_26 (.node(controlled_buffer_23_out));
  Shifter #(.width(30)) shifter_21 (.in(controlled_buffer_23_out), .\dist (adder_5_out), .out(shifter_21_out));
  Pull_Resistor pull_resistor_27 (.node(pull_resistor_27_node));
  assign pull_resistor_27_node = controlled_buffer_21_out ? 30'h231 : 30'bz;  // Controlled_Buffer controlled_buffer_24
  Shifter #(.width(30)) shifter_22 (.in(pull_resistor_27_node), .\dist (adder_5_out), .out(shifter_22_out));
  Pull_Resistor pull_resistor_28 (.node(pull_resistor_28_node));
  assign pull_resistor_28_node = controlled_buffer_21_out ? 30'h279 : 30'bz;  // Controlled_Buffer controlled_buffer_25
  Shifter #(.width(30)) shifter_23 (.in(pull_resistor_28_node), .\dist (adder_5_out), .out(shifter_23_out));
  assign controlled_buffer_26_out = controlled_buffer_21_out ? 30'h3ff : 30'bz;  // Controlled_Buffer controlled_buffer_26
  Pull_Resistor pull_resistor_29 (.node(controlled_buffer_26_out));
  Shifter #(.width(30)) shifter_24 (.in(controlled_buffer_26_out), .\dist (adder_5_out), .out(shifter_24_out));
  Pull_Resistor pull_resistor_30 (.node(pull_resistor_30_node));
  assign pull_resistor_30_node = controlled_buffer_21_out ? 30'hfc : 30'bz;  // Controlled_Buffer controlled_buffer_27
  Shifter #(.width(30)) shifter_25 (.in(pull_resistor_30_node), .\dist (adder_5_out), .out(shifter_25_out));
  assign controlled_buffer_28_out = controlled_buffer_21_out ? 30'hfc : 30'bz;  // Controlled_Buffer controlled_buffer_28
  Pull_Resistor pull_resistor_31 (.node(controlled_buffer_28_out));
  Shifter #(.width(30)) shifter_26 (.in(controlled_buffer_28_out), .\dist (adder_5_out), .out(shifter_26_out));
  assign controlled_buffer_29_out = controlled_buffer_21_out ? 30'h3ff : 30'bz;  // Controlled_Buffer controlled_buffer_29
  Pull_Resistor pull_resistor_32 (.node(controlled_buffer_29_out));
  Shifter #(.width(30)) shifter_27 (.in(controlled_buffer_29_out), .\dist (adder_5_out), .out(shifter_27_out));
  Pull_Resistor pull_resistor_33 (.node(pull_resistor_33_node));
  assign pull_resistor_33_node = controlled_buffer_21_out ? 30'h279 : 30'bz;  // Controlled_Buffer controlled_buffer_30
  Shifter #(.width(30)) shifter_28 (.in(pull_resistor_33_node), .\dist (adder_5_out), .out(shifter_28_out));
  assign controlled_buffer_31_out = controlled_buffer_21_out ? 30'h231 : 30'bz;  // Controlled_Buffer controlled_buffer_31
  Pull_Resistor pull_resistor_34 (.node(controlled_buffer_31_out));
  Shifter #(.width(30)) shifter_29 (.in(controlled_buffer_31_out), .\dist (adder_5_out), .out(shifter_29_out));
  assign controlled_buffer_32_out = controlled_buffer_21_out ? 30'h201 : 30'bz;  // Controlled_Buffer controlled_buffer_32
  Pull_Resistor pull_resistor_35 (.node(controlled_buffer_32_out));
  Shifter #(.width(30)) shifter_30 (.in(controlled_buffer_32_out), .\dist (adder_5_out), .out(shifter_30_out));
  assign not_2_out = ~adder_5_out;  // NOT_Gate not_2, 5 bits wide
  Adder #(.width(5)) adder_7 (.a(5'b11110), .b(adder_8_out), .out(adder_7_out));  // open: cin, cout
  Adder #(.width(5)) adder_8 (.a(not_2_out), .b(5'b00001), .out(adder_8_out));  // open: cin, cout
  Pull_Resistor pull_resistor_36 (.node(pull_resistor_36_node));
  assign pull_resistor_36_node = controlled_buffer_22_out ? 30'h279 : 30'bz;  // Controlled_Buffer controlled_buffer_33
  assign controlled_buffer_34_out = controlled_buffer_22_out ? 30'h231 : 30'bz;  // Controlled_Buffer controlled_buffer_34
  Pull_Resistor pull_resistor_37 (.node(controlled_buffer_34_out));
  assign controlled_buffer_35_out = controlled_buffer_22_out ? 30'h279 : 30'bz;  // Controlled_Buffer controlled_buffer_35
  Pull_Resistor pull_resistor_38 (.node(controlled_buffer_35_out));
  Pull_Resistor pull_resistor_39 (.node(pull_resistor_39_node));
  assign pull_resistor_39_node = controlled_buffer_22_out ? 30'h3ff : 30'bz;  // Controlled_Buffer controlled_buffer_36
  assign controlled_buffer_37_out = controlled_buffer_22_out ? 30'hfc : 30'bz;  // Controlled_Buffer controlled_buffer_37
  Pull_Resistor pull_resistor_40 (.node(controlled_buffer_37_out));
  assign controlled_buffer_38_out = controlled_buffer_22_out ? 30'hfc : 30'bz;  // Controlled_Buffer controlled_buffer_38
  Pull_Resistor pull_resistor_41 (.node(controlled_buffer_38_out));
  assign controlled_buffer_39_out = controlled_buffer_22_out ? 30'h3ff : 30'bz;  // Controlled_Buffer controlled_buffer_39
  Pull_Resistor pull_resistor_42 (.node(controlled_buffer_39_out));
  assign controlled_buffer_40_out = controlled_buffer_22_out ? 30'h279 : 30'bz;  // Controlled_Buffer controlled_buffer_40
  Pull_Resistor pull_resistor_43 (.node(controlled_buffer_40_out));
  Pull_Resistor pull_resistor_44 (.node(pull_resistor_44_node));
  assign pull_resistor_44_node = controlled_buffer_22_out ? 30'h231 : 30'bz;  // Controlled_Buffer controlled_buffer_41
  assign controlled_buffer_42_out = controlled_buffer_22_out ? 30'h201 : 30'bz;  // Controlled_Buffer controlled_buffer_42
  Pull_Resistor pull_resistor_45 (.node(controlled_buffer_42_out));
  Pull_Resistor pull_resistor_46 (.node(controlled_buffer_22_out));
  assign toFront = shifter_21_out | shifter_31_out;  // OR_Gate or_13, 30 bits wide
  assign toFront_2 = shifter_22_out | shifter_32_out;  // OR_Gate or_14, 30 bits wide
  assign toFront_3 = shifter_23_out | shifter_33_out;  // OR_Gate or_15, 30 bits wide
  assign toFront_4 = shifter_24_out | shifter_34_out;  // OR_Gate or_16, 30 bits wide
  Shifter #(.width(30), .shift("lr")) shifter_31 (
    .in(pull_resistor_36_node), .\dist (adder_7_out), .out(shifter_31_out));
  Shifter #(.width(30), .shift("lr")) shifter_32 (
    .in(controlled_buffer_34_out), .\dist (adder_7_out), .out(shifter_32_out));
  Shifter #(.width(30), .shift("lr")) shifter_33 (
    .in(controlled_buffer_35_out), .\dist (adder_7_out), .out(shifter_33_out));
  Shifter #(.width(30), .shift("lr")) shifter_34 (
    .in(pull_resistor_39_node), .\dist (adder_7_out), .out(shifter_34_out));
  Shifter #(.width(30), .shift("lr")) shifter_35 (
    .in(controlled_buffer_37_out), .\dist (adder_7_out), .out(shifter_35_out));
  Shifter #(.width(30), .shift("lr")) shifter_36 (
    .in(controlled_buffer_38_out), .\dist (adder_7_out), .out(shifter_36_out));
  Shifter #(.width(30), .shift("lr")) shifter_37 (
    .in(controlled_buffer_39_out), .\dist (adder_7_out), .out(shifter_37_out));
  Shifter #(.width(30), .shift("lr")) shifter_38 (
    .in(controlled_buffer_40_out), .\dist (adder_7_out), .out(shifter_38_out));
  Shifter #(.width(30), .shift("lr")) shifter_39 (
    .in(pull_resistor_44_node), .\dist (adder_7_out), .out(shifter_39_out));
  Shifter #(.width(30), .shift("lr")) shifter_40 (
    .in(controlled_buffer_42_out), .\dist (adder_7_out), .out(shifter_40_out));
  Shifter #(.width(30), .shift("lr")) shifter_41 (.in(toFront), .\dist (5'b00001), .out(shifter_41_out));
  Shifter #(.width(30), .shift("lr")) shifter_42 (.in(toFront_2), .\dist (5'b00001), .out(shifter_42_out));
  Shifter #(.width(30), .shift("lr")) shifter_43 (.in(toFront_3), .\dist (5'b00001), .out(shifter_43_out));
  assign toFront_5 = shifter_25_out | shifter_35_out;  // OR_Gate or_17, 30 bits wide
  assign toFront_6 = shifter_26_out | shifter_36_out;  // OR_Gate or_18, 30 bits wide
  assign toFront_7 = shifter_27_out | shifter_37_out;  // OR_Gate or_19, 30 bits wide
  assign toFront_8 = shifter_28_out | shifter_38_out;  // OR_Gate or_20, 30 bits wide
  assign toFront_9 = shifter_29_out | shifter_39_out;  // OR_Gate or_21, 30 bits wide
  assign toFront_10 = shifter_30_out | shifter_40_out;  // OR_Gate or_22, 30 bits wide
  assign toBackground = or_3_out | shifter_41_out;  // OR_Gate or_23, 30 bits wide
  assign toBackground_2 = or_4_out | shifter_42_out;  // OR_Gate or_24, 30 bits wide
  assign toBackground_3 = or_5_out | shifter_43_out;  // OR_Gate or_25, 30 bits wide
  assign toBackground_4 = or_6_out | shifter_44_out;  // OR_Gate or_26, 30 bits wide
  assign toBackground_5 = or_7_out | shifter_45_out;  // OR_Gate or_27, 30 bits wide
  Shifter #(.width(30), .shift("lr")) shifter_44 (.in(toFront_4), .\dist (5'b00001), .out(shifter_44_out));
  Shifter #(.width(30), .shift("lr")) shifter_45 (.in(toFront_5), .\dist (5'b00001), .out(shifter_45_out));
  Shifter #(.width(30), .shift("lr")) shifter_46 (.in(toFront_6), .\dist (5'b00001), .out(shifter_46_out));
  Shifter #(.width(30), .shift("lr")) shifter_47 (.in(toFront_7), .\dist (5'b00001), .out(shifter_47_out));
  Shifter #(.width(30), .shift("lr")) shifter_48 (.in(toFront_8), .\dist (5'b00001), .out(shifter_48_out));
  Shifter #(.width(30), .shift("lr")) shifter_49 (.in(toFront_9), .\dist (5'b00001), .out(shifter_49_out));
  Shifter #(.width(30), .shift("lr")) shifter_50 (.in(toFront_10), .\dist (5'b00001), .out(shifter_50_out));
  assign toBackground_6 = or_8_out | shifter_46_out;  // OR_Gate or_28, 30 bits wide
  assign toBackground_7 = or_9_out | shifter_47_out;  // OR_Gate or_29, 30 bits wide
  assign toBackground_8 = or_10_out | shifter_48_out;  // OR_Gate or_30, 30 bits wide
  assign toBackground_9 = or_11_out | shifter_49_out;  // OR_Gate or_31, 30 bits wide
  assign toBackground_10 = or_12_out | shifter_50_out;  // OR_Gate or_32, 30 bits wide

  assign outFlag = inFlag;
  assign outPlayerShiftM = inPlayerShiftM;
  assign outputBackShiftM = inputBackShiftM;

  // Notes on the sheet:
  //   MAKE SHIFT BY NEXT MATRICE
  //   MAKE SHIFT IN CURRENT MATRICE
  //   MAKE SHIFT IN CURRENT MATRICE
  //   MAKE SHIFT BY NEXT MATRICE
endmodule

module log_1x1 (
  input  [1:0] inBackShiftD,
  input  [4:0] inputBackShiftM,
  input  [1:0] inPlayerShiftD,
  input  [4:0] inPlayerShiftM,
  input  inFlag,
  output [29:0] toBackground,
  output [29:0] toBackground_2,
  output [29:0] toBackground_3,
  output [29:0] toBackground_4,
  output [1:0] outBackShiftD,
  output [29:0] toBackground_5,
  output [29:0] toBackground_6,
  output [4:0] outputBackShiftM,
  output [29:0] toBackground_7,
  output [29:0] toBackground_8,
  output [29:0] toBackground_9,
  output [29:0] toBackground_10,
  output [29:0] toFront,
  output [29:0] toFront_2,
  output [29:0] toFront_3,
  output [29:0] toFront_4,
  output [1:0] outPlayerShiftD,
  output [4:0] outPlayerShiftM,
  output [29:0] toFront_5,
  output outFlag,
  output [29:0] toFront_6,
  output [29:0] toFront_7,
  output [29:0] toFront_8,
  output [29:0] toFront_9,
  output [29:0] toFront_10
);

  wire comparator_1_eq, comparator_2_eq, comparator_3_eq, comparator_4_eq, comparator_5_eq, comparator_6_eq,
       comparator_7_eq, comparator_8_eq, comparator_9_eq, comparator_10_eq, comparator_11_eq,
       controlled_buffer_1_out, controlled_buffer_2_out, or_1_out, or_2_out, or_3_out, or_4_out, or_5_out,
       or_6_out;
  wire [1:0] adder_4_out, multiplexer_1_out;
  wire [4:0] adder_3_out, adder_5_out, adder_6_out, adder_7_out, adder_8_out, not_1_out, not_2_out;
  wire [29:0] controlled_buffer_4_out, controlled_buffer_6_out, controlled_buffer_10_out,
       controlled_buffer_11_out, controlled_buffer_13_out, controlled_buffer_14_out,
       controlled_buffer_16_out, controlled_buffer_18_out, controlled_buffer_19_out,
       controlled_buffer_20_out, controlled_buffer_21_out, controlled_buffer_24_out,
       controlled_buffer_27_out, controlled_buffer_28_out, controlled_buffer_30_out,
       controlled_buffer_32_out, controlled_buffer_36_out, controlled_buffer_37_out,
       controlled_buffer_38_out, or_7_out, or_8_out, or_9_out, or_10_out, or_11_out, or_12_out, or_13_out,
       or_14_out, or_15_out, or_16_out, pull_resistor_4_node, pull_resistor_6_node, pull_resistor_8_node,
       pull_resistor_9_node, pull_resistor_10_node, pull_resistor_13_node, pull_resistor_16_node,
       pull_resistor_18_node, pull_resistor_23_node, pull_resistor_25_node, pull_resistor_28_node,
       pull_resistor_29_node, pull_resistor_32_node, pull_resistor_34_node, pull_resistor_36_node,
       pull_resistor_37_node, pull_resistor_38_node, pull_resistor_42_node, pull_resistor_43_node,
       pull_resistor_44_node, pull_resistor_45_node, shifter_1_out, shifter_2_out, shifter_3_out,
       shifter_4_out, shifter_5_out, shifter_6_out, shifter_7_out, shifter_8_out, shifter_9_out,
       shifter_10_out, shifter_11_out, shifter_12_out, shifter_13_out, shifter_14_out, shifter_15_out,
       shifter_16_out, shifter_17_out, shifter_18_out, shifter_19_out, shifter_20_out, shifter_21_out,
       shifter_22_out, shifter_23_out, shifter_24_out, shifter_25_out, shifter_26_out, shifter_27_out,
       shifter_28_out, shifter_29_out, shifter_30_out, shifter_31_out, shifter_32_out, shifter_33_out,
       shifter_34_out, shifter_35_out, shifter_36_out, shifter_37_out, shifter_38_out, shifter_39_out,
       shifter_40_out, shifter_41_out, shifter_42_out, shifter_43_out, shifter_44_out, shifter_45_out,
       shifter_46_out, shifter_47_out, shifter_48_out, shifter_49_out, shifter_50_out;

  Adder #(.width(2)) adder_1 (.a(inBackShiftD), .b(2'b01), .out(outBackShiftD));  // open: cin, cout
  Pull_Resistor pull_resistor_1 (.node(inputBackShiftM));
  Adder #(.width(2)) adder_2 (.a(inPlayerShiftD), .b(2'b01), .out(outPlayerShiftD));  // open: cin, cout
  Pull_Resistor pull_resistor_2 (.node(inPlayerShiftM));
  Comparator #(.width(2)) comparator_1 (.a(inBackShiftD), .b(2'b11), .eq(comparator_1_eq));  // open: gt, lt
  Comparator #(.width(2)) comparator_2 (.a(2'b01), .b(inBackShiftD), .eq(comparator_2_eq));  // open: gt, lt
  Comparator #(.width(2)) comparator_3 (.a(inBackShiftD), .b(2'b10), .eq(comparator_3_eq));  // open: gt, lt
  Comparator #(.width(2)) comparator_4 (.a(2'b00), .b(inBackShiftD), .eq(comparator_4_eq));  // open: gt, lt
  // Probe on outBackShiftD
  // Probe on adder_3_out
  Adder #(.width(5)) adder_3 (.a(inPlayerShiftM), .b(5'b00001), .out(adder_3_out));  // open: cin, cout
  Multiplexer #(.width(2), .disabled(0), .enable("false")) multiplexer_1 (
    .in0(inPlayerShiftD), .in1(outPlayerShiftD), .out(multiplexer_1_out), .sel(comparator_5_eq));
  Comparator #(.width(5), .mode("unsigned")) comparator_5 (
    .a(inPlayerShiftM), .b(5'b11110), .eq(comparator_5_eq));  // open: gt, lt
  or or_1 (or_1_out, comparator_1_eq, comparator_2_eq);
  or or_2 (or_2_out, or_1_out, or_3_out);
  or or_3 (or_3_out, comparator_3_eq, comparator_4_eq);
  Comparator #(.width(2)) comparator_6 (.a(outBackShiftD), .b(2'b11), .eq(comparator_6_eq));  // open: gt, lt
  or or_4 (or_4_out, comparator_6_eq, comparator_7_eq);
  Comparator #(.width(2)) comparator_7 (.a(2'b01), .b(outBackShiftD), .eq(comparator_7_eq));  // open: gt, lt
  Comparator #(.width(2)) comparator_8 (.a(outBackShiftD), .b(2'b10), .eq(comparator_8_eq));  // open: gt, lt
  or or_5 (or_5_out, comparator_8_eq, comparator_9_eq);
  Comparator #(.width(2)) comparator_9 (.a(2'b00), .b(outBackShiftD), .eq(comparator_9_eq));  // open: gt, lt
  // Probe on multiplexer_1_out
  assign controlled_buffer_1_out = inFlag ? comparator_10_eq : 1'bz;  // Controlled_Buffer controlled_buffer_1
  Comparator #(.width(2)) comparator_10 (.a(2'b00), .b(multiplexer_1_out), .eq(comparator_10_eq));  // open: gt, lt
  Adder #(.width(2)) adder_4 (.a(multiplexer_1_out), .b(2'b01), .out(adder_4_out));  // open: cin, cout
  or or_6 (or_6_out, or_4_out, or_5_out);
  assign controlled_buffer_2_out = inFlag ? comparator_11_eq : 1'bz;  // Controlled_Buffer controlled_buffer_2
  Comparator #(.width(2)) comparator_11 (.a(2'b00), .b(adder_4_out), .eq(comparator_11_eq));  // open: gt, lt
  Pull_Resistor pull_resistor_3 (.node(or_2_out));
  Pull_Resistor pull_resistor_4 (.node(pull_resistor_4_node));
  assign pull_resistor_4_node = or_2_out ? {30{1'b0}} : 30'bz;  // Controlled_Buffer controlled_buffer_3
  assign controlled_buffer_4_out = or_2_out ? {30{1'b0}} : 30'bz;  // Controlled_Buffer controlled_buffer_4
  Pull_Resistor pull_resistor_5 (.node(controlled_buffer_4_out));
  Pull_Resistor pull_resistor_6 (.node(pull_resistor_6_node));
  assign pull_resistor_6_node = or_2_out ? 30'h3ff : 30'bz;  // Controlled_Buffer controlled_buffer_5
  assign controlled_buffer_6_out = or_2_out ? 30'h3f9 : 30'bz;  // Controlled_Buffer controlled_buffer_6
  Pull_Resistor pull_resistor_7 (.node(controlled_buffer_6_out));
  Pull_Resistor pull_resistor_8 (.node(pull_resistor_8_node));
  assign pull_resistor_8_node = or_2_out ? 30'h3ff : 30'bz;  // Controlled_Buffer controlled_buffer_7
  Pull_Resistor pull_resistor_9 (.node(pull_resistor_9_node));
  assign pull_resistor_9_node = or_2_out ? 30'h3aa : 30'bz;  // Controlled_Buffer controlled_buffer_8
  Pull_Resistor pull_resistor_10 (.node(pull_resistor_10_node));
  assign pull_resistor_10_node = or_2_out ? 30'h3fe : 30'bz;  // Controlled_Buffer controlled_buffer_9
  assign controlled_buffer_10_out = or_2_out ? 30'h3ff : 30'bz;  // Controlled_Buffer controlled_buffer_10
  Pull_Resistor pull_resistor_11 (.node(controlled_buffer_10_out));
  assign controlled_buffer_11_out = or_2_out ? {30{1'b0}} : 30'bz;  // Controlled_Buffer controlled_buffer_11
  Pull_Resistor pull_resistor_12 (.node(controlled_buffer_11_out));
  Pull_Resistor pull_resistor_13 (.node(pull_resistor_13_node));
  assign pull_resistor_13_node = or_2_out ? {30{1'b0}} : 30'bz;  // Controlled_Buffer controlled_buffer_12
  Shifter #(.width(30)) shifter_1 (.in(pull_resistor_4_node), .\dist (inputBackShiftM), .out(shifter_1_out));
  Shifter #(.width(30)) shifter_2 (.in(controlled_buffer_4_out), .\dist (inputBackShiftM), .out(shifter_2_out));
  Shifter #(.width(30)) shifter_3 (.in(pull_resistor_6_node), .\dist (inputBackShiftM), .out(shifter_3_out));
  Shifter #(.width(30)) shifter_4 (.in(controlled_buffer_6_out), .\dist (inputBackShiftM), .out(shifter_4_out));
  Shifter #(.width(30)) shifter_5 (.in(pull_resistor_8_node), .\dist (inputBackShiftM), .out(shifter_5_out));
  Shifter #(.width(30)) shifter_6 (.in(pull_resistor_9_node), .\dist (inputBackShiftM), .out(shifter_6_out));
  Shifter #(.width(30)) shifter_7 (.in(pull_resistor_10_node), .\dist (inputBackShiftM), .out(shifter_7_out));
  Shifter #(.width(30)) shifter_8 (.in(controlled_buffer_10_out), .\dist (inputBackShiftM), .out(shifter_8_out));
  Shifter #(.width(30)) shifter_9 (.in(controlled_buffer_11_out), .\dist (inputBackShiftM), .out(shifter_9_out));
  Shifter #(.width(30)) shifter_10 (.in(pull_resistor_13_node), .\dist (inputBackShiftM), .out(shifter_10_out));
  assign not_1_out = ~inputBackShiftM;  // NOT_Gate not_1, 5 bits wide
  Adder #(.width(5)) adder_5 (.a(not_1_out), .b(5'b00001), .out(adder_5_out));  // open: cin, cout
  Adder #(.width(5)) adder_6 (.a(5'b11110), .b(adder_5_out), .out(adder_6_out));  // open: cin, cout
  assign controlled_buffer_13_out = or_6_out ? {30{1'b0}} : 30'bz;  // Controlled_Buffer controlled_buffer_13
  Pull_Resistor pull_resistor_14 (.node(controlled_buffer_13_out));
  Shifter #(.width(30), .shift("lr")) shifter_11 (
    .in(controlled_buffer_13_out), .\dist (adder_6_out), .out(shifter_11_out));
  assign controlled_buffer_14_out = or_6_out ? {30{1'b0}} : 30'bz;  // Controlled_Buffer controlled_buffer_14
  Pull_Resistor pull_resistor_15 (.node(controlled_buffer_14_out));
  Shifter #(.width(30), .shift("lr")) shifter_12 (
    .in(controlled_buffer_14_out), .\dist (adder_6_out), .out(shifter_12_out));
  Pull_Resistor pull_resistor_16 (.node(pull_resistor_16_node));
  assign pull_resistor_16_node = or_6_out ? 30'h3ff : 30'bz;  // Controlled_Buffer controlled_buffer_15
  Shifter #(.width(30), .shift("lr")) shifter_13 (
    .in(pull_resistor_16_node), .\dist (adder_6_out), .out(shifter_13_out));
  assign controlled_buffer_16_out = or_6_out ? 30'h3f9 : 30'bz;  // Controlled_Buffer controlled_buffer_16
  Pull_Resistor pull_resistor_17 (.node(controlled_buffer_16_out));
  Shifter #(.width(30), .shift("lr")) shifter_14 (
    .in(controlled_buffer_16_out), .\dist (adder_6_out), .out(shifter_14_out));
  Pull_Resistor pull_resistor_18 (.node(pull_resistor_18_node));
  assign pull_resistor_18_node = or_6_out ? 30'h3ff : 30'bz;  // Controlled_Buffer controlled_buffer_17
  Shifter #(.width(30), .shift("lr")) shifter_15 (
    .in(pull_resistor_18_node), .\dist (adder_6_out), .out(shifter_15_out));
  assign controlled_buffer_18_out = or_6_out ? 30'h3aa : 30'bz;  // Controlled_Buffer controlled_buffer_18
  Pull_Resistor pull_resistor_19 (.node(controlled_buffer_18_out));
  Shifter #(.width(30), .shift("lr")) shifter_16 (
    .in(controlled_buffer_18_out), .\dist (adder_6_out), .out(shifter_16_out));
  assign controlled_buffer_19_out = or_6_out ? 30'h3fe : 30'bz;  // Controlled_Buffer controlled_buffer_19
  Pull_Resistor pull_resistor_20 (.node(controlled_buffer_19_out));
  Shifter #(.width(30), .shift("lr")) shifter_17 (
    .in(controlled_buffer_19_out), .\dist (adder_6_out), .out(shifter_17_out));
  assign controlled_buffer_20_out = or_6_out ? 30'h3ff : 30'bz;  // Controlled_Buffer controlled_buffer_20
  Pull_Resistor pull_resistor_21 (.node(controlled_buffer_20_out));
  Shifter #(.width(30), .shift("lr")) shifter_18 (
    .in(controlled_buffer_20_out), .\dist (adder_6_out), .out(shifter_18_out));
  assign controlled_buffer_21_out = or_6_out ? {30{1'b0}} : 30'bz;  // Controlled_Buffer controlled_buffer_21
  Pull_Resistor pull_resistor_22 (.node(controlled_buffer_21_out));
  Shifter #(.width(30), .shift("lr")) shifter_19 (
    .in(controlled_buffer_21_out), .\dist (adder_6_out), .out(shifter_19_out));
  Pull_Resistor pull_resistor_23 (.node(pull_resistor_23_node));
  assign pull_resistor_23_node = or_6_out ? {30{1'b0}} : 30'bz;  // Controlled_Buffer controlled_buffer_22
  Shifter #(.width(30), .shift("lr")) shifter_20 (
    .in(pull_resistor_23_node), .\dist (adder_6_out), .out(shifter_20_out));
  Pull_Resistor pull_resistor_24 (.node(or_6_out));
  assign or_7_out = shifter_1_out | shifter_11_out;  // OR_Gate or_7, 30 bits wide
  assign or_8_out = shifter_2_out | shifter_12_out;  // OR_Gate or_8, 30 bits wide
  assign or_9_out = shifter_3_out | shifter_13_out;  // OR_Gate or_9, 30 bits wide
  assign or_10_out = shifter_4_out | shifter_14_out;  // OR_Gate or_10, 30 bits wide
  assign or_11_out = shifter_5_out | shifter_15_out;  // OR_Gate or_11, 30 bits wide
  assign or_12_out = shifter_6_out | shifter_16_out;  // OR_Gate or_12, 30 bits wide
  assign or_13_out = shifter_7_out | shifter_17_out;  // OR_Gate or_13, 30 bits wide
  assign or_14_out = shifter_8_out | shifter_18_out;  // OR_Gate or_14, 30 bits wide
  assign or_15_out = shifter_9_out | shifter_19_out;  // OR_Gate or_15, 30 bits wide
  assign or_16_out = shifter_10_out | shifter_20_out;  // OR_Gate or_16, 30 bits wide
  Pull_Resistor pull_resistor_25 (.node(pull_resistor_25_node));
  Pull_Resistor pull_resistor_26 (.node(controlled_buffer_1_out));
  assign pull_resistor_25_node = controlled_buffer_1_out ? 30'h279 : 30'bz;  // Controlled_Buffer controlled_buffer_23
  assign controlled_buffer_24_out = controlled_buffer_1_out ? 30'h231 : 30'bz;  // Controlled_Buffer controlled_buffer_24
  Pull_Resistor pull_resistor_27 (.node(controlled_buffer_24_out));
  Pull_Resistor pull_resistor_28 (.node(pull_resistor_28_node));
  assign pull_resistor_28_node = controlled_buffer_1_out ? 30'h279 : 30'bz;  // Controlled_Buffer controlled_buffer_25
  Pull_Resistor pull_resistor_29 (.node(pull_resistor_29_node));
  assign pull_resistor_29_node = controlled_buffer_1_out ? 30'h3ff : 30'bz;  // Controlled_Buffer controlled_buffer_26
  assign controlled_buffer_27_out = controlled_buffer_1_out ? 30'hfc : 30'bz;  // Controlled_Buffer controlled_buffer_27
  Pull_Resistor pull_resistor_30 (.node(controlled_buffer_27_out));
  assign controlled_buffer_28_out = controlled_buffer_1_out ? 30'hfc : 30'bz;  // Controlled_Buffer controlled_buffer_28
  Pull_Resistor pull_resistor_31 (.node(controlled_buffer_28_out));
  Pull_Resistor pull_resistor_32 (.node(pull_resistor_32_node));
  assign pull_resistor_32_node = controlled_buffer_1_out ? 30'h3ff : 30'bz;  // Controlled_Buffer controlled_buffer_29
  assign controlled_buffer_30_out = controlled_buffer_1_out ? 30'h279 : 30'bz;  // Controlled_Buffer controlled_buffer_30
  Pull_Resistor pull_resistor_33 (.node(controlled_buffer_30_out));
  Pull_Resistor pull_resistor_34 (.node(pull_resistor_34_node));
  assign pull_resistor_34_node = controlled_buffer_1_out ? 30'h231 : 30'bz;  // Controlled_Buffer controlled_buffer_31
  assign controlled_buffer_32_out = controlled_buffer_1_out ? 30'h201 : 30'bz;  // Controlled_Buffer controlled_buffer_32
  Pull_Resistor pull_resistor_35 (.node(controlled_buffer_32_out));
  assign not_2_out = ~adder_3_out;  // NOT_Gate not_2, 5 bits wide
  Shifter #(.width(30)) shifter_21 (.in(pull_resistor_25_node), .\dist (adder_3_out), .out(shifter_21_out));
  Shifter #(.width(30)) shifter_22 (.in(controlled_buffer_24_out), .\dist (adder_3_out), .out(shifter_22_out));
  Shifter #(.width(30)) shifter_23 (.in(pull_resistor_28_node), .\dist (adder_3_out), .out(shifter_23_out));
  Shifter #(.width(30)) shifter_24 (.in(pull_resistor_29_node), .\dist (adder_3_out), .out(shifter_24_out));
  Shifter #(.width(30)) shifter_25 (.in(controlled_buffer_27_out), .\dist (adder_3_out), .out(shifter_25_out));
  Shifter #(.width(30)) shifter_26 (.in(controlled_buffer_28_out), .\dist (adder_3_out), .out(shifter_26_out));
  Shifter #(.width(30)) shifter_27 (.in(pull_resistor_32_node), .\dist (adder_3_out), .out(shifter_27_out));
  Shifter #(.width(30)) shifter_28 (.in(controlled_buffer_30_out), .\dist (adder_3_out), .out(shifter_28_out));
  Shifter #(.width(30)) shifter_29 (.in(pull_resistor_34_node), .\dist (adder_3_out), .out(shifter_29_out));
  Shifter #(.width(30)) shifter_30 (.in(controlled_buffer_32_out), .\dist (adder_3_out), .out(shifter_30_out));
  Adder #(.width(5)) adder_7 (.a(not_2_out), .b(5'b00001), .out(adder_7_out));  // open: cin, cout
  Pull_Resistor pull_resistor_36 (.node(pull_resistor_36_node));
  assign pull_resistor_36_node = controlled_buffer_2_out ? 30'h279 : 30'bz;  // Controlled_Buffer controlled_buffer_33
  Pull_Resistor pull_resistor_37 (.node(pull_resistor_37_node));
  assign pull_resistor_37_node = controlled_buffer_2_out ? 30'h231 : 30'bz;  // Controlled_Buffer controlled_buffer_34
  Pull_Resistor pull_resistor_38 (.node(pull_resistor_38_node));
  assign pull_resistor_38_node = controlled_buffer_2_out ? 30'h279 : 30'bz;  // Controlled_Buffer controlled_buffer_35
  assign controlled_buffer_36_out = controlled_buffer_2_out ? 30'h3ff : 30'bz;  // Controlled_Buffer controlled_buffer_36
  Pull_Resistor pull_resistor_39 (.node(controlled_buffer_36_out));
  assign controlled_buffer_37_out = controlled_buffer_2_out ? 30'hfc : 30'bz;  // Controlled_Buffer controlled_buffer_37
  Pull_Resistor pull_resistor_40 (.node(controlled_buffer_37_out));
  assign controlled_buffer_38_out = controlled_buffer_2_out ? 30'hfc : 30'bz;  // Controlled_Buffer controlled_buffer_38
  Pull_Resistor pull_resistor_41 (.node(controlled_buffer_38_out));
  Pull_Resistor pull_resistor_42 (.node(pull_resistor_42_node));
  assign pull_resistor_42_node = controlled_buffer_2_out ? 30'h3ff : 30'bz;  // Controlled_Buffer controlled_buffer_39
  Pull_Resistor pull_resistor_43 (.node(pull_resistor_43_node));
  assign pull_resistor_43_node = controlled_buffer_2_out ? 30'h279 : 30'bz;  // Controlled_Buffer controlled_buffer_40
  Pull_Resistor pull_resistor_44 (.node(pull_resistor_44_node));
  assign pull_resistor_44_node = controlled_buffer_2_out ? 30'h231 : 30'bz;  // Controlled_Buffer controlled_buffer_41
  Pull_Resistor pull_resistor_45 (.node(pull_resistor_45_node));
  assign pull_resistor_45_node = controlled_buffer_2_out ? 30'h201 : 30'bz;  // Controlled_Buffer controlled_buffer_42
  Pull_Resistor pull_resistor_46 (.node(controlled_buffer_2_out));
  assign toFront = shifter_21_out | shifter_31_out;  // OR_Gate or_17, 30 bits wide
  Adder #(.width(5)) adder_8 (.a(5'b11110), .b(adder_7_out), .out(adder_8_out));  // open: cin, cout
  Shifter #(.width(30), .shift("lr")) shifter_31 (
    .in(pull_resistor_36_node), .\dist (adder_8_out), .out(shifter_31_out));
  Shifter #(.width(30), .shift("lr")) shifter_32 (
    .in(pull_resistor_37_node), .\dist (adder_8_out), .out(shifter_32_out));
  Shifter #(.width(30), .shift("lr")) shifter_33 (
    .in(pull_resistor_38_node), .\dist (adder_8_out), .out(shifter_33_out));
  Shifter #(.width(30), .shift("lr")) shifter_34 (
    .in(controlled_buffer_36_out), .\dist (adder_8_out), .out(shifter_34_out));
  Shifter #(.width(30), .shift("lr")) shifter_35 (
    .in(controlled_buffer_37_out), .\dist (adder_8_out), .out(shifter_35_out));
  Shifter #(.width(30), .shift("lr")) shifter_36 (
    .in(controlled_buffer_38_out), .\dist (adder_8_out), .out(shifter_36_out));
  Shifter #(.width(30), .shift("lr")) shifter_37 (
    .in(pull_resistor_42_node), .\dist (adder_8_out), .out(shifter_37_out));
  Shifter #(.width(30), .shift("lr")) shifter_38 (
    .in(pull_resistor_43_node), .\dist (adder_8_out), .out(shifter_38_out));
  Shifter #(.width(30), .shift("lr")) shifter_39 (
    .in(pull_resistor_44_node), .\dist (adder_8_out), .out(shifter_39_out));
  Shifter #(.width(30), .shift("lr")) shifter_40 (
    .in(pull_resistor_45_node), .\dist (adder_8_out), .out(shifter_40_out));
  assign toFront_2 = shifter_22_out | shifter_32_out;  // OR_Gate or_18, 30 bits wide
  assign toFront_3 = shifter_23_out | shifter_33_out;  // OR_Gate or_19, 30 bits wide
  assign toFront_4 = shifter_24_out | shifter_34_out;  // OR_Gate or_20, 30 bits wide
  assign toFront_5 = shifter_25_out | shifter_35_out;  // OR_Gate or_21, 30 bits wide
  assign toFront_6 = shifter_26_out | shifter_36_out;  // OR_Gate or_22, 30 bits wide
  assign toFront_7 = shifter_27_out | shifter_37_out;  // OR_Gate or_23, 30 bits wide
  assign toFront_8 = shifter_28_out | shifter_38_out;  // OR_Gate or_24, 30 bits wide
  assign toFront_9 = shifter_29_out | shifter_39_out;  // OR_Gate or_25, 30 bits wide
  Shifter #(.width(30), .shift("lr")) shifter_41 (.in(toFront), .\dist (5'b00001), .out(shifter_41_out));
  Shifter #(.width(30), .shift("lr")) shifter_42 (.in(toFront_2), .\dist (5'b00001), .out(shifter_42_out));
  Shifter #(.width(30), .shift("lr")) shifter_43 (.in(toFront_3), .\dist (5'b00001), .out(shifter_43_out));
  Shifter #(.width(30), .shift("lr")) shifter_44 (.in(toFront_4), .\dist (5'b00001), .out(shifter_44_out));
  Shifter #(.width(30), .shift("lr")) shifter_45 (.in(toFront_5), .\dist (5'b00001), .out(shifter_45_out));
  Shifter #(.width(30), .shift("lr")) shifter_46 (.in(toFront_6), .\dist (5'b00001), .out(shifter_46_out));
  Shifter #(.width(30), .shift("lr")) shifter_47 (.in(toFront_7), .\dist (5'b00001), .out(shifter_47_out));
  assign toFront_10 = shifter_30_out | shifter_40_out;  // OR_Gate or_26, 30 bits wide
  assign toBackground = or_7_out | shifter_41_out;  // OR_Gate or_27, 30 bits wide
  assign toBackground_2 = or_8_out | shifter_42_out;  // OR_Gate or_28, 30 bits wide
  assign toBackground_3 = or_9_out | shifter_43_out;  // OR_Gate or_29, 30 bits wide
  assign toBackground_4 = or_10_out | shifter_44_out;  // OR_Gate or_30, 30 bits wide
  Shifter #(.width(30), .shift("lr")) shifter_48 (.in(toFront_8), .\dist (5'b00001), .out(shifter_48_out));
  Shifter #(.width(30), .shift("lr")) shifter_49 (.in(toFront_9), .\dist (5'b00001), .out(shifter_49_out));
  Shifter #(.width(30), .shift("lr")) shifter_50 (.in(toFront_10), .\dist (5'b00001), .out(shifter_50_out));
  assign toBackground_5 = or_11_out | shifter_45_out;  // OR_Gate or_31, 30 bits wide
  assign toBackground_6 = or_12_out | shifter_46_out;  // OR_Gate or_32, 30 bits wide
  assign toBackground_7 = or_13_out | shifter_47_out;  // OR_Gate or_33, 30 bits wide
  assign toBackground_8 = or_14_out | shifter_48_out;  // OR_Gate or_34, 30 bits wide
  assign toBackground_9 = or_15_out | shifter_49_out;  // OR_Gate or_35, 30 bits wide
  assign toBackground_10 = or_16_out | shifter_50_out;  // OR_Gate or_36, 30 bits wide

  assign outFlag = inFlag;
  assign outPlayerShiftM = inPlayerShiftM;
  assign outputBackShiftM = inputBackShiftM;

  // Notes on the sheet:
  //   MAKE SHIFT BY NEXT MATRICE
  //   MAKE SHIFT IN CURRENT MATRICE
  //   MAKE SHIFT BY NEXT MATRICE
  //   MAKE SHIFT IN CURRENT MATRICE
endmodule

module log_2x1 (
  input  [1:0] inBackShiftD,
  input  [4:0] inputBackShiftM,
  input  [1:0] inPlayerShiftD,
  input  [4:0] inPlayerShiftM,
  input  inFlag,
  output [29:0] toBackground,
  output [29:0] toBackground_2,
  output [29:0] toBackground_3,
  output [29:0] toBackground_4,
  output [29:0] toBackground_5,
  output [1:0] outBackShiftD,
  output [29:0] toBackground_6,
  output [29:0] toBackground_7,
  output [4:0] outputBackShiftM,
  output [29:0] toBackground_8,
  output [29:0] toBackground_9,
  output [29:0] toBackground_10,
  output [29:0] toFront,
  output [29:0] toFront_2,
  output [1:0] outPlayerShiftD,
  output [29:0] toFront_3,
  output [4:0] outPlayerShiftM,
  output [29:0] toFront_4,
  output outFlag,
  output [29:0] toFront_5,
  output [29:0] toFront_6,
  output [29:0] toFront_7,
  output [29:0] toFront_8,
  output [29:0] toFront_9,
  output [29:0] toFront_10
);

  wire comparator_1_eq, comparator_2_eq, comparator_3_eq, comparator_4_eq, comparator_5_eq, comparator_6_eq,
       comparator_7_eq, controlled_buffer_21_out, controlled_buffer_22_out, or_1_out, or_2_out;
  wire [1:0] adder_6_out, multiplexer_1_out;
  wire [4:0] adder_2_out, adder_3_out, adder_5_out, adder_7_out, adder_8_out, not_1_out, not_2_out;
  wire [29:0] controlled_buffer_2_out, controlled_buffer_3_out, controlled_buffer_4_out,
       controlled_buffer_15_out, controlled_buffer_17_out, controlled_buffer_20_out,
       controlled_buffer_24_out, controlled_buffer_25_out, controlled_buffer_27_out,
       controlled_buffer_28_out, controlled_buffer_29_out, controlled_buffer_32_out,
       controlled_buffer_33_out, controlled_buffer_37_out, controlled_buffer_38_out,
       controlled_buffer_39_out, or_3_out, or_4_out, or_5_out, or_6_out, or_7_out, or_8_out, or_9_out,
       or_10_out, or_11_out, or_12_out, pull_resistor_3_node, pull_resistor_7_node, pull_resistor_8_node,
       pull_resistor_9_node, pull_resistor_10_node, pull_resistor_11_node, pull_resistor_12_node,
       pull_resistor_13_node, pull_resistor_14_node, pull_resistor_15_node, pull_resistor_16_node,
       pull_resistor_18_node, pull_resistor_20_node, pull_resistor_21_node, pull_resistor_25_node,
       pull_resistor_29_node, pull_resistor_33_node, pull_resistor_34_node, pull_resistor_37_node,
       pull_resistor_38_node, pull_resistor_39_node, pull_resistor_43_node, pull_resistor_44_node,
       pull_resistor_45_node, shifter_1_out, shifter_2_out, shifter_3_out, shifter_4_out, shifter_5_out,
       shifter_6_out, shifter_7_out, shifter_8_out, shifter_9_out, shifter_10_out, shifter_11_out,
       shifter_12_out, shifter_13_out, shifter_14_out, shifter_15_out, shifter_16_out, shifter_17_out,
       shifter_18_out, shifter_19_out, shifter_20_out, shifter_21_out, shifter_22_out, shifter_23_out,
       shifter_24_out, shifter_25_out, shifter_26_out, shifter_27_out, shifter_28_out, shifter_29_out,
       shifter_30_out, shifter_31_out, shifter_32_out, shifter_33_out, shifter_34_out, shifter_35_out,
       shifter_36_out, shifter_37_out, shifter_38_out, shifter_39_out, shifter_40_out, shifter_41_out,
       shifter_42_out, shifter_43_out, shifter_44_out, shifter_45_out, shifter_46_out, shifter_47_out,
       shifter_48_out, shifter_49_out, shifter_50_out;

  Adder #(.width(2)) adder_1 (.a(inBackShiftD), .b(2'b01), .out(outBackShiftD));  // open: cin, cout
  Pull_Resistor pull_resistor_1 (.node(inputBackShiftM));
  Comparator #(.width(2)) comparator_1 (.a(inBackShiftD), .b(2'b10), .eq(comparator_1_eq));  // open: gt, lt
  Comparator #(.width(2)) comparator_2 (.a(2'b00), .b(inBackShiftD), .eq(comparator_2_eq));  // open: gt, lt
  // Probe on outBackShiftD
  or or_1 (or_1_out, comparator_1_eq, comparator_2_eq);
  Comparator #(.width(2)) comparator_3 (.a(outBackShiftD), .b(2'b10), .eq(comparator_3_eq));  // open: gt, lt
  or or_2 (or_2_out, comparator_3_eq, comparator_4_eq);
  Comparator #(.width(2)) comparator_4 (.a(2'b00), .b(outBackShiftD), .eq(comparator_4_eq));  // open: gt, lt
  Pull_Resistor pull_resistor_2 (.node(or_1_out));
  Pull_Resistor pull_resistor_3 (.node(pull_resistor_3_node));
  assign pull_resistor_3_node = or_1_out ? {30{1'b0}} : 30'bz;  // Controlled_Buffer controlled_buffer_1
  assign controlled_buffer_2_out = or_1_out ? 30'hfceaf : 30'bz;  // Controlled_Buffer controlled_buffer_2
  Pull_Resistor pull_resistor_4 (.node(controlled_buffer_2_out));
  assign controlled_buffer_3_out = or_1_out ? 30'h1ff0fa : 30'bz;  // Controlled_Buffer controlled_buffer_3
  Pull_Resistor pull_resistor_5 (.node(controlled_buffer_3_out));
  assign controlled_buffer_4_out = or_1_out ? 30'h1fffff : 30'bz;  // Controlled_Buffer controlled_buffer_4
  Pull_Resistor pull_resistor_6 (.node(controlled_buffer_4_out));
  Pull_Resistor pull_resistor_7 (.node(pull_resistor_7_node));
  assign pull_resistor_7_node = or_1_out ? 30'h1eeeee : 30'bz;  // Controlled_Buffer controlled_buffer_5
  Pull_Resistor pull_resistor_8 (.node(pull_resistor_8_node));
  assign pull_resistor_8_node = or_1_out ? 30'hfbafa : 30'bz;  // Controlled_Buffer controlled_buffer_6
  Pull_Resistor pull_resistor_9 (.node(pull_resistor_9_node));
  assign pull_resistor_9_node = or_1_out ? 30'hfffff : 30'bz;  // Controlled_Buffer controlled_buffer_7
  Pull_Resistor pull_resistor_10 (.node(pull_resistor_10_node));
  assign pull_resistor_10_node = or_1_out ? 30'h1bbbbb : 30'bz;  // Controlled_Buffer controlled_buffer_8
  Pull_Resistor pull_resistor_11 (.node(pull_resistor_11_node));
  assign pull_resistor_11_node = or_1_out ? 30'heeeee : 30'bz;  // Controlled_Buffer controlled_buffer_9
  Pull_Resistor pull_resistor_12 (.node(pull_resistor_12_node));
  assign pull_resistor_12_node = or_1_out ? {30{1'b0}} : 30'bz;  // Controlled_Buffer controlled_buffer_10
  Shifter #(.width(30)) shifter_1 (.in(pull_resistor_3_node), .\dist (inputBackShiftM), .out(shifter_1_out));
  Shifter #(.width(30)) shifter_2 (.in(controlled_buffer_2_out), .\dist (inputBackShiftM), .out(shifter_2_out));
  Shifter #(.width(30)) shifter_3 (.in(controlled_buffer_3_out), .\dist (inputBackShiftM), .out(shifter_3_out));
  Shifter #(.width(30)) shifter_4 (.in(controlled_buffer_4_out), .\dist (inputBackShiftM), .out(shifter_4_out));
  Shifter #(.width(30)) shifter_5 (.in(pull_resistor_7_node), .\dist (inputBackShiftM), .out(shifter_5_out));
  Shifter #(.width(30)) shifter_6 (.in(pull_resistor_8_node), .\dist (inputBackShiftM), .out(shifter_6_out));
  Shifter #(.width(30)) shifter_7 (.in(pull_resistor_9_node), .\dist (inputBackShiftM), .out(shifter_7_out));
  Shifter #(.width(30)) shifter_8 (.in(pull_resistor_10_node), .\dist (inputBackShiftM), .out(shifter_8_out));
  Shifter #(.width(30)) shifter_9 (.in(pull_resistor_11_node), .\dist (inputBackShiftM), .out(shifter_9_out));
  Shifter #(.width(30)) shifter_10 (.in(pull_resistor_12_node), .\dist (inputBackShiftM), .out(shifter_10_out));
  assign not_1_out = ~inputBackShiftM;  // NOT_Gate not_1, 5 bits wide
  Adder #(.width(5)) adder_2 (.a(not_1_out), .b(5'b00001), .out(adder_2_out));  // open: cin, cout
  Adder #(.width(5)) adder_3 (.a(5'b11110), .b(adder_2_out), .out(adder_3_out));  // open: cin, cout
  Pull_Resistor pull_resistor_13 (.node(pull_resistor_13_node));
  assign pull_resistor_13_node = or_2_out ? {30{1'b0}} : 30'bz;  // Controlled_Buffer controlled_buffer_11
  Shifter #(.width(30), .shift("lr")) shifter_11 (
    .in(pull_resistor_13_node), .\dist (adder_3_out), .out(shifter_11_out));
  Pull_Resistor pull_resistor_14 (.node(pull_resistor_14_node));
  assign pull_resistor_14_node = or_2_out ? 30'hfceaf : 30'bz;  // Controlled_Buffer controlled_buffer_12
  Shifter #(.width(30), .shift("lr")) shifter_12 (
    .in(pull_resistor_14_node), .\dist (adder_3_out), .out(shifter_12_out));
  Pull_Resistor pull_resistor_15 (.node(pull_resistor_15_node));
  assign pull_resistor_15_node = or_2_out ? 30'h1ff0fa : 30'bz;  // Controlled_Buffer controlled_buffer_13
  Shifter #(.width(30), .shift("lr")) shifter_13 (
    .in(pull_resistor_15_node), .\dist (adder_3_out), .out(shifter_13_out));
  Pull_Resistor pull_resistor_16 (.node(pull_resistor_16_node));
  assign pull_resistor_16_node = or_2_out ? 30'h1fffff : 30'bz;  // Controlled_Buffer controlled_buffer_14
  Shifter #(.width(30), .shift("lr")) shifter_14 (
    .in(pull_resistor_16_node), .\dist (adder_3_out), .out(shifter_14_out));
  assign controlled_buffer_15_out = or_2_out ? 30'h1eeeee : 30'bz;  // Controlled_Buffer controlled_buffer_15
  Pull_Resistor pull_resistor_17 (.node(controlled_buffer_15_out));
  Shifter #(.width(30), .shift("lr")) shifter_15 (
    .in(controlled_buffer_15_out), .\dist (adder_3_out), .out(shifter_15_out));
  Pull_Resistor pull_resistor_18 (.node(pull_resistor_18_node));
  assign pull_resistor_18_node = or_2_out ? 30'hfbafa : 30'bz;  // Controlled_Buffer controlled_buffer_16
  Shifter #(.width(30), .shift("lr")) shifter_16 (
    .in(pull_resistor_18_node), .\dist (adder_3_out), .out(shifter_16_out));
  assign controlled_buffer_17_out = or_2_out ? 30'hfffff : 30'bz;  // Controlled_Buffer controlled_buffer_17
  Pull_Resistor pull_resistor_19 (.node(controlled_buffer_17_out));
  Shifter #(.width(30), .shift("lr")) shifter_17 (
    .in(controlled_buffer_17_out), .\dist (adder_3_out), .out(shifter_17_out));
  Pull_Resistor pull_resistor_20 (.node(pull_resistor_20_node));
  assign pull_resistor_20_node = or_2_out ? 30'h1bbbbb : 30'bz;  // Controlled_Buffer controlled_buffer_18
  Shifter #(.width(30), .shift("lr")) shifter_18 (
    .in(pull_resistor_20_node), .\dist (adder_3_out), .out(shifter_18_out));
  Pull_Resistor pull_resistor_21 (.node(pull_resistor_21_node));
  assign pull_resistor_21_node = or_2_out ? 30'heeeee : 30'bz;  // Controlled_Buffer controlled_buffer_19
  Shifter #(.width(30), .shift("lr")) shifter_19 (
    .in(pull_resistor_21_node), .\dist (adder_3_out), .out(shifter_19_out));
  assign controlled_buffer_20_out = or_2_out ? {30{1'b0}} : 30'bz;  // Controlled_Buffer controlled_buffer_20
  Pull_Resistor pull_resistor_22 (.node(controlled_buffer_20_out));
  Shifter #(.width(30), .shift("lr")) shifter_20 (
    .in(controlled_buffer_20_out), .\dist (adder_3_out), .out(shifter_20_out));
  Pull_Resistor pull_resistor_23 (.node(or_2_out));
  Adder #(.width(2)) adder_4 (.a(inPlayerShiftD), .b(2'b01), .out(outPlayerShiftD));  // open: cin, cout
  Pull_Resistor pull_resistor_24 (.node(inPlayerShiftM));
  assign or_3_out = shifter_1_out | shifter_11_out;  // OR_Gate or_3, 30 bits wide
  assign or_4_out = shifter_2_out | shifter_12_out;  // OR_Gate or_4, 30 bits wide
  assign or_5_out = shifter_3_out | shifter_13_out;  // OR_Gate or_5, 30 bits wide
  assign or_6_out = shifter_4_out | shifter_14_out;  // OR_Gate or_6, 30 bits wide
  assign or_7_out = shifter_5_out | shifter_15_out;  // OR_Gate or_7, 30 bits wide
  assign or_8_out = shifter_6_out | shifter_16_out;  // OR_Gate or_8, 30 bits wide
  // Probe on adder_5_out
  Adder #(.width(5)) adder_5 (.a(inPlayerShiftM), .b(5'b00001), .out(adder_5_out));  // open: cin, cout
  Comparator #(.width(5), .mode("unsigned")) comparator_5 (
    .a(inPlayerShiftM), .b(5'b11110), .eq(comparator_5_eq));  // open: gt, lt
  assign or_9_out = shifter_7_out | shifter_17_out;  // OR_Gate or_9, 30 bits wide
  assign or_10_out = shifter_8_out | shifter_18_out;  // OR_Gate or_10, 30 bits wide
  assign or_11_out = shifter_9_out | shifter_19_out;  // OR_Gate or_11, 30 bits wide
  assign or_12_out = shifter_10_out | shifter_20_out;  // OR_Gate or_12, 30 bits wide
  // Probe on multiplexer_1_out
  Multiplexer #(.width(2), .disabled(0), .enable("false")) multiplexer_1 (
    .in0(inPlayerShiftD), .in1(outPlayerShiftD), .out(multiplexer_1_out), .sel(comparator_5_eq));
  Comparator #(.width(2)) comparator_6 (.a(2'b00), .b(multiplexer_1_out), .eq(comparator_6_eq));  // open: gt, lt
  assign controlled_buffer_21_out = inFlag ? comparator_6_eq : 1'bz;  // Controlled_Buffer controlled_buffer_21
  Comparator #(.width(2)) comparator_7 (.a(2'b00), .b(adder_6_out), .eq(comparator_7_eq));  // open: gt, lt
  assign controlled_buffer_22_out = inFlag ? comparator_7_eq : 1'bz;  // Controlled_Buffer controlled_buffer_22
  Adder #(.width(2)) adder_6 (.a(multiplexer_1_out), .b(2'b01), .out(adder_6_out));  // open: cin, cout
  Pull_Resistor pull_resistor_25 (.node(pull_resistor_25_node));
  Pull_Resistor pull_resistor_26 (.node(controlled_buffer_21_out));
  assign pull_resistor_25_node = controlled_buffer_21_out ? 30'h279 : 30'bz;  // Controlled_Buffer controlled_buffer_23
  assign controlled_buffer_24_out = controlled_buffer_21_out ? 30'h231 : 30'bz;  // Controlled_Buffer controlled_buffer_24
  Pull_Resistor pull_resistor_27 (.node(controlled_buffer_24_out));
  assign controlled_buffer_25_out = controlled_buffer_21_out ? 30'h279 : 30'bz;  // Controlled_Buffer controlled_buffer_25
  Pull_Resistor pull_resistor_28 (.node(controlled_buffer_25_out));
  Pull_Resistor pull_resistor_29 (.node(pull_resistor_29_node));
  assign pull_resistor_29_node = controlled_buffer_21_out ? 30'h3ff : 30'bz;  // Controlled_Buffer controlled_buffer_26
  assign controlled_buffer_27_out = controlled_buffer_21_out ? 30'hfc : 30'bz;  // Controlled_Buffer controlled_buffer_27
  Pull_Resistor pull_resistor_30 (.node(controlled_buffer_27_out));
  assign controlled_buffer_28_out = controlled_buffer_21_out ? 30'hfc : 30'bz;  // Controlled_Buffer controlled_buffer_28
  Pull_Resistor pull_resistor_31 (.node(controlled_buffer_28_out));
  assign controlled_buffer_29_out = controlled_buffer_21_out ? 30'h3ff : 30'bz;  // Controlled_Buffer controlled_buffer_29
  Pull_Resistor pull_resistor_32 (.node(controlled_buffer_29_out));
  Pull_Resistor pull_resistor_33 (.node(pull_resistor_33_node));
  assign pull_resistor_33_node = controlled_buffer_21_out ? 30'h279 : 30'bz;  // Controlled_Buffer controlled_buffer_30
  Pull_Resistor pull_resistor_34 (.node(pull_resistor_34_node));
  assign pull_resistor_34_node = controlled_buffer_21_out ? 30'h231 : 30'bz;  // Controlled_Buffer controlled_buffer_31
  assign controlled_buffer_32_out = controlled_buffer_21_out ? 30'h201 : 30'bz;  // Controlled_Buffer controlled_buffer_32
  Pull_Resistor pull_resistor_35 (.node(controlled_buffer_32_out));
  assign not_2_out = ~adder_5_out;  // NOT_Gate not_2, 5 bits wide
  Shifter #(.width(30)) shifter_21 (.in(pull_resistor_25_node), .\dist (adder_5_out), .out(shifter_21_out));
  Shifter #(.width(30)) shifter_22 (.in(controlled_buffer_24_out), .\dist (adder_5_out), .out(shifter_22_out));
  Shifter #(.width(30)) shifter_23 (.in(controlled_buffer_25_out), .\dist (adder_5_out), .out(shifter_23_out));
  Shifter #(.width(30)) shifter_24 (.in(pull_resistor_29_node), .\dist (adder_5_out), .out(shifter_24_out));
  Shifter #(.width(30)) shifter_25 (.in(controlled_buffer_27_out), .\dist (adder_5_out), .out(shifter_25_out));
  Shifter #(.width(30)) shifter_26 (.in(controlled_buffer_28_out), .\dist (adder_5_out), .out(shifter_26_out));
  Shifter #(.width(30)) shifter_27 (.in(controlled_buffer_29_out), .\dist (adder_5_out), .out(shifter_27_out));
  Shifter #(.width(30)) shifter_28 (.in(pull_resistor_33_node), .\dist (adder_5_out), .out(shifter_28_out));
  Shifter #(.width(30)) shifter_29 (.in(pull_resistor_34_node), .\dist (adder_5_out), .out(shifter_29_out));
  Shifter #(.width(30)) shifter_30 (.in(controlled_buffer_32_out), .\dist (adder_5_out), .out(shifter_30_out));
  Adder #(.width(5)) adder_7 (.a(not_2_out), .b(5'b00001), .out(adder_7_out));  // open: cin, cout
  assign controlled_buffer_33_out = controlled_buffer_22_out ? 30'h279 : 30'bz;  // Controlled_Buffer controlled_buffer_33
  Pull_Resistor pull_resistor_36 (.node(controlled_buffer_33_out));
  Pull_Resistor pull_resistor_37 (.node(pull_resistor_37_node));
  assign pull_resistor_37_node = controlled_buffer_22_out ? 30'h231 : 30'bz;  // Controlled_Buffer controlled_buffer_34
  Pull_Resistor pull_resistor_38 (.node(pull_resistor_38_node));
  assign pull_resistor_38_node = controlled_buffer_22_out ? 30'h279 : 30'bz;  // Controlled_Buffer controlled_buffer_35
  Pull_Resistor pull_resistor_39 (.node(pull_resistor_39_node));
  assign pull_resistor_39_node = controlled_buffer_22_out ? 30'h3ff : 30'bz;  // Controlled_Buffer controlled_buffer_36
  assign controlled_buffer_37_out = controlled_buffer_22_out ? 30'hfc : 30'bz;  // Controlled_Buffer controlled_buffer_37
  Pull_Resistor pull_resistor_40 (.node(controlled_buffer_37_out));
  assign controlled_buffer_38_out = controlled_buffer_22_out ? 30'hfc : 30'bz;  // Controlled_Buffer controlled_buffer_38
  Pull_Resistor pull_resistor_41 (.node(controlled_buffer_38_out));
  assign controlled_buffer_39_out = controlled_buffer_22_out ? 30'h3ff : 30'bz;  // Controlled_Buffer controlled_buffer_39
  Pull_Resistor pull_resistor_42 (.node(controlled_buffer_39_out));
  Pull_Resistor pull_resistor_43 (.node(pull_resistor_43_node));
  assign pull_resistor_43_node = controlled_buffer_22_out ? 30'h279 : 30'bz;  // Controlled_Buffer controlled_buffer_40
  Pull_Resistor pull_resistor_44 (.node(pull_resistor_44_node));
  assign pull_resistor_44_node = controlled_buffer_22_out ? 30'h231 : 30'bz;  // Controlled_Buffer controlled_buffer_41
  Pull_Resistor pull_resistor_45 (.node(pull_resistor_45_node));
  assign pull_resistor_45_node = controlled_buffer_22_out ? 30'h201 : 30'bz;  // Controlled_Buffer controlled_buffer_42
  Pull_Resistor pull_resistor_46 (.node(controlled_buffer_22_out));
  assign toFront = shifter_21_out | shifter_31_out;  // OR_Gate or_13, 30 bits wide
  Adder #(.width(5)) adder_8 (.a(5'b11110), .b(adder_7_out), .out(adder_8_out));  // open: cin, cout
  Shifter #(.width(30), .shift("lr")) shifter_31 (
    .in(controlled_buffer_33_out), .\dist (adder_8_out), .out(shifter_31_out));
  Shifter #(.width(30), .shift("lr")) shifter_32 (
    .in(pull_resistor_37_node), .\dist (adder_8_out), .out(shifter_32_out));
  Shifter #(.width(30), .shift("lr")) shifter_33 (
    .in(pull_resistor_38_node), .\dist (adder_8_out), .out(shifter_33_out));
  Shifter #(.width(30), .shift("lr")) shifter_34 (
    .in(pull_resistor_39_node), .\dist (adder_8_out), .out(shifter_34_out));
  Shifter #(.width(30), .shift("lr")) shifter_35 (
    .in(controlled_buffer_37_out), .\dist (adder_8_out), .out(shifter_35_out));
  Shifter #(.width(30), .shift("lr")) shifter_36 (
    .in(controlled_buffer_38_out), .\dist (adder_8_out), .out(shifter_36_out));
  Shifter #(.width(30), .shift("lr")) shifter_37 (
    .in(controlled_buffer_39_out), .\dist (adder_8_out), .out(shifter_37_out));
  Shifter #(.width(30), .shift("lr")) shifter_38 (
    .in(pull_resistor_43_node), .\dist (adder_8_out), .out(shifter_38_out));
  Shifter #(.width(30), .shift("lr")) shifter_39 (
    .in(pull_resistor_44_node), .\dist (adder_8_out), .out(shifter_39_out));
  Shifter #(.width(30), .shift("lr")) shifter_40 (
    .in(pull_resistor_45_node), .\dist (adder_8_out), .out(shifter_40_out));
  assign toFront_2 = shifter_22_out | shifter_32_out;  // OR_Gate or_14, 30 bits wide
  assign toFront_3 = shifter_23_out | shifter_33_out;  // OR_Gate or_15, 30 bits wide
  assign toFront_4 = shifter_24_out | shifter_34_out;  // OR_Gate or_16, 30 bits wide
  assign toFront_5 = shifter_25_out | shifter_35_out;  // OR_Gate or_17, 30 bits wide
  assign toFront_6 = shifter_26_out | shifter_36_out;  // OR_Gate or_18, 30 bits wide
  assign toFront_7 = shifter_27_out | shifter_37_out;  // OR_Gate or_19, 30 bits wide
  assign toFront_8 = shifter_28_out | shifter_38_out;  // OR_Gate or_20, 30 bits wide
  assign toFront_9 = shifter_29_out | shifter_39_out;  // OR_Gate or_21, 30 bits wide
  assign toBackground = or_3_out | shifter_41_out;  // OR_Gate or_22, 30 bits wide
  assign toBackground_2 = or_4_out | shifter_42_out;  // OR_Gate or_23, 30 bits wide
  Shifter #(.width(30), .shift("lr")) shifter_41 (.in(toFront), .\dist (5'b00001), .out(shifter_41_out));
  Shifter #(.width(30), .shift("lr")) shifter_42 (.in(toFront_2), .\dist (5'b00001), .out(shifter_42_out));
  Shifter #(.width(30), .shift("lr")) shifter_43 (.in(toFront_3), .\dist (5'b00001), .out(shifter_43_out));
  Shifter #(.width(30), .shift("lr")) shifter_44 (.in(toFront_4), .\dist (5'b00001), .out(shifter_44_out));
  Shifter #(.width(30), .shift("lr")) shifter_45 (.in(toFront_5), .\dist (5'b00001), .out(shifter_45_out));
  Shifter #(.width(30), .shift("lr")) shifter_46 (.in(toFront_6), .\dist (5'b00001), .out(shifter_46_out));
  Shifter #(.width(30), .shift("lr")) shifter_47 (.in(toFront_7), .\dist (5'b00001), .out(shifter_47_out));
  Shifter #(.width(30), .shift("lr")) shifter_48 (.in(toFront_8), .\dist (5'b00001), .out(shifter_48_out));
  assign toFront_10 = shifter_30_out | shifter_40_out;  // OR_Gate or_24, 30 bits wide
  assign toBackground_3 = or_5_out | shifter_43_out;  // OR_Gate or_25, 30 bits wide
  assign toBackground_4 = or_6_out | shifter_44_out;  // OR_Gate or_26, 30 bits wide
  assign toBackground_5 = or_7_out | shifter_45_out;  // OR_Gate or_27, 30 bits wide
  assign toBackground_6 = or_8_out | shifter_46_out;  // OR_Gate or_28, 30 bits wide
  assign toBackground_7 = or_9_out | shifter_47_out;  // OR_Gate or_29, 30 bits wide
  assign toBackground_8 = or_10_out | shifter_48_out;  // OR_Gate or_30, 30 bits wide
  assign toBackground_9 = or_11_out | shifter_49_out;  // OR_Gate or_31, 30 bits wide
  assign toBackground_10 = or_12_out | shifter_50_out;  // OR_Gate or_32, 30 bits wide
  Shifter #(.width(30), .shift("lr")) shifter_49 (.in(toFront_9), .\dist (5'b00001), .out(shifter_49_out));
  Shifter #(.width(30), .shift("lr")) shifter_50 (.in(toFront_10), .\dist (5'b00001), .out(shifter_50_out));

  assign outFlag = inFlag;
  assign outPlayerShiftM = inPlayerShiftM;
  assign outputBackShiftM = inputBackShiftM;

  // Notes on the sheet:
  //   MAKE SHIFT BY NEXT MATRICE
  //   MAKE SHIFT IN CURRENT MATRICE
  //   MAKE SHIFT BY NEXT MATRICE
  //   MAKE SHIFT IN CURRENT MATRICE
endmodule
// turtle3x1
module turtle_3x1 (
  input  animState,
  input  [1:0] inBackShiftD,
  input  [4:0] inputBackShiftM,
  input  [1:0] inPlayerShiftD,
  input  [4:0] inPlayerShiftM,
  input  inFlag,
  output [29:0] toBackground,
  output [29:0] toBackground_2,
  output [29:0] toBackground_3,
  output [29:0] toBackground_4,
  output [29:0] toBackground_5,
  output [1:0] outBackShiftD,
  output [29:0] toBackground_6,
  output animState_2,
  output [29:0] toBackground_7,
  output [4:0] outputBackShiftM,
  output [29:0] toBackground_8,
  output [29:0] toBackground_9,
  output [29:0] toBackground_10,
  output [29:0] toFront,
  output [29:0] toFront_2,
  output [29:0] toFront_3,
  output [29:0] toFront_4,
  output [29:0] toFront_5,
  output [29:0] toFront_6,
  output [1:0] outPlayerShiftD,
  output [4:0] outPlayerShiftM,
  output [29:0] toFront_7,
  output outFlag,
  output [29:0] toFront_8,
  output [29:0] toFront_9,
  output [29:0] toFront_10
);

  wire comparator_1_eq, comparator_2_eq, comparator_3_eq, comparator_4_eq, comparator_5_eq, comparator_6_eq,
       comparator_7_eq, controlled_buffer_41_out, controlled_buffer_42_out, or_11_out, or_12_out,
       pull_resistor_1_node;
  wire [1:0] adder_5_out, multiplexer_1_out;
  wire [4:0] adder_3_out, adder_4_out, adder_6_out, adder_7_out, adder_8_out, not_2_out, not_3_out;
  wire [29:0] _1, _2, _3, _4, _5, _6, _7, _8, _9, _10, controlled_buffer_1_out, controlled_buffer_2_out,
       controlled_buffer_3_out, controlled_buffer_4_out, controlled_buffer_5_out, controlled_buffer_6_out,
       controlled_buffer_7_out, controlled_buffer_8_out, controlled_buffer_9_out, controlled_buffer_10_out,
       controlled_buffer_11_out, controlled_buffer_12_out, controlled_buffer_13_out,
       controlled_buffer_14_out, controlled_buffer_15_out, controlled_buffer_16_out,
       controlled_buffer_17_out, controlled_buffer_18_out, controlled_buffer_19_out,
       controlled_buffer_20_out, controlled_buffer_23_out, controlled_buffer_24_out,
       controlled_buffer_26_out, controlled_buffer_28_out, controlled_buffer_30_out,
       controlled_buffer_31_out, controlled_buffer_32_out, controlled_buffer_33_out,
       controlled_buffer_34_out, controlled_buffer_37_out, controlled_buffer_38_out,
       controlled_buffer_43_out, controlled_buffer_44_out, controlled_buffer_45_out,
       controlled_buffer_47_out, controlled_buffer_48_out, controlled_buffer_49_out,
       controlled_buffer_53_out, controlled_buffer_55_out, controlled_buffer_56_out,
       controlled_buffer_58_out, controlled_buffer_62_out, or_13_out, or_14_out, or_15_out, or_16_out,
       or_17_out, or_18_out, or_19_out, or_20_out, or_21_out, or_22_out, pull_resistor_25_node,
       pull_resistor_26_node, pull_resistor_29_node, pull_resistor_31_node, pull_resistor_33_node,
       pull_resistor_39_node, pull_resistor_40_node, pull_resistor_43_node, pull_resistor_44_node,
       pull_resistor_50_node, pull_resistor_54_node, pull_resistor_55_node, pull_resistor_56_node,
       pull_resistor_58_node, pull_resistor_61_node, pull_resistor_63_node, pull_resistor_64_node,
       pull_resistor_65_node, shifter_1_out, shifter_2_out, shifter_3_out, shifter_4_out, shifter_5_out,
       shifter_6_out, shifter_7_out, shifter_8_out, shifter_9_out, shifter_10_out, shifter_11_out,
       shifter_12_out, shifter_13_out, shifter_14_out, shifter_15_out, shifter_16_out, shifter_17_out,
       shifter_18_out, shifter_19_out, shifter_20_out, shifter_21_out, shifter_22_out, shifter_23_out,
       shifter_24_out, shifter_25_out, shifter_26_out, shifter_27_out, shifter_28_out, shifter_29_out,
       shifter_30_out, shifter_31_out, shifter_32_out, shifter_33_out, shifter_34_out, shifter_35_out,
       shifter_36_out, shifter_37_out, shifter_38_out, shifter_39_out, shifter_40_out, shifter_41_out,
       shifter_42_out, shifter_43_out, shifter_44_out, shifter_45_out, shifter_46_out, shifter_47_out,
       shifter_48_out, shifter_49_out, shifter_50_out;

  assign controlled_buffer_1_out = animState ? 30'h1e779de7 : 30'bz;  // Controlled_Buffer controlled_buffer_1
  assign controlled_buffer_2_out = animState ? 30'h8421084 : 30'bz;  // Controlled_Buffer controlled_buffer_2
  assign controlled_buffer_3_out = animState ? 30'hfc3f0fc : 30'bz;  // Controlled_Buffer controlled_buffer_3
  assign controlled_buffer_4_out = animState ? 30'h1fe7f9fe : 30'bz;  // Controlled_Buffer controlled_buffer_4
  assign controlled_buffer_5_out = animState ? {30{1'b1}} : 30'bz;  // Controlled_Buffer controlled_buffer_5
  assign controlled_buffer_6_out = animState ? {30{1'b1}} : 30'bz;  // Controlled_Buffer controlled_buffer_6
  assign controlled_buffer_7_out = animState ? 30'h1fe7f9fe : 30'bz;  // Controlled_Buffer controlled_buffer_7
  assign controlled_buffer_8_out = animState ? 30'hfc3f0fc : 30'bz;  // Controlled_Buffer controlled_buffer_8
  assign controlled_buffer_9_out = animState ? 30'h8421084 : 30'bz;  // Controlled_Buffer controlled_buffer_9
  assign controlled_buffer_10_out = animState ? 30'h1e779de7 : 30'bz;  // Controlled_Buffer controlled_buffer_10
  assign controlled_buffer_11_out = pull_resistor_1_node ? 30'h1906419 : 30'bz;  // Controlled_Buffer controlled_buffer_11
  assign controlled_buffer_12_out = pull_resistor_1_node ? 30'h731cc73 : 30'bz;  // Controlled_Buffer controlled_buffer_12
  assign controlled_buffer_13_out = pull_resistor_1_node ? 30'hfc3f0fc : 30'bz;  // Controlled_Buffer controlled_buffer_13
  assign controlled_buffer_14_out = pull_resistor_1_node ? 30'h1fe7f9fe : 30'bz;  // Controlled_Buffer controlled_buffer_14
  assign controlled_buffer_15_out = pull_resistor_1_node ? {30{1'b1}} : 30'bz;  // Controlled_Buffer controlled_buffer_15
  assign controlled_buffer_16_out = pull_resistor_1_node ? {30{1'b1}} : 30'bz;  // Controlled_Buffer controlled_buffer_16
  assign controlled_buffer_17_out = pull_resistor_1_node ? 30'h1fe7f9fe : 30'bz;  // Controlled_Buffer controlled_buffer_17
  assign controlled_buffer_18_out = pull_resistor_1_node ? 30'hfc3f0fc : 30'bz;  // Controlled_Buffer controlled_buffer_18
  assign controlled_buffer_19_out = pull_resistor_1_node ? 30'h731cc73 : 30'bz;  // Controlled_Buffer controlled_buffer_19
  assign controlled_buffer_20_out = pull_resistor_1_node ? 30'h1906419 : 30'bz;  // Controlled_Buffer controlled_buffer_20
  Pull_Resistor pull_resistor_1 (.node(pull_resistor_1_node));
  not not_1 (pull_resistor_1_node, animState);
  assign _3 = controlled_buffer_3_out | controlled_buffer_13_out;  // OR_Gate or_1, 30 bits wide
  assign _2 = controlled_buffer_2_out | controlled_buffer_12_out;  // OR_Gate or_2, 30 bits wide
  assign _1 = controlled_buffer_1_out | controlled_buffer_11_out;  // OR_Gate or_3, 30 bits wide
  Pull_Resistor pull_resistor_2 (.node(controlled_buffer_3_out));
  Pull_Resistor pull_resistor_3 (.node(controlled_buffer_1_out));
  Pull_Resistor pull_resistor_4 (.node(controlled_buffer_12_out));
  Pull_Resistor pull_resistor_5 (.node(controlled_buffer_2_out));
  Pull_Resistor pull_resistor_6 (.node(controlled_buffer_11_out));
  assign _5 = controlled_buffer_5_out | controlled_buffer_15_out;  // OR_Gate or_4, 30 bits wide
  assign _4 = controlled_buffer_4_out | controlled_buffer_14_out;  // OR_Gate or_5, 30 bits wide
  Pull_Resistor pull_resistor_7 (.node(controlled_buffer_5_out));
  Pull_Resistor pull_resistor_8 (.node(controlled_buffer_15_out));
  Pull_Resistor pull_resistor_9 (.node(controlled_buffer_6_out));
  Pull_Resistor pull_resistor_10 (.node(controlled_buffer_14_out));
  Pull_Resistor pull_resistor_11 (.node(controlled_buffer_13_out));
  Pull_Resistor pull_resistor_12 (.node(controlled_buffer_4_out));
  assign _6 = controlled_buffer_6_out | controlled_buffer_16_out;  // OR_Gate or_6, 30 bits wide
  assign _7 = controlled_buffer_7_out | controlled_buffer_17_out;  // OR_Gate or_7, 30 bits wide
  assign _8 = controlled_buffer_8_out | controlled_buffer_18_out;  // OR_Gate or_8, 30 bits wide
  Pull_Resistor pull_resistor_13 (.node(controlled_buffer_18_out));
  Pull_Resistor pull_resistor_14 (.node(controlled_buffer_16_out));
  Pull_Resistor pull_resistor_15 (.node(controlled_buffer_7_out));
  Pull_Resistor pull_resistor_16 (.node(controlled_buffer_17_out));
  Pull_Resistor pull_resistor_17 (.node(controlled_buffer_8_out));
  assign _9 = controlled_buffer_9_out | controlled_buffer_19_out;  // OR_Gate or_9, 30 bits wide
  assign _10 = controlled_buffer_10_out | controlled_buffer_20_out;  // OR_Gate or_10, 30 bits wide
  Pull_Resistor pull_resistor_18 (.node(controlled_buffer_20_out));
  Pull_Resistor pull_resistor_19 (.node(controlled_buffer_19_out));
  Pull_Resistor pull_resistor_20 (.node(controlled_buffer_9_out));
  Pull_Resistor pull_resistor_21 (.node(controlled_buffer_10_out));
  Adder #(.width(2)) adder_1 (.a(inBackShiftD), .b(2'b01), .out(outBackShiftD));  // open: cin, cout
  Comparator #(.width(2)) comparator_1 (.a(inBackShiftD), .b(2'b10), .eq(comparator_1_eq));  // open: gt, lt
  or or_11 (or_11_out, comparator_1_eq, comparator_2_eq);
  Comparator #(.width(2)) comparator_2 (.a(2'b00), .b(inBackShiftD), .eq(comparator_2_eq));  // open: gt, lt
  // Probe on outBackShiftD
  Pull_Resistor pull_resistor_22 (.node(inputBackShiftM));
  Comparator #(.width(2)) comparator_3 (.a(outBackShiftD), .b(2'b10), .eq(comparator_3_eq));  // open: gt, lt
  Comparator #(.width(2)) comparator_4 (.a(2'b00), .b(outBackShiftD), .eq(comparator_4_eq));  // open: gt, lt
  Adder #(.width(2)) adder_2 (.a(inPlayerShiftD), .b(2'b01), .out(outPlayerShiftD));  // open: cin, cout
  Pull_Resistor pull_resistor_23 (.node(inPlayerShiftM));
  or or_12 (or_12_out, comparator_3_eq, comparator_4_eq);
  // Probe on adder_3_out
  Pull_Resistor pull_resistor_24 (.node(or_11_out));
  Pull_Resistor pull_resistor_25 (.node(pull_resistor_25_node));
  assign pull_resistor_25_node = or_11_out ? _1 : 30'bz;  // Controlled_Buffer controlled_buffer_21
  Pull_Resistor pull_resistor_26 (.node(pull_resistor_26_node));
  assign pull_resistor_26_node = or_11_out ? _2 : 30'bz;  // Controlled_Buffer controlled_buffer_22
  assign controlled_buffer_23_out = or_11_out ? _3 : 30'bz;  // Controlled_Buffer controlled_buffer_23
  Pull_Resistor pull_resistor_27 (.node(controlled_buffer_23_out));
  assign controlled_buffer_24_out = or_11_out ? _4 : 30'bz;  // Controlled_Buffer controlled_buffer_24
  Pull_Resistor pull_resistor_28 (.node(controlled_buffer_24_out));
  Pull_Resistor pull_resistor_29 (.node(pull_resistor_29_node));
  assign pull_resistor_29_node = or_11_out ? _5 : 30'bz;  // Controlled_Buffer controlled_buffer_25
  assign controlled_buffer_26_out = or_11_out ? _6 : 30'bz;  // Controlled_Buffer controlled_buffer_26
  Pull_Resistor pull_resistor_30 (.node(controlled_buffer_26_out));
  Pull_Resistor pull_resistor_31 (.node(pull_resistor_31_node));
  assign pull_resistor_31_node = or_11_out ? _7 : 30'bz;  // Controlled_Buffer controlled_buffer_27
  assign controlled_buffer_28_out = or_11_out ? _8 : 30'bz;  // Controlled_Buffer controlled_buffer_28
  Pull_Resistor pull_resistor_32 (.node(controlled_buffer_28_out));
  Pull_Resistor pull_resistor_33 (.node(pull_resistor_33_node));
  assign pull_resistor_33_node = or_11_out ? _9 : 30'bz;  // Controlled_Buffer controlled_buffer_29
  assign controlled_buffer_30_out = or_11_out ? _10 : 30'bz;  // Controlled_Buffer controlled_buffer_30
  Pull_Resistor pull_resistor_34 (.node(controlled_buffer_30_out));
  assign not_2_out = ~inputBackShiftM;  // NOT_Gate not_2, 5 bits wide
  // Probe on multiplexer_1_out
  Adder #(.width(5)) adder_3 (.a(inPlayerShiftM), .b(5'b00001), .out(adder_3_out));  // open: cin, cout
  Multiplexer #(.width(2), .disabled(0), .enable("false")) multiplexer_1 (
    .in0(inPlayerShiftD), .in1(outPlayerShiftD), .out(multiplexer_1_out), .sel(comparator_5_eq));
  Comparator #(.width(5), .mode("unsigned")) comparator_5 (
    .a(inPlayerShiftM), .b(5'b11110), .eq(comparator_5_eq));  // open: gt, lt
  Shifter #(.width(30)) shifter_1 (.in(pull_resistor_25_node), .\dist (inputBackShiftM), .out(shifter_1_out));
  Shifter #(.width(30)) shifter_2 (.in(pull_resistor_26_node), .\dist (inputBackShiftM), .out(shifter_2_out));
  Shifter #(.width(30)) shifter_3 (.in(controlled_buffer_23_out), .\dist (inputBackShiftM), .out(shifter_3_out));
  Shifter #(.width(30)) shifter_4 (.in(controlled_buffer_24_out), .\dist (inputBackShiftM), .out(shifter_4_out));
  Shifter #(.width(30)) shifter_5 (.in(pull_resistor_29_node), .\dist (inputBackShiftM), .out(shifter_5_out));
  Shifter #(.width(30)) shifter_6 (.in(controlled_buffer_26_out), .\dist (inputBackShiftM), .out(shifter_6_out));
  Shifter #(.width(30)) shifter_7 (.in(pull_resistor_31_node), .\dist (inputBackShiftM), .out(shifter_7_out));
  Shifter #(.width(30)) shifter_8 (.in(controlled_buffer_28_out), .\dist (inputBackShiftM), .out(shifter_8_out));
  Shifter #(.width(30)) shifter_9 (.in(pull_resistor_33_node), .\dist (inputBackShiftM), .out(shifter_9_out));
  Shifter #(.width(30)) shifter_10 (.in(controlled_buffer_30_out), .\dist (inputBackShiftM), .out(shifter_10_out));
  Adder #(.width(5)) adder_4 (.a(not_2_out), .b(5'b00001), .out(adder_4_out));  // open: cin, cout
  assign controlled_buffer_31_out = or_12_out ? _1 : 30'bz;  // Controlled_Buffer controlled_buffer_31
  Pull_Resistor pull_resistor_35 (.node(controlled_buffer_31_out));
  assign controlled_buffer_32_out = or_12_out ? _2 : 30'bz;  // Controlled_Buffer controlled_buffer_32
  Pull_Resistor pull_resistor_36 (.node(controlled_buffer_32_out));
  assign controlled_buffer_33_out = or_12_out ? _3 : 30'bz;  // Controlled_Buffer controlled_buffer_33
  Pull_Resistor pull_resistor_37 (.node(controlled_buffer_33_out));
  assign controlled_buffer_34_out = or_12_out ? _4 : 30'bz;  // Controlled_Buffer controlled_buffer_34
  Pull_Resistor pull_resistor_38 (.node(controlled_buffer_34_out));
  Pull_Resistor pull_resistor_39 (.node(pull_resistor_39_node));
  assign pull_resistor_39_node = or_12_out ? _5 : 30'bz;  // Controlled_Buffer controlled_buffer_35
  Pull_Resistor pull_resistor_40 (.node(pull_resistor_40_node));
  assign pull_resistor_40_node = or_12_out ? _6 : 30'bz;  // Controlled_Buffer controlled_buffer_36
  assign controlled_buffer_37_out = or_12_out ? _7 : 30'bz;  // Controlled_Buffer controlled_buffer_37
  Pull_Resistor pull_resistor_41 (.node(controlled_buffer_37_out));
  assign controlled_buffer_38_out = or_12_out ? _8 : 30'bz;  // Controlled_Buffer controlled_buffer_38
  Pull_Resistor pull_resistor_42 (.node(controlled_buffer_38_out));
  Pull_Resistor pull_resistor_43 (.node(pull_resistor_43_node));
  assign pull_resistor_43_node = or_12_out ? _9 : 30'bz;  // Controlled_Buffer controlled_buffer_39
  Pull_Resistor pull_resistor_44 (.node(pull_resistor_44_node));
  assign pull_resistor_44_node = or_12_out ? _10 : 30'bz;  // Controlled_Buffer controlled_buffer_40
  Pull_Resistor pull_resistor_45 (.node(or_12_out));
  assign controlled_buffer_41_out = inFlag ? comparator_6_eq : 1'bz;  // Controlled_Buffer controlled_buffer_41
  Comparator #(.width(2)) comparator_6 (.a(2'b00), .b(multiplexer_1_out), .eq(comparator_6_eq));  // open: gt, lt
  Comparator #(.width(2)) comparator_7 (.a(2'b00), .b(adder_5_out), .eq(comparator_7_eq));  // open: gt, lt
  Adder #(.width(2)) adder_5 (.a(multiplexer_1_out), .b(2'b01), .out(adder_5_out));  // open: cin, cout
  assign or_13_out = shifter_1_out | shifter_11_out;  // OR_Gate or_13, 30 bits wide
  Adder #(.width(5)) adder_6 (.a(5'b11110), .b(adder_4_out), .out(adder_6_out));  // open: cin, cout
  Shifter #(.width(30), .shift("lr")) shifter_11 (
    .in(controlled_buffer_31_out), .\dist (adder_6_out), .out(shifter_11_out));
  Shifter #(.width(30), .shift("lr")) shifter_12 (
    .in(controlled_buffer_32_out), .\dist (adder_6_out), .out(shifter_12_out));
  Shifter #(.width(30), .shift("lr")) shifter_13 (
    .in(controlled_buffer_33_out), .\dist (adder_6_out), .out(shifter_13_out));
  Shifter #(.width(30), .shift("lr")) shifter_14 (
    .in(controlled_buffer_34_out), .\dist (adder_6_out), .out(shifter_14_out));
  Shifter #(.width(30), .shift("lr")) shifter_15 (
    .in(pull_resistor_39_node), .\dist (adder_6_out), .out(shifter_15_out));
  Shifter #(.width(30), .shift("lr")) shifter_16 (
    .in(pull_resistor_40_node), .\dist (adder_6_out), .out(shifter_16_out));
  Shifter #(.width(30), .shift("lr")) shifter_17 (
    .in(controlled_buffer_37_out), .\dist (adder_6_out), .out(shifter_17_out));
  Shifter #(.width(30), .shift("lr")) shifter_18 (
    .in(controlled_buffer_38_out), .\dist (adder_6_out), .out(shifter_18_out));
  Shifter #(.width(30), .shift("lr")) shifter_19 (
    .in(pull_resistor_43_node), .\dist (adder_6_out), .out(shifter_19_out));
  Shifter #(.width(30), .shift("lr")) shifter_20 (
    .in(pull_resistor_44_node), .\dist (adder_6_out), .out(shifter_20_out));
  assign controlled_buffer_42_out = inFlag ? comparator_7_eq : 1'bz;  // Controlled_Buffer controlled_buffer_42
  assign or_14_out = shifter_2_out | shifter_12_out;  // OR_Gate or_14, 30 bits wide
  assign or_15_out = shifter_3_out | shifter_13_out;  // OR_Gate or_15, 30 bits wide
  assign or_16_out = shifter_4_out | shifter_14_out;  // OR_Gate or_16, 30 bits wide
  assign or_17_out = shifter_5_out | shifter_15_out;  // OR_Gate or_17, 30 bits wide
  assign or_18_out = shifter_6_out | shifter_16_out;  // OR_Gate or_18, 30 bits wide
  assign or_19_out = shifter_7_out | shifter_17_out;  // OR_Gate or_19, 30 bits wide
  assign or_20_out = shifter_8_out | shifter_18_out;  // OR_Gate or_20, 30 bits wide
  assign or_21_out = shifter_9_out | shifter_19_out;  // OR_Gate or_21, 30 bits wide
  assign controlled_buffer_43_out = controlled_buffer_41_out ? 30'h279 : 30'bz;  // Controlled_Buffer controlled_buffer_43
  Pull_Resistor pull_resistor_46 (.node(controlled_buffer_43_out));
  Pull_Resistor pull_resistor_47 (.node(controlled_buffer_41_out));
  assign controlled_buffer_44_out = controlled_buffer_41_out ? 30'h231 : 30'bz;  // Controlled_Buffer controlled_buffer_44
  Pull_Resistor pull_resistor_48 (.node(controlled_buffer_44_out));
  assign controlled_buffer_45_out = controlled_buffer_41_out ? 30'h279 : 30'bz;  // Controlled_Buffer controlled_buffer_45
  Pull_Resistor pull_resistor_49 (.node(controlled_buffer_45_out));
  Pull_Resistor pull_resistor_50 (.node(pull_resistor_50_node));
  assign pull_resistor_50_node = controlled_buffer_41_out ? 30'h3ff : 30'bz;  // Controlled_Buffer controlled_buffer_46
  assign controlled_buffer_47_out = controlled_buffer_41_out ? 30'hfc : 30'bz;  // Controlled_Buffer controlled_buffer_47
  Pull_Resistor pull_resistor_51 (.node(controlled_buffer_47_out));
  assign controlled_buffer_48_out = controlled_buffer_41_out ? 30'hfc : 30'bz;  // Controlled_Buffer controlled_buffer_48
  Pull_Resistor pull_resistor_52 (.node(controlled_buffer_48_out));
  assign controlled_buffer_49_out = controlled_buffer_41_out ? 30'h3ff : 30'bz;  // Controlled_Buffer controlled_buffer_49
  Pull_Resistor pull_resistor_53 (.node(controlled_buffer_49_out));
  Pull_Resistor pull_resistor_54 (.node(pull_resistor_54_node));
  assign pull_resistor_54_node = controlled_buffer_41_out ? 30'h279 : 30'bz;  // Controlled_Buffer controlled_buffer_50
  Pull_Resistor pull_resistor_55 (.node(pull_resistor_55_node));
  assign pull_resistor_55_node = controlled_buffer_41_out ? 30'h231 : 30'bz;  // Controlled_Buffer controlled_buffer_51
  Pull_Resistor pull_resistor_56 (.node(pull_resistor_56_node));
  assign pull_resistor_56_node = controlled_buffer_41_out ? 30'h201 : 30'bz;  // Controlled_Buffer controlled_buffer_52
  assign or_22_out = shifter_10_out | shifter_20_out;  // OR_Gate or_22, 30 bits wide
  Shifter #(.width(30)) shifter_21 (.in(controlled_buffer_43_out), .\dist (adder_3_out), .out(shifter_21_out));
  Shifter #(.width(30)) shifter_22 (.in(controlled_buffer_44_out), .\dist (adder_3_out), .out(shifter_22_out));
  Shifter #(.width(30)) shifter_23 (.in(controlled_buffer_45_out), .\dist (adder_3_out), .out(shifter_23_out));
  Shifter #(.width(30)) shifter_24 (.in(pull_resistor_50_node), .\dist (adder_3_out), .out(shifter_24_out));
  Shifter #(.width(30)) shifter_25 (.in(controlled_buffer_47_out), .\dist (adder_3_out), .out(shifter_25_out));
  Shifter #(.width(30)) shifter_26 (.in(controlled_buffer_48_out), .\dist (adder_3_out), .out(shifter_26_out));
  Shifter #(.width(30)) shifter_27 (.in(controlled_buffer_49_out), .\dist (adder_3_out), .out(shifter_27_out));
  Shifter #(.width(30)) shifter_28 (.in(pull_resistor_54_node), .\dist (adder_3_out), .out(shifter_28_out));
  Shifter #(.width(30)) shifter_29 (.in(pull_resistor_55_node), .\dist (adder_3_out), .out(shifter_29_out));
  Shifter #(.width(30)) shifter_30 (.in(pull_resistor_56_node), .\dist (adder_3_out), .out(shifter_30_out));
  assign not_3_out = ~adder_3_out;  // NOT_Gate not_3, 5 bits wide
  Adder #(.width(5)) adder_7 (.a(not_3_out), .b(5'b00001), .out(adder_7_out));  // open: cin, cout
  Adder #(.width(5)) adder_8 (.a(5'b11110), .b(adder_7_out), .out(adder_8_out));  // open: cin, cout
  assign controlled_buffer_53_out = controlled_buffer_42_out ? 30'h279 : 30'bz;  // Controlled_Buffer controlled_buffer_53
  Pull_Resistor pull_resistor_57 (.node(controlled_buffer_53_out));
  Shifter #(.width(30), .shift("lr")) shifter_31 (
    .in(controlled_buffer_53_out), .\dist (adder_8_out), .out(shifter_31_out));
  Pull_Resistor pull_resistor_58 (.node(pull_resistor_58_node));
  assign pull_resistor_58_node = controlled_buffer_42_out ? 30'h231 : 30'bz;  // Controlled_Buffer controlled_buffer_54
  Shifter #(.width(30), .shift("lr")) shifter_32 (
    .in(pull_resistor_58_node), .\dist (adder_8_out), .out(shifter_32_out));
  assign controlled_buffer_55_out = controlled_buffer_42_out ? 30'h279 : 30'bz;  // Controlled_Buffer controlled_buffer_55
  Pull_Resistor pull_resistor_59 (.node(controlled_buffer_55_out));
  Shifter #(.width(30), .shift("lr")) shifter_33 (
    .in(controlled_buffer_55_out), .\dist (adder_8_out), .out(shifter_33_out));
  assign controlled_buffer_56_out = controlled_buffer_42_out ? 30'h3ff : 30'bz;  // Controlled_Buffer controlled_buffer_56
  Pull_Resistor pull_resistor_60 (.node(controlled_buffer_56_out));
  Shifter #(.width(30), .shift("lr")) shifter_34 (
    .in(controlled_buffer_56_out), .\dist (adder_8_out), .out(shifter_34_out));
  Pull_Resistor pull_resistor_61 (.node(pull_resistor_61_node));
  assign pull_resistor_61_node = controlled_buffer_42_out ? 30'hfc : 30'bz;  // Controlled_Buffer controlled_buffer_57
  Shifter #(.width(30), .shift("lr")) shifter_35 (
    .in(pull_resistor_61_node), .\dist (adder_8_out), .out(shifter_35_out));
  assign controlled_buffer_58_out = controlled_buffer_42_out ? 30'hfc : 30'bz;  // Controlled_Buffer controlled_buffer_58
  Pull_Resistor pull_resistor_62 (.node(controlled_buffer_58_out));
  Shifter #(.width(30), .shift("lr")) shifter_36 (
    .in(controlled_buffer_58_out), .\dist (adder_8_out), .out(shifter_36_out));
  Pull_Resistor pull_resistor_63 (.node(pull_resistor_63_node));
  assign pull_resistor_63_node = controlled_buffer_42_out ? 30'h3ff : 30'bz;  // Controlled_Buffer controlled_buffer_59
  Shifter #(.width(30), .shift("lr")) shifter_37 (
    .in(pull_resistor_63_node), .\dist (adder_8_out), .out(shifter_37_out));
  Pull_Resistor pull_resistor_64 (.node(pull_resistor_64_node));
  assign pull_resistor_64_node = controlled_buffer_42_out ? 30'h279 : 30'bz;  // Controlled_Buffer controlled_buffer_60
  Shifter #(.width(30), .shift("lr")) shifter_38 (
    .in(pull_resistor_64_node), .\dist (adder_8_out), .out(shifter_38_out));
  Pull_Resistor pull_resistor_65 (.node(pull_resistor_65_node));
  assign pull_resistor_65_node = controlled_buffer_42_out ? 30'h231 : 30'bz;  // Controlled_Buffer controlled_buffer_61
  Shifter #(.width(30), .shift("lr")) shifter_39 (
    .in(pull_resistor_65_node), .\dist (adder_8_out), .out(shifter_39_out));
  assign controlled_buffer_62_out = controlled_buffer_42_out ? 30'h201 : 30'bz;  // Controlled_Buffer controlled_buffer_62
  Pull_Resistor pull_resistor_66 (.node(controlled_buffer_62_out));
  Shifter #(.width(30), .shift("lr")) shifter_40 (
    .in(controlled_buffer_62_out), .\dist (adder_8_out), .out(shifter_40_out));
  Pull_Resistor pull_resistor_67 (.node(controlled_buffer_42_out));
  assign toFront = shifter_21_out | shifter_31_out;  // OR_Gate or_23, 30 bits wide
  assign toFront_2 = shifter_22_out | shifter_32_out;  // OR_Gate or_24, 30 bits wide
  assign toFront_3 = shifter_23_out | shifter_33_out;  // OR_Gate or_25, 30 bits wide
  assign toFront_4 = shifter_24_out | shifter_34_out;  // OR_Gate or_26, 30 bits wide
  assign toFront_5 = shifter_25_out | shifter_35_out;  // OR_Gate or_27, 30 bits wide
  assign toFront_6 = shifter_26_out | shifter_36_out;  // OR_Gate or_28, 30 bits wide
  assign toFront_7 = shifter_27_out | shifter_37_out;  // OR_Gate or_29, 30 bits wide
  Shifter #(.width(30), .shift("lr")) shifter_41 (.in(toFront), .\dist (5'b00001), .out(shifter_41_out));
  Shifter #(.width(30), .shift("lr")) shifter_42 (.in(toFront_2), .\dist (5'b00001), .out(shifter_42_out));
  Shifter #(.width(30), .shift("lr")) shifter_43 (.in(toFront_3), .\dist (5'b00001), .out(shifter_43_out));
  Shifter #(.width(30), .shift("lr")) shifter_44 (.in(toFront_4), .\dist (5'b00001), .out(shifter_44_out));
  Shifter #(.width(30), .shift("lr")) shifter_45 (.in(toFront_5), .\dist (5'b00001), .out(shifter_45_out));
  Shifter #(.width(30), .shift("lr")) shifter_46 (.in(toFront_6), .\dist (5'b00001), .out(shifter_46_out));
  assign toFront_8 = shifter_28_out | shifter_38_out;  // OR_Gate or_30, 30 bits wide
  assign toFront_9 = shifter_29_out | shifter_39_out;  // OR_Gate or_31, 30 bits wide
  assign toFront_10 = shifter_30_out | shifter_40_out;  // OR_Gate or_32, 30 bits wide
  assign toBackground = or_13_out | shifter_41_out;  // OR_Gate or_33, 30 bits wide
  assign toBackground_2 = or_14_out | shifter_42_out;  // OR_Gate or_34, 30 bits wide
  assign toBackground_3 = or_15_out | shifter_43_out;  // OR_Gate or_35, 30 bits wide
  assign toBackground_4 = or_16_out | shifter_44_out;  // OR_Gate or_36, 30 bits wide
  assign toBackground_5 = or_17_out | shifter_45_out;  // OR_Gate or_37, 30 bits wide
  assign toBackground_6 = or_18_out | shifter_46_out;  // OR_Gate or_38, 30 bits wide
  assign toBackground_7 = or_19_out | shifter_47_out;  // OR_Gate or_39, 30 bits wide
  assign toBackground_8 = or_20_out | shifter_48_out;  // OR_Gate or_40, 30 bits wide
  Shifter #(.width(30), .shift("lr")) shifter_47 (.in(toFront_7), .\dist (5'b00001), .out(shifter_47_out));
  Shifter #(.width(30), .shift("lr")) shifter_48 (.in(toFront_8), .\dist (5'b00001), .out(shifter_48_out));
  Shifter #(.width(30), .shift("lr")) shifter_49 (.in(toFront_9), .\dist (5'b00001), .out(shifter_49_out));
  Shifter #(.width(30), .shift("lr")) shifter_50 (.in(toFront_10), .\dist (5'b00001), .out(shifter_50_out));
  assign toBackground_9 = or_21_out | shifter_49_out;  // OR_Gate or_41, 30 bits wide
  assign toBackground_10 = or_22_out | shifter_50_out;  // OR_Gate or_42, 30 bits wide

  assign animState_2 = animState;
  assign outFlag = inFlag;
  assign outPlayerShiftM = inPlayerShiftM;
  assign outputBackShiftM = inputBackShiftM;

  // Notes on the sheet:
  //   MAKE SHIFT BY NEXT MATRICE
  //   MAKE SHIFT IN CURRENT MATRICE
  //   MAKE SHIFT IN CURRENT MATRICE
  //   MAKE SHIFT BY NEXT MATRICE
endmodule

module turtle_2x1 (
  input  [1:0] inBackShiftD,
  input  [4:0] inputBackShiftM,
  input  [3:0] animState,
  input  [1:0] inPlayerShiftD,
  input  [4:0] inPlayerShiftM,
  input  inFlag,
  output [29:0] toBackground,
  output [29:0] toBackground_2,
  output [29:0] toBackground_3,
  output [29:0] toBackground_4,
  output [29:0] toBackground_5,
  output [29:0] toBackground_6,
  output [1:0] outBackShiftD,
  output [29:0] toBackground_7,
  output [4:0] outputBackShiftM,
  output [29:0] toBackground_8,
  output [29:0] toBackground_9,
  output [29:0] toBackground_10,
  output [29:0] toFront,
  output [29:0] toFront_2,
  output [29:0] toFront_3,
  output [29:0] toFront_4,
  output [29:0] toFront_5,
  output [29:0] toFront_6,
  output [1:0] outPlayerShiftD,
  output [4:0] outPlayerShiftM,
  output [29:0] toFront_7,
  output outFlag,
  output [29:0] toFront_8,
  output [3:0] animState_2,
  output [29:0] toFront_9,
  output [29:0] toFront_10
);

  wire comparator_1_lt, comparator_2_gt, comparator_3_eq, comparator_4_eq, comparator_5_eq, comparator_6_eq,
       comparator_7_eq, comparator_8_eq, comparator_9_eq, comparator_10_eq, comparator_11_eq,
       comparator_12_eq, comparator_13_eq, comparator_14_eq, comparator_15_eq, comparator_16_eq,
       comparator_17_eq, comparator_18_eq, comparator_19_eq, comparator_20_eq, comparator_21_eq,
       comparator_22_eq, comparator_23_eq, comparator_24_eq, controlled_buffer_81_out,
       controlled_buffer_82_out, or_1_out, or_2_out, or_3_out, or_4_out, or_5_out, or_6_out, or_17_out,
       or_18_out, or_19_out, or_20_out, or_21_out, or_22_out;
  wire [1:0] adder_6_out, multiplexer_1_out;
  wire [4:0] adder_2_out, adder_3_out, adder_5_out, adder_7_out, adder_8_out, not_1_out, not_2_out;
  wire [29:0] _1, _2, _3, _4, _5, _6, _7, _8, _9, _10, controlled_buffer_1_out, controlled_buffer_2_out,
       controlled_buffer_3_out, controlled_buffer_4_out, controlled_buffer_5_out, controlled_buffer_6_out,
       controlled_buffer_7_out, controlled_buffer_8_out, controlled_buffer_9_out, controlled_buffer_10_out,
       controlled_buffer_11_out, controlled_buffer_12_out, controlled_buffer_13_out,
       controlled_buffer_14_out, controlled_buffer_15_out, controlled_buffer_16_out,
       controlled_buffer_17_out, controlled_buffer_18_out, controlled_buffer_19_out,
       controlled_buffer_20_out, controlled_buffer_21_out, controlled_buffer_22_out,
       controlled_buffer_23_out, controlled_buffer_24_out, controlled_buffer_25_out,
       controlled_buffer_26_out, controlled_buffer_27_out, controlled_buffer_28_out,
       controlled_buffer_29_out, controlled_buffer_30_out, controlled_buffer_31_out,
       controlled_buffer_32_out, controlled_buffer_33_out, controlled_buffer_34_out,
       controlled_buffer_35_out, controlled_buffer_36_out, controlled_buffer_37_out,
       controlled_buffer_39_out, controlled_buffer_40_out, controlled_buffer_41_out,
       controlled_buffer_42_out, controlled_buffer_43_out, controlled_buffer_44_out,
       controlled_buffer_45_out, controlled_buffer_46_out, controlled_buffer_47_out,
       controlled_buffer_48_out, controlled_buffer_49_out, controlled_buffer_50_out,
       controlled_buffer_51_out, controlled_buffer_52_out, controlled_buffer_53_out,
       controlled_buffer_54_out, controlled_buffer_55_out, controlled_buffer_56_out,
       controlled_buffer_57_out, controlled_buffer_59_out, controlled_buffer_60_out,
       controlled_buffer_61_out, controlled_buffer_64_out, controlled_buffer_67_out,
       controlled_buffer_68_out, controlled_buffer_70_out, controlled_buffer_71_out,
       controlled_buffer_73_out, controlled_buffer_75_out, controlled_buffer_76_out,
       controlled_buffer_79_out, controlled_buffer_80_out, controlled_buffer_84_out,
       controlled_buffer_86_out, controlled_buffer_87_out, controlled_buffer_88_out,
       controlled_buffer_89_out, controlled_buffer_92_out, controlled_buffer_94_out,
       controlled_buffer_95_out, controlled_buffer_97_out, controlled_buffer_99_out,
       controlled_buffer_100_out, controlled_buffer_101_out, controlled_buffer_102_out, or_23_out, or_24_out,
       or_25_out, or_26_out, or_27_out, or_28_out, or_29_out, or_30_out, or_31_out, or_32_out,
       pull_resistor_40_node, pull_resistor_65_node, pull_resistor_66_node, pull_resistor_68_node,
       pull_resistor_69_node, pull_resistor_72_node, pull_resistor_75_node, pull_resistor_77_node,
       pull_resistor_80_node, pull_resistor_81_node, pull_resistor_87_node, pull_resistor_89_node,
       pull_resistor_94_node, pull_resistor_95_node, pull_resistor_97_node, pull_resistor_100_node,
       pull_resistor_102_node, shifter_1_out, shifter_2_out, shifter_3_out, shifter_4_out, shifter_5_out,
       shifter_6_out, shifter_7_out, shifter_8_out, shifter_9_out, shifter_10_out, shifter_11_out,
       shifter_12_out, shifter_13_out, shifter_14_out, shifter_15_out, shifter_16_out, shifter_17_out,
       shifter_18_out, shifter_19_out, shifter_20_out, shifter_21_out, shifter_22_out, shifter_23_out,
       shifter_24_out, shifter_25_out, shifter_26_out, shifter_27_out, shifter_28_out, shifter_29_out,
       shifter_30_out, shifter_31_out, shifter_32_out, shifter_33_out, shifter_34_out, shifter_35_out,
       shifter_36_out, shifter_37_out, shifter_38_out, shifter_39_out, shifter_40_out, shifter_41_out,
       shifter_42_out, shifter_43_out, shifter_44_out, shifter_45_out, shifter_46_out, shifter_47_out,
       shifter_48_out, shifter_49_out, shifter_50_out;

  Pull_Resistor pull_resistor_1 (.node(animState));
  assign controlled_buffer_1_out = or_1_out ? 30'h79de7 : 30'bz;  // Controlled_Buffer controlled_buffer_1
  assign controlled_buffer_2_out = or_1_out ? 30'h21084 : 30'bz;  // Controlled_Buffer controlled_buffer_2
  assign controlled_buffer_3_out = or_1_out ? 30'h3f0fc : 30'bz;  // Controlled_Buffer controlled_buffer_3
  assign controlled_buffer_4_out = or_1_out ? 30'h7f9fe : 30'bz;  // Controlled_Buffer controlled_buffer_4
  assign controlled_buffer_5_out = or_1_out ? 30'hfffff : 30'bz;  // Controlled_Buffer controlled_buffer_5
  assign controlled_buffer_6_out = or_1_out ? 30'hfffff : 30'bz;  // Controlled_Buffer controlled_buffer_6
  assign controlled_buffer_7_out = or_1_out ? 30'h7f9fe : 30'bz;  // Controlled_Buffer controlled_buffer_7
  assign controlled_buffer_8_out = or_1_out ? 30'h3f0fc : 30'bz;  // Controlled_Buffer controlled_buffer_8
  assign controlled_buffer_9_out = or_1_out ? 30'h21084 : 30'bz;  // Controlled_Buffer controlled_buffer_9
  assign controlled_buffer_10_out = or_1_out ? 30'h79de7 : 30'bz;  // Controlled_Buffer controlled_buffer_10
  assign controlled_buffer_11_out = or_2_out ? {30{1'b0}} : 30'bz;  // Controlled_Buffer controlled_buffer_11
  assign controlled_buffer_12_out = or_2_out ? 30'h318c6 : 30'bz;  // Controlled_Buffer controlled_buffer_12
  assign controlled_buffer_13_out = or_2_out ? 30'h3f0fc : 30'bz;  // Controlled_Buffer controlled_buffer_13
  assign controlled_buffer_14_out = or_2_out ? 30'h7f9fe : 30'bz;  // Controlled_Buffer controlled_buffer_14
  assign controlled_buffer_15_out = or_2_out ? 30'hfffff : 30'bz;  // Controlled_Buffer controlled_buffer_15
  assign controlled_buffer_16_out = or_2_out ? 30'hfffff : 30'bz;  // Controlled_Buffer controlled_buffer_16
  assign controlled_buffer_17_out = or_2_out ? 30'h7f9fe : 30'bz;  // Controlled_Buffer controlled_buffer_17
  assign controlled_buffer_18_out = or_2_out ? 30'h3f0fc : 30'bz;  // Controlled_Buffer controlled_buffer_18
  assign controlled_buffer_19_out = or_2_out ? 30'h318c6 : 30'bz;  // Controlled_Buffer controlled_buffer_19
  assign controlled_buffer_20_out = or_2_out ? {30{1'b0}} : 30'bz;  // Controlled_Buffer controlled_buffer_20
  or or_1 (or_1_out, comparator_1_lt, comparator_2_gt);
  Comparator #(.width(4), .mode("unsigned")) comparator_1 (
    .a(animState), .b(4'b0010), .lt(comparator_1_lt));  // open: gt, eq
  Comparator #(.width(4), .mode("unsigned")) comparator_2 (
    .a(animState), .b(4'b1100), .gt(comparator_2_gt));  // open: eq, lt
  or or_2 (or_2_out, comparator_3_eq, comparator_13_eq);
  or or_3 (or_3_out, comparator_4_eq, comparator_12_eq);
  Comparator #(.width(4), .mode("unsigned")) comparator_3 (
    .a(animState), .b(4'b0010), .eq(comparator_3_eq));  // open: gt, lt
  Comparator #(.width(4), .mode("unsigned")) comparator_4 (
    .a(animState), .b(4'b0011), .eq(comparator_4_eq));  // open: gt, lt
  Comparator #(.width(4), .mode("unsigned")) comparator_5 (
    .a(animState), .b(4'b0100), .eq(comparator_5_eq));  // open: gt, lt
  Comparator #(.width(4), .mode("unsigned")) comparator_6 (
    .a(animState), .b(4'b0101), .eq(comparator_6_eq));  // open: gt, lt
  Comparator #(.width(4), .mode("unsigned")) comparator_7 (
    .a(animState), .b(4'b0110), .eq(comparator_7_eq));  // open: gt, lt
  Comparator #(.width(4), .mode("unsigned")) comparator_8 (
    .a(animState), .b(4'b0111), .eq(comparator_8_eq));  // open: gt, lt
  Comparator #(.width(4), .mode("unsigned")) comparator_9 (
    .a(animState), .b(4'b1000), .eq(comparator_9_eq));  // open: gt, lt
  Comparator #(.width(4), .mode("unsigned")) comparator_10 (
    .a(animState), .b(4'b1001), .eq(comparator_10_eq));  // open: gt, lt
  Comparator #(.width(4), .mode("unsigned")) comparator_11 (
    .a(animState), .b(4'b1010), .eq(comparator_11_eq));  // open: gt, lt
  Comparator #(.width(4), .mode("unsigned")) comparator_12 (
    .a(animState), .b(4'b1011), .eq(comparator_12_eq));  // open: gt, lt
  Comparator #(.width(4), .mode("unsigned")) comparator_13 (
    .a(animState), .b(4'b1100), .eq(comparator_13_eq));  // open: gt, lt
  assign controlled_buffer_21_out = or_3_out ? {30{1'b0}} : 30'bz;  // Controlled_Buffer controlled_buffer_21
  assign controlled_buffer_22_out = or_3_out ? {30{1'b0}} : 30'bz;  // Controlled_Buffer controlled_buffer_22
  assign controlled_buffer_23_out = or_3_out ? 30'h3f0fc : 30'bz;  // Controlled_Buffer controlled_buffer_23
  assign controlled_buffer_24_out = or_3_out ? 30'h7f9fe : 30'bz;  // Controlled_Buffer controlled_buffer_24
  assign controlled_buffer_25_out = or_3_out ? 30'hfffff : 30'bz;  // Controlled_Buffer controlled_buffer_25
  assign controlled_buffer_26_out = or_3_out ? 30'hfffff : 30'bz;  // Controlled_Buffer controlled_buffer_26
  assign controlled_buffer_27_out = or_3_out ? 30'h7f9fe : 30'bz;  // Controlled_Buffer controlled_buffer_27
  assign controlled_buffer_28_out = or_3_out ? 30'h3f0fc : 30'bz;  // Controlled_Buffer controlled_buffer_28
  assign controlled_buffer_29_out = or_3_out ? {30{1'b0}} : 30'bz;  // Controlled_Buffer controlled_buffer_29
  assign controlled_buffer_30_out = or_3_out ? {30{1'b0}} : 30'bz;  // Controlled_Buffer controlled_buffer_30
  assign controlled_buffer_31_out = or_4_out ? {30{1'b0}} : 30'bz;  // Controlled_Buffer controlled_buffer_31
  assign controlled_buffer_32_out = or_4_out ? {30{1'b0}} : 30'bz;  // Controlled_Buffer controlled_buffer_32
  assign controlled_buffer_33_out = or_4_out ? 30'hc030 : 30'bz;  // Controlled_Buffer controlled_buffer_33
  assign controlled_buffer_34_out = or_4_out ? 30'h1e078 : 30'bz;  // Controlled_Buffer controlled_buffer_34
  assign controlled_buffer_35_out = or_4_out ? 30'h3f0fc : 30'bz;  // Controlled_Buffer controlled_buffer_35
  assign controlled_buffer_36_out = or_4_out ? 30'h3f0fc : 30'bz;  // Controlled_Buffer controlled_buffer_36
  assign controlled_buffer_37_out = or_4_out ? 30'h1e078 : 30'bz;  // Controlled_Buffer controlled_buffer_37
  assign controlled_buffer_27_out = or_4_out ? 30'hc030 : 30'bz;  // Controlled_Buffer controlled_buffer_38
  assign controlled_buffer_39_out = or_4_out ? {30{1'b0}} : 30'bz;  // Controlled_Buffer controlled_buffer_39
  assign controlled_buffer_40_out = or_4_out ? {30{1'b0}} : 30'bz;  // Controlled_Buffer controlled_buffer_40
  assign controlled_buffer_41_out = or_5_out ? {30{1'b0}} : 30'bz;  // Controlled_Buffer controlled_buffer_41
  assign controlled_buffer_42_out = or_5_out ? {30{1'b0}} : 30'bz;  // Controlled_Buffer controlled_buffer_42
  assign controlled_buffer_43_out = or_5_out ? {30{1'b0}} : 30'bz;  // Controlled_Buffer controlled_buffer_43
  assign controlled_buffer_44_out = or_5_out ? {30{1'b0}} : 30'bz;  // Controlled_Buffer controlled_buffer_44
  assign controlled_buffer_45_out = or_5_out ? 30'hc030 : 30'bz;  // Controlled_Buffer controlled_buffer_45
  assign controlled_buffer_46_out = or_5_out ? 30'hc030 : 30'bz;  // Controlled_Buffer controlled_buffer_46
  assign controlled_buffer_47_out = or_5_out ? {30{1'b0}} : 30'bz;  // Controlled_Buffer controlled_buffer_47
  assign controlled_buffer_48_out = or_5_out ? {30{1'b0}} : 30'bz;  // Controlled_Buffer controlled_buffer_48
  assign controlled_buffer_49_out = or_5_out ? {30{1'b0}} : 30'bz;  // Controlled_Buffer controlled_buffer_49
  assign controlled_buffer_50_out = or_5_out ? {30{1'b0}} : 30'bz;  // Controlled_Buffer controlled_buffer_50
  assign controlled_buffer_51_out = or_6_out ? {30{1'b0}} : 30'bz;  // Controlled_Buffer controlled_buffer_51
  assign controlled_buffer_52_out = or_6_out ? {30{1'b0}} : 30'bz;  // Controlled_Buffer controlled_buffer_52
  assign controlled_buffer_53_out = or_6_out ? {30{1'b0}} : 30'bz;  // Controlled_Buffer controlled_buffer_53
  assign controlled_buffer_54_out = or_6_out ? {30{1'b0}} : 30'bz;  // Controlled_Buffer controlled_buffer_54
  assign controlled_buffer_55_out = or_6_out ? {30{1'b0}} : 30'bz;  // Controlled_Buffer controlled_buffer_55
  assign controlled_buffer_56_out = or_6_out ? {30{1'b0}} : 30'bz;  // Controlled_Buffer controlled_buffer_56
  assign controlled_buffer_57_out = or_6_out ? {30{1'b0}} : 30'bz;  // Controlled_Buffer controlled_buffer_57
  assign controlled_buffer_47_out = or_6_out ? {30{1'b0}} : 30'bz;  // Controlled_Buffer controlled_buffer_58
  assign controlled_buffer_59_out = or_6_out ? {30{1'b0}} : 30'bz;  // Controlled_Buffer controlled_buffer_59
  assign controlled_buffer_60_out = or_6_out ? {30{1'b0}} : 30'bz;  // Controlled_Buffer controlled_buffer_60
  or or_4 (or_4_out, comparator_5_eq, comparator_11_eq);
  or or_5 (or_5_out, comparator_6_eq, comparator_10_eq);
  or or_6 (or_6_out, comparator_7_eq, comparator_8_eq, comparator_9_eq);
  Pull_Resistor pull_resistor_2 (.node(controlled_buffer_1_out));
  Pull_Resistor pull_resistor_3 (.node(controlled_buffer_11_out));
  Pull_Resistor pull_resistor_4 (.node(controlled_buffer_21_out));
  Pull_Resistor pull_resistor_5 (.node(controlled_buffer_31_out));
  Pull_Resistor pull_resistor_6 (.node(controlled_buffer_41_out));
  Pull_Resistor pull_resistor_7 (.node(controlled_buffer_2_out));
  Pull_Resistor pull_resistor_8 (.node(controlled_buffer_12_out));
  Pull_Resistor pull_resistor_9 (.node(controlled_buffer_22_out));
  Pull_Resistor pull_resistor_10 (.node(controlled_buffer_32_out));
  Pull_Resistor pull_resistor_11 (.node(controlled_buffer_42_out));
  Pull_Resistor pull_resistor_12 (.node(controlled_buffer_3_out));
  Pull_Resistor pull_resistor_13 (.node(controlled_buffer_13_out));
  Pull_Resistor pull_resistor_14 (.node(controlled_buffer_23_out));
  Pull_Resistor pull_resistor_15 (.node(controlled_buffer_33_out));
  Pull_Resistor pull_resistor_16 (.node(controlled_buffer_43_out));
  Pull_Resistor pull_resistor_17 (.node(controlled_buffer_4_out));
  Pull_Resistor pull_resistor_18 (.node(controlled_buffer_14_out));
  Pull_Resistor pull_resistor_19 (.node(controlled_buffer_24_out));
  Pull_Resistor pull_resistor_20 (.node(controlled_buffer_34_out));
  Pull_Resistor pull_resistor_21 (.node(controlled_buffer_44_out));
  Pull_Resistor pull_resistor_22 (.node(controlled_buffer_5_out));
  Pull_Resistor pull_resistor_23 (.node(controlled_buffer_15_out));
  Pull_Resistor pull_resistor_24 (.node(controlled_buffer_25_out));
  Pull_Resistor pull_resistor_25 (.node(controlled_buffer_35_out));
  Pull_Resistor pull_resistor_26 (.node(controlled_buffer_45_out));
  Pull_Resistor pull_resistor_27 (.node(controlled_buffer_6_out));
  Pull_Resistor pull_resistor_28 (.node(controlled_buffer_16_out));
  Pull_Resistor pull_resistor_29 (.node(controlled_buffer_26_out));
  Pull_Resistor pull_resistor_30 (.node(controlled_buffer_36_out));
  Pull_Resistor pull_resistor_31 (.node(controlled_buffer_46_out));
  Pull_Resistor pull_resistor_32 (.node(controlled_buffer_7_out));
  Pull_Resistor pull_resistor_33 (.node(controlled_buffer_17_out));
  Pull_Resistor pull_resistor_34 (.node(controlled_buffer_27_out));
  Pull_Resistor pull_resistor_35 (.node(controlled_buffer_37_out));
  Pull_Resistor pull_resistor_36 (.node(controlled_buffer_47_out));
  Pull_Resistor pull_resistor_37 (.node(controlled_buffer_8_out));
  Pull_Resistor pull_resistor_38 (.node(controlled_buffer_18_out));
  Pull_Resistor pull_resistor_39 (.node(controlled_buffer_28_out));
  Pull_Resistor pull_resistor_40 (.node(pull_resistor_40_node));
  Pull_Resistor pull_resistor_41 (.node(controlled_buffer_48_out));
  Pull_Resistor pull_resistor_42 (.node(controlled_buffer_9_out));
  Pull_Resistor pull_resistor_43 (.node(controlled_buffer_19_out));
  Pull_Resistor pull_resistor_44 (.node(controlled_buffer_29_out));
  Pull_Resistor pull_resistor_45 (.node(controlled_buffer_39_out));
  Pull_Resistor pull_resistor_46 (.node(controlled_buffer_49_out));
  Pull_Resistor pull_resistor_47 (.node(controlled_buffer_10_out));
  Pull_Resistor pull_resistor_48 (.node(controlled_buffer_20_out));
  Pull_Resistor pull_resistor_49 (.node(controlled_buffer_30_out));
  Pull_Resistor pull_resistor_50 (.node(controlled_buffer_40_out));
  Pull_Resistor pull_resistor_51 (.node(controlled_buffer_50_out));
  assign _1 = controlled_buffer_1_out | controlled_buffer_11_out | controlled_buffer_21_out | controlled_buffer_31_out | controlled_buffer_41_out | controlled_buffer_51_out;  // OR_Gate or_7, 30 bits wide
  Pull_Resistor pull_resistor_52 (.node(controlled_buffer_51_out));
  assign _2 = controlled_buffer_2_out | controlled_buffer_12_out | controlled_buffer_22_out | controlled_buffer_32_out | controlled_buffer_42_out | controlled_buffer_52_out;  // OR_Gate or_8, 30 bits wide
  Pull_Resistor pull_resistor_53 (.node(controlled_buffer_52_out));
  assign _3 = controlled_buffer_3_out | controlled_buffer_13_out | controlled_buffer_23_out | controlled_buffer_33_out | controlled_buffer_43_out | controlled_buffer_53_out;  // OR_Gate or_9, 30 bits wide
  Pull_Resistor pull_resistor_54 (.node(controlled_buffer_53_out));
  assign _4 = controlled_buffer_4_out | controlled_buffer_14_out | controlled_buffer_24_out | controlled_buffer_34_out | controlled_buffer_44_out | controlled_buffer_54_out;  // OR_Gate or_10, 30 bits wide
  Pull_Resistor pull_resistor_55 (.node(controlled_buffer_54_out));
  assign _5 = controlled_buffer_5_out | controlled_buffer_15_out | controlled_buffer_25_out | controlled_buffer_35_out | controlled_buffer_45_out | controlled_buffer_55_out;  // OR_Gate or_11, 30 bits wide
  Pull_Resistor pull_resistor_56 (.node(controlled_buffer_55_out));
  assign _6 = controlled_buffer_6_out | controlled_buffer_16_out | controlled_buffer_26_out | controlled_buffer_36_out | controlled_buffer_46_out | controlled_buffer_56_out;  // OR_Gate or_12, 30 bits wide
  Pull_Resistor pull_resistor_57 (.node(controlled_buffer_56_out));
  assign _7 = controlled_buffer_7_out | controlled_buffer_17_out | controlled_buffer_27_out | controlled_buffer_37_out | controlled_buffer_47_out | controlled_buffer_57_out;  // OR_Gate or_13, 30 bits wide
  Pull_Resistor pull_resistor_58 (.node(controlled_buffer_57_out));
  assign _8 = controlled_buffer_8_out | controlled_buffer_18_out | controlled_buffer_28_out | pull_resistor_40_node | controlled_buffer_48_out | controlled_buffer_47_out;  // OR_Gate or_14, 30 bits wide
  Pull_Resistor pull_resistor_59 (.node(controlled_buffer_47_out));
  assign _9 = controlled_buffer_9_out | controlled_buffer_19_out | controlled_buffer_29_out | controlled_buffer_39_out | controlled_buffer_49_out | controlled_buffer_59_out;  // OR_Gate or_15, 30 bits wide
  Pull_Resistor pull_resistor_60 (.node(controlled_buffer_59_out));
  assign _10 = controlled_buffer_10_out | controlled_buffer_20_out | controlled_buffer_30_out | controlled_buffer_40_out | controlled_buffer_50_out | controlled_buffer_60_out;  // OR_Gate or_16, 30 bits wide
  Pull_Resistor pull_resistor_61 (.node(controlled_buffer_60_out));
  Adder #(.width(2)) adder_1 (.a(inBackShiftD), .b(2'b01), .out(outBackShiftD));  // open: cin, cout
  Pull_Resistor pull_resistor_62 (.node(inputBackShiftM));
  Comparator #(.width(2)) comparator_14 (.a(inBackShiftD), .b(2'b11), .eq(comparator_14_eq));  // open: gt, lt
  or or_17 (or_17_out, comparator_14_eq, comparator_15_eq);
  Comparator #(.width(2)) comparator_15 (.a(2'b01), .b(inBackShiftD), .eq(comparator_15_eq));  // open: gt, lt
  Comparator #(.width(2)) comparator_16 (.a(inBackShiftD), .b(2'b10), .eq(comparator_16_eq));  // open: gt, lt
  or or_18 (or_18_out, comparator_16_eq, comparator_17_eq);
  Comparator #(.width(2)) comparator_17 (.a(2'b00), .b(inBackShiftD), .eq(comparator_17_eq));  // open: gt, lt
  // Probe on outBackShiftD
  or or_19 (or_19_out, or_17_out, or_18_out);
  Comparator #(.width(2)) comparator_18 (.a(outBackShiftD), .b(2'b11), .eq(comparator_18_eq));  // open: gt, lt
  or or_20 (or_20_out, comparator_18_eq, comparator_19_eq);
  Comparator #(.width(2)) comparator_19 (.a(2'b01), .b(outBackShiftD), .eq(comparator_19_eq));  // open: gt, lt
  Comparator #(.width(2)) comparator_20 (.a(outBackShiftD), .b(2'b10), .eq(comparator_20_eq));  // open: gt, lt
  or or_21 (or_21_out, comparator_20_eq, comparator_21_eq);
  Comparator #(.width(2)) comparator_21 (.a(2'b00), .b(outBackShiftD), .eq(comparator_21_eq));  // open: gt, lt
  or or_22 (or_22_out, or_20_out, or_21_out);
  Pull_Resistor pull_resistor_63 (.node(or_19_out));
  assign controlled_buffer_61_out = or_19_out ? _1 : 30'bz;  // Controlled_Buffer controlled_buffer_61
  Pull_Resistor pull_resistor_64 (.node(controlled_buffer_61_out));
  Shifter #(.width(30)) shifter_1 (.in(controlled_buffer_61_out), .\dist (inputBackShiftM), .out(shifter_1_out));
  Pull_Resistor pull_resistor_65 (.node(pull_resistor_65_node));
  assign pull_resistor_65_node = or_19_out ? _2 : 30'bz;  // Controlled_Buffer controlled_buffer_62
  Shifter #(.width(30)) shifter_2 (.in(pull_resistor_65_node), .\dist (inputBackShiftM), .out(shifter_2_out));
  Pull_Resistor pull_resistor_66 (.node(pull_resistor_66_node));
  assign pull_resistor_66_node = or_19_out ? _3 : 30'bz;  // Controlled_Buffer controlled_buffer_63
  Shifter #(.width(30)) shifter_3 (.in(pull_resistor_66_node), .\dist (inputBackShiftM), .out(shifter_3_out));
  assign controlled_buffer_64_out = or_19_out ? _4 : 30'bz;  // Controlled_Buffer controlled_buffer_64
  Pull_Resistor pull_resistor_67 (.node(controlled_buffer_64_out));
  Shifter #(.width(30)) shifter_4 (.in(controlled_buffer_64_out), .\dist (inputBackShiftM), .out(shifter_4_out));
  Pull_Resistor pull_resistor_68 (.node(pull_resistor_68_node));
  assign pull_resistor_68_node = or_19_out ? _5 : 30'bz;  // Controlled_Buffer controlled_buffer_65
  Shifter #(.width(30)) shifter_5 (.in(pull_resistor_68_node), .\dist (inputBackShiftM), .out(shifter_5_out));
  Pull_Resistor pull_resistor_69 (.node(pull_resistor_69_node));
  assign pull_resistor_69_node = or_19_out ? _6 : 30'bz;  // Controlled_Buffer controlled_buffer_66
  Shifter #(.width(30)) shifter_6 (.in(pull_resistor_69_node), .\dist (inputBackShiftM), .out(shifter_6_out));
  assign controlled_buffer_67_out = or_19_out ? _7 : 30'bz;  // Controlled_Buffer controlled_buffer_67
  Pull_Resistor pull_resistor_70 (.node(controlled_buffer_67_out));
  Shifter #(.width(30)) shifter_7 (.in(controlled_buffer_67_out), .\dist (inputBackShiftM), .out(shifter_7_out));
  assign controlled_buffer_68_out = or_19_out ? _8 : 30'bz;  // Controlled_Buffer controlled_buffer_68
  Pull_Resistor pull_resistor_71 (.node(controlled_buffer_68_out));
  Shifter #(.width(30)) shifter_8 (.in(controlled_buffer_68_out), .\dist (inputBackShiftM), .out(shifter_8_out));
  Pull_Resistor pull_resistor_72 (.node(pull_resistor_72_node));
  assign pull_resistor_72_node = or_19_out ? _9 : 30'bz;  // Controlled_Buffer controlled_buffer_69
  Shifter #(.width(30)) shifter_9 (.in(pull_resistor_72_node), .\dist (inputBackShiftM), .out(shifter_9_out));
  assign controlled_buffer_70_out = or_19_out ? _10 : 30'bz;  // Controlled_Buffer controlled_buffer_70
  Pull_Resistor pull_resistor_73 (.node(controlled_buffer_70_out));
  Shifter #(.width(30)) shifter_10 (.in(controlled_buffer_70_out), .\dist (inputBackShiftM), .out(shifter_10_out));
  assign not_1_out = ~inputBackShiftM;  // NOT_Gate not_1, 5 bits wide
  Adder #(.width(5)) adder_2 (.a(5'b11110), .b(adder_3_out), .out(adder_2_out));  // open: cin, cout
  Adder #(.width(5)) adder_3 (.a(not_1_out), .b(5'b00001), .out(adder_3_out));  // open: cin, cout
  assign controlled_buffer_71_out = or_22_out ? _1 : 30'bz;  // Controlled_Buffer controlled_buffer_71
  Pull_Resistor pull_resistor_74 (.node(controlled_buffer_71_out));
  Pull_Resistor pull_resistor_75 (.node(pull_resistor_75_node));
  assign pull_resistor_75_node = or_22_out ? _2 : 30'bz;  // Controlled_Buffer controlled_buffer_72
  assign controlled_buffer_73_out = or_22_out ? _3 : 30'bz;  // Controlled_Buffer controlled_buffer_73
  Pull_Resistor pull_resistor_76 (.node(controlled_buffer_73_out));
  Pull_Resistor pull_resistor_77 (.node(pull_resistor_77_node));
  assign pull_resistor_77_node = or_22_out ? _4 : 30'bz;  // Controlled_Buffer controlled_buffer_74
  assign controlled_buffer_75_out = or_22_out ? _5 : 30'bz;  // Controlled_Buffer controlled_buffer_75
  Pull_Resistor pull_resistor_78 (.node(controlled_buffer_75_out));
  assign controlled_buffer_76_out = or_22_out ? _6 : 30'bz;  // Controlled_Buffer controlled_buffer_76
  Pull_Resistor pull_resistor_79 (.node(controlled_buffer_76_out));
  Pull_Resistor pull_resistor_80 (.node(pull_resistor_80_node));
  assign pull_resistor_80_node = or_22_out ? _7 : 30'bz;  // Controlled_Buffer controlled_buffer_77
  Pull_Resistor pull_resistor_81 (.node(pull_resistor_81_node));
  assign pull_resistor_81_node = or_22_out ? _8 : 30'bz;  // Controlled_Buffer controlled_buffer_78
  assign controlled_buffer_79_out = or_22_out ? _9 : 30'bz;  // Controlled_Buffer controlled_buffer_79
  Pull_Resistor pull_resistor_82 (.node(controlled_buffer_79_out));
  assign controlled_buffer_80_out = or_22_out ? _10 : 30'bz;  // Controlled_Buffer controlled_buffer_80
  Pull_Resistor pull_resistor_83 (.node(controlled_buffer_80_out));
  Pull_Resistor pull_resistor_84 (.node(or_22_out));
  assign or_23_out = shifter_1_out | shifter_11_out;  // OR_Gate or_23, 30 bits wide
  assign or_24_out = shifter_2_out | shifter_12_out;  // OR_Gate or_24, 30 bits wide
  assign or_25_out = shifter_3_out | shifter_13_out;  // OR_Gate or_25, 30 bits wide
  assign or_26_out = shifter_4_out | shifter_14_out;  // OR_Gate or_26, 30 bits wide
  Shifter #(.width(30), .shift("lr")) shifter_11 (
    .in(controlled_buffer_71_out), .\dist (adder_2_out), .out(shifter_11_out));
  Shifter #(.width(30), .shift("lr")) shifter_12 (
    .in(pull_resistor_75_node), .\dist (adder_2_out), .out(shifter_12_out));
  Shifter #(.width(30), .shift("lr")) shifter_13 (
    .in(controlled_buffer_73_out), .\dist (adder_2_out), .out(shifter_13_out));
  Shifter #(.width(30), .shift("lr")) shifter_14 (
    .in(pull_resistor_77_node), .\dist (adder_2_out), .out(shifter_14_out));
  Shifter #(.width(30), .shift("lr")) shifter_15 (
    .in(controlled_buffer_75_out), .\dist (adder_2_out), .out(shifter_15_out));
  Shifter #(.width(30), .shift("lr")) shifter_16 (
    .in(controlled_buffer_76_out), .\dist (adder_2_out), .out(shifter_16_out));
  Shifter #(.width(30), .shift("lr")) shifter_17 (
    .in(pull_resistor_80_node), .\dist (adder_2_out), .out(shifter_17_out));
  Shifter #(.width(30), .shift("lr")) shifter_18 (
    .in(pull_resistor_81_node), .\dist (adder_2_out), .out(shifter_18_out));
  Shifter #(.width(30), .shift("lr")) shifter_19 (
    .in(controlled_buffer_79_out), .\dist (adder_2_out), .out(shifter_19_out));
  Shifter #(.width(30), .shift("lr")) shifter_20 (
    .in(controlled_buffer_80_out), .\dist (adder_2_out), .out(shifter_20_out));
  Adder #(.width(2)) adder_4 (.a(inPlayerShiftD), .b(2'b01), .out(outPlayerShiftD));  // open: cin, cout
  Pull_Resistor pull_resistor_85 (.node(inPlayerShiftM));
  assign or_27_out = shifter_5_out | shifter_15_out;  // OR_Gate or_27, 30 bits wide
  assign or_28_out = shifter_6_out | shifter_16_out;  // OR_Gate or_28, 30 bits wide
  assign or_29_out = shifter_7_out | shifter_17_out;  // OR_Gate or_29, 30 bits wide
  assign or_30_out = shifter_8_out | shifter_18_out;  // OR_Gate or_30, 30 bits wide
  assign or_31_out = shifter_9_out | shifter_19_out;  // OR_Gate or_31, 30 bits wide
  assign or_32_out = shifter_10_out | shifter_20_out;  // OR_Gate or_32, 30 bits wide
  // Probe on adder_5_out
  Adder #(.width(5)) adder_5 (.a(inPlayerShiftM), .b(5'b00001), .out(adder_5_out));  // open: cin, cout
  Multiplexer #(.width(2), .disabled(0), .enable("false")) multiplexer_1 (
    .in0(inPlayerShiftD), .in1(outPlayerShiftD), .out(multiplexer_1_out), .sel(comparator_22_eq));
  Comparator #(.width(5), .mode("unsigned")) comparator_22 (
    .a(inPlayerShiftM), .b(5'b11110), .eq(comparator_22_eq));  // open: gt, lt
  // Probe on multiplexer_1_out
  Comparator #(.width(2)) comparator_23 (.a(2'b00), .b(multiplexer_1_out), .eq(comparator_23_eq));  // open: gt, lt
  assign controlled_buffer_81_out = inFlag ? comparator_23_eq : 1'bz;  // Controlled_Buffer controlled_buffer_81
  Adder #(.width(2)) adder_6 (.a(multiplexer_1_out), .b(2'b01), .out(adder_6_out));  // open: cin, cout
  Comparator #(.width(2)) comparator_24 (.a(2'b00), .b(adder_6_out), .eq(comparator_24_eq));  // open: gt, lt
  assign controlled_buffer_82_out = inFlag ? comparator_24_eq : 1'bz;  // Controlled_Buffer controlled_buffer_82
  Pull_Resistor pull_resistor_86 (.node(controlled_buffer_81_out));
  Pull_Resistor pull_resistor_87 (.node(pull_resistor_87_node));
  assign pull_resistor_87_node = controlled_buffer_81_out ? 30'h279 : 30'bz;  // Controlled_Buffer controlled_buffer_83
  Shifter #(.width(30)) shifter_21 (.in(pull_resistor_87_node), .\dist (adder_5_out), .out(shifter_21_out));
  assign controlled_buffer_84_out = controlled_buffer_81_out ? 30'h231 : 30'bz;  // Controlled_Buffer controlled_buffer_84
  Pull_Resistor pull_resistor_88 (.node(controlled_buffer_84_out));
  Shifter #(.width(30)) shifter_22 (.in(controlled_buffer_84_out), .\dist (adder_5_out), .out(shifter_22_out));
  Pull_Resistor pull_resistor_89 (.node(pull_resistor_89_node));
  assign pull_resistor_89_node = controlled_buffer_81_out ? 30'h279 : 30'bz;  // Controlled_Buffer controlled_buffer_85
  Shifter #(.width(30)) shifter_23 (.in(pull_resistor_89_node), .\dist (adder_5_out), .out(shifter_23_out));
  assign controlled_buffer_86_out = controlled_buffer_81_out ? 30'h3ff : 30'bz;  // Controlled_Buffer controlled_buffer_86
  Pull_Resistor pull_resistor_90 (.node(controlled_buffer_86_out));
  Shifter #(.width(30)) shifter_24 (.in(controlled_buffer_86_out), .\dist (adder_5_out), .out(shifter_24_out));
  assign controlled_buffer_87_out = controlled_buffer_81_out ? 30'hfc : 30'bz;  // Controlled_Buffer controlled_buffer_87
  Pull_Resistor pull_resistor_91 (.node(controlled_buffer_87_out));
  Shifter #(.width(30)) shifter_25 (.in(controlled_buffer_87_out), .\dist (adder_5_out), .out(shifter_25_out));
  assign controlled_buffer_88_out = controlled_buffer_81_out ? 30'hfc : 30'bz;  // Controlled_Buffer controlled_buffer_88
  Pull_Resistor pull_resistor_92 (.node(controlled_buffer_88_out));
  Shifter #(.width(30)) shifter_26 (.in(controlled_buffer_88_out), .\dist (adder_5_out), .out(shifter_26_out));
  assign controlled_buffer_89_out = controlled_buffer_81_out ? 30'h3ff : 30'bz;  // Controlled_Buffer controlled_buffer_89
  Pull_Resistor pull_resistor_93 (.node(controlled_buffer_89_out));
  Shifter #(.width(30)) shifter_27 (.in(controlled_buffer_89_out), .\dist (adder_5_out), .out(shifter_27_out));
  Pull_Resistor pull_resistor_94 (.node(pull_resistor_94_node));
  assign pull_resistor_94_node = controlled_buffer_81_out ? 30'h279 : 30'bz;  // Controlled_Buffer controlled_buffer_90
  Shifter #(.width(30)) shifter_28 (.in(pull_resistor_94_node), .\dist (adder_5_out), .out(shifter_28_out));
  Pull_Resistor pull_resistor_95 (.node(pull_resistor_95_node));
  assign pull_resistor_95_node = controlled_buffer_81_out ? 30'h231 : 30'bz;  // Controlled_Buffer controlled_buffer_91
  Shifter #(.width(30)) shifter_29 (.in(pull_resistor_95_node), .\dist (adder_5_out), .out(shifter_29_out));
  assign controlled_buffer_92_out = controlled_buffer_81_out ? 30'h201 : 30'bz;  // Controlled_Buffer controlled_buffer_92
  Pull_Resistor pull_resistor_96 (.node(controlled_buffer_92_out));
  Shifter #(.width(30)) shifter_30 (.in(controlled_buffer_92_out), .\dist (adder_5_out), .out(shifter_30_out));
  assign not_2_out = ~adder_5_out;  // NOT_Gate not_2, 5 bits wide
  Adder #(.width(5)) adder_7 (.a(5'b11110), .b(adder_8_out), .out(adder_7_out));  // open: cin, cout
  Adder #(.width(5)) adder_8 (.a(not_2_out), .b(5'b00001), .out(adder_8_out));  // open: cin, cout
  Pull_Resistor pull_resistor_97 (.node(pull_resistor_97_node));
  assign pull_resistor_97_node = controlled_buffer_82_out ? 30'h279 : 30'bz;  // Controlled_Buffer controlled_buffer_93
  assign controlled_buffer_94_out = controlled_buffer_82_out ? 30'h231 : 30'bz;  // Controlled_Buffer controlled_buffer_94
  Pull_Resistor pull_resistor_98 (.node(controlled_buffer_94_out));
  assign controlled_buffer_95_out = controlled_buffer_82_out ? 30'h279 : 30'bz;  // Controlled_Buffer controlled_buffer_95
  Pull_Resistor pull_resistor_99 (.node(controlled_buffer_95_out));
  Pull_Resistor pull_resistor_100 (.node(pull_resistor_100_node));
  assign pull_resistor_100_node = controlled_buffer_82_out ? 30'h3ff : 30'bz;  // Controlled_Buffer controlled_buffer_96
  assign controlled_buffer_97_out = controlled_buffer_82_out ? 30'hfc : 30'bz;  // Controlled_Buffer controlled_buffer_97
  Pull_Resistor pull_resistor_101 (.node(controlled_buffer_97_out));
  Pull_Resistor pull_resistor_102 (.node(pull_resistor_102_node));
  assign pull_resistor_102_node = controlled_buffer_82_out ? 30'hfc : 30'bz;  // Controlled_Buffer controlled_buffer_98
  assign controlled_buffer_99_out = controlled_buffer_82_out ? 30'h3ff : 30'bz;  // Controlled_Buffer controlled_buffer_99
  Pull_Resistor pull_resistor_103 (.node(controlled_buffer_99_out));
  assign controlled_buffer_100_out = controlled_buffer_82_out ? 30'h279 : 30'bz;  // Controlled_Buffer controlled_buffer_100
  Pull_Resistor pull_resistor_104 (.node(controlled_buffer_100_out));
  assign controlled_buffer_101_out = controlled_buffer_82_out ? 30'h231 : 30'bz;  // Controlled_Buffer controlled_buffer_101
  Pull_Resistor pull_resistor_105 (.node(controlled_buffer_101_out));
  assign controlled_buffer_102_out = controlled_buffer_82_out ? 30'h201 : 30'bz;  // Controlled_Buffer controlled_buffer_102
  Pull_Resistor pull_resistor_106 (.node(controlled_buffer_102_out));
  Pull_Resistor pull_resistor_107 (.node(controlled_buffer_82_out));
  assign toFront = shifter_21_out | shifter_31_out;  // OR_Gate or_33, 30 bits wide
  assign toFront_2 = shifter_22_out | shifter_32_out;  // OR_Gate or_34, 30 bits wide
  assign toFront_3 = shifter_23_out | shifter_33_out;  // OR_Gate or_35, 30 bits wide
  Shifter #(.width(30), .shift("lr")) shifter_31 (
    .in(pull_resistor_97_node), .\dist (adder_7_out), .out(shifter_31_out));
  Shifter #(.width(30), .shift("lr")) shifter_32 (
    .in(controlled_buffer_94_out), .\dist (adder_7_out), .out(shifter_32_out));
  Shifter #(.width(30), .shift("lr")) shifter_33 (
    .in(controlled_buffer_95_out), .\dist (adder_7_out), .out(shifter_33_out));
  Shifter #(.width(30), .shift("lr")) shifter_34 (
    .in(pull_resistor_100_node), .\dist (adder_7_out), .out(shifter_34_out));
  Shifter #(.width(30), .shift("lr")) shifter_35 (
    .in(controlled_buffer_97_out), .\dist (adder_7_out), .out(shifter_35_out));
  Shifter #(.width(30), .shift("lr")) shifter_36 (
    .in(pull_resistor_102_node), .\dist (adder_7_out), .out(shifter_36_out));
  Shifter #(.width(30), .shift("lr")) shifter_37 (
    .in(controlled_buffer_99_out), .\dist (adder_7_out), .out(shifter_37_out));
  Shifter #(.width(30), .shift("lr")) shifter_38 (
    .in(controlled_buffer_100_out), .\dist (adder_7_out), .out(shifter_38_out));
  Shifter #(.width(30), .shift("lr")) shifter_39 (
    .in(controlled_buffer_101_out), .\dist (adder_7_out), .out(shifter_39_out));
  Shifter #(.width(30), .shift("lr")) shifter_40 (
    .in(controlled_buffer_102_out), .\dist (adder_7_out), .out(shifter_40_out));
  Shifter #(.width(30), .shift("lr")) shifter_41 (.in(toFront), .\dist (5'b00001), .out(shifter_41_out));
  Shifter #(.width(30), .shift("lr")) shifter_42 (.in(toFront_2), .\dist (5'b00001), .out(shifter_42_out));
  assign toFront_4 = shifter_24_out | shifter_34_out;  // OR_Gate or_36, 30 bits wide
  assign toFront_5 = shifter_25_out | shifter_35_out;  // OR_Gate or_37, 30 bits wide
  assign toFront_6 = shifter_26_out | shifter_36_out;  // OR_Gate or_38, 30 bits wide
  assign toFront_7 = shifter_27_out | shifter_37_out;  // OR_Gate or_39, 30 bits wide
  assign toFront_8 = shifter_28_out | shifter_38_out;  // OR_Gate or_40, 30 bits wide
  assign toFront_9 = shifter_29_out | shifter_39_out;  // OR_Gate or_41, 30 bits wide
  assign toFront_10 = shifter_30_out | shifter_40_out;  // OR_Gate or_42, 30 bits wide
  assign toBackground = or_23_out | shifter_41_out;  // OR_Gate or_43, 30 bits wide
  assign toBackground_2 = or_24_out | shifter_42_out;  // OR_Gate or_44, 30 bits wide
  assign toBackground_3 = or_25_out | shifter_43_out;  // OR_Gate or_45, 30 bits wide
  assign toBackground_4 = or_26_out | shifter_44_out;  // OR_Gate or_46, 30 bits wide
  Shifter #(.width(30), .shift("lr")) shifter_43 (.in(toFront_3), .\dist (5'b00001), .out(shifter_43_out));
  Shifter #(.width(30), .shift("lr")) shifter_44 (.in(toFront_4), .\dist (5'b00001), .out(shifter_44_out));
  Shifter #(.width(30), .shift("lr")) shifter_45 (.in(toFront_5), .\dist (5'b00001), .out(shifter_45_out));
  Shifter #(.width(30), .shift("lr")) shifter_46 (.in(toFront_6), .\dist (5'b00001), .out(shifter_46_out));
  Shifter #(.width(30), .shift("lr")) shifter_47 (.in(toFront_7), .\dist (5'b00001), .out(shifter_47_out));
  Shifter #(.width(30), .shift("lr")) shifter_48 (.in(toFront_8), .\dist (5'b00001), .out(shifter_48_out));
  Shifter #(.width(30), .shift("lr")) shifter_49 (.in(toFront_9), .\dist (5'b00001), .out(shifter_49_out));
  Shifter #(.width(30), .shift("lr")) shifter_50 (.in(toFront_10), .\dist (5'b00001), .out(shifter_50_out));
  assign toBackground_5 = or_27_out | shifter_45_out;  // OR_Gate or_47, 30 bits wide
  assign toBackground_6 = or_28_out | shifter_46_out;  // OR_Gate or_48, 30 bits wide
  assign toBackground_7 = or_29_out | shifter_47_out;  // OR_Gate or_49, 30 bits wide
  assign toBackground_8 = or_30_out | shifter_48_out;  // OR_Gate or_50, 30 bits wide
  assign toBackground_9 = or_31_out | shifter_49_out;  // OR_Gate or_51, 30 bits wide
  assign toBackground_10 = or_32_out | shifter_50_out;  // OR_Gate or_52, 30 bits wide

  assign animState_2 = animState;
  assign outFlag = inFlag;
  assign outPlayerShiftM = inPlayerShiftM;
  assign outputBackShiftM = inputBackShiftM;

  // Notes on the sheet:
  //   MAKE SHIFT BY NEXT MATRICE
  //   MAKE SHIFT IN CURRENT MATRICE
  //   MAKE SHIFT BY NEXT MATRICE
  //   MAKE SHIFT IN CURRENT MATRICE
endmodule

module finishConnector (
  input  [3:0] positions,
  input  [1:0] circNumber,
  output [29:0] toBackground,
  output [29:0] toBackground_2,
  output [29:0] toBackground_3,
  output [29:0] toBackground_4,
  output [29:0] toBackground_5,
  output [29:0] toBackground_6,
  output [29:0] toBackground_7,
  output [29:0] toBackground_8,
  output [29:0] toBackground_9,
  output [29:0] toBackground_10,
  output [29:0] toBackground_11,
  output [29:0] toBackground_12,
  output [1:0] circNumber_2,
  output [3:0] positions_2
);

  wire comparator_1_eq, comparator_2_eq, comparator_3_eq, comparator_4_eq, controlled_buffer_11_out,
       controlled_buffer_12_out, controlled_buffer_13_out, or_1_out, pull_resistor_15_node,
       pull_resistor_27_node;
  wire [29:0] controlled_buffer_1_out, controlled_buffer_2_out, controlled_buffer_3_out,
       controlled_buffer_5_out, controlled_buffer_6_out, controlled_buffer_7_out, controlled_buffer_8_out,
       controlled_buffer_9_out, controlled_buffer_10_out, controlled_buffer_18_out, controlled_buffer_19_out,
       controlled_buffer_20_out, controlled_buffer_22_out, controlled_buffer_23_out,
       controlled_buffer_24_out, pull_resistor_4_node, pull_resistor_17_node, pull_resistor_18_node,
       pull_resistor_19_node, pull_resistor_23_node;

  // Probe on 30'h3fc3f0ff
  // Probe on controlled_buffer_5_out
  Comparator #(.width(2), .mode("unsigned")) comparator_1 (
    .a(circNumber), .b(2'b11), .eq(comparator_1_eq));  // open: gt, lt
  Comparator #(.width(2), .mode("unsigned")) comparator_2 (
    .a(circNumber), .b(2'b10), .eq(comparator_2_eq));  // open: gt, lt
  Comparator #(.width(2), .mode("unsigned")) comparator_3 (
    .a(circNumber), .b(2'b01), .eq(comparator_3_eq));  // open: gt, lt
  Comparator #(.width(2), .mode("unsigned")) comparator_4 (
    .a(circNumber), .b(2'b00), .eq(comparator_4_eq));  // open: gt, lt
  assign controlled_buffer_1_out = or_1_out ? 30'h3fc9e4ff : 30'bz;  // Controlled_Buffer controlled_buffer_1
  Pull_Resistor pull_resistor_1 (.node(controlled_buffer_1_out));
  assign controlled_buffer_2_out = or_1_out ? 30'h3fc8c4ff : 30'bz;  // Controlled_Buffer controlled_buffer_2
  Pull_Resistor pull_resistor_2 (.node(controlled_buffer_2_out));
  assign controlled_buffer_3_out = or_1_out ? 30'h3fc9e4ff : 30'bz;  // Controlled_Buffer controlled_buffer_3
  Pull_Resistor pull_resistor_3 (.node(controlled_buffer_3_out));
  Pull_Resistor pull_resistor_4 (.node(pull_resistor_4_node));
  assign pull_resistor_4_node = or_1_out ? 30'h3fcffcff : 30'bz;  // Controlled_Buffer controlled_buffer_4
  assign controlled_buffer_5_out = or_1_out ? 30'h3fc3f0ff : 30'bz;  // Controlled_Buffer controlled_buffer_5
  Pull_Resistor pull_resistor_5 (.node(controlled_buffer_5_out));
  assign controlled_buffer_6_out = or_1_out ? 30'h3fc3f0ff : 30'bz;  // Controlled_Buffer controlled_buffer_6
  Pull_Resistor pull_resistor_6 (.node(controlled_buffer_6_out));
  assign controlled_buffer_7_out = or_1_out ? 30'h3fcffcff : 30'bz;  // Controlled_Buffer controlled_buffer_7
  Pull_Resistor pull_resistor_7 (.node(controlled_buffer_7_out));
  assign controlled_buffer_8_out = or_1_out ? 30'h3fc9e4ff : 30'bz;  // Controlled_Buffer controlled_buffer_8
  Pull_Resistor pull_resistor_8 (.node(controlled_buffer_8_out));
  assign controlled_buffer_9_out = or_1_out ? 30'h3fc8c4ff : 30'bz;  // Controlled_Buffer controlled_buffer_9
  Pull_Resistor pull_resistor_9 (.node(controlled_buffer_9_out));
  assign controlled_buffer_10_out = or_1_out ? 30'h3fc804ff : 30'bz;  // Controlled_Buffer controlled_buffer_10
  Pull_Resistor pull_resistor_10 (.node(controlled_buffer_10_out));
  or or_1 (or_1_out, pull_resistor_15_node, controlled_buffer_13_out, controlled_buffer_12_out, controlled_buffer_11_out);
  Pull_Resistor pull_resistor_11 (.node(or_1_out));
  assign controlled_buffer_11_out = comparator_1_eq ? positions[3] : 1'bz;  // Controlled_Buffer controlled_buffer_11
  Pull_Resistor pull_resistor_12 (.node(controlled_buffer_11_out));
  assign controlled_buffer_12_out = comparator_2_eq ? positions[2] : 1'bz;  // Controlled_Buffer controlled_buffer_12
  Pull_Resistor pull_resistor_13 (.node(controlled_buffer_12_out));
  assign controlled_buffer_13_out = comparator_3_eq ? positions[1] : 1'bz;  // Controlled_Buffer controlled_buffer_13
  Pull_Resistor pull_resistor_14 (.node(controlled_buffer_13_out));
  Pull_Resistor pull_resistor_15 (.node(pull_resistor_15_node));
  assign pull_resistor_15_node = comparator_4_eq ? positions[0] : 1'bz;  // Controlled_Buffer controlled_buffer_14
  Pull_Resistor pull_resistor_16 (.node(positions));
  Pull_Resistor pull_resistor_17 (.node(pull_resistor_17_node));
  assign pull_resistor_17_node = pull_resistor_27_node ? 30'h3fc000ff : 30'bz;  // Controlled_Buffer controlled_buffer_15
  Pull_Resistor pull_resistor_18 (.node(pull_resistor_18_node));
  assign pull_resistor_18_node = pull_resistor_27_node ? 30'h3fc000ff : 30'bz;  // Controlled_Buffer controlled_buffer_16
  Pull_Resistor pull_resistor_19 (.node(pull_resistor_19_node));
  assign pull_resistor_19_node = pull_resistor_27_node ? 30'h3fc210ff : 30'bz;  // Controlled_Buffer controlled_buffer_17
  assign controlled_buffer_18_out = pull_resistor_27_node ? 30'h3fc738ff : 30'bz;  // Controlled_Buffer controlled_buffer_18
  Pull_Resistor pull_resistor_20 (.node(controlled_buffer_18_out));
  assign controlled_buffer_19_out = pull_resistor_27_node ? 30'h3fc3f0ff : 30'bz;  // Controlled_Buffer controlled_buffer_19
  Pull_Resistor pull_resistor_21 (.node(controlled_buffer_19_out));
  assign controlled_buffer_20_out = pull_resistor_27_node ? 30'h3fc3f0ff : 30'bz;  // Controlled_Buffer controlled_buffer_20
  Pull_Resistor pull_resistor_22 (.node(controlled_buffer_20_out));
  Pull_Resistor pull_resistor_23 (.node(pull_resistor_23_node));
  assign pull_resistor_23_node = pull_resistor_27_node ? 30'h3fc3f0ff : 30'bz;  // Controlled_Buffer controlled_buffer_21
  assign controlled_buffer_22_out = pull_resistor_27_node ? 30'h3fc120ff : 30'bz;  // Controlled_Buffer controlled_buffer_22
  Pull_Resistor pull_resistor_24 (.node(controlled_buffer_22_out));
  assign controlled_buffer_23_out = pull_resistor_27_node ? 30'h3fc000ff : 30'bz;  // Controlled_Buffer controlled_buffer_23
  Pull_Resistor pull_resistor_25 (.node(controlled_buffer_23_out));
  assign controlled_buffer_24_out = pull_resistor_27_node ? 30'h3fc000ff : 30'bz;  // Controlled_Buffer controlled_buffer_24
  Pull_Resistor pull_resistor_26 (.node(controlled_buffer_24_out));
  Pull_Resistor #(.pull(1)) pull_resistor_27 (.node(pull_resistor_27_node));
  assign toBackground_3 = controlled_buffer_1_out | pull_resistor_17_node;  // OR_Gate or_2, 30 bits wide
  assign toBackground_4 = controlled_buffer_2_out | pull_resistor_18_node;  // OR_Gate or_3, 30 bits wide
  assign toBackground_5 = controlled_buffer_3_out | pull_resistor_19_node;  // OR_Gate or_4, 30 bits wide
  assign toBackground_6 = pull_resistor_4_node | controlled_buffer_18_out;  // OR_Gate or_5, 30 bits wide
  assign toBackground_7 = controlled_buffer_5_out | controlled_buffer_19_out;  // OR_Gate or_6, 30 bits wide
  assign toBackground_8 = controlled_buffer_6_out | controlled_buffer_20_out;  // OR_Gate or_7, 30 bits wide
  assign toBackground_9 = controlled_buffer_7_out | pull_resistor_23_node;  // OR_Gate or_8, 30 bits wide
  assign toBackground_10 = controlled_buffer_8_out | controlled_buffer_22_out;  // OR_Gate or_9, 30 bits wide
  assign toBackground_11 = controlled_buffer_9_out | controlled_buffer_23_out;  // OR_Gate or_10, 30 bits wide
  assign toBackground_12 = controlled_buffer_10_out | controlled_buffer_24_out;  // OR_Gate or_11, 30 bits wide
  // Probe on toBackground_7
  // Probe on 30'h3fc3f0ff
  Adder #(.width(2)) adder_1 (.a(circNumber), .b(2'b01), .out(circNumber_2));  // open: cin, cout

  assign positions_2 = positions;
  assign toBackground = {30{1'b1}};
  assign toBackground_2 = 30'h3fc000ff;
endmodule

module SUVDriver (
  input  [1:0] inBackShiftD,
  input  [4:0] inputBackShiftM,
  input  [1:0] inPlayerShiftD,
  input  [4:0] inPlayerShiftM,
  input  inFlag,
  output [29:0] toBackground,
  output [29:0] toBackground_2,
  output [29:0] toBackground_3,
  output [29:0] toBackground_4,
  output [29:0] toBackground_5,
  output [1:0] outBackShiftD,
  output [29:0] toBackground_6,
  output [4:0] outputBackShiftM,
  output [29:0] toBackground_7,
  output [29:0] toBackground_8,
  output [29:0] toBackground_9,
  output [29:0] toBackground_10,
  output [1:0] outPlayerShiftD,
  output [4:0] outPlayerShiftM,
  output outFlag,
  output [29:0] toFront,
  output [29:0] toFront_2,
  output [29:0] toFront_3,
  output [29:0] toFront_4,
  output [29:0] toFront_5,
  output [29:0] toFront_6,
  output [29:0] toFront_7,
  output [29:0] toFront_8,
  output [29:0] toFront_9,
  output [29:0] toFront_10
);

  wire comparator_1_eq, comparator_2_eq, comparator_3_eq, comparator_4_eq, comparator_5_eq,
       controlled_buffer_21_out, controlled_buffer_22_out;
  wire [1:0] adder_5_out, multiplexer_1_out;
  wire [4:0] adder_3_out, adder_4_out, adder_6_out, adder_7_out, adder_8_out, not_1_out, not_2_out;
  wire [29:0] controlled_buffer_1_out, controlled_buffer_2_out, controlled_buffer_3_out,
       controlled_buffer_5_out, controlled_buffer_6_out, controlled_buffer_9_out, controlled_buffer_10_out,
       controlled_buffer_13_out, controlled_buffer_15_out, controlled_buffer_18_out,
       controlled_buffer_20_out, controlled_buffer_23_out, controlled_buffer_29_out,
       controlled_buffer_30_out, controlled_buffer_31_out, controlled_buffer_33_out,
       controlled_buffer_34_out, controlled_buffer_36_out, controlled_buffer_38_out,
       controlled_buffer_39_out, controlled_buffer_42_out, or_1_out, or_2_out, or_3_out, or_4_out, or_5_out,
       or_6_out, or_7_out, or_8_out, or_9_out, or_10_out, pull_resistor_7_node, pull_resistor_10_node,
       pull_resistor_11_node, pull_resistor_14_node, pull_resistor_15_node, pull_resistor_17_node,
       pull_resistor_19_node, pull_resistor_20_node, pull_resistor_22_node, pull_resistor_27_node,
       pull_resistor_28_node, pull_resistor_29_node, pull_resistor_30_node, pull_resistor_31_node,
       pull_resistor_35_node, pull_resistor_39_node, pull_resistor_41_node, pull_resistor_44_node,
       pull_resistor_45_node, shifter_1_out, shifter_2_out, shifter_3_out, shifter_4_out, shifter_5_out,
       shifter_6_out, shifter_7_out, shifter_8_out, shifter_9_out, shifter_10_out, shifter_11_out,
       shifter_12_out, shifter_13_out, shifter_14_out, shifter_15_out, shifter_16_out, shifter_17_out,
       shifter_18_out, shifter_19_out, shifter_20_out, shifter_21_out, shifter_22_out, shifter_23_out,
       shifter_24_out, shifter_25_out, shifter_26_out, shifter_27_out, shifter_28_out, shifter_29_out,
       shifter_30_out, shifter_31_out, shifter_32_out, shifter_33_out, shifter_34_out, shifter_35_out,
       shifter_36_out, shifter_37_out, shifter_38_out, shifter_39_out, shifter_40_out, shifter_41_out,
       shifter_42_out, shifter_43_out, shifter_44_out, shifter_45_out, shifter_46_out, shifter_47_out,
       shifter_48_out, shifter_49_out, shifter_50_out;

  Pull_Resistor pull_resistor_1 (.node(inputBackShiftM));
  Comparator #(.width(2)) comparator_1 (.a(2'b00), .b(inBackShiftD), .eq(comparator_1_eq));  // open: gt, lt
  // Probe on outBackShiftD
  Adder #(.width(2)) adder_1 (.a(inBackShiftD), .b(2'b01), .out(outBackShiftD));  // open: cin, cout
  // Probe on outBackShiftD
  // Probe on 2'b00
  Comparator #(.width(2)) comparator_2 (.a(outBackShiftD), .b(2'b00), .eq(comparator_2_eq));  // open: gt, lt
  Adder #(.width(2)) adder_2 (.a(inPlayerShiftD), .b(2'b01), .out(outPlayerShiftD));  // open: cin, cout
  Pull_Resistor pull_resistor_2 (.node(inPlayerShiftM));
  Adder #(.width(5)) adder_3 (.a(inPlayerShiftM), .b(5'b00001), .out(adder_3_out));  // open: cin, cout
  Comparator #(.width(5), .mode("unsigned")) comparator_3 (
    .a(inPlayerShiftM), .b(5'b11110), .eq(comparator_3_eq));  // open: gt, lt
  assign controlled_buffer_1_out = comparator_1_eq ? 30'h84 : 30'bz;  // Controlled_Buffer controlled_buffer_1
  Pull_Resistor pull_resistor_3 (.node(controlled_buffer_1_out));
  Pull_Resistor pull_resistor_4 (.node(comparator_1_eq));
  assign controlled_buffer_2_out = comparator_1_eq ? 30'h1ce : 30'bz;  // Controlled_Buffer controlled_buffer_2
  Pull_Resistor pull_resistor_5 (.node(controlled_buffer_2_out));
  assign controlled_buffer_3_out = comparator_1_eq ? 30'h1fe : 30'bz;  // Controlled_Buffer controlled_buffer_3
  Pull_Resistor pull_resistor_6 (.node(controlled_buffer_3_out));
  Pull_Resistor pull_resistor_7 (.node(pull_resistor_7_node));
  assign pull_resistor_7_node = comparator_1_eq ? 30'h343 : 30'bz;  // Controlled_Buffer controlled_buffer_4
  assign controlled_buffer_5_out = comparator_1_eq ? 30'h243 : 30'bz;  // Controlled_Buffer controlled_buffer_5
  Pull_Resistor pull_resistor_8 (.node(controlled_buffer_5_out));
  assign controlled_buffer_6_out = comparator_1_eq ? 30'h243 : 30'bz;  // Controlled_Buffer controlled_buffer_6
  Pull_Resistor pull_resistor_9 (.node(controlled_buffer_6_out));
  Pull_Resistor pull_resistor_10 (.node(pull_resistor_10_node));
  assign pull_resistor_10_node = comparator_1_eq ? 30'h343 : 30'bz;  // Controlled_Buffer controlled_buffer_7
  Pull_Resistor pull_resistor_11 (.node(pull_resistor_11_node));
  assign pull_resistor_11_node = comparator_1_eq ? 30'h1fe : 30'bz;  // Controlled_Buffer controlled_buffer_8
  assign controlled_buffer_9_out = comparator_1_eq ? 30'h1ce : 30'bz;  // Controlled_Buffer controlled_buffer_9
  Pull_Resistor pull_resistor_12 (.node(controlled_buffer_9_out));
  assign controlled_buffer_10_out = comparator_1_eq ? 30'h84 : 30'bz;  // Controlled_Buffer controlled_buffer_10
  Pull_Resistor pull_resistor_13 (.node(controlled_buffer_10_out));
  assign not_1_out = ~inputBackShiftM;  // NOT_Gate not_1, 5 bits wide
  Multiplexer #(.width(2), .disabled(0), .enable("false")) multiplexer_1 (
    .in0(inPlayerShiftD), .in1(outPlayerShiftD), .out(multiplexer_1_out), .sel(comparator_3_eq));
  Shifter #(.width(30)) shifter_1 (.in(controlled_buffer_1_out), .\dist (inputBackShiftM), .out(shifter_1_out));
  Shifter #(.width(30)) shifter_2 (.in(controlled_buffer_2_out), .\dist (inputBackShiftM), .out(shifter_2_out));
  Shifter #(.width(30)) shifter_3 (.in(controlled_buffer_3_out), .\dist (inputBackShiftM), .out(shifter_3_out));
  Shifter #(.width(30)) shifter_4 (.in(pull_resistor_7_node), .\dist (inputBackShiftM), .out(shifter_4_out));
  Shifter #(.width(30)) shifter_5 (.in(controlled_buffer_5_out), .\dist (inputBackShiftM), .out(shifter_5_out));
  Shifter #(.width(30)) shifter_6 (.in(controlled_buffer_6_out), .\dist (inputBackShiftM), .out(shifter_6_out));
  Shifter #(.width(30)) shifter_7 (.in(pull_resistor_10_node), .\dist (inputBackShiftM), .out(shifter_7_out));
  Shifter #(.width(30)) shifter_8 (.in(pull_resistor_11_node), .\dist (inputBackShiftM), .out(shifter_8_out));
  Shifter #(.width(30)) shifter_9 (.in(controlled_buffer_9_out), .\dist (inputBackShiftM), .out(shifter_9_out));
  Shifter #(.width(30)) shifter_10 (.in(controlled_buffer_10_out), .\dist (inputBackShiftM), .out(shifter_10_out));
  Adder #(.width(5)) adder_4 (.a(not_1_out), .b(5'b00001), .out(adder_4_out));  // open: cin, cout
  Pull_Resistor pull_resistor_14 (.node(pull_resistor_14_node));
  assign pull_resistor_14_node = comparator_2_eq ? 30'h84 : 30'bz;  // Controlled_Buffer controlled_buffer_11
  Pull_Resistor pull_resistor_15 (.node(pull_resistor_15_node));
  assign pull_resistor_15_node = comparator_2_eq ? 30'h1ce : 30'bz;  // Controlled_Buffer controlled_buffer_12
  assign controlled_buffer_13_out = comparator_2_eq ? 30'h1fe : 30'bz;  // Controlled_Buffer controlled_buffer_13
  Pull_Resistor pull_resistor_16 (.node(controlled_buffer_13_out));
  Pull_Resistor pull_resistor_17 (.node(pull_resistor_17_node));
  assign pull_resistor_17_node = comparator_2_eq ? 30'h343 : 30'bz;  // Controlled_Buffer controlled_buffer_14
  assign controlled_buffer_15_out = comparator_2_eq ? 30'h243 : 30'bz;  // Controlled_Buffer controlled_buffer_15
  Pull_Resistor pull_resistor_18 (.node(controlled_buffer_15_out));
  Pull_Resistor pull_resistor_19 (.node(pull_resistor_19_node));
  assign pull_resistor_19_node = comparator_2_eq ? 30'h243 : 30'bz;  // Controlled_Buffer controlled_buffer_16
  Pull_Resistor pull_resistor_20 (.node(pull_resistor_20_node));
  assign pull_resistor_20_node = comparator_2_eq ? 30'h343 : 30'bz;  // Controlled_Buffer controlled_buffer_17
  assign controlled_buffer_18_out = comparator_2_eq ? 30'h1fe : 30'bz;  // Controlled_Buffer controlled_buffer_18
  Pull_Resistor pull_resistor_21 (.node(controlled_buffer_18_out));
  Pull_Resistor pull_resistor_22 (.node(pull_resistor_22_node));
  assign pull_resistor_22_node = comparator_2_eq ? 30'h1ce : 30'bz;  // Controlled_Buffer controlled_buffer_19
  assign controlled_buffer_20_out = comparator_2_eq ? 30'h84 : 30'bz;  // Controlled_Buffer controlled_buffer_20
  Pull_Resistor pull_resistor_23 (.node(controlled_buffer_20_out));
  Pull_Resistor pull_resistor_24 (.node(comparator_2_eq));
  assign controlled_buffer_21_out = inFlag ? comparator_4_eq : 1'bz;  // Controlled_Buffer controlled_buffer_21
  Comparator #(.width(2)) comparator_4 (.a(2'b00), .b(multiplexer_1_out), .eq(comparator_4_eq));  // open: gt, lt
  Comparator #(.width(2)) comparator_5 (.a(2'b00), .b(adder_5_out), .eq(comparator_5_eq));  // open: gt, lt
  Adder #(.width(2)) adder_5 (.a(multiplexer_1_out), .b(2'b01), .out(adder_5_out));  // open: cin, cout
  assign or_1_out = shifter_1_out | shifter_11_out;  // OR_Gate or_1, 30 bits wide
  Adder #(.width(5)) adder_6 (.a(5'b11110), .b(adder_4_out), .out(adder_6_out));  // open: cin, cout
  Shifter #(.width(30), .shift("lr")) shifter_11 (
    .in(pull_resistor_14_node), .\dist (adder_6_out), .out(shifter_11_out));
  Shifter #(.width(30), .shift("lr")) shifter_12 (
    .in(pull_resistor_15_node), .\dist (adder_6_out), .out(shifter_12_out));
  Shifter #(.width(30), .shift("lr")) shifter_13 (
    .in(controlled_buffer_13_out), .\dist (adder_6_out), .out(shifter_13_out));
  Shifter #(.width(30), .shift("lr")) shifter_14 (
    .in(pull_resistor_17_node), .\dist (adder_6_out), .out(shifter_14_out));
  Shifter #(.width(30), .shift("lr")) shifter_15 (
    .in(controlled_buffer_15_out), .\dist (adder_6_out), .out(shifter_15_out));
  Shifter #(.width(30), .shift("lr")) shifter_16 (
    .in(pull_resistor_19_node), .\dist (adder_6_out), .out(shifter_16_out));
  Shifter #(.width(30), .shift("lr")) shifter_17 (
    .in(pull_resistor_20_node), .\dist (adder_6_out), .out(shifter_17_out));
  Shifter #(.width(30), .shift("lr")) shifter_18 (
    .in(controlled_buffer_18_out), .\dist (adder_6_out), .out(shifter_18_out));
  Shifter #(.width(30), .shift("lr")) shifter_19 (
    .in(pull_resistor_22_node), .\dist (adder_6_out), .out(shifter_19_out));
  Shifter #(.width(30), .shift("lr")) shifter_20 (
    .in(controlled_buffer_20_out), .\dist (adder_6_out), .out(shifter_20_out));
  assign or_2_out = shifter_2_out | shifter_12_out;  // OR_Gate or_2, 30 bits wide
  assign or_3_out = shifter_3_out | shifter_13_out;  // OR_Gate or_3, 30 bits wide
  assign or_4_out = shifter_4_out | shifter_14_out;  // OR_Gate or_4, 30 bits wide
  assign or_5_out = shifter_5_out | shifter_15_out;  // OR_Gate or_5, 30 bits wide
  assign or_6_out = shifter_6_out | shifter_16_out;  // OR_Gate or_6, 30 bits wide
  assign or_7_out = shifter_7_out | shifter_17_out;  // OR_Gate or_7, 30 bits wide
  assign or_8_out = shifter_8_out | shifter_18_out;  // OR_Gate or_8, 30 bits wide
  assign or_9_out = shifter_9_out | shifter_19_out;  // OR_Gate or_9, 30 bits wide
  assign controlled_buffer_22_out = inFlag ? comparator_5_eq : 1'bz;  // Controlled_Buffer controlled_buffer_22
  assign or_10_out = shifter_10_out | shifter_20_out;  // OR_Gate or_10, 30 bits wide
  Pull_Resistor pull_resistor_25 (.node(controlled_buffer_21_out));
  assign controlled_buffer_23_out = controlled_buffer_21_out ? 30'h279 : 30'bz;  // Controlled_Buffer controlled_buffer_23
  Pull_Resistor pull_resistor_26 (.node(controlled_buffer_23_out));
  Pull_Resistor pull_resistor_27 (.node(pull_resistor_27_node));
  assign pull_resistor_27_node = controlled_buffer_21_out ? 30'h231 : 30'bz;  // Controlled_Buffer controlled_buffer_24
  Pull_Resistor pull_resistor_28 (.node(pull_resistor_28_node));
  assign pull_resistor_28_node = controlled_buffer_21_out ? 30'h279 : 30'bz;  // Controlled_Buffer controlled_buffer_25
  Pull_Resistor pull_resistor_29 (.node(pull_resistor_29_node));
  assign pull_resistor_29_node = controlled_buffer_21_out ? 30'h3ff : 30'bz;  // Controlled_Buffer controlled_buffer_26
  Pull_Resistor pull_resistor_30 (.node(pull_resistor_30_node));
  assign pull_resistor_30_node = controlled_buffer_21_out ? 30'hfc : 30'bz;  // Controlled_Buffer controlled_buffer_27
  Pull_Resistor pull_resistor_31 (.node(pull_resistor_31_node));
  assign pull_resistor_31_node = controlled_buffer_21_out ? 30'hfc : 30'bz;  // Controlled_Buffer controlled_buffer_28
  assign controlled_buffer_29_out = controlled_buffer_21_out ? 30'h3ff : 30'bz;  // Controlled_Buffer controlled_buffer_29
  Pull_Resistor pull_resistor_32 (.node(controlled_buffer_29_out));
  assign controlled_buffer_30_out = controlled_buffer_21_out ? 30'h279 : 30'bz;  // Controlled_Buffer controlled_buffer_30
  Pull_Resistor pull_resistor_33 (.node(controlled_buffer_30_out));
  assign controlled_buffer_31_out = controlled_buffer_21_out ? 30'h231 : 30'bz;  // Controlled_Buffer controlled_buffer_31
  Pull_Resistor pull_resistor_34 (.node(controlled_buffer_31_out));
  Pull_Resistor pull_resistor_35 (.node(pull_resistor_35_node));
  assign pull_resistor_35_node = controlled_buffer_21_out ? 30'h201 : 30'bz;  // Controlled_Buffer controlled_buffer_32
  Shifter #(.width(30)) shifter_21 (.in(controlled_buffer_23_out), .\dist (adder_3_out), .out(shifter_21_out));
  Shifter #(.width(30)) shifter_22 (.in(pull_resistor_27_node), .\dist (adder_3_out), .out(shifter_22_out));
  Shifter #(.width(30)) shifter_23 (.in(pull_resistor_28_node), .\dist (adder_3_out), .out(shifter_23_out));
  Shifter #(.width(30)) shifter_24 (.in(pull_resistor_29_node), .\dist (adder_3_out), .out(shifter_24_out));
  Shifter #(.width(30)) shifter_25 (.in(pull_resistor_30_node), .\dist (adder_3_out), .out(shifter_25_out));
  Shifter #(.width(30)) shifter_26 (.in(pull_resistor_31_node), .\dist (adder_3_out), .out(shifter_26_out));
  Shifter #(.width(30)) shifter_27 (.in(controlled_buffer_29_out), .\dist (adder_3_out), .out(shifter_27_out));
  Shifter #(.width(30)) shifter_28 (.in(controlled_buffer_30_out), .\dist (adder_3_out), .out(shifter_28_out));
  Shifter #(.width(30)) shifter_29 (.in(controlled_buffer_31_out), .\dist (adder_3_out), .out(shifter_29_out));
  Shifter #(.width(30)) shifter_30 (.in(pull_resistor_35_node), .\dist (adder_3_out), .out(shifter_30_out));
  assign not_2_out = ~adder_3_out;  // NOT_Gate not_2, 5 bits wide
  Adder #(.width(5)) adder_7 (.a(not_2_out), .b(5'b00001), .out(adder_7_out));  // open: cin, cout
  Pull_Resistor pull_resistor_36 (.node(controlled_buffer_22_out));
  Adder #(.width(5)) adder_8 (.a(5'b11110), .b(adder_7_out), .out(adder_8_out));  // open: cin, cout
  assign controlled_buffer_33_out = controlled_buffer_22_out ? 30'h279 : 30'bz;  // Controlled_Buffer controlled_buffer_33
  Pull_Resistor pull_resistor_37 (.node(controlled_buffer_33_out));
  Shifter #(.width(30), .shift("lr")) shifter_31 (
    .in(controlled_buffer_33_out), .\dist (adder_8_out), .out(shifter_31_out));
  assign controlled_buffer_34_out = controlled_buffer_22_out ? 30'h231 : 30'bz;  // Controlled_Buffer controlled_buffer_34
  Pull_Resistor pull_resistor_38 (.node(controlled_buffer_34_out));
  Shifter #(.width(30), .shift("lr")) shifter_32 (
    .in(controlled_buffer_34_out), .\dist (adder_8_out), .out(shifter_32_out));
  Pull_Resistor pull_resistor_39 (.node(pull_resistor_39_node));
  assign pull_resistor_39_node = controlled_buffer_22_out ? 30'h279 : 30'bz;  // Controlled_Buffer controlled_buffer_35
  Shifter #(.width(30), .shift("lr")) shifter_33 (
    .in(pull_resistor_39_node), .\dist (adder_8_out), .out(shifter_33_out));
  assign controlled_buffer_36_out = controlled_buffer_22_out ? 30'h3ff : 30'bz;  // Controlled_Buffer controlled_buffer_36
  Pull_Resistor pull_resistor_40 (.node(controlled_buffer_36_out));
  Shifter #(.width(30), .shift("lr")) shifter_34 (
    .in(controlled_buffer_36_out), .\dist (adder_8_out), .out(shifter_34_out));
  Pull_Resistor pull_resistor_41 (.node(pull_resistor_41_node));
  assign pull_resistor_41_node = controlled_buffer_22_out ? 30'hfc : 30'bz;  // Controlled_Buffer controlled_buffer_37
  Shifter #(.width(30), .shift("lr")) shifter_35 (
    .in(pull_resistor_41_node), .\dist (adder_8_out), .out(shifter_35_out));
  assign controlled_buffer_38_out = controlled_buffer_22_out ? 30'hfc : 30'bz;  // Controlled_Buffer controlled_buffer_38
  Pull_Resistor pull_resistor_42 (.node(controlled_buffer_38_out));
  Shifter #(.width(30), .shift("lr")) shifter_36 (
    .in(controlled_buffer_38_out), .\dist (adder_8_out), .out(shifter_36_out));
  assign controlled_buffer_39_out = controlled_buffer_22_out ? 30'h3ff : 30'bz;  // Controlled_Buffer controlled_buffer_39
  Pull_Resistor pull_resistor_43 (.node(controlled_buffer_39_out));
  Shifter #(.width(30), .shift("lr")) shifter_37 (
    .in(controlled_buffer_39_out), .\dist (adder_8_out), .out(shifter_37_out));
  Pull_Resistor pull_resistor_44 (.node(pull_resistor_44_node));
  assign pull_resistor_44_node = controlled_buffer_22_out ? 30'h279 : 30'bz;  // Controlled_Buffer controlled_buffer_40
  Shifter #(.width(30), .shift("lr")) shifter_38 (
    .in(pull_resistor_44_node), .\dist (adder_8_out), .out(shifter_38_out));
  Pull_Resistor pull_resistor_45 (.node(pull_resistor_45_node));
  assign pull_resistor_45_node = controlled_buffer_22_out ? 30'h231 : 30'bz;  // Controlled_Buffer controlled_buffer_41
  Shifter #(.width(30), .shift("lr")) shifter_39 (
    .in(pull_resistor_45_node), .\dist (adder_8_out), .out(shifter_39_out));
  assign controlled_buffer_42_out = controlled_buffer_22_out ? 30'h201 : 30'bz;  // Controlled_Buffer controlled_buffer_42
  Pull_Resistor pull_resistor_46 (.node(controlled_buffer_42_out));
  Shifter #(.width(30), .shift("lr")) shifter_40 (
    .in(controlled_buffer_42_out), .\dist (adder_8_out), .out(shifter_40_out));
  assign toFront = shifter_21_out | shifter_31_out;  // OR_Gate or_11, 30 bits wide
  assign toFront_2 = shifter_22_out | shifter_32_out;  // OR_Gate or_12, 30 bits wide
  assign toFront_3 = shifter_23_out | shifter_33_out;  // OR_Gate or_13, 30 bits wide
  assign toFront_4 = shifter_24_out | shifter_34_out;  // OR_Gate or_14, 30 bits wide
  assign toFront_5 = shifter_25_out | shifter_35_out;  // OR_Gate or_15, 30 bits wide
  assign toFront_6 = shifter_26_out | shifter_36_out;  // OR_Gate or_16, 30 bits wide
  assign toFront_7 = shifter_27_out | shifter_37_out;  // OR_Gate or_17, 30 bits wide
  assign toFront_8 = shifter_28_out | shifter_38_out;  // OR_Gate or_18, 30 bits wide
  assign toBackground = or_1_out | shifter_41_out;  // OR_Gate or_19, 30 bits wide
  Shifter #(.width(30), .shift("lr")) shifter_41 (.in(toFront), .\dist (5'b00001), .out(shifter_41_out));
  Shifter #(.width(30), .shift("lr")) shifter_42 (.in(toFront_2), .\dist (5'b00001), .out(shifter_42_out));
  Shifter #(.width(30), .shift("lr")) shifter_43 (.in(toFront_3), .\dist (5'b00001), .out(shifter_43_out));
  Shifter #(.width(30), .shift("lr")) shifter_44 (.in(toFront_4), .\dist (5'b00001), .out(shifter_44_out));
  Shifter #(.width(30), .shift("lr")) shifter_45 (.in(toFront_5), .\dist (5'b00001), .out(shifter_45_out));
  Shifter #(.width(30), .shift("lr")) shifter_46 (.in(toFront_6), .\dist (5'b00001), .out(shifter_46_out));
  Shifter #(.width(30), .shift("lr")) shifter_47 (.in(toFront_7), .\dist (5'b00001), .out(shifter_47_out));
  assign toFront_9 = shifter_29_out | shifter_39_out;  // OR_Gate or_20, 30 bits wide
  assign toFront_10 = shifter_30_out | shifter_40_out;  // OR_Gate or_21, 30 bits wide
  assign toBackground_2 = or_2_out | shifter_42_out;  // OR_Gate or_22, 30 bits wide
  assign toBackground_3 = or_3_out | shifter_43_out;  // OR_Gate or_23, 30 bits wide
  assign toBackground_4 = or_4_out | shifter_44_out;  // OR_Gate or_24, 30 bits wide
  assign toBackground_5 = or_5_out | shifter_45_out;  // OR_Gate or_25, 30 bits wide
  assign toBackground_6 = or_6_out | shifter_46_out;  // OR_Gate or_26, 30 bits wide
  assign toBackground_7 = or_7_out | shifter_47_out;  // OR_Gate or_27, 30 bits wide
  assign toBackground_8 = or_8_out | shifter_48_out;  // OR_Gate or_28, 30 bits wide
  assign toBackground_9 = or_9_out | shifter_49_out;  // OR_Gate or_29, 30 bits wide
  Shifter #(.width(30), .shift("lr")) shifter_48 (.in(toFront_8), .\dist (5'b00001), .out(shifter_48_out));
  Shifter #(.width(30), .shift("lr")) shifter_49 (.in(toFront_9), .\dist (5'b00001), .out(shifter_49_out));
  Shifter #(.width(30), .shift("lr")) shifter_50 (.in(toFront_10), .\dist (5'b00001), .out(shifter_50_out));
  assign toBackground_10 = or_10_out | shifter_50_out;  // OR_Gate or_30, 30 bits wide

  assign outFlag = inFlag;
  assign outPlayerShiftM = inPlayerShiftM;
  assign outputBackShiftM = inputBackShiftM;

  // Notes on the sheet:
  //   MAKE SHIFT BY NEXT MATRICE
  //   MAKE SHIFT IN CURRENT MATRICE
  //   MAKE SHIFT IN CURRENT MATRICE
  //   MAKE SHIFT BY NEXT MATRICE
endmodule
module bolidDriver (
  input  [1:0] inBackShiftD,
  input  [4:0] inputBackShiftM,
  input  [1:0] inPlayerShiftD,
  input  [4:0] inPlayerShiftM,
  input  inFlag,
  output [29:0] toBackground,
  output [29:0] toBackground_2,
  output [29:0] toBackground_3,
  output [29:0] toBackground_4,
  output [29:0] toBackground_5,
  output [1:0] outBackShiftD,
  output [29:0] toBackground_6,
  output [4:0] outputBackShiftM,
  output [29:0] toBackground_7,
  output [29:0] toBackground_8,
  output [29:0] toBackground_9,
  output [29:0] toBackground_10,
  output [1:0] outPlayerShiftD,
  output [4:0] outPlayerShiftM,
  output outFlag,
  output [29:0] toFront,
  output [29:0] toFront_2,
  output [29:0] toFront_3,
  output [29:0] toFront_4,
  output [29:0] toFront_5,
  output [29:0] toFront_6,
  output [29:0] toFront_7,
  output [29:0] toFront_8,
  output [29:0] toFront_9,
  output [29:0] toFront_10
);

  wire comparator_1_eq, comparator_2_eq, comparator_3_eq, comparator_4_eq, comparator_5_eq,
       controlled_buffer_21_out, controlled_buffer_22_out;
  wire [1:0] adder_5_out, multiplexer_1_out;
  wire [4:0] adder_3_out, adder_4_out, adder_6_out, adder_7_out, adder_8_out, not_1_out, not_2_out;
  wire [29:0] controlled_buffer_3_out, controlled_buffer_4_out, controlled_buffer_8_out,
       controlled_buffer_10_out, controlled_buffer_11_out, controlled_buffer_12_out,
       controlled_buffer_13_out, controlled_buffer_15_out, controlled_buffer_16_out,
       controlled_buffer_17_out, controlled_buffer_23_out, controlled_buffer_24_out,
       controlled_buffer_26_out, controlled_buffer_28_out, controlled_buffer_29_out,
       controlled_buffer_33_out, controlled_buffer_34_out, controlled_buffer_35_out,
       controlled_buffer_39_out, controlled_buffer_40_out, or_1_out, or_2_out, or_3_out, or_4_out, or_5_out,
       or_6_out, or_7_out, or_8_out, or_9_out, or_10_out, pull_resistor_4_node, pull_resistor_5_node,
       pull_resistor_8_node, pull_resistor_9_node, pull_resistor_10_node, pull_resistor_12_node,
       pull_resistor_17_node, pull_resistor_21_node, pull_resistor_22_node, pull_resistor_23_node,
       pull_resistor_28_node, pull_resistor_30_node, pull_resistor_33_node, pull_resistor_34_node,
       pull_resistor_35_node, pull_resistor_40_node, pull_resistor_41_node, pull_resistor_42_node,
       pull_resistor_45_node, pull_resistor_46_node, shifter_1_out, shifter_2_out, shifter_3_out,
       shifter_4_out, shifter_5_out, shifter_6_out, shifter_7_out, shifter_8_out, shifter_9_out,
       shifter_10_out, shifter_11_out, shifter_12_out, shifter_13_out, shifter_14_out, shifter_15_out,
       shifter_16_out, shifter_17_out, shifter_18_out, shifter_19_out, shifter_20_out, shifter_21_out,
       shifter_22_out, shifter_23_out, shifter_24_out, shifter_25_out, shifter_26_out, shifter_27_out,
       shifter_28_out, shifter_29_out, shifter_30_out, shifter_31_out, shifter_32_out, shifter_33_out,
       shifter_34_out, shifter_35_out, shifter_36_out, shifter_37_out, shifter_38_out, shifter_39_out,
       shifter_40_out, shifter_41_out, shifter_42_out, shifter_43_out, shifter_44_out, shifter_45_out,
       shifter_46_out, shifter_47_out, shifter_48_out, shifter_49_out, shifter_50_out;

  Pull_Resistor pull_resistor_1 (.node(inputBackShiftM));
  Comparator #(.width(2)) comparator_1 (.a(2'b00), .b(inBackShiftD), .eq(comparator_1_eq));  // open: gt, lt
  // Probe on outBackShiftD
  Adder #(.width(2)) adder_1 (.a(inBackShiftD), .b(2'b01), .out(outBackShiftD));  // open: cin, cout
  // Probe on 2'b00
  // Probe on outBackShiftD
  Comparator #(.width(2)) comparator_2 (.a(outBackShiftD), .b(2'b00), .eq(comparator_2_eq));  // open: gt, lt
  Adder #(.width(2)) adder_2 (.a(inPlayerShiftD), .b(2'b01), .out(outPlayerShiftD));  // open: cin, cout
  Pull_Resistor pull_resistor_2 (.node(inPlayerShiftM));
  Adder #(.width(5)) adder_3 (.a(inPlayerShiftM), .b(5'b00001), .out(adder_3_out));  // open: cin, cout
  Comparator #(.width(5), .mode("unsigned")) comparator_3 (
    .a(inPlayerShiftM), .b(5'b11110), .eq(comparator_3_eq));  // open: gt, lt
  Pull_Resistor pull_resistor_3 (.node(comparator_1_eq));
  Pull_Resistor pull_resistor_4 (.node(pull_resistor_4_node));
  assign pull_resistor_4_node = comparator_1_eq ? 30'h78000 : 30'bz;  // Controlled_Buffer controlled_buffer_1
  Pull_Resistor pull_resistor_5 (.node(pull_resistor_5_node));
  assign pull_resistor_5_node = comparator_1_eq ? 30'h1c078000 : 30'bz;  // Controlled_Buffer controlled_buffer_2
  assign controlled_buffer_3_out = comparator_1_eq ? 30'h287fa000 : 30'bz;  // Controlled_Buffer controlled_buffer_3
  Pull_Resistor pull_resistor_6 (.node(controlled_buffer_3_out));
  assign controlled_buffer_4_out = comparator_1_eq ? 30'h3fffe000 : 30'bz;  // Controlled_Buffer controlled_buffer_4
  Pull_Resistor pull_resistor_7 (.node(controlled_buffer_4_out));
  Pull_Resistor pull_resistor_8 (.node(pull_resistor_8_node));
  assign pull_resistor_8_node = comparator_1_eq ? 30'h3f0fe000 : 30'bz;  // Controlled_Buffer controlled_buffer_5
  Pull_Resistor pull_resistor_9 (.node(pull_resistor_9_node));
  assign pull_resistor_9_node = comparator_1_eq ? 30'h3f0fe000 : 30'bz;  // Controlled_Buffer controlled_buffer_6
  Pull_Resistor pull_resistor_10 (.node(pull_resistor_10_node));
  assign pull_resistor_10_node = comparator_1_eq ? 30'h3fffe000 : 30'bz;  // Controlled_Buffer controlled_buffer_7
  assign controlled_buffer_8_out = comparator_1_eq ? 30'h287fa000 : 30'bz;  // Controlled_Buffer controlled_buffer_8
  Pull_Resistor pull_resistor_11 (.node(controlled_buffer_8_out));
  Pull_Resistor pull_resistor_12 (.node(pull_resistor_12_node));
  assign pull_resistor_12_node = comparator_1_eq ? 30'h1c078000 : 30'bz;  // Controlled_Buffer controlled_buffer_9
  assign controlled_buffer_10_out = comparator_1_eq ? 30'h78000 : 30'bz;  // Controlled_Buffer controlled_buffer_10
  Pull_Resistor pull_resistor_13 (.node(controlled_buffer_10_out));
  assign not_1_out = ~inputBackShiftM;  // NOT_Gate not_1, 5 bits wide
  Multiplexer #(.width(2), .disabled(0), .enable("false")) multiplexer_1 (
    .in0(inPlayerShiftD), .in1(outPlayerShiftD), .out(multiplexer_1_out), .sel(comparator_3_eq));
  Shifter #(.width(30)) shifter_1 (.in(pull_resistor_4_node), .\dist (inputBackShiftM), .out(shifter_1_out));
  Shifter #(.width(30)) shifter_2 (.in(pull_resistor_5_node), .\dist (inputBackShiftM), .out(shifter_2_out));
  Shifter #(.width(30)) shifter_3 (.in(controlled_buffer_3_out), .\dist (inputBackShiftM), .out(shifter_3_out));
  Shifter #(.width(30)) shifter_4 (.in(controlled_buffer_4_out), .\dist (inputBackShiftM), .out(shifter_4_out));
  Shifter #(.width(30)) shifter_5 (.in(pull_resistor_8_node), .\dist (inputBackShiftM), .out(shifter_5_out));
  Shifter #(.width(30)) shifter_6 (.in(pull_resistor_9_node), .\dist (inputBackShiftM), .out(shifter_6_out));
  Shifter #(.width(30)) shifter_7 (.in(pull_resistor_10_node), .\dist (inputBackShiftM), .out(shifter_7_out));
  Shifter #(.width(30)) shifter_8 (.in(controlled_buffer_8_out), .\dist (inputBackShiftM), .out(shifter_8_out));
  Shifter #(.width(30)) shifter_9 (.in(pull_resistor_12_node), .\dist (inputBackShiftM), .out(shifter_9_out));
  Shifter #(.width(30)) shifter_10 (.in(controlled_buffer_10_out), .\dist (inputBackShiftM), .out(shifter_10_out));
  Adder #(.width(5)) adder_4 (.a(not_1_out), .b(5'b00001), .out(adder_4_out));  // open: cin, cout
  assign controlled_buffer_11_out = comparator_2_eq ? 30'h78000 : 30'bz;  // Controlled_Buffer controlled_buffer_11
  Pull_Resistor pull_resistor_14 (.node(controlled_buffer_11_out));
  assign controlled_buffer_12_out = comparator_2_eq ? 30'h1c078000 : 30'bz;  // Controlled_Buffer controlled_buffer_12
  Pull_Resistor pull_resistor_15 (.node(controlled_buffer_12_out));
  assign controlled_buffer_13_out = comparator_2_eq ? 30'h287fa000 : 30'bz;  // Controlled_Buffer controlled_buffer_13
  Pull_Resistor pull_resistor_16 (.node(controlled_buffer_13_out));
  Pull_Resistor pull_resistor_17 (.node(pull_resistor_17_node));
  assign pull_resistor_17_node = comparator_2_eq ? 30'h3fffe000 : 30'bz;  // Controlled_Buffer controlled_buffer_14
  assign controlled_buffer_15_out = comparator_2_eq ? 30'h3f0fe000 : 30'bz;  // Controlled_Buffer controlled_buffer_15
  Pull_Resistor pull_resistor_18 (.node(controlled_buffer_15_out));
  assign controlled_buffer_16_out = comparator_2_eq ? 30'h3f0fe000 : 30'bz;  // Controlled_Buffer controlled_buffer_16
  Pull_Resistor pull_resistor_19 (.node(controlled_buffer_16_out));
  assign controlled_buffer_17_out = comparator_2_eq ? 30'h3fffe000 : 30'bz;  // Controlled_Buffer controlled_buffer_17
  Pull_Resistor pull_resistor_20 (.node(controlled_buffer_17_out));
  Pull_Resistor pull_resistor_21 (.node(pull_resistor_21_node));
  assign pull_resistor_21_node = comparator_2_eq ? 30'h287fa000 : 30'bz;  // Controlled_Buffer controlled_buffer_18
  Pull_Resistor pull_resistor_22 (.node(pull_resistor_22_node));
  assign pull_resistor_22_node = comparator_2_eq ? 30'h1c078000 : 30'bz;  // Controlled_Buffer controlled_buffer_19
  Pull_Resistor pull_resistor_23 (.node(pull_resistor_23_node));
  assign pull_resistor_23_node = comparator_2_eq ? 30'h78000 : 30'bz;  // Controlled_Buffer controlled_buffer_20
  Pull_Resistor pull_resistor_24 (.node(comparator_2_eq));
  Comparator #(.width(2)) comparator_4 (.a(2'b00), .b(multiplexer_1_out), .eq(comparator_4_eq));  // open: gt, lt
  assign controlled_buffer_21_out = inFlag ? comparator_4_eq : 1'bz;  // Controlled_Buffer controlled_buffer_21
  Comparator #(.width(2)) comparator_5 (.a(2'b00), .b(adder_5_out), .eq(comparator_5_eq));  // open: gt, lt
  Adder #(.width(2)) adder_5 (.a(multiplexer_1_out), .b(2'b01), .out(adder_5_out));  // open: cin, cout
  assign or_1_out = shifter_1_out | shifter_11_out;  // OR_Gate or_1, 30 bits wide
  Adder #(.width(5)) adder_6 (.a(5'b11110), .b(adder_4_out), .out(adder_6_out));  // open: cin, cout
  Shifter #(.width(30), .shift("lr")) shifter_11 (
    .in(controlled_buffer_11_out), .\dist (adder_6_out), .out(shifter_11_out));
  Shifter #(.width(30), .shift("lr")) shifter_12 (
    .in(controlled_buffer_12_out), .\dist (adder_6_out), .out(shifter_12_out));
  Shifter #(.width(30), .shift("lr")) shifter_13 (
    .in(controlled_buffer_13_out), .\dist (adder_6_out), .out(shifter_13_out));
  Shifter #(.width(30), .shift("lr")) shifter_14 (
    .in(pull_resistor_17_node), .\dist (adder_6_out), .out(shifter_14_out));
  Shifter #(.width(30), .shift("lr")) shifter_15 (
    .in(controlled_buffer_15_out), .\dist (adder_6_out), .out(shifter_15_out));
  Shifter #(.width(30), .shift("lr")) shifter_16 (
    .in(controlled_buffer_16_out), .\dist (adder_6_out), .out(shifter_16_out));
  Shifter #(.width(30), .shift("lr")) shifter_17 (
    .in(controlled_buffer_17_out), .\dist (adder_6_out), .out(shifter_17_out));
  Shifter #(.width(30), .shift("lr")) shifter_18 (
    .in(pull_resistor_21_node), .\dist (adder_6_out), .out(shifter_18_out));
  Shifter #(.width(30), .shift("lr")) shifter_19 (
    .in(pull_resistor_22_node), .\dist (adder_6_out), .out(shifter_19_out));
  Shifter #(.width(30), .shift("lr")) shifter_20 (
    .in(pull_resistor_23_node), .\dist (adder_6_out), .out(shifter_20_out));
  assign or_2_out = shifter_2_out | shifter_12_out;  // OR_Gate or_2, 30 bits wide
  assign or_3_out = shifter_3_out | shifter_13_out;  // OR_Gate or_3, 30 bits wide
  assign or_4_out = shifter_4_out | shifter_14_out;  // OR_Gate or_4, 30 bits wide
  assign or_5_out = shifter_5_out | shifter_15_out;  // OR_Gate or_5, 30 bits wide
  assign or_6_out = shifter_6_out | shifter_16_out;  // OR_Gate or_6, 30 bits wide
  assign or_7_out = shifter_7_out | shifter_17_out;  // OR_Gate or_7, 30 bits wide
  assign or_8_out = shifter_8_out | shifter_18_out;  // OR_Gate or_8, 30 bits wide
  assign or_9_out = shifter_9_out | shifter_19_out;  // OR_Gate or_9, 30 bits wide
  assign controlled_buffer_22_out = inFlag ? comparator_5_eq : 1'bz;  // Controlled_Buffer controlled_buffer_22
  assign or_10_out = shifter_10_out | shifter_20_out;  // OR_Gate or_10, 30 bits wide
  Pull_Resistor pull_resistor_25 (.node(controlled_buffer_21_out));
  assign controlled_buffer_23_out = controlled_buffer_21_out ? 30'h279 : 30'bz;  // Controlled_Buffer controlled_buffer_23
  Pull_Resistor pull_resistor_26 (.node(controlled_buffer_23_out));
  assign controlled_buffer_24_out = controlled_buffer_21_out ? 30'h231 : 30'bz;  // Controlled_Buffer controlled_buffer_24
  Pull_Resistor pull_resistor_27 (.node(controlled_buffer_24_out));
  Pull_Resistor pull_resistor_28 (.node(pull_resistor_28_node));
  assign pull_resistor_28_node = controlled_buffer_21_out ? 30'h279 : 30'bz;  // Controlled_Buffer controlled_buffer_25
  assign controlled_buffer_26_out = controlled_buffer_21_out ? 30'h3ff : 30'bz;  // Controlled_Buffer controlled_buffer_26
  Pull_Resistor pull_resistor_29 (.node(controlled_buffer_26_out));
  Pull_Resistor pull_resistor_30 (.node(pull_resistor_30_node));
  assign pull_resistor_30_node = controlled_buffer_21_out ? 30'hfc : 30'bz;  // Controlled_Buffer controlled_buffer_27
  assign controlled_buffer_28_out = controlled_buffer_21_out ? 30'hfc : 30'bz;  // Controlled_Buffer controlled_buffer_28
  Pull_Resistor pull_resistor_31 (.node(controlled_buffer_28_out));
  assign controlled_buffer_29_out = controlled_buffer_21_out ? 30'h3ff : 30'bz;  // Controlled_Buffer controlled_buffer_29
  Pull_Resistor pull_resistor_32 (.node(controlled_buffer_29_out));
  Pull_Resistor pull_resistor_33 (.node(pull_resistor_33_node));
  assign pull_resistor_33_node = controlled_buffer_21_out ? 30'h279 : 30'bz;  // Controlled_Buffer controlled_buffer_30
  Pull_Resistor pull_resistor_34 (.node(pull_resistor_34_node));
  assign pull_resistor_34_node = controlled_buffer_21_out ? 30'h231 : 30'bz;  // Controlled_Buffer controlled_buffer_31
  Pull_Resistor pull_resistor_35 (.node(pull_resistor_35_node));
  assign pull_resistor_35_node = controlled_buffer_21_out ? 30'h201 : 30'bz;  // Controlled_Buffer controlled_buffer_32
  Shifter #(.width(30)) shifter_21 (.in(controlled_buffer_23_out), .\dist (adder_3_out), .out(shifter_21_out));
  Shifter #(.width(30)) shifter_22 (.in(controlled_buffer_24_out), .\dist (adder_3_out), .out(shifter_22_out));
  Shifter #(.width(30)) shifter_23 (.in(pull_resistor_28_node), .\dist (adder_3_out), .out(shifter_23_out));
  Shifter #(.width(30)) shifter_24 (.in(controlled_buffer_26_out), .\dist (adder_3_out), .out(shifter_24_out));
  Shifter #(.width(30)) shifter_25 (.in(pull_resistor_30_node), .\dist (adder_3_out), .out(shifter_25_out));
  Shifter #(.width(30)) shifter_26 (.in(controlled_buffer_28_out), .\dist (adder_3_out), .out(shifter_26_out));
  Shifter #(.width(30)) shifter_27 (.in(controlled_buffer_29_out), .\dist (adder_3_out), .out(shifter_27_out));
  Shifter #(.width(30)) shifter_28 (.in(pull_resistor_33_node), .\dist (adder_3_out), .out(shifter_28_out));
  Shifter #(.width(30)) shifter_29 (.in(pull_resistor_34_node), .\dist (adder_3_out), .out(shifter_29_out));
  Shifter #(.width(30)) shifter_30 (.in(pull_resistor_35_node), .\dist (adder_3_out), .out(shifter_30_out));
  assign not_2_out = ~adder_3_out;  // NOT_Gate not_2, 5 bits wide
  Adder #(.width(5)) adder_7 (.a(not_2_out), .b(5'b00001), .out(adder_7_out));  // open: cin, cout
  Pull_Resistor pull_resistor_36 (.node(controlled_buffer_22_out));
  Adder #(.width(5)) adder_8 (.a(5'b11110), .b(adder_7_out), .out(adder_8_out));  // open: cin, cout
  assign controlled_buffer_33_out = controlled_buffer_22_out ? 30'h279 : 30'bz;  // Controlled_Buffer controlled_buffer_33
  Pull_Resistor pull_resistor_37 (.node(controlled_buffer_33_out));
  Shifter #(.width(30), .shift("lr")) shifter_31 (
    .in(controlled_buffer_33_out), .\dist (adder_8_out), .out(shifter_31_out));
  assign controlled_buffer_34_out = controlled_buffer_22_out ? 30'h231 : 30'bz;  // Controlled_Buffer controlled_buffer_34
  Pull_Resistor pull_resistor_38 (.node(controlled_buffer_34_out));
  Shifter #(.width(30), .shift("lr")) shifter_32 (
    .in(controlled_buffer_34_out), .\dist (adder_8_out), .out(shifter_32_out));
  assign controlled_buffer_35_out = controlled_buffer_22_out ? 30'h279 : 30'bz;  // Controlled_Buffer controlled_buffer_35
  Pull_Resistor pull_resistor_39 (.node(controlled_buffer_35_out));
  Shifter #(.width(30), .shift("lr")) shifter_33 (
    .in(controlled_buffer_35_out), .\dist (adder_8_out), .out(shifter_33_out));
  Pull_Resistor pull_resistor_40 (.node(pull_resistor_40_node));
  assign pull_resistor_40_node = controlled_buffer_22_out ? 30'h3ff : 30'bz;  // Controlled_Buffer controlled_buffer_36
  Shifter #(.width(30), .shift("lr")) shifter_34 (
    .in(pull_resistor_40_node), .\dist (adder_8_out), .out(shifter_34_out));
  Pull_Resistor pull_resistor_41 (.node(pull_resistor_41_node));
  assign pull_resistor_41_node = controlled_buffer_22_out ? 30'hfc : 30'bz;  // Controlled_Buffer controlled_buffer_37
  Shifter #(.width(30), .shift("lr")) shifter_35 (
    .in(pull_resistor_41_node), .\dist (adder_8_out), .out(shifter_35_out));
  Pull_Resistor pull_resistor_42 (.node(pull_resistor_42_node));
  assign pull_resistor_42_node = controlled_buffer_22_out ? 30'hfc : 30'bz;  // Controlled_Buffer controlled_buffer_38
  Shifter #(.width(30), .shift("lr")) shifter_36 (
    .in(pull_resistor_42_node), .\dist (adder_8_out), .out(shifter_36_out));
  assign controlled_buffer_39_out = controlled_buffer_22_out ? 30'h3ff : 30'bz;  // Controlled_Buffer controlled_buffer_39
  Pull_Resistor pull_resistor_43 (.node(controlled_buffer_39_out));
  Shifter #(.width(30), .shift("lr")) shifter_37 (
    .in(controlled_buffer_39_out), .\dist (adder_8_out), .out(shifter_37_out));
  assign controlled_buffer_40_out = controlled_buffer_22_out ? 30'h279 : 30'bz;  // Controlled_Buffer controlled_buffer_40
  Pull_Resistor pull_resistor_44 (.node(controlled_buffer_40_out));
  Shifter #(.width(30), .shift("lr")) shifter_38 (
    .in(controlled_buffer_40_out), .\dist (adder_8_out), .out(shifter_38_out));
  Pull_Resistor pull_resistor_45 (.node(pull_resistor_45_node));
  assign pull_resistor_45_node = controlled_buffer_22_out ? 30'h231 : 30'bz;  // Controlled_Buffer controlled_buffer_41
  Shifter #(.width(30), .shift("lr")) shifter_39 (
    .in(pull_resistor_45_node), .\dist (adder_8_out), .out(shifter_39_out));
  Pull_Resistor pull_resistor_46 (.node(pull_resistor_46_node));
  assign pull_resistor_46_node = controlled_buffer_22_out ? 30'h201 : 30'bz;  // Controlled_Buffer controlled_buffer_42
  Shifter #(.width(30), .shift("lr")) shifter_40 (
    .in(pull_resistor_46_node), .\dist (adder_8_out), .out(shifter_40_out));
  assign toFront = shifter_21_out | shifter_31_out;  // OR_Gate or_11, 30 bits wide
  assign toFront_2 = shifter_22_out | shifter_32_out;  // OR_Gate or_12, 30 bits wide
  assign toFront_3 = shifter_23_out | shifter_33_out;  // OR_Gate or_13, 30 bits wide
  assign toFront_4 = shifter_24_out | shifter_34_out;  // OR_Gate or_14, 30 bits wide
  assign toFront_5 = shifter_25_out | shifter_35_out;  // OR_Gate or_15, 30 bits wide
  assign toFront_6 = shifter_26_out | shifter_36_out;  // OR_Gate or_16, 30 bits wide
  assign toFront_7 = shifter_27_out | shifter_37_out;  // OR_Gate or_17, 30 bits wide
  assign toFront_8 = shifter_28_out | shifter_38_out;  // OR_Gate or_18, 30 bits wide
  assign toBackground = or_1_out | shifter_41_out;  // OR_Gate or_19, 30 bits wide
  Shifter #(.width(30), .shift("lr")) shifter_41 (.in(toFront), .\dist (5'b00001), .out(shifter_41_out));
  Shifter #(.width(30), .shift("lr")) shifter_42 (.in(toFront_2), .\dist (5'b00001), .out(shifter_42_out));
  Shifter #(.width(30), .shift("lr")) shifter_43 (.in(toFront_3), .\dist (5'b00001), .out(shifter_43_out));
  Shifter #(.width(30), .shift("lr")) shifter_44 (.in(toFront_4), .\dist (5'b00001), .out(shifter_44_out));
  Shifter #(.width(30), .shift("lr")) shifter_45 (.in(toFront_5), .\dist (5'b00001), .out(shifter_45_out));
  Shifter #(.width(30), .shift("lr")) shifter_46 (.in(toFront_6), .\dist (5'b00001), .out(shifter_46_out));
  Shifter #(.width(30), .shift("lr")) shifter_47 (.in(toFront_7), .\dist (5'b00001), .out(shifter_47_out));
  assign toFront_9 = shifter_29_out | shifter_39_out;  // OR_Gate or_20, 30 bits wide
  assign toFront_10 = shifter_30_out | shifter_40_out;  // OR_Gate or_21, 30 bits wide
  assign toBackground_2 = or_2_out | shifter_42_out;  // OR_Gate or_22, 30 bits wide
  assign toBackground_3 = or_3_out | shifter_43_out;  // OR_Gate or_23, 30 bits wide
  assign toBackground_4 = or_4_out | shifter_44_out;  // OR_Gate or_24, 30 bits wide
  assign toBackground_5 = or_5_out | shifter_45_out;  // OR_Gate or_25, 30 bits wide
  assign toBackground_6 = or_6_out | shifter_46_out;  // OR_Gate or_26, 30 bits wide
  assign toBackground_7 = or_7_out | shifter_47_out;  // OR_Gate or_27, 30 bits wide
  assign toBackground_8 = or_8_out | shifter_48_out;  // OR_Gate or_28, 30 bits wide
  assign toBackground_9 = or_9_out | shifter_49_out;  // OR_Gate or_29, 30 bits wide
  Shifter #(.width(30), .shift("lr")) shifter_48 (.in(toFront_8), .\dist (5'b00001), .out(shifter_48_out));
  Shifter #(.width(30), .shift("lr")) shifter_49 (.in(toFront_9), .\dist (5'b00001), .out(shifter_49_out));
  Shifter #(.width(30), .shift("lr")) shifter_50 (.in(toFront_10), .\dist (5'b00001), .out(shifter_50_out));
  assign toBackground_10 = or_10_out | shifter_50_out;  // OR_Gate or_30, 30 bits wide

  assign outFlag = inFlag;
  assign outPlayerShiftM = inPlayerShiftM;
  assign outputBackShiftM = inputBackShiftM;

  // Notes on the sheet:
  //   MAKE SHIFT BY NEXT MATRICE
  //   MAKE SHIFT IN CURRENT MATRICE
  //   MAKE SHIFT IN CURRENT MATRICE
  //   MAKE SHIFT BY NEXT MATRICE
endmodule

module truckDriver (
  input  [1:0] inBackShiftD,
  input  [4:0] inputBackShiftM,
  input  [1:0] inPlayerShiftD,
  input  [4:0] inPlayerShiftM,
  input  inFlag,
  output [29:0] toBackground,
  output [29:0] toBackground_2,
  output [29:0] toBackground_3,
  output [29:0] toBackground_4,
  output [29:0] toBackground_5,
  output [1:0] outBackShiftD,
  output [29:0] toBackground_6,
  output [4:0] outputBackShiftM,
  output [29:0] toBackground_7,
  output [29:0] toBackground_8,
  output [29:0] toBackground_9,
  output [29:0] toBackground_10,
  output [1:0] outPlayerShiftD,
  output [4:0] outPlayerShiftM,
  output outFlag,
  output [29:0] toFront,
  output [29:0] toFront_2,
  output [29:0] toFront_3,
  output [29:0] toFront_4,
  output [29:0] toFront_5,
  output [29:0] toFront_6,
  output [29:0] toFront_7,
  output [29:0] toFront_8,
  output [29:0] toFront_9,
  output [29:0] toFront_10
);

  wire comparator_1_eq, comparator_2_eq, comparator_3_eq, comparator_4_eq, comparator_5_eq,
       controlled_buffer_21_out, controlled_buffer_22_out;
  wire [1:0] adder_5_out, multiplexer_1_out;
  wire [4:0] adder_3_out, adder_4_out, adder_6_out, adder_7_out, adder_8_out, not_1_out, not_2_out;
  wire [29:0] controlled_buffer_2_out, controlled_buffer_4_out, controlled_buffer_5_out,
       controlled_buffer_8_out, controlled_buffer_11_out, controlled_buffer_14_out, controlled_buffer_20_out,
       controlled_buffer_23_out, controlled_buffer_24_out, controlled_buffer_26_out,
       controlled_buffer_28_out, controlled_buffer_32_out, controlled_buffer_34_out,
       controlled_buffer_35_out, controlled_buffer_37_out, controlled_buffer_38_out,
       controlled_buffer_39_out, controlled_buffer_40_out, or_1_out, or_2_out, or_3_out, or_4_out, or_5_out,
       or_6_out, or_7_out, or_8_out, or_9_out, or_10_out, pull_resistor_4_node, pull_resistor_6_node,
       pull_resistor_9_node, pull_resistor_10_node, pull_resistor_12_node, pull_resistor_13_node,
       pull_resistor_15_node, pull_resistor_16_node, pull_resistor_18_node, pull_resistor_19_node,
       pull_resistor_20_node, pull_resistor_21_node, pull_resistor_22_node, pull_resistor_28_node,
       pull_resistor_30_node, pull_resistor_32_node, pull_resistor_33_node, pull_resistor_34_node,
       pull_resistor_37_node, pull_resistor_40_node, pull_resistor_45_node, pull_resistor_46_node,
       shifter_1_out, shifter_2_out, shifter_3_out, shifter_4_out, shifter_5_out, shifter_6_out,
       shifter_7_out, shifter_8_out, shifter_9_out, shifter_10_out, shifter_11_out, shifter_12_out,
       shifter_13_out, shifter_14_out, shifter_15_out, shifter_16_out, shifter_17_out, shifter_18_out,
       shifter_19_out, shifter_20_out, shifter_21_out, shifter_22_out, shifter_23_out, shifter_24_out,
       shifter_25_out, shifter_26_out, shifter_27_out, shifter_28_out, shifter_29_out, shifter_30_out,
       shifter_31_out, shifter_32_out, shifter_33_out, shifter_34_out, shifter_35_out, shifter_36_out,
       shifter_37_out, shifter_38_out, shifter_39_out, shifter_40_out, shifter_41_out, shifter_42_out,
       shifter_43_out, shifter_44_out, shifter_45_out, shifter_46_out, shifter_47_out, shifter_48_out,
       shifter_49_out, shifter_50_out;

  Pull_Resistor pull_resistor_1 (.node(inputBackShiftM));
  Comparator #(.width(2)) comparator_1 (.a(2'b00), .b(inBackShiftD), .eq(comparator_1_eq));  // open: gt, lt
  // Probe on outBackShiftD
  Adder #(.width(2)) adder_1 (.a(inBackShiftD), .b(2'b01), .out(outBackShiftD));  // open: cin, cout
  // Probe on 2'b00
  // Probe on outBackShiftD
  Comparator #(.width(2)) comparator_2 (.a(outBackShiftD), .b(2'b00), .eq(comparator_2_eq));  // open: gt, lt
  Adder #(.width(2)) adder_2 (.a(inPlayerShiftD), .b(2'b01), .out(outPlayerShiftD));  // open: cin, cout
  Pull_Resistor pull_resistor_2 (.node(inPlayerShiftM));
  Adder #(.width(5)) adder_3 (.a(inPlayerShiftM), .b(5'b00001), .out(adder_3_out));  // open: cin, cout
  Comparator #(.width(5), .mode("unsigned")) comparator_3 (
    .a(inPlayerShiftM), .b(5'b11110), .eq(comparator_3_eq));  // open: gt, lt
  Pull_Resistor pull_resistor_3 (.node(comparator_1_eq));
  Pull_Resistor pull_resistor_4 (.node(pull_resistor_4_node));
  assign pull_resistor_4_node = comparator_1_eq ? 30'h3c078 : 30'bz;  // Controlled_Buffer controlled_buffer_1
  assign controlled_buffer_2_out = comparator_1_eq ? 30'h3c078 : 30'bz;  // Controlled_Buffer controlled_buffer_2
  Pull_Resistor pull_resistor_5 (.node(controlled_buffer_2_out));
  Pull_Resistor pull_resistor_6 (.node(pull_resistor_6_node));
  assign pull_resistor_6_node = comparator_1_eq ? 30'h79fff : 30'bz;  // Controlled_Buffer controlled_buffer_3
  assign controlled_buffer_4_out = comparator_1_eq ? 30'h89242 : 30'bz;  // Controlled_Buffer controlled_buffer_4
  Pull_Resistor pull_resistor_7 (.node(controlled_buffer_4_out));
  assign controlled_buffer_5_out = comparator_1_eq ? 30'hf9fff : 30'bz;  // Controlled_Buffer controlled_buffer_5
  Pull_Resistor pull_resistor_8 (.node(controlled_buffer_5_out));
  Pull_Resistor pull_resistor_9 (.node(pull_resistor_9_node));
  assign pull_resistor_9_node = comparator_1_eq ? 30'hf9fff : 30'bz;  // Controlled_Buffer controlled_buffer_6
  Pull_Resistor pull_resistor_10 (.node(pull_resistor_10_node));
  assign pull_resistor_10_node = comparator_1_eq ? 30'h89242 : 30'bz;  // Controlled_Buffer controlled_buffer_7
  assign controlled_buffer_8_out = comparator_1_eq ? 30'h79fff : 30'bz;  // Controlled_Buffer controlled_buffer_8
  Pull_Resistor pull_resistor_11 (.node(controlled_buffer_8_out));
  Pull_Resistor pull_resistor_12 (.node(pull_resistor_12_node));
  assign pull_resistor_12_node = comparator_1_eq ? 30'h3c078 : 30'bz;  // Controlled_Buffer controlled_buffer_9
  Pull_Resistor pull_resistor_13 (.node(pull_resistor_13_node));
  assign pull_resistor_13_node = comparator_1_eq ? 30'h3c078 : 30'bz;  // Controlled_Buffer controlled_buffer_10
  assign not_1_out = ~inputBackShiftM;  // NOT_Gate not_1, 5 bits wide
  Multiplexer #(.width(2), .disabled(0), .enable("false")) multiplexer_1 (
    .in0(inPlayerShiftD), .in1(outPlayerShiftD), .out(multiplexer_1_out), .sel(comparator_3_eq));
  Shifter #(.width(30)) shifter_1 (.in(pull_resistor_4_node), .\dist (inputBackShiftM), .out(shifter_1_out));
  Shifter #(.width(30)) shifter_2 (.in(controlled_buffer_2_out), .\dist (inputBackShiftM), .out(shifter_2_out));
  Shifter #(.width(30)) shifter_3 (.in(pull_resistor_6_node), .\dist (inputBackShiftM), .out(shifter_3_out));
  Shifter #(.width(30)) shifter_4 (.in(controlled_buffer_4_out), .\dist (inputBackShiftM), .out(shifter_4_out));
  Shifter #(.width(30)) shifter_5 (.in(controlled_buffer_5_out), .\dist (inputBackShiftM), .out(shifter_5_out));
  Shifter #(.width(30)) shifter_6 (.in(pull_resistor_9_node), .\dist (inputBackShiftM), .out(shifter_6_out));
  Shifter #(.width(30)) shifter_7 (.in(pull_resistor_10_node), .\dist (inputBackShiftM), .out(shifter_7_out));
  Shifter #(.width(30)) shifter_8 (.in(controlled_buffer_8_out), .\dist (inputBackShiftM), .out(shifter_8_out));
  Shifter #(.width(30)) shifter_9 (.in(pull_resistor_12_node), .\dist (inputBackShiftM), .out(shifter_9_out));
  Shifter #(.width(30)) shifter_10 (.in(pull_resistor_13_node), .\dist (inputBackShiftM), .out(shifter_10_out));
  Adder #(.width(5)) adder_4 (.a(not_1_out), .b(5'b00001), .out(adder_4_out));  // open: cin, cout
  assign controlled_buffer_11_out = comparator_2_eq ? 30'h3c078 : 30'bz;  // Controlled_Buffer controlled_buffer_11
  Pull_Resistor pull_resistor_14 (.node(controlled_buffer_11_out));
  Pull_Resistor pull_resistor_15 (.node(pull_resistor_15_node));
  assign pull_resistor_15_node = comparator_2_eq ? 30'h3c078 : 30'bz;  // Controlled_Buffer controlled_buffer_12
  Pull_Resistor pull_resistor_16 (.node(pull_resistor_16_node));
  assign pull_resistor_16_node = comparator_2_eq ? 30'h79fff : 30'bz;  // Controlled_Buffer controlled_buffer_13
  assign controlled_buffer_14_out = comparator_2_eq ? 30'h89242 : 30'bz;  // Controlled_Buffer controlled_buffer_14
  Pull_Resistor pull_resistor_17 (.node(controlled_buffer_14_out));
  Pull_Resistor pull_resistor_18 (.node(pull_resistor_18_node));
  assign pull_resistor_18_node = comparator_2_eq ? 30'hf9fff : 30'bz;  // Controlled_Buffer controlled_buffer_15
  Pull_Resistor pull_resistor_19 (.node(pull_resistor_19_node));
  assign pull_resistor_19_node = comparator_2_eq ? 30'hf9fff : 30'bz;  // Controlled_Buffer controlled_buffer_16
  Pull_Resistor pull_resistor_20 (.node(pull_resistor_20_node));
  assign pull_resistor_20_node = comparator_2_eq ? 30'h89242 : 30'bz;  // Controlled_Buffer controlled_buffer_17
  Pull_Resistor pull_resistor_21 (.node(pull_resistor_21_node));
  assign pull_resistor_21_node = comparator_2_eq ? 30'h79fff : 30'bz;  // Controlled_Buffer controlled_buffer_18
  Pull_Resistor pull_resistor_22 (.node(pull_resistor_22_node));
  assign pull_resistor_22_node = comparator_2_eq ? 30'h3c078 : 30'bz;  // Controlled_Buffer controlled_buffer_19
  assign controlled_buffer_20_out = comparator_2_eq ? 30'h3c078 : 30'bz;  // Controlled_Buffer controlled_buffer_20
  Pull_Resistor pull_resistor_23 (.node(controlled_buffer_20_out));
  Pull_Resistor pull_resistor_24 (.node(comparator_2_eq));
  Comparator #(.width(2)) comparator_4 (.a(2'b00), .b(multiplexer_1_out), .eq(comparator_4_eq));  // open: gt, lt
  assign controlled_buffer_21_out = inFlag ? comparator_4_eq : 1'bz;  // Controlled_Buffer controlled_buffer_21
  Comparator #(.width(2)) comparator_5 (.a(2'b00), .b(adder_5_out), .eq(comparator_5_eq));  // open: gt, lt
  Adder #(.width(2)) adder_5 (.a(multiplexer_1_out), .b(2'b01), .out(adder_5_out));  // open: cin, cout
  assign or_1_out = shifter_1_out | shifter_11_out;  // OR_Gate or_1, 30 bits wide
  Adder #(.width(5)) adder_6 (.a(5'b11110), .b(adder_4_out), .out(adder_6_out));  // open: cin, cout
  Shifter #(.width(30), .shift("lr")) shifter_11 (
    .in(controlled_buffer_11_out), .\dist (adder_6_out), .out(shifter_11_out));
  Shifter #(.width(30), .shift("lr")) shifter_12 (
    .in(pull_resistor_15_node), .\dist (adder_6_out), .out(shifter_12_out));
  Shifter #(.width(30), .shift("lr")) shifter_13 (
    .in(pull_resistor_16_node), .\dist (adder_6_out), .out(shifter_13_out));
  Shifter #(.width(30), .shift("lr")) shifter_14 (
    .in(controlled_buffer_14_out), .\dist (adder_6_out), .out(shifter_14_out));
  Shifter #(.width(30), .shift("lr")) shifter_15 (
    .in(pull_resistor_18_node), .\dist (adder_6_out), .out(shifter_15_out));
  Shifter #(.width(30), .shift("lr")) shifter_16 (
    .in(pull_resistor_19_node), .\dist (adder_6_out), .out(shifter_16_out));
  Shifter #(.width(30), .shift("lr")) shifter_17 (
    .in(pull_resistor_20_node), .\dist (adder_6_out), .out(shifter_17_out));
  Shifter #(.width(30), .shift("lr")) shifter_18 (
    .in(pull_resistor_21_node), .\dist (adder_6_out), .out(shifter_18_out));
  Shifter #(.width(30), .shift("lr")) shifter_19 (
    .in(pull_resistor_22_node), .\dist (adder_6_out), .out(shifter_19_out));
  Shifter #(.width(30), .shift("lr")) shifter_20 (
    .in(controlled_buffer_20_out), .\dist (adder_6_out), .out(shifter_20_out));
  assign or_2_out = shifter_2_out | shifter_12_out;  // OR_Gate or_2, 30 bits wide
  assign or_3_out = shifter_3_out | shifter_13_out;  // OR_Gate or_3, 30 bits wide
  assign or_4_out = shifter_4_out | shifter_14_out;  // OR_Gate or_4, 30 bits wide
  assign or_5_out = shifter_5_out | shifter_15_out;  // OR_Gate or_5, 30 bits wide
  assign or_6_out = shifter_6_out | shifter_16_out;  // OR_Gate or_6, 30 bits wide
  assign or_7_out = shifter_7_out | shifter_17_out;  // OR_Gate or_7, 30 bits wide
  assign or_8_out = shifter_8_out | shifter_18_out;  // OR_Gate or_8, 30 bits wide
  assign or_9_out = shifter_9_out | shifter_19_out;  // OR_Gate or_9, 30 bits wide
  assign controlled_buffer_22_out = inFlag ? comparator_5_eq : 1'bz;  // Controlled_Buffer controlled_buffer_22
  assign or_10_out = shifter_10_out | shifter_20_out;  // OR_Gate or_10, 30 bits wide
  assign controlled_buffer_23_out = controlled_buffer_21_out ? 30'h279 : 30'bz;  // Controlled_Buffer controlled_buffer_23
  Pull_Resistor pull_resistor_25 (.node(controlled_buffer_23_out));
  Pull_Resistor pull_resistor_26 (.node(controlled_buffer_21_out));
  assign controlled_buffer_24_out = controlled_buffer_21_out ? 30'h231 : 30'bz;  // Controlled_Buffer controlled_buffer_24
  Pull_Resistor pull_resistor_27 (.node(controlled_buffer_24_out));
  Pull_Resistor pull_resistor_28 (.node(pull_resistor_28_node));
  assign pull_resistor_28_node = controlled_buffer_21_out ? 30'h279 : 30'bz;  // Controlled_Buffer controlled_buffer_25
  assign controlled_buffer_26_out = controlled_buffer_21_out ? 30'h3ff : 30'bz;  // Controlled_Buffer controlled_buffer_26
  Pull_Resistor pull_resistor_29 (.node(controlled_buffer_26_out));
  Pull_Resistor pull_resistor_30 (.node(pull_resistor_30_node));
  assign pull_resistor_30_node = controlled_buffer_21_out ? 30'hfc : 30'bz;  // Controlled_Buffer controlled_buffer_27
  assign controlled_buffer_28_out = controlled_buffer_21_out ? 30'hfc : 30'bz;  // Controlled_Buffer controlled_buffer_28
  Pull_Resistor pull_resistor_31 (.node(controlled_buffer_28_out));
  Pull_Resistor pull_resistor_32 (.node(pull_resistor_32_node));
  assign pull_resistor_32_node = controlled_buffer_21_out ? 30'h3ff : 30'bz;  // Controlled_Buffer controlled_buffer_29
  Pull_Resistor pull_resistor_33 (.node(pull_resistor_33_node));
  assign pull_resistor_33_node = controlled_buffer_21_out ? 30'h279 : 30'bz;  // Controlled_Buffer controlled_buffer_30
  Pull_Resistor pull_resistor_34 (.node(pull_resistor_34_node));
  assign pull_resistor_34_node = controlled_buffer_21_out ? 30'h231 : 30'bz;  // Controlled_Buffer controlled_buffer_31
  assign controlled_buffer_32_out = controlled_buffer_21_out ? 30'h201 : 30'bz;  // Controlled_Buffer controlled_buffer_32
  Pull_Resistor pull_resistor_35 (.node(controlled_buffer_32_out));
  Shifter #(.width(30)) shifter_21 (.in(controlled_buffer_23_out), .\dist (adder_3_out), .out(shifter_21_out));
  Shifter #(.width(30)) shifter_22 (.in(controlled_buffer_24_out), .\dist (adder_3_out), .out(shifter_22_out));
  Shifter #(.width(30)) shifter_23 (.in(pull_resistor_28_node), .\dist (adder_3_out), .out(shifter_23_out));
  Shifter #(.width(30)) shifter_24 (.in(controlled_buffer_26_out), .\dist (adder_3_out), .out(shifter_24_out));
  Shifter #(.width(30)) shifter_25 (.in(pull_resistor_30_node), .\dist (adder_3_out), .out(shifter_25_out));
  Shifter #(.width(30)) shifter_26 (.in(controlled_buffer_28_out), .\dist (adder_3_out), .out(shifter_26_out));
  Shifter #(.width(30)) shifter_27 (.in(pull_resistor_32_node), .\dist (adder_3_out), .out(shifter_27_out));
  Shifter #(.width(30)) shifter_28 (.in(pull_resistor_33_node), .\dist (adder_3_out), .out(shifter_28_out));
  Shifter #(.width(30)) shifter_29 (.in(pull_resistor_34_node), .\dist (adder_3_out), .out(shifter_29_out));
  Shifter #(.width(30)) shifter_30 (.in(controlled_buffer_32_out), .\dist (adder_3_out), .out(shifter_30_out));
  assign not_2_out = ~adder_3_out;  // NOT_Gate not_2, 5 bits wide
  Adder #(.width(5)) adder_7 (.a(not_2_out), .b(5'b00001), .out(adder_7_out));  // open: cin, cout
  Pull_Resistor pull_resistor_36 (.node(controlled_buffer_22_out));
  Adder #(.width(5)) adder_8 (.a(5'b11110), .b(adder_7_out), .out(adder_8_out));  // open: cin, cout
  Pull_Resistor pull_resistor_37 (.node(pull_resistor_37_node));
  assign pull_resistor_37_node = controlled_buffer_22_out ? 30'h279 : 30'bz;  // Controlled_Buffer controlled_buffer_33
  Shifter #(.width(30), .shift("lr")) shifter_31 (
    .in(pull_resistor_37_node), .\dist (adder_8_out), .out(shifter_31_out));
  assign controlled_buffer_34_out = controlled_buffer_22_out ? 30'h231 : 30'bz;  // Controlled_Buffer controlled_buffer_34
  Pull_Resistor pull_resistor_38 (.node(controlled_buffer_34_out));
  Shifter #(.width(30), .shift("lr")) shifter_32 (
    .in(controlled_buffer_34_out), .\dist (adder_8_out), .out(shifter_32_out));
  assign controlled_buffer_35_out = controlled_buffer_22_out ? 30'h279 : 30'bz;  // Controlled_Buffer controlled_buffer_35
  Pull_Resistor pull_resistor_39 (.node(controlled_buffer_35_out));
  Shifter #(.width(30), .shift("lr")) shifter_33 (
    .in(controlled_buffer_35_out), .\dist (adder_8_out), .out(shifter_33_out));
  Pull_Resistor pull_resistor_40 (.node(pull_resistor_40_node));
  assign pull_resistor_40_node = controlled_buffer_22_out ? 30'h3ff : 30'bz;  // Controlled_Buffer controlled_buffer_36
  Shifter #(.width(30), .shift("lr")) shifter_34 (
    .in(pull_resistor_40_node), .\dist (adder_8_out), .out(shifter_34_out));
  assign controlled_buffer_37_out = controlled_buffer_22_out ? 30'hfc : 30'bz;  // Controlled_Buffer controlled_buffer_37
  Pull_Resistor pull_resistor_41 (.node(controlled_buffer_37_out));
  Shifter #(.width(30), .shift("lr")) shifter_35 (
    .in(controlled_buffer_37_out), .\dist (adder_8_out), .out(shifter_35_out));
  assign controlled_buffer_38_out = controlled_buffer_22_out ? 30'hfc : 30'bz;  // Controlled_Buffer controlled_buffer_38
  Pull_Resistor pull_resistor_42 (.node(controlled_buffer_38_out));
  Shifter #(.width(30), .shift("lr")) shifter_36 (
    .in(controlled_buffer_38_out), .\dist (adder_8_out), .out(shifter_36_out));
  assign controlled_buffer_39_out = controlled_buffer_22_out ? 30'h3ff : 30'bz;  // Controlled_Buffer controlled_buffer_39
  Pull_Resistor pull_resistor_43 (.node(controlled_buffer_39_out));
  Shifter #(.width(30), .shift("lr")) shifter_37 (
    .in(controlled_buffer_39_out), .\dist (adder_8_out), .out(shifter_37_out));
  assign controlled_buffer_40_out = controlled_buffer_22_out ? 30'h279 : 30'bz;  // Controlled_Buffer controlled_buffer_40
  Pull_Resistor pull_resistor_44 (.node(controlled_buffer_40_out));
  Shifter #(.width(30), .shift("lr")) shifter_38 (
    .in(controlled_buffer_40_out), .\dist (adder_8_out), .out(shifter_38_out));
  Pull_Resistor pull_resistor_45 (.node(pull_resistor_45_node));
  assign pull_resistor_45_node = controlled_buffer_22_out ? 30'h231 : 30'bz;  // Controlled_Buffer controlled_buffer_41
  Shifter #(.width(30), .shift("lr")) shifter_39 (
    .in(pull_resistor_45_node), .\dist (adder_8_out), .out(shifter_39_out));
  Pull_Resistor pull_resistor_46 (.node(pull_resistor_46_node));
  assign pull_resistor_46_node = controlled_buffer_22_out ? 30'h201 : 30'bz;  // Controlled_Buffer controlled_buffer_42
  Shifter #(.width(30), .shift("lr")) shifter_40 (
    .in(pull_resistor_46_node), .\dist (adder_8_out), .out(shifter_40_out));
  assign toFront = shifter_21_out | shifter_31_out;  // OR_Gate or_11, 30 bits wide
  assign toFront_2 = shifter_22_out | shifter_32_out;  // OR_Gate or_12, 30 bits wide
  assign toFront_3 = shifter_23_out | shifter_33_out;  // OR_Gate or_13, 30 bits wide
  assign toFront_4 = shifter_24_out | shifter_34_out;  // OR_Gate or_14, 30 bits wide
  assign toFront_5 = shifter_25_out | shifter_35_out;  // OR_Gate or_15, 30 bits wide
  assign toFront_6 = shifter_26_out | shifter_36_out;  // OR_Gate or_16, 30 bits wide
  assign toFront_7 = shifter_27_out | shifter_37_out;  // OR_Gate or_17, 30 bits wide
  assign toFront_8 = shifter_28_out | shifter_38_out;  // OR_Gate or_18, 30 bits wide
  assign toBackground = or_1_out | shifter_41_out;  // OR_Gate or_19, 30 bits wide
  Shifter #(.width(30), .shift("lr")) shifter_41 (.in(toFront), .\dist (5'b00001), .out(shifter_41_out));
  Shifter #(.width(30), .shift("lr")) shifter_42 (.in(toFront_2), .\dist (5'b00001), .out(shifter_42_out));
  Shifter #(.width(30), .shift("lr")) shifter_43 (.in(toFront_3), .\dist (5'b00001), .out(shifter_43_out));
  Shifter #(.width(30), .shift("lr")) shifter_44 (.in(toFront_4), .\dist (5'b00001), .out(shifter_44_out));
  Shifter #(.width(30), .shift("lr")) shifter_45 (.in(toFront_5), .\dist (5'b00001), .out(shifter_45_out));
  Shifter #(.width(30), .shift("lr")) shifter_46 (.in(toFront_6), .\dist (5'b00001), .out(shifter_46_out));
  Shifter #(.width(30), .shift("lr")) shifter_47 (.in(toFront_7), .\dist (5'b00001), .out(shifter_47_out));
  assign toFront_9 = shifter_29_out | shifter_39_out;  // OR_Gate or_20, 30 bits wide
  assign toFront_10 = shifter_30_out | shifter_40_out;  // OR_Gate or_21, 30 bits wide
  assign toBackground_2 = or_2_out | shifter_42_out;  // OR_Gate or_22, 30 bits wide
  assign toBackground_3 = or_3_out | shifter_43_out;  // OR_Gate or_23, 30 bits wide
  assign toBackground_4 = or_4_out | shifter_44_out;  // OR_Gate or_24, 30 bits wide
  assign toBackground_5 = or_5_out | shifter_45_out;  // OR_Gate or_25, 30 bits wide
  assign toBackground_6 = or_6_out | shifter_46_out;  // OR_Gate or_26, 30 bits wide
  assign toBackground_7 = or_7_out | shifter_47_out;  // OR_Gate or_27, 30 bits wide
  assign toBackground_8 = or_8_out | shifter_48_out;  // OR_Gate or_28, 30 bits wide
  assign toBackground_9 = or_9_out | shifter_49_out;  // OR_Gate or_29, 30 bits wide
  Shifter #(.width(30), .shift("lr")) shifter_48 (.in(toFront_8), .\dist (5'b00001), .out(shifter_48_out));
  Shifter #(.width(30), .shift("lr")) shifter_49 (.in(toFront_9), .\dist (5'b00001), .out(shifter_49_out));
  Shifter #(.width(30), .shift("lr")) shifter_50 (.in(toFront_10), .\dist (5'b00001), .out(shifter_50_out));
  assign toBackground_10 = or_10_out | shifter_50_out;  // OR_Gate or_30, 30 bits wide

  assign outFlag = inFlag;
  assign outPlayerShiftM = inPlayerShiftM;
  assign outputBackShiftM = inputBackShiftM;

  // Notes on the sheet:
  //   MAKE SHIFT BY NEXT MATRICE
  //   MAKE SHIFT IN CURRENT MATRICE
  //   MAKE SHIFT IN CURRENT MATRICE
  //   MAKE SHIFT BY NEXT MATRICE
endmodule

module swampDriver (
  input  [1:0] inPlayerShiftD,
  input  [4:0] inPlayerShiftM,
  input  inFlag,
  output [29:0] toBackground,
  output [29:0] toBackground_2,
  output [29:0] toBackground_3,
  output [29:0] toBackground_4,
  output [29:0] toBackground_5,
  output [29:0] toBackground_6,
  output [29:0] toBackground_7,
  output [29:0] toFront,
  output [29:0] toBackground_8,
  output [29:0] toFront_2,
  output [29:0] toBackground_9,
  output [29:0] toFront_3,
  output [29:0] toBackground_10,
  output [29:0] toFront_4,
  output [29:0] toFront_5,
  output [29:0] toFront_6,
  output [1:0] outPlayerShiftD,
  output [4:0] outPlayerShiftM,
  output [29:0] toFront_7,
  output outFlag,
  output [29:0] toFront_8,
  output [29:0] toFront_9,
  output [29:0] toFront_10
);

  wire comparator_1_eq, comparator_2_eq, comparator_3_eq, controlled_buffer_1_out, controlled_buffer_2_out;
  wire [1:0] adder_3_out, multiplexer_1_out;
  wire [4:0] adder_2_out, adder_4_out, adder_5_out, not_1_out;
  wire [29:0] controlled_buffer_3_out, controlled_buffer_4_out, controlled_buffer_8_out,
       controlled_buffer_10_out, controlled_buffer_12_out, controlled_buffer_14_out,
       controlled_buffer_15_out, controlled_buffer_16_out, controlled_buffer_17_out,
       controlled_buffer_19_out, controlled_buffer_21_out, controlled_buffer_22_out, pull_resistor_5_node,
       pull_resistor_6_node, pull_resistor_7_node, pull_resistor_9_node, pull_resistor_11_node,
       pull_resistor_13_node, pull_resistor_18_node, pull_resistor_20_node, shifter_1_out, shifter_2_out,
       shifter_3_out, shifter_4_out, shifter_5_out, shifter_6_out, shifter_7_out, shifter_8_out,
       shifter_9_out, shifter_10_out, shifter_11_out, shifter_12_out, shifter_13_out, shifter_14_out,
       shifter_15_out, shifter_16_out, shifter_17_out, shifter_18_out, shifter_19_out, shifter_20_out,
       shifter_21_out, shifter_22_out, shifter_23_out, shifter_24_out, shifter_25_out, shifter_26_out,
       shifter_27_out, shifter_28_out, shifter_29_out, shifter_30_out;

  Adder #(.width(2)) adder_1 (.a(inPlayerShiftD), .b(2'b01), .out(outPlayerShiftD));  // open: cin, cout
  Pull_Resistor pull_resistor_1 (.node(inPlayerShiftM));
  Adder #(.width(5)) adder_2 (.a(inPlayerShiftM), .b(5'b00001), .out(adder_2_out));  // open: cin, cout
  Multiplexer #(.width(2), .disabled(0), .enable("false")) multiplexer_1 (
    .in0(inPlayerShiftD), .in1(outPlayerShiftD), .out(multiplexer_1_out), .sel(comparator_1_eq));
  Comparator #(.width(5), .mode("unsigned")) comparator_1 (
    .a(inPlayerShiftM), .b(5'b11110), .eq(comparator_1_eq));  // open: gt, lt
  Comparator #(.width(2)) comparator_2 (.a(2'b00), .b(multiplexer_1_out), .eq(comparator_2_eq));  // open: gt, lt
  assign controlled_buffer_1_out = inFlag ? comparator_2_eq : 1'bz;  // Controlled_Buffer controlled_buffer_1
  Comparator #(.width(2)) comparator_3 (.a(2'b00), .b(adder_3_out), .eq(comparator_3_eq));  // open: gt, lt
  Adder #(.width(2)) adder_3 (.a(multiplexer_1_out), .b(2'b01), .out(adder_3_out));  // open: cin, cout
  assign controlled_buffer_2_out = inFlag ? comparator_3_eq : 1'bz;  // Controlled_Buffer controlled_buffer_2
  assign controlled_buffer_3_out = controlled_buffer_1_out ? 30'h279 : 30'bz;  // Controlled_Buffer controlled_buffer_3
  Pull_Resistor pull_resistor_2 (.node(controlled_buffer_1_out));
  Pull_Resistor pull_resistor_3 (.node(controlled_buffer_3_out));
  assign controlled_buffer_4_out = controlled_buffer_1_out ? 30'h231 : 30'bz;  // Controlled_Buffer controlled_buffer_4
  Pull_Resistor pull_resistor_4 (.node(controlled_buffer_4_out));
  Pull_Resistor pull_resistor_5 (.node(pull_resistor_5_node));
  assign pull_resistor_5_node = controlled_buffer_1_out ? 30'h279 : 30'bz;  // Controlled_Buffer controlled_buffer_5
  Pull_Resistor pull_resistor_6 (.node(pull_resistor_6_node));
  assign pull_resistor_6_node = controlled_buffer_1_out ? 30'h3ff : 30'bz;  // Controlled_Buffer controlled_buffer_6
  Pull_Resistor pull_resistor_7 (.node(pull_resistor_7_node));
  assign pull_resistor_7_node = controlled_buffer_1_out ? 30'hfc : 30'bz;  // Controlled_Buffer controlled_buffer_7
  assign controlled_buffer_8_out = controlled_buffer_1_out ? 30'hfc : 30'bz;  // Controlled_Buffer controlled_buffer_8
  Pull_Resistor pull_resistor_8 (.node(controlled_buffer_8_out));
  Pull_Resistor pull_resistor_9 (.node(pull_resistor_9_node));
  assign pull_resistor_9_node = controlled_buffer_1_out ? 30'h3ff : 30'bz;  // Controlled_Buffer controlled_buffer_9
  assign controlled_buffer_10_out = controlled_buffer_1_out ? 30'h279 : 30'bz;  // Controlled_Buffer controlled_buffer_10
  Pull_Resistor pull_resistor_10 (.node(controlled_buffer_10_out));
  Pull_Resistor pull_resistor_11 (.node(pull_resistor_11_node));
  assign pull_resistor_11_node = controlled_buffer_1_out ? 30'h231 : 30'bz;  // Controlled_Buffer controlled_buffer_11
  assign controlled_buffer_12_out = controlled_buffer_1_out ? 30'h201 : 30'bz;  // Controlled_Buffer controlled_buffer_12
  Pull_Resistor pull_resistor_12 (.node(controlled_buffer_12_out));
  Shifter #(.width(30)) shifter_1 (.in(controlled_buffer_3_out), .\dist (adder_2_out), .out(shifter_1_out));
  Shifter #(.width(30)) shifter_2 (.in(controlled_buffer_4_out), .\dist (adder_2_out), .out(shifter_2_out));
  Shifter #(.width(30)) shifter_3 (.in(pull_resistor_5_node), .\dist (adder_2_out), .out(shifter_3_out));
  Shifter #(.width(30)) shifter_4 (.in(pull_resistor_6_node), .\dist (adder_2_out), .out(shifter_4_out));
  Shifter #(.width(30)) shifter_5 (.in(pull_resistor_7_node), .\dist (adder_2_out), .out(shifter_5_out));
  Shifter #(.width(30)) shifter_6 (.in(controlled_buffer_8_out), .\dist (adder_2_out), .out(shifter_6_out));
  Shifter #(.width(30)) shifter_7 (.in(pull_resistor_9_node), .\dist (adder_2_out), .out(shifter_7_out));
  Shifter #(.width(30)) shifter_8 (.in(controlled_buffer_10_out), .\dist (adder_2_out), .out(shifter_8_out));
  Shifter #(.width(30)) shifter_9 (.in(pull_resistor_11_node), .\dist (adder_2_out), .out(shifter_9_out));
  Shifter #(.width(30)) shifter_10 (.in(controlled_buffer_12_out), .\dist (adder_2_out), .out(shifter_10_out));
  assign not_1_out = ~adder_2_out;  // NOT_Gate not_1, 5 bits wide
  Adder #(.width(5)) adder_4 (.a(not_1_out), .b(5'b00001), .out(adder_4_out));  // open: cin, cout
  Adder #(.width(5)) adder_5 (.a(5'b11110), .b(adder_4_out), .out(adder_5_out));  // open: cin, cout
  Pull_Resistor pull_resistor_13 (.node(pull_resistor_13_node));
  assign pull_resistor_13_node = controlled_buffer_2_out ? 30'h279 : 30'bz;  // Controlled_Buffer controlled_buffer_13
  Shifter #(.width(30), .shift("lr")) shifter_11 (
    .in(pull_resistor_13_node), .\dist (adder_5_out), .out(shifter_11_out));
  assign controlled_buffer_14_out = controlled_buffer_2_out ? 30'h231 : 30'bz;  // Controlled_Buffer controlled_buffer_14
  Pull_Resistor pull_resistor_14 (.node(controlled_buffer_14_out));
  Shifter #(.width(30), .shift("lr")) shifter_12 (
    .in(controlled_buffer_14_out), .\dist (adder_5_out), .out(shifter_12_out));
  assign controlled_buffer_15_out = controlled_buffer_2_out ? 30'h279 : 30'bz;  // Controlled_Buffer controlled_buffer_15
  Pull_Resistor pull_resistor_15 (.node(controlled_buffer_15_out));
  Shifter #(.width(30), .shift("lr")) shifter_13 (
    .in(controlled_buffer_15_out), .\dist (adder_5_out), .out(shifter_13_out));
  assign controlled_buffer_16_out = controlled_buffer_2_out ? 30'h3ff : 30'bz;  // Controlled_Buffer controlled_buffer_16
  Pull_Resistor pull_resistor_16 (.node(controlled_buffer_16_out));
  Shifter #(.width(30), .shift("lr")) shifter_14 (
    .in(controlled_buffer_16_out), .\dist (adder_5_out), .out(shifter_14_out));
  assign controlled_buffer_17_out = controlled_buffer_2_out ? 30'hfc : 30'bz;  // Controlled_Buffer controlled_buffer_17
  Pull_Resistor pull_resistor_17 (.node(controlled_buffer_17_out));
  Shifter #(.width(30), .shift("lr")) shifter_15 (
    .in(controlled_buffer_17_out), .\dist (adder_5_out), .out(shifter_15_out));
  Pull_Resistor pull_resistor_18 (.node(pull_resistor_18_node));
  assign pull_resistor_18_node = controlled_buffer_2_out ? 30'hfc : 30'bz;  // Controlled_Buffer controlled_buffer_18
  Shifter #(.width(30), .shift("lr")) shifter_16 (
    .in(pull_resistor_18_node), .\dist (adder_5_out), .out(shifter_16_out));
  assign controlled_buffer_19_out = controlled_buffer_2_out ? 30'h3ff : 30'bz;  // Controlled_Buffer controlled_buffer_19
  Pull_Resistor pull_resistor_19 (.node(controlled_buffer_19_out));
  Shifter #(.width(30), .shift("lr")) shifter_17 (
    .in(controlled_buffer_19_out), .\dist (adder_5_out), .out(shifter_17_out));
  Pull_Resistor pull_resistor_20 (.node(pull_resistor_20_node));
  assign pull_resistor_20_node = controlled_buffer_2_out ? 30'h279 : 30'bz;  // Controlled_Buffer controlled_buffer_20
  Shifter #(.width(30), .shift("lr")) shifter_18 (
    .in(pull_resistor_20_node), .\dist (adder_5_out), .out(shifter_18_out));
  assign controlled_buffer_21_out = controlled_buffer_2_out ? 30'h231 : 30'bz;  // Controlled_Buffer controlled_buffer_21
  Pull_Resistor pull_resistor_21 (.node(controlled_buffer_21_out));
  Shifter #(.width(30), .shift("lr")) shifter_19 (
    .in(controlled_buffer_21_out), .\dist (adder_5_out), .out(shifter_19_out));
  assign controlled_buffer_22_out = controlled_buffer_2_out ? 30'h201 : 30'bz;  // Controlled_Buffer controlled_buffer_22
  Pull_Resistor pull_resistor_22 (.node(controlled_buffer_22_out));
  Shifter #(.width(30), .shift("lr")) shifter_20 (
    .in(controlled_buffer_22_out), .\dist (adder_5_out), .out(shifter_20_out));
  Pull_Resistor pull_resistor_23 (.node(controlled_buffer_2_out));
  assign toFront = shifter_1_out | shifter_11_out;  // OR_Gate or_1, 30 bits wide
  assign toFront_2 = shifter_2_out | shifter_12_out;  // OR_Gate or_2, 30 bits wide
  assign toFront_3 = shifter_3_out | shifter_13_out;  // OR_Gate or_3, 30 bits wide
  assign toFront_4 = shifter_4_out | shifter_14_out;  // OR_Gate or_4, 30 bits wide
  assign toFront_5 = shifter_5_out | shifter_15_out;  // OR_Gate or_5, 30 bits wide
  assign toFront_6 = shifter_6_out | shifter_16_out;  // OR_Gate or_6, 30 bits wide
  assign toBackground = {30{1'b0}} | shifter_21_out;  // OR_Gate or_7, 30 bits wide
  Shifter #(.width(30), .shift("lr")) shifter_21 (.in(toFront), .\dist (5'b00001), .out(shifter_21_out));
  Shifter #(.width(30), .shift("lr")) shifter_22 (.in(toFront_2), .\dist (5'b00001), .out(shifter_22_out));
  Shifter #(.width(30), .shift("lr")) shifter_23 (.in(toFront_3), .\dist (5'b00001), .out(shifter_23_out));
  Shifter #(.width(30), .shift("lr")) shifter_24 (.in(toFront_4), .\dist (5'b00001), .out(shifter_24_out));
  Shifter #(.width(30), .shift("lr")) shifter_25 (.in(toFront_5), .\dist (5'b00001), .out(shifter_25_out));
  assign toFront_7 = shifter_7_out | shifter_17_out;  // OR_Gate or_8, 30 bits wide
  assign toFront_8 = shifter_8_out | shifter_18_out;  // OR_Gate or_9, 30 bits wide
  assign toFront_9 = shifter_9_out | shifter_19_out;  // OR_Gate or_10, 30 bits wide
  assign toFront_10 = shifter_10_out | shifter_20_out;  // OR_Gate or_11, 30 bits wide
  assign toBackground_2 = {30{1'b0}} | shifter_22_out;  // OR_Gate or_12, 30 bits wide
  assign toBackground_3 = 30'hcc330cc | shifter_23_out;  // OR_Gate or_13, 30 bits wide
  assign toBackground_4 = 30'h1ce739ce | shifter_24_out;  // OR_Gate or_14, 30 bits wide
  assign toBackground_5 = 30'h1fe7f9fe | shifter_25_out;  // OR_Gate or_15, 30 bits wide
  assign toBackground_6 = 30'h1fe7f9fe | shifter_26_out;  // OR_Gate or_16, 30 bits wide
  Shifter #(.width(30), .shift("lr")) shifter_26 (.in(toFront_6), .\dist (5'b00001), .out(shifter_26_out));
  assign toBackground_7 = 30'h1ce739ce | shifter_27_out;  // OR_Gate or_17, 30 bits wide
  Shifter #(.width(30), .shift("lr")) shifter_27 (.in(toFront_7), .\dist (5'b00001), .out(shifter_27_out));
  assign toBackground_8 = 30'hcc330cc | shifter_28_out;  // OR_Gate or_18, 30 bits wide
  Shifter #(.width(30), .shift("lr")) shifter_28 (.in(toFront_8), .\dist (5'b00001), .out(shifter_28_out));
  assign toBackground_9 = {30{1'b0}} | shifter_29_out;  // OR_Gate or_19, 30 bits wide
  Shifter #(.width(30), .shift("lr")) shifter_29 (.in(toFront_9), .\dist (5'b00001), .out(shifter_29_out));
  Shifter #(.width(30), .shift("lr")) shifter_30 (.in(toFront_10), .\dist (5'b00001), .out(shifter_30_out));
  assign toBackground_10 = {30{1'b0}} | shifter_30_out;  // OR_Gate or_20, 30 bits wide

  assign outFlag = inFlag;
  assign outPlayerShiftM = inPlayerShiftM;

  // Notes on the sheet:
  //   MAKE SHIFT BY NEXT MATRICE
  //   MAKE SHIFT IN CURRENT MATRICE
endmodule
