// Logisim project keyboard.circ as structural Verilog: 8 circuits, main circuit latency
module latency (
  input  in,
  output out
);

  wire not_1_out, not_2_out, not_3_out, not_4_out, not_5_out, not_6_out, not_7_out, not_8_out, not_9_out,
       not_10_out, not_11_out, not_12_out, not_13_out, not_14_out, not_15_out, not_16_out, not_17_out,
       not_18_out, not_19_out, not_20_out, not_21_out, not_22_out, not_23_out, not_24_out, not_25_out,
       not_26_out, not_27_out, not_28_out, not_29_out, not_30_out, not_31_out, not_32_out, not_33_out,
       not_34_out, not_35_out, not_36_out, not_37_out, not_38_out, not_39_out, not_40_out, not_41_out,
       not_42_out, not_43_out, not_44_out, not_45_out, not_46_out, not_47_out, not_48_out, not_49_out,
       not_50_out, not_52_out, not_53_out, not_54_out;

  not not_1 (not_1_out, in);
  not not_2 (not_2_out, not_1_out);
  not not_3 (not_3_out, not_5_out);
  not not_4 (not_4_out, not_6_out);
  not not_5 (not_5_out, not_4_out);
  not not_6 (not_6_out, not_2_out);
  not not_7 (not_7_out, not_3_out);
  not not_8 (not_8_out, not_9_out);
  not not_9 (not_9_out, not_7_out);
  not not_10 (not_10_out, not_8_out);
  not not_11 (not_11_out, not_12_out);
  not not_12 (not_12_out, not_13_out);
  not not_13 (not_13_out, not_14_out);
  not not_14 (not_14_out, not_10_out);
  not not_15 (not_15_out, not_17_out);
  not not_16 (not_16_out, not_15_out);
  not not_17 (not_17_out, not_18_out);
  not not_18 (not_18_out, not_11_out);
  not not_19 (not_19_out, not_22_out);
  not not_20 (not_20_out, not_19_out);
  not not_21 (not_21_out, not_16_out);
  not not_22 (not_22_out, not_21_out);
  not not_23 (not_23_out, not_26_out);
  not not_24 (not_24_out, not_23_out);
  not not_25 (not_25_out, not_20_out);
  not not_26 (not_26_out, not_25_out);
  not not_27 (not_27_out, not_30_out);
  not not_28 (not_28_out, not_27_out);
  not not_29 (not_29_out, not_24_out);
  not not_30 (not_30_out, not_29_out);
  not not_31 (not_31_out, not_28_out);
  not not_32 (not_32_out, not_31_out);
  not not_33 (not_33_out, not_34_out);
  not not_34 (not_34_out, not_32_out);
  not not_35 (not_35_out, not_37_out);
  not not_36 (not_36_out, not_33_out);
  not not_37 (not_37_out, not_38_out);
  not not_38 (not_38_out, not_36_out);
  not not_39 (not_39_out, not_35_out);
  not not_40 (not_40_out, not_39_out);
  not not_41 (not_41_out, not_42_out);
  not not_42 (not_42_out, not_40_out);
  not not_43 (not_43_out, not_46_out);
  not not_44 (not_44_out, not_45_out);
  not not_45 (not_45_out, not_41_out);
  not not_46 (not_46_out, not_44_out);
  not not_47 (not_47_out, not_43_out);
  not not_48 (not_48_out, not_47_out);
  not not_49 (not_49_out, not_50_out);
  not not_50 (not_50_out, not_48_out);
  not not_51 (out, not_53_out);
  not not_52 (not_52_out, not_49_out);
  not not_53 (not_53_out, not_54_out);
  not not_54 (not_54_out, not_52_out);
endmodule

module playerEngine (
  input  [6:0] keyboardIn,
  input  [2:0] lefter,
  input  [2:0] righter,
  input  res,
  output [3:0] Y,
  output [4:0] XM,
  output [1:0] XD,
  output die
);

  wire activateX, and_2_out, clock_1_out, comparator_1_eq, comparator_2_eq, comparator_3_eq, comparator_4_eq,
       comparator_5_eq, comparator_6_eq, comparator_7_eq, comparator_8_eq, comparator_9_eq, comparator_10_eq,
       comparator_11_eq, comparator_12_eq, comparator_13_eq, comparator_14_eq, comparator_15_eq,
       comparator_18_gt, comparator_19_lt, controlled_buffer_16_out, controlled_buffer_17_out, DResM, DResP,
       envRes, latency_1_out, latency_2_out, latency_3_out, latency_4_out, latency_5_out, latency_6_out,
       latency_7_out, latency_8_out, latency_9_out, latency_10_out, latency_11_out, latency_12_out,
       latency_13_out, latency_14_out, latency_15_out, latency_16_out, latency_17_out, latency_18_out,
       latency_19_out, latency_20_out, latency_21_out, latency_22_out, latency_23_out, n8latency_1_out,
       n8latency_2_out, not_1_out, not_2_out, not_3_out, not_4_out, not_5_out, not_6_out, not_7_out,
       not_8_out, or_5_out, or_6_out, or_7_out, or_8_out, or_9_out, or_11_out, or_13_out, or_16_out,
       or_17_out, pull_resistor_13_node, pull_resistor_14_node, pull_resistor_15_node, pull_resistor_19_node,
       res_out, Ssign, state, Wsign;
  wire [2:0] adder_6_out, controlled_buffer_18_out, controlled_buffer_20_out, incterD, or_15_out,
       pull_resistor_18_node, subtractor_6_out;
  wire [2:2] subtractor_8_out;
  wire [5:0] adder_1_out, adder_2_out, adder_3_out, adder_4_out, adder_5_out, controlled_buffer_3_out,
       controlled_buffer_4_out, controlled_buffer_5_out, controlled_buffer_6_out, controlled_buffer_7_out,
       controlled_buffer_8_out, controlled_buffer_9_out, controlled_buffer_10_out, controlled_buffer_11_out,
       controlled_buffer_13_out, incter, or_10_out, or_12_out, pull_resistor_1_node, pull_resistor_2_node,
       pull_resistor_11_node, register_1_q, subtractor_1_out, subtractor_2_out, subtractor_3_out,
       subtractor_4_out, subtractor_5_out;
  wire [5:5] subtractor_7_out;

  Clock clock_1 (.out(clock_1_out));
  Keyboard keyboard_1 (.clk(clock_1_out));  // open: re, clr, avail, data
  Button u_res (.out(res_out));
  latency latency_1 (.in(res_out), .out(latency_1_out));
  latency latency_2 (.in(latency_1_out), .out(latency_2_out));
  latency latency_3 (.in(latency_2_out), .out(latency_3_out));
  latency latency_4 (.in(latency_6_out), .out(latency_4_out));
  latency latency_5 (.in(latency_3_out), .out(latency_5_out));
  latency latency_6 (.in(latency_5_out), .out(latency_6_out));
  Button res_2 ();  // open: out
  Button res_3 ();  // open: out
  // OR_Gate or_1 is placed but not wired
  or or_2 (envRes, latency_4_out, latency_4_out);
  Comparator #(.width(7), .mode("unsigned")) comparator_1 (
    .a(keyboardIn), .b(7'b1110111), .eq(comparator_1_eq));  // open: gt, lt
  or or_3 (Wsign, comparator_1_eq, comparator_2_eq);
  Comparator #(.width(7), .mode("unsigned")) comparator_2 (
    .a(keyboardIn), .b(7'b1010111), .eq(comparator_2_eq));  // open: gt, lt
  Comparator #(.width(7), .mode("unsigned")) comparator_3 (
    .a(keyboardIn), .b(7'b1110011), .eq(comparator_3_eq));  // open: gt, lt
  or or_4 (Ssign, comparator_3_eq, comparator_4_eq);
  Comparator #(.width(7), .mode("unsigned")) comparator_4 (
    .a(keyboardIn), .b(7'b1010011), .eq(comparator_4_eq));  // open: gt, lt
  Comparator #(.width(7), .mode("unsigned")) comparator_5 (
    .a(keyboardIn), .b(7'b1100001), .eq(comparator_5_eq));  // open: gt, lt
  or or_5 (or_5_out, comparator_5_eq, comparator_6_eq);
  Comparator #(.width(7), .mode("unsigned")) comparator_6 (
    .a(keyboardIn), .b(7'b1000001), .eq(comparator_6_eq));  // open: gt, lt
  Comparator #(.width(7), .mode("unsigned")) comparator_7 (
    .a(keyboardIn), .b(7'b1100100), .eq(comparator_7_eq));  // open: gt, lt
  or or_6 (or_6_out, comparator_7_eq, comparator_8_eq);
  Comparator #(.width(7), .mode("unsigned")) comparator_8 (
    .a(keyboardIn), .b(7'b1000100), .eq(comparator_8_eq));  // open: gt, lt
  Comparator #(.width(3), .mode("unsigned")) comparator_9 (
    .a(lefter), .b(3'b001), .eq(comparator_9_eq));  // open: gt, lt
  Comparator #(.width(3), .mode("unsigned")) comparator_10 (
    .a(lefter), .b(3'b010), .eq(comparator_10_eq));  // open: gt, lt
  Comparator #(.width(3), .mode("unsigned")) comparator_11 (
    .a(lefter), .b(3'b100), .eq(comparator_11_eq));  // open: gt, lt
  Comparator #(.width(3), .mode("unsigned")) comparator_12 (
    .a(righter), .b(3'b001), .eq(comparator_12_eq));  // open: gt, lt
  Comparator #(.width(3), .mode("unsigned")) comparator_13 (
    .a(righter), .b(3'b010), .eq(comparator_13_eq));  // open: gt, lt
  Comparator #(.width(3), .mode("unsigned")) comparator_14 (
    .a(righter), .b(3'b100), .eq(comparator_14_eq));  // open: gt, lt
  Register #(.width(6)) register_1 (.D(incter), .Q(register_1_q), .clk(activateX), .clr(res));  // open: en
  not not_1 (not_1_out, DResP);
  or or_7 (or_7_out, or_5_out, or_6_out, comparator_9_eq, comparator_10_eq, comparator_11_eq, comparator_12_eq, comparator_13_eq, comparator_14_eq);
  not not_2 (not_2_out, DResM);
  Pull_Resistor pull_resistor_1 (.node(pull_resistor_1_node));
  Adder #(.width(6)) adder_1 (.a(register_1_q), .b(6'b001010), .out(adder_1_out));  // open: cin, cout
  assign pull_resistor_1_node = or_5_out ? adder_1_out : 6'bz;  // Controlled_Buffer controlled_buffer_1
  Subtractor #(.width(6)) subtractor_1 (.a(register_1_q), .b(6'b001010), .out(subtractor_1_out));  // open: bin, bout
  Pull_Resistor pull_resistor_2 (.node(pull_resistor_2_node));
  assign pull_resistor_2_node = or_6_out ? subtractor_1_out : 6'bz;  // Controlled_Buffer controlled_buffer_2
  Adder #(.width(6)) adder_2 (.a(register_1_q), .b(6'b000001), .out(adder_2_out));  // open: cin, cout
  assign controlled_buffer_3_out = comparator_9_eq ? adder_2_out : 6'bz;  // Controlled_Buffer controlled_buffer_3
  Adder #(.width(6)) adder_3 (.a(register_1_q), .b(6'b000010), .out(adder_3_out));  // open: cin, cout
  assign controlled_buffer_4_out = comparator_10_eq ? adder_3_out : 6'bz;  // Controlled_Buffer controlled_buffer_4
  Adder #(.width(6)) adder_4 (.a(register_1_q), .b(6'b000100), .out(adder_4_out));  // open: cin, cout
  assign controlled_buffer_5_out = comparator_11_eq ? adder_4_out : 6'bz;  // Controlled_Buffer controlled_buffer_5
  assign controlled_buffer_6_out = comparator_12_eq ? subtractor_2_out : 6'bz;  // Controlled_Buffer controlled_buffer_6
  Subtractor #(.width(6)) subtractor_2 (.a(register_1_q), .b(6'b000001), .out(subtractor_2_out));  // open: bin, bout
  assign controlled_buffer_7_out = comparator_13_eq ? subtractor_3_out : 6'bz;  // Controlled_Buffer controlled_buffer_7
  Subtractor #(.width(6)) subtractor_3 (.a(register_1_q), .b(6'b000010), .out(subtractor_3_out));  // open: bin, bout
  assign controlled_buffer_8_out = comparator_14_eq ? subtractor_4_out : 6'bz;  // Controlled_Buffer controlled_buffer_8
  Subtractor #(.width(6)) subtractor_4 (.a(register_1_q), .b(6'b000100), .out(subtractor_4_out));  // open: bin, bout
  or or_8 (or_8_out, Wsign, Ssign);
  or or_9 (or_9_out, Wsign, Ssign);
  and and_1 (activateX, not_1_out, or_7_out, not_2_out);
  Pull_Resistor pull_resistor_3 (.node(controlled_buffer_3_out));
  Pull_Resistor pull_resistor_4 (.node(controlled_buffer_4_out));
  Pull_Resistor pull_resistor_5 (.node(controlled_buffer_5_out));
  Pull_Resistor pull_resistor_6 (.node(controlled_buffer_6_out));
  Pull_Resistor pull_resistor_7 (.node(controlled_buffer_7_out));
  Pull_Resistor pull_resistor_8 (.node(controlled_buffer_8_out));
  Counter #(.width(4), .max('hf), .ongoal("stay")) counter_1 (
    .load(Wsign), .count(or_8_out), .Q(Y), .clk(or_9_out), .clr(res));  // open: D, carry
  assign or_10_out = pull_resistor_1_node | pull_resistor_2_node | controlled_buffer_3_out | controlled_buffer_4_out | controlled_buffer_5_out | controlled_buffer_6_out | controlled_buffer_7_out | controlled_buffer_8_out;  // OR_Gate or_10, 6 bits wide
  Subtractor #(.width(6)) subtractor_5 (.a(incter), .b(6'b011110), .out(subtractor_5_out));  // open: bin, bout
  assign controlled_buffer_9_out = DResP ? subtractor_5_out : 6'bz;  // Controlled_Buffer controlled_buffer_9
  Adder #(.width(6)) adder_5 (.a(incter), .b(6'b011110), .out(adder_5_out));  // open: cin, cout
  assign controlled_buffer_10_out = DResM ? adder_5_out : 6'bz;  // Controlled_Buffer controlled_buffer_10
  or or_11 (or_11_out, activateX, and_2_out);
  // Probe on controlled_buffer_11_out
  assign controlled_buffer_11_out = envRes ? 6'b010000 : 6'bz;  // Controlled_Buffer controlled_buffer_11
  Pull_Resistor pull_resistor_9 (.node(controlled_buffer_11_out));
  not not_3 (not_3_out, envRes);
  Pull_Resistor pull_resistor_10 (.node(controlled_buffer_9_out));
  Pull_Resistor pull_resistor_11 (.node(pull_resistor_11_node));
  assign pull_resistor_11_node = not_3_out ? controlled_buffer_10_out : 6'bz;  // Controlled_Buffer controlled_buffer_12
  assign controlled_buffer_13_out = or_11_out ? or_10_out : 6'bz;  // Controlled_Buffer controlled_buffer_13
  Pull_Resistor pull_resistor_12 (.node(controlled_buffer_13_out));
  // Probe on controlled_buffer_13_out
  not not_4 (not_4_out, DResM);
  not not_5 (not_5_out, DResP);
  // Probe on incter
  // Probe on controlled_buffer_9_out
  Register #(.width(6)) u_XM (.D(or_12_out), .Q(incter), .clk(or_13_out), .clr(res));  // open: en
  assign or_12_out = controlled_buffer_11_out | controlled_buffer_9_out | pull_resistor_11_node | controlled_buffer_13_out;  // OR_Gate or_12, 6 bits wide
  // Probe on pull_resistor_11_node
  or or_13 (or_13_out, and_2_out, latency_8_out, latency_7_out, latency_9_out);
  and and_2 (and_2_out, not_4_out, not_5_out, n8latency_1_out);
  latency latency_7 (.in(pull_resistor_14_node), .out(latency_7_out));
  latency latency_8 (.in(pull_resistor_13_node), .out(latency_8_out));
  latency latency_9 (.in(latency_10_out), .out(latency_9_out));
  latency latency_10 (.in(envRes), .out(latency_10_out));
  _8latency u_8latency_1 (.in(n8latency_2_out), .out(n8latency_1_out));
  _8latency u_8latency_2 (.in(activateX), .out(n8latency_2_out));
  Pull_Resistor pull_resistor_13 (.node(pull_resistor_13_node));
  assign pull_resistor_13_node = not_6_out ? DResP : 1'bz;  // Controlled_Buffer controlled_buffer_14
  Pull_Resistor pull_resistor_14 (.node(pull_resistor_14_node));
  assign pull_resistor_14_node = not_6_out ? DResM : 1'bz;  // Controlled_Buffer controlled_buffer_15
  not not_6 (not_6_out, envRes);
  Comparator #(.width(6), .mode("unsigned")) comparator_15 (
    .a(incter), .b({6{1'b0}}), .eq(comparator_15_eq));  // open: gt, lt
  not not_7 (not_7_out, comparator_15_eq);
  D_Flip_Flop u_state (.clk(not_7_out), .Q(state), .preset(not_7_out), .reset(res));  // open: D, Qn, en
  Pull_Resistor pull_resistor_15 (.node(pull_resistor_15_node));
  // OR_Gate or_14 has open pins: in0=latency_11_out, in1=controlled_buffer_16_out, in2=latency_13_out, in3=latency_15_out, out=open
  latency latency_11 (.in(latency_12_out), .out(latency_11_out));
  latency latency_12 (.in(activateX), .out(latency_12_out));
  assign controlled_buffer_16_out = not_8_out ? DResP : 1'bz;  // Controlled_Buffer controlled_buffer_16
  Pull_Resistor pull_resistor_16 (.node(controlled_buffer_16_out));
  not not_8 (not_8_out, envRes);
  Comparator #(.width(6), .mode("unsigned")) comparator_16 (.a(incter), .b(6'b101101), .gt(DResP));  // open: eq, lt
  Comparator #(.width(6), .mode("unsigned")) comparator_17 (.a(incter), .b(6'b010000), .lt(DResM));  // open: gt, eq
  latency latency_13 (.in(latency_14_out), .out(latency_13_out));
  latency latency_14 (.in(controlled_buffer_17_out), .out(latency_14_out));
  latency latency_15 (.in(latency_16_out), .out(latency_15_out));
  latency latency_16 (.in(envRes), .out(latency_16_out));
  assign controlled_buffer_17_out = not_8_out ? DResM : 1'bz;  // Controlled_Buffer controlled_buffer_17
  Pull_Resistor pull_resistor_17 (.node(controlled_buffer_17_out));
  Subtractor #(.width(3)) subtractor_6 (.a(incterD), .b(3'b001), .out(subtractor_6_out));  // open: bin, bout
  assign controlled_buffer_18_out = DResM ? subtractor_6_out : 3'bz;  // Controlled_Buffer controlled_buffer_18
  Pull_Resistor pull_resistor_18 (.node(pull_resistor_18_node));
  assign pull_resistor_18_node = envRes ? 3'b010 : 3'bz;  // Controlled_Buffer controlled_buffer_19
  assign controlled_buffer_20_out = DResP ? adder_6_out : 3'bz;  // Controlled_Buffer controlled_buffer_20
  Adder #(.width(3)) adder_6 (.a(incterD), .b(3'b001), .out(adder_6_out));  // open: cin, cout
  Pull_Resistor pull_resistor_19 (.node(pull_resistor_19_node));
  Pull_Resistor pull_resistor_20 (.node(controlled_buffer_18_out));
  assign or_15_out = controlled_buffer_18_out | pull_resistor_18_node | controlled_buffer_20_out;  // OR_Gate or_15, 3 bits wide
  or or_16 (or_16_out, latency_18_out, latency_17_out, latency_19_out);
  Pull_Resistor pull_resistor_21 (.node(controlled_buffer_20_out));
  latency latency_17 (.in(DResM), .out(latency_17_out));
  latency latency_18 (.in(DResP), .out(latency_18_out));
  Comparator #(.width(3), .mode("unsigned")) comparator_18 (
    .a(incterD), .b(3'b101), .gt(comparator_18_gt));  // open: eq, lt
  Comparator #(.width(3), .mode("unsigned")) comparator_19 (
    .a(incterD), .b(3'b010), .lt(comparator_19_lt));  // open: gt, eq
  Register #(.width(3)) u_XD (.D(or_15_out), .Q(incterD), .clk(or_16_out), .clr(res));  // open: en
  latency latency_19 (.in(latency_20_out), .out(latency_19_out));
  latency latency_20 (.in(latency_21_out), .out(latency_20_out));
  latency latency_21 (.in(latency_22_out), .out(latency_21_out));
  latency latency_22 (.in(latency_23_out), .out(latency_22_out));
  latency latency_23 (.in(envRes), .out(latency_23_out));
  or or_17 (or_17_out, comparator_18_gt, comparator_19_lt);
  and and_3 (die, or_17_out, state);
  Subtractor #(.width(6)) subtractor_7 (.a(incter), .b(6'b001111), .out({subtractor_7_out[5], XM}));  // open: bin, bout
  Subtractor #(.width(3)) subtractor_8 (.a(incterD), .b(3'b010), .out({subtractor_8_out[2], XD}));  // open: bin, bout

  // Other names for the same wires on the sheet: allRes = res

  // Notes on the sheet:
  //   w
  //   s
  //   a
  //   d
  //   >45 || <16
  //   D is <2 || > 5
endmodule

module register6bit (
  input  reset,
  input  write,
  input  [5:0] load,
  output [5:0] \output 
);

  wire and_1_out, and_2_out, and_3_out, and_4_out, and_5_out, and_6_out;
  wire [5:0] pull_resistor_2_node;

  Pull_Resistor pull_resistor_1 (.node(load));
  Pull_Resistor pull_resistor_2 (.node(pull_resistor_2_node));
  assign pull_resistor_2_node = write ? load : 6'bz;  // Controlled_Buffer controlled_buffer_1
  D_Flip_Flop d_ff_1 (.Q(\output [5]), .preset(and_2_out), .reset(reset));  // open: clk, D, Qn, en
  and and_1 (and_1_out, write, pull_resistor_2_node[4]);
  and and_2 (and_2_out, write, pull_resistor_2_node[5]);
  D_Flip_Flop d_ff_2 (.Q(\output [4]), .preset(and_1_out), .reset(reset));  // open: clk, D, Qn, en
  and and_3 (and_3_out, write, pull_resistor_2_node[3]);
  D_Flip_Flop d_ff_3 (.Q(\output [2]), .preset(and_4_out), .reset(reset));  // open: clk, D, Qn, en
  D_Flip_Flop d_ff_4 (.Q(\output [3]), .preset(and_3_out), .reset(reset));  // open: clk, D, Qn, en
  and and_4 (and_4_out, write, pull_resistor_2_node[2]);
  D_Flip_Flop d_ff_5 (.Q(\output [1]), .preset(and_5_out), .reset(reset));  // open: clk, D, Qn, en
  and and_5 (and_5_out, write, pull_resistor_2_node[1]);
  and and_6 (and_6_out, write, pull_resistor_2_node[0]);
  Pull_Resistor pull_resistor_3 (.node(\output ));
  D_Flip_Flop d_ff_6 (.Q(\output [0]), .preset(and_6_out), .reset(reset));  // open: clk, D, Qn, en
endmodule

// 2
module _2latency (
  input  in,
  output out
);

  wire not_1_out;

  not not_1 (not_1_out, in);
  not not_2 (out, not_1_out);
endmodule

// 4
module _4latency (
  input  in,
  output out
);

  wire not_1_out, not_2_out, not_4_out;

  not not_1 (not_1_out, not_2_out);
  not not_2 (not_2_out, in);
  not not_3 (out, not_4_out);
  not not_4 (not_4_out, not_1_out);
endmodule

// 8
module _8latency (
  input  in,
  output out
);

  wire not_1_out, not_2_out, not_3_out, not_4_out, not_5_out, not_6_out, not_7_out;

  not not_1 (not_1_out, not_2_out);
  not not_2 (not_2_out, in);
  not not_3 (not_3_out, not_4_out);
  not not_4 (not_4_out, not_1_out);
  not not_5 (not_5_out, not_6_out);
  not not_6 (not_6_out, not_3_out);
  not not_7 (not_7_out, not_5_out);
  not not_8 (out, not_7_out);
endmodule

// B
module biglatency (
  input  in,
  output out
);

  wire not_1_out, not_2_out, not_3_out, not_4_out, not_5_out, not_6_out, not_7_out, not_8_out, not_9_out,
       not_10_out, not_11_out, not_12_out, not_13_out, not_14_out, not_15_out, not_16_out, not_17_out,
       not_18_out, not_19_out, not_20_out, not_21_out, not_22_out, not_23_out, not_24_out, not_25_out,
       not_26_out, not_27_out, not_28_out, not_29_out, not_30_out, not_32_out;

  not not_1 (not_1_out, in);
  not not_2 (not_2_out, not_1_out);
  not not_3 (not_3_out, not_2_out);
  not not_4 (not_4_out, not_3_out);
  not not_5 (not_5_out, not_6_out);
  not not_6 (not_6_out, not_4_out);
  not not_7 (not_7_out, not_5_out);
  not not_8 (not_8_out, not_10_out);
  not not_9 (not_9_out, not_7_out);
  not not_10 (not_10_out, not_9_out);
  not not_11 (not_11_out, not_13_out);
  not not_12 (not_12_out, not_8_out);
  not not_13 (not_13_out, not_14_out);
  not not_14 (not_14_out, not_12_out);
  not not_15 (not_15_out, not_17_out);
  not not_16 (not_16_out, not_11_out);
  not not_17 (not_17_out, not_18_out);
  not not_18 (not_18_out, not_16_out);
  not not_19 (not_19_out, not_15_out);
  not not_20 (not_20_out, not_21_out);
  not not_21 (not_21_out, not_19_out);
  not not_22 (not_22_out, not_20_out);
  not not_23 (not_23_out, not_24_out);
  not not_24 (not_24_out, not_22_out);
  not not_25 (not_25_out, not_26_out);
  not not_26 (not_26_out, not_23_out);
  not not_27 (not_27_out, not_30_out);
  not not_28 (not_28_out, not_29_out);
  not not_29 (not_29_out, not_27_out);
  not not_30 (not_30_out, not_25_out);
  not not_31 (out, not_32_out);
  not not_32 (not_32_out, not_28_out);
endmodule

module keyboard (
  input  [6:0] keyboardIn,
  input  [2:0] lefter,
  input  [2:0] righter,
  input  res,
  output [3:0] Y,
  output [4:0] XM,
  output [1:0] XD,
  output die
);

  wire activateX, allRes, and_1_out, and_3_out, and_4_out, and_5_out, and_6_out, and_7_out, approx,
       biglatency_1_out, biglatency_2_out, biglatency_3_out, comparator_1_eq, comparator_2_eq,
       comparator_3_eq, comparator_4_eq, comparator_5_eq, comparator_6_eq, comparator_7_eq, comparator_8_eq,
       comparator_9_eq, comparator_10_eq, comparator_11_eq, comparator_12_eq, comparator_13_eq,
       comparator_14_eq, comparator_15_eq, comparator_16_eq, comparator_17_eq, comparator_18_eq,
       comparator_19_gt, comparator_20_gt, comparator_21_eq, comparator_22_eq, comparator_23_eq,
       comparator_24_gt, comparator_25_lt, comparator_26_gt, comparator_27_lt, controlled_buffer_19_out,
       controlled_buffer_20_out, controlled_buffer_24_out, controlled_buffer_26_out,
       controlled_buffer_27_out, DResM, DResP, envRes, latency_2_out, latency_3_out, latency_4_out,
       latency_5_out, latency_6_out, latency_7_out, latency_8_out, latency_9_out, latency_10_out,
       n2latency_1_out, n2latency_2_out, n2latency_3_out, n2latency_4_out, n2latency_5_out, n4latency_1_out,
       n8latency_1_out, n8latency_2_out, n8latency_5_out, n8latency_6_out, not_1_out, not_2_out, not_3_out,
       not_4_out, not_5_out, not_6_out, not_7_out, not_8_out, not_9_out, not_10_out, not_11_out, not_12_out,
       not_13_out, not_14_out, not_15_out, not_16_out, or_2_out, or_3_out, or_6_out, or_7_out, or_8_out,
       or_10_out, or_11_out, or_13_out, or_17_out, or_18_out, pull_resistor_1_node, pull_resistor_25_node,
       pull_resistor_30_node, pull_resistor_31_node, pull_resistor_32_node, res_out, Ssign, state, undriven,
       undriven_2, undriven_3, Wsign;
  wire [2:0] adder_6_out, controlled_buffer_1_out, controlled_buffer_2_out, controlled_buffer_30_out,
       incterD, or_16_out, pull_resistor_27_node, pull_resistor_28_node, subtractor_6_out, subtractor_8_out;
  wire [5:0] adder_1_out, adder_2_out, adder_3_out, adder_4_out, adder_5_out, controlled_buffer_3_out,
       controlled_buffer_5_out, controlled_buffer_6_out, controlled_buffer_7_out, controlled_buffer_8_out,
       controlled_buffer_9_out, controlled_buffer_10_out, controlled_buffer_11_out, controlled_buffer_12_out,
       controlled_buffer_13_out, controlled_buffer_14_out, controlled_buffer_17_out,
       controlled_buffer_18_out, controlled_buffer_21_out, controlled_buffer_22_out, incter, near, or_9_out,
       or_12_out, or_14_out, pull_resistor_5_node, pull_resistor_13_node, pull_resistor_14_node,
       pull_resistor_21_node, subtractor_1_out, subtractor_2_out, subtractor_3_out, subtractor_4_out,
       subtractor_5_out;
  wire [5:5] subtractor_7_out;

  Button u_res (.out(res_out));
  Pull_Resistor pull_resistor_1 (.node(pull_resistor_1_node));
  or or_1 (allRes, res_out, pull_resistor_1_node, res);
  Button res_2 ();  // open: out
  latency latency_1 (.in(allRes), .out(envRes));
  assign controlled_buffer_1_out = comparator_1_eq ? lefter : 3'bz;  // Controlled_Buffer controlled_buffer_1
  assign controlled_buffer_2_out = comparator_1_eq ? righter : 3'bz;  // Controlled_Buffer controlled_buffer_2
  Pull_Resistor pull_resistor_2 (.node(controlled_buffer_1_out));
  Pull_Resistor pull_resistor_3 (.node(controlled_buffer_2_out));
  _8latency u_8latency_1 (.in(comparator_1_eq), .out(n8latency_1_out));
  Comparator #(.width(7), .mode("unsigned")) comparator_1 (
    .a(keyboardIn), .b({7{1'b0}}), .eq(comparator_1_eq));  // open: gt, lt
  latency latency_2 (.in(undriven), .out(latency_2_out));
  Comparator #(.width(7), .mode("unsigned")) comparator_2 (
    .a(keyboardIn), .b(7'b1100001), .eq(comparator_2_eq));  // open: gt, lt
  or or_2 (or_2_out, comparator_2_eq, comparator_3_eq);
  Comparator #(.width(7), .mode("unsigned")) comparator_3 (
    .a(keyboardIn), .b(7'b1000001), .eq(comparator_3_eq));  // open: gt, lt
  Comparator #(.width(7), .mode("unsigned")) comparator_4 (
    .a(keyboardIn), .b(7'b1100100), .eq(comparator_4_eq));  // open: gt, lt
  or or_3 (or_3_out, comparator_4_eq, comparator_5_eq);
  Comparator #(.width(7), .mode("unsigned")) comparator_5 (
    .a(keyboardIn), .b(7'b1000100), .eq(comparator_5_eq));  // open: gt, lt
  Comparator #(.width(3), .mode("unsigned")) comparator_6 (
    .a(controlled_buffer_1_out), .b(3'b001), .eq(comparator_6_eq));  // open: gt, lt
  Comparator #(.width(3), .mode("unsigned")) comparator_7 (
    .a(controlled_buffer_1_out), .b(3'b010), .eq(comparator_7_eq));  // open: gt, lt
  Comparator #(.width(3), .mode("unsigned")) comparator_8 (
    .a(controlled_buffer_1_out), .b(3'b100), .eq(comparator_8_eq));  // open: gt, lt
  Comparator #(.width(3), .mode("unsigned")) comparator_9 (
    .a(controlled_buffer_2_out), .b(3'b001), .eq(comparator_9_eq));  // open: gt, lt
  Comparator #(.width(3), .mode("unsigned")) comparator_10 (
    .a(controlled_buffer_2_out), .b(3'b010), .eq(comparator_10_eq));  // open: gt, lt
  Comparator #(.width(3), .mode("unsigned")) comparator_11 (
    .a(controlled_buffer_2_out), .b(3'b100), .eq(comparator_11_eq));  // open: gt, lt
  and and_1 (and_1_out, n8latency_1_out, latency_2_out, undriven, n2latency_1_out, n4latency_1_out);
  _2latency u_2latency_1 (.in(undriven), .out(n2latency_1_out));
  _4latency u_4latency_1 (.in(undriven), .out(n4latency_1_out));
  Comparator #(.width(7), .mode("unsigned")) comparator_12 (
    .a(keyboardIn), .b(7'b1110111), .eq(comparator_12_eq));  // open: gt, lt
  Comparator #(.width(7), .mode("unsigned")) comparator_13 (
    .a(keyboardIn), .b(7'b1010111), .eq(comparator_13_eq));  // open: gt, lt
  Comparator #(.width(7), .mode("unsigned")) comparator_14 (
    .a(keyboardIn), .b(7'b1110011), .eq(comparator_14_eq));  // open: gt, lt
  Comparator #(.width(7), .mode("unsigned")) comparator_15 (
    .a(keyboardIn), .b(7'b1010011), .eq(comparator_15_eq));  // open: gt, lt
  or or_4 (Wsign, comparator_12_eq, comparator_13_eq);
  or or_5 (Ssign, comparator_14_eq, comparator_15_eq);
  not not_1 (not_1_out, DResP);
  or or_6 (or_6_out, or_2_out, or_3_out, comparator_6_eq, comparator_7_eq, comparator_8_eq, comparator_9_eq, comparator_10_eq, comparator_11_eq);
  not not_2 (not_2_out, DResM);
  assign controlled_buffer_3_out = or_2_out ? adder_1_out : 6'bz;  // Controlled_Buffer controlled_buffer_3
  Pull_Resistor pull_resistor_4 (.node(controlled_buffer_3_out));
  Adder #(.width(6)) adder_1 (.a(incter), .b(6'b001010), .out(adder_1_out));  // open: cin, cout
  Subtractor #(.width(6)) subtractor_1 (.a(incter), .b(6'b001010), .out(subtractor_1_out));  // open: bin, bout
  Pull_Resistor pull_resistor_5 (.node(pull_resistor_5_node));
  assign pull_resistor_5_node = or_3_out ? subtractor_1_out : 6'bz;  // Controlled_Buffer controlled_buffer_4
  assign controlled_buffer_5_out = comparator_6_eq ? adder_2_out : 6'bz;  // Controlled_Buffer controlled_buffer_5
  Adder #(.width(6)) adder_2 (.a(incter), .b(6'b000001), .out(adder_2_out));  // open: cin, cout
  assign controlled_buffer_6_out = comparator_7_eq ? adder_3_out : 6'bz;  // Controlled_Buffer controlled_buffer_6
  Adder #(.width(6)) adder_3 (.a(incter), .b(6'b000010), .out(adder_3_out));  // open: cin, cout
  assign controlled_buffer_7_out = comparator_8_eq ? adder_4_out : 6'bz;  // Controlled_Buffer controlled_buffer_7
  Adder #(.width(6)) adder_4 (.a(incter), .b(6'b000100), .out(adder_4_out));  // open: cin, cout
  assign controlled_buffer_8_out = comparator_9_eq ? subtractor_2_out : 6'bz;  // Controlled_Buffer controlled_buffer_8
  Subtractor #(.width(6)) subtractor_2 (.a(incter), .b(6'b000001), .out(subtractor_2_out));  // open: bin, bout
  assign controlled_buffer_9_out = comparator_10_eq ? subtractor_3_out : 6'bz;  // Controlled_Buffer controlled_buffer_9
  Subtractor #(.width(6)) subtractor_3 (.a(incter), .b(6'b000010), .out(subtractor_3_out));  // open: bin, bout
  Subtractor #(.width(6)) subtractor_4 (.a(incter), .b(6'b000100), .out(subtractor_4_out));  // open: bin, bout
  assign controlled_buffer_10_out = comparator_11_eq ? subtractor_4_out : 6'bz;  // Controlled_Buffer controlled_buffer_10
  Register #(.width(6)) register_1 ();  // open: D, en, Q, clk, clr
  or or_7 (or_7_out, Ssign, Wsign);
  or or_8 (or_8_out, Ssign, Wsign);
  and and_2 (activateX, not_1_out, or_6_out, not_2_out);
  Pull_Resistor pull_resistor_6 (.node(controlled_buffer_5_out));
  Pull_Resistor pull_resistor_7 (.node(controlled_buffer_6_out));
  Pull_Resistor pull_resistor_8 (.node(controlled_buffer_7_out));
  Pull_Resistor pull_resistor_9 (.node(controlled_buffer_8_out));
  Pull_Resistor pull_resistor_10 (.node(controlled_buffer_9_out));
  Pull_Resistor pull_resistor_11 (.node(controlled_buffer_10_out));
  Counter #(.width(4), .max('hf), .ongoal("stay")) counter_1 (
    .load(Ssign), .count(or_7_out), .Q(Y), .clk(or_8_out), .clr(allRes));  // open: D, carry
  assign or_9_out = controlled_buffer_3_out | pull_resistor_5_node | controlled_buffer_5_out | controlled_buffer_6_out | controlled_buffer_7_out | controlled_buffer_8_out | controlled_buffer_9_out | controlled_buffer_10_out;  // OR_Gate or_9, 6 bits wide
  assign controlled_buffer_11_out = DResP ? subtractor_5_out : 6'bz;  // Controlled_Buffer controlled_buffer_11
  Subtractor #(.width(6)) subtractor_5 (.a(incter), .b(6'b011110), .out(subtractor_5_out));  // open: bin, bout
  assign controlled_buffer_12_out = approx ? near : 6'bz;  // Controlled_Buffer controlled_buffer_12
  Adder #(.width(6)) adder_5 (.a(incter), .b(6'b011110), .out(adder_5_out));  // open: cin, cout
  assign controlled_buffer_13_out = DResM ? adder_5_out : 6'bz;  // Controlled_Buffer controlled_buffer_13
  or or_10 (or_10_out, activateX, and_6_out);
  Comparator #(.width(6), .mode("unsigned")) comparator_16 (
    .a(incter), .b(6'b010000), .eq(comparator_16_eq));  // open: gt, lt
  Comparator #(.width(6), .mode("unsigned")) comparator_17 (
    .a(incter), .b(6'b011010), .eq(comparator_17_eq));  // open: gt, lt
  Comparator #(.width(6), .mode("unsigned")) comparator_18 (
    .a(incter), .b(6'b100100), .eq(comparator_18_eq));  // open: gt, lt
  Comparator #(.width(6), .mode("unsigned")) comparator_19 (
    .a(incter), .b(6'b010100), .gt(comparator_19_gt));  // open: eq, lt
  Comparator #(.width(6), .mode("unsigned")) comparator_20 (
    .a(incter), .b(6'b011110), .gt(comparator_20_gt));  // open: eq, lt
  // Probe on controlled_buffer_14_out
  assign controlled_buffer_14_out = envRes ? 6'b010000 : 6'bz;  // Controlled_Buffer controlled_buffer_14
  Pull_Resistor pull_resistor_12 (.node(controlled_buffer_14_out));
  not not_3 (not_3_out, envRes);
  Pull_Resistor pull_resistor_13 (.node(pull_resistor_13_node));
  assign pull_resistor_13_node = not_3_out ? controlled_buffer_11_out : 6'bz;  // Controlled_Buffer controlled_buffer_15
  Pull_Resistor pull_resistor_14 (.node(pull_resistor_14_node));
  assign pull_resistor_14_node = not_3_out ? controlled_buffer_12_out : 6'bz;  // Controlled_Buffer controlled_buffer_16
  assign controlled_buffer_17_out = not_3_out ? controlled_buffer_13_out : 6'bz;  // Controlled_Buffer controlled_buffer_17
  Pull_Resistor pull_resistor_15 (.node(controlled_buffer_17_out));
  assign controlled_buffer_18_out = or_10_out ? or_9_out : 6'bz;  // Controlled_Buffer controlled_buffer_18
  Pull_Resistor pull_resistor_16 (.node(controlled_buffer_18_out));
  // Probe on controlled_buffer_18_out
  not not_4 (not_4_out, DResM);
  not not_5 (not_5_out, DResP);
  not not_6 (not_6_out, comparator_16_eq);
  not not_7 (not_7_out, comparator_17_eq);
  and and_3 (and_3_out, not_6_out, not_7_out, not_8_out);
  not not_8 (not_8_out, comparator_18_eq);
  and and_4 (and_4_out, not_10_out, not_9_out);
  not not_9 (not_9_out, comparator_19_gt);
  and and_5 (and_5_out, comparator_19_gt, not_10_out);
  not not_10 (not_10_out, comparator_20_gt);
  or or_11 (or_11_out, comparator_20_gt, and_5_out, and_4_out);
  // Probe on incter
  // Probe on pull_resistor_13_node
  assign or_12_out = controlled_buffer_14_out | pull_resistor_13_node | pull_resistor_14_node | controlled_buffer_17_out | controlled_buffer_18_out;  // OR_Gate or_12, 6 bits wide
  Register #(.width(6)) u_XM (.D(or_12_out), .Q(incter), .clk(or_13_out), .clr(undriven_2));  // open: en
  // Probe on controlled_buffer_17_out
  or or_13 (or_13_out, and_6_out, biglatency_1_out, latency_4_out, biglatency_2_out, n2latency_2_out);
  and and_6 (and_6_out, not_4_out, not_5_out, n8latency_2_out);
  biglatency biglatency_1 (.in(controlled_buffer_20_out), .out(biglatency_1_out));
  biglatency biglatency_2 (.in(controlled_buffer_19_out), .out(biglatency_2_out));
  _8latency u_8latency_2 (.in(activateX), .out(n8latency_2_out));
  assign controlled_buffer_19_out = state ? DResM : 1'bz;  // Controlled_Buffer controlled_buffer_19
  assign controlled_buffer_20_out = state ? DResP : 1'bz;  // Controlled_Buffer controlled_buffer_20
  Pull_Resistor pull_resistor_17 (.node(controlled_buffer_19_out));
  Pull_Resistor pull_resistor_18 (.node(controlled_buffer_20_out));
  Comparator #(.width(4), .mode("unsigned")) comparator_21 (.a(Y), .b(4'b0110), .eq(comparator_21_eq));  // open: gt, lt
  Comparator #(.width(6), .mode("unsigned")) comparator_22 (
    .a(incter), .b(6'b101110), .eq(comparator_22_eq));  // open: gt, lt
  not not_11 (not_11_out, comparator_22_eq);
  assign controlled_buffer_21_out = and_4_out ? 6'b010000 : 6'bz;  // Controlled_Buffer controlled_buffer_21
  Pull_Resistor pull_resistor_19 (.node(controlled_buffer_21_out));
  assign controlled_buffer_22_out = and_5_out ? 6'b011010 : 6'bz;  // Controlled_Buffer controlled_buffer_22
  Pull_Resistor pull_resistor_20 (.node(controlled_buffer_22_out));
  Pull_Resistor pull_resistor_21 (.node(pull_resistor_21_node));
  assign pull_resistor_21_node = comparator_20_gt ? 6'b100100 : 6'bz;  // Controlled_Buffer controlled_buffer_23
  not not_12 (not_12_out, envRes);
  latency latency_3 (.in(not_12_out), .out(latency_3_out));
  biglatency biglatency_3 (.in(not_13_out), .out(biglatency_3_out));
  not not_13 (not_13_out, activateX);
  Comparator #(.width(6), .mode("unsigned")) comparator_23 (
    .a(incter), .b({6{1'b0}}), .eq(comparator_23_eq));  // open: gt, lt
  _2latency u_2latency_2 (.in(envRes), .out(n2latency_2_out));
  latency latency_4 (.in(controlled_buffer_24_out), .out(latency_4_out));
  assign controlled_buffer_24_out = state ? approx : 1'bz;  // Controlled_Buffer controlled_buffer_24
  Pull_Resistor pull_resistor_22 (.node(controlled_buffer_24_out));
  and and_7 (and_7_out, comparator_21_eq, not_11_out, and_3_out);
  assign near = and_7_out ? or_14_out : 6'bz;  // Controlled_Buffer controlled_buffer_25
  assign or_14_out = controlled_buffer_21_out | controlled_buffer_22_out | pull_resistor_21_node;  // OR_Gate or_14, 6 bits wide
  Pull_Resistor pull_resistor_23 (.node(near));
  D_Flip_Flop u_state (.clk(not_14_out), .Q(state), .preset(not_14_out), .reset(allRes));  // open: D, Qn, en
  not not_14 (not_14_out, comparator_23_eq);
  _8latency u_8latency_3 ();  // open: in, out
  _8latency u_8latency_4 ();  // open: in, out
  // OR_Gate or_15 has open pins: in0=latency_5_out, in1=controlled_buffer_26_out, in2=latency_7_out, in3=latency_9_out, out=open
  latency latency_5 (.in(latency_6_out), .out(latency_5_out));
  latency latency_6 (.in(activateX), .out(latency_6_out));
  assign controlled_buffer_26_out = not_15_out ? DResP : 1'bz;  // Controlled_Buffer controlled_buffer_26
  Pull_Resistor pull_resistor_24 (.node(controlled_buffer_26_out));
  not not_15 (not_15_out, envRes);
  and and_8 (approx, and_7_out, state, or_11_out, not_12_out, latency_3_out, not_13_out, biglatency_3_out);
  Pull_Resistor pull_resistor_25 (.node(pull_resistor_25_node));
  latency latency_7 (.in(latency_8_out), .out(latency_7_out));
  latency latency_8 (.in(controlled_buffer_27_out), .out(latency_8_out));
  latency latency_9 (.in(latency_10_out), .out(latency_9_out));
  latency latency_10 (.in(envRes), .out(latency_10_out));
  assign controlled_buffer_27_out = not_15_out ? DResM : 1'bz;  // Controlled_Buffer controlled_buffer_27
  Pull_Resistor pull_resistor_26 (.node(controlled_buffer_27_out));
  Pull_Resistor pull_resistor_27 (.node(pull_resistor_27_node));
  assign pull_resistor_27_node = DResM ? subtractor_6_out : 3'bz;  // Controlled_Buffer controlled_buffer_28
  Subtractor #(.width(3)) subtractor_6 (.a(incterD), .b(3'b001), .out(subtractor_6_out));  // open: bin, bout
  Pull_Resistor pull_resistor_28 (.node(pull_resistor_28_node));
  assign pull_resistor_28_node = envRes ? 3'b010 : 3'bz;  // Controlled_Buffer controlled_buffer_29
  Adder #(.width(3)) adder_6 (.a(incterD), .b(3'b001), .out(adder_6_out));  // open: cin, cout
  assign controlled_buffer_30_out = DResP ? adder_6_out : 3'bz;  // Controlled_Buffer controlled_buffer_30
  Comparator #(.width(6), .mode("unsigned")) comparator_24 (
    .a(incter), .b(6'b101101), .gt(comparator_24_gt));  // open: eq, lt
  Comparator #(.width(6), .mode("unsigned")) comparator_25 (
    .a(incter), .b(6'b010000), .lt(comparator_25_lt));  // open: gt, eq
  // Probe on pull_resistor_27_node
  assign or_16_out = pull_resistor_27_node | pull_resistor_28_node | controlled_buffer_30_out;  // OR_Gate or_16, 3 bits wide
  // Probe on pull_resistor_28_node
  // Probe on or_16_out
  or or_17 (or_17_out, n2latency_4_out, n2latency_3_out, n2latency_5_out);
  Pull_Resistor pull_resistor_29 (.node(controlled_buffer_30_out));
  // Probe on controlled_buffer_30_out
  _2latency u_2latency_3 (.in(n8latency_6_out), .out(n2latency_3_out));
  _2latency u_2latency_4 (.in(n8latency_5_out), .out(n2latency_4_out));
  _8latency u_8latency_5 (.in(pull_resistor_30_node), .out(n8latency_5_out));
  _8latency u_8latency_6 (.in(pull_resistor_31_node), .out(n8latency_6_out));
  Pull_Resistor pull_resistor_30 (.node(pull_resistor_30_node));
  assign pull_resistor_30_node = not_16_out ? DResP : 1'bz;  // Controlled_Buffer controlled_buffer_31
  Pull_Resistor pull_resistor_31 (.node(pull_resistor_31_node));
  assign pull_resistor_31_node = not_16_out ? DResM : 1'bz;  // Controlled_Buffer controlled_buffer_32
  not not_16 (not_16_out, envRes);
  and and_9 (DResP, comparator_24_gt, state);
  and and_10 (DResM, state, comparator_25_lt);
  Register #(.width(3)) u_XD (.D(or_16_out), .Q(incterD), .clk(or_17_out), .clr(undriven_3));  // open: en
  _2latency u_2latency_5 (.in(envRes), .out(n2latency_5_out));
  Pull_Resistor pull_resistor_32 (.node(pull_resistor_32_node));
  Subtractor #(.width(6)) subtractor_7 (.a(incter), .b(6'b010000), .out({subtractor_7_out[5], XM}));  // open: bin, bout
  Subtractor #(.width(3)) subtractor_8 (.a(incterD), .b(3'b010), .out(subtractor_8_out));  // open: bin, bout
  Comparator #(.width(3), .mode("unsigned")) comparator_26 (
    .a(incterD), .b(3'b101), .gt(comparator_26_gt));  // open: eq, lt
  Comparator #(.width(3), .mode("unsigned")) comparator_27 (
    .a(incterD), .b(3'b010), .lt(comparator_27_lt));  // open: gt, eq
  or or_18 (or_18_out, comparator_26_gt, comparator_27_lt);
  and and_11 (die, or_18_out, state);
  Adder #(.width(2)) adder_7 (.a(subtractor_8_out[1:0]), .b(2'b01), .out(XD));  // open: cin, cout

  // Notes on the sheet:
  //   a
  //   d
  //   w
  //   s
  //   >45 || <16
  //   D is <2 || > 5
endmodule
