// Logisim project plain_dead.circ as structural Verilog: 22 circuits, main circuit main
module main (
  output [3:0] out_1,
  output [4:0] out_2,
  output [1:0] out_3
);

  wire _0, _1, _2, _8, _9, _11, carconnectorv2_1_outflag, carconnectorv2_2_outflag, carconnectorv2_3_outflag,
       carconnectorv2_4_outflag, carconnectorv2_5_outflag, carconnectorv2_6_outflag,
       carconnectorv2_7_outflag, carconnectorv2_8_outflag, carconnectorv2_9_outflag,
       carconnectorv2_10_outflag, carconnectorv2_11_outflag, carconnectorv2_12_outflag,
       carconnectorv2_13_outflag, carconnectorv2_14_outflag, carconnectorv2_15_outflag, clock_1_out,
       clock_2_out, comparator_1_eq, comparator_2_eq, comparator_3_eq, comparator_4_eq,
       computeintresection_1_outintersect, computeintresection_2_outintersect,
       computeintresection_3_outintersect, controlled_buffer_1_out, heightflag_4_eqy, heightflag_5_eqy,
       heightflag_6_eqy, heightflag_7_eqy, heightflag_11_eqy, log_1x1_1_outflag, log_1x1_2_outflag,
       log_1x1_3_outflag, log_2x1_1_outflag, log_2x1_3_outflag, log_2x1_4_outflag, log_3x2_1_outflag,
       log_3x2_3_outflag, log_3x2_4_outflag, not_1_out, res_out, stop_out, stopgame_1_stopper,
       swamp_1_outflag, swamp_2_outflag, swamp_3_outflag, swamp_4_outflag, swamp_5_outflag, swamp_6_outflag,
       undriven, undriven_2, waterintersect_1_outintersect, waterintersect_2_outintersect;
  wire [1:0] carconnectorv2_1_outbackshiftd, carconnectorv2_1_outplayershiftd,
       carconnectorv2_2_outbackshiftd, carconnectorv2_2_outplayershiftd, carconnectorv2_3_outbackshiftd,
       carconnectorv2_3_outplayershiftd, carconnectorv2_4_outbackshiftd, carconnectorv2_4_outplayershiftd,
       carconnectorv2_5_outbackshiftd, carconnectorv2_5_outplayershiftd, carconnectorv2_6_outbackshiftd,
       carconnectorv2_6_outplayershiftd, carconnectorv2_7_outbackshiftd, carconnectorv2_7_outplayershiftd,
       carconnectorv2_8_outbackshiftd, carconnectorv2_8_outplayershiftd, carconnectorv2_9_outbackshiftd,
       carconnectorv2_9_outplayershiftd, carconnectorv2_10_outbackshiftd, carconnectorv2_10_outplayershiftd,
       carconnectorv2_11_outbackshiftd, carconnectorv2_11_outplayershiftd, carconnectorv2_12_outbackshiftd,
       carconnectorv2_12_outplayershiftd, carconnectorv2_13_outbackshiftd, carconnectorv2_13_outplayershiftd,
       carconnectorv2_14_outbackshiftd, carconnectorv2_14_outplayershiftd, carconnectorv2_15_outbackshiftd,
       carconnectorv2_15_outplayershiftd, leftshifter_1_shiftd, leftshifter_2_shiftd,
       log_1x1_1_outbackshiftd, log_1x1_1_outplayershiftd, log_1x1_2_outbackshiftd,
       log_1x1_2_outplayershiftd, log_1x1_3_outbackshiftd, log_1x1_3_outplayershiftd,
       log_2x1_1_outbackshiftd, log_2x1_1_outplayershiftd, log_2x1_3_outbackshiftd,
       log_2x1_3_outplayershiftd, log_2x1_4_outbackshiftd, log_2x1_4_outplayershiftd,
       log_3x2_1_outbackshiftd, log_3x2_1_outplayershiftd, log_3x2_3_outbackshiftd,
       log_3x2_3_outplayershiftd, log_3x2_4_outbackshiftd, log_3x2_4_outplayershiftd, rightshifter_1_shiftd,
       rightshifter_2_shiftd, rightshifter_3_shiftd, rightshifter_4_shiftd, rightshifter_5_shiftd,
       swamp_1_outplayershiftd, swamp_2_outplayershiftd, swamp_3_outplayershiftd, swamp_4_outplayershiftd,
       swamp_5_outplayershiftd, swamp_6_outplayershiftd;
  wire [4:0] carconnectorv2_1_outplayershiftm, carconnectorv2_1_outputbackshiftm,
       carconnectorv2_2_outplayershiftm, carconnectorv2_2_outputbackshiftm, carconnectorv2_3_outplayershiftm,
       carconnectorv2_3_outputbackshiftm, carconnectorv2_4_outplayershiftm,
       carconnectorv2_4_outputbackshiftm, carconnectorv2_5_outplayershiftm,
       carconnectorv2_5_outputbackshiftm, carconnectorv2_6_outplayershiftm,
       carconnectorv2_6_outputbackshiftm, carconnectorv2_7_outplayershiftm,
       carconnectorv2_7_outputbackshiftm, carconnectorv2_8_outplayershiftm,
       carconnectorv2_8_outputbackshiftm, carconnectorv2_9_outplayershiftm,
       carconnectorv2_9_outputbackshiftm, carconnectorv2_10_outplayershiftm,
       carconnectorv2_10_outputbackshiftm, carconnectorv2_11_outplayershiftm,
       carconnectorv2_11_outputbackshiftm, carconnectorv2_12_outplayershiftm,
       carconnectorv2_12_outputbackshiftm, carconnectorv2_13_outplayershiftm,
       carconnectorv2_13_outputbackshiftm, carconnectorv2_14_outplayershiftm,
       carconnectorv2_14_outputbackshiftm, carconnectorv2_15_outplayershiftm,
       carconnectorv2_15_outputbackshiftm, leftshifter_1_shiftm, leftshifter_2_shiftm,
       log_1x1_1_outplayershiftm, log_1x1_1_outputbackshiftm, log_1x1_2_outplayershiftm,
       log_1x1_2_outputbackshiftm, log_1x1_3_outplayershiftm, log_1x1_3_outputbackshiftm,
       log_2x1_1_outplayershiftm, log_2x1_1_outputbackshiftm, log_2x1_3_outplayershiftm,
       log_2x1_3_outputbackshiftm, log_2x1_4_outplayershiftm, log_2x1_4_outputbackshiftm,
       log_3x2_1_outplayershiftm, log_3x2_1_outputbackshiftm, log_3x2_3_outplayershiftm,
       log_3x2_3_outputbackshiftm, log_3x2_4_outplayershiftm, log_3x2_4_outputbackshiftm,
       rightshifter_1_shiftm, rightshifter_2_shiftm, rightshifter_3_shiftm, rightshifter_4_shiftm,
       rightshifter_5_shiftm, swamp_1_outplayershiftm, swamp_2_outplayershiftm, swamp_3_outplayershiftm,
       swamp_4_outplayershiftm, swamp_5_outplayershiftm, swamp_6_outplayershiftm;
  wire [6:0] keyboard_1_data;
  wire [29:0] carconnectorv2_1_tobackground, carconnectorv2_1_tobackground_2,
       carconnectorv2_1_tobackground_3, carconnectorv2_1_tobackground_4, carconnectorv2_1_tobackground_5,
       carconnectorv2_1_tobackground_6, carconnectorv2_1_tobackground_7, carconnectorv2_1_tobackground_8,
       carconnectorv2_1_tobackground_9, carconnectorv2_1_tobackground_10, carconnectorv2_1_tofront,
       carconnectorv2_1_tofront_2, carconnectorv2_1_tofront_3, carconnectorv2_1_tofront_4,
       carconnectorv2_1_tofront_5, carconnectorv2_1_tofront_6, carconnectorv2_1_tofront_7,
       carconnectorv2_1_tofront_8, carconnectorv2_1_tofront_9, carconnectorv2_1_tofront_10,
       carconnectorv2_2_tobackground, carconnectorv2_2_tobackground_2, carconnectorv2_2_tobackground_3,
       carconnectorv2_2_tobackground_4, carconnectorv2_2_tobackground_5, carconnectorv2_2_tobackground_6,
       carconnectorv2_2_tobackground_7, carconnectorv2_2_tobackground_8, carconnectorv2_2_tobackground_9,
       carconnectorv2_2_tobackground_10, carconnectorv2_2_tofront, carconnectorv2_2_tofront_2,
       carconnectorv2_2_tofront_3, carconnectorv2_2_tofront_4, carconnectorv2_2_tofront_5,
       carconnectorv2_2_tofront_6, carconnectorv2_2_tofront_7, carconnectorv2_2_tofront_8,
       carconnectorv2_2_tofront_9, carconnectorv2_2_tofront_10, carconnectorv2_3_tobackground,
       carconnectorv2_3_tobackground_2, carconnectorv2_3_tobackground_3, carconnectorv2_3_tobackground_4,
       carconnectorv2_3_tobackground_5, carconnectorv2_3_tobackground_6, carconnectorv2_3_tobackground_7,
       carconnectorv2_3_tobackground_8, carconnectorv2_3_tobackground_9, carconnectorv2_3_tobackground_10,
       carconnectorv2_3_tofront, carconnectorv2_3_tofront_2, carconnectorv2_3_tofront_3,
       carconnectorv2_3_tofront_4, carconnectorv2_3_tofront_5, carconnectorv2_3_tofront_6,
       carconnectorv2_3_tofront_7, carconnectorv2_3_tofront_8, carconnectorv2_3_tofront_9,
       carconnectorv2_3_tofront_10, carconnectorv2_4_tobackground, carconnectorv2_4_tobackground_2,
       carconnectorv2_4_tobackground_3, carconnectorv2_4_tobackground_4, carconnectorv2_4_tobackground_5,
       carconnectorv2_4_tobackground_6, carconnectorv2_4_tobackground_7, carconnectorv2_4_tobackground_8,
       carconnectorv2_4_tobackground_9, carconnectorv2_4_tobackground_10, carconnectorv2_4_tofront,
       carconnectorv2_4_tofront_2, carconnectorv2_4_tofront_3, carconnectorv2_4_tofront_4,
       carconnectorv2_4_tofront_5, carconnectorv2_4_tofront_6, carconnectorv2_4_tofront_7,
       carconnectorv2_4_tofront_8, carconnectorv2_4_tofront_9, carconnectorv2_4_tofront_10,
       carconnectorv2_5_tobackground, carconnectorv2_5_tobackground_2, carconnectorv2_5_tobackground_3,
       carconnectorv2_5_tobackground_4, carconnectorv2_5_tobackground_5, carconnectorv2_5_tobackground_6,
       carconnectorv2_5_tobackground_7, carconnectorv2_5_tobackground_8, carconnectorv2_5_tobackground_9,
       carconnectorv2_5_tobackground_10, carconnectorv2_5_tofront, carconnectorv2_5_tofront_2,
       carconnectorv2_5_tofront_3, carconnectorv2_5_tofront_4, carconnectorv2_5_tofront_5,
       carconnectorv2_5_tofront_6, carconnectorv2_5_tofront_7, carconnectorv2_5_tofront_8,
       carconnectorv2_5_tofront_9, carconnectorv2_5_tofront_10, carconnectorv2_6_tobackground,
       carconnectorv2_6_tobackground_2, carconnectorv2_6_tobackground_3, carconnectorv2_6_tobackground_4,
       carconnectorv2_6_tobackground_5, carconnectorv2_6_tobackground_6, carconnectorv2_6_tobackground_7,
       carconnectorv2_6_tobackground_8, carconnectorv2_6_tobackground_9, carconnectorv2_6_tobackground_10,
       carconnectorv2_6_tofront, carconnectorv2_6_tofront_2, carconnectorv2_6_tofront_3,
       carconnectorv2_6_tofront_4, carconnectorv2_6_tofront_5, carconnectorv2_6_tofront_6,
       carconnectorv2_6_tofront_7, carconnectorv2_6_tofront_8, carconnectorv2_6_tofront_9,
       carconnectorv2_6_tofront_10, carconnectorv2_7_tobackground, carconnectorv2_7_tobackground_2,
       carconnectorv2_7_tobackground_3, carconnectorv2_7_tobackground_4, carconnectorv2_7_tobackground_5,
       carconnectorv2_7_tobackground_6, carconnectorv2_7_tobackground_7, carconnectorv2_7_tobackground_8,
       carconnectorv2_7_tobackground_9, carconnectorv2_7_tobackground_10, carconnectorv2_7_tofront,
       carconnectorv2_7_tofront_2, carconnectorv2_7_tofront_3, carconnectorv2_7_tofront_4,
       carconnectorv2_7_tofront_5, carconnectorv2_7_tofront_6, carconnectorv2_7_tofront_7,
       carconnectorv2_7_tofront_8, carconnectorv2_7_tofront_9, carconnectorv2_7_tofront_10,
       carconnectorv2_8_tobackground, carconnectorv2_8_tobackground_2, carconnectorv2_8_tobackground_3,
       carconnectorv2_8_tobackground_4, carconnectorv2_8_tobackground_5, carconnectorv2_8_tobackground_6,
       carconnectorv2_8_tobackground_7, carconnectorv2_8_tobackground_8, carconnectorv2_8_tobackground_9,
       carconnectorv2_8_tobackground_10, carconnectorv2_8_tofront, carconnectorv2_8_tofront_2,
       carconnectorv2_8_tofront_3, carconnectorv2_8_tofront_4, carconnectorv2_8_tofront_5,
       carconnectorv2_8_tofront_6, carconnectorv2_8_tofront_7, carconnectorv2_8_tofront_8,
       carconnectorv2_8_tofront_9, carconnectorv2_8_tofront_10, carconnectorv2_9_tobackground,
       carconnectorv2_9_tobackground_2, carconnectorv2_9_tobackground_3, carconnectorv2_9_tobackground_4,
       carconnectorv2_9_tobackground_5, carconnectorv2_9_tobackground_6, carconnectorv2_9_tobackground_7,
       carconnectorv2_9_tobackground_8, carconnectorv2_9_tobackground_9, carconnectorv2_9_tobackground_10,
       carconnectorv2_9_tofront, carconnectorv2_9_tofront_2, carconnectorv2_9_tofront_3,
       carconnectorv2_9_tofront_4, carconnectorv2_9_tofront_5, carconnectorv2_9_tofront_6,
       carconnectorv2_9_tofront_7, carconnectorv2_9_tofront_8, carconnectorv2_9_tofront_9,
       carconnectorv2_9_tofront_10, carconnectorv2_10_tobackground, carconnectorv2_10_tobackground_2,
       carconnectorv2_10_tobackground_3, carconnectorv2_10_tobackground_4, carconnectorv2_10_tobackground_5,
       carconnectorv2_10_tobackground_6, carconnectorv2_10_tobackground_7, carconnectorv2_10_tobackground_8,
       carconnectorv2_10_tobackground_9, carconnectorv2_10_tobackground_10, carconnectorv2_10_tofront,
       carconnectorv2_10_tofront_2, carconnectorv2_10_tofront_3, carconnectorv2_10_tofront_4,
       carconnectorv2_10_tofront_5, carconnectorv2_10_tofront_6, carconnectorv2_10_tofront_7,
       carconnectorv2_10_tofront_8, carconnectorv2_10_tofront_9, carconnectorv2_10_tofront_10,
       carconnectorv2_11_tobackground, carconnectorv2_11_tobackground_2, carconnectorv2_11_tobackground_3,
       carconnectorv2_11_tobackground_4, carconnectorv2_11_tobackground_5, carconnectorv2_11_tobackground_6,
       carconnectorv2_11_tobackground_7, carconnectorv2_11_tobackground_8, carconnectorv2_11_tobackground_9,
       carconnectorv2_11_tobackground_10, carconnectorv2_11_tofront, carconnectorv2_11_tofront_2,
       carconnectorv2_11_tofront_3, carconnectorv2_11_tofront_4, carconnectorv2_11_tofront_5,
       carconnectorv2_11_tofront_6, carconnectorv2_11_tofront_7, carconnectorv2_11_tofront_8,
       carconnectorv2_11_tofront_9, carconnectorv2_11_tofront_10, carconnectorv2_12_tobackground,
       carconnectorv2_12_tobackground_2, carconnectorv2_12_tobackground_3, carconnectorv2_12_tobackground_4,
       carconnectorv2_12_tobackground_5, carconnectorv2_12_tobackground_6, carconnectorv2_12_tobackground_7,
       carconnectorv2_12_tobackground_8, carconnectorv2_12_tobackground_9, carconnectorv2_12_tobackground_10,
       carconnectorv2_12_tofront, carconnectorv2_12_tofront_2, carconnectorv2_12_tofront_3,
       carconnectorv2_12_tofront_4, carconnectorv2_12_tofront_5, carconnectorv2_12_tofront_6,
       carconnectorv2_12_tofront_7, carconnectorv2_12_tofront_8, carconnectorv2_12_tofront_9,
       carconnectorv2_12_tofront_10, carconnectorv2_13_tobackground, carconnectorv2_13_tobackground_2,
       carconnectorv2_13_tobackground_3, carconnectorv2_13_tobackground_4, carconnectorv2_13_tobackground_5,
       carconnectorv2_13_tobackground_6, carconnectorv2_13_tobackground_7, carconnectorv2_13_tobackground_8,
       carconnectorv2_13_tobackground_9, carconnectorv2_13_tobackground_10, carconnectorv2_13_tofront,
       carconnectorv2_13_tofront_2, carconnectorv2_13_tofront_3, carconnectorv2_13_tofront_4,
       carconnectorv2_13_tofront_5, carconnectorv2_13_tofront_6, carconnectorv2_13_tofront_7,
       carconnectorv2_13_tofront_8, carconnectorv2_13_tofront_9, carconnectorv2_13_tofront_10,
       carconnectorv2_14_tobackground, carconnectorv2_14_tobackground_2, carconnectorv2_14_tobackground_3,
       carconnectorv2_14_tobackground_4, carconnectorv2_14_tobackground_5, carconnectorv2_14_tobackground_6,
       carconnectorv2_14_tobackground_7, carconnectorv2_14_tobackground_8, carconnectorv2_14_tobackground_9,
       carconnectorv2_14_tobackground_10, carconnectorv2_14_tofront, carconnectorv2_14_tofront_2,
       carconnectorv2_14_tofront_3, carconnectorv2_14_tofront_4, carconnectorv2_14_tofront_5,
       carconnectorv2_14_tofront_6, carconnectorv2_14_tofront_7, carconnectorv2_14_tofront_8,
       carconnectorv2_14_tofront_9, carconnectorv2_14_tofront_10, carconnectorv2_15_tobackground,
       carconnectorv2_15_tobackground_2, carconnectorv2_15_tobackground_3, carconnectorv2_15_tobackground_4,
       carconnectorv2_15_tobackground_5, carconnectorv2_15_tobackground_6, carconnectorv2_15_tobackground_7,
       carconnectorv2_15_tobackground_8, carconnectorv2_15_tobackground_9, carconnectorv2_15_tobackground_10,
       carconnectorv2_15_tofront, carconnectorv2_15_tofront_2, carconnectorv2_15_tofront_3,
       carconnectorv2_15_tofront_4, carconnectorv2_15_tofront_5, carconnectorv2_15_tofront_6,
       carconnectorv2_15_tofront_7, carconnectorv2_15_tofront_8, carconnectorv2_15_tofront_9,
       carconnectorv2_15_tofront_10, carconnectorv2_16_tobackground, carconnectorv2_16_tobackground_2,
       carconnectorv2_16_tobackground_3, carconnectorv2_16_tobackground_4, carconnectorv2_16_tobackground_5,
       carconnectorv2_16_tobackground_6, carconnectorv2_16_tobackground_7, carconnectorv2_16_tobackground_8,
       carconnectorv2_16_tobackground_9, carconnectorv2_16_tobackground_10, carconnectorv2_16_tofront,
       carconnectorv2_16_tofront_2, carconnectorv2_16_tofront_3, carconnectorv2_16_tofront_4,
       carconnectorv2_16_tofront_5, carconnectorv2_16_tofront_6, carconnectorv2_16_tofront_7,
       carconnectorv2_16_tofront_8, carconnectorv2_16_tofront_9, carconnectorv2_16_tofront_10,
       carconnectorv2_17_tobackground, carconnectorv2_17_tobackground_2, carconnectorv2_17_tobackground_3,
       carconnectorv2_17_tobackground_4, carconnectorv2_17_tobackground_5, carconnectorv2_17_tobackground_6,
       carconnectorv2_17_tobackground_7, carconnectorv2_17_tobackground_8, carconnectorv2_17_tobackground_9,
       carconnectorv2_17_tobackground_10, carconnectorv2_17_tofront, carconnectorv2_17_tofront_2,
       carconnectorv2_17_tofront_3, carconnectorv2_17_tofront_4, carconnectorv2_17_tofront_5,
       carconnectorv2_17_tofront_6, carconnectorv2_17_tofront_7, carconnectorv2_17_tofront_8,
       carconnectorv2_17_tofront_9, carconnectorv2_17_tofront_10, carconnectorv2_18_tobackground,
       carconnectorv2_18_tobackground_2, carconnectorv2_18_tobackground_3, carconnectorv2_18_tobackground_4,
       carconnectorv2_18_tobackground_5, carconnectorv2_18_tobackground_6, carconnectorv2_18_tobackground_7,
       carconnectorv2_18_tobackground_8, carconnectorv2_18_tobackground_9, carconnectorv2_18_tobackground_10,
       carconnectorv2_18_tofront, carconnectorv2_18_tofront_2, carconnectorv2_18_tofront_3,
       carconnectorv2_18_tofront_4, carconnectorv2_18_tofront_5, carconnectorv2_18_tofront_6,
       carconnectorv2_18_tofront_7, carconnectorv2_18_tofront_8, carconnectorv2_18_tofront_9,
       carconnectorv2_18_tofront_10, carconnectorv2_19_tobackground, carconnectorv2_19_tobackground_2,
       carconnectorv2_19_tobackground_3, carconnectorv2_19_tobackground_4, carconnectorv2_19_tobackground_5,
       carconnectorv2_19_tobackground_6, carconnectorv2_19_tobackground_7, carconnectorv2_19_tobackground_8,
       carconnectorv2_19_tobackground_9, carconnectorv2_19_tobackground_10, carconnectorv2_19_tofront,
       carconnectorv2_19_tofront_2, carconnectorv2_19_tofront_3, carconnectorv2_19_tofront_4,
       carconnectorv2_19_tofront_5, carconnectorv2_19_tofront_6, carconnectorv2_19_tofront_7,
       carconnectorv2_19_tofront_8, carconnectorv2_19_tofront_9, carconnectorv2_19_tofront_10,
       carconnectorv2_20_tobackground, carconnectorv2_20_tobackground_2, carconnectorv2_20_tobackground_3,
       carconnectorv2_20_tobackground_4, carconnectorv2_20_tobackground_5, carconnectorv2_20_tobackground_6,
       carconnectorv2_20_tobackground_7, carconnectorv2_20_tobackground_8, carconnectorv2_20_tobackground_9,
       carconnectorv2_20_tobackground_10, carconnectorv2_20_tofront, carconnectorv2_20_tofront_2,
       carconnectorv2_20_tofront_3, carconnectorv2_20_tofront_4, carconnectorv2_20_tofront_5,
       carconnectorv2_20_tofront_6, carconnectorv2_20_tofront_7, carconnectorv2_20_tofront_8,
       carconnectorv2_20_tofront_9, carconnectorv2_20_tofront_10, log_1x1_1_tobackground,
       log_1x1_1_tobackground_2, log_1x1_1_tobackground_3, log_1x1_1_tobackground_4,
       log_1x1_1_tobackground_5, log_1x1_1_tobackground_6, log_1x1_1_tobackground_7,
       log_1x1_1_tobackground_8, log_1x1_1_tobackground_9, log_1x1_1_tobackground_10, log_1x1_1_tofront,
       log_1x1_1_tofront_2, log_1x1_1_tofront_3, log_1x1_1_tofront_4, log_1x1_1_tofront_5,
       log_1x1_1_tofront_6, log_1x1_1_tofront_7, log_1x1_1_tofront_8, log_1x1_1_tofront_9,
       log_1x1_1_tofront_10, log_1x1_2_tobackground, log_1x1_2_tobackground_2, log_1x1_2_tobackground_3,
       log_1x1_2_tobackground_4, log_1x1_2_tobackground_5, log_1x1_2_tobackground_6,
       log_1x1_2_tobackground_7, log_1x1_2_tobackground_8, log_1x1_2_tobackground_9,
       log_1x1_2_tobackground_10, log_1x1_2_tofront, log_1x1_2_tofront_2, log_1x1_2_tofront_3,
       log_1x1_2_tofront_4, log_1x1_2_tofront_5, log_1x1_2_tofront_6, log_1x1_2_tofront_7,
       log_1x1_2_tofront_8, log_1x1_2_tofront_9, log_1x1_2_tofront_10, log_1x1_3_tobackground,
       log_1x1_3_tobackground_2, log_1x1_3_tobackground_3, log_1x1_3_tobackground_4,
       log_1x1_3_tobackground_5, log_1x1_3_tobackground_6, log_1x1_3_tobackground_7,
       log_1x1_3_tobackground_8, log_1x1_3_tobackground_9, log_1x1_3_tobackground_10, log_1x1_3_tofront,
       log_1x1_3_tofront_2, log_1x1_3_tofront_3, log_1x1_3_tofront_4, log_1x1_3_tofront_5,
       log_1x1_3_tofront_6, log_1x1_3_tofront_7, log_1x1_3_tofront_8, log_1x1_3_tofront_9,
       log_1x1_3_tofront_10, log_1x1_4_tobackground, log_1x1_4_tobackground_2, log_1x1_4_tobackground_3,
       log_1x1_4_tobackground_4, log_1x1_4_tobackground_5, log_1x1_4_tobackground_6,
       log_1x1_4_tobackground_7, log_1x1_4_tobackground_8, log_1x1_4_tobackground_9,
       log_1x1_4_tobackground_10, log_1x1_4_tofront, log_1x1_4_tofront_2, log_1x1_4_tofront_3,
       log_1x1_4_tofront_4, log_1x1_4_tofront_5, log_1x1_4_tofront_6, log_1x1_4_tofront_7,
       log_1x1_4_tofront_8, log_1x1_4_tofront_9, log_1x1_4_tofront_10, log_2x1_1_tobackground,
       log_2x1_1_tobackground_2, log_2x1_1_tobackground_3, log_2x1_1_tobackground_4,
       log_2x1_1_tobackground_5, log_2x1_1_tobackground_6, log_2x1_1_tobackground_7,
       log_2x1_1_tobackground_8, log_2x1_1_tobackground_9, log_2x1_1_tobackground_10, log_2x1_1_tofront,
       log_2x1_1_tofront_2, log_2x1_1_tofront_3, log_2x1_1_tofront_4, log_2x1_1_tofront_5,
       log_2x1_1_tofront_6, log_2x1_1_tofront_7, log_2x1_1_tofront_8, log_2x1_1_tofront_9,
       log_2x1_1_tofront_10, log_2x1_3_tobackground, log_2x1_3_tobackground_2, log_2x1_3_tobackground_3,
       log_2x1_3_tobackground_4, log_2x1_3_tobackground_5, log_2x1_3_tobackground_6,
       log_2x1_3_tobackground_7, log_2x1_3_tobackground_8, log_2x1_3_tobackground_9,
       log_2x1_3_tobackground_10, log_2x1_3_tofront, log_2x1_3_tofront_2, log_2x1_3_tofront_3,
       log_2x1_3_tofront_4, log_2x1_3_tofront_5, log_2x1_3_tofront_6, log_2x1_3_tofront_7,
       log_2x1_3_tofront_8, log_2x1_3_tofront_9, log_2x1_3_tofront_10, log_2x1_4_tobackground,
       log_2x1_4_tobackground_2, log_2x1_4_tobackground_3, log_2x1_4_tobackground_4,
       log_2x1_4_tobackground_5, log_2x1_4_tobackground_6, log_2x1_4_tobackground_7,
       log_2x1_4_tobackground_8, log_2x1_4_tobackground_9, log_2x1_4_tobackground_10, log_2x1_4_tofront,
       log_2x1_4_tofront_2, log_2x1_4_tofront_3, log_2x1_4_tofront_4, log_2x1_4_tofront_5,
       log_2x1_4_tofront_6, log_2x1_4_tofront_7, log_2x1_4_tofront_8, log_2x1_4_tofront_9,
       log_2x1_4_tofront_10, log_2x1_5_tobackground, log_2x1_5_tobackground_2, log_2x1_5_tobackground_3,
       log_2x1_5_tobackground_4, log_2x1_5_tobackground_5, log_2x1_5_tobackground_6,
       log_2x1_5_tobackground_7, log_2x1_5_tobackground_8, log_2x1_5_tobackground_9,
       log_2x1_5_tobackground_10, log_3x2_1_tobackground, log_3x2_1_tobackground_2, log_3x2_1_tobackground_3,
       log_3x2_1_tobackground_4, log_3x2_1_tobackground_5, log_3x2_1_tobackground_6,
       log_3x2_1_tobackground_7, log_3x2_1_tobackground_8, log_3x2_1_tobackground_9,
       log_3x2_1_tobackground_10, log_3x2_1_tofront, log_3x2_1_tofront_2, log_3x2_1_tofront_3,
       log_3x2_1_tofront_4, log_3x2_1_tofront_5, log_3x2_1_tofront_6, log_3x2_1_tofront_7,
       log_3x2_1_tofront_8, log_3x2_1_tofront_9, log_3x2_1_tofront_10, log_3x2_3_tobackground,
       log_3x2_3_tobackground_2, log_3x2_3_tobackground_3, log_3x2_3_tobackground_4,
       log_3x2_3_tobackground_5, log_3x2_3_tobackground_6, log_3x2_3_tobackground_7,
       log_3x2_3_tobackground_8, log_3x2_3_tobackground_9, log_3x2_3_tobackground_10, log_3x2_3_tofront,
       log_3x2_3_tofront_2, log_3x2_3_tofront_3, log_3x2_3_tofront_4, log_3x2_3_tofront_5,
       log_3x2_3_tofront_6, log_3x2_3_tofront_7, log_3x2_3_tofront_8, log_3x2_3_tofront_9,
       log_3x2_3_tofront_10, log_3x2_4_tobackground, log_3x2_4_tobackground_2, log_3x2_4_tobackground_3,
       log_3x2_4_tobackground_4, log_3x2_4_tobackground_5, log_3x2_4_tobackground_6,
       log_3x2_4_tobackground_7, log_3x2_4_tobackground_8, log_3x2_4_tobackground_9,
       log_3x2_4_tobackground_10, log_3x2_4_tofront, log_3x2_4_tofront_2, log_3x2_4_tofront_3,
       log_3x2_4_tofront_4, log_3x2_4_tofront_5, log_3x2_4_tofront_6, log_3x2_4_tofront_7,
       log_3x2_4_tofront_8, log_3x2_4_tofront_9, log_3x2_4_tofront_10, log_3x2_5_tobackground,
       log_3x2_5_tobackground_2, log_3x2_5_tobackground_3, log_3x2_5_tobackground_4,
       log_3x2_5_tobackground_5, log_3x2_5_tobackground_6, log_3x2_5_tobackground_7,
       log_3x2_5_tobackground_8, log_3x2_5_tobackground_9, log_3x2_5_tobackground_10, log_3x2_5_tofront,
       log_3x2_5_tofront_2, log_3x2_5_tofront_3, log_3x2_5_tofront_4, log_3x2_5_tofront_5,
       log_3x2_5_tofront_6, log_3x2_5_tofront_7, log_3x2_5_tofront_8, log_3x2_5_tofront_9,
       log_3x2_5_tofront_10, swamp_1_tobackground, swamp_1_tobackground_2, swamp_1_tobackground_3,
       swamp_1_tobackground_4, swamp_1_tobackground_5, swamp_1_tobackground_6, swamp_1_tobackground_7,
       swamp_1_tobackground_8, swamp_1_tobackground_9, swamp_1_tobackground_10, swamp_1_tofront,
       swamp_1_tofront_2, swamp_1_tofront_3, swamp_1_tofront_4, swamp_1_tofront_5, swamp_1_tofront_6,
       swamp_1_tofront_7, swamp_1_tofront_8, swamp_1_tofront_9, swamp_1_tofront_10, swamp_2_tobackground,
       swamp_2_tobackground_2, swamp_2_tobackground_3, swamp_2_tobackground_4, swamp_2_tobackground_5,
       swamp_2_tobackground_6, swamp_2_tobackground_7, swamp_2_tobackground_8, swamp_2_tobackground_9,
       swamp_2_tobackground_10, swamp_2_tofront, swamp_2_tofront_2, swamp_2_tofront_3, swamp_2_tofront_4,
       swamp_2_tofront_5, swamp_2_tofront_6, swamp_2_tofront_7, swamp_2_tofront_8, swamp_2_tofront_9,
       swamp_2_tofront_10, swamp_3_tobackground, swamp_3_tobackground_2, swamp_3_tobackground_3,
       swamp_3_tobackground_4, swamp_3_tobackground_5, swamp_3_tobackground_6, swamp_3_tobackground_7,
       swamp_3_tobackground_8, swamp_3_tobackground_9, swamp_3_tobackground_10, swamp_3_tofront,
       swamp_3_tofront_2, swamp_3_tofront_3, swamp_3_tofront_4, swamp_3_tofront_5, swamp_3_tofront_6,
       swamp_3_tofront_7, swamp_3_tofront_8, swamp_3_tofront_9, swamp_3_tofront_10, swamp_4_tobackground,
       swamp_4_tobackground_2, swamp_4_tobackground_3, swamp_4_tobackground_4, swamp_4_tobackground_5,
       swamp_4_tobackground_6, swamp_4_tobackground_7, swamp_4_tobackground_8, swamp_4_tobackground_9,
       swamp_4_tobackground_10, swamp_4_tofront, swamp_4_tofront_2, swamp_4_tofront_3, swamp_4_tofront_4,
       swamp_4_tofront_5, swamp_4_tofront_6, swamp_4_tofront_7, swamp_4_tofront_8, swamp_4_tofront_9,
       swamp_4_tofront_10, swamp_5_tobackground, swamp_5_tobackground_2, swamp_5_tobackground_3,
       swamp_5_tobackground_4, swamp_5_tobackground_5, swamp_5_tobackground_6, swamp_5_tobackground_7,
       swamp_5_tobackground_8, swamp_5_tobackground_9, swamp_5_tobackground_10, swamp_5_tofront,
       swamp_5_tofront_2, swamp_5_tofront_3, swamp_5_tofront_4, swamp_5_tofront_5, swamp_5_tofront_6,
       swamp_5_tofront_7, swamp_5_tofront_8, swamp_5_tofront_9, swamp_5_tofront_10, swamp_6_tobackground,
       swamp_6_tobackground_2, swamp_6_tobackground_3, swamp_6_tobackground_4, swamp_6_tobackground_5,
       swamp_6_tobackground_6, swamp_6_tobackground_7, swamp_6_tobackground_8, swamp_6_tobackground_9,
       swamp_6_tobackground_10, swamp_6_tofront, swamp_6_tofront_2, swamp_6_tofront_3, swamp_6_tofront_4,
       swamp_6_tofront_5, swamp_6_tofront_6, swamp_6_tofront_7, swamp_6_tofront_8, swamp_6_tofront_9,
       swamp_6_tofront_10, swamp_7_tobackground, swamp_7_tobackground_2, swamp_7_tobackground_3,
       swamp_7_tobackground_4, swamp_7_tobackground_5, swamp_7_tobackground_6, swamp_7_tobackground_7,
       swamp_7_tobackground_8, swamp_7_tobackground_9, swamp_7_tobackground_10, swamp_7_tofront,
       swamp_7_tofront_2, swamp_7_tofront_3, swamp_7_tofront_4, swamp_7_tofront_5, swamp_7_tofront_6,
       swamp_7_tofront_7, swamp_7_tofront_8, swamp_7_tofront_9, swamp_7_tofront_10, swamp_8_tobackground,
       swamp_8_tobackground_2, swamp_8_tobackground_3, swamp_8_tobackground_4, swamp_8_tobackground_5,
       swamp_8_tobackground_6, swamp_8_tobackground_7, swamp_8_tobackground_8, swamp_8_tobackground_9,
       swamp_8_tobackground_10, swamp_8_tofront, swamp_8_tofront_2, swamp_8_tofront_3, swamp_8_tofront_4,
       swamp_8_tofront_5, swamp_8_tofront_6, swamp_8_tofront_7, swamp_8_tofront_8, swamp_8_tofront_9,
       swamp_8_tofront_10;

  Clock clock_1 (.out(clock_1_out));
  Keyboard keyboard_1 (.clk(clock_1_out), .data(keyboard_1_data));  // open: re, clr, avail
  rightShifter rightshifter_1 (
    .shiftM(rightshifter_1_shiftm), .shiftD(rightshifter_1_shiftd), .shiftCounts(2'b01),
    .tactGen(controlled_buffer_1_out));  // open: reset
  rightShifter rightshifter_2 (
    .shiftM(rightshifter_2_shiftm), .shiftD(rightshifter_2_shiftd), .shiftCounts(2'b00),
    .tactGen(controlled_buffer_1_out));  // open: reset
  rightShifter rightshifter_3 (
    .shiftM(rightshifter_3_shiftm), .shiftD(rightshifter_3_shiftd), .shiftCounts(2'b10),
    .tactGen(controlled_buffer_1_out));  // open: reset
  rightShifter rightshifter_4 (
    .shiftM(rightshifter_4_shiftm), .shiftD(rightshifter_4_shiftd), .shiftCounts(2'b00),
    .tactGen(controlled_buffer_1_out));  // open: reset
  leftShifter leftshifter_1 (
    .shiftD(leftshifter_1_shiftd), .shiftCounts(3'b010), .shiftM(leftshifter_1_shiftm),
    .tactGen(controlled_buffer_1_out), .reset(stopgame_1_stopper));
  rightShifter rightshifter_5 (
    .shiftM(rightshifter_5_shiftm), .shiftD(rightshifter_5_shiftd), .shiftCounts(2'b00),
    .tactGen(controlled_buffer_1_out), .reset(stopgame_1_stopper));
  leftShifter leftshifter_2 (
    .shiftD(leftshifter_2_shiftd), .shiftCounts(3'b000), .shiftM(leftshifter_2_shiftm),
    .tactGen(controlled_buffer_1_out), .reset(stopgame_1_stopper));
  assign controlled_buffer_1_out = not_1_out ? clock_2_out : 1'bz;  // Controlled_Buffer controlled_buffer_1
  Pull_Resistor pull_resistor_1 (.node(controlled_buffer_1_out));
  not not_1 (not_1_out, stopgame_1_stopper);
  Clock clock_2 (.out(clock_2_out));
  stopGame stopgame_1 (.tact(clock_2_out), .\event (undriven), .stopper(stopgame_1_stopper));
  Pull_Resistor pull_resistor_2 (.node(stopgame_1_stopper));
  // Probe on keyboard_1_data
  waterIntersect waterintersect_1 (
    .backLen(5'b10001), .inBackM(rightshifter_1_shiftm), .inBackD(rightshifter_1_shiftd), .inFrogM(out_2),
    .inFrogD(out_3), .doIntersect(_11), .outIntersect(waterintersect_1_outintersect));  // open: inIntersect
  waterIntersect waterintersect_2 (
    .backLen(5'b11001), .inBackM(rightshifter_2_shiftm), .inBackD(rightshifter_2_shiftd), .inFrogM(out_2),
    .inFrogD(out_3), .inIntersect(waterintersect_1_outintersect), .doIntersect(_9),
    .outIntersect(waterintersect_2_outintersect));
  smallLogIntersect smalllogintersect_1 (
    .backLen(5'b00111), .inBackM(rightshifter_3_shiftm), .inFrogM(out_2),
    .inIntersect(waterintersect_2_outintersect), .doIntersect(_8));  // open: outIntersect
  waterIntersect waterintersect_3 (
    .backLen(5'b11001), .inBackM(rightshifter_4_shiftm), .inBackD(rightshifter_4_shiftd), .inFrogM(out_2),
    .inFrogD(out_3), .doIntersect(_9));  // open: inIntersect, outIntersect
  computeIntresection computeintresection_1 (
    .backLen(5'b10100), .inBackM(leftshifter_1_shiftm), .inBackD(leftshifter_1_shiftd), .inFrogD(out_3),
    .outIntersect(computeintresection_1_outintersect), .inFrogM(out_2), .doCompute(_2));  // open: inIntersect
  computeIntresection computeintresection_2 (
    .backLen(5'b10100), .inBackM(rightshifter_5_shiftm), .inBackD(rightshifter_5_shiftd), .inFrogD(out_3),
    .outIntersect(computeintresection_2_outintersect), .inFrogM(out_2),
    .inIntersect(computeintresection_1_outintersect), .doCompute(_1));
  computeIntresection computeintresection_3 (
    .backLen(5'b10100), .inBackM(leftshifter_2_shiftm), .inBackD(leftshifter_2_shiftd), .inFrogD(out_3),
    .outIntersect(computeintresection_3_outintersect), .inFrogM(out_2),
    .inIntersect(computeintresection_2_outintersect), .doCompute(_0));
  // Probe on out_3
  // Probe on out_2
  Comparator #(.width(7)) comparator_1 (.a(keyboard_1_data), .b(7'b1110111), .eq(comparator_1_eq));  // open: gt, lt
  mod_vertical mod_vertical_1 (
    .W(comparator_1_eq), .S(comparator_2_eq), .stop(stop_out), .Y(out_1), .reset(undriven_2));
  Comparator #(.width(7)) comparator_2 (.a(keyboard_1_data), .b(7'b1110011), .eq(comparator_2_eq));  // open: gt, lt
  Comparator #(.width(7)) comparator_3 (.a(keyboard_1_data), .b(7'b1100001), .eq(comparator_3_eq));  // open: gt, lt
  mod_horizon_3__works_correctly mod_horizon_3_works_correctly_1 (
    .A(comparator_3_eq), .D(comparator_4_eq), .stop(stop_out), .Xmatrice(out_2), .Xdisplay(out_3),
    .reset(res_out));
  Comparator #(.width(7)) comparator_4 (.a(keyboard_1_data), .b(7'b1100100), .eq(comparator_4_eq));  // open: gt, lt
  Button res (.out(res_out));
  Button stop (.out(stop_out));
  DotMatrix #(.inputtype("row"), .matrixcols(30), .matrixrows(10)) dotmatrix_1 (
    .row0(log_2x1_1_tofront), .row1(log_2x1_1_tofront_2), .row2(log_2x1_1_tofront_3),
    .row3(log_2x1_1_tofront_4), .row4(log_2x1_1_tofront_5), .row5(log_2x1_1_tofront_6),
    .row6(log_2x1_1_tofront_7), .row7(log_2x1_1_tofront_8), .row8(log_2x1_1_tofront_9),
    .row9(log_2x1_1_tofront_10));
  DotMatrix #(.inputtype("row"), .matrixcols(30), .matrixrows(10)) dotmatrix_2 (
    .row0(log_2x1_1_tobackground), .row1(log_2x1_1_tobackground_2), .row2(log_2x1_1_tobackground_3),
    .row3(log_2x1_1_tobackground_4), .row4(log_2x1_1_tobackground_5), .row5(log_2x1_1_tobackground_6),
    .row6(log_2x1_1_tobackground_7), .row7(log_2x1_1_tobackground_8), .row8(log_2x1_1_tobackground_9),
    .row9(log_2x1_1_tobackground_10));
  log_2x1 log_2x1_1 (
    .inBackShiftD(rightshifter_1_shiftd), .outBackShiftD(log_2x1_1_outbackshiftd),
    .inputBackShiftM(rightshifter_1_shiftm), .outputBackShiftM(log_2x1_1_outputbackshiftm),
    .inPlayerShiftD(out_3), .outPlayerShiftD(log_2x1_1_outplayershiftd), .inPlayerShiftM(out_2),
    .outPlayerShiftM(log_2x1_1_outplayershiftm), .inFlag(_11), .outFlag(log_2x1_1_outflag),
    .toBackground(log_2x1_1_tobackground), .toBackground_2(log_2x1_1_tobackground_2),
    .toBackground_3(log_2x1_1_tobackground_3), .toBackground_4(log_2x1_1_tobackground_4),
    .toBackground_5(log_2x1_1_tobackground_5), .toBackground_6(log_2x1_1_tobackground_6),
    .toBackground_7(log_2x1_1_tobackground_7), .toBackground_8(log_2x1_1_tobackground_8),
    .toBackground_9(log_2x1_1_tobackground_9), .toBackground_10(log_2x1_1_tobackground_10),
    .toFront(log_2x1_1_tofront), .toFront_2(log_2x1_1_tofront_2), .toFront_3(log_2x1_1_tofront_3),
    .toFront_4(log_2x1_1_tofront_4), .toFront_5(log_2x1_1_tofront_5), .toFront_6(log_2x1_1_tofront_6),
    .toFront_7(log_2x1_1_tofront_7), .toFront_8(log_2x1_1_tofront_8), .toFront_9(log_2x1_1_tofront_9),
    .toFront_10(log_2x1_1_tofront_10));
  heightFlag heightflag_1 (.height(4'b1011), .playerY(out_1), .eqY(_11));
  log_2x1 log_2x1_2 ();  // open: inBackShiftD, outBackShiftD, inputBackShiftM, outputBackShiftM, inPlayerShiftD, outPlayerShiftD, inPlayerShiftM, outPlayerShiftM, inFlag, outFlag, toBackground, toBackground_2, toBackground_3, toBackground_4, toBackground_5, toBackground_6, toBackground_7, toBackground_8, toBackground_9, toBackground_10, toFront, toFront_2, toFront_3, toFront_4, toFront_5, toFront_6, toFront_7, toFront_8, toFront_9, toFront_10
  DotMatrix #(.inputtype("row"), .matrixcols(30), .matrixrows(10)) dotmatrix_3 (
    .row0(log_3x2_1_tobackground), .row1(log_3x2_1_tobackground_2), .row2(log_3x2_1_tobackground_3),
    .row3(log_3x2_1_tobackground_4), .row4(log_3x2_1_tobackground_5), .row5(log_3x2_1_tobackground_6),
    .row6(log_3x2_1_tobackground_7), .row7(log_3x2_1_tobackground_8), .row8(log_3x2_1_tobackground_9),
    .row9(log_3x2_1_tobackground_10));
  DotMatrix #(.inputtype("row"), .matrixcols(30), .matrixrows(10)) dotmatrix_4 (
    .row0(log_3x2_1_tofront), .row1(log_3x2_1_tofront_2), .row2(log_3x2_1_tofront_3),
    .row3(log_3x2_1_tofront_4), .row4(log_3x2_1_tofront_5), .row5(log_3x2_1_tofront_6),
    .row6(log_3x2_1_tofront_7), .row7(log_3x2_1_tofront_8), .row8(log_3x2_1_tofront_9),
    .row9(log_3x2_1_tofront_10));
  log_3x2 log_3x2_1 (
    .inBackShiftD(rightshifter_2_shiftd), .outBackShiftD(log_3x2_1_outbackshiftd),
    .inputBackShiftM(rightshifter_2_shiftm), .outputBackShiftM(log_3x2_1_outputbackshiftm),
    .inPlayerShiftD(out_3), .outPlayerShiftD(log_3x2_1_outplayershiftd), .inPlayerShiftM(out_2),
    .outPlayerShiftM(log_3x2_1_outplayershiftm), .inFlag(_9), .outFlag(log_3x2_1_outflag),
    .toBackground(log_3x2_1_tobackground), .toBackground_2(log_3x2_1_tobackground_2),
    .toBackground_3(log_3x2_1_tobackground_3), .toBackground_4(log_3x2_1_tobackground_4),
    .toBackground_5(log_3x2_1_tobackground_5), .toBackground_6(log_3x2_1_tobackground_6),
    .toBackground_7(log_3x2_1_tobackground_7), .toBackground_8(log_3x2_1_tobackground_8),
    .toBackground_9(log_3x2_1_tobackground_9), .toBackground_10(log_3x2_1_tobackground_10),
    .toFront(log_3x2_1_tofront), .toFront_2(log_3x2_1_tofront_2), .toFront_3(log_3x2_1_tofront_3),
    .toFront_4(log_3x2_1_tofront_4), .toFront_5(log_3x2_1_tofront_5), .toFront_6(log_3x2_1_tofront_6),
    .toFront_7(log_3x2_1_tofront_7), .toFront_8(log_3x2_1_tofront_8), .toFront_9(log_3x2_1_tofront_9),
    .toFront_10(log_3x2_1_tofront_10));
  heightFlag heightflag_2 (.height(4'b1001), .playerY(out_1), .eqY(_9));
  DotMatrix #(.inputtype("row"), .matrixcols(30), .matrixrows(10)) dotmatrix_5 (
    .row0(log_1x1_1_tofront), .row1(log_1x1_1_tofront_2), .row2(log_1x1_1_tofront_3),
    .row3(log_1x1_1_tofront_4), .row4(log_1x1_1_tofront_5), .row5(log_1x1_1_tofront_6),
    .row6(log_1x1_1_tofront_7), .row7(log_1x1_1_tofront_8), .row8(log_1x1_1_tofront_9),
    .row9(log_1x1_1_tofront_10));
  log_1x1 log_1x1_1 (
    .inBackShiftD(rightshifter_3_shiftd), .outBackShiftD(log_1x1_1_outbackshiftd),
    .inputBackShiftM(rightshifter_3_shiftm), .outputBackShiftM(log_1x1_1_outputbackshiftm),
    .inPlayerShiftD(out_3), .outPlayerShiftD(log_1x1_1_outplayershiftd), .inPlayerShiftM(out_2),
    .outPlayerShiftM(log_1x1_1_outplayershiftm), .inFlag(_8), .outFlag(log_1x1_1_outflag),
    .toBackground(log_1x1_1_tobackground), .toBackground_2(log_1x1_1_tobackground_2),
    .toBackground_3(log_1x1_1_tobackground_3), .toBackground_4(log_1x1_1_tobackground_4),
    .toBackground_5(log_1x1_1_tobackground_5), .toBackground_6(log_1x1_1_tobackground_6),
    .toBackground_7(log_1x1_1_tobackground_7), .toBackground_8(log_1x1_1_tobackground_8),
    .toBackground_9(log_1x1_1_tobackground_9), .toBackground_10(log_1x1_1_tobackground_10),
    .toFront(log_1x1_1_tofront), .toFront_2(log_1x1_1_tofront_2), .toFront_3(log_1x1_1_tofront_3),
    .toFront_4(log_1x1_1_tofront_4), .toFront_5(log_1x1_1_tofront_5), .toFront_6(log_1x1_1_tofront_6),
    .toFront_7(log_1x1_1_tofront_7), .toFront_8(log_1x1_1_tofront_8), .toFront_9(log_1x1_1_tofront_9),
    .toFront_10(log_1x1_1_tofront_10));
  DotMatrix #(.inputtype("row"), .matrixcols(30), .matrixrows(10)) dotmatrix_6 (
    .row0(log_1x1_1_tobackground), .row1(log_1x1_1_tobackground_2), .row2(log_1x1_1_tobackground_3),
    .row3(log_1x1_1_tobackground_4), .row4(log_1x1_1_tobackground_5), .row5(log_1x1_1_tobackground_6),
    .row6(log_1x1_1_tobackground_7), .row7(log_1x1_1_tobackground_8), .row8(log_1x1_1_tobackground_9),
    .row9(log_1x1_1_tobackground_10));
  heightFlag heightflag_3 (.height(4'b1000), .playerY(out_1), .eqY(_8));
  log_3x2 log_3x2_2 (
    .inBackShiftD(rightshifter_4_shiftd), .inputBackShiftM(rightshifter_4_shiftm), .inPlayerShiftD(out_3),
    .inPlayerShiftM(out_2), .inFlag(heightflag_4_eqy));  // open: outBackShiftD, outputBackShiftM, outPlayerShiftD, outPlayerShiftM, outFlag, toBackground, toBackground_2, toBackground_3, toBackground_4, toBackground_5, toBackground_6, toBackground_7, toBackground_8, toBackground_9, toBackground_10, toFront, toFront_2, toFront_3, toFront_4, toFront_5, toFront_6, toFront_7, toFront_8, toFront_9, toFront_10
  heightFlag heightflag_4 (.height(4'b1001), .playerY(out_1), .eqY(heightflag_4_eqy));
  swamp swamp_1 (
    .inPlayerShiftD(out_3), .outPlayerShiftD(swamp_1_outplayershiftd), .inPlayerShiftM(out_2),
    .outPlayerShiftM(swamp_1_outplayershiftm), .inFlag(heightflag_5_eqy), .outFlag(swamp_1_outflag),
    .toBackground(swamp_1_tobackground), .toFront(swamp_1_tofront), .toBackground_2(swamp_1_tobackground_2),
    .toFront_2(swamp_1_tofront_2), .toBackground_3(swamp_1_tobackground_3), .toFront_3(swamp_1_tofront_3),
    .toBackground_4(swamp_1_tobackground_4), .toFront_4(swamp_1_tofront_4),
    .toBackground_5(swamp_1_tobackground_5), .toFront_5(swamp_1_tofront_5),
    .toBackground_6(swamp_1_tobackground_6), .toFront_6(swamp_1_tofront_6),
    .toBackground_7(swamp_1_tobackground_7), .toFront_7(swamp_1_tofront_7),
    .toBackground_8(swamp_1_tobackground_8), .toFront_8(swamp_1_tofront_8),
    .toBackground_9(swamp_1_tobackground_9), .toFront_9(swamp_1_tofront_9),
    .toBackground_10(swamp_1_tobackground_10), .toFront_10(swamp_1_tofront_10));
  DotMatrix #(.inputtype("row"), .matrixcols(30), .matrixrows(10)) dotmatrix_7 (
    .row0(swamp_1_tofront), .row1(swamp_1_tofront_2), .row2(swamp_1_tofront_3), .row3(swamp_1_tofront_4),
    .row4(swamp_1_tofront_5), .row5(swamp_1_tofront_6), .row6(swamp_1_tofront_7), .row7(swamp_1_tofront_8),
    .row8(swamp_1_tofront_9), .row9(swamp_1_tofront_10));
  DotMatrix #(.inputtype("row"), .matrixcols(30), .matrixrows(10)) dotmatrix_8 (
    .row0(swamp_1_tobackground), .row1(swamp_1_tobackground_2), .row2(swamp_1_tobackground_3),
    .row3(swamp_1_tobackground_4), .row4(swamp_1_tobackground_5), .row5(swamp_1_tobackground_6),
    .row6(swamp_1_tobackground_7), .row7(swamp_1_tobackground_8), .row8(swamp_1_tobackground_9),
    .row9(swamp_1_tobackground_10));
  heightFlag heightflag_5 (.height(4'b0110), .playerY(out_1), .eqY(heightflag_5_eqy));
  DotMatrix #(.inputtype("row"), .matrixcols(30), .matrixrows(2)) dotmatrix_9 (
    .row0(carconnectorv2_1_tobackground), .row1(carconnectorv2_1_tobackground_2));
  DotMatrix #(.inputtype("row"), .matrixcols(30), .matrixrows(10)) dotmatrix_10 (
    .row0(carconnectorv2_1_tofront), .row1(carconnectorv2_1_tofront_2), .row2(carconnectorv2_1_tofront_3),
    .row3(carconnectorv2_1_tofront_4), .row4(carconnectorv2_1_tofront_5), .row5(carconnectorv2_1_tofront_6),
    .row6(carconnectorv2_1_tofront_7), .row7(carconnectorv2_1_tofront_8), .row8(carconnectorv2_1_tofront_9),
    .row9(carconnectorv2_1_tofront_10));
  carConnectorV2 carconnectorv2_1 (
    .inBackShiftD(leftshifter_2_shiftd), .outBackShiftD(carconnectorv2_1_outbackshiftd),
    .inputBackShiftM(leftshifter_2_shiftm), .outputBackShiftM(carconnectorv2_1_outputbackshiftm),
    .outPlayerShiftD(carconnectorv2_1_outplayershiftd), .inPlayerShiftM(out_2),
    .outPlayerShiftM(carconnectorv2_1_outplayershiftm), .inFlag(heightflag_6_eqy),
    .outFlag(carconnectorv2_1_outflag), .toBackground(carconnectorv2_1_tobackground),
    .toBackground_2(carconnectorv2_1_tobackground_2), .toBackground_3(carconnectorv2_1_tobackground_3),
    .toBackground_4(carconnectorv2_1_tobackground_4), .toBackground_5(carconnectorv2_1_tobackground_5),
    .toBackground_6(carconnectorv2_1_tobackground_6), .toBackground_7(carconnectorv2_1_tobackground_7),
    .toBackground_8(carconnectorv2_1_tobackground_8), .toBackground_9(carconnectorv2_1_tobackground_9),
    .toBackground_10(carconnectorv2_1_tobackground_10), .toFront(carconnectorv2_1_tofront),
    .toFront_2(carconnectorv2_1_tofront_2), .toFront_3(carconnectorv2_1_tofront_3),
    .toFront_4(carconnectorv2_1_tofront_4), .toFront_5(carconnectorv2_1_tofront_5),
    .toFront_6(carconnectorv2_1_tofront_6), .toFront_7(carconnectorv2_1_tofront_7),
    .toFront_8(carconnectorv2_1_tofront_8), .toFront_9(carconnectorv2_1_tofront_9),
    .toFront_10(carconnectorv2_1_tofront_10), .inPlayerShiftD(out_3));
  DotMatrix #(.inputtype("row"), .matrixcols(30), .matrixrows(6)) dotmatrix_11 (
    .row0(carconnectorv2_1_tobackground_3), .row1(carconnectorv2_1_tobackground_4),
    .row2(carconnectorv2_1_tobackground_5), .row3(carconnectorv2_1_tobackground_6),
    .row4(carconnectorv2_1_tobackground_7), .row5(carconnectorv2_1_tobackground_8));
  DotMatrix #(.inputtype("row"), .matrixcols(30), .matrixrows(2)) dotmatrix_12 (
    .row0(carconnectorv2_1_tobackground_9), .row1(carconnectorv2_1_tobackground_10));
  heightFlag heightflag_6 (.height(4'b0101), .playerY(out_1), .eqY(heightflag_6_eqy));
  DotMatrix #(.inputtype("row"), .matrixcols(30), .matrixrows(2)) dotmatrix_13 (
    .row0(carconnectorv2_2_tobackground), .row1(carconnectorv2_2_tobackground_2));
  carConnectorV2 carconnectorv2_2 (
    .inBackShiftD(rightshifter_5_shiftd), .outBackShiftD(carconnectorv2_2_outbackshiftd),
    .inputBackShiftM(rightshifter_5_shiftm), .outputBackShiftM(carconnectorv2_2_outputbackshiftm),
    .outPlayerShiftD(carconnectorv2_2_outplayershiftd), .inPlayerShiftM(out_2),
    .outPlayerShiftM(carconnectorv2_2_outplayershiftm), .inFlag(heightflag_7_eqy),
    .outFlag(carconnectorv2_2_outflag), .toBackground(carconnectorv2_2_tobackground),
    .toBackground_2(carconnectorv2_2_tobackground_2), .toBackground_3(carconnectorv2_2_tobackground_3),
    .toBackground_4(carconnectorv2_2_tobackground_4), .toBackground_5(carconnectorv2_2_tobackground_5),
    .toBackground_6(carconnectorv2_2_tobackground_6), .toBackground_7(carconnectorv2_2_tobackground_7),
    .toBackground_8(carconnectorv2_2_tobackground_8), .toBackground_9(carconnectorv2_2_tobackground_9),
    .toBackground_10(carconnectorv2_2_tobackground_10), .toFront(carconnectorv2_2_tofront),
    .toFront_2(carconnectorv2_2_tofront_2), .toFront_3(carconnectorv2_2_tofront_3),
    .toFront_4(carconnectorv2_2_tofront_4), .toFront_5(carconnectorv2_2_tofront_5),
    .toFront_6(carconnectorv2_2_tofront_6), .toFront_7(carconnectorv2_2_tofront_7),
    .toFront_8(carconnectorv2_2_tofront_8), .toFront_9(carconnectorv2_2_tofront_9),
    .toFront_10(carconnectorv2_2_tofront_10), .inPlayerShiftD(out_3));
  DotMatrix #(.inputtype("row"), .matrixcols(30), .matrixrows(10)) dotmatrix_14 (
    .row0(carconnectorv2_2_tofront), .row1(carconnectorv2_2_tofront_2), .row2(carconnectorv2_2_tofront_3),
    .row3(carconnectorv2_2_tofront_4), .row4(carconnectorv2_2_tofront_5), .row5(carconnectorv2_2_tofront_6),
    .row6(carconnectorv2_2_tofront_7), .row7(carconnectorv2_2_tofront_8), .row8(carconnectorv2_2_tofront_9),
    .row9(carconnectorv2_2_tofront_10));
  DotMatrix #(.inputtype("row"), .matrixcols(30), .matrixrows(6)) dotmatrix_15 (
    .row0(carconnectorv2_2_tobackground_3), .row1(carconnectorv2_2_tobackground_4),
    .row2(carconnectorv2_2_tobackground_5), .row3(carconnectorv2_2_tobackground_6),
    .row4(carconnectorv2_2_tobackground_7), .row5(carconnectorv2_2_tobackground_8));
  DotMatrix #(.inputtype("row"), .matrixcols(30), .matrixrows(2)) dotmatrix_16 (
    .row0(carconnectorv2_2_tobackground_9), .row1(carconnectorv2_2_tobackground_10));
  heightFlag heightflag_7 (.height(4'b0100), .playerY(out_1), .eqY(heightflag_7_eqy));
  DotMatrix #(.inputtype("row"), .matrixcols(30), .matrixrows(10)) dotmatrix_17 (
    .row0(carconnectorv2_3_tofront), .row1(carconnectorv2_3_tofront_2), .row2(carconnectorv2_3_tofront_3),
    .row3(carconnectorv2_3_tofront_4), .row4(carconnectorv2_3_tofront_5), .row5(carconnectorv2_3_tofront_6),
    .row6(carconnectorv2_3_tofront_7), .row7(carconnectorv2_3_tofront_8), .row8(carconnectorv2_3_tofront_9),
    .row9(carconnectorv2_3_tofront_10));
  carConnectorV2 carconnectorv2_3 (
    .inBackShiftD(leftshifter_1_shiftd), .outBackShiftD(carconnectorv2_3_outbackshiftd),
    .inputBackShiftM(leftshifter_1_shiftm), .outputBackShiftM(carconnectorv2_3_outputbackshiftm),
    .outPlayerShiftD(carconnectorv2_3_outplayershiftd), .inPlayerShiftM(out_2),
    .outPlayerShiftM(carconnectorv2_3_outplayershiftm), .inFlag(_2), .outFlag(carconnectorv2_3_outflag),
    .toBackground(carconnectorv2_3_tobackground), .toBackground_2(carconnectorv2_3_tobackground_2),
    .toBackground_3(carconnectorv2_3_tobackground_3), .toBackground_4(carconnectorv2_3_tobackground_4),
    .toBackground_5(carconnectorv2_3_tobackground_5), .toBackground_6(carconnectorv2_3_tobackground_6),
    .toBackground_7(carconnectorv2_3_tobackground_7), .toBackground_8(carconnectorv2_3_tobackground_8),
    .toBackground_9(carconnectorv2_3_tobackground_9), .toBackground_10(carconnectorv2_3_tobackground_10),
    .toFront(carconnectorv2_3_tofront), .toFront_2(carconnectorv2_3_tofront_2),
    .toFront_3(carconnectorv2_3_tofront_3), .toFront_4(carconnectorv2_3_tofront_4),
    .toFront_5(carconnectorv2_3_tofront_5), .toFront_6(carconnectorv2_3_tofront_6),
    .toFront_7(carconnectorv2_3_tofront_7), .toFront_8(carconnectorv2_3_tofront_8),
    .toFront_9(carconnectorv2_3_tofront_9), .toFront_10(carconnectorv2_3_tofront_10), .inPlayerShiftD(out_3));
  DotMatrix #(.inputtype("row"), .matrixcols(30), .matrixrows(2)) dotmatrix_18 (
    .row0(carconnectorv2_3_tobackground), .row1(carconnectorv2_3_tobackground_2));
  DotMatrix #(.inputtype("row"), .matrixcols(30), .matrixrows(6)) dotmatrix_19 (
    .row0(carconnectorv2_3_tobackground_3), .row1(carconnectorv2_3_tobackground_4),
    .row2(carconnectorv2_3_tobackground_5), .row3(carconnectorv2_3_tobackground_6),
    .row4(carconnectorv2_3_tobackground_7), .row5(carconnectorv2_3_tobackground_8));
  DotMatrix #(.inputtype("row"), .matrixcols(30), .matrixrows(2)) dotmatrix_20 (
    .row0(carconnectorv2_3_tobackground_9), .row1(carconnectorv2_3_tobackground_10));
  heightFlag heightflag_8 (.height(4'b0011), .playerY(out_1), .eqY(_2));
  carConnectorV2 carconnectorv2_4 (
    .inBackShiftD(rightshifter_5_shiftd), .outBackShiftD(carconnectorv2_4_outbackshiftd),
    .inputBackShiftM(rightshifter_5_shiftm), .outputBackShiftM(carconnectorv2_4_outputbackshiftm),
    .outPlayerShiftD(carconnectorv2_4_outplayershiftd), .inPlayerShiftM(out_2),
    .outPlayerShiftM(carconnectorv2_4_outplayershiftm), .inFlag(_1), .outFlag(carconnectorv2_4_outflag),
    .toBackground(carconnectorv2_4_tobackground), .toBackground_2(carconnectorv2_4_tobackground_2),
    .toBackground_3(carconnectorv2_4_tobackground_3), .toBackground_4(carconnectorv2_4_tobackground_4),
    .toBackground_5(carconnectorv2_4_tobackground_5), .toBackground_6(carconnectorv2_4_tobackground_6),
    .toBackground_7(carconnectorv2_4_tobackground_7), .toBackground_8(carconnectorv2_4_tobackground_8),
    .toBackground_9(carconnectorv2_4_tobackground_9), .toBackground_10(carconnectorv2_4_tobackground_10),
    .toFront(carconnectorv2_4_tofront), .toFront_2(carconnectorv2_4_tofront_2),
    .toFront_3(carconnectorv2_4_tofront_3), .toFront_4(carconnectorv2_4_tofront_4),
    .toFront_5(carconnectorv2_4_tofront_5), .toFront_6(carconnectorv2_4_tofront_6),
    .toFront_7(carconnectorv2_4_tofront_7), .toFront_8(carconnectorv2_4_tofront_8),
    .toFront_9(carconnectorv2_4_tofront_9), .toFront_10(carconnectorv2_4_tofront_10), .inPlayerShiftD(out_3));
  DotMatrix #(.inputtype("row"), .matrixcols(30), .matrixrows(10)) dotmatrix_21 (
    .row0(carconnectorv2_4_tofront), .row1(carconnectorv2_4_tofront_2), .row2(carconnectorv2_4_tofront_3),
    .row3(carconnectorv2_4_tofront_4), .row4(carconnectorv2_4_tofront_5), .row5(carconnectorv2_4_tofront_6),
    .row6(carconnectorv2_4_tofront_7), .row7(carconnectorv2_4_tofront_8), .row8(carconnectorv2_4_tofront_9),
    .row9(carconnectorv2_4_tofront_10));
  DotMatrix #(.inputtype("row"), .matrixcols(30), .matrixrows(2)) dotmatrix_22 (
    .row0(carconnectorv2_4_tobackground), .row1(carconnectorv2_4_tobackground_2));
  DotMatrix #(.inputtype("row"), .matrixcols(30), .matrixrows(6)) dotmatrix_23 (
    .row0(carconnectorv2_4_tobackground_3), .row1(carconnectorv2_4_tobackground_4),
    .row2(carconnectorv2_4_tobackground_5), .row3(carconnectorv2_4_tobackground_6),
    .row4(carconnectorv2_4_tobackground_7), .row5(carconnectorv2_4_tobackground_8));
  DotMatrix #(.inputtype("row"), .matrixcols(30), .matrixrows(2)) dotmatrix_24 (
    .row0(carconnectorv2_4_tobackground_9), .row1(carconnectorv2_4_tobackground_10));
  heightFlag heightflag_9 (.height(4'b0010), .playerY(out_1), .eqY(_1));
  DotMatrix #(.inputtype("row"), .matrixcols(30), .matrixrows(10)) dotmatrix_25 (
    .row0(carconnectorv2_5_tofront), .row1(carconnectorv2_5_tofront_2), .row2(carconnectorv2_5_tofront_3),
    .row3(carconnectorv2_5_tofront_4), .row4(carconnectorv2_5_tofront_5), .row5(carconnectorv2_5_tofront_6),
    .row6(carconnectorv2_5_tofront_7), .row7(carconnectorv2_5_tofront_8), .row8(carconnectorv2_5_tofront_9),
    .row9(carconnectorv2_5_tofront_10));
  carConnectorV2 carconnectorv2_5 (
    .inBackShiftD(leftshifter_2_shiftd), .outBackShiftD(carconnectorv2_5_outbackshiftd),
    .inputBackShiftM(leftshifter_2_shiftm), .outputBackShiftM(carconnectorv2_5_outputbackshiftm),
    .outPlayerShiftD(carconnectorv2_5_outplayershiftd), .inPlayerShiftM(out_2),
    .outPlayerShiftM(carconnectorv2_5_outplayershiftm), .inFlag(_0), .outFlag(carconnectorv2_5_outflag),
    .toBackground(carconnectorv2_5_tobackground), .toBackground_2(carconnectorv2_5_tobackground_2),
    .toBackground_3(carconnectorv2_5_tobackground_3), .toBackground_4(carconnectorv2_5_tobackground_4),
    .toBackground_5(carconnectorv2_5_tobackground_5), .toBackground_6(carconnectorv2_5_tobackground_6),
    .toBackground_7(carconnectorv2_5_tobackground_7), .toBackground_8(carconnectorv2_5_tobackground_8),
    .toBackground_9(carconnectorv2_5_tobackground_9), .toBackground_10(carconnectorv2_5_tobackground_10),
    .toFront(carconnectorv2_5_tofront), .toFront_2(carconnectorv2_5_tofront_2),
    .toFront_3(carconnectorv2_5_tofront_3), .toFront_4(carconnectorv2_5_tofront_4),
    .toFront_5(carconnectorv2_5_tofront_5), .toFront_6(carconnectorv2_5_tofront_6),
    .toFront_7(carconnectorv2_5_tofront_7), .toFront_8(carconnectorv2_5_tofront_8),
    .toFront_9(carconnectorv2_5_tofront_9), .toFront_10(carconnectorv2_5_tofront_10), .inPlayerShiftD(out_3));
  DotMatrix #(.inputtype("row"), .matrixcols(30), .matrixrows(2)) dotmatrix_26 (
    .row0(carconnectorv2_5_tobackground), .row1(carconnectorv2_5_tobackground_2));
  DotMatrix #(.inputtype("row"), .matrixcols(30), .matrixrows(6)) dotmatrix_27 (
    .row0(carconnectorv2_5_tobackground_3), .row1(carconnectorv2_5_tobackground_4),
    .row2(carconnectorv2_5_tobackground_5), .row3(carconnectorv2_5_tobackground_6),
    .row4(carconnectorv2_5_tobackground_7), .row5(carconnectorv2_5_tobackground_8));
  DotMatrix #(.inputtype("row"), .matrixcols(30), .matrixrows(2)) dotmatrix_28 (
    .row0(carconnectorv2_5_tobackground_9), .row1(carconnectorv2_5_tobackground_10));
  heightFlag heightflag_10 (.height(4'b0001), .playerY(out_1), .eqY(_0));
  DotMatrix #(.inputtype("row"), .matrixcols(30), .matrixrows(10)) dotmatrix_29 (
    .row0(swamp_2_tobackground), .row1(swamp_2_tobackground_2), .row2(swamp_2_tobackground_3),
    .row3(swamp_2_tobackground_4), .row4(swamp_2_tobackground_5), .row5(swamp_2_tobackground_6),
    .row6(swamp_2_tobackground_7), .row7(swamp_2_tobackground_8), .row8(swamp_2_tobackground_9),
    .row9(swamp_2_tobackground_10));
  swamp swamp_2 (
    .inPlayerShiftD(out_3), .outPlayerShiftD(swamp_2_outplayershiftd), .inPlayerShiftM(out_2),
    .outPlayerShiftM(swamp_2_outplayershiftm), .inFlag(heightflag_11_eqy), .outFlag(swamp_2_outflag),
    .toBackground(swamp_2_tobackground), .toFront(swamp_2_tofront), .toBackground_2(swamp_2_tobackground_2),
    .toFront_2(swamp_2_tofront_2), .toBackground_3(swamp_2_tobackground_3), .toFront_3(swamp_2_tofront_3),
    .toBackground_4(swamp_2_tobackground_4), .toFront_4(swamp_2_tofront_4),
    .toBackground_5(swamp_2_tobackground_5), .toFront_5(swamp_2_tofront_5),
    .toBackground_6(swamp_2_tobackground_6), .toFront_6(swamp_2_tofront_6),
    .toBackground_7(swamp_2_tobackground_7), .toFront_7(swamp_2_tofront_7),
    .toBackground_8(swamp_2_tobackground_8), .toFront_8(swamp_2_tofront_8),
    .toBackground_9(swamp_2_tobackground_9), .toFront_9(swamp_2_tofront_9),
    .toBackground_10(swamp_2_tobackground_10), .toFront_10(swamp_2_tofront_10));
  DotMatrix #(.inputtype("row"), .matrixcols(30), .matrixrows(10)) dotmatrix_30 (
    .row0(swamp_2_tofront), .row1(swamp_2_tofront_2), .row2(swamp_2_tofront_3), .row3(swamp_2_tofront_4),
    .row4(swamp_2_tofront_5), .row5(swamp_2_tofront_6), .row6(swamp_2_tofront_7), .row7(swamp_2_tofront_8),
    .row8(swamp_2_tofront_9), .row9(swamp_2_tofront_10));
  heightFlag heightflag_11 (.height(4'b0000), .playerY(out_1), .eqY(heightflag_11_eqy));
  DotMatrix #(.inputtype("row"), .matrixcols(30), .matrixrows(10)) dotmatrix_31 (
    .row0(log_2x1_3_tobackground), .row1(log_2x1_3_tobackground_2), .row2(log_2x1_3_tobackground_3),
    .row3(log_2x1_3_tobackground_4), .row4(log_2x1_3_tobackground_5), .row5(log_2x1_3_tobackground_6),
    .row6(log_2x1_3_tobackground_7), .row7(log_2x1_3_tobackground_8), .row8(log_2x1_3_tobackground_9),
    .row9(log_2x1_3_tobackground_10));
  DotMatrix #(.inputtype("row"), .matrixcols(30), .matrixrows(10)) dotmatrix_32 (
    .row0(log_2x1_3_tofront), .row1(log_2x1_3_tofront_2), .row2(log_2x1_3_tofront_3),
    .row3(log_2x1_3_tofront_4), .row4(log_2x1_3_tofront_5), .row5(log_2x1_3_tofront_6),
    .row6(log_2x1_3_tofront_7), .row7(log_2x1_3_tofront_8), .row8(log_2x1_3_tofront_9),
    .row9(log_2x1_3_tofront_10));
  log_2x1 log_2x1_3 (
    .inBackShiftD(log_2x1_1_outbackshiftd), .outBackShiftD(log_2x1_3_outbackshiftd),
    .inputBackShiftM(log_2x1_1_outputbackshiftm), .outputBackShiftM(log_2x1_3_outputbackshiftm),
    .inPlayerShiftD(log_2x1_1_outplayershiftd), .outPlayerShiftD(log_2x1_3_outplayershiftd),
    .inPlayerShiftM(log_2x1_1_outplayershiftm), .outPlayerShiftM(log_2x1_3_outplayershiftm),
    .inFlag(log_2x1_1_outflag), .outFlag(log_2x1_3_outflag), .toBackground(log_2x1_3_tobackground),
    .toBackground_2(log_2x1_3_tobackground_2), .toBackground_3(log_2x1_3_tobackground_3),
    .toBackground_4(log_2x1_3_tobackground_4), .toBackground_5(log_2x1_3_tobackground_5),
    .toBackground_6(log_2x1_3_tobackground_6), .toBackground_7(log_2x1_3_tobackground_7),
    .toBackground_8(log_2x1_3_tobackground_8), .toBackground_9(log_2x1_3_tobackground_9),
    .toBackground_10(log_2x1_3_tobackground_10), .toFront(log_2x1_3_tofront),
    .toFront_2(log_2x1_3_tofront_2), .toFront_3(log_2x1_3_tofront_3), .toFront_4(log_2x1_3_tofront_4),
    .toFront_5(log_2x1_3_tofront_5), .toFront_6(log_2x1_3_tofront_6), .toFront_7(log_2x1_3_tofront_7),
    .toFront_8(log_2x1_3_tofront_8), .toFront_9(log_2x1_3_tofront_9), .toFront_10(log_2x1_3_tofront_10));
  DotMatrix #(.inputtype("row"), .matrixcols(30), .matrixrows(10)) dotmatrix_33 (
    .row0(log_3x2_3_tofront), .row1(log_3x2_3_tofront_2), .row2(log_3x2_3_tofront_3),
    .row3(log_3x2_3_tofront_4), .row4(log_3x2_3_tofront_5), .row5(log_3x2_3_tofront_6),
    .row6(log_3x2_3_tofront_7), .row7(log_3x2_3_tofront_8), .row8(log_3x2_3_tofront_9),
    .row9(log_3x2_3_tofront_10));
  DotMatrix #(.inputtype("row"), .matrixcols(30), .matrixrows(10)) dotmatrix_34 (
    .row0(log_3x2_3_tobackground), .row1(log_3x2_3_tobackground_2), .row2(log_3x2_3_tobackground_3),
    .row3(log_3x2_3_tobackground_4), .row4(log_3x2_3_tobackground_5), .row5(log_3x2_3_tobackground_6),
    .row6(log_3x2_3_tobackground_7), .row7(log_3x2_3_tobackground_8), .row8(log_3x2_3_tobackground_9),
    .row9(log_3x2_3_tobackground_10));
  log_3x2 log_3x2_3 (
    .inBackShiftD(log_3x2_1_outbackshiftd), .outBackShiftD(log_3x2_3_outbackshiftd),
    .inputBackShiftM(log_3x2_1_outputbackshiftm), .outputBackShiftM(log_3x2_3_outputbackshiftm),
    .inPlayerShiftD(log_3x2_1_outplayershiftd), .outPlayerShiftD(log_3x2_3_outplayershiftd),
    .inPlayerShiftM(log_3x2_1_outplayershiftm), .outPlayerShiftM(log_3x2_3_outplayershiftm),
    .inFlag(log_3x2_1_outflag), .outFlag(log_3x2_3_outflag), .toBackground(log_3x2_3_tobackground),
    .toBackground_2(log_3x2_3_tobackground_2), .toBackground_3(log_3x2_3_tobackground_3),
    .toBackground_4(log_3x2_3_tobackground_4), .toBackground_5(log_3x2_3_tobackground_5),
    .toBackground_6(log_3x2_3_tobackground_6), .toBackground_7(log_3x2_3_tobackground_7),
    .toBackground_8(log_3x2_3_tobackground_8), .toBackground_9(log_3x2_3_tobackground_9),
    .toBackground_10(log_3x2_3_tobackground_10), .toFront(log_3x2_3_tofront),
    .toFront_2(log_3x2_3_tofront_2), .toFront_3(log_3x2_3_tofront_3), .toFront_4(log_3x2_3_tofront_4),
    .toFront_5(log_3x2_3_tofront_5), .toFront_6(log_3x2_3_tofront_6), .toFront_7(log_3x2_3_tofront_7),
    .toFront_8(log_3x2_3_tofront_8), .toFront_9(log_3x2_3_tofront_9), .toFront_10(log_3x2_3_tofront_10));
  DotMatrix #(.inputtype("row"), .matrixcols(30), .matrixrows(10)) dotmatrix_35 (
    .row0(log_1x1_2_tofront), .row1(log_1x1_2_tofront_2), .row2(log_1x1_2_tofront_3),
    .row3(log_1x1_2_tofront_4), .row4(log_1x1_2_tofront_5), .row5(log_1x1_2_tofront_6),
    .row6(log_1x1_2_tofront_7), .row7(log_1x1_2_tofront_8), .row8(log_1x1_2_tofront_9),
    .row9(log_1x1_2_tofront_10));
  log_1x1 log_1x1_2 (
    .inBackShiftD(log_1x1_1_outbackshiftd), .outBackShiftD(log_1x1_2_outbackshiftd),
    .inputBackShiftM(log_1x1_1_outputbackshiftm), .outputBackShiftM(log_1x1_2_outputbackshiftm),
    .inPlayerShiftD(log_1x1_1_outplayershiftd), .outPlayerShiftD(log_1x1_2_outplayershiftd),
    .inPlayerShiftM(log_1x1_1_outplayershiftm), .outPlayerShiftM(log_1x1_2_outplayershiftm),
    .inFlag(log_1x1_1_outflag), .outFlag(log_1x1_2_outflag), .toBackground(log_1x1_2_tobackground),
    .toBackground_2(log_1x1_2_tobackground_2), .toBackground_3(log_1x1_2_tobackground_3),
    .toBackground_4(log_1x1_2_tobackground_4), .toBackground_5(log_1x1_2_tobackground_5),
    .toBackground_6(log_1x1_2_tobackground_6), .toBackground_7(log_1x1_2_tobackground_7),
    .toBackground_8(log_1x1_2_tobackground_8), .toBackground_9(log_1x1_2_tobackground_9),
    .toBackground_10(log_1x1_2_tobackground_10), .toFront(log_1x1_2_tofront),
    .toFront_2(log_1x1_2_tofront_2), .toFront_3(log_1x1_2_tofront_3), .toFront_4(log_1x1_2_tofront_4),
    .toFront_5(log_1x1_2_tofront_5), .toFront_6(log_1x1_2_tofront_6), .toFront_7(log_1x1_2_tofront_7),
    .toFront_8(log_1x1_2_tofront_8), .toFront_9(log_1x1_2_tofront_9), .toFront_10(log_1x1_2_tofront_10));
  DotMatrix #(.inputtype("row"), .matrixcols(30), .matrixrows(10)) dotmatrix_36 (
    .row0(log_1x1_2_tobackground), .row1(log_1x1_2_tobackground_2), .row2(log_1x1_2_tobackground_3),
    .row3(log_1x1_2_tobackground_4), .row4(log_1x1_2_tobackground_5), .row5(log_1x1_2_tobackground_6),
    .row6(log_1x1_2_tobackground_7), .row7(log_1x1_2_tobackground_8), .row8(log_1x1_2_tobackground_9),
    .row9(log_1x1_2_tobackground_10));
  swamp swamp_3 (
    .inPlayerShiftD(swamp_1_outplayershiftd), .outPlayerShiftD(swamp_3_outplayershiftd),
    .inPlayerShiftM(swamp_1_outplayershiftm), .outPlayerShiftM(swamp_3_outplayershiftm),
    .inFlag(swamp_1_outflag), .outFlag(swamp_3_outflag), .toBackground(swamp_3_tobackground),
    .toFront(swamp_3_tofront), .toBackground_2(swamp_3_tobackground_2), .toFront_2(swamp_3_tofront_2),
    .toBackground_3(swamp_3_tobackground_3), .toFront_3(swamp_3_tofront_3),
    .toBackground_4(swamp_3_tobackground_4), .toFront_4(swamp_3_tofront_4),
    .toBackground_5(swamp_3_tobackground_5), .toFront_5(swamp_3_tofront_5),
    .toBackground_6(swamp_3_tobackground_6), .toFront_6(swamp_3_tofront_6),
    .toBackground_7(swamp_3_tobackground_7), .toFront_7(swamp_3_tofront_7),
    .toBackground_8(swamp_3_tobackground_8), .toFront_8(swamp_3_tofront_8),
    .toBackground_9(swamp_3_tobackground_9), .toFront_9(swamp_3_tofront_9),
    .toBackground_10(swamp_3_tobackground_10), .toFront_10(swamp_3_tofront_10));
  DotMatrix #(.inputtype("row"), .matrixcols(30), .matrixrows(10)) dotmatrix_37 (
    .row0(swamp_3_tofront), .row1(swamp_3_tofront_2), .row2(swamp_3_tofront_3), .row3(swamp_3_tofront_4),
    .row4(swamp_3_tofront_5), .row5(swamp_3_tofront_6), .row6(swamp_3_tofront_7), .row7(swamp_3_tofront_8),
    .row8(swamp_3_tofront_9), .row9(swamp_3_tofront_10));
  DotMatrix #(.inputtype("row"), .matrixcols(30), .matrixrows(10)) dotmatrix_38 (
    .row0(swamp_3_tobackground), .row1(swamp_3_tobackground_2), .row2(swamp_3_tobackground_3),
    .row3(swamp_3_tobackground_4), .row4(swamp_3_tobackground_5), .row5(swamp_3_tobackground_6),
    .row6(swamp_3_tobackground_7), .row7(swamp_3_tobackground_8), .row8(swamp_3_tobackground_9),
    .row9(swamp_3_tobackground_10));
  DotMatrix #(.inputtype("row"), .matrixcols(30), .matrixrows(2)) dotmatrix_39 (
    .row0(carconnectorv2_6_tobackground), .row1(carconnectorv2_6_tobackground_2));
  carConnectorV2 carconnectorv2_6 (
    .inBackShiftD(carconnectorv2_1_outbackshiftd), .outBackShiftD(carconnectorv2_6_outbackshiftd),
    .inputBackShiftM(carconnectorv2_1_outputbackshiftm),
    .outputBackShiftM(carconnectorv2_6_outputbackshiftm), .outPlayerShiftD(carconnectorv2_6_outplayershiftd),
    .inPlayerShiftM(carconnectorv2_1_outplayershiftm), .outPlayerShiftM(carconnectorv2_6_outplayershiftm),
    .inFlag(carconnectorv2_1_outflag), .outFlag(carconnectorv2_6_outflag),
    .toBackground(carconnectorv2_6_tobackground), .toBackground_2(carconnectorv2_6_tobackground_2),
    .toBackground_3(carconnectorv2_6_tobackground_3), .toBackground_4(carconnectorv2_6_tobackground_4),
    .toBackground_5(carconnectorv2_6_tobackground_5), .toBackground_6(carconnectorv2_6_tobackground_6),
    .toBackground_7(carconnectorv2_6_tobackground_7), .toBackground_8(carconnectorv2_6_tobackground_8),
    .toBackground_9(carconnectorv2_6_tobackground_9), .toBackground_10(carconnectorv2_6_tobackground_10),
    .toFront(carconnectorv2_6_tofront), .toFront_2(carconnectorv2_6_tofront_2),
    .toFront_3(carconnectorv2_6_tofront_3), .toFront_4(carconnectorv2_6_tofront_4),
    .toFront_5(carconnectorv2_6_tofront_5), .toFront_6(carconnectorv2_6_tofront_6),
    .toFront_7(carconnectorv2_6_tofront_7), .toFront_8(carconnectorv2_6_tofront_8),
    .toFront_9(carconnectorv2_6_tofront_9), .toFront_10(carconnectorv2_6_tofront_10),
    .inPlayerShiftD(carconnectorv2_1_outplayershiftd));
  DotMatrix #(.inputtype("row"), .matrixcols(30), .matrixrows(10)) dotmatrix_40 (
    .row0(carconnectorv2_6_tofront), .row1(carconnectorv2_6_tofront_2), .row2(carconnectorv2_6_tofront_3),
    .row3(carconnectorv2_6_tofront_4), .row4(carconnectorv2_6_tofront_5), .row5(carconnectorv2_6_tofront_6),
    .row6(carconnectorv2_6_tofront_7), .row7(carconnectorv2_6_tofront_8), .row8(carconnectorv2_6_tofront_9),
    .row9(carconnectorv2_6_tofront_10));
  DotMatrix #(.inputtype("row"), .matrixcols(30), .matrixrows(6)) dotmatrix_41 (
    .row0(carconnectorv2_6_tobackground_3), .row1(carconnectorv2_6_tobackground_4),
    .row2(carconnectorv2_6_tobackground_5), .row3(carconnectorv2_6_tobackground_6),
    .row4(carconnectorv2_6_tobackground_7), .row5(carconnectorv2_6_tobackground_8));
  DotMatrix #(.inputtype("row"), .matrixcols(30), .matrixrows(2)) dotmatrix_42 (
    .row0(carconnectorv2_6_tobackground_9), .row1(carconnectorv2_6_tobackground_10));
  carConnectorV2 carconnectorv2_7 (
    .inBackShiftD(carconnectorv2_2_outbackshiftd), .outBackShiftD(carconnectorv2_7_outbackshiftd),
    .inputBackShiftM(carconnectorv2_2_outputbackshiftm),
    .outputBackShiftM(carconnectorv2_7_outputbackshiftm), .outPlayerShiftD(carconnectorv2_7_outplayershiftd),
    .inPlayerShiftM(carconnectorv2_2_outplayershiftm), .outPlayerShiftM(carconnectorv2_7_outplayershiftm),
    .inFlag(carconnectorv2_2_outflag), .outFlag(carconnectorv2_7_outflag),
    .toBackground(carconnectorv2_7_tobackground), .toBackground_2(carconnectorv2_7_tobackground_2),
    .toBackground_3(carconnectorv2_7_tobackground_3), .toBackground_4(carconnectorv2_7_tobackground_4),
    .toBackground_5(carconnectorv2_7_tobackground_5), .toBackground_6(carconnectorv2_7_tobackground_6),
    .toBackground_7(carconnectorv2_7_tobackground_7), .toBackground_8(carconnectorv2_7_tobackground_8),
    .toBackground_9(carconnectorv2_7_tobackground_9), .toBackground_10(carconnectorv2_7_tobackground_10),
    .toFront(carconnectorv2_7_tofront), .toFront_2(carconnectorv2_7_tofront_2),
    .toFront_3(carconnectorv2_7_tofront_3), .toFront_4(carconnectorv2_7_tofront_4),
    .toFront_5(carconnectorv2_7_tofront_5), .toFront_6(carconnectorv2_7_tofront_6),
    .toFront_7(carconnectorv2_7_tofront_7), .toFront_8(carconnectorv2_7_tofront_8),
    .toFront_9(carconnectorv2_7_tofront_9), .toFront_10(carconnectorv2_7_tofront_10),
    .inPlayerShiftD(carconnectorv2_2_outplayershiftd));
  DotMatrix #(.inputtype("row"), .matrixcols(30), .matrixrows(2)) dotmatrix_43 (
    .row0(carconnectorv2_7_tobackground), .row1(carconnectorv2_7_tobackground_2));
  DotMatrix #(.inputtype("row"), .matrixcols(30), .matrixrows(10)) dotmatrix_44 (
    .row0(carconnectorv2_7_tofront), .row1(carconnectorv2_7_tofront_2), .row2(carconnectorv2_7_tofront_3),
    .row3(carconnectorv2_7_tofront_4), .row4(carconnectorv2_7_tofront_5), .row5(carconnectorv2_7_tofront_6),
    .row6(carconnectorv2_7_tofront_7), .row7(carconnectorv2_7_tofront_8), .row8(carconnectorv2_7_tofront_9),
    .row9(carconnectorv2_7_tofront_10));
  DotMatrix #(.inputtype("row"), .matrixcols(30), .matrixrows(6)) dotmatrix_45 (
    .row0(carconnectorv2_7_tobackground_3), .row1(carconnectorv2_7_tobackground_4),
    .row2(carconnectorv2_7_tobackground_5), .row3(carconnectorv2_7_tobackground_6),
    .row4(carconnectorv2_7_tobackground_7), .row5(carconnectorv2_7_tobackground_8));
  DotMatrix #(.inputtype("row"), .matrixcols(30), .matrixrows(2)) dotmatrix_46 (
    .row0(carconnectorv2_7_tobackground_9), .row1(carconnectorv2_7_tobackground_10));
  carConnectorV2 carconnectorv2_8 (
    .inBackShiftD(carconnectorv2_3_outbackshiftd), .outBackShiftD(carconnectorv2_8_outbackshiftd),
    .inputBackShiftM(carconnectorv2_3_outputbackshiftm),
    .outputBackShiftM(carconnectorv2_8_outputbackshiftm), .outPlayerShiftD(carconnectorv2_8_outplayershiftd),
    .inPlayerShiftM(carconnectorv2_3_outplayershiftm), .outPlayerShiftM(carconnectorv2_8_outplayershiftm),
    .inFlag(carconnectorv2_3_outflag), .outFlag(carconnectorv2_8_outflag),
    .toBackground(carconnectorv2_8_tobackground), .toBackground_2(carconnectorv2_8_tobackground_2),
    .toBackground_3(carconnectorv2_8_tobackground_3), .toBackground_4(carconnectorv2_8_tobackground_4),
    .toBackground_5(carconnectorv2_8_tobackground_5), .toBackground_6(carconnectorv2_8_tobackground_6),
    .toBackground_7(carconnectorv2_8_tobackground_7), .toBackground_8(carconnectorv2_8_tobackground_8),
    .toBackground_9(carconnectorv2_8_tobackground_9), .toBackground_10(carconnectorv2_8_tobackground_10),
    .toFront(carconnectorv2_8_tofront), .toFront_2(carconnectorv2_8_tofront_2),
    .toFront_3(carconnectorv2_8_tofront_3), .toFront_4(carconnectorv2_8_tofront_4),
    .toFront_5(carconnectorv2_8_tofront_5), .toFront_6(carconnectorv2_8_tofront_6),
    .toFront_7(carconnectorv2_8_tofront_7), .toFront_8(carconnectorv2_8_tofront_8),
    .toFront_9(carconnectorv2_8_tofront_9), .toFront_10(carconnectorv2_8_tofront_10),
    .inPlayerShiftD(carconnectorv2_3_outplayershiftd));
  DotMatrix #(.inputtype("row"), .matrixcols(30), .matrixrows(2)) dotmatrix_47 (
    .row0(carconnectorv2_8_tobackground), .row1(carconnectorv2_8_tobackground_2));
  DotMatrix #(.inputtype("row"), .matrixcols(30), .matrixrows(10)) dotmatrix_48 (
    .row0(carconnectorv2_8_tofront), .row1(carconnectorv2_8_tofront_2), .row2(carconnectorv2_8_tofront_3),
    .row3(carconnectorv2_8_tofront_4), .row4(carconnectorv2_8_tofront_5), .row5(carconnectorv2_8_tofront_6),
    .row6(carconnectorv2_8_tofront_7), .row7(carconnectorv2_8_tofront_8), .row8(carconnectorv2_8_tofront_9),
    .row9(carconnectorv2_8_tofront_10));
  DotMatrix #(.inputtype("row"), .matrixcols(30), .matrixrows(6)) dotmatrix_49 (
    .row0(carconnectorv2_8_tobackground_3), .row1(carconnectorv2_8_tobackground_4),
    .row2(carconnectorv2_8_tobackground_5), .row3(carconnectorv2_8_tobackground_6),
    .row4(carconnectorv2_8_tobackground_7), .row5(carconnectorv2_8_tobackground_8));
  DotMatrix #(.inputtype("row"), .matrixcols(30), .matrixrows(2)) dotmatrix_50 (
    .row0(carconnectorv2_8_tobackground_9), .row1(carconnectorv2_8_tobackground_10));
  carConnectorV2 carconnectorv2_9 (
    .inBackShiftD(carconnectorv2_4_outbackshiftd), .outBackShiftD(carconnectorv2_9_outbackshiftd),
    .inputBackShiftM(carconnectorv2_4_outputbackshiftm),
    .outputBackShiftM(carconnectorv2_9_outputbackshiftm), .outPlayerShiftD(carconnectorv2_9_outplayershiftd),
    .inPlayerShiftM(carconnectorv2_4_outplayershiftm), .outPlayerShiftM(carconnectorv2_9_outplayershiftm),
    .inFlag(carconnectorv2_4_outflag), .outFlag(carconnectorv2_9_outflag),
    .toBackground(carconnectorv2_9_tobackground), .toBackground_2(carconnectorv2_9_tobackground_2),
    .toBackground_3(carconnectorv2_9_tobackground_3), .toBackground_4(carconnectorv2_9_tobackground_4),
    .toBackground_5(carconnectorv2_9_tobackground_5), .toBackground_6(carconnectorv2_9_tobackground_6),
    .toBackground_7(carconnectorv2_9_tobackground_7), .toBackground_8(carconnectorv2_9_tobackground_8),
    .toBackground_9(carconnectorv2_9_tobackground_9), .toBackground_10(carconnectorv2_9_tobackground_10),
    .toFront(carconnectorv2_9_tofront), .toFront_2(carconnectorv2_9_tofront_2),
    .toFront_3(carconnectorv2_9_tofront_3), .toFront_4(carconnectorv2_9_tofront_4),
    .toFront_5(carconnectorv2_9_tofront_5), .toFront_6(carconnectorv2_9_tofront_6),
    .toFront_7(carconnectorv2_9_tofront_7), .toFront_8(carconnectorv2_9_tofront_8),
    .toFront_9(carconnectorv2_9_tofront_9), .toFront_10(carconnectorv2_9_tofront_10),
    .inPlayerShiftD(carconnectorv2_4_outplayershiftd));
  DotMatrix #(.inputtype("row"), .matrixcols(30), .matrixrows(10)) dotmatrix_51 (
    .row0(carconnectorv2_9_tofront), .row1(carconnectorv2_9_tofront_2), .row2(carconnectorv2_9_tofront_3),
    .row3(carconnectorv2_9_tofront_4), .row4(carconnectorv2_9_tofront_5), .row5(carconnectorv2_9_tofront_6),
    .row6(carconnectorv2_9_tofront_7), .row7(carconnectorv2_9_tofront_8), .row8(carconnectorv2_9_tofront_9),
    .row9(carconnectorv2_9_tofront_10));
  DotMatrix #(.inputtype("row"), .matrixcols(30), .matrixrows(2)) dotmatrix_52 (
    .row0(carconnectorv2_9_tobackground), .row1(carconnectorv2_9_tobackground_2));
  DotMatrix #(.inputtype("row"), .matrixcols(30), .matrixrows(6)) dotmatrix_53 (
    .row0(carconnectorv2_9_tobackground_3), .row1(carconnectorv2_9_tobackground_4),
    .row2(carconnectorv2_9_tobackground_5), .row3(carconnectorv2_9_tobackground_6),
    .row4(carconnectorv2_9_tobackground_7), .row5(carconnectorv2_9_tobackground_8));
  DotMatrix #(.inputtype("row"), .matrixcols(30), .matrixrows(2)) dotmatrix_54 (
    .row0(carconnectorv2_9_tobackground_9), .row1(carconnectorv2_9_tobackground_10));
  carConnectorV2 carconnectorv2_10 (
    .inBackShiftD(carconnectorv2_5_outbackshiftd), .outBackShiftD(carconnectorv2_10_outbackshiftd),
    .inputBackShiftM(carconnectorv2_5_outputbackshiftm),
    .outputBackShiftM(carconnectorv2_10_outputbackshiftm),
    .outPlayerShiftD(carconnectorv2_10_outplayershiftd), .inPlayerShiftM(carconnectorv2_5_outplayershiftm),
    .outPlayerShiftM(carconnectorv2_10_outplayershiftm), .inFlag(carconnectorv2_5_outflag),
    .outFlag(carconnectorv2_10_outflag), .toBackground(carconnectorv2_10_tobackground),
    .toBackground_2(carconnectorv2_10_tobackground_2), .toBackground_3(carconnectorv2_10_tobackground_3),
    .toBackground_4(carconnectorv2_10_tobackground_4), .toBackground_5(carconnectorv2_10_tobackground_5),
    .toBackground_6(carconnectorv2_10_tobackground_6), .toBackground_7(carconnectorv2_10_tobackground_7),
    .toBackground_8(carconnectorv2_10_tobackground_8), .toBackground_9(carconnectorv2_10_tobackground_9),
    .toBackground_10(carconnectorv2_10_tobackground_10), .toFront(carconnectorv2_10_tofront),
    .toFront_2(carconnectorv2_10_tofront_2), .toFront_3(carconnectorv2_10_tofront_3),
    .toFront_4(carconnectorv2_10_tofront_4), .toFront_5(carconnectorv2_10_tofront_5),
    .toFront_6(carconnectorv2_10_tofront_6), .toFront_7(carconnectorv2_10_tofront_7),
    .toFront_8(carconnectorv2_10_tofront_8), .toFront_9(carconnectorv2_10_tofront_9),
    .toFront_10(carconnectorv2_10_tofront_10), .inPlayerShiftD(carconnectorv2_5_outplayershiftd));
  DotMatrix #(.inputtype("row"), .matrixcols(30), .matrixrows(2)) dotmatrix_55 (
    .row0(carconnectorv2_10_tobackground), .row1(carconnectorv2_10_tobackground_2));
  DotMatrix #(.inputtype("row"), .matrixcols(30), .matrixrows(10)) dotmatrix_56 (
    .row0(carconnectorv2_10_tofront), .row1(carconnectorv2_10_tofront_2), .row2(carconnectorv2_10_tofront_3),
    .row3(carconnectorv2_10_tofront_4), .row4(carconnectorv2_10_tofront_5),
    .row5(carconnectorv2_10_tofront_6), .row6(carconnectorv2_10_tofront_7),
    .row7(carconnectorv2_10_tofront_8), .row8(carconnectorv2_10_tofront_9),
    .row9(carconnectorv2_10_tofront_10));
  DotMatrix #(.inputtype("row"), .matrixcols(30), .matrixrows(6)) dotmatrix_57 (
    .row0(carconnectorv2_10_tobackground_3), .row1(carconnectorv2_10_tobackground_4),
    .row2(carconnectorv2_10_tobackground_5), .row3(carconnectorv2_10_tobackground_6),
    .row4(carconnectorv2_10_tobackground_7), .row5(carconnectorv2_10_tobackground_8));
  DotMatrix #(.inputtype("row"), .matrixcols(30), .matrixrows(2)) dotmatrix_58 (
    .row0(carconnectorv2_10_tobackground_9), .row1(carconnectorv2_10_tobackground_10));
  DotMatrix #(.inputtype("row"), .matrixcols(30), .matrixrows(10)) dotmatrix_59 (
    .row0(swamp_4_tofront), .row1(swamp_4_tofront_2), .row2(swamp_4_tofront_3), .row3(swamp_4_tofront_4),
    .row4(swamp_4_tofront_5), .row5(swamp_4_tofront_6), .row6(swamp_4_tofront_7), .row7(swamp_4_tofront_8),
    .row8(swamp_4_tofront_9), .row9(swamp_4_tofront_10));
  DotMatrix #(.inputtype("row"), .matrixcols(30), .matrixrows(10)) dotmatrix_60 (
    .row0(swamp_4_tobackground), .row1(swamp_4_tobackground_2), .row2(swamp_4_tobackground_3),
    .row3(swamp_4_tobackground_4), .row4(swamp_4_tobackground_5), .row5(swamp_4_tobackground_6),
    .row6(swamp_4_tobackground_7), .row7(swamp_4_tobackground_8), .row8(swamp_4_tobackground_9),
    .row9(swamp_4_tobackground_10));
  swamp swamp_4 (
    .inPlayerShiftD(swamp_2_outplayershiftd), .outPlayerShiftD(swamp_4_outplayershiftd),
    .inPlayerShiftM(swamp_2_outplayershiftm), .outPlayerShiftM(swamp_4_outplayershiftm),
    .inFlag(swamp_2_outflag), .outFlag(swamp_4_outflag), .toBackground(swamp_4_tobackground),
    .toFront(swamp_4_tofront), .toBackground_2(swamp_4_tobackground_2), .toFront_2(swamp_4_tofront_2),
    .toBackground_3(swamp_4_tobackground_3), .toFront_3(swamp_4_tofront_3),
    .toBackground_4(swamp_4_tobackground_4), .toFront_4(swamp_4_tofront_4),
    .toBackground_5(swamp_4_tobackground_5), .toFront_5(swamp_4_tofront_5),
    .toBackground_6(swamp_4_tobackground_6), .toFront_6(swamp_4_tofront_6),
    .toBackground_7(swamp_4_tobackground_7), .toFront_7(swamp_4_tofront_7),
    .toBackground_8(swamp_4_tobackground_8), .toFront_8(swamp_4_tofront_8),
    .toBackground_9(swamp_4_tobackground_9), .toFront_9(swamp_4_tofront_9),
    .toBackground_10(swamp_4_tobackground_10), .toFront_10(swamp_4_tofront_10));
  DotMatrix #(.inputtype("row"), .matrixcols(30), .matrixrows(10)) dotmatrix_61 (
    .row0(log_2x1_4_tobackground), .row1(log_2x1_4_tobackground_2), .row2(log_2x1_4_tobackground_3),
    .row3(log_2x1_4_tobackground_4), .row4(log_2x1_4_tobackground_5), .row5(log_2x1_4_tobackground_6),
    .row6(log_2x1_4_tobackground_7), .row7(log_2x1_4_tobackground_8), .row8(log_2x1_4_tobackground_9),
    .row9(log_2x1_4_tobackground_10));
  DotMatrix #(.inputtype("row"), .matrixcols(30), .matrixrows(10)) dotmatrix_62 (
    .row0(log_2x1_4_tofront), .row1(log_2x1_4_tofront_2), .row2(log_2x1_4_tofront_3),
    .row3(log_2x1_4_tofront_4), .row4(log_2x1_4_tofront_5), .row5(log_2x1_4_tofront_6),
    .row6(log_2x1_4_tofront_7), .row7(log_2x1_4_tofront_8), .row8(log_2x1_4_tofront_9),
    .row9(log_2x1_4_tofront_10));
  log_2x1 log_2x1_4 (
    .inBackShiftD(log_2x1_3_outbackshiftd), .outBackShiftD(log_2x1_4_outbackshiftd),
    .inputBackShiftM(log_2x1_3_outputbackshiftm), .outputBackShiftM(log_2x1_4_outputbackshiftm),
    .inPlayerShiftD(log_2x1_3_outplayershiftd), .outPlayerShiftD(log_2x1_4_outplayershiftd),
    .inPlayerShiftM(log_2x1_3_outplayershiftm), .outPlayerShiftM(log_2x1_4_outplayershiftm),
    .inFlag(log_2x1_3_outflag), .outFlag(log_2x1_4_outflag), .toBackground(log_2x1_4_tobackground),
    .toBackground_2(log_2x1_4_tobackground_2), .toBackground_3(log_2x1_4_tobackground_3),
    .toBackground_4(log_2x1_4_tobackground_4), .toBackground_5(log_2x1_4_tobackground_5),
    .toBackground_6(log_2x1_4_tobackground_6), .toBackground_7(log_2x1_4_tobackground_7),
    .toBackground_8(log_2x1_4_tobackground_8), .toBackground_9(log_2x1_4_tobackground_9),
    .toBackground_10(log_2x1_4_tobackground_10), .toFront(log_2x1_4_tofront),
    .toFront_2(log_2x1_4_tofront_2), .toFront_3(log_2x1_4_tofront_3), .toFront_4(log_2x1_4_tofront_4),
    .toFront_5(log_2x1_4_tofront_5), .toFront_6(log_2x1_4_tofront_6), .toFront_7(log_2x1_4_tofront_7),
    .toFront_8(log_2x1_4_tofront_8), .toFront_9(log_2x1_4_tofront_9), .toFront_10(log_2x1_4_tofront_10));
  DotMatrix #(.inputtype("row"), .matrixcols(30), .matrixrows(10)) dotmatrix_63 (
    .row0(log_3x2_4_tofront), .row1(log_3x2_4_tofront_2), .row2(log_3x2_4_tofront_3),
    .row3(log_3x2_4_tofront_4), .row4(log_3x2_4_tofront_5), .row5(log_3x2_4_tofront_6),
    .row6(log_3x2_4_tofront_7), .row7(log_3x2_4_tofront_8), .row8(log_3x2_4_tofront_9),
    .row9(log_3x2_4_tofront_10));
  DotMatrix #(.inputtype("row"), .matrixcols(30), .matrixrows(10)) dotmatrix_64 (
    .row0(log_3x2_4_tobackground), .row1(log_3x2_4_tobackground_2), .row2(log_3x2_4_tobackground_3),
    .row3(log_3x2_4_tobackground_4), .row4(log_3x2_4_tobackground_5), .row5(log_3x2_4_tobackground_6),
    .row6(log_3x2_4_tobackground_7), .row7(log_3x2_4_tobackground_8), .row8(log_3x2_4_tobackground_9),
    .row9(log_3x2_4_tobackground_10));
  log_3x2 log_3x2_4 (
    .inBackShiftD(log_3x2_3_outbackshiftd), .outBackShiftD(log_3x2_4_outbackshiftd),
    .inputBackShiftM(log_3x2_3_outputbackshiftm), .outputBackShiftM(log_3x2_4_outputbackshiftm),
    .inPlayerShiftD(log_3x2_3_outplayershiftd), .outPlayerShiftD(log_3x2_4_outplayershiftd),
    .inPlayerShiftM(log_3x2_3_outplayershiftm), .outPlayerShiftM(log_3x2_4_outplayershiftm),
    .inFlag(log_3x2_3_outflag), .outFlag(log_3x2_4_outflag), .toBackground(log_3x2_4_tobackground),
    .toBackground_2(log_3x2_4_tobackground_2), .toBackground_3(log_3x2_4_tobackground_3),
    .toBackground_4(log_3x2_4_tobackground_4), .toBackground_5(log_3x2_4_tobackground_5),
    .toBackground_6(log_3x2_4_tobackground_6), .toBackground_7(log_3x2_4_tobackground_7),
    .toBackground_8(log_3x2_4_tobackground_8), .toBackground_9(log_3x2_4_tobackground_9),
    .toBackground_10(log_3x2_4_tobackground_10), .toFront(log_3x2_4_tofront),
    .toFront_2(log_3x2_4_tofront_2), .toFront_3(log_3x2_4_tofront_3), .toFront_4(log_3x2_4_tofront_4),
    .toFront_5(log_3x2_4_tofront_5), .toFront_6(log_3x2_4_tofront_6), .toFront_7(log_3x2_4_tofront_7),
    .toFront_8(log_3x2_4_tofront_8), .toFront_9(log_3x2_4_tofront_9), .toFront_10(log_3x2_4_tofront_10));
  DotMatrix #(.inputtype("row"), .matrixcols(30), .matrixrows(10)) dotmatrix_65 (
    .row0(log_1x1_3_tofront), .row1(log_1x1_3_tofront_2), .row2(log_1x1_3_tofront_3),
    .row3(log_1x1_3_tofront_4), .row4(log_1x1_3_tofront_5), .row5(log_1x1_3_tofront_6),
    .row6(log_1x1_3_tofront_7), .row7(log_1x1_3_tofront_8), .row8(log_1x1_3_tofront_9),
    .row9(log_1x1_3_tofront_10));
  log_1x1 log_1x1_3 (
    .inBackShiftD(log_1x1_2_outbackshiftd), .outBackShiftD(log_1x1_3_outbackshiftd),
    .inputBackShiftM(log_1x1_2_outputbackshiftm), .outputBackShiftM(log_1x1_3_outputbackshiftm),
    .inPlayerShiftD(log_1x1_2_outplayershiftd), .outPlayerShiftD(log_1x1_3_outplayershiftd),
    .inPlayerShiftM(log_1x1_2_outplayershiftm), .outPlayerShiftM(log_1x1_3_outplayershiftm),
    .inFlag(log_1x1_2_outflag), .outFlag(log_1x1_3_outflag), .toBackground(log_1x1_3_tobackground),
    .toBackground_2(log_1x1_3_tobackground_2), .toBackground_3(log_1x1_3_tobackground_3),
    .toBackground_4(log_1x1_3_tobackground_4), .toBackground_5(log_1x1_3_tobackground_5),
    .toBackground_6(log_1x1_3_tobackground_6), .toBackground_7(log_1x1_3_tobackground_7),
    .toBackground_8(log_1x1_3_tobackground_8), .toBackground_9(log_1x1_3_tobackground_9),
    .toBackground_10(log_1x1_3_tobackground_10), .toFront(log_1x1_3_tofront),
    .toFront_2(log_1x1_3_tofront_2), .toFront_3(log_1x1_3_tofront_3), .toFront_4(log_1x1_3_tofront_4),
    .toFront_5(log_1x1_3_tofront_5), .toFront_6(log_1x1_3_tofront_6), .toFront_7(log_1x1_3_tofront_7),
    .toFront_8(log_1x1_3_tofront_8), .toFront_9(log_1x1_3_tofront_9), .toFront_10(log_1x1_3_tofront_10));
  DotMatrix #(.inputtype("row"), .matrixcols(30), .matrixrows(10)) dotmatrix_66 (
    .row0(log_1x1_3_tobackground), .row1(log_1x1_3_tobackground_2), .row2(log_1x1_3_tobackground_3),
    .row3(log_1x1_3_tobackground_4), .row4(log_1x1_3_tobackground_5), .row5(log_1x1_3_tobackground_6),
    .row6(log_1x1_3_tobackground_7), .row7(log_1x1_3_tobackground_8), .row8(log_1x1_3_tobackground_9),
    .row9(log_1x1_3_tobackground_10));
  DotMatrix #(.inputtype("row"), .matrixcols(30), .matrixrows(10)) dotmatrix_67 (
    .row0(swamp_5_tobackground), .row1(swamp_5_tobackground_2), .row2(swamp_5_tobackground_3),
    .row3(swamp_5_tobackground_4), .row4(swamp_5_tobackground_5), .row5(swamp_5_tobackground_6),
    .row6(swamp_5_tobackground_7), .row7(swamp_5_tobackground_8), .row8(swamp_5_tobackground_9),
    .row9(swamp_5_tobackground_10));
  DotMatrix #(.inputtype("row"), .matrixcols(30), .matrixrows(10)) dotmatrix_68 (
    .row0(swamp_5_tofront), .row1(swamp_5_tofront_2), .row2(swamp_5_tofront_3), .row3(swamp_5_tofront_4),
    .row4(swamp_5_tofront_5), .row5(swamp_5_tofront_6), .row6(swamp_5_tofront_7), .row7(swamp_5_tofront_8),
    .row8(swamp_5_tofront_9), .row9(swamp_5_tofront_10));
  swamp swamp_5 (
    .inPlayerShiftD(swamp_3_outplayershiftd), .outPlayerShiftD(swamp_5_outplayershiftd),
    .inPlayerShiftM(swamp_3_outplayershiftm), .outPlayerShiftM(swamp_5_outplayershiftm),
    .inFlag(swamp_3_outflag), .outFlag(swamp_5_outflag), .toBackground(swamp_5_tobackground),
    .toFront(swamp_5_tofront), .toBackground_2(swamp_5_tobackground_2), .toFront_2(swamp_5_tofront_2),
    .toBackground_3(swamp_5_tobackground_3), .toFront_3(swamp_5_tofront_3),
    .toBackground_4(swamp_5_tobackground_4), .toFront_4(swamp_5_tofront_4),
    .toBackground_5(swamp_5_tobackground_5), .toFront_5(swamp_5_tofront_5),
    .toBackground_6(swamp_5_tobackground_6), .toFront_6(swamp_5_tofront_6),
    .toBackground_7(swamp_5_tobackground_7), .toFront_7(swamp_5_tofront_7),
    .toBackground_8(swamp_5_tobackground_8), .toFront_8(swamp_5_tofront_8),
    .toBackground_9(swamp_5_tobackground_9), .toFront_9(swamp_5_tofront_9),
    .toBackground_10(swamp_5_tobackground_10), .toFront_10(swamp_5_tofront_10));
  carConnectorV2 carconnectorv2_11 (
    .inBackShiftD(carconnectorv2_6_outbackshiftd), .outBackShiftD(carconnectorv2_11_outbackshiftd),
    .inputBackShiftM(carconnectorv2_6_outputbackshiftm),
    .outputBackShiftM(carconnectorv2_11_outputbackshiftm),
    .outPlayerShiftD(carconnectorv2_11_outplayershiftd), .inPlayerShiftM(carconnectorv2_6_outplayershiftm),
    .outPlayerShiftM(carconnectorv2_11_outplayershiftm), .inFlag(carconnectorv2_6_outflag),
    .outFlag(carconnectorv2_11_outflag), .toBackground(carconnectorv2_11_tobackground),
    .toBackground_2(carconnectorv2_11_tobackground_2), .toBackground_3(carconnectorv2_11_tobackground_3),
    .toBackground_4(carconnectorv2_11_tobackground_4), .toBackground_5(carconnectorv2_11_tobackground_5),
    .toBackground_6(carconnectorv2_11_tobackground_6), .toBackground_7(carconnectorv2_11_tobackground_7),
    .toBackground_8(carconnectorv2_11_tobackground_8), .toBackground_9(carconnectorv2_11_tobackground_9),
    .toBackground_10(carconnectorv2_11_tobackground_10), .toFront(carconnectorv2_11_tofront),
    .toFront_2(carconnectorv2_11_tofront_2), .toFront_3(carconnectorv2_11_tofront_3),
    .toFront_4(carconnectorv2_11_tofront_4), .toFront_5(carconnectorv2_11_tofront_5),
    .toFront_6(carconnectorv2_11_tofront_6), .toFront_7(carconnectorv2_11_tofront_7),
    .toFront_8(carconnectorv2_11_tofront_8), .toFront_9(carconnectorv2_11_tofront_9),
    .toFront_10(carconnectorv2_11_tofront_10), .inPlayerShiftD(carconnectorv2_6_outplayershiftd));
  DotMatrix #(.inputtype("row"), .matrixcols(30), .matrixrows(2)) dotmatrix_69 (
    .row0(carconnectorv2_11_tobackground), .row1(carconnectorv2_11_tobackground_2));
  DotMatrix #(.inputtype("row"), .matrixcols(30), .matrixrows(10)) dotmatrix_70 (
    .row0(carconnectorv2_11_tofront), .row1(carconnectorv2_11_tofront_2), .row2(carconnectorv2_11_tofront_3),
    .row3(carconnectorv2_11_tofront_4), .row4(carconnectorv2_11_tofront_5),
    .row5(carconnectorv2_11_tofront_6), .row6(carconnectorv2_11_tofront_7),
    .row7(carconnectorv2_11_tofront_8), .row8(carconnectorv2_11_tofront_9),
    .row9(carconnectorv2_11_tofront_10));
  DotMatrix #(.inputtype("row"), .matrixcols(30), .matrixrows(6)) dotmatrix_71 (
    .row0(carconnectorv2_11_tobackground_3), .row1(carconnectorv2_11_tobackground_4),
    .row2(carconnectorv2_11_tobackground_5), .row3(carconnectorv2_11_tobackground_6),
    .row4(carconnectorv2_11_tobackground_7), .row5(carconnectorv2_11_tobackground_8));
  DotMatrix #(.inputtype("row"), .matrixcols(30), .matrixrows(2)) dotmatrix_72 (
    .row0(carconnectorv2_11_tobackground_9), .row1(carconnectorv2_11_tobackground_10));
  carConnectorV2 carconnectorv2_12 (
    .inBackShiftD(carconnectorv2_7_outbackshiftd), .outBackShiftD(carconnectorv2_12_outbackshiftd),
    .inputBackShiftM(carconnectorv2_7_outputbackshiftm),
    .outputBackShiftM(carconnectorv2_12_outputbackshiftm),
    .outPlayerShiftD(carconnectorv2_12_outplayershiftd), .inPlayerShiftM(carconnectorv2_7_outplayershiftm),
    .outPlayerShiftM(carconnectorv2_12_outplayershiftm), .inFlag(carconnectorv2_7_outflag),
    .outFlag(carconnectorv2_12_outflag), .toBackground(carconnectorv2_12_tobackground),
    .toBackground_2(carconnectorv2_12_tobackground_2), .toBackground_3(carconnectorv2_12_tobackground_3),
    .toBackground_4(carconnectorv2_12_tobackground_4), .toBackground_5(carconnectorv2_12_tobackground_5),
    .toBackground_6(carconnectorv2_12_tobackground_6), .toBackground_7(carconnectorv2_12_tobackground_7),
    .toBackground_8(carconnectorv2_12_tobackground_8), .toBackground_9(carconnectorv2_12_tobackground_9),
    .toBackground_10(carconnectorv2_12_tobackground_10), .toFront(carconnectorv2_12_tofront),
    .toFront_2(carconnectorv2_12_tofront_2), .toFront_3(carconnectorv2_12_tofront_3),
    .toFront_4(carconnectorv2_12_tofront_4), .toFront_5(carconnectorv2_12_tofront_5),
    .toFront_6(carconnectorv2_12_tofront_6), .toFront_7(carconnectorv2_12_tofront_7),
    .toFront_8(carconnectorv2_12_tofront_8), .toFront_9(carconnectorv2_12_tofront_9),
    .toFront_10(carconnectorv2_12_tofront_10), .inPlayerShiftD(carconnectorv2_7_outplayershiftd));
  DotMatrix #(.inputtype("row"), .matrixcols(30), .matrixrows(2)) dotmatrix_73 (
    .row0(carconnectorv2_12_tobackground), .row1(carconnectorv2_12_tobackground_2));
  DotMatrix #(.inputtype("row"), .matrixcols(30), .matrixrows(10)) dotmatrix_74 (
    .row0(carconnectorv2_12_tofront), .row1(carconnectorv2_12_tofront_2), .row2(carconnectorv2_12_tofront_3),
    .row3(carconnectorv2_12_tofront_4), .row4(carconnectorv2_12_tofront_5),
    .row5(carconnectorv2_12_tofront_6), .row6(carconnectorv2_12_tofront_7),
    .row7(carconnectorv2_12_tofront_8), .row8(carconnectorv2_12_tofront_9),
    .row9(carconnectorv2_12_tofront_10));
  DotMatrix #(.inputtype("row"), .matrixcols(30), .matrixrows(6)) dotmatrix_75 (
    .row0(carconnectorv2_12_tobackground_3), .row1(carconnectorv2_12_tobackground_4),
    .row2(carconnectorv2_12_tobackground_5), .row3(carconnectorv2_12_tobackground_6),
    .row4(carconnectorv2_12_tobackground_7), .row5(carconnectorv2_12_tobackground_8));
  DotMatrix #(.inputtype("row"), .matrixcols(30), .matrixrows(2)) dotmatrix_76 (
    .row0(carconnectorv2_12_tobackground_9), .row1(carconnectorv2_12_tobackground_10));
  DotMatrix #(.inputtype("row"), .matrixcols(30), .matrixrows(10)) dotmatrix_77 (
    .row0(carconnectorv2_13_tofront), .row1(carconnectorv2_13_tofront_2), .row2(carconnectorv2_13_tofront_3),
    .row3(carconnectorv2_13_tofront_4), .row4(carconnectorv2_13_tofront_5),
    .row5(carconnectorv2_13_tofront_6), .row6(carconnectorv2_13_tofront_7),
    .row7(carconnectorv2_13_tofront_8), .row8(carconnectorv2_13_tofront_9),
    .row9(carconnectorv2_13_tofront_10));
  DotMatrix #(.inputtype("row"), .matrixcols(30), .matrixrows(2)) dotmatrix_78 (
    .row0(carconnectorv2_13_tobackground), .row1(carconnectorv2_13_tobackground_2));
  carConnectorV2 carconnectorv2_13 (
    .inBackShiftD(carconnectorv2_8_outbackshiftd), .outBackShiftD(carconnectorv2_13_outbackshiftd),
    .inputBackShiftM(carconnectorv2_8_outputbackshiftm),
    .outputBackShiftM(carconnectorv2_13_outputbackshiftm),
    .outPlayerShiftD(carconnectorv2_13_outplayershiftd), .inPlayerShiftM(carconnectorv2_8_outplayershiftm),
    .outPlayerShiftM(carconnectorv2_13_outplayershiftm), .inFlag(carconnectorv2_8_outflag),
    .outFlag(carconnectorv2_13_outflag), .toBackground(carconnectorv2_13_tobackground),
    .toBackground_2(carconnectorv2_13_tobackground_2), .toBackground_3(carconnectorv2_13_tobackground_3),
    .toBackground_4(carconnectorv2_13_tobackground_4), .toBackground_5(carconnectorv2_13_tobackground_5),
    .toBackground_6(carconnectorv2_13_tobackground_6), .toBackground_7(carconnectorv2_13_tobackground_7),
    .toBackground_8(carconnectorv2_13_tobackground_8), .toBackground_9(carconnectorv2_13_tobackground_9),
    .toBackground_10(carconnectorv2_13_tobackground_10), .toFront(carconnectorv2_13_tofront),
    .toFront_2(carconnectorv2_13_tofront_2), .toFront_3(carconnectorv2_13_tofront_3),
    .toFront_4(carconnectorv2_13_tofront_4), .toFront_5(carconnectorv2_13_tofront_5),
    .toFront_6(carconnectorv2_13_tofront_6), .toFront_7(carconnectorv2_13_tofront_7),
    .toFront_8(carconnectorv2_13_tofront_8), .toFront_9(carconnectorv2_13_tofront_9),
    .toFront_10(carconnectorv2_13_tofront_10), .inPlayerShiftD(carconnectorv2_8_outplayershiftd));
  DotMatrix #(.inputtype("row"), .matrixcols(30), .matrixrows(6)) dotmatrix_79 (
    .row0(carconnectorv2_13_tobackground_3), .row1(carconnectorv2_13_tobackground_4),
    .row2(carconnectorv2_13_tobackground_5), .row3(carconnectorv2_13_tobackground_6),
    .row4(carconnectorv2_13_tobackground_7), .row5(carconnectorv2_13_tobackground_8));
  DotMatrix #(.inputtype("row"), .matrixcols(30), .matrixrows(2)) dotmatrix_80 (
    .row0(carconnectorv2_13_tobackground_9), .row1(carconnectorv2_13_tobackground_10));
  DotMatrix #(.inputtype("row"), .matrixcols(30), .matrixrows(10)) dotmatrix_81 (
    .row0(carconnectorv2_14_tofront), .row1(carconnectorv2_14_tofront_2), .row2(carconnectorv2_14_tofront_3),
    .row3(carconnectorv2_14_tofront_4), .row4(carconnectorv2_14_tofront_5),
    .row5(carconnectorv2_14_tofront_6), .row6(carconnectorv2_14_tofront_7),
    .row7(carconnectorv2_14_tofront_8), .row8(carconnectorv2_14_tofront_9),
    .row9(carconnectorv2_14_tofront_10));
  DotMatrix #(.inputtype("row"), .matrixcols(30), .matrixrows(2)) dotmatrix_82 (
    .row0(carconnectorv2_14_tobackground), .row1(carconnectorv2_14_tobackground_2));
  carConnectorV2 carconnectorv2_14 (
    .inBackShiftD(carconnectorv2_9_outbackshiftd), .outBackShiftD(carconnectorv2_14_outbackshiftd),
    .inputBackShiftM(carconnectorv2_9_outputbackshiftm),
    .outputBackShiftM(carconnectorv2_14_outputbackshiftm),
    .outPlayerShiftD(carconnectorv2_14_outplayershiftd), .inPlayerShiftM(carconnectorv2_9_outplayershiftm),
    .outPlayerShiftM(carconnectorv2_14_outplayershiftm), .inFlag(carconnectorv2_9_outflag),
    .outFlag(carconnectorv2_14_outflag), .toBackground(carconnectorv2_14_tobackground),
    .toBackground_2(carconnectorv2_14_tobackground_2), .toBackground_3(carconnectorv2_14_tobackground_3),
    .toBackground_4(carconnectorv2_14_tobackground_4), .toBackground_5(carconnectorv2_14_tobackground_5),
    .toBackground_6(carconnectorv2_14_tobackground_6), .toBackground_7(carconnectorv2_14_tobackground_7),
    .toBackground_8(carconnectorv2_14_tobackground_8), .toBackground_9(carconnectorv2_14_tobackground_9),
    .toBackground_10(carconnectorv2_14_tobackground_10), .toFront(carconnectorv2_14_tofront),
    .toFront_2(carconnectorv2_14_tofront_2), .toFront_3(carconnectorv2_14_tofront_3),
    .toFront_4(carconnectorv2_14_tofront_4), .toFront_5(carconnectorv2_14_tofront_5),
    .toFront_6(carconnectorv2_14_tofront_6), .toFront_7(carconnectorv2_14_tofront_7),
    .toFront_8(carconnectorv2_14_tofront_8), .toFront_9(carconnectorv2_14_tofront_9),
    .toFront_10(carconnectorv2_14_tofront_10), .inPlayerShiftD(carconnectorv2_9_outplayershiftd));
  DotMatrix #(.inputtype("row"), .matrixcols(30), .matrixrows(6)) dotmatrix_83 (
    .row0(carconnectorv2_14_tobackground_3), .row1(carconnectorv2_14_tobackground_4),
    .row2(carconnectorv2_14_tobackground_5), .row3(carconnectorv2_14_tobackground_6),
    .row4(carconnectorv2_14_tobackground_7), .row5(carconnectorv2_14_tobackground_8));
  DotMatrix #(.inputtype("row"), .matrixcols(30), .matrixrows(2)) dotmatrix_84 (
    .row0(carconnectorv2_14_tobackground_9), .row1(carconnectorv2_14_tobackground_10));
  DotMatrix #(.inputtype("row"), .matrixcols(30), .matrixrows(10)) dotmatrix_85 (
    .row0(carconnectorv2_15_tofront), .row1(carconnectorv2_15_tofront_2), .row2(carconnectorv2_15_tofront_3),
    .row3(carconnectorv2_15_tofront_4), .row4(carconnectorv2_15_tofront_5),
    .row5(carconnectorv2_15_tofront_6), .row6(carconnectorv2_15_tofront_7),
    .row7(carconnectorv2_15_tofront_8), .row8(carconnectorv2_15_tofront_9),
    .row9(carconnectorv2_15_tofront_10));
  carConnectorV2 carconnectorv2_15 (
    .inBackShiftD(carconnectorv2_10_outbackshiftd), .outBackShiftD(carconnectorv2_15_outbackshiftd),
    .inputBackShiftM(carconnectorv2_10_outputbackshiftm),
    .outputBackShiftM(carconnectorv2_15_outputbackshiftm),
    .outPlayerShiftD(carconnectorv2_15_outplayershiftd), .inPlayerShiftM(carconnectorv2_10_outplayershiftm),
    .outPlayerShiftM(carconnectorv2_15_outplayershiftm), .inFlag(carconnectorv2_10_outflag),
    .outFlag(carconnectorv2_15_outflag), .toBackground(carconnectorv2_15_tobackground),
    .toBackground_2(carconnectorv2_15_tobackground_2), .toBackground_3(carconnectorv2_15_tobackground_3),
    .toBackground_4(carconnectorv2_15_tobackground_4), .toBackground_5(carconnectorv2_15_tobackground_5),
    .toBackground_6(carconnectorv2_15_tobackground_6), .toBackground_7(carconnectorv2_15_tobackground_7),
    .toBackground_8(carconnectorv2_15_tobackground_8), .toBackground_9(carconnectorv2_15_tobackground_9),
    .toBackground_10(carconnectorv2_15_tobackground_10), .toFront(carconnectorv2_15_tofront),
    .toFront_2(carconnectorv2_15_tofront_2), .toFront_3(carconnectorv2_15_tofront_3),
    .toFront_4(carconnectorv2_15_tofront_4), .toFront_5(carconnectorv2_15_tofront_5),
    .toFront_6(carconnectorv2_15_tofront_6), .toFront_7(carconnectorv2_15_tofront_7),
    .toFront_8(carconnectorv2_15_tofront_8), .toFront_9(carconnectorv2_15_tofront_9),
    .toFront_10(carconnectorv2_15_tofront_10), .inPlayerShiftD(carconnectorv2_10_outplayershiftd));
  DotMatrix #(.inputtype("row"), .matrixcols(30), .matrixrows(2)) dotmatrix_86 (
    .row0(carconnectorv2_15_tobackground), .row1(carconnectorv2_15_tobackground_2));
  DotMatrix #(.inputtype("row"), .matrixcols(30), .matrixrows(6)) dotmatrix_87 (
    .row0(carconnectorv2_15_tobackground_3), .row1(carconnectorv2_15_tobackground_4),
    .row2(carconnectorv2_15_tobackground_5), .row3(carconnectorv2_15_tobackground_6),
    .row4(carconnectorv2_15_tobackground_7), .row5(carconnectorv2_15_tobackground_8));
  DotMatrix #(.inputtype("row"), .matrixcols(30), .matrixrows(2)) dotmatrix_88 (
    .row0(carconnectorv2_15_tobackground_9), .row1(carconnectorv2_15_tobackground_10));
  swamp swamp_6 (
    .inPlayerShiftD(swamp_4_outplayershiftd), .outPlayerShiftD(swamp_6_outplayershiftd),
    .inPlayerShiftM(swamp_4_outplayershiftm), .outPlayerShiftM(swamp_6_outplayershiftm),
    .inFlag(swamp_4_outflag), .outFlag(swamp_6_outflag), .toBackground(swamp_6_tobackground),
    .toFront(swamp_6_tofront), .toBackground_2(swamp_6_tobackground_2), .toFront_2(swamp_6_tofront_2),
    .toBackground_3(swamp_6_tobackground_3), .toFront_3(swamp_6_tofront_3),
    .toBackground_4(swamp_6_tobackground_4), .toFront_4(swamp_6_tofront_4),
    .toBackground_5(swamp_6_tobackground_5), .toFront_5(swamp_6_tofront_5),
    .toBackground_6(swamp_6_tobackground_6), .toFront_6(swamp_6_tofront_6),
    .toBackground_7(swamp_6_tobackground_7), .toFront_7(swamp_6_tofront_7),
    .toBackground_8(swamp_6_tobackground_8), .toFront_8(swamp_6_tofront_8),
    .toBackground_9(swamp_6_tobackground_9), .toFront_9(swamp_6_tofront_9),
    .toBackground_10(swamp_6_tobackground_10), .toFront_10(swamp_6_tofront_10));
  DotMatrix #(.inputtype("row"), .matrixcols(30), .matrixrows(10)) dotmatrix_89 (
    .row0(swamp_6_tobackground), .row1(swamp_6_tobackground_2), .row2(swamp_6_tobackground_3),
    .row3(swamp_6_tobackground_4), .row4(swamp_6_tobackground_5), .row5(swamp_6_tobackground_6),
    .row6(swamp_6_tobackground_7), .row7(swamp_6_tobackground_8), .row8(swamp_6_tobackground_9),
    .row9(swamp_6_tobackground_10));
  DotMatrix #(.inputtype("row"), .matrixcols(30), .matrixrows(10)) dotmatrix_90 (
    .row0(swamp_6_tofront), .row1(swamp_6_tofront_2), .row2(swamp_6_tofront_3), .row3(swamp_6_tofront_4),
    .row4(swamp_6_tofront_5), .row5(swamp_6_tofront_6), .row6(swamp_6_tofront_7), .row7(swamp_6_tofront_8),
    .row8(swamp_6_tofront_9), .row9(swamp_6_tofront_10));
  DotMatrix #(.inputtype("row"), .matrixcols(30), .matrixrows(10)) dotmatrix_91 (
    .row0(log_2x1_5_tobackground), .row1(log_2x1_5_tobackground_2), .row2(log_2x1_5_tobackground_3),
    .row3(log_2x1_5_tobackground_4), .row4(log_2x1_5_tobackground_5), .row5(log_2x1_5_tobackground_6),
    .row6(log_2x1_5_tobackground_7), .row7(log_2x1_5_tobackground_8), .row8(log_2x1_5_tobackground_9),
    .row9(log_2x1_5_tobackground_10));
  log_2x1 log_2x1_5 (
    .inBackShiftD(log_2x1_4_outbackshiftd), .inputBackShiftM(log_2x1_4_outputbackshiftm),
    .inPlayerShiftD(log_2x1_4_outplayershiftd), .inPlayerShiftM(log_2x1_4_outplayershiftm),
    .inFlag(log_2x1_4_outflag), .toBackground(log_2x1_5_tobackground),
    .toBackground_2(log_2x1_5_tobackground_2), .toBackground_3(log_2x1_5_tobackground_3),
    .toBackground_4(log_2x1_5_tobackground_4), .toBackground_5(log_2x1_5_tobackground_5),
    .toBackground_6(log_2x1_5_tobackground_6), .toBackground_7(log_2x1_5_tobackground_7),
    .toBackground_8(log_2x1_5_tobackground_8), .toBackground_9(log_2x1_5_tobackground_9),
    .toBackground_10(log_2x1_5_tobackground_10));  // open: outBackShiftD, outputBackShiftM, outPlayerShiftD, outPlayerShiftM, outFlag, toFront, toFront_2, toFront_3, toFront_4, toFront_5, toFront_6, toFront_7, toFront_8, toFront_9, toFront_10
  DotMatrix #(.inputtype("row"), .matrixcols(30), .matrixrows(10)) dotmatrix_92 (
    .row0(log_3x2_5_tofront), .row1(log_3x2_5_tofront_2), .row2(log_3x2_5_tofront_3),
    .row3(log_3x2_5_tofront_4), .row4(log_3x2_5_tofront_5), .row5(log_3x2_5_tofront_6),
    .row6(log_3x2_5_tofront_7), .row7(log_3x2_5_tofront_8), .row8(log_3x2_5_tofront_9),
    .row9(log_3x2_5_tofront_10));
  log_3x2 log_3x2_5 (
    .inBackShiftD(log_3x2_4_outbackshiftd), .inputBackShiftM(log_3x2_4_outputbackshiftm),
    .inPlayerShiftD(log_3x2_4_outplayershiftd), .inPlayerShiftM(log_3x2_4_outplayershiftm),
    .inFlag(log_3x2_4_outflag), .toBackground(log_3x2_5_tobackground),
    .toBackground_2(log_3x2_5_tobackground_2), .toBackground_3(log_3x2_5_tobackground_3),
    .toBackground_4(log_3x2_5_tobackground_4), .toBackground_5(log_3x2_5_tobackground_5),
    .toBackground_6(log_3x2_5_tobackground_6), .toBackground_7(log_3x2_5_tobackground_7),
    .toBackground_8(log_3x2_5_tobackground_8), .toBackground_9(log_3x2_5_tobackground_9),
    .toBackground_10(log_3x2_5_tobackground_10), .toFront(log_3x2_5_tofront),
    .toFront_2(log_3x2_5_tofront_2), .toFront_3(log_3x2_5_tofront_3), .toFront_4(log_3x2_5_tofront_4),
    .toFront_5(log_3x2_5_tofront_5), .toFront_6(log_3x2_5_tofront_6), .toFront_7(log_3x2_5_tofront_7),
    .toFront_8(log_3x2_5_tofront_8), .toFront_9(log_3x2_5_tofront_9), .toFront_10(log_3x2_5_tofront_10));  // open: outBackShiftD, outputBackShiftM, outPlayerShiftD, outPlayerShiftM, outFlag
  DotMatrix #(.inputtype("row"), .matrixcols(30), .matrixrows(10)) dotmatrix_93 (
    .row0(log_3x2_5_tobackground), .row1(log_3x2_5_tobackground_2), .row2(log_3x2_5_tobackground_3),
    .row3(log_3x2_5_tobackground_4), .row4(log_3x2_5_tobackground_5), .row5(log_3x2_5_tobackground_6),
    .row6(log_3x2_5_tobackground_7), .row7(log_3x2_5_tobackground_8), .row8(log_3x2_5_tobackground_9),
    .row9(log_3x2_5_tobackground_10));
  DotMatrix #(.inputtype("row"), .matrixcols(30), .matrixrows(10)) dotmatrix_94 (
    .row0(log_1x1_4_tobackground), .row1(log_1x1_4_tobackground_2), .row2(log_1x1_4_tobackground_3),
    .row3(log_1x1_4_tobackground_4), .row4(log_1x1_4_tobackground_5), .row5(log_1x1_4_tobackground_6),
    .row6(log_1x1_4_tobackground_7), .row7(log_1x1_4_tobackground_8), .row8(log_1x1_4_tobackground_9),
    .row9(log_1x1_4_tobackground_10));
  log_1x1 log_1x1_4 (
    .inBackShiftD(log_1x1_3_outbackshiftd), .inputBackShiftM(log_1x1_3_outputbackshiftm),
    .inPlayerShiftD(log_1x1_3_outplayershiftd), .inPlayerShiftM(log_1x1_3_outplayershiftm),
    .inFlag(log_1x1_3_outflag), .toBackground(log_1x1_4_tobackground),
    .toBackground_2(log_1x1_4_tobackground_2), .toBackground_3(log_1x1_4_tobackground_3),
    .toBackground_4(log_1x1_4_tobackground_4), .toBackground_5(log_1x1_4_tobackground_5),
    .toBackground_6(log_1x1_4_tobackground_6), .toBackground_7(log_1x1_4_tobackground_7),
    .toBackground_8(log_1x1_4_tobackground_8), .toBackground_9(log_1x1_4_tobackground_9),
    .toBackground_10(log_1x1_4_tobackground_10), .toFront(log_1x1_4_tofront),
    .toFront_2(log_1x1_4_tofront_2), .toFront_3(log_1x1_4_tofront_3), .toFront_4(log_1x1_4_tofront_4),
    .toFront_5(log_1x1_4_tofront_5), .toFront_6(log_1x1_4_tofront_6), .toFront_7(log_1x1_4_tofront_7),
    .toFront_8(log_1x1_4_tofront_8), .toFront_9(log_1x1_4_tofront_9), .toFront_10(log_1x1_4_tofront_10));  // open: outBackShiftD, outputBackShiftM, outPlayerShiftD, outPlayerShiftM, outFlag
  DotMatrix #(.inputtype("row"), .matrixcols(30), .matrixrows(10)) dotmatrix_95 (
    .row0(log_1x1_4_tofront), .row1(log_1x1_4_tofront_2), .row2(log_1x1_4_tofront_3),
    .row3(log_1x1_4_tofront_4), .row4(log_1x1_4_tofront_5), .row5(log_1x1_4_tofront_6),
    .row6(log_1x1_4_tofront_7), .row7(log_1x1_4_tofront_8), .row8(log_1x1_4_tofront_9),
    .row9(log_1x1_4_tofront_10));
  swamp swamp_7 (
    .inPlayerShiftD(swamp_5_outplayershiftd), .inPlayerShiftM(swamp_5_outplayershiftm),
    .inFlag(swamp_5_outflag), .toBackground(swamp_7_tobackground), .toFront(swamp_7_tofront),
    .toBackground_2(swamp_7_tobackground_2), .toFront_2(swamp_7_tofront_2),
    .toBackground_3(swamp_7_tobackground_3), .toFront_3(swamp_7_tofront_3),
    .toBackground_4(swamp_7_tobackground_4), .toFront_4(swamp_7_tofront_4),
    .toBackground_5(swamp_7_tobackground_5), .toFront_5(swamp_7_tofront_5),
    .toBackground_6(swamp_7_tobackground_6), .toFront_6(swamp_7_tofront_6),
    .toBackground_7(swamp_7_tobackground_7), .toFront_7(swamp_7_tofront_7),
    .toBackground_8(swamp_7_tobackground_8), .toFront_8(swamp_7_tofront_8),
    .toBackground_9(swamp_7_tobackground_9), .toFront_9(swamp_7_tofront_9),
    .toBackground_10(swamp_7_tobackground_10), .toFront_10(swamp_7_tofront_10));  // open: outPlayerShiftD, outPlayerShiftM, outFlag
  DotMatrix #(.inputtype("row"), .matrixcols(30), .matrixrows(10)) dotmatrix_96 (
    .row0(swamp_7_tobackground), .row1(swamp_7_tobackground_2), .row2(swamp_7_tobackground_3),
    .row3(swamp_7_tobackground_4), .row4(swamp_7_tobackground_5), .row5(swamp_7_tobackground_6),
    .row6(swamp_7_tobackground_7), .row7(swamp_7_tobackground_8), .row8(swamp_7_tobackground_9),
    .row9(swamp_7_tobackground_10));
  DotMatrix #(.inputtype("row"), .matrixcols(30), .matrixrows(10)) dotmatrix_97 (
    .row0(swamp_7_tofront), .row1(swamp_7_tofront_2), .row2(swamp_7_tofront_3), .row3(swamp_7_tofront_4),
    .row4(swamp_7_tofront_5), .row5(swamp_7_tofront_6), .row6(swamp_7_tofront_7), .row7(swamp_7_tofront_8),
    .row8(swamp_7_tofront_9), .row9(swamp_7_tofront_10));
  carConnectorV2 carconnectorv2_16 (
    .inBackShiftD(carconnectorv2_11_outbackshiftd), .inputBackShiftM(carconnectorv2_11_outputbackshiftm),
    .inPlayerShiftM(carconnectorv2_11_outplayershiftm), .inFlag(carconnectorv2_11_outflag),
    .toBackground(carconnectorv2_16_tobackground), .toBackground_2(carconnectorv2_16_tobackground_2),
    .toBackground_3(carconnectorv2_16_tobackground_3), .toBackground_4(carconnectorv2_16_tobackground_4),
    .toBackground_5(carconnectorv2_16_tobackground_5), .toBackground_6(carconnectorv2_16_tobackground_6),
    .toBackground_7(carconnectorv2_16_tobackground_7), .toBackground_8(carconnectorv2_16_tobackground_8),
    .toBackground_9(carconnectorv2_16_tobackground_9), .toBackground_10(carconnectorv2_16_tobackground_10),
    .toFront(carconnectorv2_16_tofront), .toFront_2(carconnectorv2_16_tofront_2),
    .toFront_3(carconnectorv2_16_tofront_3), .toFront_4(carconnectorv2_16_tofront_4),
    .toFront_5(carconnectorv2_16_tofront_5), .toFront_6(carconnectorv2_16_tofront_6),
    .toFront_7(carconnectorv2_16_tofront_7), .toFront_8(carconnectorv2_16_tofront_8),
    .toFront_9(carconnectorv2_16_tofront_9), .toFront_10(carconnectorv2_16_tofront_10),
    .inPlayerShiftD(carconnectorv2_11_outplayershiftd));  // open: outBackShiftD, outputBackShiftM, outPlayerShiftD, outPlayerShiftM, outFlag
  DotMatrix #(.inputtype("row"), .matrixcols(30), .matrixrows(10)) dotmatrix_98 (
    .row0(carconnectorv2_16_tofront), .row1(carconnectorv2_16_tofront_2), .row2(carconnectorv2_16_tofront_3),
    .row3(carconnectorv2_16_tofront_4), .row4(carconnectorv2_16_tofront_5),
    .row5(carconnectorv2_16_tofront_6), .row6(carconnectorv2_16_tofront_7),
    .row7(carconnectorv2_16_tofront_8), .row8(carconnectorv2_16_tofront_9),
    .row9(carconnectorv2_16_tofront_10));
  DotMatrix #(.inputtype("row"), .matrixcols(30), .matrixrows(2)) dotmatrix_99 (
    .row0(carconnectorv2_16_tobackground), .row1(carconnectorv2_16_tobackground_2));
  DotMatrix #(.inputtype("row"), .matrixcols(30), .matrixrows(6)) dotmatrix_100 (
    .row0(carconnectorv2_16_tobackground_3), .row1(carconnectorv2_16_tobackground_4),
    .row2(carconnectorv2_16_tobackground_5), .row3(carconnectorv2_16_tobackground_6),
    .row4(carconnectorv2_16_tobackground_7), .row5(carconnectorv2_16_tobackground_8));
  DotMatrix #(.inputtype("row"), .matrixcols(30), .matrixrows(2)) dotmatrix_101 (
    .row0(carconnectorv2_16_tobackground_9), .row1(carconnectorv2_16_tobackground_10));
  DotMatrix #(.inputtype("row"), .matrixcols(30), .matrixrows(2)) dotmatrix_102 (
    .row0(carconnectorv2_17_tobackground), .row1(carconnectorv2_17_tobackground_2));
  DotMatrix #(.inputtype("row"), .matrixcols(30), .matrixrows(10)) dotmatrix_103 (
    .row0(carconnectorv2_17_tofront), .row1(carconnectorv2_17_tofront_2), .row2(carconnectorv2_17_tofront_3),
    .row3(carconnectorv2_17_tofront_4), .row4(carconnectorv2_17_tofront_5),
    .row5(carconnectorv2_17_tofront_6), .row6(carconnectorv2_17_tofront_7),
    .row7(carconnectorv2_17_tofront_8), .row8(carconnectorv2_17_tofront_9),
    .row9(carconnectorv2_17_tofront_10));
  carConnectorV2 carconnectorv2_17 (
    .inBackShiftD(carconnectorv2_12_outbackshiftd), .inputBackShiftM(carconnectorv2_12_outputbackshiftm),
    .inPlayerShiftM(carconnectorv2_12_outplayershiftm), .inFlag(carconnectorv2_12_outflag),
    .toBackground(carconnectorv2_17_tobackground), .toBackground_2(carconnectorv2_17_tobackground_2),
    .toBackground_3(carconnectorv2_17_tobackground_3), .toBackground_4(carconnectorv2_17_tobackground_4),
    .toBackground_5(carconnectorv2_17_tobackground_5), .toBackground_6(carconnectorv2_17_tobackground_6),
    .toBackground_7(carconnectorv2_17_tobackground_7), .toBackground_8(carconnectorv2_17_tobackground_8),
    .toBackground_9(carconnectorv2_17_tobackground_9), .toBackground_10(carconnectorv2_17_tobackground_10),
    .toFront(carconnectorv2_17_tofront), .toFront_2(carconnectorv2_17_tofront_2),
    .toFront_3(carconnectorv2_17_tofront_3), .toFront_4(carconnectorv2_17_tofront_4),
    .toFront_5(carconnectorv2_17_tofront_5), .toFront_6(carconnectorv2_17_tofront_6),
    .toFront_7(carconnectorv2_17_tofront_7), .toFront_8(carconnectorv2_17_tofront_8),
    .toFront_9(carconnectorv2_17_tofront_9), .toFront_10(carconnectorv2_17_tofront_10),
    .inPlayerShiftD(carconnectorv2_12_outplayershiftd));  // open: outBackShiftD, outputBackShiftM, outPlayerShiftD, outPlayerShiftM, outFlag
  DotMatrix #(.inputtype("row"), .matrixcols(30), .matrixrows(6)) dotmatrix_104 (
    .row0(carconnectorv2_17_tobackground_3), .row1(carconnectorv2_17_tobackground_4),
    .row2(carconnectorv2_17_tobackground_5), .row3(carconnectorv2_17_tobackground_6),
    .row4(carconnectorv2_17_tobackground_7), .row5(carconnectorv2_17_tobackground_8));
  DotMatrix #(.inputtype("row"), .matrixcols(30), .matrixrows(2)) dotmatrix_105 (
    .row0(carconnectorv2_17_tobackground_9), .row1(carconnectorv2_17_tobackground_10));
  DotMatrix #(.inputtype("row"), .matrixcols(30), .matrixrows(2)) dotmatrix_106 (
    .row0(carconnectorv2_18_tobackground), .row1(carconnectorv2_18_tobackground_2));
  DotMatrix #(.inputtype("row"), .matrixcols(30), .matrixrows(10)) dotmatrix_107 (
    .row0(carconnectorv2_18_tofront), .row1(carconnectorv2_18_tofront_2), .row2(carconnectorv2_18_tofront_3),
    .row3(carconnectorv2_18_tofront_4), .row4(carconnectorv2_18_tofront_5),
    .row5(carconnectorv2_18_tofront_6), .row6(carconnectorv2_18_tofront_7),
    .row7(carconnectorv2_18_tofront_8), .row8(carconnectorv2_18_tofront_9),
    .row9(carconnectorv2_18_tofront_10));
  carConnectorV2 carconnectorv2_18 (
    .inBackShiftD(carconnectorv2_13_outbackshiftd), .inputBackShiftM(carconnectorv2_13_outputbackshiftm),
    .inPlayerShiftM(carconnectorv2_13_outplayershiftm), .inFlag(carconnectorv2_13_outflag),
    .toBackground(carconnectorv2_18_tobackground), .toBackground_2(carconnectorv2_18_tobackground_2),
    .toBackground_3(carconnectorv2_18_tobackground_3), .toBackground_4(carconnectorv2_18_tobackground_4),
    .toBackground_5(carconnectorv2_18_tobackground_5), .toBackground_6(carconnectorv2_18_tobackground_6),
    .toBackground_7(carconnectorv2_18_tobackground_7), .toBackground_8(carconnectorv2_18_tobackground_8),
    .toBackground_9(carconnectorv2_18_tobackground_9), .toBackground_10(carconnectorv2_18_tobackground_10),
    .toFront(carconnectorv2_18_tofront), .toFront_2(carconnectorv2_18_tofront_2),
    .toFront_3(carconnectorv2_18_tofront_3), .toFront_4(carconnectorv2_18_tofront_4),
    .toFront_5(carconnectorv2_18_tofront_5), .toFront_6(carconnectorv2_18_tofront_6),
    .toFront_7(carconnectorv2_18_tofront_7), .toFront_8(carconnectorv2_18_tofront_8),
    .toFront_9(carconnectorv2_18_tofront_9), .toFront_10(carconnectorv2_18_tofront_10),
    .inPlayerShiftD(carconnectorv2_13_outplayershiftd));  // open: outBackShiftD, outputBackShiftM, outPlayerShiftD, outPlayerShiftM, outFlag
  DotMatrix #(.inputtype("row"), .matrixcols(30), .matrixrows(6)) dotmatrix_108 (
    .row0(carconnectorv2_18_tobackground_3), .row1(carconnectorv2_18_tobackground_4),
    .row2(carconnectorv2_18_tobackground_5), .row3(carconnectorv2_18_tobackground_6),
    .row4(carconnectorv2_18_tobackground_7), .row5(carconnectorv2_18_tobackground_8));
  DotMatrix #(.inputtype("row"), .matrixcols(30), .matrixrows(2)) dotmatrix_109 (
    .row0(carconnectorv2_18_tobackground_9), .row1(carconnectorv2_18_tobackground_10));
  DotMatrix #(.inputtype("row"), .matrixcols(30), .matrixrows(10)) dotmatrix_110 (
    .row0(carconnectorv2_19_tofront), .row1(carconnectorv2_19_tofront_2), .row2(carconnectorv2_19_tofront_3),
    .row3(carconnectorv2_19_tofront_4), .row4(carconnectorv2_19_tofront_5),
    .row5(carconnectorv2_19_tofront_6), .row6(carconnectorv2_19_tofront_7),
    .row7(carconnectorv2_19_tofront_8), .row8(carconnectorv2_19_tofront_9),
    .row9(carconnectorv2_19_tofront_10));
  DotMatrix #(.inputtype("row"), .matrixcols(30), .matrixrows(2)) dotmatrix_111 (
    .row0(carconnectorv2_19_tobackground), .row1(carconnectorv2_19_tobackground_2));
  carConnectorV2 carconnectorv2_19 (
    .inBackShiftD(carconnectorv2_14_outbackshiftd), .inputBackShiftM(carconnectorv2_14_outputbackshiftm),
    .inPlayerShiftM(carconnectorv2_14_outplayershiftm), .inFlag(carconnectorv2_14_outflag),
    .toBackground(carconnectorv2_19_tobackground), .toBackground_2(carconnectorv2_19_tobackground_2),
    .toBackground_3(carconnectorv2_19_tobackground_3), .toBackground_4(carconnectorv2_19_tobackground_4),
    .toBackground_5(carconnectorv2_19_tobackground_5), .toBackground_6(carconnectorv2_19_tobackground_6),
    .toBackground_7(carconnectorv2_19_tobackground_7), .toBackground_8(carconnectorv2_19_tobackground_8),
    .toBackground_9(carconnectorv2_19_tobackground_9), .toBackground_10(carconnectorv2_19_tobackground_10),
    .toFront(carconnectorv2_19_tofront), .toFront_2(carconnectorv2_19_tofront_2),
    .toFront_3(carconnectorv2_19_tofront_3), .toFront_4(carconnectorv2_19_tofront_4),
    .toFront_5(carconnectorv2_19_tofront_5), .toFront_6(carconnectorv2_19_tofront_6),
    .toFront_7(carconnectorv2_19_tofront_7), .toFront_8(carconnectorv2_19_tofront_8),
    .toFront_9(carconnectorv2_19_tofront_9), .toFront_10(carconnectorv2_19_tofront_10),
    .inPlayerShiftD(carconnectorv2_14_outplayershiftd));  // open: outBackShiftD, outputBackShiftM, outPlayerShiftD, outPlayerShiftM, outFlag
  DotMatrix #(.inputtype("row"), .matrixcols(30), .matrixrows(6)) dotmatrix_112 (
    .row0(carconnectorv2_19_tobackground_3), .row1(carconnectorv2_19_tobackground_4),
    .row2(carconnectorv2_19_tobackground_5), .row3(carconnectorv2_19_tobackground_6),
    .row4(carconnectorv2_19_tobackground_7), .row5(carconnectorv2_19_tobackground_8));
  DotMatrix #(.inputtype("row"), .matrixcols(30), .matrixrows(2)) dotmatrix_113 (
    .row0(carconnectorv2_19_tobackground_9), .row1(carconnectorv2_19_tobackground_10));
  carConnectorV2 carconnectorv2_20 (
    .inBackShiftD(carconnectorv2_15_outbackshiftd), .inputBackShiftM(carconnectorv2_15_outputbackshiftm),
    .inPlayerShiftM(carconnectorv2_15_outplayershiftm), .inFlag(carconnectorv2_15_outflag),
    .toBackground(carconnectorv2_20_tobackground), .toBackground_2(carconnectorv2_20_tobackground_2),
    .toBackground_3(carconnectorv2_20_tobackground_3), .toBackground_4(carconnectorv2_20_tobackground_4),
    .toBackground_5(carconnectorv2_20_tobackground_5), .toBackground_6(carconnectorv2_20_tobackground_6),
    .toBackground_7(carconnectorv2_20_tobackground_7), .toBackground_8(carconnectorv2_20_tobackground_8),
    .toBackground_9(carconnectorv2_20_tobackground_9), .toBackground_10(carconnectorv2_20_tobackground_10),
    .toFront(carconnectorv2_20_tofront), .toFront_2(carconnectorv2_20_tofront_2),
    .toFront_3(carconnectorv2_20_tofront_3), .toFront_4(carconnectorv2_20_tofront_4),
    .toFront_5(carconnectorv2_20_tofront_5), .toFront_6(carconnectorv2_20_tofront_6),
    .toFront_7(carconnectorv2_20_tofront_7), .toFront_8(carconnectorv2_20_tofront_8),
    .toFront_9(carconnectorv2_20_tofront_9), .toFront_10(carconnectorv2_20_tofront_10),
    .inPlayerShiftD(carconnectorv2_15_outplayershiftd));  // open: outBackShiftD, outputBackShiftM, outPlayerShiftD, outPlayerShiftM, outFlag
  DotMatrix #(.inputtype("row"), .matrixcols(30), .matrixrows(2)) dotmatrix_114 (
    .row0(carconnectorv2_20_tobackground), .row1(carconnectorv2_20_tobackground_2));
  DotMatrix #(.inputtype("row"), .matrixcols(30), .matrixrows(10)) dotmatrix_115 (
    .row0(carconnectorv2_20_tofront), .row1(carconnectorv2_20_tofront_2), .row2(carconnectorv2_20_tofront_3),
    .row3(carconnectorv2_20_tofront_4), .row4(carconnectorv2_20_tofront_5),
    .row5(carconnectorv2_20_tofront_6), .row6(carconnectorv2_20_tofront_7),
    .row7(carconnectorv2_20_tofront_8), .row8(carconnectorv2_20_tofront_9),
    .row9(carconnectorv2_20_tofront_10));
  DotMatrix #(.inputtype("row"), .matrixcols(30), .matrixrows(6)) dotmatrix_116 (
    .row0(carconnectorv2_20_tobackground_3), .row1(carconnectorv2_20_tobackground_4),
    .row2(carconnectorv2_20_tobackground_5), .row3(carconnectorv2_20_tobackground_6),
    .row4(carconnectorv2_20_tobackground_7), .row5(carconnectorv2_20_tobackground_8));
  DotMatrix #(.inputtype("row"), .matrixcols(30), .matrixrows(2)) dotmatrix_117 (
    .row0(carconnectorv2_20_tobackground_9), .row1(carconnectorv2_20_tobackground_10));
  DotMatrix #(.inputtype("row"), .matrixcols(30), .matrixrows(10)) dotmatrix_118 (
    .row0(swamp_8_tobackground), .row1(swamp_8_tobackground_2), .row2(swamp_8_tobackground_3),
    .row3(swamp_8_tobackground_4), .row4(swamp_8_tobackground_5), .row5(swamp_8_tobackground_6),
    .row6(swamp_8_tobackground_7), .row7(swamp_8_tobackground_8), .row8(swamp_8_tobackground_9),
    .row9(swamp_8_tobackground_10));
  swamp swamp_8 (
    .inPlayerShiftD(swamp_6_outplayershiftd), .inPlayerShiftM(swamp_6_outplayershiftm),
    .inFlag(swamp_6_outflag), .toBackground(swamp_8_tobackground), .toFront(swamp_8_tofront),
    .toBackground_2(swamp_8_tobackground_2), .toFront_2(swamp_8_tofront_2),
    .toBackground_3(swamp_8_tobackground_3), .toFront_3(swamp_8_tofront_3),
    .toBackground_4(swamp_8_tobackground_4), .toFront_4(swamp_8_tofront_4),
    .toBackground_5(swamp_8_tobackground_5), .toFront_5(swamp_8_tofront_5),
    .toBackground_6(swamp_8_tobackground_6), .toFront_6(swamp_8_tofront_6),
    .toBackground_7(swamp_8_tobackground_7), .toFront_7(swamp_8_tofront_7),
    .toBackground_8(swamp_8_tobackground_8), .toFront_8(swamp_8_tofront_8),
    .toBackground_9(swamp_8_tobackground_9), .toFront_9(swamp_8_tofront_9),
    .toBackground_10(swamp_8_tobackground_10), .toFront_10(swamp_8_tofront_10));  // open: outPlayerShiftD, outPlayerShiftM, outFlag
  DotMatrix #(.inputtype("row"), .matrixcols(30), .matrixrows(10)) dotmatrix_119 (
    .row0(swamp_8_tofront), .row1(swamp_8_tofront_2), .row2(swamp_8_tofront_3), .row3(swamp_8_tofront_4),
    .row4(swamp_8_tofront_5), .row5(swamp_8_tofront_6), .row6(swamp_8_tofront_7), .row7(swamp_8_tofront_8),
    .row8(swamp_8_tofront_9), .row9(swamp_8_tofront_10));
endmodule

module _10x10_models (
);

  wire undriven;
  wire [31:0] random_1_out;

  DotMatrix #(.inputtype("row"), .matrixcols(20), .matrixrows(2)) dotmatrix_1 (.row0(20'h3c078), .row1(20'h3c078));
  DotMatrix #(.inputtype("row"), .matrixcols(20), .matrixrows(6)) dotmatrix_2 (
    .row0(20'h79fff), .row1(20'h89242), .row2(20'hf9fff), .row3(20'hf9fff), .row4(20'h89242), .row5(20'h79fff));
  DotMatrix #(.inputtype("row"), .matrixcols(20), .matrixrows(2)) dotmatrix_3 (.row0(20'h3c078), .row1(20'h3c078));
  DotMatrix #(.inputtype("row"), .matrixcols(10), .matrixrows(2)) dotmatrix_4 (.row0(10'h1e7), .row1(10'h84));
  DotMatrix #(.inputtype("row"), .matrixcols(10), .matrixrows(6)) dotmatrix_5 (
    .row0(10'hfc), .row1(10'h1fe), .row2({10{1'b1}}), .row3({10{1'b1}}), .row4(10'h1fe), .row5(10'hfc));
  DotMatrix #(.inputtype("row"), .matrixcols(10), .matrixrows(2)) dotmatrix_6 (.row0(10'h84), .row1(10'h1e7));
  DotMatrix #(.inputtype("row"), .matrixcols(30), .matrixrows(2)) dotmatrix_7 (.row0(30'h1e779de7), .row1(30'h8421084));
  DotMatrix #(.inputtype("row"), .matrixcols(30), .matrixrows(6)) dotmatrix_8 (
    .row0(30'hfc3f0fc), .row1(30'h1fe7f9fe), .row2({30{1'b1}}), .row3({30{1'b1}}), .row4(30'h1fe7f9fe),
    .row5(30'hfc3f0fc));
  DotMatrix #(.inputtype("row"), .matrixcols(30), .matrixrows(2)) dotmatrix_9 (.row0(30'h8421084), .row1(30'h1e779de7));
  DotMatrix #(.inputtype("row"), .matrixcols(30), .matrixrows(2)) dotmatrix_10 (.row0({30{1'b0}}), .row1(30'hc6318c6));
  DotMatrix #(.inputtype("row"), .matrixcols(30), .matrixrows(6)) dotmatrix_11 (
    .row0(30'hfc3f0fc), .row1(30'h1fe7f9fe), .row2({30{1'b1}}), .row3({30{1'b1}}), .row4(30'h1fe7f9fe),
    .row5(30'hfc3f0fc));
  DotMatrix #(.inputtype("row"), .matrixcols(30), .matrixrows(2)) dotmatrix_12 (.row0(30'hc6318c6), .row1({30{1'b0}}));
  DotMatrix #(.inputtype("row"), .matrixcols(30), .matrixrows(2)) dotmatrix_13 (.row0({30{1'b0}}), .row1({30{1'b0}}));
  DotMatrix #(.inputtype("row"), .matrixcols(30), .matrixrows(6)) dotmatrix_14 (
    .row0(30'hfc3f0fc), .row1(30'h1fe7f9fe), .row2({30{1'b1}}), .row3({30{1'b1}}), .row4(30'h1fe7f9fe),
    .row5(30'hfc3f0fc));
  DotMatrix #(.inputtype("row"), .matrixcols(30), .matrixrows(2)) dotmatrix_15 (.row0({30{1'b0}}), .row1({30{1'b0}}));
  DotMatrix #(.inputtype("row"), .matrixcols(20), .matrixrows(2)) dotmatrix_16 (.row0(20'h79de7), .row1(20'h21084));
  DotMatrix #(.inputtype("row"), .matrixcols(20), .matrixrows(6)) dotmatrix_17 (
    .row0(20'h3f0fc), .row1(20'h7f9fe), .row2({20{1'b1}}), .row3({20{1'b1}}), .row4(20'h7f9fe),
    .row5(20'h3f0fc));
  DotMatrix #(.inputtype("row"), .matrixcols(20), .matrixrows(2)) dotmatrix_18 (.row0(20'h21084), .row1(20'h79de7));
  DotMatrix #(.inputtype("row"), .matrixcols(20), .matrixrows(2)) dotmatrix_19 (.row0({20{1'b0}}), .row1(20'h318c6));
  DotMatrix #(.inputtype("row"), .matrixcols(20), .matrixrows(6)) dotmatrix_20 (
    .row0(20'h3f0fc), .row1(20'h7f9fe), .row2({20{1'b1}}), .row3({20{1'b1}}), .row4(20'h7f9fe),
    .row5(20'h3f0fc));
  DotMatrix #(.inputtype("row"), .matrixcols(20), .matrixrows(2)) dotmatrix_21 (.row0(20'h318c6), .row1({20{1'b0}}));
  DotMatrix #(.inputtype("row"), .matrixcols(20), .matrixrows(2)) dotmatrix_22 (.row0({20{1'b0}}), .row1({20{1'b0}}));
  DotMatrix #(.inputtype("row"), .matrixcols(20), .matrixrows(6)) dotmatrix_23 (
    .row0(20'h3f0fc), .row1(20'h7f9fe), .row2({20{1'b1}}), .row3({20{1'b1}}), .row4(20'h7f9fe),
    .row5(20'h3f0fc));
  DotMatrix #(.inputtype("row"), .matrixcols(20), .matrixrows(2)) dotmatrix_24 (.row0({20{1'b0}}), .row1({20{1'b0}}));
  DotMatrix #(.inputtype("row"), .matrixcols(30), .matrixrows(2)) dotmatrix_25 (
    .row0(30'h8421084), .row1(30'h1ce739ce));
  DotMatrix #(.inputtype("row"), .matrixcols(30), .matrixrows(3)) dotmatrix_26 (
    .row0({30{1'b1}}), .row1(30'h1ce739ce), .row2(30'h8421084));
  DotMatrix #(.inputtype("row"), .matrixcols(30), .matrixrows(1)) dotmatrix_27 (.row0(30'h8421084));
  DotMatrix #(.inputtype("row"), .matrixcols(30), .matrixrows(2)) dotmatrix_28 (.row0(30'h1ce739ce), .row1({30{1'b1}}));
  DotMatrix #(.inputtype("row"), .matrixcols(30), .matrixrows(2)) dotmatrix_29 (
    .row0(30'h1ce739ce), .row1(30'h8421084));
  DotMatrix #(.inputtype("row"), .matrixcols(30), .matrixrows(2)) dotmatrix_30 (.row0({30{1'b0}}), .row1({30{1'b0}}));
  DotMatrix #(.inputtype("row"), .matrixcols(30), .matrixrows(3)) dotmatrix_31 (
    .row0(30'h3ff), .row1(30'h3f9), .row2(30'h3ff));
  DotMatrix #(.inputtype("row"), .matrixcols(30), .matrixrows(1)) dotmatrix_32 (.row0(30'h3aa));
  DotMatrix #(.inputtype("row"), .matrixcols(30), .matrixrows(2)) dotmatrix_33 (.row0(30'h3fe), .row1(30'h3ff));
  DotMatrix #(.inputtype("row"), .matrixcols(30), .matrixrows(2)) dotmatrix_34 (.row0({30{1'b0}}), .row1({30{1'b0}}));
  DotMatrix #(.inputtype("row"), .matrixcols(30), .matrixrows(2)) dotmatrix_35 (.row0({30{1'b0}}), .row1({30{1'b1}}));
  DotMatrix #(.inputtype("row"), .matrixcols(30), .matrixrows(3)) dotmatrix_36 (
    .row0(30'h2fbfcfef), .row1(30'h3fafafaf), .row2(30'h3eeeeeee));
  DotMatrix #(.inputtype("row"), .matrixcols(30), .matrixrows(1)) dotmatrix_37 (.row0(30'h2edfbafa));
  DotMatrix #(.inputtype("row"), .matrixcols(30), .matrixrows(2)) dotmatrix_38 (.row0({30{1'b1}}), .row1(30'h3f7ba9f));
  DotMatrix #(.inputtype("row"), .matrixcols(30), .matrixrows(2)) dotmatrix_39 (.row0({30{1'b1}}), .row1({30{1'b0}}));
  DotMatrix #(.inputtype("row"), .matrixcols(10), .matrixrows(2)) dotmatrix_40 (.row0({10{1'b0}}), .row1(10'hc6));
  DotMatrix #(.inputtype("row"), .matrixcols(10), .matrixrows(6)) dotmatrix_41 (
    .row0(10'hfc), .row1(10'h1fe), .row2({10{1'b1}}), .row3({10{1'b1}}), .row4(10'h1fe), .row5(10'hfc));
  DotMatrix #(.inputtype("row"), .matrixcols(10), .matrixrows(2)) dotmatrix_42 (.row0(10'hc6), .row1({10{1'b0}}));
  DotMatrix #(.inputtype("row"), .matrixcols(30), .matrixrows(2)) dotmatrix_43 (.row0(30'h300c030), .row1(30'h781e078));
  DotMatrix #(.inputtype("row"), .matrixcols(30), .matrixrows(3)) dotmatrix_44 (
    .row0(30'hfc3f0fc), .row1(30'h1fe7f9fe), .row2({30{1'b1}}));
  DotMatrix #(.inputtype("row"), .matrixcols(30), .matrixrows(1)) dotmatrix_45 (.row0({30{1'b1}}));
  DotMatrix #(.inputtype("row"), .matrixcols(30), .matrixrows(2)) dotmatrix_46 (
    .row0(30'h1fe7f9fe), .row1(30'hfc3f0fc));
  DotMatrix #(.inputtype("row"), .matrixcols(30), .matrixrows(2)) dotmatrix_47 (.row0(30'h781e078), .row1(30'h300c030));
  Random #(.width(32)) random_1 (.clk(undriven), .out(random_1_out));  // open: next, clr
  DotMatrix #(.inputtype("row"), .matrixcols(10), .matrixrows(3)) dotmatrix_48 (
    .row0({10{1'b0}}), .row1({10{1'b0}}), .row2(10'h86));
  DotMatrix #(.inputtype("row"), .matrixcols(10), .matrixrows(1)) dotmatrix_49 (.row0(10'hfe));
  DotMatrix #(.inputtype("row"), .matrixcols(10), .matrixrows(2)) dotmatrix_50 (.row0(10'h1ff), .row1(10'h1ff));
  DotMatrix #(.inputtype("row"), .matrixcols(10), .matrixrows(1)) dotmatrix_51 (.row0(10'hfe));
  DotMatrix #(.inputtype("row"), .matrixcols(10), .matrixrows(3)) dotmatrix_52 (
    .row0(10'h86), .row1({10{1'b0}}), .row2({10{1'b0}}));
  DotMatrix #(.inputtype("row"), .matrixcols(10), .matrixrows(2)) dotmatrix_53 (.row0({10{1'b0}}), .row1({10{1'b0}}));
  DotMatrix #(.inputtype("row"), .matrixcols(10), .matrixrows(6)) dotmatrix_54 (
    .row0(10'hfc), .row1(10'h1fe), .row2({10{1'b1}}), .row3({10{1'b1}}), .row4(10'h1fe), .row5(10'hfc));
  DotMatrix #(.inputtype("row"), .matrixcols(10), .matrixrows(2)) dotmatrix_55 (.row0({10{1'b0}}), .row1({10{1'b0}}));
  // Probe on random_1_out
  // Probe on random_1_out
  DotMatrix #(.inputtype("row"), .matrixcols(10), .matrixrows(10)) dotmatrix_56 (
    .row0(10'h279), .row1(10'h231), .row2(10'h279), .row3({10{1'b1}}), .row4(10'hfc), .row5(10'hfc),
    .row6({10{1'b1}}), .row7(10'h279), .row8(10'h231), .row9(10'h201));
  DotMatrix #(.inputtype("row"), .matrixcols(10), .matrixrows(2)) dotmatrix_57 (.row0({10{1'b0}}), .row1(10'h84));
  DotMatrix #(.inputtype("row"), .matrixcols(10), .matrixrows(6)) dotmatrix_58 (
    .row0(10'h1fe), .row1(10'h343), .row2(10'h243), .row3(10'h243), .row4(10'h343), .row5(10'h1fe));
  DotMatrix #(.inputtype("row"), .matrixcols(10), .matrixrows(2)) dotmatrix_59 (.row0(10'h84), .row1({10{1'b0}}));
  DotMatrix #(.inputtype("row"), .matrixcols(10), .matrixrows(2)) dotmatrix_60 (.row0({10{1'b0}}), .row1({10{1'b0}}));
  DotMatrix #(.inputtype("row"), .matrixcols(10), .matrixrows(6)) dotmatrix_61 (
    .row0(10'h30), .row1(10'h78), .row2(10'hfc), .row3(10'hfc), .row4(10'h78), .row5(10'h30));
  DotMatrix #(.inputtype("row"), .matrixcols(10), .matrixrows(2)) dotmatrix_62 (.row0({10{1'b0}}), .row1({10{1'b0}}));
  DotMatrix #(.inputtype("row"), .matrixcols(30), .matrixrows(2)) dotmatrix_63 (.row0({30{1'b0}}), .row1({30{1'b0}}));
  DotMatrix #(.inputtype("row"), .matrixcols(30), .matrixrows(6)) dotmatrix_64 (
    .row0(30'h300c030), .row1(30'h781e078), .row2(30'hfc3f0fc), .row3(30'hfc3f0fc), .row4(30'h781e078),
    .row5(30'h300c030));
  DotMatrix #(.inputtype("row"), .matrixcols(30), .matrixrows(2)) dotmatrix_65 (.row0({30{1'b0}}), .row1({30{1'b0}}));
  DotMatrix #(.inputtype("row"), .matrixcols(30), .matrixrows(2)) dotmatrix_66 (.row0({30{1'b0}}), .row1({30{1'b0}}));
  DotMatrix #(.inputtype("row"), .matrixcols(30), .matrixrows(6)) dotmatrix_67 (
    .row0({30{1'b0}}), .row1({30{1'b0}}), .row2(30'h300c030), .row3(30'h300c030), .row4({30{1'b0}}),
    .row5({30{1'b0}}));
  DotMatrix #(.inputtype("row"), .matrixcols(30), .matrixrows(2)) dotmatrix_68 (.row0({30{1'b0}}), .row1({30{1'b0}}));
  DotMatrix #(.inputtype("row"), .matrixcols(30), .matrixrows(2)) dotmatrix_69 (.row0({30{1'b0}}), .row1({30{1'b0}}));
  DotMatrix #(.inputtype("row"), .matrixcols(30), .matrixrows(6)) dotmatrix_70 (
    .row0({30{1'b0}}), .row1({30{1'b0}}), .row2({30{1'b0}}), .row3({30{1'b0}}), .row4({30{1'b0}}),
    .row5({30{1'b0}}));
  DotMatrix #(.inputtype("row"), .matrixcols(30), .matrixrows(2)) dotmatrix_71 (.row0({30{1'b0}}), .row1({30{1'b0}}));
  DotMatrix #(.inputtype("row"), .matrixcols(20), .matrixrows(2)) dotmatrix_72 (.row0({20{1'b0}}), .row1({20{1'b0}}));
  DotMatrix #(.inputtype("row"), .matrixcols(20), .matrixrows(6)) dotmatrix_73 (
    .row0(20'hc030), .row1(20'h1e078), .row2(20'h3f0fc), .row3(20'h3f0fc), .row4(20'h1e078), .row5(20'hc030));
  DotMatrix #(.inputtype("row"), .matrixcols(20), .matrixrows(2)) dotmatrix_74 (.row0({20{1'b0}}), .row1({20{1'b0}}));
  DotMatrix #(.inputtype("row"), .matrixcols(20), .matrixrows(2)) dotmatrix_75 (.row0({20{1'b0}}), .row1({20{1'b0}}));
  DotMatrix #(.inputtype("row"), .matrixcols(20), .matrixrows(6)) dotmatrix_76 (
    .row0({20{1'b0}}), .row1({20{1'b0}}), .row2(20'hc030), .row3(20'hc030), .row4({20{1'b0}}),
    .row5({20{1'b0}}));
  DotMatrix #(.inputtype("row"), .matrixcols(20), .matrixrows(2)) dotmatrix_77 (.row0({20{1'b0}}), .row1({20{1'b0}}));
  DotMatrix #(.inputtype("row"), .matrixcols(20), .matrixrows(2)) dotmatrix_78 (.row0({20{1'b0}}), .row1({20{1'b0}}));
  DotMatrix #(.inputtype("row"), .matrixcols(20), .matrixrows(6)) dotmatrix_79 (
    .row0({20{1'b0}}), .row1({20{1'b0}}), .row2({20{1'b0}}), .row3({20{1'b0}}), .row4({20{1'b0}}),
    .row5({20{1'b0}}));
  DotMatrix #(.inputtype("row"), .matrixcols(20), .matrixrows(2)) dotmatrix_80 (.row0({20{1'b0}}), .row1({20{1'b0}}));
  DotMatrix #(.inputtype("row"), .matrixcols(30), .matrixrows(2)) dotmatrix_81 (.row0({30{1'b0}}), .row1(30'hfceaf));
  DotMatrix #(.inputtype("row"), .matrixcols(30), .matrixrows(3)) dotmatrix_82 (
    .row0(30'h1ff0fa), .row1(30'h1fffff), .row2(30'h1eeeee));
  DotMatrix #(.inputtype("row"), .matrixcols(30), .matrixrows(1)) dotmatrix_83 (.row0(30'hfbafa));
  DotMatrix #(.inputtype("row"), .matrixcols(30), .matrixrows(2)) dotmatrix_84 (.row0(30'hfffff), .row1(30'h1bbbbb));
  DotMatrix #(.inputtype("row"), .matrixcols(30), .matrixrows(2)) dotmatrix_85 (.row0(30'heeeee), .row1({30{1'b0}}));
  DotMatrix #(.inputtype("row"), .matrixcols(10), .matrixrows(2)) dotmatrix_86 (.row0(10'h84), .row1(10'h1ce));
  DotMatrix #(.inputtype("row"), .matrixcols(10), .matrixrows(6)) dotmatrix_87 (
    .row0(10'h1fe), .row1(10'h343), .row2(10'h243), .row3(10'h243), .row4(10'h343), .row5(10'h1fe));
  DotMatrix #(.inputtype("row"), .matrixcols(10), .matrixrows(2)) dotmatrix_88 (.row0(10'h1ce), .row1(10'h84));
  DotMatrix #(.inputtype("row"), .matrixcols(10), .matrixrows(2)) dotmatrix_89 (.row0({10{1'b0}}), .row1({10{1'b0}}));
  DotMatrix #(.inputtype("row"), .matrixcols(10), .matrixrows(6)) dotmatrix_90 (
    .row0({10{1'b0}}), .row1({10{1'b0}}), .row2(10'h30), .row3(10'h30), .row4({10{1'b0}}), .row5({10{1'b0}}));
  DotMatrix #(.inputtype("row"), .matrixcols(10), .matrixrows(2)) dotmatrix_91 (.row0({10{1'b0}}), .row1({10{1'b0}}));
  DotMatrix #(.inputtype("row"), .matrixcols(30), .matrixrows(10)) dotmatrix_92 (
    .row0(30'h279), .row1(30'h231), .row2(30'h279), .row3(30'h3ff), .row4(30'hfc), .row5(30'hfc),
    .row6(30'h3ff), .row7(30'h279), .row8(30'h231), .row9(30'h201));
  DotMatrix #(.inputtype("row"), .matrixcols(10), .matrixrows(2)) dotmatrix_93 (.row0({10{1'b0}}), .row1({10{1'b0}}));
  DotMatrix #(.inputtype("row"), .matrixcols(10), .matrixrows(6)) dotmatrix_94 (
    .row0({10{1'b0}}), .row1({10{1'b0}}), .row2({10{1'b0}}), .row3({10{1'b0}}), .row4({10{1'b0}}),
    .row5({10{1'b0}}));
  DotMatrix #(.inputtype("row"), .matrixcols(10), .matrixrows(2)) dotmatrix_95 (.row0({10{1'b0}}), .row1({10{1'b0}}));

  // Notes on the sheet:
  //   ALL TURTLE'S STAGES
  //   all turtles stages on full matrice
  //   LOGS of len 1 2 and 3 (colors will be another)
  //   FROG
  //   FORMULA TO MAKE 3 MODELS = 10x10 val * (100_000+400+1)
  //   FORMULA TO MAKE 2 MODELS = 10x10 val * (400+1)
  //   FROG in full matrice
endmodule

// shifter
module shiftMaker (
  input  tactGen,
  input  reset,
  output [4:0] shiftM,
  output [1:0] shiftD
);

  wire comparator_1_eq, or_1_out;

  Counter #(.width(5), .max('h1f)) matricePos (
    .Q(shiftM), .clk(tactGen), .clr(or_1_out));  // open: load, D, count, carry
  Comparator #(.width(5), .mode("unsigned")) comparator_1 (
    .a(shiftM), .b(5'b11110), .eq(comparator_1_eq));  // open: gt, lt
  or or_1 (or_1_out, comparator_1_eq, reset);
  Counter #(.width(2), .max('h3)) displayPos (
    .Q(shiftD), .clk(comparator_1_eq), .clr(reset));  // open: load, D, count, carry
  Pull_Resistor pull_resistor_1 (.node(reset));
endmodule

module controller (
  input  D,
  input  A,
  input  reset,
  output [4:0] shiftM,
  output [1:0] shiftD
);

  wire comparator_1_eq, or_1_out, or_2_out;
  wire [4:0] mPos_2_q, mPos_q, shifter_1_out, shifter_2_out;

  or or_1 (or_1_out, D, A);
  // Probe on mPos_2_q
  Counter #(.width(5), .max('h1f)) mPos (
    .load(D), .D(5'b00001), .count(or_1_out), .Q(mPos_q), .clk(or_1_out), .clr(or_2_out));  // open: carry
  Counter #(.width(5), .max('h1f)) mPos_2 (
    .load(D), .count(or_1_out), .Q(mPos_2_q), .clk(or_1_out), .clr(or_2_out));  // open: D, carry
  // Probe on shifter_2_out
  // Probe on mPos_q
  Shifter #(.width(5)) shifter_1 (.in(mPos_q), .\dist (3'b011), .out(shifter_1_out));
  Shifter #(.width(5)) shifter_2 (.in(mPos_2_q), .\dist (3'b001), .out(shifter_2_out));
  // Probe on shifter_1_out
  Adder #(.width(5)) adder_1 (.a(shifter_1_out), .b(shifter_2_out), .out(shiftM));  // open: cin, cout
  // Probe on shiftM
  Comparator #(.width(5), .mode("unsigned")) comparator_1 (
    .a(shiftM), .b(5'b11110), .eq(comparator_1_eq));  // open: gt, lt
  or or_2 (or_2_out, comparator_1_eq, reset);
  // Probe on shiftD
  Counter #(.width(2), .max('h3)) displayPos (
    .Q(shiftD), .clk(comparator_1_eq), .clr(reset));  // open: load, D, count, carry
  Pull_Resistor pull_resistor_1 (.node(reset));
endmodule

// carConnector
module carConnectorV2 (
  input  [1:0] inBackShiftD,
  input  [4:0] inputBackShiftM,
  input  [1:0] inPlayerShiftD,
  input  [4:0] inPlayerShiftM,
  input  inFlag,
  output [29:0] toBackground,
  output [29:0] toFront,
  output [29:0] toBackground_2,
  output [29:0] toFront_2,
  output [29:0] toBackground_3,
  output [29:0] toFront_3,
  output [29:0] toBackground_4,
  output [29:0] toFront_4,
  output [29:0] toBackground_5,
  output [29:0] toFront_5,
  output [1:0] outBackShiftD,
  output [29:0] toBackground_6,
  output [29:0] toFront_6,
  output [4:0] outputBackShiftM,
  output [29:0] toBackground_7,
  output [29:0] toFront_7,
  output [29:0] toBackground_8,
  output [29:0] toFront_8,
  output [29:0] toBackground_9,
  output [29:0] toFront_9,
  output [29:0] toBackground_10,
  output [29:0] toFront_10,
  output [1:0] outPlayerShiftD,
  output [4:0] outPlayerShiftM,
  output outFlag
);

  wire comparator_1_eq, comparator_2_eq, comparator_3_eq, comparator_4_eq, comparator_5_eq,
       controlled_buffer_21_out, controlled_buffer_22_out;
  wire [1:0] adder_5_out, multiplexer_1_out;
  wire [4:0] adder_3_out, adder_4_out, adder_6_out, adder_7_out, adder_8_out, not_1_out, not_2_out;
  wire [29:0] controlled_buffer_5_out, controlled_buffer_7_out, controlled_buffer_8_out,
       controlled_buffer_9_out, controlled_buffer_10_out, controlled_buffer_11_out, controlled_buffer_12_out,
       controlled_buffer_13_out, controlled_buffer_16_out, controlled_buffer_18_out,
       controlled_buffer_19_out, controlled_buffer_20_out, controlled_buffer_25_out,
       controlled_buffer_28_out, controlled_buffer_29_out, controlled_buffer_32_out,
       controlled_buffer_33_out, controlled_buffer_34_out, controlled_buffer_35_out,
       controlled_buffer_36_out, controlled_buffer_39_out, controlled_buffer_41_out, pull_resistor_3_node,
       pull_resistor_5_node, pull_resistor_6_node, pull_resistor_7_node, pull_resistor_9_node,
       pull_resistor_17_node, pull_resistor_18_node, pull_resistor_20_node, pull_resistor_25_node,
       pull_resistor_27_node, pull_resistor_29_node, pull_resistor_30_node, pull_resistor_33_node,
       pull_resistor_34_node, pull_resistor_40_node, pull_resistor_41_node, pull_resistor_43_node,
       pull_resistor_45_node, shifter_1_out, shifter_2_out, shifter_3_out, shifter_4_out, shifter_5_out,
       shifter_6_out, shifter_7_out, shifter_8_out, shifter_9_out, shifter_10_out, shifter_11_out,
       shifter_12_out, shifter_13_out, shifter_14_out, shifter_15_out, shifter_16_out, shifter_17_out,
       shifter_18_out, shifter_19_out, shifter_20_out, shifter_21_out, shifter_22_out, shifter_23_out,
       shifter_24_out, shifter_25_out, shifter_26_out, shifter_27_out, shifter_28_out, shifter_29_out,
       shifter_30_out, shifter_31_out, shifter_32_out, shifter_33_out, shifter_34_out, shifter_35_out,
       shifter_36_out, shifter_37_out, shifter_38_out, shifter_39_out, shifter_40_out;

  Pull_Resistor pull_resistor_1 (.node(inputBackShiftM));
  Comparator #(.width(2)) comparator_1 (.a(2'b00), .b(inBackShiftD), .eq(comparator_1_eq));  // open: gt, lt
  Adder #(.width(2)) adder_1 (.a(inBackShiftD), .b(2'b01), .out(outBackShiftD));  // open: cin, cout
  // Probe on outBackShiftD
  // Probe on outBackShiftD
  // Probe on 2'b00
  Comparator #(.width(2)) comparator_2 (.a(outBackShiftD), .b(2'b00), .eq(comparator_2_eq));  // open: gt, lt
  Adder #(.width(2)) adder_2 (.a(inPlayerShiftD), .b(2'b01), .out(outPlayerShiftD));  // open: cin, cout
  Pull_Resistor pull_resistor_2 (.node(inPlayerShiftM));
  Adder #(.width(5)) adder_3 (.a(inPlayerShiftM), .b(5'b00001), .out(adder_3_out));  // open: cin, cout
  Comparator #(.width(5), .mode("unsigned")) comparator_3 (
    .a(inPlayerShiftM), .b(5'b11110), .eq(comparator_3_eq));  // open: gt, lt
  Pull_Resistor pull_resistor_3 (.node(pull_resistor_3_node));
  Pull_Resistor pull_resistor_4 (.node(comparator_1_eq));
  assign pull_resistor_3_node = comparator_1_eq ? 30'h3c078 : 30'bz;  // Controlled_Buffer controlled_buffer_1
  Pull_Resistor pull_resistor_5 (.node(pull_resistor_5_node));
  assign pull_resistor_5_node = comparator_1_eq ? 30'h3c078 : 30'bz;  // Controlled_Buffer controlled_buffer_2
  Pull_Resistor pull_resistor_6 (.node(pull_resistor_6_node));
  assign pull_resistor_6_node = comparator_1_eq ? 30'h79fff : 30'bz;  // Controlled_Buffer controlled_buffer_3
  Pull_Resistor pull_resistor_7 (.node(pull_resistor_7_node));
  assign pull_resistor_7_node = comparator_1_eq ? 30'h89242 : 30'bz;  // Controlled_Buffer controlled_buffer_4
  assign controlled_buffer_5_out = comparator_1_eq ? 30'hf9fff : 30'bz;  // Controlled_Buffer controlled_buffer_5
  Pull_Resistor pull_resistor_8 (.node(controlled_buffer_5_out));
  Pull_Resistor pull_resistor_9 (.node(pull_resistor_9_node));
  assign pull_resistor_9_node = comparator_1_eq ? 30'hf9fff : 30'bz;  // Controlled_Buffer controlled_buffer_6
  assign controlled_buffer_7_out = comparator_1_eq ? 30'h89242 : 30'bz;  // Controlled_Buffer controlled_buffer_7
  Pull_Resistor pull_resistor_10 (.node(controlled_buffer_7_out));
  assign controlled_buffer_8_out = comparator_1_eq ? 30'h79fff : 30'bz;  // Controlled_Buffer controlled_buffer_8
  Pull_Resistor pull_resistor_11 (.node(controlled_buffer_8_out));
  assign controlled_buffer_9_out = comparator_1_eq ? 30'h3c078 : 30'bz;  // Controlled_Buffer controlled_buffer_9
  Pull_Resistor pull_resistor_12 (.node(controlled_buffer_9_out));
  assign controlled_buffer_10_out = comparator_1_eq ? 30'h3c078 : 30'bz;  // Controlled_Buffer controlled_buffer_10
  Pull_Resistor pull_resistor_13 (.node(controlled_buffer_10_out));
  assign not_1_out = ~inputBackShiftM;  // NOT_Gate not_1, 5 bits wide
  Multiplexer #(.width(2), .disabled(0), .enable("false")) multiplexer_1 (
    .in0(inPlayerShiftD), .in1(outPlayerShiftD), .out(multiplexer_1_out), .sel(comparator_3_eq));
  Shifter #(.width(30)) shifter_1 (.in(pull_resistor_3_node), .\dist (inputBackShiftM), .out(shifter_1_out));
  Shifter #(.width(30)) shifter_2 (.in(pull_resistor_5_node), .\dist (inputBackShiftM), .out(shifter_2_out));
  Shifter #(.width(30)) shifter_3 (.in(pull_resistor_6_node), .\dist (inputBackShiftM), .out(shifter_3_out));
  Shifter #(.width(30)) shifter_4 (.in(pull_resistor_7_node), .\dist (inputBackShiftM), .out(shifter_4_out));
  Shifter #(.width(30)) shifter_5 (.in(controlled_buffer_5_out), .\dist (inputBackShiftM), .out(shifter_5_out));
  Shifter #(.width(30)) shifter_6 (.in(pull_resistor_9_node), .\dist (inputBackShiftM), .out(shifter_6_out));
  Shifter #(.width(30)) shifter_7 (.in(controlled_buffer_7_out), .\dist (inputBackShiftM), .out(shifter_7_out));
  Shifter #(.width(30)) shifter_8 (.in(controlled_buffer_8_out), .\dist (inputBackShiftM), .out(shifter_8_out));
  Shifter #(.width(30)) shifter_9 (.in(controlled_buffer_9_out), .\dist (inputBackShiftM), .out(shifter_9_out));
  Shifter #(.width(30)) shifter_10 (.in(controlled_buffer_10_out), .\dist (inputBackShiftM), .out(shifter_10_out));
  Adder #(.width(5)) adder_4 (.a(not_1_out), .b(5'b00001), .out(adder_4_out));  // open: cin, cout
  assign controlled_buffer_11_out = comparator_2_eq ? 30'h3c078 : 30'bz;  // Controlled_Buffer controlled_buffer_11
  Pull_Resistor pull_resistor_14 (.node(controlled_buffer_11_out));
  assign controlled_buffer_12_out = comparator_2_eq ? 30'h3c078 : 30'bz;  // Controlled_Buffer controlled_buffer_12
  Pull_Resistor pull_resistor_15 (.node(controlled_buffer_12_out));
  assign controlled_buffer_13_out = comparator_2_eq ? 30'h79fff : 30'bz;  // Controlled_Buffer controlled_buffer_13
  Pull_Resistor pull_resistor_16 (.node(controlled_buffer_13_out));
  Pull_Resistor pull_resistor_17 (.node(pull_resistor_17_node));
  assign pull_resistor_17_node = comparator_2_eq ? 30'h89242 : 30'bz;  // Controlled_Buffer controlled_buffer_14
  Pull_Resistor pull_resistor_18 (.node(pull_resistor_18_node));
  assign pull_resistor_18_node = comparator_2_eq ? 30'hf9fff : 30'bz;  // Controlled_Buffer controlled_buffer_15
  assign controlled_buffer_16_out = comparator_2_eq ? 30'hf9fff : 30'bz;  // Controlled_Buffer controlled_buffer_16
  Pull_Resistor pull_resistor_19 (.node(controlled_buffer_16_out));
  Pull_Resistor pull_resistor_20 (.node(pull_resistor_20_node));
  assign pull_resistor_20_node = comparator_2_eq ? 30'h89242 : 30'bz;  // Controlled_Buffer controlled_buffer_17
  assign controlled_buffer_18_out = comparator_2_eq ? 30'h79fff : 30'bz;  // Controlled_Buffer controlled_buffer_18
  Pull_Resistor pull_resistor_21 (.node(controlled_buffer_18_out));
  assign controlled_buffer_19_out = comparator_2_eq ? 30'h3c078 : 30'bz;  // Controlled_Buffer controlled_buffer_19
  Pull_Resistor pull_resistor_22 (.node(controlled_buffer_19_out));
  assign controlled_buffer_20_out = comparator_2_eq ? 30'h3c078 : 30'bz;  // Controlled_Buffer controlled_buffer_20
  Pull_Resistor pull_resistor_23 (.node(controlled_buffer_20_out));
  Pull_Resistor pull_resistor_24 (.node(comparator_2_eq));
  Comparator #(.width(2)) comparator_4 (.a(2'b00), .b(multiplexer_1_out), .eq(comparator_4_eq));  // open: gt, lt
  assign controlled_buffer_21_out = inFlag ? comparator_4_eq : 1'bz;  // Controlled_Buffer controlled_buffer_21
  Comparator #(.width(2)) comparator_5 (.a(2'b00), .b(adder_5_out), .eq(comparator_5_eq));  // open: gt, lt
  Adder #(.width(2)) adder_5 (.a(multiplexer_1_out), .b(2'b01), .out(adder_5_out));  // open: cin, cout
  assign toBackground = shifter_1_out | shifter_11_out;  // OR_Gate or_1, 30 bits wide
  Adder #(.width(5)) adder_6 (.a(5'b11110), .b(adder_4_out), .out(adder_6_out));  // open: cin, cout
  Shifter #(.width(30), .shift("lr")) shifter_11 (
    .in(controlled_buffer_11_out), .\dist (adder_6_out), .out(shifter_11_out));
  Shifter #(.width(30), .shift("lr")) shifter_12 (
    .in(controlled_buffer_12_out), .\dist (adder_6_out), .out(shifter_12_out));
  Shifter #(.width(30), .shift("lr")) shifter_13 (
    .in(controlled_buffer_13_out), .\dist (adder_6_out), .out(shifter_13_out));
  Shifter #(.width(30), .shift("lr")) shifter_14 (
    .in(pull_resistor_17_node), .\dist (adder_6_out), .out(shifter_14_out));
  Shifter #(.width(30), .shift("lr")) shifter_15 (
    .in(pull_resistor_18_node), .\dist (adder_6_out), .out(shifter_15_out));
  Shifter #(.width(30), .shift("lr")) shifter_16 (
    .in(controlled_buffer_16_out), .\dist (adder_6_out), .out(shifter_16_out));
  Shifter #(.width(30), .shift("lr")) shifter_17 (
    .in(pull_resistor_20_node), .\dist (adder_6_out), .out(shifter_17_out));
  Shifter #(.width(30), .shift("lr")) shifter_18 (
    .in(controlled_buffer_18_out), .\dist (adder_6_out), .out(shifter_18_out));
  Shifter #(.width(30), .shift("lr")) shifter_19 (
    .in(controlled_buffer_19_out), .\dist (adder_6_out), .out(shifter_19_out));
  Shifter #(.width(30), .shift("lr")) shifter_20 (
    .in(controlled_buffer_20_out), .\dist (adder_6_out), .out(shifter_20_out));
  assign toBackground_2 = shifter_2_out | shifter_12_out;  // OR_Gate or_2, 30 bits wide
  assign toBackground_3 = shifter_3_out | shifter_13_out;  // OR_Gate or_3, 30 bits wide
  assign toBackground_4 = shifter_4_out | shifter_14_out;  // OR_Gate or_4, 30 bits wide
  assign toBackground_5 = shifter_5_out | shifter_15_out;  // OR_Gate or_5, 30 bits wide
  assign toBackground_6 = shifter_6_out | shifter_16_out;  // OR_Gate or_6, 30 bits wide
  assign toBackground_7 = shifter_7_out | shifter_17_out;  // OR_Gate or_7, 30 bits wide
  assign toBackground_8 = shifter_8_out | shifter_18_out;  // OR_Gate or_8, 30 bits wide
  assign toBackground_9 = shifter_9_out | shifter_19_out;  // OR_Gate or_9, 30 bits wide
  assign toBackground_10 = shifter_10_out | shifter_20_out;  // OR_Gate or_10, 30 bits wide
  assign controlled_buffer_22_out = inFlag ? comparator_5_eq : 1'bz;  // Controlled_Buffer controlled_buffer_22
  Pull_Resistor pull_resistor_25 (.node(pull_resistor_25_node));
  Pull_Resistor pull_resistor_26 (.node(controlled_buffer_21_out));
  assign pull_resistor_25_node = controlled_buffer_21_out ? 30'h279 : 30'bz;  // Controlled_Buffer controlled_buffer_23
  Pull_Resistor pull_resistor_27 (.node(pull_resistor_27_node));
  assign pull_resistor_27_node = controlled_buffer_21_out ? 30'h231 : 30'bz;  // Controlled_Buffer controlled_buffer_24
  assign controlled_buffer_25_out = controlled_buffer_21_out ? 30'h279 : 30'bz;  // Controlled_Buffer controlled_buffer_25
  Pull_Resistor pull_resistor_28 (.node(controlled_buffer_25_out));
  Pull_Resistor pull_resistor_29 (.node(pull_resistor_29_node));
  assign pull_resistor_29_node = controlled_buffer_21_out ? 30'h3ff : 30'bz;  // Controlled_Buffer controlled_buffer_26
  Pull_Resistor pull_resistor_30 (.node(pull_resistor_30_node));
  assign pull_resistor_30_node = controlled_buffer_21_out ? 30'hfc : 30'bz;  // Controlled_Buffer controlled_buffer_27
  assign controlled_buffer_28_out = controlled_buffer_21_out ? 30'hfc : 30'bz;  // Controlled_Buffer controlled_buffer_28
  Pull_Resistor pull_resistor_31 (.node(controlled_buffer_28_out));
  assign controlled_buffer_29_out = controlled_buffer_21_out ? 30'h3ff : 30'bz;  // Controlled_Buffer controlled_buffer_29
  Pull_Resistor pull_resistor_32 (.node(controlled_buffer_29_out));
  Pull_Resistor pull_resistor_33 (.node(pull_resistor_33_node));
  assign pull_resistor_33_node = controlled_buffer_21_out ? 30'h279 : 30'bz;  // Controlled_Buffer controlled_buffer_30
  Pull_Resistor pull_resistor_34 (.node(pull_resistor_34_node));
  assign pull_resistor_34_node = controlled_buffer_21_out ? 30'h231 : 30'bz;  // Controlled_Buffer controlled_buffer_31
  assign controlled_buffer_32_out = controlled_buffer_21_out ? 30'h201 : 30'bz;  // Controlled_Buffer controlled_buffer_32
  Pull_Resistor pull_resistor_35 (.node(controlled_buffer_32_out));
  Shifter #(.width(30)) shifter_21 (.in(pull_resistor_25_node), .\dist (adder_3_out), .out(shifter_21_out));
  Shifter #(.width(30)) shifter_22 (.in(pull_resistor_27_node), .\dist (adder_3_out), .out(shifter_22_out));
  Shifter #(.width(30)) shifter_23 (.in(controlled_buffer_25_out), .\dist (adder_3_out), .out(shifter_23_out));
  Shifter #(.width(30)) shifter_24 (.in(pull_resistor_29_node), .\dist (adder_3_out), .out(shifter_24_out));
  Shifter #(.width(30)) shifter_25 (.in(pull_resistor_30_node), .\dist (adder_3_out), .out(shifter_25_out));
  Shifter #(.width(30)) shifter_26 (.in(controlled_buffer_28_out), .\dist (adder_3_out), .out(shifter_26_out));
  Shifter #(.width(30)) shifter_27 (.in(controlled_buffer_29_out), .\dist (adder_3_out), .out(shifter_27_out));
  Shifter #(.width(30)) shifter_28 (.in(pull_resistor_33_node), .\dist (adder_3_out), .out(shifter_28_out));
  Shifter #(.width(30)) shifter_29 (.in(pull_resistor_34_node), .\dist (adder_3_out), .out(shifter_29_out));
  Shifter #(.width(30)) shifter_30 (.in(controlled_buffer_32_out), .\dist (adder_3_out), .out(shifter_30_out));
  assign not_2_out = ~adder_3_out;  // NOT_Gate not_2, 5 bits wide
  Adder #(.width(5)) adder_7 (.a(not_2_out), .b(5'b00001), .out(adder_7_out));  // open: cin, cout
  Adder #(.width(5)) adder_8 (.a(5'b11110), .b(adder_7_out), .out(adder_8_out));  // open: cin, cout
  assign controlled_buffer_33_out = controlled_buffer_22_out ? 30'h279 : 30'bz;  // Controlled_Buffer controlled_buffer_33
  Pull_Resistor pull_resistor_36 (.node(controlled_buffer_33_out));
  Shifter #(.width(30), .shift("lr")) shifter_31 (
    .in(controlled_buffer_33_out), .\dist (adder_8_out), .out(shifter_31_out));
  assign controlled_buffer_34_out = controlled_buffer_22_out ? 30'h231 : 30'bz;  // Controlled_Buffer controlled_buffer_34
  Pull_Resistor pull_resistor_37 (.node(controlled_buffer_34_out));
  Shifter #(.width(30), .shift("lr")) shifter_32 (
    .in(controlled_buffer_34_out), .\dist (adder_8_out), .out(shifter_32_out));
  assign controlled_buffer_35_out = controlled_buffer_22_out ? 30'h279 : 30'bz;  // Controlled_Buffer controlled_buffer_35
  Pull_Resistor pull_resistor_38 (.node(controlled_buffer_35_out));
  Shifter #(.width(30), .shift("lr")) shifter_33 (
    .in(controlled_buffer_35_out), .\dist (adder_8_out), .out(shifter_33_out));
  assign controlled_buffer_36_out = controlled_buffer_22_out ? 30'h3ff : 30'bz;  // Controlled_Buffer controlled_buffer_36
  Pull_Resistor pull_resistor_39 (.node(controlled_buffer_36_out));
  Shifter #(.width(30), .shift("lr")) shifter_34 (
    .in(controlled_buffer_36_out), .\dist (adder_8_out), .out(shifter_34_out));
  Pull_Resistor pull_resistor_40 (.node(pull_resistor_40_node));
  assign pull_resistor_40_node = controlled_buffer_22_out ? 30'hfc : 30'bz;  // Controlled_Buffer controlled_buffer_37
  Shifter #(.width(30), .shift("lr")) shifter_35 (
    .in(pull_resistor_40_node), .\dist (adder_8_out), .out(shifter_35_out));
  Pull_Resistor pull_resistor_41 (.node(pull_resistor_41_node));
  assign pull_resistor_41_node = controlled_buffer_22_out ? 30'hfc : 30'bz;  // Controlled_Buffer controlled_buffer_38
  Shifter #(.width(30), .shift("lr")) shifter_36 (
    .in(pull_resistor_41_node), .\dist (adder_8_out), .out(shifter_36_out));
  assign controlled_buffer_39_out = controlled_buffer_22_out ? 30'h3ff : 30'bz;  // Controlled_Buffer controlled_buffer_39
  Pull_Resistor pull_resistor_42 (.node(controlled_buffer_39_out));
  Shifter #(.width(30), .shift("lr")) shifter_37 (
    .in(controlled_buffer_39_out), .\dist (adder_8_out), .out(shifter_37_out));
  Pull_Resistor pull_resistor_43 (.node(pull_resistor_43_node));
  assign pull_resistor_43_node = controlled_buffer_22_out ? 30'h279 : 30'bz;  // Controlled_Buffer controlled_buffer_40
  Shifter #(.width(30), .shift("lr")) shifter_38 (
    .in(pull_resistor_43_node), .\dist (adder_8_out), .out(shifter_38_out));
  assign controlled_buffer_41_out = controlled_buffer_22_out ? 30'h231 : 30'bz;  // Controlled_Buffer controlled_buffer_41
  Pull_Resistor pull_resistor_44 (.node(controlled_buffer_41_out));
  Shifter #(.width(30), .shift("lr")) shifter_39 (
    .in(controlled_buffer_41_out), .\dist (adder_8_out), .out(shifter_39_out));
  Pull_Resistor pull_resistor_45 (.node(pull_resistor_45_node));
  assign pull_resistor_45_node = controlled_buffer_22_out ? 30'h201 : 30'bz;  // Controlled_Buffer controlled_buffer_42
  Shifter #(.width(30), .shift("lr")) shifter_40 (
    .in(pull_resistor_45_node), .\dist (adder_8_out), .out(shifter_40_out));
  Pull_Resistor pull_resistor_46 (.node(controlled_buffer_22_out));
  assign toFront = shifter_21_out | shifter_31_out;  // OR_Gate or_11, 30 bits wide
  assign toFront_2 = shifter_22_out | shifter_32_out;  // OR_Gate or_12, 30 bits wide
  assign toFront_3 = shifter_23_out | shifter_33_out;  // OR_Gate or_13, 30 bits wide
  assign toFront_4 = shifter_24_out | shifter_34_out;  // OR_Gate or_14, 30 bits wide
  assign toFront_5 = shifter_25_out | shifter_35_out;  // OR_Gate or_15, 30 bits wide
  assign toFront_6 = shifter_26_out | shifter_36_out;  // OR_Gate or_16, 30 bits wide
  assign toFront_7 = shifter_27_out | shifter_37_out;  // OR_Gate or_17, 30 bits wide
  assign toFront_8 = shifter_28_out | shifter_38_out;  // OR_Gate or_18, 30 bits wide
  assign toFront_9 = shifter_29_out | shifter_39_out;  // OR_Gate or_19, 30 bits wide
  assign toFront_10 = shifter_30_out | shifter_40_out;  // OR_Gate or_20, 30 bits wide

  assign outFlag = inFlag;
  assign outPlayerShiftM = inPlayerShiftM;
  assign outputBackShiftM = inputBackShiftM;

  // Notes on the sheet:
  //   MAKE SHIFT BY NEXT MATRICE
  //   MAKE SHIFT IN CURRENT MATRICE
  //   MAKE SHIFT BY NEXT MATRICE
  //   MAKE SHIFT IN CURRENT MATRICE
endmodule

// shifter
module leftShifter (
  input  [2:0] shiftCounts,
  input  tactGen,
  input  reset,
  output [4:0] shiftM,
  output [1:0] shiftD
);

  wire and_1_out, and_2_out, comparator_1_lt, comparator_2_eq, comparator_3_eq, comparator_4_lt,
       comparator_5_eq, not_1_out, not_2_out, or_1_out, or_2_out;
  wire [1:0] undriven;
  wire [4:0] matricePos_q, pull_resistor_3_node;
  wire [6:2] undriven_2;

  Counter #(.width(5), .max('h1f)) matricePos (
    .Q(matricePos_q), .clk(tactGen), .clr(or_2_out));  // open: load, D, count, carry
  Pull_Resistor pull_resistor_1 (.node(tactGen));
  Shifter #(.width(5)) shifter_1 (.in(matricePos_q), .\dist (shiftCounts), .out(shiftM));
  Comparator #(.width(5), .mode("unsigned")) comparator_1 (
    .a(shiftM), .b(5'b11100), .lt(comparator_1_lt));  // open: gt, eq
  not not_1 (not_1_out, comparator_1_lt);
  Comparator #(.width(3), .mode("unsigned")) comparator_2 (
    .a(shiftCounts), .b(3'b010), .eq(comparator_2_eq));  // open: gt, lt
  Comparator #(.width(5), .mode("unsigned")) comparator_3 (
    .a(shiftM), .b(5'b11110), .eq(comparator_3_eq));  // open: gt, lt
  Comparator #(.width(3), .mode("unsigned")) comparator_4 (
    .a(shiftCounts), .b(3'b000), .lt(comparator_4_lt));  // open: gt, eq
  not not_2 (not_2_out, comparator_4_lt);
  and and_1 (and_1_out, not_1_out, comparator_2_eq);
  or or_1 (or_1_out, and_1_out, and_2_out);
  and and_2 (and_2_out, comparator_3_eq, not_2_out);
  or or_2 (or_2_out, or_1_out, reset);
  Comparator #(.width(2), .mode("unsigned")) comparator_5 (
    .a(undriven), .b(2'b10), .eq(comparator_5_eq));  // open: gt, lt
  Counter #(.width(2), .max('h3)) displayPos (.Q(shiftD), .clk(or_1_out), .clr(reset));  // open: load, D, count, carry
  Pull_Resistor pull_resistor_2 (.node(reset));
  Pull_Resistor pull_resistor_3 (.node(pull_resistor_3_node));
  assign pull_resistor_3_node = comparator_5_eq ? undriven_2 : 5'bz;  // Controlled_Buffer controlled_buffer_1
endmodule

module rightShifter (
  input  [1:0] shiftCounts,
  input  tactGen,
  input  reset,
  output [4:0] shiftM,
  output [1:0] shiftD
);

  wire comparator_1_eq, comparator_2_eq, comparator_3_eq, comparator_4_gt, comparator_5_eq, or_2_out;
  wire [1:0] displayPos_q, matricePos_q, not_2_out;
  wire [4:0] controlled_buffer_1_out, controlled_buffer_2_out, controlled_buffer_4_out, matricePos_q_2,
       not_1_out, or_1_out, pull_resistor_4_node;

  Pull_Resistor pull_resistor_1 (.node(tactGen));
  Counter #(.width(7), .max('h7f)) matricePos (
    .Q({matricePos_q_2, matricePos_q}), .clk(tactGen), .clr(or_2_out));  // open: load, D, count, carry
  Comparator #(.width(2), .mode("unsigned")) comparator_1 (
    .a(shiftCounts), .b(2'b00), .eq(comparator_1_eq));  // open: gt, lt
  Comparator #(.width(2), .mode("unsigned")) comparator_2 (
    .a(shiftCounts), .b(2'b01), .eq(comparator_2_eq));  // open: gt, lt
  Comparator #(.width(2), .mode("unsigned")) comparator_3 (
    .a(shiftCounts), .b(2'b10), .eq(comparator_3_eq));  // open: gt, lt
  Comparator #(.width(2), .mode("unsigned")) comparator_4 (
    .a(shiftCounts), .b(2'b10), .gt(comparator_4_gt));  // open: eq, lt
  assign controlled_buffer_1_out = comparator_1_eq ? {matricePos_q_2[2:0], matricePos_q} : 5'bz;  // Controlled_Buffer controlled_buffer_1
  Pull_Resistor pull_resistor_2 (.node(controlled_buffer_1_out));
  assign controlled_buffer_2_out = comparator_2_eq ? {matricePos_q_2[3:0], matricePos_q[1]} : 5'bz;  // Controlled_Buffer controlled_buffer_2
  Pull_Resistor pull_resistor_3 (.node(controlled_buffer_2_out));
  Pull_Resistor pull_resistor_4 (.node(pull_resistor_4_node));
  assign pull_resistor_4_node = comparator_3_eq ? matricePos_q_2 : 5'bz;  // Controlled_Buffer controlled_buffer_3
  assign controlled_buffer_4_out = comparator_4_gt ? matricePos_q_2 : 5'bz;  // Controlled_Buffer controlled_buffer_4
  Pull_Resistor pull_resistor_5 (.node(controlled_buffer_4_out));
  assign not_1_out = ~or_1_out;  // NOT_Gate not_1, 5 bits wide
  assign or_1_out = controlled_buffer_1_out | controlled_buffer_2_out | pull_resistor_4_node;  // OR_Gate or_1, 5 bits wide
  Comparator #(.width(5), .mode("unsigned")) comparator_5 (
    .a(or_1_out), .b(5'b11110), .eq(comparator_5_eq));  // open: gt, lt
  or or_2 (or_2_out, comparator_5_eq, reset);
  Adder #(.width(5)) adder_1 (.a(not_1_out), .b({5{1'b1}}), .out(shiftM));  // open: cin, cout
  Counter #(.width(2), .max('h3)) displayPos (
    .Q(displayPos_q), .clk(comparator_5_eq), .clr(reset));  // open: load, D, count, carry
  assign not_2_out = ~displayPos_q;  // NOT_Gate not_2, 2 bits wide
  Pull_Resistor pull_resistor_6 (.node(reset));
  Adder #(.width(2)) adder_2 (.a(not_2_out), .b(2'b01), .out(shiftD));  // open: cin, cout
endmodule

module oldCar (
  input  [1:0] matriceX,
  input  [1:0] inBackShiftD,
  input  [4:0] inputBackShiftM,
  input  inReset,
  input  [1:0] inPlayerShiftD,
  input  [4:0] inPlayerShiftM,
  input  [3:0] inPlayerY,
  input  [3:0] inY,
  output [29:0] toBackground,
  output [29:0] toBackground_2,
  output [29:0] toBackground_3,
  output [29:0] toBackground_4,
  output [1:0] nextMatriceX,
  output [29:0] toBackground_5,
  output [1:0] outBackShiftD,
  output [29:0] toBackground_6,
  output [29:0] toBackground_7,
  output [4:0] outputBackShiftM,
  output [29:0] toBackground_8,
  output [29:0] toBackground_9,
  output [29:0] toBackground_10,
  output outReset,
  output [1:0] outPlayerShiftD,
  output [4:0] outPlayerShiftM,
  output [3:0] outY,
  output [29:0] toFront,
  output [3:0] outPlayerY,
  output [29:0] toFront_2,
  output [29:0] toFront_3,
  output [29:0] toFront_4,
  output [29:0] toFront_5,
  output [29:0] toFront_6,
  output [29:0] toFront_7,
  output [29:0] toFront_8,
  output [29:0] toFront_9,
  output [29:0] toFront_10
);

  wire and_1_out, and_2_out, and_3_out, and_4_out, comparator_1_eq, comparator_2_eq, comparator_3_gt,
       comparator_5_eq, comparator_6_gt, comparator_7_gt, comparator_8_eq, comparator_9_eq, comparator_10_gt,
       comparator_11_gt, comparator_12_eq, comparator_13_eq, comparator_14_eq, comparator_15_eq,
       comparator_16_eq, comparator_17_eq, comparator_18_eq, controlled_buffer_1_out,
       controlled_buffer_2_out, controlled_buffer_33_out, controlled_buffer_34_out, or_1_out,
       pull_resistor_1_node;
  wire [1:0] adder_3_out, adder_6_out, adder_16_out, multiplexer_1_out;
  wire [4:0] adder_14_out, adder_15_out, adder_17_out, adder_18_out, adder_19_out, adder_20_out,
       adder_21_out, not_3_out, not_4_out, not_5_out;
  wire [6:0] adder_1_out, adder_2_out, adder_4_out, adder_5_out, adder_7_out, adder_8_out, adder_10_out,
       adder_11_out, bit_extender_1_out, bit_extender_2_out, bit_extender_3_out, bit_extender_4_out,
       bit_extender_5_out, bit_extender_6_out, bit_extender_7_out, bit_extender_8_out, bit_extender_9_out,
       bit_extender_10_out, bit_extender_11_out, bit_extender_12_out, not_1_out, not_2_out;
  wire [29:0] controlled_buffer_3_out, controlled_buffer_5_out, controlled_buffer_6_out,
       controlled_buffer_9_out, controlled_buffer_11_out, controlled_buffer_12_out, controlled_buffer_18_out,
       controlled_buffer_20_out, controlled_buffer_21_out, controlled_buffer_22_out,
       controlled_buffer_23_out, controlled_buffer_24_out, controlled_buffer_25_out,
       controlled_buffer_28_out, controlled_buffer_30_out, controlled_buffer_31_out,
       controlled_buffer_32_out, controlled_buffer_35_out, controlled_buffer_37_out,
       controlled_buffer_38_out, controlled_buffer_41_out, controlled_buffer_46_out,
       controlled_buffer_48_out, controlled_buffer_50_out, controlled_buffer_51_out,
       controlled_buffer_52_out, controlled_buffer_53_out, controlled_buffer_56_out,
       controlled_buffer_57_out, controlled_buffer_58_out, controlled_buffer_59_out,
       controlled_buffer_62_out, controlled_buffer_64_out, or_3_out, or_4_out, or_5_out, or_6_out, or_7_out,
       or_8_out, or_9_out, or_10_out, or_11_out, or_12_out, or_13_out, or_14_out, or_15_out, or_16_out,
       or_17_out, or_18_out, or_19_out, or_20_out, or_24_out, or_25_out, pull_resistor_7_node,
       pull_resistor_10_node, pull_resistor_11_node, pull_resistor_13_node, pull_resistor_16_node,
       pull_resistor_18_node, pull_resistor_19_node, pull_resistor_20_node, pull_resistor_21_node,
       pull_resistor_23_node, pull_resistor_30_node, pull_resistor_31_node, pull_resistor_33_node,
       pull_resistor_40_node, pull_resistor_43_node, pull_resistor_44_node, pull_resistor_46_node,
       pull_resistor_47_node, pull_resistor_48_node, pull_resistor_49_node, pull_resistor_52_node,
       pull_resistor_54_node, pull_resistor_59_node, pull_resistor_61_node, pull_resistor_66_node,
       pull_resistor_67_node, pull_resistor_69_node, shifter_1_out, shifter_2_out, shifter_3_out,
       shifter_4_out, shifter_5_out, shifter_6_out, shifter_7_out, shifter_8_out, shifter_9_out,
       shifter_10_out, shifter_11_out, shifter_12_out, shifter_13_out, shifter_14_out, shifter_15_out,
       shifter_16_out, shifter_17_out, shifter_18_out, shifter_19_out, shifter_20_out, shifter_21_out,
       shifter_22_out, shifter_23_out, shifter_24_out, shifter_25_out, shifter_26_out, shifter_27_out,
       shifter_28_out, shifter_29_out, shifter_30_out, shifter_31_out, shifter_32_out, shifter_33_out,
       shifter_34_out, shifter_35_out, shifter_36_out, shifter_37_out, shifter_38_out, shifter_39_out,
       shifter_40_out, shifter_41_out, shifter_42_out, shifter_43_out, shifter_44_out, shifter_45_out,
       shifter_46_out, shifter_47_out, shifter_48_out, shifter_49_out, shifter_50_out, shifter_51_out,
       shifter_52_out, shifter_53_out, shifter_54_out, shifter_55_out, shifter_56_out, shifter_57_out,
       shifter_58_out, shifter_59_out, shifter_60_out;

  // Probe on adder_1_out
  assign bit_extender_1_out = {{2{1'b0}}, 5'b01010};  // Bit_Extender bit_extender_1
  Adder #(.width(7)) adder_1 (.a(bit_extender_1_out), .b(bit_extender_2_out), .out(adder_1_out));  // open: cin, cout
  assign bit_extender_2_out = {{2{1'b0}}, inPlayerShiftM};  // Bit_Extender bit_extender_2
  Adder #(.width(7)) adder_2 (.a(7'b0000001), .b(not_1_out), .out(adder_2_out));  // open: cin, cout
  assign bit_extender_3_out = {{2{1'b0}}, inputBackShiftM};  // Bit_Extender bit_extender_3
  assign not_1_out = ~bit_extender_3_out;  // NOT_Gate not_1, 7 bits wide
  Adder #(.width(2)) adder_3 (.a(inPlayerShiftD), .b(2'b01), .out(adder_3_out));  // open: cin, cout
  // Probe on adder_4_out
  assign bit_extender_4_out = {{2{1'b0}}, 5'b10100};  // Bit_Extender bit_extender_4
  Adder #(.width(7)) adder_4 (.a(bit_extender_4_out), .b(bit_extender_5_out), .out(adder_4_out));  // open: cin, cout
  assign bit_extender_5_out = {{2{1'b0}}, inputBackShiftM};  // Bit_Extender bit_extender_5
  Adder #(.width(7)) adder_5 (.a(7'b0000001), .b(not_2_out), .out(adder_5_out));  // open: cin, cout
  assign bit_extender_6_out = {{2{1'b0}}, inPlayerShiftM};  // Bit_Extender bit_extender_6
  assign not_2_out = ~bit_extender_6_out;  // NOT_Gate not_2, 7 bits wide
  Adder #(.width(2)) adder_6 (.a(inBackShiftD), .b(2'b01), .out(adder_6_out));  // open: cin, cout
  assign bit_extender_7_out = {{2{1'b0}}, 5'b01010};  // Bit_Extender bit_extender_7
  Adder #(.width(7)) adder_7 (.a(bit_extender_7_out), .b(bit_extender_8_out), .out(adder_7_out));  // open: cin, cout
  assign bit_extender_8_out = {{2{1'b0}}, inPlayerShiftM};  // Bit_Extender bit_extender_8
  assign bit_extender_9_out = {{2{1'b0}}, inputBackShiftM};  // Bit_Extender bit_extender_9
  assign bit_extender_10_out = {{2{1'b0}}, 5'b10100};  // Bit_Extender bit_extender_10
  Adder #(.width(7)) adder_8 (.a(bit_extender_10_out), .b(bit_extender_11_out), .out(adder_8_out));  // open: cin, cout
  assign bit_extender_11_out = {{2{1'b0}}, inputBackShiftM};  // Bit_Extender bit_extender_11
  assign bit_extender_12_out = {{2{1'b0}}, inPlayerShiftM};  // Bit_Extender bit_extender_12
  Adder #(.width(4)) adder_9 (.a(4'b0001), .b(inY), .out(outY));  // open: cin, cout
  // Probe on adder_10_out
  // Probe on adder_2_out
  Adder #(.width(7)) adder_10 (.a(adder_1_out), .b(adder_2_out), .out(adder_10_out));  // open: cin, cout
  Comparator #(.width(2), .mode("unsigned")) comparator_1 (
    .a(inBackShiftD), .b(adder_3_out), .eq(comparator_1_eq));  // open: gt, lt
  // Probe on adder_5_out
  // Probe on adder_11_out
  Adder #(.width(7)) adder_11 (.a(adder_4_out), .b(adder_5_out), .out(adder_11_out));  // open: cin, cout
  Comparator #(.width(2), .mode("unsigned")) comparator_2 (
    .a(inPlayerShiftD), .b(adder_6_out), .eq(comparator_2_eq));  // open: gt, lt
  Comparator #(.width(7)) comparator_3 (.a(adder_7_out), .b(bit_extender_9_out), .gt(comparator_3_gt));  // open: eq, lt
  Pull_Resistor #(.pull(1)) pull_resistor_1 (.node(pull_resistor_1_node));
  Comparator #(.width(7)) comparator_4 (.a(7'b0011110), .b(adder_7_out));  // open: gt, eq, lt
  Comparator #(.width(2), .mode("unsigned")) comparator_5 (
    .a(inBackShiftD), .b(inPlayerShiftD), .eq(comparator_5_eq));  // open: gt, lt
  Comparator #(.width(7)) comparator_6 (
    .a(adder_8_out), .b(bit_extender_12_out), .gt(comparator_6_gt));  // open: eq, lt
  Comparator #(.width(7)) comparator_7 (.a(7'b0011110), .b(adder_8_out), .gt(comparator_7_gt));  // open: eq, lt
  Comparator #(.width(2), .mode("unsigned")) comparator_8 (
    .a(inBackShiftD), .b(inPlayerShiftD), .eq(comparator_8_eq));  // open: gt, lt
  Comparator #(.width(4)) comparator_9 (.a(inPlayerY), .b(inY), .eq(comparator_9_eq));  // open: gt, lt
  Pull_Resistor pull_resistor_2 (.node(comparator_9_eq));
  and and_1 (and_1_out, comparator_10_gt, comparator_1_eq);
  Comparator #(.width(7)) comparator_10 (.a(adder_10_out), .b(7'b0011110), .gt(comparator_10_gt));  // open: eq, lt
  and and_2 (and_2_out, comparator_11_gt, comparator_2_eq);
  Comparator #(.width(7)) comparator_11 (.a(adder_11_out), .b(7'b0011110), .gt(comparator_11_gt));  // open: eq, lt
  and and_3 (and_3_out, comparator_3_gt, comparator_5_eq, pull_resistor_1_node);
  and and_4 (and_4_out, comparator_6_gt, comparator_8_eq, comparator_7_gt);
  or or_1 (or_1_out, and_1_out, and_2_out, and_3_out, and_4_out);
  or or_2 (outReset, or_1_out, inReset);
  Adder #(.width(2)) adder_12 (.a(inPlayerShiftD), .b(2'b01), .out(outPlayerShiftD));  // open: cin, cout
  Pull_Resistor pull_resistor_3 (.node(inPlayerShiftM));
  assign controlled_buffer_1_out = comparator_9_eq ? comparator_12_eq : 1'bz;  // Controlled_Buffer controlled_buffer_1
  Comparator #(.width(2)) comparator_12 (.a(outPlayerShiftD), .b(matriceX), .eq(comparator_12_eq));  // open: gt, lt
  Adder #(.width(2)) adder_13 (.a(inBackShiftD), .b(2'b01), .out(outBackShiftD));  // open: cin, cout
  Pull_Resistor pull_resistor_4 (.node(inputBackShiftM));
  Comparator #(.width(2)) comparator_13 (.a(matriceX), .b(inPlayerShiftD), .eq(comparator_13_eq));  // open: gt, lt
  assign controlled_buffer_2_out = comparator_9_eq ? comparator_13_eq : 1'bz;  // Controlled_Buffer controlled_buffer_2
  Comparator #(.width(2)) comparator_14 (.a(matriceX), .b(inBackShiftD), .eq(comparator_14_eq));  // open: gt, lt
  Comparator #(.width(2)) comparator_15 (.a(outBackShiftD), .b(matriceX), .eq(comparator_15_eq));  // open: gt, lt
  Adder #(.width(5)) adder_14 (.a(inPlayerShiftM), .b(5'b00001), .out(adder_14_out));  // open: cin, cout
  Comparator #(.width(5), .mode("unsigned")) comparator_16 (
    .a(inPlayerShiftM), .b(5'b11110), .eq(comparator_16_eq));  // open: gt, lt
  Pull_Resistor pull_resistor_5 (.node(comparator_14_eq));
  assign controlled_buffer_3_out = comparator_14_eq ? 30'h3c078 : 30'bz;  // Controlled_Buffer controlled_buffer_3
  Pull_Resistor pull_resistor_6 (.node(controlled_buffer_3_out));
  Pull_Resistor pull_resistor_7 (.node(pull_resistor_7_node));
  assign pull_resistor_7_node = comparator_14_eq ? 30'h3c078 : 30'bz;  // Controlled_Buffer controlled_buffer_4
  assign controlled_buffer_5_out = comparator_14_eq ? 30'h79fff : 30'bz;  // Controlled_Buffer controlled_buffer_5
  Pull_Resistor pull_resistor_8 (.node(controlled_buffer_5_out));
  assign controlled_buffer_6_out = comparator_14_eq ? 30'h89242 : 30'bz;  // Controlled_Buffer controlled_buffer_6
  Pull_Resistor pull_resistor_9 (.node(controlled_buffer_6_out));
  Pull_Resistor pull_resistor_10 (.node(pull_resistor_10_node));
  assign pull_resistor_10_node = comparator_14_eq ? 30'hf9fff : 30'bz;  // Controlled_Buffer controlled_buffer_7
  Pull_Resistor pull_resistor_11 (.node(pull_resistor_11_node));
  assign pull_resistor_11_node = comparator_14_eq ? 30'hf9fff : 30'bz;  // Controlled_Buffer controlled_buffer_8
  assign controlled_buffer_9_out = comparator_14_eq ? 30'h89242 : 30'bz;  // Controlled_Buffer controlled_buffer_9
  Pull_Resistor pull_resistor_12 (.node(controlled_buffer_9_out));
  Pull_Resistor pull_resistor_13 (.node(pull_resistor_13_node));
  assign pull_resistor_13_node = comparator_14_eq ? 30'h79fff : 30'bz;  // Controlled_Buffer controlled_buffer_10
  assign controlled_buffer_11_out = comparator_14_eq ? 30'h3c078 : 30'bz;  // Controlled_Buffer controlled_buffer_11
  Pull_Resistor pull_resistor_14 (.node(controlled_buffer_11_out));
  assign controlled_buffer_12_out = comparator_14_eq ? 30'h3c078 : 30'bz;  // Controlled_Buffer controlled_buffer_12
  Pull_Resistor pull_resistor_15 (.node(controlled_buffer_12_out));
  Shifter #(.width(30)) shifter_1 (.in(controlled_buffer_3_out), .\dist (inputBackShiftM), .out(shifter_1_out));
  Shifter #(.width(30)) shifter_2 (.in(pull_resistor_7_node), .\dist (inputBackShiftM), .out(shifter_2_out));
  Shifter #(.width(30)) shifter_3 (.in(controlled_buffer_5_out), .\dist (inputBackShiftM), .out(shifter_3_out));
  Shifter #(.width(30)) shifter_4 (.in(controlled_buffer_6_out), .\dist (inputBackShiftM), .out(shifter_4_out));
  Shifter #(.width(30)) shifter_5 (.in(pull_resistor_10_node), .\dist (inputBackShiftM), .out(shifter_5_out));
  Shifter #(.width(30)) shifter_6 (.in(pull_resistor_11_node), .\dist (inputBackShiftM), .out(shifter_6_out));
  Shifter #(.width(30)) shifter_7 (.in(controlled_buffer_9_out), .\dist (inputBackShiftM), .out(shifter_7_out));
  Shifter #(.width(30)) shifter_8 (.in(pull_resistor_13_node), .\dist (inputBackShiftM), .out(shifter_8_out));
  Shifter #(.width(30)) shifter_9 (.in(controlled_buffer_11_out), .\dist (inputBackShiftM), .out(shifter_9_out));
  Shifter #(.width(30)) shifter_10 (.in(controlled_buffer_12_out), .\dist (inputBackShiftM), .out(shifter_10_out));
  assign not_3_out = ~inputBackShiftM;  // NOT_Gate not_3, 5 bits wide
  Adder #(.width(5)) adder_15 (.a(not_3_out), .b(5'b00001), .out(adder_15_out));  // open: cin, cout
  Pull_Resistor pull_resistor_16 (.node(pull_resistor_16_node));
  assign pull_resistor_16_node = controlled_buffer_2_out ? 30'h279 : 30'bz;  // Controlled_Buffer controlled_buffer_13
  Pull_Resistor pull_resistor_17 (.node(controlled_buffer_2_out));
  Pull_Resistor pull_resistor_18 (.node(pull_resistor_18_node));
  assign pull_resistor_18_node = controlled_buffer_2_out ? 30'h231 : 30'bz;  // Controlled_Buffer controlled_buffer_14
  Pull_Resistor pull_resistor_19 (.node(pull_resistor_19_node));
  assign pull_resistor_19_node = controlled_buffer_2_out ? 30'h279 : 30'bz;  // Controlled_Buffer controlled_buffer_15
  Pull_Resistor pull_resistor_20 (.node(pull_resistor_20_node));
  assign pull_resistor_20_node = controlled_buffer_2_out ? 30'h3ff : 30'bz;  // Controlled_Buffer controlled_buffer_16
  Pull_Resistor pull_resistor_21 (.node(pull_resistor_21_node));
  assign pull_resistor_21_node = controlled_buffer_2_out ? 30'hfc : 30'bz;  // Controlled_Buffer controlled_buffer_17
  assign controlled_buffer_18_out = controlled_buffer_2_out ? 30'hfc : 30'bz;  // Controlled_Buffer controlled_buffer_18
  Pull_Resistor pull_resistor_22 (.node(controlled_buffer_18_out));
  Pull_Resistor pull_resistor_23 (.node(pull_resistor_23_node));
  assign pull_resistor_23_node = controlled_buffer_2_out ? 30'h3ff : 30'bz;  // Controlled_Buffer controlled_buffer_19
  assign controlled_buffer_20_out = controlled_buffer_2_out ? 30'h279 : 30'bz;  // Controlled_Buffer controlled_buffer_20
  Pull_Resistor pull_resistor_24 (.node(controlled_buffer_20_out));
  assign controlled_buffer_21_out = controlled_buffer_2_out ? 30'h231 : 30'bz;  // Controlled_Buffer controlled_buffer_21
  Pull_Resistor pull_resistor_25 (.node(controlled_buffer_21_out));
  assign controlled_buffer_22_out = controlled_buffer_2_out ? 30'h201 : 30'bz;  // Controlled_Buffer controlled_buffer_22
  Pull_Resistor pull_resistor_26 (.node(controlled_buffer_22_out));
  Comparator #(.width(2)) comparator_17 (.a(matriceX), .b(multiplexer_1_out), .eq(comparator_17_eq));  // open: gt, lt
  Multiplexer #(.width(2), .disabled(0), .enable("false")) multiplexer_1 (
    .in0(inPlayerShiftD), .in1(outPlayerShiftD), .out(multiplexer_1_out), .sel(comparator_16_eq));
  Adder #(.width(2)) adder_16 (.a(multiplexer_1_out), .b(2'b01), .out(adder_16_out));  // open: cin, cout
  Adder #(.width(5)) adder_17 (.a(5'b11110), .b(adder_15_out), .out(adder_17_out));  // open: cin, cout
  assign controlled_buffer_23_out = comparator_15_eq ? 30'h3c078 : 30'bz;  // Controlled_Buffer controlled_buffer_23
  Pull_Resistor pull_resistor_27 (.node(controlled_buffer_23_out));
  Shifter #(.width(30), .shift("lr")) shifter_11 (
    .in(controlled_buffer_23_out), .\dist (adder_17_out), .out(shifter_11_out));
  assign controlled_buffer_24_out = comparator_15_eq ? 30'h3c078 : 30'bz;  // Controlled_Buffer controlled_buffer_24
  Pull_Resistor pull_resistor_28 (.node(controlled_buffer_24_out));
  Shifter #(.width(30), .shift("lr")) shifter_12 (
    .in(controlled_buffer_24_out), .\dist (adder_17_out), .out(shifter_12_out));
  assign controlled_buffer_25_out = comparator_15_eq ? 30'h79fff : 30'bz;  // Controlled_Buffer controlled_buffer_25
  Pull_Resistor pull_resistor_29 (.node(controlled_buffer_25_out));
  Shifter #(.width(30), .shift("lr")) shifter_13 (
    .in(controlled_buffer_25_out), .\dist (adder_17_out), .out(shifter_13_out));
  Pull_Resistor pull_resistor_30 (.node(pull_resistor_30_node));
  assign pull_resistor_30_node = comparator_15_eq ? 30'h89242 : 30'bz;  // Controlled_Buffer controlled_buffer_26
  Shifter #(.width(30), .shift("lr")) shifter_14 (
    .in(pull_resistor_30_node), .\dist (adder_17_out), .out(shifter_14_out));
  Pull_Resistor pull_resistor_31 (.node(pull_resistor_31_node));
  assign pull_resistor_31_node = comparator_15_eq ? 30'hf9fff : 30'bz;  // Controlled_Buffer controlled_buffer_27
  Shifter #(.width(30), .shift("lr")) shifter_15 (
    .in(pull_resistor_31_node), .\dist (adder_17_out), .out(shifter_15_out));
  assign controlled_buffer_28_out = comparator_15_eq ? 30'hf9fff : 30'bz;  // Controlled_Buffer controlled_buffer_28
  Pull_Resistor pull_resistor_32 (.node(controlled_buffer_28_out));
  Shifter #(.width(30), .shift("lr")) shifter_16 (
    .in(controlled_buffer_28_out), .\dist (adder_17_out), .out(shifter_16_out));
  Pull_Resistor pull_resistor_33 (.node(pull_resistor_33_node));
  assign pull_resistor_33_node = comparator_15_eq ? 30'h89242 : 30'bz;  // Controlled_Buffer controlled_buffer_29
  Shifter #(.width(30), .shift("lr")) shifter_17 (
    .in(pull_resistor_33_node), .\dist (adder_17_out), .out(shifter_17_out));
  assign controlled_buffer_30_out = comparator_15_eq ? 30'h79fff : 30'bz;  // Controlled_Buffer controlled_buffer_30
  Pull_Resistor pull_resistor_34 (.node(controlled_buffer_30_out));
  Shifter #(.width(30), .shift("lr")) shifter_18 (
    .in(controlled_buffer_30_out), .\dist (adder_17_out), .out(shifter_18_out));
  assign controlled_buffer_31_out = comparator_15_eq ? 30'h3c078 : 30'bz;  // Controlled_Buffer controlled_buffer_31
  Pull_Resistor pull_resistor_35 (.node(controlled_buffer_31_out));
  Shifter #(.width(30), .shift("lr")) shifter_19 (
    .in(controlled_buffer_31_out), .\dist (adder_17_out), .out(shifter_19_out));
  assign controlled_buffer_32_out = comparator_15_eq ? 30'h3c078 : 30'bz;  // Controlled_Buffer controlled_buffer_32
  Pull_Resistor pull_resistor_36 (.node(controlled_buffer_32_out));
  Shifter #(.width(30), .shift("lr")) shifter_20 (
    .in(controlled_buffer_32_out), .\dist (adder_17_out), .out(shifter_20_out));
  Pull_Resistor pull_resistor_37 (.node(comparator_15_eq));
  Shifter #(.width(30)) shifter_21 (.in(pull_resistor_16_node), .\dist (inPlayerShiftM), .out(shifter_21_out));
  Shifter #(.width(30)) shifter_22 (.in(pull_resistor_18_node), .\dist (inPlayerShiftM), .out(shifter_22_out));
  Shifter #(.width(30)) shifter_23 (.in(pull_resistor_19_node), .\dist (inPlayerShiftM), .out(shifter_23_out));
  Shifter #(.width(30)) shifter_24 (.in(pull_resistor_20_node), .\dist (inPlayerShiftM), .out(shifter_24_out));
  Shifter #(.width(30)) shifter_25 (.in(pull_resistor_21_node), .\dist (inPlayerShiftM), .out(shifter_25_out));
  Shifter #(.width(30)) shifter_26 (.in(controlled_buffer_18_out), .\dist (inPlayerShiftM), .out(shifter_26_out));
  Shifter #(.width(30)) shifter_27 (.in(pull_resistor_23_node), .\dist (inPlayerShiftM), .out(shifter_27_out));
  Shifter #(.width(30)) shifter_28 (.in(controlled_buffer_20_out), .\dist (inPlayerShiftM), .out(shifter_28_out));
  Shifter #(.width(30)) shifter_29 (.in(controlled_buffer_21_out), .\dist (inPlayerShiftM), .out(shifter_29_out));
  Shifter #(.width(30)) shifter_30 (.in(controlled_buffer_22_out), .\dist (inPlayerShiftM), .out(shifter_30_out));
  assign not_4_out = ~inPlayerShiftM;  // NOT_Gate not_4, 5 bits wide
  Adder #(.width(5)) adder_18 (.a(not_4_out), .b(5'b00001), .out(adder_18_out));  // open: cin, cout
  Pull_Resistor pull_resistor_38 (.node(controlled_buffer_1_out));
  assign controlled_buffer_33_out = comparator_9_eq ? comparator_17_eq : 1'bz;  // Controlled_Buffer controlled_buffer_33
  Comparator #(.width(2)) comparator_18 (.a(matriceX), .b(adder_16_out), .eq(comparator_18_eq));  // open: gt, lt
  assign controlled_buffer_34_out = comparator_9_eq ? comparator_18_eq : 1'bz;  // Controlled_Buffer controlled_buffer_34
  assign or_3_out = shifter_1_out | shifter_11_out;  // OR_Gate or_3, 30 bits wide
  assign or_4_out = shifter_2_out | shifter_12_out;  // OR_Gate or_4, 30 bits wide
  assign or_5_out = shifter_3_out | shifter_13_out;  // OR_Gate or_5, 30 bits wide
  assign or_6_out = shifter_4_out | shifter_14_out;  // OR_Gate or_6, 30 bits wide
  assign or_7_out = shifter_5_out | shifter_15_out;  // OR_Gate or_7, 30 bits wide
  assign or_8_out = shifter_6_out | shifter_16_out;  // OR_Gate or_8, 30 bits wide
  Adder #(.width(5)) adder_19 (.a(5'b11110), .b(adder_18_out), .out(adder_19_out));  // open: cin, cout
  assign controlled_buffer_35_out = controlled_buffer_1_out ? 30'h279 : 30'bz;  // Controlled_Buffer controlled_buffer_35
  Pull_Resistor pull_resistor_39 (.node(controlled_buffer_35_out));
  Shifter #(.width(30), .shift("lr")) shifter_31 (
    .in(controlled_buffer_35_out), .\dist (adder_19_out), .out(shifter_31_out));
  Pull_Resistor pull_resistor_40 (.node(pull_resistor_40_node));
  assign pull_resistor_40_node = controlled_buffer_1_out ? 30'h231 : 30'bz;  // Controlled_Buffer controlled_buffer_36
  Shifter #(.width(30), .shift("lr")) shifter_32 (
    .in(pull_resistor_40_node), .\dist (adder_19_out), .out(shifter_32_out));
  assign controlled_buffer_37_out = controlled_buffer_1_out ? 30'h279 : 30'bz;  // Controlled_Buffer controlled_buffer_37
  Pull_Resistor pull_resistor_41 (.node(controlled_buffer_37_out));
  Shifter #(.width(30), .shift("lr")) shifter_33 (
    .in(controlled_buffer_37_out), .\dist (adder_19_out), .out(shifter_33_out));
  assign controlled_buffer_38_out = controlled_buffer_1_out ? 30'h3ff : 30'bz;  // Controlled_Buffer controlled_buffer_38
  Pull_Resistor pull_resistor_42 (.node(controlled_buffer_38_out));
  Shifter #(.width(30), .shift("lr")) shifter_34 (
    .in(controlled_buffer_38_out), .\dist (adder_19_out), .out(shifter_34_out));
  Pull_Resistor pull_resistor_43 (.node(pull_resistor_43_node));
  assign pull_resistor_43_node = controlled_buffer_1_out ? 30'hfc : 30'bz;  // Controlled_Buffer controlled_buffer_39
  Shifter #(.width(30), .shift("lr")) shifter_35 (
    .in(pull_resistor_43_node), .\dist (adder_19_out), .out(shifter_35_out));
  Pull_Resistor pull_resistor_44 (.node(pull_resistor_44_node));
  assign pull_resistor_44_node = controlled_buffer_1_out ? 30'hfc : 30'bz;  // Controlled_Buffer controlled_buffer_40
  Shifter #(.width(30), .shift("lr")) shifter_36 (
    .in(pull_resistor_44_node), .\dist (adder_19_out), .out(shifter_36_out));
  assign controlled_buffer_41_out = controlled_buffer_1_out ? 30'h3ff : 30'bz;  // Controlled_Buffer controlled_buffer_41
  Pull_Resistor pull_resistor_45 (.node(controlled_buffer_41_out));
  Shifter #(.width(30), .shift("lr")) shifter_37 (
    .in(controlled_buffer_41_out), .\dist (adder_19_out), .out(shifter_37_out));
  Pull_Resistor pull_resistor_46 (.node(pull_resistor_46_node));
  assign pull_resistor_46_node = controlled_buffer_1_out ? 30'h279 : 30'bz;  // Controlled_Buffer controlled_buffer_42
  Shifter #(.width(30), .shift("lr")) shifter_38 (
    .in(pull_resistor_46_node), .\dist (adder_19_out), .out(shifter_38_out));
  Pull_Resistor pull_resistor_47 (.node(pull_resistor_47_node));
  assign pull_resistor_47_node = controlled_buffer_1_out ? 30'h231 : 30'bz;  // Controlled_Buffer controlled_buffer_43
  Shifter #(.width(30), .shift("lr")) shifter_39 (
    .in(pull_resistor_47_node), .\dist (adder_19_out), .out(shifter_39_out));
  Pull_Resistor pull_resistor_48 (.node(pull_resistor_48_node));
  assign pull_resistor_48_node = controlled_buffer_1_out ? 30'h201 : 30'bz;  // Controlled_Buffer controlled_buffer_44
  Shifter #(.width(30), .shift("lr")) shifter_40 (
    .in(pull_resistor_48_node), .\dist (adder_19_out), .out(shifter_40_out));
  assign or_9_out = shifter_7_out | shifter_17_out;  // OR_Gate or_9, 30 bits wide
  assign or_10_out = shifter_8_out | shifter_18_out;  // OR_Gate or_10, 30 bits wide
  assign or_11_out = shifter_9_out | shifter_19_out;  // OR_Gate or_11, 30 bits wide
  assign or_12_out = shifter_10_out | shifter_20_out;  // OR_Gate or_12, 30 bits wide
  assign or_13_out = shifter_21_out | shifter_31_out;  // OR_Gate or_13, 30 bits wide
  assign or_14_out = shifter_22_out | shifter_32_out;  // OR_Gate or_14, 30 bits wide
  assign or_15_out = shifter_23_out | shifter_33_out;  // OR_Gate or_15, 30 bits wide
  assign or_16_out = shifter_24_out | shifter_34_out;  // OR_Gate or_16, 30 bits wide
  assign or_17_out = shifter_25_out | shifter_35_out;  // OR_Gate or_17, 30 bits wide
  assign or_18_out = shifter_26_out | shifter_36_out;  // OR_Gate or_18, 30 bits wide
  assign or_19_out = shifter_27_out | shifter_37_out;  // OR_Gate or_19, 30 bits wide
  assign or_20_out = shifter_28_out | shifter_38_out;  // OR_Gate or_20, 30 bits wide
  assign toBackground_8 = or_10_out | or_20_out;  // OR_Gate or_21, 30 bits wide
  assign toBackground_9 = or_11_out | or_24_out;  // OR_Gate or_22, 30 bits wide
  assign toBackground_10 = or_12_out | or_25_out;  // OR_Gate or_23, 30 bits wide
  assign or_24_out = shifter_29_out | shifter_39_out;  // OR_Gate or_24, 30 bits wide
  assign or_25_out = shifter_30_out | shifter_40_out;  // OR_Gate or_25, 30 bits wide
  assign toBackground_5 = or_7_out | or_17_out;  // OR_Gate or_26, 30 bits wide
  assign toBackground_6 = or_8_out | or_18_out;  // OR_Gate or_27, 30 bits wide
  assign toBackground_7 = or_9_out | or_19_out;  // OR_Gate or_28, 30 bits wide
  Pull_Resistor pull_resistor_49 (.node(pull_resistor_49_node));
  Pull_Resistor pull_resistor_50 (.node(controlled_buffer_33_out));
  assign pull_resistor_49_node = controlled_buffer_33_out ? 30'h279 : 30'bz;  // Controlled_Buffer controlled_buffer_45
  assign controlled_buffer_46_out = controlled_buffer_33_out ? 30'h231 : 30'bz;  // Controlled_Buffer controlled_buffer_46
  Pull_Resistor pull_resistor_51 (.node(controlled_buffer_46_out));
  Pull_Resistor pull_resistor_52 (.node(pull_resistor_52_node));
  assign pull_resistor_52_node = controlled_buffer_33_out ? 30'h279 : 30'bz;  // Controlled_Buffer controlled_buffer_47
  assign controlled_buffer_48_out = controlled_buffer_33_out ? 30'h3ff : 30'bz;  // Controlled_Buffer controlled_buffer_48
  Pull_Resistor pull_resistor_53 (.node(controlled_buffer_48_out));
  Pull_Resistor pull_resistor_54 (.node(pull_resistor_54_node));
  assign pull_resistor_54_node = controlled_buffer_33_out ? 30'hfc : 30'bz;  // Controlled_Buffer controlled_buffer_49
  assign controlled_buffer_50_out = controlled_buffer_33_out ? 30'hfc : 30'bz;  // Controlled_Buffer controlled_buffer_50
  Pull_Resistor pull_resistor_55 (.node(controlled_buffer_50_out));
  assign controlled_buffer_51_out = controlled_buffer_33_out ? 30'h3ff : 30'bz;  // Controlled_Buffer controlled_buffer_51
  Pull_Resistor pull_resistor_56 (.node(controlled_buffer_51_out));
  assign controlled_buffer_52_out = controlled_buffer_33_out ? 30'h279 : 30'bz;  // Controlled_Buffer controlled_buffer_52
  Pull_Resistor pull_resistor_57 (.node(controlled_buffer_52_out));
  assign controlled_buffer_53_out = controlled_buffer_33_out ? 30'h231 : 30'bz;  // Controlled_Buffer controlled_buffer_53
  Pull_Resistor pull_resistor_58 (.node(controlled_buffer_53_out));
  Pull_Resistor pull_resistor_59 (.node(pull_resistor_59_node));
  assign pull_resistor_59_node = controlled_buffer_33_out ? 30'h201 : 30'bz;  // Controlled_Buffer controlled_buffer_54
  assign toBackground_2 = or_4_out | or_14_out;  // OR_Gate or_29, 30 bits wide
  assign toBackground_3 = or_5_out | or_15_out;  // OR_Gate or_30, 30 bits wide
  assign toBackground_4 = or_6_out | or_16_out;  // OR_Gate or_31, 30 bits wide
  Shifter #(.width(30)) shifter_41 (.in(pull_resistor_49_node), .\dist (adder_14_out), .out(shifter_41_out));
  Shifter #(.width(30)) shifter_42 (.in(controlled_buffer_46_out), .\dist (adder_14_out), .out(shifter_42_out));
  Shifter #(.width(30)) shifter_43 (.in(pull_resistor_52_node), .\dist (adder_14_out), .out(shifter_43_out));
  Shifter #(.width(30)) shifter_44 (.in(controlled_buffer_48_out), .\dist (adder_14_out), .out(shifter_44_out));
  Shifter #(.width(30)) shifter_45 (.in(pull_resistor_54_node), .\dist (adder_14_out), .out(shifter_45_out));
  Shifter #(.width(30)) shifter_46 (.in(controlled_buffer_50_out), .\dist (adder_14_out), .out(shifter_46_out));
  Shifter #(.width(30)) shifter_47 (.in(controlled_buffer_51_out), .\dist (adder_14_out), .out(shifter_47_out));
  Shifter #(.width(30)) shifter_48 (.in(controlled_buffer_52_out), .\dist (adder_14_out), .out(shifter_48_out));
  Shifter #(.width(30)) shifter_49 (.in(controlled_buffer_53_out), .\dist (adder_14_out), .out(shifter_49_out));
  Shifter #(.width(30)) shifter_50 (.in(pull_resistor_59_node), .\dist (adder_14_out), .out(shifter_50_out));
  assign not_5_out = ~adder_14_out;  // NOT_Gate not_5, 5 bits wide
  Adder #(.width(5)) adder_20 (.a(not_5_out), .b(5'b00001), .out(adder_20_out));  // open: cin, cout
  Pull_Resistor pull_resistor_60 (.node(controlled_buffer_34_out));
  assign toBackground = or_3_out | or_13_out;  // OR_Gate or_32, 30 bits wide
  Adder #(.width(5)) adder_21 (.a(5'b11110), .b(adder_20_out), .out(adder_21_out));  // open: cin, cout
  Pull_Resistor pull_resistor_61 (.node(pull_resistor_61_node));
  assign pull_resistor_61_node = controlled_buffer_34_out ? 30'h279 : 30'bz;  // Controlled_Buffer controlled_buffer_55
  Shifter #(.width(30), .shift("lr")) shifter_51 (
    .in(pull_resistor_61_node), .\dist (adder_21_out), .out(shifter_51_out));
  assign controlled_buffer_56_out = controlled_buffer_34_out ? 30'h231 : 30'bz;  // Controlled_Buffer controlled_buffer_56
  Pull_Resistor pull_resistor_62 (.node(controlled_buffer_56_out));
  Shifter #(.width(30), .shift("lr")) shifter_52 (
    .in(controlled_buffer_56_out), .\dist (adder_21_out), .out(shifter_52_out));
  assign controlled_buffer_57_out = controlled_buffer_34_out ? 30'h279 : 30'bz;  // Controlled_Buffer controlled_buffer_57
  Pull_Resistor pull_resistor_63 (.node(controlled_buffer_57_out));
  Shifter #(.width(30), .shift("lr")) shifter_53 (
    .in(controlled_buffer_57_out), .\dist (adder_21_out), .out(shifter_53_out));
  assign controlled_buffer_58_out = controlled_buffer_34_out ? 30'h3ff : 30'bz;  // Controlled_Buffer controlled_buffer_58
  Pull_Resistor pull_resistor_64 (.node(controlled_buffer_58_out));
  Shifter #(.width(30), .shift("lr")) shifter_54 (
    .in(controlled_buffer_58_out), .\dist (adder_21_out), .out(shifter_54_out));
  assign controlled_buffer_59_out = controlled_buffer_34_out ? 30'hfc : 30'bz;  // Controlled_Buffer controlled_buffer_59
  Pull_Resistor pull_resistor_65 (.node(controlled_buffer_59_out));
  Shifter #(.width(30), .shift("lr")) shifter_55 (
    .in(controlled_buffer_59_out), .\dist (adder_21_out), .out(shifter_55_out));
  Pull_Resistor pull_resistor_66 (.node(pull_resistor_66_node));
  assign pull_resistor_66_node = controlled_buffer_34_out ? 30'hfc : 30'bz;  // Controlled_Buffer controlled_buffer_60
  Shifter #(.width(30), .shift("lr")) shifter_56 (
    .in(pull_resistor_66_node), .\dist (adder_21_out), .out(shifter_56_out));
  Pull_Resistor pull_resistor_67 (.node(pull_resistor_67_node));
  assign pull_resistor_67_node = controlled_buffer_34_out ? 30'h3ff : 30'bz;  // Controlled_Buffer controlled_buffer_61
  Shifter #(.width(30), .shift("lr")) shifter_57 (
    .in(pull_resistor_67_node), .\dist (adder_21_out), .out(shifter_57_out));
  assign controlled_buffer_62_out = controlled_buffer_34_out ? 30'h279 : 30'bz;  // Controlled_Buffer controlled_buffer_62
  Pull_Resistor pull_resistor_68 (.node(controlled_buffer_62_out));
  Shifter #(.width(30), .shift("lr")) shifter_58 (
    .in(controlled_buffer_62_out), .\dist (adder_21_out), .out(shifter_58_out));
  Pull_Resistor pull_resistor_69 (.node(pull_resistor_69_node));
  assign pull_resistor_69_node = controlled_buffer_34_out ? 30'h231 : 30'bz;  // Controlled_Buffer controlled_buffer_63
  Shifter #(.width(30), .shift("lr")) shifter_59 (
    .in(pull_resistor_69_node), .\dist (adder_21_out), .out(shifter_59_out));
  assign controlled_buffer_64_out = controlled_buffer_34_out ? 30'h201 : 30'bz;  // Controlled_Buffer controlled_buffer_64
  Pull_Resistor pull_resistor_70 (.node(controlled_buffer_64_out));
  Shifter #(.width(30), .shift("lr")) shifter_60 (
    .in(controlled_buffer_64_out), .\dist (adder_21_out), .out(shifter_60_out));
  assign toFront = shifter_41_out | shifter_51_out;  // OR_Gate or_33, 30 bits wide
  assign toFront_2 = shifter_42_out | shifter_52_out;  // OR_Gate or_34, 30 bits wide
  assign toFront_3 = shifter_43_out | shifter_53_out;  // OR_Gate or_35, 30 bits wide
  assign toFront_4 = shifter_44_out | shifter_54_out;  // OR_Gate or_36, 30 bits wide
  assign toFront_5 = shifter_45_out | shifter_55_out;  // OR_Gate or_37, 30 bits wide
  assign toFront_6 = shifter_46_out | shifter_56_out;  // OR_Gate or_38, 30 bits wide
  assign toFront_7 = shifter_47_out | shifter_57_out;  // OR_Gate or_39, 30 bits wide
  assign toFront_8 = shifter_48_out | shifter_58_out;  // OR_Gate or_40, 30 bits wide
  assign toFront_9 = shifter_49_out | shifter_59_out;  // OR_Gate or_41, 30 bits wide
  assign toFront_10 = shifter_50_out | shifter_60_out;  // OR_Gate or_42, 30 bits wide

  assign nextMatriceX = matriceX;
  assign outPlayerShiftM = inPlayerShiftM;
  assign outPlayerY = inPlayerY;
  assign outputBackShiftM = inputBackShiftM;

  // Notes on the sheet:
  //   len+shift
  //   -shiftPM
  //   -shiftPM
  //   len+shift
  //   back's M lefter then player's M
  //   back's M righter then player's M
  //   back's M lefter then player's M
  //   len-shiftPm+shiftBm>30
  //   len-shiftPm+shiftBm>30
  //   MAKE SHIFT BY NEXT MATRICE
  //   MAKE SHIFT IN CURRENT MATRICE
  //   MAKE SHIFT IN CURRENT MATRICE
  //   MAKE SHIFT BY NEXT MATRICE
  //   MAKE SHIFT IN CURRENT MATRICE
  //   MAKE SHIFT BY NEXT MATRICE
endmodule
// cross
module computeIntresection (
  input  [4:0] backLen,
  input  [4:0] inBackM,
  input  [1:0] inBackD,
  input  [4:0] inFrogM,
  input  [1:0] inFrogD,
  input  inIntersect,
  input  doCompute,
  output outIntersect
);

  wire and_1_out, and_2_out, and_3_out, and_4_out, comparator_1_gt, comparator_2_eq, comparator_3_gt,
       comparator_4_eq, comparator_5_lt, comparator_6_gt, comparator_7_lt, comparator_8_gt, not_3_out,
       not_4_out, not_5_out, not_6_out, or_1_out;
  wire [1:0] adder_3_out, adder_6_out;
  wire [6:0] adder_1_out, adder_2_out, adder_4_out, adder_5_out, adder_7_out, adder_8_out, adder_9_out,
       adder_10_out, adder_11_out, adder_12_out, bit_extender_1_out, bit_extender_2_out, bit_extender_3_out,
       bit_extender_4_out, bit_extender_5_out, multiplier_1_out, multiplier_2_out, not_1_out, not_2_out;

  assign bit_extender_1_out = {{2{1'b0}}, backLen};  // Bit_Extender bit_extender_1
  assign bit_extender_2_out = {{2{1'b0}}, inBackM};  // Bit_Extender bit_extender_2
  assign bit_extender_3_out = {{5{1'b0}}, inBackD};  // Bit_Extender bit_extender_3
  assign bit_extender_4_out = {{2{1'b0}}, inFrogM};  // Bit_Extender bit_extender_4
  assign bit_extender_5_out = {{5{1'b0}}, inFrogD};  // Bit_Extender bit_extender_5
  Adder #(.width(7)) adder_1 (.a(7'b0001010), .b(bit_extender_4_out), .out(adder_1_out));  // open: cin, cout
  Adder #(.width(7)) adder_2 (.a(7'b0000001), .b(not_1_out), .out(adder_2_out));  // open: cin, cout
  assign not_1_out = ~bit_extender_2_out;  // NOT_Gate not_1, 7 bits wide
  Adder #(.width(2)) adder_3 (.a(inFrogD), .b(2'b01), .out(adder_3_out));  // open: cin, cout
  Adder #(.width(7)) adder_4 (.a(7'b0010100), .b(bit_extender_2_out), .out(adder_4_out));  // open: cin, cout
  Adder #(.width(7)) adder_5 (.a(7'b0000001), .b(not_2_out), .out(adder_5_out));  // open: cin, cout
  assign not_2_out = ~bit_extender_4_out;  // NOT_Gate not_2, 7 bits wide
  Adder #(.width(2)) adder_6 (.a(inBackD), .b(2'b01), .out(adder_6_out));  // open: cin, cout
  Adder #(.width(7)) adder_7 (.a(adder_1_out), .b(adder_2_out), .out(adder_7_out));  // open: cin, cout
  Comparator #(.width(7)) comparator_1 (.a(adder_7_out), .b(7'b0011110), .gt(comparator_1_gt));  // open: eq, lt
  Comparator #(.width(2), .mode("unsigned")) comparator_2 (
    .a(inBackD), .b(adder_3_out), .eq(comparator_2_eq));  // open: gt, lt
  Adder #(.width(7)) adder_8 (.a(adder_4_out), .b(adder_5_out), .out(adder_8_out));  // open: cin, cout
  Comparator #(.width(7)) comparator_3 (.a(adder_8_out), .b(7'b0011110), .gt(comparator_3_gt));  // open: eq, lt
  Comparator #(.width(2), .mode("unsigned")) comparator_4 (
    .a(inFrogD), .b(adder_6_out), .eq(comparator_4_eq));  // open: gt, lt
  and and_1 (and_1_out, comparator_1_gt, comparator_2_eq);
  and and_2 (and_2_out, comparator_3_gt, comparator_4_eq);
  Adder #(.width(7)) adder_9 (.a(bit_extender_2_out), .b(multiplier_1_out), .out(adder_9_out));  // open: cin, cout
  Multiplier #(.width(7)) multiplier_1 (
    .a(bit_extender_3_out), .b(7'b0011110), .out(multiplier_1_out));  // open: cin, cout
  // Probe on 7'b0001010
  // Probe on bit_extender_4_out
  Adder #(.width(7)) adder_10 (.a(bit_extender_4_out), .b(multiplier_2_out), .out(adder_10_out));  // open: cin, cout
  Multiplier #(.width(7)) multiplier_2 (
    .a(bit_extender_5_out), .b(7'b0011110), .out(multiplier_2_out));  // open: cin, cout
  Adder #(.width(7)) adder_11 (.a(bit_extender_1_out), .b(adder_9_out), .out(adder_11_out));  // open: cin, cout
  Adder #(.width(7)) adder_12 (.a(7'b0001010), .b(adder_10_out), .out(adder_12_out));  // open: cin, cout
  Comparator #(.width(7), .mode("unsigned")) comparator_5 (
    .a(adder_12_out), .b(adder_9_out), .lt(comparator_5_lt));  // open: gt, eq
  not not_3 (not_3_out, comparator_5_lt);
  not not_4 (not_4_out, comparator_6_gt);
  Comparator #(.width(7), .mode("unsigned")) comparator_6 (
    .a(adder_12_out), .b(adder_11_out), .gt(comparator_6_gt));  // open: eq, lt
  Comparator #(.width(7), .mode("unsigned")) comparator_7 (
    .a(adder_10_out), .b(adder_9_out), .lt(comparator_7_lt));  // open: gt, eq
  not not_5 (not_5_out, comparator_7_lt);
  not not_6 (not_6_out, comparator_8_gt);
  Comparator #(.width(7), .mode("unsigned")) comparator_8 (
    .a(adder_10_out), .b(adder_11_out), .gt(comparator_8_gt));  // open: eq, lt
  and and_3 (and_3_out, not_3_out, not_4_out);
  and and_4 (and_4_out, not_5_out, not_6_out);
  Pull_Resistor pull_resistor_1 (.node(inIntersect));
  or or_1 (or_1_out, and_3_out, and_4_out, inIntersect, and_1_out, and_2_out);
  and and_5 (outIntersect, or_1_out, doCompute);
  Pull_Resistor pull_resistor_2 (.node(doCompute));
  Pull_Resistor pull_resistor_3 (.node(outIntersect));

  // Notes on the sheet:
  //   BD * 30 + BM
  //   Bh
  //   Bl
  //   Fl
  //   Fh >= Bl && Fh <= Bh
  //   Fl >= Bl && Fl <= Bh
endmodule

// Y
module heightFlag (
  input  [3:0] height,
  input  [3:0] playerY,
  output eqY
);

  Comparator #(.width(4), .mode("unsigned")) comparator_1 (.a(height), .b(playerY), .eq(eqY));  // open: gt, lt
endmodule

// swampCon
module swamp (
  input  [1:0] inPlayerShiftD,
  input  [4:0] inPlayerShiftM,
  input  inFlag,
  output [29:0] toBackground,
  output [29:0] toFront,
  output [29:0] toBackground_2,
  output [29:0] toFront_2,
  output [29:0] toBackground_3,
  output [29:0] toFront_3,
  output [29:0] toBackground_4,
  output [29:0] toFront_4,
  output [29:0] toBackground_5,
  output [29:0] toFront_5,
  output [29:0] toBackground_6,
  output [29:0] toFront_6,
  output [1:0] outPlayerShiftD,
  output [29:0] toBackground_7,
  output [4:0] outPlayerShiftM,
  output [29:0] toFront_7,
  output outFlag,
  output [29:0] toBackground_8,
  output [29:0] toFront_8,
  output [29:0] toBackground_9,
  output [29:0] toFront_9,
  output [29:0] toBackground_10,
  output [29:0] toFront_10
);

  wire comparator_1_eq, comparator_2_eq, comparator_3_eq, controlled_buffer_1_out, controlled_buffer_2_out;
  wire [1:0] adder_3_out, multiplexer_1_out;
  wire [4:0] adder_2_out, adder_4_out, adder_5_out, not_1_out;
  wire [29:0] controlled_buffer_6_out, controlled_buffer_7_out, controlled_buffer_10_out,
       controlled_buffer_11_out, controlled_buffer_14_out, controlled_buffer_15_out,
       controlled_buffer_16_out, controlled_buffer_17_out, controlled_buffer_19_out,
       controlled_buffer_21_out, pull_resistor_3_node, pull_resistor_4_node, pull_resistor_5_node,
       pull_resistor_8_node, pull_resistor_9_node, pull_resistor_12_node, pull_resistor_13_node,
       pull_resistor_18_node, pull_resistor_20_node, pull_resistor_22_node, shifter_1_out, shifter_2_out,
       shifter_3_out, shifter_4_out, shifter_5_out, shifter_6_out, shifter_7_out, shifter_8_out,
       shifter_9_out, shifter_10_out, shifter_11_out, shifter_12_out, shifter_13_out, shifter_14_out,
       shifter_15_out, shifter_16_out, shifter_17_out, shifter_18_out, shifter_19_out, shifter_20_out;

  Pull_Resistor pull_resistor_1 (.node(inPlayerShiftM));
  Adder #(.width(2)) adder_1 (.a(inPlayerShiftD), .b(2'b01), .out(outPlayerShiftD));  // open: cin, cout
  Adder #(.width(5)) adder_2 (.a(inPlayerShiftM), .b(5'b00001), .out(adder_2_out));  // open: cin, cout
  Multiplexer #(.width(2), .disabled(0), .enable("false")) multiplexer_1 (
    .in0(inPlayerShiftD), .in1(outPlayerShiftD), .out(multiplexer_1_out), .sel(comparator_1_eq));
  Comparator #(.width(5), .mode("unsigned")) comparator_1 (
    .a(inPlayerShiftM), .b(5'b11110), .eq(comparator_1_eq));  // open: gt, lt
  assign controlled_buffer_1_out = inFlag ? comparator_2_eq : 1'bz;  // Controlled_Buffer controlled_buffer_1
  Comparator #(.width(2)) comparator_2 (.a(2'b00), .b(multiplexer_1_out), .eq(comparator_2_eq));  // open: gt, lt
  Adder #(.width(2)) adder_3 (.a(multiplexer_1_out), .b(2'b01), .out(adder_3_out));  // open: cin, cout
  assign controlled_buffer_2_out = inFlag ? comparator_3_eq : 1'bz;  // Controlled_Buffer controlled_buffer_2
  Comparator #(.width(2)) comparator_3 (.a(2'b00), .b(adder_3_out), .eq(comparator_3_eq));  // open: gt, lt
  Pull_Resistor pull_resistor_2 (.node(controlled_buffer_1_out));
  Pull_Resistor pull_resistor_3 (.node(pull_resistor_3_node));
  assign pull_resistor_3_node = controlled_buffer_1_out ? 30'h279 : 30'bz;  // Controlled_Buffer controlled_buffer_3
  Pull_Resistor pull_resistor_4 (.node(pull_resistor_4_node));
  assign pull_resistor_4_node = controlled_buffer_1_out ? 30'h231 : 30'bz;  // Controlled_Buffer controlled_buffer_4
  Pull_Resistor pull_resistor_5 (.node(pull_resistor_5_node));
  assign pull_resistor_5_node = controlled_buffer_1_out ? 30'h279 : 30'bz;  // Controlled_Buffer controlled_buffer_5
  assign controlled_buffer_6_out = controlled_buffer_1_out ? 30'h3ff : 30'bz;  // Controlled_Buffer controlled_buffer_6
  Pull_Resistor pull_resistor_6 (.node(controlled_buffer_6_out));
  assign controlled_buffer_7_out = controlled_buffer_1_out ? 30'hfc : 30'bz;  // Controlled_Buffer controlled_buffer_7
  Pull_Resistor pull_resistor_7 (.node(controlled_buffer_7_out));
  Pull_Resistor pull_resistor_8 (.node(pull_resistor_8_node));
  assign pull_resistor_8_node = controlled_buffer_1_out ? 30'hfc : 30'bz;  // Controlled_Buffer controlled_buffer_8
  Pull_Resistor pull_resistor_9 (.node(pull_resistor_9_node));
  assign pull_resistor_9_node = controlled_buffer_1_out ? 30'h3ff : 30'bz;  // Controlled_Buffer controlled_buffer_9
  assign controlled_buffer_10_out = controlled_buffer_1_out ? 30'h279 : 30'bz;  // Controlled_Buffer controlled_buffer_10
  Pull_Resistor pull_resistor_10 (.node(controlled_buffer_10_out));
  assign controlled_buffer_11_out = controlled_buffer_1_out ? 30'h231 : 30'bz;  // Controlled_Buffer controlled_buffer_11
  Pull_Resistor pull_resistor_11 (.node(controlled_buffer_11_out));
  Pull_Resistor pull_resistor_12 (.node(pull_resistor_12_node));
  assign pull_resistor_12_node = controlled_buffer_1_out ? 30'h201 : 30'bz;  // Controlled_Buffer controlled_buffer_12
  Shifter #(.width(30)) shifter_1 (.in(pull_resistor_3_node), .\dist (adder_2_out), .out(shifter_1_out));
  Shifter #(.width(30)) shifter_2 (.in(pull_resistor_4_node), .\dist (adder_2_out), .out(shifter_2_out));
  Shifter #(.width(30)) shifter_3 (.in(pull_resistor_5_node), .\dist (adder_2_out), .out(shifter_3_out));
  Shifter #(.width(30)) shifter_4 (.in(controlled_buffer_6_out), .\dist (adder_2_out), .out(shifter_4_out));
  Shifter #(.width(30)) shifter_5 (.in(controlled_buffer_7_out), .\dist (adder_2_out), .out(shifter_5_out));
  Shifter #(.width(30)) shifter_6 (.in(pull_resistor_8_node), .\dist (adder_2_out), .out(shifter_6_out));
  Shifter #(.width(30)) shifter_7 (.in(pull_resistor_9_node), .\dist (adder_2_out), .out(shifter_7_out));
  Shifter #(.width(30)) shifter_8 (.in(controlled_buffer_10_out), .\dist (adder_2_out), .out(shifter_8_out));
  Shifter #(.width(30)) shifter_9 (.in(controlled_buffer_11_out), .\dist (adder_2_out), .out(shifter_9_out));
  Shifter #(.width(30)) shifter_10 (.in(pull_resistor_12_node), .\dist (adder_2_out), .out(shifter_10_out));
  assign not_1_out = ~adder_2_out;  // NOT_Gate not_1, 5 bits wide
  Adder #(.width(5)) adder_4 (.a(not_1_out), .b(5'b00001), .out(adder_4_out));  // open: cin, cout
  Adder #(.width(5)) adder_5 (.a(5'b11110), .b(adder_4_out), .out(adder_5_out));  // open: cin, cout
  Pull_Resistor pull_resistor_13 (.node(pull_resistor_13_node));
  assign pull_resistor_13_node = controlled_buffer_2_out ? 30'h279 : 30'bz;  // Controlled_Buffer controlled_buffer_13
  assign controlled_buffer_14_out = controlled_buffer_2_out ? 30'h231 : 30'bz;  // Controlled_Buffer controlled_buffer_14
  Pull_Resistor pull_resistor_14 (.node(controlled_buffer_14_out));
  assign controlled_buffer_15_out = controlled_buffer_2_out ? 30'h279 : 30'bz;  // Controlled_Buffer controlled_buffer_15
  Pull_Resistor pull_resistor_15 (.node(controlled_buffer_15_out));
  assign controlled_buffer_16_out = controlled_buffer_2_out ? 30'h3ff : 30'bz;  // Controlled_Buffer controlled_buffer_16
  Pull_Resistor pull_resistor_16 (.node(controlled_buffer_16_out));
  assign controlled_buffer_17_out = controlled_buffer_2_out ? 30'hfc : 30'bz;  // Controlled_Buffer controlled_buffer_17
  Pull_Resistor pull_resistor_17 (.node(controlled_buffer_17_out));
  Pull_Resistor pull_resistor_18 (.node(pull_resistor_18_node));
  assign pull_resistor_18_node = controlled_buffer_2_out ? 30'hfc : 30'bz;  // Controlled_Buffer controlled_buffer_18
  assign controlled_buffer_19_out = controlled_buffer_2_out ? 30'h3ff : 30'bz;  // Controlled_Buffer controlled_buffer_19
  Pull_Resistor pull_resistor_19 (.node(controlled_buffer_19_out));
  Pull_Resistor pull_resistor_20 (.node(pull_resistor_20_node));
  assign pull_resistor_20_node = controlled_buffer_2_out ? 30'h279 : 30'bz;  // Controlled_Buffer controlled_buffer_20
  assign controlled_buffer_21_out = controlled_buffer_2_out ? 30'h231 : 30'bz;  // Controlled_Buffer controlled_buffer_21
  Pull_Resistor pull_resistor_21 (.node(controlled_buffer_21_out));
  Pull_Resistor pull_resistor_22 (.node(pull_resistor_22_node));
  assign pull_resistor_22_node = controlled_buffer_2_out ? 30'h201 : 30'bz;  // Controlled_Buffer controlled_buffer_22
  Pull_Resistor pull_resistor_23 (.node(controlled_buffer_2_out));
  assign toFront = shifter_1_out | shifter_11_out;  // OR_Gate or_1, 30 bits wide
  assign toFront_2 = shifter_2_out | shifter_12_out;  // OR_Gate or_2, 30 bits wide
  assign toFront_3 = shifter_3_out | shifter_13_out;  // OR_Gate or_3, 30 bits wide
  assign toFront_4 = shifter_4_out | shifter_14_out;  // OR_Gate or_4, 30 bits wide
  assign toFront_5 = shifter_5_out | shifter_15_out;  // OR_Gate or_5, 30 bits wide
  Shifter #(.width(30), .shift("lr")) shifter_11 (
    .in(pull_resistor_13_node), .\dist (adder_5_out), .out(shifter_11_out));
  Shifter #(.width(30), .shift("lr")) shifter_12 (
    .in(controlled_buffer_14_out), .\dist (adder_5_out), .out(shifter_12_out));
  Shifter #(.width(30), .shift("lr")) shifter_13 (
    .in(controlled_buffer_15_out), .\dist (adder_5_out), .out(shifter_13_out));
  Shifter #(.width(30), .shift("lr")) shifter_14 (
    .in(controlled_buffer_16_out), .\dist (adder_5_out), .out(shifter_14_out));
  Shifter #(.width(30), .shift("lr")) shifter_15 (
    .in(controlled_buffer_17_out), .\dist (adder_5_out), .out(shifter_15_out));
  Shifter #(.width(30), .shift("lr")) shifter_16 (
    .in(pull_resistor_18_node), .\dist (adder_5_out), .out(shifter_16_out));
  Shifter #(.width(30), .shift("lr")) shifter_17 (
    .in(controlled_buffer_19_out), .\dist (adder_5_out), .out(shifter_17_out));
  Shifter #(.width(30), .shift("lr")) shifter_18 (
    .in(pull_resistor_20_node), .\dist (adder_5_out), .out(shifter_18_out));
  Shifter #(.width(30), .shift("lr")) shifter_19 (
    .in(controlled_buffer_21_out), .\dist (adder_5_out), .out(shifter_19_out));
  Shifter #(.width(30), .shift("lr")) shifter_20 (
    .in(pull_resistor_22_node), .\dist (adder_5_out), .out(shifter_20_out));
  assign toFront_6 = shifter_6_out | shifter_16_out;  // OR_Gate or_6, 30 bits wide
  assign toFront_7 = shifter_7_out | shifter_17_out;  // OR_Gate or_7, 30 bits wide
  assign toFront_8 = shifter_8_out | shifter_18_out;  // OR_Gate or_8, 30 bits wide
  assign toFront_9 = shifter_9_out | shifter_19_out;  // OR_Gate or_9, 30 bits wide
  assign toFront_10 = shifter_10_out | shifter_20_out;  // OR_Gate or_10, 30 bits wide

  assign outFlag = inFlag;
  assign outPlayerShiftM = inPlayerShiftM;
  assign toBackground = 30'h300c030;
  assign toBackground_2 = 30'h781e078;
  assign toBackground_3 = 30'hfc3f0fc;
  assign toBackground_4 = 30'h1fe7f9fe;
  assign toBackground_5 = {30{1'b1}};
  assign toBackground_6 = {30{1'b1}};
  assign toBackground_7 = 30'h1fe7f9fe;
  assign toBackground_8 = 30'hfc3f0fc;
  assign toBackground_9 = 30'h781e078;
  assign toBackground_10 = 30'h300c030;

  // Notes on the sheet:
  //   MAKE SHIFT BY NEXT MATRICE
  //   MAKE SHIFT IN CURRENT MATRICE
endmodule

module waterIntersect (
  input  [4:0] backLen,
  input  [4:0] inBackM,
  input  [1:0] inBackD,
  input  [4:0] inFrogM,
  input  [1:0] inFrogD,
  input  inIntersect,
  input  doIntersect,
  output outIntersect
);

  wire and_1_out, and_2_out, and_3_out, and_4_out, and_5_out, and_6_out, and_7_out, and_8_out,
       comparator_1_eq, comparator_2_eq, comparator_3_gt, comparator_4_gt, comparator_5_eq, comparator_6_eq,
       comparator_7_gt, comparator_8_gt, comparator_9_lt, comparator_10_gt, comparator_11_lt,
       comparator_12_gt, comparator_13_lt, comparator_14_gt, comparator_15_lt, comparator_16_gt, not_5_out,
       not_6_out, not_7_out, not_8_out, not_9_out, not_10_out, not_11_out, not_12_out, not_13_out, or_1_out,
       or_2_out, or_3_out;
  wire [1:0] adder_1_out, adder_2_out, adder_9_out, adder_10_out, subtractor_1_out;
  wire [4:0] subtractor_2_out;
  wire [6:0] adder_3_out, adder_4_out, adder_5_out, adder_6_out, adder_7_out, adder_8_out, adder_11_out,
       adder_12_out, adder_13_out, adder_14_out, adder_15_out, adder_16_out, adder_17_out, adder_18_out,
       adder_19_out, adder_20_out, adder_21_out, adder_22_out, adder_23_out, adder_24_out,
       bit_extender_1_out, bit_extender_2_out, bit_extender_3_out, bit_extender_4_out, bit_extender_5_out,
       bit_extender_6_out, bit_extender_7_out, multiplier_1_out, multiplier_2_out, multiplier_3_out,
       multiplier_4_out, not_1_out, not_2_out, not_3_out, not_4_out;

  assign not_1_out = ~bit_extender_2_out;  // NOT_Gate not_1, 7 bits wide
  Adder #(.width(2)) adder_1 (.a(inFrogD), .b(2'b01), .out(adder_1_out));  // open: cin, cout
  assign not_2_out = ~bit_extender_7_out;  // NOT_Gate not_2, 7 bits wide
  Adder #(.width(2)) adder_2 (.a(inBackD), .b(2'b01), .out(adder_2_out));  // open: cin, cout
  Subtractor #(.width(2)) subtractor_1 (.a(inBackD), .b(2'b10), .out(subtractor_1_out));  // open: bin, bout
  // Probe on subtractor_1_out
  // Probe on subtractor_1_out
  assign bit_extender_1_out = {{2{1'b0}}, backLen};  // Bit_Extender bit_extender_1
  assign bit_extender_2_out = {{2{1'b0}}, inBackM};  // Bit_Extender bit_extender_2
  assign bit_extender_3_out = {{5{1'b0}}, inBackD};  // Bit_Extender bit_extender_3
  // Probe on bit_extender_3_out
  // Probe on bit_extender_3_out
  Subtractor #(.width(5)) subtractor_2 (.a(inFrogM), .b({5{1'b0}}), .out(subtractor_2_out));  // open: bin, bout
  assign bit_extender_4_out = {{5{1'b0}}, inFrogD};  // Bit_Extender bit_extender_4
  Adder #(.width(7)) adder_3 (.a(7'b0000101), .b(bit_extender_7_out), .out(adder_3_out));  // open: cin, cout
  Adder #(.width(7)) adder_4 (.a(adder_3_out), .b(adder_5_out), .out(adder_4_out));  // open: cin, cout
  Adder #(.width(7)) adder_5 (.a(7'b0000001), .b(not_1_out), .out(adder_5_out));  // open: cin, cout
  Comparator #(.width(2), .mode("unsigned")) comparator_1 (
    .a(inBackD), .b(adder_1_out), .eq(comparator_1_eq));  // open: gt, lt
  Adder #(.width(7)) adder_6 (.a(bit_extender_1_out), .b(bit_extender_2_out), .out(adder_6_out));  // open: cin, cout
  Adder #(.width(7)) adder_7 (.a(adder_6_out), .b(adder_8_out), .out(adder_7_out));  // open: cin, cout
  Adder #(.width(7)) adder_8 (.a(7'b0000001), .b(not_2_out), .out(adder_8_out));  // open: cin, cout
  Comparator #(.width(2), .mode("unsigned")) comparator_2 (
    .a(inFrogD), .b(adder_2_out), .eq(comparator_2_eq));  // open: gt, lt
  assign bit_extender_5_out = {{5{1'b0}}, subtractor_1_out};  // Bit_Extender bit_extender_5
  assign bit_extender_6_out = {{5{1'b0}}, inFrogD};  // Bit_Extender bit_extender_6
  assign not_3_out = ~bit_extender_2_out;  // NOT_Gate not_3, 7 bits wide
  Adder #(.width(2)) adder_9 (.a(inFrogD), .b(2'b01), .out(adder_9_out));  // open: cin, cout
  assign not_4_out = ~bit_extender_7_out;  // NOT_Gate not_4, 7 bits wide
  Adder #(.width(2)) adder_10 (.a(subtractor_1_out), .b(2'b01), .out(adder_10_out));  // open: cin, cout
  assign bit_extender_7_out = {{2{1'b0}}, subtractor_2_out};  // Bit_Extender bit_extender_7
  Comparator #(.width(7)) comparator_3 (.a(adder_4_out), .b(7'b0011110), .gt(comparator_3_gt));  // open: eq, lt
  Comparator #(.width(7)) comparator_4 (.a(adder_7_out), .b(7'b0011110), .gt(comparator_4_gt));  // open: eq, lt
  Adder #(.width(7)) adder_11 (.a(7'b0000101), .b(bit_extender_7_out), .out(adder_11_out));  // open: cin, cout
  Adder #(.width(7)) adder_12 (.a(adder_11_out), .b(adder_13_out), .out(adder_12_out));  // open: cin, cout
  Adder #(.width(7)) adder_13 (.a(7'b0000001), .b(not_3_out), .out(adder_13_out));  // open: cin, cout
  Comparator #(.width(2), .mode("unsigned")) comparator_5 (
    .a(subtractor_1_out), .b(adder_9_out), .eq(comparator_5_eq));  // open: gt, lt
  Adder #(.width(7)) adder_14 (.a(bit_extender_1_out), .b(bit_extender_2_out), .out(adder_14_out));  // open: cin, cout
  Adder #(.width(7)) adder_15 (.a(adder_14_out), .b(adder_16_out), .out(adder_15_out));  // open: cin, cout
  Adder #(.width(7)) adder_16 (.a(7'b0000001), .b(not_4_out), .out(adder_16_out));  // open: cin, cout
  Comparator #(.width(2), .mode("unsigned")) comparator_6 (
    .a(inFrogD), .b(adder_10_out), .eq(comparator_6_eq));  // open: gt, lt
  Multiplier #(.width(7)) multiplier_1 (
    .a(bit_extender_3_out), .b(7'b0011110), .out(multiplier_1_out));  // open: cin, cout
  Multiplier #(.width(7)) multiplier_2 (
    .a(bit_extender_4_out), .b(7'b0011110), .out(multiplier_2_out));  // open: cin, cout
  and and_1 (and_1_out, comparator_3_gt, comparator_1_eq);
  and and_2 (and_2_out, comparator_4_gt, comparator_2_eq);
  and and_3 (and_3_out, comparator_7_gt, comparator_5_eq);
  Comparator #(.width(7)) comparator_7 (.a(adder_12_out), .b(7'b0011110), .gt(comparator_7_gt));  // open: eq, lt
  and and_4 (and_4_out, comparator_8_gt, comparator_6_eq);
  Comparator #(.width(7)) comparator_8 (.a(adder_15_out), .b(7'b0011110), .gt(comparator_8_gt));  // open: eq, lt
  Adder #(.width(7)) adder_17 (.a(bit_extender_2_out), .b(multiplier_1_out), .out(adder_17_out));  // open: cin, cout
  Adder #(.width(7)) adder_18 (.a(bit_extender_7_out), .b(multiplier_2_out), .out(adder_18_out));  // open: cin, cout
  Multiplier #(.width(7)) multiplier_3 (
    .a(bit_extender_5_out), .b(7'b0011110), .out(multiplier_3_out));  // open: cin, cout
  // Probe on bit_extender_7_out
  Multiplier #(.width(7)) multiplier_4 (
    .a(bit_extender_6_out), .b(7'b0011110), .out(multiplier_4_out));  // open: cin, cout
  Adder #(.width(7)) adder_19 (.a(bit_extender_1_out), .b(adder_17_out), .out(adder_19_out));  // open: cin, cout
  Adder #(.width(7)) adder_20 (.a(7'b0000101), .b(adder_18_out), .out(adder_20_out));  // open: cin, cout
  Adder #(.width(7)) adder_21 (.a(bit_extender_2_out), .b(multiplier_3_out), .out(adder_21_out));  // open: cin, cout
  Adder #(.width(7)) adder_22 (.a(bit_extender_7_out), .b(multiplier_4_out), .out(adder_22_out));  // open: cin, cout
  Comparator #(.width(7), .mode("unsigned")) comparator_9 (
    .a(adder_20_out), .b(adder_17_out), .lt(comparator_9_lt));  // open: gt, eq
  not not_5 (not_5_out, comparator_9_lt);
  and and_5 (and_5_out, not_5_out, not_6_out);
  not not_6 (not_6_out, comparator_10_gt);
  Comparator #(.width(7), .mode("unsigned")) comparator_10 (
    .a(adder_20_out), .b(adder_19_out), .gt(comparator_10_gt));  // open: eq, lt
  Comparator #(.width(7), .mode("unsigned")) comparator_11 (
    .a(adder_18_out), .b(adder_17_out), .lt(comparator_11_lt));  // open: gt, eq
  not not_7 (not_7_out, comparator_11_lt);
  and and_6 (and_6_out, not_7_out, not_8_out);
  not not_8 (not_8_out, comparator_12_gt);
  Comparator #(.width(7), .mode("unsigned")) comparator_12 (
    .a(adder_18_out), .b(adder_19_out), .gt(comparator_12_gt));  // open: eq, lt
  Adder #(.width(7)) adder_23 (.a(bit_extender_1_out), .b(adder_21_out), .out(adder_23_out));  // open: cin, cout
  Adder #(.width(7)) adder_24 (.a(7'b0000101), .b(adder_22_out), .out(adder_24_out));  // open: cin, cout
  Pull_Resistor pull_resistor_1 (.node(inIntersect));
  Comparator #(.width(7), .mode("unsigned")) comparator_13 (
    .a(adder_24_out), .b(adder_21_out), .lt(comparator_13_lt));  // open: gt, eq
  not not_9 (not_9_out, comparator_13_lt);
  and and_7 (and_7_out, not_9_out, not_10_out);
  not not_10 (not_10_out, comparator_14_gt);
  Comparator #(.width(7), .mode("unsigned")) comparator_14 (
    .a(adder_24_out), .b(adder_23_out), .gt(comparator_14_gt));  // open: eq, lt
  Comparator #(.width(7), .mode("unsigned")) comparator_15 (
    .a(adder_22_out), .b(adder_21_out), .lt(comparator_15_lt));  // open: gt, eq
  not not_11 (not_11_out, comparator_15_lt);
  and and_8 (and_8_out, not_11_out, not_12_out);
  not not_12 (not_12_out, comparator_16_gt);
  Comparator #(.width(7), .mode("unsigned")) comparator_16 (
    .a(adder_22_out), .b(adder_23_out), .gt(comparator_16_gt));  // open: eq, lt
  or or_1 (or_1_out, and_5_out, and_6_out, inIntersect, and_1_out, and_2_out);
  not not_13 (not_13_out, or_2_out);
  or or_2 (or_2_out, or_1_out, or_3_out);
  or or_3 (or_3_out, and_7_out, and_8_out, and_3_out, and_4_out);
  and and_9 (outIntersect, not_13_out, doIntersect);

  // Notes on the sheet:
  //   len+shift
  //   -shiftPM
  //   len+shift
  //   -shiftPM
  //   -shiftPM
  //   len+shift
  //   -shiftPM
  //   len-shiftPm+shiftBm>30
  //   len-shiftPm+shiftBm>30
  //   BD * 30 + BM
  //   len-shiftPm+shiftBm>30
  //   Bh
  //   Bl
  //   Fl
  //   Bh
  //   Bl
  //   Fl
  //   Fh >= Bl && Fh <= Bh
  //   Fl >= Bl && Fl <= Bh
endmodule

module log_3x2 (
  input  [1:0] inBackShiftD,
  input  [4:0] inputBackShiftM,
  input  [1:0] inPlayerShiftD,
  input  [4:0] inPlayerShiftM,
  input  inFlag,
  output [29:0] toBackground,
  output [29:0] toBackground_2,
  output [29:0] toBackground_3,
  output [29:0] toBackground_4,
  output [29:0] toBackground_5,
  output [1:0] outBackShiftD,
  output [29:0] toBackground_6,
  output [29:0] toBackground_7,
  output [4:0] outputBackShiftM,
  output [29:0] toBackground_8,
  output [29:0] toBackground_9,
  output [29:0] toBackground_10,
  output [29:0] toFront,
  output [29:0] toFront_2,
  output [29:0] toFront_3,
  output [29:0] toFront_4,
  output [29:0] toFront_5,
  output [29:0] toFront_6,
  output [1:0] outPlayerShiftD,
  output [4:0] outPlayerShiftM,
  output [29:0] toFront_7,
  output outFlag,
  output [29:0] toFront_8,
  output [29:0] toFront_9,
  output [29:0] toFront_10
);

  wire comparator_1_eq, comparator_2_eq, comparator_3_eq, comparator_4_eq, comparator_5_eq, comparator_6_eq,
       comparator_7_eq, controlled_buffer_21_out, controlled_buffer_22_out, or_1_out, or_2_out;
  wire [1:0] adder_6_out, multiplexer_1_out;
  wire [4:0] adder_2_out, adder_3_out, adder_5_out, adder_7_out, adder_8_out, not_1_out, not_2_out;
  wire [29:0] controlled_buffer_1_out, controlled_buffer_5_out, controlled_buffer_6_out,
       controlled_buffer_7_out, controlled_buffer_9_out, controlled_buffer_10_out, controlled_buffer_11_out,
       controlled_buffer_13_out, controlled_buffer_15_out, controlled_buffer_16_out,
       controlled_buffer_17_out, controlled_buffer_28_out, controlled_buffer_31_out,
       controlled_buffer_32_out, controlled_buffer_33_out, controlled_buffer_36_out,
       controlled_buffer_38_out, controlled_buffer_40_out, controlled_buffer_41_out,
       controlled_buffer_42_out, pull_resistor_4_node, pull_resistor_5_node, pull_resistor_6_node,
       pull_resistor_10_node, pull_resistor_14_node, pull_resistor_16_node, pull_resistor_20_node,
       pull_resistor_21_node, pull_resistor_22_node, pull_resistor_25_node, pull_resistor_27_node,
       pull_resistor_28_node, pull_resistor_29_node, pull_resistor_30_node, pull_resistor_32_node,
       pull_resistor_33_node, pull_resistor_38_node, pull_resistor_39_node, pull_resistor_41_node,
       pull_resistor_43_node, shifter_1_out, shifter_2_out, shifter_3_out, shifter_4_out, shifter_5_out,
       shifter_6_out, shifter_7_out, shifter_8_out, shifter_9_out, shifter_10_out, shifter_11_out,
       shifter_12_out, shifter_13_out, shifter_14_out, shifter_15_out, shifter_16_out, shifter_17_out,
       shifter_18_out, shifter_19_out, shifter_20_out, shifter_21_out, shifter_22_out, shifter_23_out,
       shifter_24_out, shifter_25_out, shifter_26_out, shifter_27_out, shifter_28_out, shifter_29_out,
       shifter_30_out, shifter_31_out, shifter_32_out, shifter_33_out, shifter_34_out, shifter_35_out,
       shifter_36_out, shifter_37_out, shifter_38_out, shifter_39_out, shifter_40_out;

  Adder #(.width(2)) adder_1 (.a(inBackShiftD), .b(2'b01), .out(outBackShiftD));  // open: cin, cout
  Pull_Resistor pull_resistor_1 (.node(inputBackShiftM));
  Comparator #(.width(2)) comparator_1 (.a(inBackShiftD), .b(2'b10), .eq(comparator_1_eq));  // open: gt, lt
  Comparator #(.width(2)) comparator_2 (.a(2'b00), .b(inBackShiftD), .eq(comparator_2_eq));  // open: gt, lt
  // Probe on outBackShiftD
  or or_1 (or_1_out, comparator_1_eq, comparator_2_eq);
  Comparator #(.width(2)) comparator_3 (.a(outBackShiftD), .b(2'b10), .eq(comparator_3_eq));  // open: gt, lt
  or or_2 (or_2_out, comparator_3_eq, comparator_4_eq);
  Comparator #(.width(2)) comparator_4 (.a(2'b00), .b(outBackShiftD), .eq(comparator_4_eq));  // open: gt, lt
  Pull_Resistor pull_resistor_2 (.node(or_1_out));
  assign controlled_buffer_1_out = or_1_out ? {30{1'b0}} : 30'bz;  // Controlled_Buffer controlled_buffer_1
  Pull_Resistor pull_resistor_3 (.node(controlled_buffer_1_out));
  Pull_Resistor pull_resistor_4 (.node(pull_resistor_4_node));
  assign pull_resistor_4_node = or_1_out ? {30{1'b1}} : 30'bz;  // Controlled_Buffer controlled_buffer_2
  Pull_Resistor pull_resistor_5 (.node(pull_resistor_5_node));
  assign pull_resistor_5_node = or_1_out ? 30'h2fbfcfef : 30'bz;  // Controlled_Buffer controlled_buffer_3
  Pull_Resistor pull_resistor_6 (.node(pull_resistor_6_node));
  assign pull_resistor_6_node = or_1_out ? 30'h3fafafaf : 30'bz;  // Controlled_Buffer controlled_buffer_4
  assign controlled_buffer_5_out = or_1_out ? 30'h3eeeeeee : 30'bz;  // Controlled_Buffer controlled_buffer_5
  Pull_Resistor pull_resistor_7 (.node(controlled_buffer_5_out));
  assign controlled_buffer_6_out = or_1_out ? 30'h2edfbafa : 30'bz;  // Controlled_Buffer controlled_buffer_6
  Pull_Resistor pull_resistor_8 (.node(controlled_buffer_6_out));
  assign controlled_buffer_7_out = or_1_out ? {30{1'b1}} : 30'bz;  // Controlled_Buffer controlled_buffer_7
  Pull_Resistor pull_resistor_9 (.node(controlled_buffer_7_out));
  Pull_Resistor pull_resistor_10 (.node(pull_resistor_10_node));
  assign pull_resistor_10_node = or_1_out ? 30'h3f7ba9f : 30'bz;  // Controlled_Buffer controlled_buffer_8
  assign controlled_buffer_9_out = or_1_out ? {30{1'b1}} : 30'bz;  // Controlled_Buffer controlled_buffer_9
  Pull_Resistor pull_resistor_11 (.node(controlled_buffer_9_out));
  assign controlled_buffer_10_out = or_1_out ? {30{1'b0}} : 30'bz;  // Controlled_Buffer controlled_buffer_10
  Pull_Resistor pull_resistor_12 (.node(controlled_buffer_10_out));
  Shifter #(.width(30)) shifter_1 (.in(controlled_buffer_1_out), .\dist (inputBackShiftM), .out(shifter_1_out));
  Shifter #(.width(30)) shifter_2 (.in(pull_resistor_4_node), .\dist (inputBackShiftM), .out(shifter_2_out));
  Shifter #(.width(30)) shifter_3 (.in(pull_resistor_5_node), .\dist (inputBackShiftM), .out(shifter_3_out));
  Shifter #(.width(30)) shifter_4 (.in(pull_resistor_6_node), .\dist (inputBackShiftM), .out(shifter_4_out));
  Shifter #(.width(30)) shifter_5 (.in(controlled_buffer_5_out), .\dist (inputBackShiftM), .out(shifter_5_out));
  Shifter #(.width(30)) shifter_6 (.in(controlled_buffer_6_out), .\dist (inputBackShiftM), .out(shifter_6_out));
  Shifter #(.width(30)) shifter_7 (.in(controlled_buffer_7_out), .\dist (inputBackShiftM), .out(shifter_7_out));
  Shifter #(.width(30)) shifter_8 (.in(pull_resistor_10_node), .\dist (inputBackShiftM), .out(shifter_8_out));
  Shifter #(.width(30)) shifter_9 (.in(controlled_buffer_9_out), .\dist (inputBackShiftM), .out(shifter_9_out));
  Shifter #(.width(30)) shifter_10 (.in(controlled_buffer_10_out), .\dist (inputBackShiftM), .out(shifter_10_out));
  assign not_1_out = ~inputBackShiftM;  // NOT_Gate not_1, 5 bits wide
  Adder #(.width(5)) adder_2 (.a(not_1_out), .b(5'b00001), .out(adder_2_out));  // open: cin, cout
  Adder #(.width(5)) adder_3 (.a(5'b11110), .b(adder_2_out), .out(adder_3_out));  // open: cin, cout
  assign controlled_buffer_11_out = or_2_out ? {30{1'b0}} : 30'bz;  // Controlled_Buffer controlled_buffer_11
  Pull_Resistor pull_resistor_13 (.node(controlled_buffer_11_out));
  Shifter #(.width(30), .shift("lr")) shifter_11 (
    .in(controlled_buffer_11_out), .\dist (adder_3_out), .out(shifter_11_out));
  Pull_Resistor pull_resistor_14 (.node(pull_resistor_14_node));
  assign pull_resistor_14_node = or_2_out ? {30{1'b1}} : 30'bz;  // Controlled_Buffer controlled_buffer_12
  Shifter #(.width(30), .shift("lr")) shifter_12 (
    .in(pull_resistor_14_node), .\dist (adder_3_out), .out(shifter_12_out));
  assign controlled_buffer_13_out = or_2_out ? 30'h2fbfcfef : 30'bz;  // Controlled_Buffer controlled_buffer_13
  Pull_Resistor pull_resistor_15 (.node(controlled_buffer_13_out));
  Shifter #(.width(30), .shift("lr")) shifter_13 (
    .in(controlled_buffer_13_out), .\dist (adder_3_out), .out(shifter_13_out));
  Pull_Resistor pull_resistor_16 (.node(pull_resistor_16_node));
  assign pull_resistor_16_node = or_2_out ? 30'h3fafafaf : 30'bz;  // Controlled_Buffer controlled_buffer_14
  Shifter #(.width(30), .shift("lr")) shifter_14 (
    .in(pull_resistor_16_node), .\dist (adder_3_out), .out(shifter_14_out));
  assign controlled_buffer_15_out = or_2_out ? 30'h3eeeeeee : 30'bz;  // Controlled_Buffer controlled_buffer_15
  Pull_Resistor pull_resistor_17 (.node(controlled_buffer_15_out));
  Shifter #(.width(30), .shift("lr")) shifter_15 (
    .in(controlled_buffer_15_out), .\dist (adder_3_out), .out(shifter_15_out));
  assign controlled_buffer_16_out = or_2_out ? 30'h2edfbafa : 30'bz;  // Controlled_Buffer controlled_buffer_16
  Pull_Resistor pull_resistor_18 (.node(controlled_buffer_16_out));
  Shifter #(.width(30), .shift("lr")) shifter_16 (
    .in(controlled_buffer_16_out), .\dist (adder_3_out), .out(shifter_16_out));
  assign controlled_buffer_17_out = or_2_out ? {30{1'b1}} : 30'bz;  // Controlled_Buffer controlled_buffer_17
  Pull_Resistor pull_resistor_19 (.node(controlled_buffer_17_out));
  Shifter #(.width(30), .shift("lr")) shifter_17 (
    .in(controlled_buffer_17_out), .\dist (adder_3_out), .out(shifter_17_out));
  Pull_Resistor pull_resistor_20 (.node(pull_resistor_20_node));
  assign pull_resistor_20_node = or_2_out ? 30'h3f7ba9f : 30'bz;  // Controlled_Buffer controlled_buffer_18
  Shifter #(.width(30), .shift("lr")) shifter_18 (
    .in(pull_resistor_20_node), .\dist (adder_3_out), .out(shifter_18_out));
  Pull_Resistor pull_resistor_21 (.node(pull_resistor_21_node));
  assign pull_resistor_21_node = or_2_out ? {30{1'b1}} : 30'bz;  // Controlled_Buffer controlled_buffer_19
  Shifter #(.width(30), .shift("lr")) shifter_19 (
    .in(pull_resistor_21_node), .\dist (adder_3_out), .out(shifter_19_out));
  Pull_Resistor pull_resistor_22 (.node(pull_resistor_22_node));
  assign pull_resistor_22_node = or_2_out ? {30{1'b0}} : 30'bz;  // Controlled_Buffer controlled_buffer_20
  Shifter #(.width(30), .shift("lr")) shifter_20 (
    .in(pull_resistor_22_node), .\dist (adder_3_out), .out(shifter_20_out));
  Pull_Resistor pull_resistor_23 (.node(or_2_out));
  Adder #(.width(2)) adder_4 (.a(inPlayerShiftD), .b(2'b01), .out(outPlayerShiftD));  // open: cin, cout
  Pull_Resistor pull_resistor_24 (.node(inPlayerShiftM));
  assign toBackground = shifter_1_out | shifter_11_out;  // OR_Gate or_3, 30 bits wide
  assign toBackground_2 = shifter_2_out | shifter_12_out;  // OR_Gate or_4, 30 bits wide
  assign toBackground_3 = shifter_3_out | shifter_13_out;  // OR_Gate or_5, 30 bits wide
  assign toBackground_4 = shifter_4_out | shifter_14_out;  // OR_Gate or_6, 30 bits wide
  assign toBackground_5 = shifter_5_out | shifter_15_out;  // OR_Gate or_7, 30 bits wide
  assign toBackground_6 = shifter_6_out | shifter_16_out;  // OR_Gate or_8, 30 bits wide
  // Probe on adder_5_out
  Adder #(.width(5)) adder_5 (.a(inPlayerShiftM), .b(5'b00001), .out(adder_5_out));  // open: cin, cout
  Comparator #(.width(5), .mode("unsigned")) comparator_5 (
    .a(inPlayerShiftM), .b(5'b11110), .eq(comparator_5_eq));  // open: gt, lt
  assign toBackground_7 = shifter_7_out | shifter_17_out;  // OR_Gate or_9, 30 bits wide
  assign toBackground_8 = shifter_8_out | shifter_18_out;  // OR_Gate or_10, 30 bits wide
  assign toBackground_9 = shifter_9_out | shifter_19_out;  // OR_Gate or_11, 30 bits wide
  assign toBackground_10 = shifter_10_out | shifter_20_out;  // OR_Gate or_12, 30 bits wide
  // Probe on multiplexer_1_out
  Multiplexer #(.width(2), .disabled(0), .enable("false")) multiplexer_1 (
    .in0(inPlayerShiftD), .in1(outPlayerShiftD), .out(multiplexer_1_out), .sel(comparator_5_eq));
  assign controlled_buffer_21_out = inFlag ? comparator_6_eq : 1'bz;  // Controlled_Buffer controlled_buffer_21
  Comparator #(.width(2)) comparator_6 (.a(2'b00), .b(multiplexer_1_out), .eq(comparator_6_eq));  // open: gt, lt
  Comparator #(.width(2)) comparator_7 (.a(2'b00), .b(adder_6_out), .eq(comparator_7_eq));  // open: gt, lt
  assign controlled_buffer_22_out = inFlag ? comparator_7_eq : 1'bz;  // Controlled_Buffer controlled_buffer_22
  Adder #(.width(2)) adder_6 (.a(multiplexer_1_out), .b(2'b01), .out(adder_6_out));  // open: cin, cout
  Pull_Resistor pull_resistor_25 (.node(pull_resistor_25_node));
  assign pull_resistor_25_node = controlled_buffer_21_out ? 30'h279 : 30'bz;  // Controlled_Buffer controlled_buffer_23
  Pull_Resistor pull_resistor_26 (.node(controlled_buffer_21_out));
  Pull_Resistor pull_resistor_27 (.node(pull_resistor_27_node));
  assign pull_resistor_27_node = controlled_buffer_21_out ? 30'h231 : 30'bz;  // Controlled_Buffer controlled_buffer_24
  Pull_Resistor pull_resistor_28 (.node(pull_resistor_28_node));
  assign pull_resistor_28_node = controlled_buffer_21_out ? 30'h279 : 30'bz;  // Controlled_Buffer controlled_buffer_25
  Pull_Resistor pull_resistor_29 (.node(pull_resistor_29_node));
  assign pull_resistor_29_node = controlled_buffer_21_out ? 30'h3ff : 30'bz;  // Controlled_Buffer controlled_buffer_26
  Pull_Resistor pull_resistor_30 (.node(pull_resistor_30_node));
  assign pull_resistor_30_node = controlled_buffer_21_out ? 30'hfc : 30'bz;  // Controlled_Buffer controlled_buffer_27
  assign controlled_buffer_28_out = controlled_buffer_21_out ? 30'hfc : 30'bz;  // Controlled_Buffer controlled_buffer_28
  Pull_Resistor pull_resistor_31 (.node(controlled_buffer_28_out));
  Pull_Resistor pull_resistor_32 (.node(pull_resistor_32_node));
  assign pull_resistor_32_node = controlled_buffer_21_out ? 30'h3ff : 30'bz;  // Controlled_Buffer controlled_buffer_29
  Pull_Resistor pull_resistor_33 (.node(pull_resistor_33_node));
  assign pull_resistor_33_node = controlled_buffer_21_out ? 30'h279 : 30'bz;  // Controlled_Buffer controlled_buffer_30
  assign controlled_buffer_31_out = controlled_buffer_21_out ? 30'h231 : 30'bz;  // Controlled_Buffer controlled_buffer_31
  Pull_Resistor pull_resistor_34 (.node(controlled_buffer_31_out));
  assign controlled_buffer_32_out = controlled_buffer_21_out ? 30'h201 : 30'bz;  // Controlled_Buffer controlled_buffer_32
  Pull_Resistor pull_resistor_35 (.node(controlled_buffer_32_out));
  Shifter #(.width(30)) shifter_21 (.in(pull_resistor_25_node), .\dist (adder_5_out), .out(shifter_21_out));
  Shifter #(.width(30)) shifter_22 (.in(pull_resistor_27_node), .\dist (adder_5_out), .out(shifter_22_out));
  Shifter #(.width(30)) shifter_23 (.in(pull_resistor_28_node), .\dist (adder_5_out), .out(shifter_23_out));
  Shifter #(.width(30)) shifter_24 (.in(pull_resistor_29_node), .\dist (adder_5_out), .out(shifter_24_out));
  Shifter #(.width(30)) shifter_25 (.in(pull_resistor_30_node), .\dist (adder_5_out), .out(shifter_25_out));
  Shifter #(.width(30)) shifter_26 (.in(controlled_buffer_28_out), .\dist (adder_5_out), .out(shifter_26_out));
  Shifter #(.width(30)) shifter_27 (.in(pull_resistor_32_node), .\dist (adder_5_out), .out(shifter_27_out));
  Shifter #(.width(30)) shifter_28 (.in(pull_resistor_33_node), .\dist (adder_5_out), .out(shifter_28_out));
  Shifter #(.width(30)) shifter_29 (.in(controlled_buffer_31_out), .\dist (adder_5_out), .out(shifter_29_out));
  Shifter #(.width(30)) shifter_30 (.in(controlled_buffer_32_out), .\dist (adder_5_out), .out(shifter_30_out));
  assign not_2_out = ~adder_5_out;  // NOT_Gate not_2, 5 bits wide
  Adder #(.width(5)) adder_7 (.a(not_2_out), .b(5'b00001), .out(adder_7_out));  // open: cin, cout
  Pull_Resistor pull_resistor_36 (.node(controlled_buffer_22_out));
  Adder #(.width(5)) adder_8 (.a(5'b11110), .b(adder_7_out), .out(adder_8_out));  // open: cin, cout
  assign controlled_buffer_33_out = controlled_buffer_22_out ? 30'h279 : 30'bz;  // Controlled_Buffer controlled_buffer_33
  Pull_Resistor pull_resistor_37 (.node(controlled_buffer_33_out));
  Shifter #(.width(30), .shift("lr")) shifter_31 (
    .in(controlled_buffer_33_out), .\dist (adder_8_out), .out(shifter_31_out));
  Pull_Resistor pull_resistor_38 (.node(pull_resistor_38_node));
  assign pull_resistor_38_node = controlled_buffer_22_out ? 30'h231 : 30'bz;  // Controlled_Buffer controlled_buffer_34
  Shifter #(.width(30), .shift("lr")) shifter_32 (
    .in(pull_resistor_38_node), .\dist (adder_8_out), .out(shifter_32_out));
  Pull_Resistor pull_resistor_39 (.node(pull_resistor_39_node));
  assign pull_resistor_39_node = controlled_buffer_22_out ? 30'h279 : 30'bz;  // Controlled_Buffer controlled_buffer_35
  Shifter #(.width(30), .shift("lr")) shifter_33 (
    .in(pull_resistor_39_node), .\dist (adder_8_out), .out(shifter_33_out));
  assign controlled_buffer_36_out = controlled_buffer_22_out ? 30'h3ff : 30'bz;  // Controlled_Buffer controlled_buffer_36
  Pull_Resistor pull_resistor_40 (.node(controlled_buffer_36_out));
  Shifter #(.width(30), .shift("lr")) shifter_34 (
    .in(controlled_buffer_36_out), .\dist (adder_8_out), .out(shifter_34_out));
  Pull_Resistor pull_resistor_41 (.node(pull_resistor_41_node));
  assign pull_resistor_41_node = controlled_buffer_22_out ? 30'hfc : 30'bz;  // Controlled_Buffer controlled_buffer_37
  Shifter #(.width(30), .shift("lr")) shifter_35 (
    .in(pull_resistor_41_node), .\dist (adder_8_out), .out(shifter_35_out));
  assign controlled_buffer_38_out = controlled_buffer_22_out ? 30'hfc : 30'bz;  // Controlled_Buffer controlled_buffer_38
  Pull_Resistor pull_resistor_42 (.node(controlled_buffer_38_out));
  Shifter #(.width(30), .shift("lr")) shifter_36 (
    .in(controlled_buffer_38_out), .\dist (adder_8_out), .out(shifter_36_out));
  Pull_Resistor pull_resistor_43 (.node(pull_resistor_43_node));
  assign pull_resistor_43_node = controlled_buffer_22_out ? 30'h3ff : 30'bz;  // Controlled_Buffer controlled_buffer_39
  Shifter #(.width(30), .shift("lr")) shifter_37 (
    .in(pull_resistor_43_node), .\dist (adder_8_out), .out(shifter_37_out));
  assign controlled_buffer_40_out = controlled_buffer_22_out ? 30'h279 : 30'bz;  // Controlled_Buffer controlled_buffer_40
  Pull_Resistor pull_resistor_44 (.node(controlled_buffer_40_out));
  Shifter #(.width(30), .shift("lr")) shifter_38 (
    .in(controlled_buffer_40_out), .\dist (adder_8_out), .out(shifter_38_out));
  assign controlled_buffer_41_out = controlled_buffer_22_out ? 30'h231 : 30'bz;  // Controlled_Buffer controlled_buffer_41
  Pull_Resistor pull_resistor_45 (.node(controlled_buffer_41_out));
  Shifter #(.width(30), .shift("lr")) shifter_39 (
    .in(controlled_buffer_41_out), .\dist (adder_8_out), .out(shifter_39_out));
  assign controlled_buffer_42_out = controlled_buffer_22_out ? 30'h201 : 30'bz;  // Controlled_Buffer controlled_buffer_42
  Pull_Resistor pull_resistor_46 (.node(controlled_buffer_42_out));
  Shifter #(.width(30), .shift("lr")) shifter_40 (
    .in(controlled_buffer_42_out), .\dist (adder_8_out), .out(shifter_40_out));
  assign toFront = shifter_21_out | shifter_31_out;  // OR_Gate or_13, 30 bits wide
  assign toFront_2 = shifter_22_out | shifter_32_out;  // OR_Gate or_14, 30 bits wide
  assign toFront_3 = shifter_23_out | shifter_33_out;  // OR_Gate or_15, 30 bits wide
  assign toFront_4 = shifter_24_out | shifter_34_out;  // OR_Gate or_16, 30 bits wide
  assign toFront_5 = shifter_25_out | shifter_35_out;  // OR_Gate or_17, 30 bits wide
  assign toFront_6 = shifter_26_out | shifter_36_out;  // OR_Gate or_18, 30 bits wide
  assign toFront_7 = shifter_27_out | shifter_37_out;  // OR_Gate or_19, 30 bits wide
  assign toFront_8 = shifter_28_out | shifter_38_out;  // OR_Gate or_20, 30 bits wide
  assign toFront_9 = shifter_29_out | shifter_39_out;  // OR_Gate or_21, 30 bits wide
  assign toFront_10 = shifter_30_out | shifter_40_out;  // OR_Gate or_22, 30 bits wide

  assign outFlag = inFlag;
  assign outPlayerShiftM = inPlayerShiftM;
  assign outputBackShiftM = inputBackShiftM;

  // Notes on the sheet:
  //   MAKE SHIFT BY NEXT MATRICE
  //   MAKE SHIFT IN CURRENT MATRICE
  //   MAKE SHIFT IN CURRENT MATRICE
  //   MAKE SHIFT BY NEXT MATRICE
endmodule

module documentation (
);

  leftShifter leftshifter_1 ();  // open: shiftD, shiftCounts, shiftM, tactGen, reset
  rightShifter rightshifter_1 ();  // open: shiftM, shiftD, shiftCounts, tactGen, reset
  computeIntresection computeintresection_1 ();  // open: backLen, inBackM, inBackD, inFrogD, outIntersect, inFrogM, inIntersect, doCompute
  heightFlag heightflag_1 ();  // open: height, playerY, eqY
  controller controller_1 ();  // open: D, A, shiftM, shiftD, reset
  carConnectorV2 carconnectorv2_1 ();  // open: inBackShiftD, outBackShiftD, inputBackShiftM, outputBackShiftM, outPlayerShiftD, inPlayerShiftM, outPlayerShiftM, inFlag, outFlag, toBackground, toBackground_2, toBackground_3, toBackground_4, toBackground_5, toBackground_6, toBackground_7, toBackground_8, toBackground_9, toBackground_10, toFront, toFront_2, toFront_3, toFront_4, toFront_5, toFront_6, toFront_7, toFront_8, toFront_9, toFront_10, inPlayerShiftD

  // Notes on the sheet:
  //   temporary keyboard
  //   it gives a picture by all shifts
  //   similar for previous, but decline shift (move cars right) 
  //   compute intersection buy PM, PD, BM, BD
  //   PM - shift on player's matrice (0-20) determine where on matrice is placed frog
  //   PB - shift on player's display (0-3) determine in which matrice player placed
  //   BM and BD - are similar for prefious, but it for cars / logs / trurtles, not for frog
  //   plain thing - return 0/1 if frog on the same level as this thing (defined by constant)
  //   increase shift (models move left), receive tact (tik), and res signal, give matrice shift (0-20) and display shift (0-3)
endmodule

module log_1x1 (
  input  [1:0] inBackShiftD,
  input  [4:0] inputBackShiftM,
  input  [1:0] inPlayerShiftD,
  input  [4:0] inPlayerShiftM,
  input  inFlag,
  output [29:0] toBackground,
  output [29:0] toBackground_2,
  output [29:0] toBackground_3,
  output [29:0] toBackground_4,
  output [29:0] toBackground_5,
  output [1:0] outBackShiftD,
  output [29:0] toBackground_6,
  output [29:0] toBackground_7,
  output [4:0] outputBackShiftM,
  output [29:0] toBackground_8,
  output [29:0] toBackground_9,
  output [29:0] toBackground_10,
  output [29:0] toFront,
  output [29:0] toFront_2,
  output [29:0] toFront_3,
  output [29:0] toFront_4,
  output [29:0] toFront_5,
  output [29:0] toFront_6,
  output [1:0] outPlayerShiftD,
  output [4:0] outPlayerShiftM,
  output [29:0] toFront_7,
  output outFlag,
  output [29:0] toFront_8,
  output [29:0] toFront_9,
  output [29:0] toFront_10
);

  wire comparator_1_eq, comparator_2_eq, comparator_3_eq, comparator_4_eq, comparator_5_eq, comparator_6_eq,
       comparator_7_eq, comparator_8_eq, comparator_9_eq, comparator_10_eq, comparator_11_eq,
       controlled_buffer_21_out, controlled_buffer_22_out, or_1_out, or_2_out, or_3_out, or_4_out, or_5_out,
       or_6_out;
  wire [1:0] adder_6_out, multiplexer_1_out;
  wire [4:0] adder_2_out, adder_3_out, adder_5_out, adder_7_out, adder_8_out, not_1_out, not_2_out;
  wire [29:0] controlled_buffer_2_out, controlled_buffer_3_out, controlled_buffer_6_out,
       controlled_buffer_7_out, controlled_buffer_11_out, controlled_buffer_12_out, controlled_buffer_13_out,
       controlled_buffer_14_out, controlled_buffer_16_out, controlled_buffer_17_out,
       controlled_buffer_18_out, controlled_buffer_19_out, controlled_buffer_23_out,
       controlled_buffer_24_out, controlled_buffer_25_out, controlled_buffer_26_out,
       controlled_buffer_28_out, controlled_buffer_30_out, controlled_buffer_31_out,
       controlled_buffer_33_out, controlled_buffer_35_out, controlled_buffer_36_out,
       controlled_buffer_39_out, controlled_buffer_40_out, controlled_buffer_42_out, pull_resistor_3_node,
       pull_resistor_6_node, pull_resistor_7_node, pull_resistor_10_node, pull_resistor_11_node,
       pull_resistor_12_node, pull_resistor_17_node, pull_resistor_22_node, pull_resistor_30_node,
       pull_resistor_32_node, pull_resistor_35_node, pull_resistor_38_node, pull_resistor_41_node,
       pull_resistor_42_node, pull_resistor_45_node, shifter_1_out, shifter_2_out, shifter_3_out,
       shifter_4_out, shifter_5_out, shifter_6_out, shifter_7_out, shifter_8_out, shifter_9_out,
       shifter_10_out, shifter_11_out, shifter_12_out, shifter_13_out, shifter_14_out, shifter_15_out,
       shifter_16_out, shifter_17_out, shifter_18_out, shifter_19_out, shifter_20_out, shifter_21_out,
       shifter_22_out, shifter_23_out, shifter_24_out, shifter_25_out, shifter_26_out, shifter_27_out,
       shifter_28_out, shifter_29_out, shifter_30_out, shifter_31_out, shifter_32_out, shifter_33_out,
       shifter_34_out, shifter_35_out, shifter_36_out, shifter_37_out, shifter_38_out, shifter_39_out,
       shifter_40_out;

  Adder #(.width(2)) adder_1 (.a(inBackShiftD), .b(2'b01), .out(outBackShiftD));  // open: cin, cout
  Pull_Resistor pull_resistor_1 (.node(inputBackShiftM));
  Comparator #(.width(2)) comparator_1 (.a(inBackShiftD), .b(2'b11), .eq(comparator_1_eq));  // open: gt, lt
  Comparator #(.width(2)) comparator_2 (.a(2'b01), .b(inBackShiftD), .eq(comparator_2_eq));  // open: gt, lt
  Comparator #(.width(2)) comparator_3 (.a(inBackShiftD), .b(2'b10), .eq(comparator_3_eq));  // open: gt, lt
  Comparator #(.width(2)) comparator_4 (.a(2'b00), .b(inBackShiftD), .eq(comparator_4_eq));  // open: gt, lt
  // Probe on outBackShiftD
  or or_1 (or_1_out, comparator_1_eq, comparator_2_eq);
  or or_2 (or_2_out, or_1_out, or_3_out);
  or or_3 (or_3_out, comparator_3_eq, comparator_4_eq);
  Comparator #(.width(2)) comparator_5 (.a(outBackShiftD), .b(2'b11), .eq(comparator_5_eq));  // open: gt, lt
  or or_4 (or_4_out, comparator_5_eq, comparator_6_eq);
  Comparator #(.width(2)) comparator_6 (.a(2'b01), .b(outBackShiftD), .eq(comparator_6_eq));  // open: gt, lt
  Comparator #(.width(2)) comparator_7 (.a(outBackShiftD), .b(2'b10), .eq(comparator_7_eq));  // open: gt, lt
  or or_5 (or_5_out, comparator_7_eq, comparator_8_eq);
  Comparator #(.width(2)) comparator_8 (.a(2'b00), .b(outBackShiftD), .eq(comparator_8_eq));  // open: gt, lt
  or or_6 (or_6_out, or_4_out, or_5_out);
  Pull_Resistor pull_resistor_2 (.node(or_2_out));
  Pull_Resistor pull_resistor_3 (.node(pull_resistor_3_node));
  assign pull_resistor_3_node = or_2_out ? {30{1'b0}} : 30'bz;  // Controlled_Buffer controlled_buffer_1
  assign controlled_buffer_2_out = or_2_out ? {30{1'b0}} : 30'bz;  // Controlled_Buffer controlled_buffer_2
  Pull_Resistor pull_resistor_4 (.node(controlled_buffer_2_out));
  assign controlled_buffer_3_out = or_2_out ? 30'h3ff : 30'bz;  // Controlled_Buffer controlled_buffer_3
  Pull_Resistor pull_resistor_5 (.node(controlled_buffer_3_out));
  Pull_Resistor pull_resistor_6 (.node(pull_resistor_6_node));
  assign pull_resistor_6_node = or_2_out ? 30'h3f9 : 30'bz;  // Controlled_Buffer controlled_buffer_4
  Pull_Resistor pull_resistor_7 (.node(pull_resistor_7_node));
  assign pull_resistor_7_node = or_2_out ? 30'h3ff : 30'bz;  // Controlled_Buffer controlled_buffer_5
  assign controlled_buffer_6_out = or_2_out ? 30'h3aa : 30'bz;  // Controlled_Buffer controlled_buffer_6
  Pull_Resistor pull_resistor_8 (.node(controlled_buffer_6_out));
  assign controlled_buffer_7_out = or_2_out ? 30'h3fe : 30'bz;  // Controlled_Buffer controlled_buffer_7
  Pull_Resistor pull_resistor_9 (.node(controlled_buffer_7_out));
  Pull_Resistor pull_resistor_10 (.node(pull_resistor_10_node));
  assign pull_resistor_10_node = or_2_out ? 30'h3ff : 30'bz;  // Controlled_Buffer controlled_buffer_8
  Pull_Resistor pull_resistor_11 (.node(pull_resistor_11_node));
  assign pull_resistor_11_node = or_2_out ? {30{1'b0}} : 30'bz;  // Controlled_Buffer controlled_buffer_9
  Pull_Resistor pull_resistor_12 (.node(pull_resistor_12_node));
  assign pull_resistor_12_node = or_2_out ? {30{1'b0}} : 30'bz;  // Controlled_Buffer controlled_buffer_10
  Shifter #(.width(30)) shifter_1 (.in(pull_resistor_3_node), .\dist (inputBackShiftM), .out(shifter_1_out));
  Shifter #(.width(30)) shifter_2 (.in(controlled_buffer_2_out), .\dist (inputBackShiftM), .out(shifter_2_out));
  Shifter #(.width(30)) shifter_3 (.in(controlled_buffer_3_out), .\dist (inputBackShiftM), .out(shifter_3_out));
  Shifter #(.width(30)) shifter_4 (.in(pull_resistor_6_node), .\dist (inputBackShiftM), .out(shifter_4_out));
  Shifter #(.width(30)) shifter_5 (.in(pull_resistor_7_node), .\dist (inputBackShiftM), .out(shifter_5_out));
  Shifter #(.width(30)) shifter_6 (.in(controlled_buffer_6_out), .\dist (inputBackShiftM), .out(shifter_6_out));
  Shifter #(.width(30)) shifter_7 (.in(controlled_buffer_7_out), .\dist (inputBackShiftM), .out(shifter_7_out));
  Shifter #(.width(30)) shifter_8 (.in(pull_resistor_10_node), .\dist (inputBackShiftM), .out(shifter_8_out));
  Shifter #(.width(30)) shifter_9 (.in(pull_resistor_11_node), .\dist (inputBackShiftM), .out(shifter_9_out));
  Shifter #(.width(30)) shifter_10 (.in(pull_resistor_12_node), .\dist (inputBackShiftM), .out(shifter_10_out));
  assign not_1_out = ~inputBackShiftM;  // NOT_Gate not_1, 5 bits wide
  Adder #(.width(5)) adder_2 (.a(not_1_out), .b(5'b00001), .out(adder_2_out));  // open: cin, cout
  Adder #(.width(5)) adder_3 (.a(5'b11110), .b(adder_2_out), .out(adder_3_out));  // open: cin, cout
  assign controlled_buffer_11_out = or_6_out ? {30{1'b0}} : 30'bz;  // Controlled_Buffer controlled_buffer_11
  Pull_Resistor pull_resistor_13 (.node(controlled_buffer_11_out));
  Shifter #(.width(30), .shift("lr")) shifter_11 (
    .in(controlled_buffer_11_out), .\dist (adder_3_out), .out(shifter_11_out));
  assign controlled_buffer_12_out = or_6_out ? {30{1'b0}} : 30'bz;  // Controlled_Buffer controlled_buffer_12
  Pull_Resistor pull_resistor_14 (.node(controlled_buffer_12_out));
  Shifter #(.width(30), .shift("lr")) shifter_12 (
    .in(controlled_buffer_12_out), .\dist (adder_3_out), .out(shifter_12_out));
  assign controlled_buffer_13_out = or_6_out ? 30'h3ff : 30'bz;  // Controlled_Buffer controlled_buffer_13
  Pull_Resistor pull_resistor_15 (.node(controlled_buffer_13_out));
  Shifter #(.width(30), .shift("lr")) shifter_13 (
    .in(controlled_buffer_13_out), .\dist (adder_3_out), .out(shifter_13_out));
  assign controlled_buffer_14_out = or_6_out ? 30'h3f9 : 30'bz;  // Controlled_Buffer controlled_buffer_14
  Pull_Resistor pull_resistor_16 (.node(controlled_buffer_14_out));
  Shifter #(.width(30), .shift("lr")) shifter_14 (
    .in(controlled_buffer_14_out), .\dist (adder_3_out), .out(shifter_14_out));
  Pull_Resistor pull_resistor_17 (.node(pull_resistor_17_node));
  assign pull_resistor_17_node = or_6_out ? 30'h3ff : 30'bz;  // Controlled_Buffer controlled_buffer_15
  Shifter #(.width(30), .shift("lr")) shifter_15 (
    .in(pull_resistor_17_node), .\dist (adder_3_out), .out(shifter_15_out));
  assign controlled_buffer_16_out = or_6_out ? 30'h3aa : 30'bz;  // Controlled_Buffer controlled_buffer_16
  Pull_Resistor pull_resistor_18 (.node(controlled_buffer_16_out));
  Shifter #(.width(30), .shift("lr")) shifter_16 (
    .in(controlled_buffer_16_out), .\dist (adder_3_out), .out(shifter_16_out));
  assign controlled_buffer_17_out = or_6_out ? 30'h3fe : 30'bz;  // Controlled_Buffer controlled_buffer_17
  Pull_Resistor pull_resistor_19 (.node(controlled_buffer_17_out));
  Shifter #(.width(30), .shift("lr")) shifter_17 (
    .in(controlled_buffer_17_out), .\dist (adder_3_out), .out(shifter_17_out));
  assign controlled_buffer_18_out = or_6_out ? 30'h3ff : 30'bz;  // Controlled_Buffer controlled_buffer_18
  Pull_Resistor pull_resistor_20 (.node(controlled_buffer_18_out));
  Shifter #(.width(30), .shift("lr")) shifter_18 (
    .in(controlled_buffer_18_out), .\dist (adder_3_out), .out(shifter_18_out));
  assign controlled_buffer_19_out = or_6_out ? {30{1'b0}} : 30'bz;  // Controlled_Buffer controlled_buffer_19
  Pull_Resistor pull_resistor_21 (.node(controlled_buffer_19_out));
  Shifter #(.width(30), .shift("lr")) shifter_19 (
    .in(controlled_buffer_19_out), .\dist (adder_3_out), .out(shifter_19_out));
  Pull_Resistor pull_resistor_22 (.node(pull_resistor_22_node));
  assign pull_resistor_22_node = or_6_out ? {30{1'b0}} : 30'bz;  // Controlled_Buffer controlled_buffer_20
  Shifter #(.width(30), .shift("lr")) shifter_20 (
    .in(pull_resistor_22_node), .\dist (adder_3_out), .out(shifter_20_out));
  Pull_Resistor pull_resistor_23 (.node(or_6_out));
  Adder #(.width(2)) adder_4 (.a(inPlayerShiftD), .b(2'b01), .out(outPlayerShiftD));  // open: cin, cout
  Pull_Resistor pull_resistor_24 (.node(inPlayerShiftM));
  assign toBackground = shifter_1_out | shifter_11_out;  // OR_Gate or_7, 30 bits wide
  assign toBackground_2 = shifter_2_out | shifter_12_out;  // OR_Gate or_8, 30 bits wide
  assign toBackground_3 = shifter_3_out | shifter_13_out;  // OR_Gate or_9, 30 bits wide
  assign toBackground_4 = shifter_4_out | shifter_14_out;  // OR_Gate or_10, 30 bits wide
  assign toBackground_5 = shifter_5_out | shifter_15_out;  // OR_Gate or_11, 30 bits wide
  assign toBackground_6 = shifter_6_out | shifter_16_out;  // OR_Gate or_12, 30 bits wide
  // Probe on adder_5_out
  Adder #(.width(5)) adder_5 (.a(inPlayerShiftM), .b(5'b00001), .out(adder_5_out));  // open: cin, cout
  Comparator #(.width(5), .mode("unsigned")) comparator_9 (
    .a(inPlayerShiftM), .b(5'b11110), .eq(comparator_9_eq));  // open: gt, lt
  assign toBackground_7 = shifter_7_out | shifter_17_out;  // OR_Gate or_13, 30 bits wide
  assign toBackground_8 = shifter_8_out | shifter_18_out;  // OR_Gate or_14, 30 bits wide
  assign toBackground_9 = shifter_9_out | shifter_19_out;  // OR_Gate or_15, 30 bits wide
  assign toBackground_10 = shifter_10_out | shifter_20_out;  // OR_Gate or_16, 30 bits wide
  // Probe on multiplexer_1_out
  Multiplexer #(.width(2), .disabled(0), .enable("false")) multiplexer_1 (
    .in0(inPlayerShiftD), .in1(outPlayerShiftD), .out(multiplexer_1_out), .sel(comparator_9_eq));
  Comparator #(.width(2)) comparator_10 (.a(2'b00), .b(multiplexer_1_out), .eq(comparator_10_eq));  // open: gt, lt
  assign controlled_buffer_21_out = inFlag ? comparator_10_eq : 1'bz;  // Controlled_Buffer controlled_buffer_21
  Comparator #(.width(2)) comparator_11 (.a(2'b00), .b(adder_6_out), .eq(comparator_11_eq));  // open: gt, lt
  assign controlled_buffer_22_out = inFlag ? comparator_11_eq : 1'bz;  // Controlled_Buffer controlled_buffer_22
  Adder #(.width(2)) adder_6 (.a(multiplexer_1_out), .b(2'b01), .out(adder_6_out));  // open: cin, cout
  assign controlled_buffer_23_out = controlled_buffer_21_out ? 30'h279 : 30'bz;  // Controlled_Buffer controlled_buffer_23
  Pull_Resistor pull_resistor_25 (.node(controlled_buffer_21_out));
  Pull_Resistor pull_resistor_26 (.node(controlled_buffer_23_out));
  assign controlled_buffer_24_out = controlled_buffer_21_out ? 30'h231 : 30'bz;  // Controlled_Buffer controlled_buffer_24
  Pull_Resistor pull_resistor_27 (.node(controlled_buffer_24_out));
  assign controlled_buffer_25_out = controlled_buffer_21_out ? 30'h279 : 30'bz;  // Controlled_Buffer controlled_buffer_25
  Pull_Resistor pull_resistor_28 (.node(controlled_buffer_25_out));
  assign controlled_buffer_26_out = controlled_buffer_21_out ? 30'h3ff : 30'bz;  // Controlled_Buffer controlled_buffer_26
  Pull_Resistor pull_resistor_29 (.node(controlled_buffer_26_out));
  Pull_Resistor pull_resistor_30 (.node(pull_resistor_30_node));
  assign pull_resistor_30_node = controlled_buffer_21_out ? 30'hfc : 30'bz;  // Controlled_Buffer controlled_buffer_27
  assign controlled_buffer_28_out = controlled_buffer_21_out ? 30'hfc : 30'bz;  // Controlled_Buffer controlled_buffer_28
  Pull_Resistor pull_resistor_31 (.node(controlled_buffer_28_out));
  Pull_Resistor pull_resistor_32 (.node(pull_resistor_32_node));
  assign pull_resistor_32_node = controlled_buffer_21_out ? 30'h3ff : 30'bz;  // Controlled_Buffer controlled_buffer_29
  assign controlled_buffer_30_out = controlled_buffer_21_out ? 30'h279 : 30'bz;  // Controlled_Buffer controlled_buffer_30
  Pull_Resistor pull_resistor_33 (.node(controlled_buffer_30_out));
  assign controlled_buffer_31_out = controlled_buffer_21_out ? 30'h231 : 30'bz;  // Controlled_Buffer controlled_buffer_31
  Pull_Resistor pull_resistor_34 (.node(controlled_buffer_31_out));
  Pull_Resistor pull_resistor_35 (.node(pull_resistor_35_node));
  assign pull_resistor_35_node = controlled_buffer_21_out ? 30'h201 : 30'bz;  // Controlled_Buffer controlled_buffer_32
  Shifter #(.width(30)) shifter_21 (.in(controlled_buffer_23_out), .\dist (adder_5_out), .out(shifter_21_out));
  Shifter #(.width(30)) shifter_22 (.in(controlled_buffer_24_out), .\dist (adder_5_out), .out(shifter_22_out));
  Shifter #(.width(30)) shifter_23 (.in(controlled_buffer_25_out), .\dist (adder_5_out), .out(shifter_23_out));
  Shifter #(.width(30)) shifter_24 (.in(controlled_buffer_26_out), .\dist (adder_5_out), .out(shifter_24_out));
  Shifter #(.width(30)) shifter_25 (.in(pull_resistor_30_node), .\dist (adder_5_out), .out(shifter_25_out));
  Shifter #(.width(30)) shifter_26 (.in(controlled_buffer_28_out), .\dist (adder_5_out), .out(shifter_26_out));
  Shifter #(.width(30)) shifter_27 (.in(pull_resistor_32_node), .\dist (adder_5_out), .out(shifter_27_out));
  Shifter #(.width(30)) shifter_28 (.in(controlled_buffer_30_out), .\dist (adder_5_out), .out(shifter_28_out));
  Shifter #(.width(30)) shifter_29 (.in(controlled_buffer_31_out), .\dist (adder_5_out), .out(shifter_29_out));
  Shifter #(.width(30)) shifter_30 (.in(pull_resistor_35_node), .\dist (adder_5_out), .out(shifter_30_out));
  assign not_2_out = ~adder_5_out;  // NOT_Gate not_2, 5 bits wide
  Adder #(.width(5)) adder_7 (.a(not_2_out), .b(5'b00001), .out(adder_7_out));  // open: cin, cout
  Pull_Resistor pull_resistor_36 (.node(controlled_buffer_22_out));
  Adder #(.width(5)) adder_8 (.a(5'b11110), .b(adder_7_out), .out(adder_8_out));  // open: cin, cout
  assign controlled_buffer_33_out = controlled_buffer_22_out ? 30'h279 : 30'bz;  // Controlled_Buffer controlled_buffer_33
  Pull_Resistor pull_resistor_37 (.node(controlled_buffer_33_out));
  Shifter #(.width(30), .shift("lr")) shifter_31 (
    .in(controlled_buffer_33_out), .\dist (adder_8_out), .out(shifter_31_out));
  Pull_Resistor pull_resistor_38 (.node(pull_resistor_38_node));
  assign pull_resistor_38_node = controlled_buffer_22_out ? 30'h231 : 30'bz;  // Controlled_Buffer controlled_buffer_34
  Shifter #(.width(30), .shift("lr")) shifter_32 (
    .in(pull_resistor_38_node), .\dist (adder_8_out), .out(shifter_32_out));
  assign controlled_buffer_35_out = controlled_buffer_22_out ? 30'h279 : 30'bz;  // Controlled_Buffer controlled_buffer_35
  Pull_Resistor pull_resistor_39 (.node(controlled_buffer_35_out));
  Shifter #(.width(30), .shift("lr")) shifter_33 (
    .in(controlled_buffer_35_out), .\dist (adder_8_out), .out(shifter_33_out));
  assign controlled_buffer_36_out = controlled_buffer_22_out ? 30'h3ff : 30'bz;  // Controlled_Buffer controlled_buffer_36
  Pull_Resistor pull_resistor_40 (.node(controlled_buffer_36_out));
  Shifter #(.width(30), .shift("lr")) shifter_34 (
    .in(controlled_buffer_36_out), .\dist (adder_8_out), .out(shifter_34_out));
  Pull_Resistor pull_resistor_41 (.node(pull_resistor_41_node));
  assign pull_resistor_41_node = controlled_buffer_22_out ? 30'hfc : 30'bz;  // Controlled_Buffer controlled_buffer_37
  Shifter #(.width(30), .shift("lr")) shifter_35 (
    .in(pull_resistor_41_node), .\dist (adder_8_out), .out(shifter_35_out));
  Pull_Resistor pull_resistor_42 (.node(pull_resistor_42_node));
  assign pull_resistor_42_node = controlled_buffer_22_out ? 30'hfc : 30'bz;  // Controlled_Buffer controlled_buffer_38
  Shifter #(.width(30), .shift("lr")) shifter_36 (
    .in(pull_resistor_42_node), .\dist (adder_8_out), .out(shifter_36_out));
  assign controlled_buffer_39_out = controlled_buffer_22_out ? 30'h3ff : 30'bz;  // Controlled_Buffer controlled_buffer_39
  Pull_Resistor pull_resistor_43 (.node(controlled_buffer_39_out));
  Shifter #(.width(30), .shift("lr")) shifter_37 (
    .in(controlled_buffer_39_out), .\dist (adder_8_out), .out(shifter_37_out));
  assign controlled_buffer_40_out = controlled_buffer_22_out ? 30'h279 : 30'bz;  // Controlled_Buffer controlled_buffer_40
  Pull_Resistor pull_resistor_44 (.node(controlled_buffer_40_out));
  Shifter #(.width(30), .shift("lr")) shifter_38 (
    .in(controlled_buffer_40_out), .\dist (adder_8_out), .out(shifter_38_out));
  Pull_Resistor pull_resistor_45 (.node(pull_resistor_45_node));
  assign pull_resistor_45_node = controlled_buffer_22_out ? 30'h231 : 30'bz;  // Controlled_Buffer controlled_buffer_41
  Shifter #(.width(30), .shift("lr")) shifter_39 (
    .in(pull_resistor_45_node), .\dist (adder_8_out), .out(shifter_39_out));
  assign controlled_buffer_42_out = controlled_buffer_22_out ? 30'h201 : 30'bz;  // Controlled_Buffer controlled_buffer_42
  Pull_Resistor pull_resistor_46 (.node(controlled_buffer_42_out));
  Shifter #(.width(30), .shift("lr")) shifter_40 (
    .in(controlled_buffer_42_out), .\dist (adder_8_out), .out(shifter_40_out));
  assign toFront = shifter_21_out | shifter_31_out;  // OR_Gate or_17, 30 bits wide
  assign toFront_2 = shifter_22_out | shifter_32_out;  // OR_Gate or_18, 30 bits wide
  assign toFront_3 = shifter_23_out | shifter_33_out;  // OR_Gate or_19, 30 bits wide
  assign toFront_4 = shifter_24_out | shifter_34_out;  // OR_Gate or_20, 30 bits wide
  assign toFront_5 = shifter_25_out | shifter_35_out;  // OR_Gate or_21, 30 bits wide
  assign toFront_6 = shifter_26_out | shifter_36_out;  // OR_Gate or_22, 30 bits wide
  assign toFront_7 = shifter_27_out | shifter_37_out;  // OR_Gate or_23, 30 bits wide
  assign toFront_8 = shifter_28_out | shifter_38_out;  // OR_Gate or_24, 30 bits wide
  assign toFront_9 = shifter_29_out | shifter_39_out;  // OR_Gate or_25, 30 bits wide
  assign toFront_10 = shifter_30_out | shifter_40_out;  // OR_Gate or_26, 30 bits wide

  assign outFlag = inFlag;
  assign outPlayerShiftM = inPlayerShiftM;
  assign outputBackShiftM = inputBackShiftM;

  // Notes on the sheet:
  //   MAKE SHIFT BY NEXT MATRICE
  //   MAKE SHIFT IN CURRENT MATRICE
  //   MAKE SHIFT IN CURRENT MATRICE
  //   MAKE SHIFT BY NEXT MATRICE
endmodule

module log_2x1 (
  input  [1:0] inBackShiftD,
  input  [4:0] inputBackShiftM,
  input  [1:0] inPlayerShiftD,
  input  [4:0] inPlayerShiftM,
  input  inFlag,
  output [29:0] toBackground,
  output [29:0] toBackground_2,
  output [29:0] toBackground_3,
  output [29:0] toBackground_4,
  output [29:0] toBackground_5,
  output [1:0] outBackShiftD,
  output [29:0] toBackground_6,
  output [29:0] toBackground_7,
  output [4:0] outputBackShiftM,
  output [29:0] toBackground_8,
  output [29:0] toBackground_9,
  output [29:0] toBackground_10,
  output [29:0] toFront,
  output [29:0] toFront_2,
  output [29:0] toFront_3,
  output [29:0] toFront_4,
  output [29:0] toFront_5,
  output [29:0] toFront_6,
  output [1:0] outPlayerShiftD,
  output [4:0] outPlayerShiftM,
  output [29:0] toFront_7,
  output outFlag,
  output [29:0] toFront_8,
  output [29:0] toFront_9,
  output [29:0] toFront_10
);

  wire comparator_1_eq, comparator_2_eq, comparator_3_eq, comparator_4_eq, comparator_5_eq, comparator_6_eq,
       comparator_7_eq, controlled_buffer_21_out, controlled_buffer_22_out, or_1_out, or_2_out;
  wire [1:0] adder_6_out, multiplexer_1_out;
  wire [4:0] adder_2_out, adder_3_out, adder_5_out, adder_7_out, adder_8_out, not_1_out, not_2_out;
  wire [29:0] controlled_buffer_4_out, controlled_buffer_6_out, controlled_buffer_8_out,
       controlled_buffer_10_out, controlled_buffer_12_out, controlled_buffer_13_out,
       controlled_buffer_14_out, controlled_buffer_15_out, controlled_buffer_16_out,
       controlled_buffer_17_out, controlled_buffer_18_out, controlled_buffer_19_out,
       controlled_buffer_20_out, controlled_buffer_25_out, controlled_buffer_28_out,
       controlled_buffer_29_out, controlled_buffer_30_out, controlled_buffer_31_out,
       controlled_buffer_32_out, controlled_buffer_33_out, controlled_buffer_36_out,
       controlled_buffer_38_out, controlled_buffer_40_out, controlled_buffer_41_out, pull_resistor_3_node,
       pull_resistor_4_node, pull_resistor_5_node, pull_resistor_7_node, pull_resistor_9_node,
       pull_resistor_11_node, pull_resistor_13_node, pull_resistor_25_node, pull_resistor_27_node,
       pull_resistor_29_node, pull_resistor_30_node, pull_resistor_38_node, pull_resistor_39_node,
       pull_resistor_41_node, pull_resistor_43_node, pull_resistor_46_node, shifter_1_out, shifter_2_out,
       shifter_3_out, shifter_4_out, shifter_5_out, shifter_6_out, shifter_7_out, shifter_8_out,
       shifter_9_out, shifter_10_out, shifter_11_out, shifter_12_out, shifter_13_out, shifter_14_out,
       shifter_15_out, shifter_16_out, shifter_17_out, shifter_18_out, shifter_19_out, shifter_20_out,
       shifter_21_out, shifter_22_out, shifter_23_out, shifter_24_out, shifter_25_out, shifter_26_out,
       shifter_27_out, shifter_28_out, shifter_29_out, shifter_30_out, shifter_31_out, shifter_32_out,
       shifter_33_out, shifter_34_out, shifter_35_out, shifter_36_out, shifter_37_out, shifter_38_out,
       shifter_39_out, shifter_40_out;

  Adder #(.width(2)) adder_1 (.a(inBackShiftD), .b(2'b01), .out(outBackShiftD));  // open: cin, cout
  Pull_Resistor pull_resistor_1 (.node(inputBackShiftM));
  Comparator #(.width(2)) comparator_1 (.a(inBackShiftD), .b(2'b10), .eq(comparator_1_eq));  // open: gt, lt
  Comparator #(.width(2)) comparator_2 (.a(2'b00), .b(inBackShiftD), .eq(comparator_2_eq));  // open: gt, lt
  // Probe on outBackShiftD
  or or_1 (or_1_out, comparator_1_eq, comparator_2_eq);
  Comparator #(.width(2)) comparator_3 (.a(outBackShiftD), .b(2'b10), .eq(comparator_3_eq));  // open: gt, lt
  or or_2 (or_2_out, comparator_3_eq, comparator_4_eq);
  Comparator #(.width(2)) comparator_4 (.a(2'b00), .b(outBackShiftD), .eq(comparator_4_eq));  // open: gt, lt
  Pull_Resistor pull_resistor_2 (.node(or_1_out));
  Pull_Resistor pull_resistor_3 (.node(pull_resistor_3_node));
  assign pull_resistor_3_node = or_1_out ? {30{1'b0}} : 30'bz;  // Controlled_Buffer controlled_buffer_1
  Pull_Resistor pull_resistor_4 (.node(pull_resistor_4_node));
  assign pull_resistor_4_node = or_1_out ? 30'hfceaf : 30'bz;  // Controlled_Buffer controlled_buffer_2
  Pull_Resistor pull_resistor_5 (.node(pull_resistor_5_node));
  assign pull_resistor_5_node = or_1_out ? 30'h1ff0fa : 30'bz;  // Controlled_Buffer controlled_buffer_3
  assign controlled_buffer_4_out = or_1_out ? 30'h1fffff : 30'bz;  // Controlled_Buffer controlled_buffer_4
  Pull_Resistor pull_resistor_6 (.node(controlled_buffer_4_out));
  Pull_Resistor pull_resistor_7 (.node(pull_resistor_7_node));
  assign pull_resistor_7_node = or_1_out ? 30'h1eeeee : 30'bz;  // Controlled_Buffer controlled_buffer_5
  assign controlled_buffer_6_out = or_1_out ? 30'hfbafa : 30'bz;  // Controlled_Buffer controlled_buffer_6
  Pull_Resistor pull_resistor_8 (.node(controlled_buffer_6_out));
  Pull_Resistor pull_resistor_9 (.node(pull_resistor_9_node));
  assign pull_resistor_9_node = or_1_out ? 30'hfffff : 30'bz;  // Controlled_Buffer controlled_buffer_7
  assign controlled_buffer_8_out = or_1_out ? 30'h1bbbbb : 30'bz;  // Controlled_Buffer controlled_buffer_8
  Pull_Resistor pull_resistor_10 (.node(controlled_buffer_8_out));
  Pull_Resistor pull_resistor_11 (.node(pull_resistor_11_node));
  assign pull_resistor_11_node = or_1_out ? 30'heeeee : 30'bz;  // Controlled_Buffer controlled_buffer_9
  assign controlled_buffer_10_out = or_1_out ? {30{1'b0}} : 30'bz;  // Controlled_Buffer controlled_buffer_10
  Pull_Resistor pull_resistor_12 (.node(controlled_buffer_10_out));
  Shifter #(.width(30)) shifter_1 (.in(pull_resistor_3_node), .\dist (inputBackShiftM), .out(shifter_1_out));
  Shifter #(.width(30)) shifter_2 (.in(pull_resistor_4_node), .\dist (inputBackShiftM), .out(shifter_2_out));
  Shifter #(.width(30)) shifter_3 (.in(pull_resistor_5_node), .\dist (inputBackShiftM), .out(shifter_3_out));
  Shifter #(.width(30)) shifter_4 (.in(controlled_buffer_4_out), .\dist (inputBackShiftM), .out(shifter_4_out));
  Shifter #(.width(30)) shifter_5 (.in(pull_resistor_7_node), .\dist (inputBackShiftM), .out(shifter_5_out));
  Shifter #(.width(30)) shifter_6 (.in(controlled_buffer_6_out), .\dist (inputBackShiftM), .out(shifter_6_out));
  Shifter #(.width(30)) shifter_7 (.in(pull_resistor_9_node), .\dist (inputBackShiftM), .out(shifter_7_out));
  Shifter #(.width(30)) shifter_8 (.in(controlled_buffer_8_out), .\dist (inputBackShiftM), .out(shifter_8_out));
  Shifter #(.width(30)) shifter_9 (.in(pull_resistor_11_node), .\dist (inputBackShiftM), .out(shifter_9_out));
  Shifter #(.width(30)) shifter_10 (.in(controlled_buffer_10_out), .\dist (inputBackShiftM), .out(shifter_10_out));
  assign not_1_out = ~inputBackShiftM;  // NOT_Gate not_1, 5 bits wide
  Adder #(.width(5)) adder_2 (.a(not_1_out), .b(5'b00001), .out(adder_2_out));  // open: cin, cout
  Adder #(.width(5)) adder_3 (.a(5'b11110), .b(adder_2_out), .out(adder_3_out));  // open: cin, cout
  Pull_Resistor pull_resistor_13 (.node(pull_resistor_13_node));
  assign pull_resistor_13_node = or_2_out ? {30{1'b0}} : 30'bz;  // Controlled_Buffer controlled_buffer_11
  Shifter #(.width(30), .shift("lr")) shifter_11 (
    .in(pull_resistor_13_node), .\dist (adder_3_out), .out(shifter_11_out));
  assign controlled_buffer_12_out = or_2_out ? 30'hfceaf : 30'bz;  // Controlled_Buffer controlled_buffer_12
  Pull_Resistor pull_resistor_14 (.node(controlled_buffer_12_out));
  Shifter #(.width(30), .shift("lr")) shifter_12 (
    .in(controlled_buffer_12_out), .\dist (adder_3_out), .out(shifter_12_out));
  assign controlled_buffer_13_out = or_2_out ? 30'h1ff0fa : 30'bz;  // Controlled_Buffer controlled_buffer_13
  Pull_Resistor pull_resistor_15 (.node(controlled_buffer_13_out));
  Shifter #(.width(30), .shift("lr")) shifter_13 (
    .in(controlled_buffer_13_out), .\dist (adder_3_out), .out(shifter_13_out));
  assign controlled_buffer_14_out = or_2_out ? 30'h1fffff : 30'bz;  // Controlled_Buffer controlled_buffer_14
  Pull_Resistor pull_resistor_16 (.node(controlled_buffer_14_out));
  Shifter #(.width(30), .shift("lr")) shifter_14 (
    .in(controlled_buffer_14_out), .\dist (adder_3_out), .out(shifter_14_out));
  assign controlled_buffer_15_out = or_2_out ? 30'h1eeeee : 30'bz;  // Controlled_Buffer controlled_buffer_15
  Pull_Resistor pull_resistor_17 (.node(controlled_buffer_15_out));
  Shifter #(.width(30), .shift("lr")) shifter_15 (
    .in(controlled_buffer_15_out), .\dist (adder_3_out), .out(shifter_15_out));
  assign controlled_buffer_16_out = or_2_out ? 30'hfbafa : 30'bz;  // Controlled_Buffer controlled_buffer_16
  Pull_Resistor pull_resistor_18 (.node(controlled_buffer_16_out));
  Shifter #(.width(30), .shift("lr")) shifter_16 (
    .in(controlled_buffer_16_out), .\dist (adder_3_out), .out(shifter_16_out));
  assign controlled_buffer_17_out = or_2_out ? 30'hfffff : 30'bz;  // Controlled_Buffer controlled_buffer_17
  Pull_Resistor pull_resistor_19 (.node(controlled_buffer_17_out));
  Shifter #(.width(30), .shift("lr")) shifter_17 (
    .in(controlled_buffer_17_out), .\dist (adder_3_out), .out(shifter_17_out));
  assign controlled_buffer_18_out = or_2_out ? 30'h1bbbbb : 30'bz;  // Controlled_Buffer controlled_buffer_18
  Pull_Resistor pull_resistor_20 (.node(controlled_buffer_18_out));
  Shifter #(.width(30), .shift("lr")) shifter_18 (
    .in(controlled_buffer_18_out), .\dist (adder_3_out), .out(shifter_18_out));
  assign controlled_buffer_19_out = or_2_out ? 30'heeeee : 30'bz;  // Controlled_Buffer controlled_buffer_19
  Pull_Resistor pull_resistor_21 (.node(controlled_buffer_19_out));
  Shifter #(.width(30), .shift("lr")) shifter_19 (
    .in(controlled_buffer_19_out), .\dist (adder_3_out), .out(shifter_19_out));
  assign controlled_buffer_20_out = or_2_out ? {30{1'b0}} : 30'bz;  // Controlled_Buffer controlled_buffer_20
  Pull_Resistor pull_resistor_22 (.node(controlled_buffer_20_out));
  Shifter #(.width(30), .shift("lr")) shifter_20 (
    .in(controlled_buffer_20_out), .\dist (adder_3_out), .out(shifter_20_out));
  Pull_Resistor pull_resistor_23 (.node(or_2_out));
  Adder #(.width(2)) adder_4 (.a(inPlayerShiftD), .b(2'b01), .out(outPlayerShiftD));  // open: cin, cout
  Pull_Resistor pull_resistor_24 (.node(inPlayerShiftM));
  assign toBackground = shifter_1_out | shifter_11_out;  // OR_Gate or_3, 30 bits wide
  assign toBackground_2 = shifter_2_out | shifter_12_out;  // OR_Gate or_4, 30 bits wide
  assign toBackground_3 = shifter_3_out | shifter_13_out;  // OR_Gate or_5, 30 bits wide
  assign toBackground_4 = shifter_4_out | shifter_14_out;  // OR_Gate or_6, 30 bits wide
  assign toBackground_5 = shifter_5_out | shifter_15_out;  // OR_Gate or_7, 30 bits wide
  assign toBackground_6 = shifter_6_out | shifter_16_out;  // OR_Gate or_8, 30 bits wide
  // Probe on adder_5_out
  Adder #(.width(5)) adder_5 (.a(inPlayerShiftM), .b(5'b00001), .out(adder_5_out));  // open: cin, cout
  Comparator #(.width(5), .mode("unsigned")) comparator_5 (
    .a(inPlayerShiftM), .b(5'b11110), .eq(comparator_5_eq));  // open: gt, lt
  assign toBackground_7 = shifter_7_out | shifter_17_out;  // OR_Gate or_9, 30 bits wide
  assign toBackground_8 = shifter_8_out | shifter_18_out;  // OR_Gate or_10, 30 bits wide
  assign toBackground_9 = shifter_9_out | shifter_19_out;  // OR_Gate or_11, 30 bits wide
  assign toBackground_10 = shifter_10_out | shifter_20_out;  // OR_Gate or_12, 30 bits wide
  // Probe on multiplexer_1_out
  Multiplexer #(.width(2), .disabled(0), .enable("false")) multiplexer_1 (
    .in0(inPlayerShiftD), .in1(outPlayerShiftD), .out(multiplexer_1_out), .sel(comparator_5_eq));
  assign controlled_buffer_21_out = inFlag ? comparator_6_eq : 1'bz;  // Controlled_Buffer controlled_buffer_21
  Comparator #(.width(2)) comparator_6 (.a(2'b00), .b(multiplexer_1_out), .eq(comparator_6_eq));  // open: gt, lt
  Comparator #(.width(2)) comparator_7 (.a(2'b00), .b(adder_6_out), .eq(comparator_7_eq));  // open: gt, lt
  assign controlled_buffer_22_out = inFlag ? comparator_7_eq : 1'bz;  // Controlled_Buffer controlled_buffer_22
  Adder #(.width(2)) adder_6 (.a(multiplexer_1_out), .b(2'b01), .out(adder_6_out));  // open: cin, cout
  Pull_Resistor pull_resistor_25 (.node(pull_resistor_25_node));
  Pull_Resistor pull_resistor_26 (.node(controlled_buffer_21_out));
  assign pull_resistor_25_node = controlled_buffer_21_out ? 30'h279 : 30'bz;  // Controlled_Buffer controlled_buffer_23
  Pull_Resistor pull_resistor_27 (.node(pull_resistor_27_node));
  assign pull_resistor_27_node = controlled_buffer_21_out ? 30'h231 : 30'bz;  // Controlled_Buffer controlled_buffer_24
  assign controlled_buffer_25_out = controlled_buffer_21_out ? 30'h279 : 30'bz;  // Controlled_Buffer controlled_buffer_25
  Pull_Resistor pull_resistor_28 (.node(controlled_buffer_25_out));
  Pull_Resistor pull_resistor_29 (.node(pull_resistor_29_node));
  assign pull_resistor_29_node = controlled_buffer_21_out ? 30'h3ff : 30'bz;  // Controlled_Buffer controlled_buffer_26
  Pull_Resistor pull_resistor_30 (.node(pull_resistor_30_node));
  assign pull_resistor_30_node = controlled_buffer_21_out ? 30'hfc : 30'bz;  // Controlled_Buffer controlled_buffer_27
  assign controlled_buffer_28_out = controlled_buffer_21_out ? 30'hfc : 30'bz;  // Controlled_Buffer controlled_buffer_28
  Pull_Resistor pull_resistor_31 (.node(controlled_buffer_28_out));
  assign controlled_buffer_29_out = controlled_buffer_21_out ? 30'h3ff : 30'bz;  // Controlled_Buffer controlled_buffer_29
  Pull_Resistor pull_resistor_32 (.node(controlled_buffer_29_out));
  assign controlled_buffer_30_out = controlled_buffer_21_out ? 30'h279 : 30'bz;  // Controlled_Buffer controlled_buffer_30
  Pull_Resistor pull_resistor_33 (.node(controlled_buffer_30_out));
  assign controlled_buffer_31_out = controlled_buffer_21_out ? 30'h231 : 30'bz;  // Controlled_Buffer controlled_buffer_31
  Pull_Resistor pull_resistor_34 (.node(controlled_buffer_31_out));
  assign controlled_buffer_32_out = controlled_buffer_21_out ? 30'h201 : 30'bz;  // Controlled_Buffer controlled_buffer_32
  Pull_Resistor pull_resistor_35 (.node(controlled_buffer_32_out));
  Shifter #(.width(30)) shifter_21 (.in(pull_resistor_25_node), .\dist (adder_5_out), .out(shifter_21_out));
  Shifter #(.width(30)) shifter_22 (.in(pull_resistor_27_node), .\dist (adder_5_out), .out(shifter_22_out));
  Shifter #(.width(30)) shifter_23 (.in(controlled_buffer_25_out), .\dist (adder_5_out), .out(shifter_23_out));
  Shifter #(.width(30)) shifter_24 (.in(pull_resistor_29_node), .\dist (adder_5_out), .out(shifter_24_out));
  Shifter #(.width(30)) shifter_25 (.in(pull_resistor_30_node), .\dist (adder_5_out), .out(shifter_25_out));
  Shifter #(.width(30)) shifter_26 (.in(controlled_buffer_28_out), .\dist (adder_5_out), .out(shifter_26_out));
  Shifter #(.width(30)) shifter_27 (.in(controlled_buffer_29_out), .\dist (adder_5_out), .out(shifter_27_out));
  Shifter #(.width(30)) shifter_28 (.in(controlled_buffer_30_out), .\dist (adder_5_out), .out(shifter_28_out));
  Shifter #(.width(30)) shifter_29 (.in(controlled_buffer_31_out), .\dist (adder_5_out), .out(shifter_29_out));
  Shifter #(.width(30)) shifter_30 (.in(controlled_buffer_32_out), .\dist (adder_5_out), .out(shifter_30_out));
  assign not_2_out = ~adder_5_out;  // NOT_Gate not_2, 5 bits wide
  Adder #(.width(5)) adder_7 (.a(not_2_out), .b(5'b00001), .out(adder_7_out));  // open: cin, cout
  Pull_Resistor pull_resistor_36 (.node(controlled_buffer_22_out));
  Adder #(.width(5)) adder_8 (.a(5'b11110), .b(adder_7_out), .out(adder_8_out));  // open: cin, cout
  assign controlled_buffer_33_out = controlled_buffer_22_out ? 30'h279 : 30'bz;  // Controlled_Buffer controlled_buffer_33
  Pull_Resistor pull_resistor_37 (.node(controlled_buffer_33_out));
  Shifter #(.width(30), .shift("lr")) shifter_31 (
    .in(controlled_buffer_33_out), .\dist (adder_8_out), .out(shifter_31_out));
  Pull_Resistor pull_resistor_38 (.node(pull_resistor_38_node));
  assign pull_resistor_38_node = controlled_buffer_22_out ? 30'h231 : 30'bz;  // Controlled_Buffer controlled_buffer_34
  Shifter #(.width(30), .shift("lr")) shifter_32 (
    .in(pull_resistor_38_node), .\dist (adder_8_out), .out(shifter_32_out));
  Pull_Resistor pull_resistor_39 (.node(pull_resistor_39_node));
  assign pull_resistor_39_node = controlled_buffer_22_out ? 30'h279 : 30'bz;  // Controlled_Buffer controlled_buffer_35
  Shifter #(.width(30), .shift("lr")) shifter_33 (
    .in(pull_resistor_39_node), .\dist (adder_8_out), .out(shifter_33_out));
  assign controlled_buffer_36_out = controlled_buffer_22_out ? 30'h3ff : 30'bz;  // Controlled_Buffer controlled_buffer_36
  Pull_Resistor pull_resistor_40 (.node(controlled_buffer_36_out));
  Shifter #(.width(30), .shift("lr")) shifter_34 (
    .in(controlled_buffer_36_out), .\dist (adder_8_out), .out(shifter_34_out));
  Pull_Resistor pull_resistor_41 (.node(pull_resistor_41_node));
  assign pull_resistor_41_node = controlled_buffer_22_out ? 30'hfc : 30'bz;  // Controlled_Buffer controlled_buffer_37
  Shifter #(.width(30), .shift("lr")) shifter_35 (
    .in(pull_resistor_41_node), .\dist (adder_8_out), .out(shifter_35_out));
  assign controlled_buffer_38_out = controlled_buffer_22_out ? 30'hfc : 30'bz;  // Controlled_Buffer controlled_buffer_38
  Pull_Resistor pull_resistor_42 (.node(controlled_buffer_38_out));
  Shifter #(.width(30), .shift("lr")) shifter_36 (
    .in(controlled_buffer_38_out), .\dist (adder_8_out), .out(shifter_36_out));
  Pull_Resistor pull_resistor_43 (.node(pull_resistor_43_node));
  assign pull_resistor_43_node = controlled_buffer_22_out ? 30'h3ff : 30'bz;  // Controlled_Buffer controlled_buffer_39
  Shifter #(.width(30), .shift("lr")) shifter_37 (
    .in(pull_resistor_43_node), .\dist (adder_8_out), .out(shifter_37_out));
  assign controlled_buffer_40_out = controlled_buffer_22_out ? 30'h279 : 30'bz;  // Controlled_Buffer controlled_buffer_40
  Pull_Resistor pull_resistor_44 (.node(controlled_buffer_40_out));
  Shifter #(.width(30), .shift("lr")) shifter_38 (
    .in(controlled_buffer_40_out), .\dist (adder_8_out), .out(shifter_38_out));
  assign controlled_buffer_41_out = controlled_buffer_22_out ? 30'h231 : 30'bz;  // Controlled_Buffer controlled_buffer_41
  Pull_Resistor pull_resistor_45 (.node(controlled_buffer_41_out));
  Shifter #(.width(30), .shift("lr")) shifter_39 (
    .in(controlled_buffer_41_out), .\dist (adder_8_out), .out(shifter_39_out));
  Pull_Resistor pull_resistor_46 (.node(pull_resistor_46_node));
  assign pull_resistor_46_node = controlled_buffer_22_out ? 30'h201 : 30'bz;  // Controlled_Buffer controlled_buffer_42
  Shifter #(.width(30), .shift("lr")) shifter_40 (
    .in(pull_resistor_46_node), .\dist (adder_8_out), .out(shifter_40_out));
  assign toFront = shifter_21_out | shifter_31_out;  // OR_Gate or_13, 30 bits wide
  assign toFront_2 = shifter_22_out | shifter_32_out;  // OR_Gate or_14, 30 bits wide
  assign toFront_3 = shifter_23_out | shifter_33_out;  // OR_Gate or_15, 30 bits wide
  assign toFront_4 = shifter_24_out | shifter_34_out;  // OR_Gate or_16, 30 bits wide
  assign toFront_5 = shifter_25_out | shifter_35_out;  // OR_Gate or_17, 30 bits wide
  assign toFront_6 = shifter_26_out | shifter_36_out;  // OR_Gate or_18, 30 bits wide
  assign toFront_7 = shifter_27_out | shifter_37_out;  // OR_Gate or_19, 30 bits wide
  assign toFront_8 = shifter_28_out | shifter_38_out;  // OR_Gate or_20, 30 bits wide
  assign toFront_9 = shifter_29_out | shifter_39_out;  // OR_Gate or_21, 30 bits wide
  assign toFront_10 = shifter_30_out | shifter_40_out;  // OR_Gate or_22, 30 bits wide

  assign outFlag = inFlag;
  assign outPlayerShiftM = inPlayerShiftM;
  assign outputBackShiftM = inputBackShiftM;

  // Notes on the sheet:
  //   MAKE SHIFT BY NEXT MATRICE
  //   MAKE SHIFT IN CURRENT MATRICE
  //   MAKE SHIFT IN CURRENT MATRICE
  //   MAKE SHIFT BY NEXT MATRICE
endmodule

module turtleState (
  input  inTact,
  input  [1:0] speedDiv,
  output [3:0] state
);
endmodule

module smallLogIntersect (
  input  [4:0] backLen,
  input  [4:0] inBackM,
  input  [4:0] inFrogM,
  input  inIntersect,
  input  doIntersect,
  output outIntersect
);

  wire and_1_out, and_2_out, and_3_out, and_4_out, comparator_1_lt, comparator_2_gt, comparator_3_lt,
       comparator_4_gt, comparator_5_lt, comparator_6_gt, comparator_7_lt, comparator_8_gt, not_1_out,
       not_2_out, not_3_out, not_4_out, not_5_out, not_6_out, not_7_out, not_8_out, not_9_out, or_1_out,
       or_2_out;
  wire [6:0] adder_1_out, adder_2_out, adder_3_out, adder_4_out, adder_5_out, bit_extender_1_out,
       bit_extender_2_out, bit_extender_3_out;

  assign bit_extender_1_out = {{2{1'b0}}, inBackM};  // Bit_Extender bit_extender_1
  assign bit_extender_2_out = {{2{1'b0}}, inFrogM};  // Bit_Extender bit_extender_2
  assign bit_extender_3_out = {{2{1'b0}}, backLen};  // Bit_Extender bit_extender_3
  // Probe on bit_extender_2_out
  // Probe on 7'b0000111
  Adder #(.width(7)) adder_1 (.a(bit_extender_2_out), .b(7'b0011110), .out(adder_1_out));  // open: cin, cout
  // Probe on bit_extender_3_out
  // Probe on bit_extender_1_out
  // Probe on 7'b0000111
  // Probe on bit_extender_3_out
  // Probe on bit_extender_1_out
  Adder #(.width(7)) adder_2 (.a(7'b0000111), .b(adder_1_out), .out(adder_2_out));  // open: cin, cout
  Adder #(.width(7)) adder_3 (.a(bit_extender_3_out), .b(bit_extender_1_out), .out(adder_3_out));  // open: cin, cout
  Adder #(.width(7)) adder_4 (.a(7'b0000111), .b(bit_extender_2_out), .out(adder_4_out));  // open: cin, cout
  Adder #(.width(7)) adder_5 (.a(bit_extender_3_out), .b(bit_extender_1_out), .out(adder_5_out));  // open: cin, cout
  Comparator #(.width(7), .mode("unsigned")) comparator_1 (
    .a(adder_2_out), .b(bit_extender_1_out), .lt(comparator_1_lt));  // open: gt, eq
  Comparator #(.width(7), .mode("unsigned")) comparator_2 (
    .a(adder_2_out), .b(adder_5_out), .gt(comparator_2_gt));  // open: eq, lt
  Comparator #(.width(7), .mode("unsigned")) comparator_3 (
    .a(adder_1_out), .b(bit_extender_1_out), .lt(comparator_3_lt));  // open: gt, eq
  Comparator #(.width(7), .mode("unsigned")) comparator_4 (
    .a(adder_1_out), .b(adder_5_out), .gt(comparator_4_gt));  // open: eq, lt
  Comparator #(.width(7), .mode("unsigned")) comparator_5 (
    .a(adder_4_out), .b(bit_extender_1_out), .lt(comparator_5_lt));  // open: gt, eq
  not not_1 (not_1_out, comparator_5_lt);
  and and_1 (and_1_out, not_1_out, not_2_out);
  not not_2 (not_2_out, comparator_6_gt);
  Comparator #(.width(7), .mode("unsigned")) comparator_6 (
    .a(adder_4_out), .b(adder_3_out), .gt(comparator_6_gt));  // open: eq, lt
  Comparator #(.width(7), .mode("unsigned")) comparator_7 (
    .a(bit_extender_2_out), .b(bit_extender_1_out), .lt(comparator_7_lt));  // open: gt, eq
  not not_3 (not_3_out, comparator_7_lt);
  and and_2 (and_2_out, not_3_out, not_4_out);
  not not_4 (not_4_out, comparator_8_gt);
  Comparator #(.width(7), .mode("unsigned")) comparator_8 (
    .a(bit_extender_2_out), .b(adder_3_out), .gt(comparator_8_gt));  // open: eq, lt
  not not_5 (not_5_out, comparator_1_lt);
  and and_3 (and_3_out, not_5_out, not_6_out);
  not not_6 (not_6_out, comparator_2_gt);
  not not_7 (not_7_out, comparator_3_lt);
  and and_4 (and_4_out, not_7_out, not_8_out);
  not not_8 (not_8_out, comparator_4_gt);
  Pull_Resistor pull_resistor_1 (.node(inIntersect));
  or or_1 (or_1_out, and_1_out, and_2_out, inIntersect);
  not not_9 (not_9_out, or_2_out);
  or or_2 (or_2_out, or_1_out, and_3_out, and_4_out);
  and and_5 (outIntersect, not_9_out, doIntersect);

  // Notes on the sheet:
  //   BD * 30 + BM
  //   BD * 30 + BM
  //   Bh
  //   Bl
  //   Fl
  //   Bh
  //   Bl
  //   Fl
  //   Fh >= Bl && Fh <= Bh
  //   Fl >= Bl && Fl <= Bh
  //   Fh >= Bl && Fh <= Bh
  //   Fl >= Bl && Fl <= Bh
endmodule

// stop
module stopGame (
  input  tact,
  input  \event ,
  output stopper
);

  wire and_1_out, controlled_buffer_1_out, not_2_out, pull_resistor_2_node, pull_resistor_3_node,
       pull_resistor_4_node, pull_resistor_8_node, pull_resistor_9_node;
  wire [4:0] pull_resistor_5_node;

  Pull_Resistor pull_resistor_1 (.node(\event ));
  Pull_Resistor pull_resistor_2 (.node(pull_resistor_2_node));
  Pull_Resistor pull_resistor_3 (.node(pull_resistor_3_node));
  assign controlled_buffer_1_out = pull_resistor_3_node ? and_1_out : 1'bz;  // Controlled_Buffer controlled_buffer_1
  Pull_Resistor pull_resistor_4 (.node(pull_resistor_4_node));
  not not_1 (pull_resistor_3_node, pull_resistor_9_node);
  Pull_Resistor pull_resistor_5 (.node(pull_resistor_5_node));
  Counter #(.width(5), .max('h1f)) counter_1 (
    .Q(pull_resistor_5_node), .clk(and_1_out), .clr(not_2_out));  // open: load, D, count, carry
  not not_2 (not_2_out, \event );
  and and_1 (and_1_out, tact, \event );
  Pull_Resistor pull_resistor_6 (.node(and_1_out));
  D_Flip_Flop d_ff_1 (
    .clk(pull_resistor_2_node), .D(pull_resistor_4_node), .Q(stopper), .preset(controlled_buffer_1_out),
    .en(pull_resistor_8_node), .reset(pull_resistor_9_node));  // open: Qn
  Pull_Resistor pull_resistor_7 (.node(controlled_buffer_1_out));
  Pull_Resistor pull_resistor_8 (.node(pull_resistor_8_node));
  Pull_Resistor pull_resistor_9 (.node(pull_resistor_9_node));
  Pull_Resistor pull_resistor_10 (.node(stopper));
  Comparator #(.width(5), .mode("unsigned")) comparator_1 (
    .a(pull_resistor_5_node), .b(5'b11101), .eq(pull_resistor_9_node));  // open: gt, lt
  Pull_Resistor pull_resistor_11 (.node(pull_resistor_9_node));
endmodule

module mod_vertical (
  input  W,
  input  S,
  input  reset,
  input  stop,
  output [3:0] Y
);

  wire counter_1_q, multiplexer_1_out, multiplexer_2_out, or_1_out, or_2_out;

  Multiplexer multiplexer_1 (.in0(W), .in1(1'b0), .out(multiplexer_1_out), .sel(counter_1_q));  // open: en
  Multiplexer multiplexer_2 (.in0(S), .in1(1'b0), .out(multiplexer_2_out), .sel(counter_1_q));  // open: en
  Counter #(.width(1), .max('h1)) counter_1 (.count(stop), .Q(counter_1_q), .clk(stop));  // open: load, D, carry, clr
  or or_1 (or_1_out, multiplexer_2_out, multiplexer_1_out);
  Counter #(.width(4), .max('hf), .ongoal("stay")) counter_2 (
    .load(multiplexer_2_out), .count(or_1_out), .Q(Y), .clk(or_2_out), .clr(reset));  // open: D, carry
  or or_2 (or_2_out, multiplexer_2_out, multiplexer_1_out);
endmodule

module mod_horizon_3__works_correctly (
  input  A,
  input  D,
  input  reset,
  input  stop,
  output [4:0] Xmatrice,
  output [1:0] Xdisplay
);

  wire counter_1_q, multiplexer_1_out, multiplexer_2_out, or_1_out, or_2_out;
  wire [1:0] multiplexer_4_out;
  wire [3:0] counter_2_q;

  Multiplexer multiplexer_1 (.in0(A), .in1(1'b0), .out(multiplexer_1_out), .sel(counter_1_q));  // open: en
  Multiplexer multiplexer_2 (.in0(D), .in1(1'b0), .out(multiplexer_2_out), .sel(counter_1_q));  // open: en
  Counter #(.width(1), .max('h1)) counter_1 (.count(stop), .Q(counter_1_q), .clk(stop));  // open: load, D, carry, clr
  or or_1 (or_1_out, multiplexer_2_out, multiplexer_1_out);
  or or_2 (or_2_out, multiplexer_1_out, multiplexer_2_out);
  Counter #(.width(4), .max('hb), .ongoal("stay")) counter_2 (
    .load(multiplexer_2_out), .count(or_1_out), .Q(counter_2_q), .clk(or_2_out), .clr(reset));  // open: D, carry
  Multiplexer #(.select(4), .width(5), .disabled(0), .enable("false")) multiplexer_3 (
    .in0({5{1'b0}}), .in1(5'b01010), .in2(5'b10100), .in3({5{1'b0}}), .in4(5'b01010), .in5(5'b10100),
    .in6({5{1'b0}}), .in7(5'b01010), .in8(5'b10100), .in9({5{1'b0}}), .in10(5'b01010), .in11(5'b10100),
    .in12({5{1'b0}}), .in13(5'b01010), .in14(5'b10100), .in15({5{1'b0}}), .out(Xmatrice), .sel(counter_2_q));
  Multiplexer #(.select(4), .width(2), .disabled(0), .enable("false")) multiplexer_4 (
    .in0(2'b00), .in1(2'b00), .in2(2'b00), .in3(2'b01), .in4(2'b01), .in5(2'b01), .in6(2'b10), .in7(2'b10),
    .in8(2'b10), .in9(2'b11), .in10(2'b11), .in11(2'b11), .out(multiplexer_4_out), .sel(counter_2_q));  // open: in12, in13, in14, in15
  // Probe on Xmatrice
  Adder #(.width(2)) adder_1 (.a(multiplexer_4_out), .b(2'b01), .out(Xdisplay));  // open: cin, cout
endmodule
// turtle3x1
module turtle_3x1 (
  input  [1:0] inBackShiftD,
  input  [4:0] inputBackShiftM,
  input  [1:0] inPlayerShiftD,
  input  [4:0] inPlayerShiftM,
  input  inFlag,
  output [29:0] toBackground,
  output [29:0] toBackground_2,
  output [29:0] toBackground_3,
  output [29:0] toBackground_4,
  output [29:0] toBackground_5,
  output [1:0] outBackShiftD,
  output [29:0] toBackground_6,
  output [29:0] toBackground_7,
  output [4:0] outputBackShiftM,
  output [29:0] toBackground_8,
  output [29:0] toBackground_9,
  output [29:0] toBackground_10,
  output [29:0] toFront,
  output [29:0] toFront_2,
  output [29:0] toFront_3,
  output [29:0] toFront_4,
  output [29:0] toFront_5,
  output [29:0] toFront_6,
  output [1:0] outPlayerShiftD,
  output [4:0] outPlayerShiftM,
  output [29:0] toFront_7,
  output outFlag,
  output [29:0] toFront_8,
  output [29:0] toFront_9,
  output [29:0] toFront_10
);

  wire comparator_1_eq, comparator_2_eq, comparator_3_eq, comparator_4_eq, comparator_5_eq, comparator_6_eq,
       comparator_7_eq, controlled_buffer_21_out, controlled_buffer_22_out, or_1_out, or_2_out;
  wire [1:0] adder_6_out, multiplexer_1_out;
  wire [4:0] adder_2_out, adder_3_out, adder_5_out, adder_7_out, adder_8_out, not_1_out, not_2_out;
  wire [29:0] controlled_buffer_1_out, controlled_buffer_3_out, controlled_buffer_4_out,
       controlled_buffer_5_out, controlled_buffer_6_out, controlled_buffer_8_out, controlled_buffer_13_out,
       controlled_buffer_14_out, controlled_buffer_15_out, controlled_buffer_16_out,
       controlled_buffer_19_out, controlled_buffer_29_out, controlled_buffer_30_out,
       controlled_buffer_31_out, controlled_buffer_32_out, controlled_buffer_33_out,
       controlled_buffer_34_out, controlled_buffer_36_out, controlled_buffer_37_out,
       controlled_buffer_38_out, controlled_buffer_39_out, pull_resistor_4_node, pull_resistor_9_node,
       pull_resistor_11_node, pull_resistor_12_node, pull_resistor_13_node, pull_resistor_14_node,
       pull_resistor_19_node, pull_resistor_20_node, pull_resistor_22_node, pull_resistor_26_node,
       pull_resistor_27_node, pull_resistor_28_node, pull_resistor_29_node, pull_resistor_30_node,
       pull_resistor_31_node, pull_resistor_39_node, pull_resistor_44_node, pull_resistor_45_node,
       pull_resistor_46_node, shifter_1_out, shifter_2_out, shifter_3_out, shifter_4_out, shifter_5_out,
       shifter_6_out, shifter_7_out, shifter_8_out, shifter_9_out, shifter_10_out, shifter_11_out,
       shifter_12_out, shifter_13_out, shifter_14_out, shifter_15_out, shifter_16_out, shifter_17_out,
       shifter_18_out, shifter_19_out, shifter_20_out, shifter_21_out, shifter_22_out, shifter_23_out,
       shifter_24_out, shifter_25_out, shifter_26_out, shifter_27_out, shifter_28_out, shifter_29_out,
       shifter_30_out, shifter_31_out, shifter_32_out, shifter_33_out, shifter_34_out, shifter_35_out,
       shifter_36_out, shifter_37_out, shifter_38_out, shifter_39_out, shifter_40_out;

  Adder #(.width(2)) adder_1 (.a(inBackShiftD), .b(2'b01), .out(outBackShiftD));  // open: cin, cout
  Pull_Resistor pull_resistor_1 (.node(inputBackShiftM));
  Comparator #(.width(2)) comparator_1 (.a(inBackShiftD), .b(2'b10), .eq(comparator_1_eq));  // open: gt, lt
  Comparator #(.width(2)) comparator_2 (.a(2'b00), .b(inBackShiftD), .eq(comparator_2_eq));  // open: gt, lt
  // Probe on outBackShiftD
  or or_1 (or_1_out, comparator_1_eq, comparator_2_eq);
  Comparator #(.width(2)) comparator_3 (.a(outBackShiftD), .b(2'b10), .eq(comparator_3_eq));  // open: gt, lt
  or or_2 (or_2_out, comparator_3_eq, comparator_4_eq);
  Comparator #(.width(2)) comparator_4 (.a(2'b00), .b(outBackShiftD), .eq(comparator_4_eq));  // open: gt, lt
  Pull_Resistor pull_resistor_2 (.node(or_1_out));
  assign controlled_buffer_1_out = or_1_out ? {30{1'b0}} : 30'bz;  // Controlled_Buffer controlled_buffer_1
  Pull_Resistor pull_resistor_3 (.node(controlled_buffer_1_out));
  Pull_Resistor pull_resistor_4 (.node(pull_resistor_4_node));
  assign pull_resistor_4_node = or_1_out ? {30{1'b1}} : 30'bz;  // Controlled_Buffer controlled_buffer_2
  assign controlled_buffer_3_out = or_1_out ? 30'h2fbfcfef : 30'bz;  // Controlled_Buffer controlled_buffer_3
  Pull_Resistor pull_resistor_5 (.node(controlled_buffer_3_out));
  assign controlled_buffer_4_out = or_1_out ? 30'h3fafafaf : 30'bz;  // Controlled_Buffer controlled_buffer_4
  Pull_Resistor pull_resistor_6 (.node(controlled_buffer_4_out));
  assign controlled_buffer_5_out = or_1_out ? 30'h3eeeeeee : 30'bz;  // Controlled_Buffer controlled_buffer_5
  Pull_Resistor pull_resistor_7 (.node(controlled_buffer_5_out));
  assign controlled_buffer_6_out = or_1_out ? 30'h2edfbafa : 30'bz;  // Controlled_Buffer controlled_buffer_6
  Pull_Resistor pull_resistor_8 (.node(controlled_buffer_6_out));
  Pull_Resistor pull_resistor_9 (.node(pull_resistor_9_node));
  assign pull_resistor_9_node = or_1_out ? {30{1'b1}} : 30'bz;  // Controlled_Buffer controlled_buffer_7
  assign controlled_buffer_8_out = or_1_out ? 30'h3f7ba9f : 30'bz;  // Controlled_Buffer controlled_buffer_8
  Pull_Resistor pull_resistor_10 (.node(controlled_buffer_8_out));
  Pull_Resistor pull_resistor_11 (.node(pull_resistor_11_node));
  assign pull_resistor_11_node = or_1_out ? {30{1'b1}} : 30'bz;  // Controlled_Buffer controlled_buffer_9
  Pull_Resistor pull_resistor_12 (.node(pull_resistor_12_node));
  assign pull_resistor_12_node = or_1_out ? {30{1'b0}} : 30'bz;  // Controlled_Buffer controlled_buffer_10
  Shifter #(.width(30)) shifter_1 (.in(controlled_buffer_1_out), .\dist (inputBackShiftM), .out(shifter_1_out));
  Shifter #(.width(30)) shifter_2 (.in(pull_resistor_4_node), .\dist (inputBackShiftM), .out(shifter_2_out));
  Shifter #(.width(30)) shifter_3 (.in(controlled_buffer_3_out), .\dist (inputBackShiftM), .out(shifter_3_out));
  Shifter #(.width(30)) shifter_4 (.in(controlled_buffer_4_out), .\dist (inputBackShiftM), .out(shifter_4_out));
  Shifter #(.width(30)) shifter_5 (.in(controlled_buffer_5_out), .\dist (inputBackShiftM), .out(shifter_5_out));
  Shifter #(.width(30)) shifter_6 (.in(controlled_buffer_6_out), .\dist (inputBackShiftM), .out(shifter_6_out));
  Shifter #(.width(30)) shifter_7 (.in(pull_resistor_9_node), .\dist (inputBackShiftM), .out(shifter_7_out));
  Shifter #(.width(30)) shifter_8 (.in(controlled_buffer_8_out), .\dist (inputBackShiftM), .out(shifter_8_out));
  Shifter #(.width(30)) shifter_9 (.in(pull_resistor_11_node), .\dist (inputBackShiftM), .out(shifter_9_out));
  Shifter #(.width(30)) shifter_10 (.in(pull_resistor_12_node), .\dist (inputBackShiftM), .out(shifter_10_out));
  assign not_1_out = ~inputBackShiftM;  // NOT_Gate not_1, 5 bits wide
  Adder #(.width(5)) adder_2 (.a(not_1_out), .b(5'b00001), .out(adder_2_out));  // open: cin, cout
  Adder #(.width(5)) adder_3 (.a(5'b11110), .b(adder_2_out), .out(adder_3_out));  // open: cin, cout
  Pull_Resistor pull_resistor_13 (.node(pull_resistor_13_node));
  assign pull_resistor_13_node = or_2_out ? {30{1'b0}} : 30'bz;  // Controlled_Buffer controlled_buffer_11
  Shifter #(.width(30), .shift("lr")) shifter_11 (
    .in(pull_resistor_13_node), .\dist (adder_3_out), .out(shifter_11_out));
  Pull_Resistor pull_resistor_14 (.node(pull_resistor_14_node));
  assign pull_resistor_14_node = or_2_out ? {30{1'b1}} : 30'bz;  // Controlled_Buffer controlled_buffer_12
  Shifter #(.width(30), .shift("lr")) shifter_12 (
    .in(pull_resistor_14_node), .\dist (adder_3_out), .out(shifter_12_out));
  assign controlled_buffer_13_out = or_2_out ? 30'h2fbfcfef : 30'bz;  // Controlled_Buffer controlled_buffer_13
  Pull_Resistor pull_resistor_15 (.node(controlled_buffer_13_out));
  Shifter #(.width(30), .shift("lr")) shifter_13 (
    .in(controlled_buffer_13_out), .\dist (adder_3_out), .out(shifter_13_out));
  assign controlled_buffer_14_out = or_2_out ? 30'h3fafafaf : 30'bz;  // Controlled_Buffer controlled_buffer_14
  Pull_Resistor pull_resistor_16 (.node(controlled_buffer_14_out));
  Shifter #(.width(30), .shift("lr")) shifter_14 (
    .in(controlled_buffer_14_out), .\dist (adder_3_out), .out(shifter_14_out));
  assign controlled_buffer_15_out = or_2_out ? 30'h3eeeeeee : 30'bz;  // Controlled_Buffer controlled_buffer_15
  Pull_Resistor pull_resistor_17 (.node(controlled_buffer_15_out));
  Shifter #(.width(30), .shift("lr")) shifter_15 (
    .in(controlled_buffer_15_out), .\dist (adder_3_out), .out(shifter_15_out));
  assign controlled_buffer_16_out = or_2_out ? 30'h2edfbafa : 30'bz;  // Controlled_Buffer controlled_buffer_16
  Pull_Resistor pull_resistor_18 (.node(controlled_buffer_16_out));
  Shifter #(.width(30), .shift("lr")) shifter_16 (
    .in(controlled_buffer_16_out), .\dist (adder_3_out), .out(shifter_16_out));
  Pull_Resistor pull_resistor_19 (.node(pull_resistor_19_node));
  assign pull_resistor_19_node = or_2_out ? {30{1'b1}} : 30'bz;  // Controlled_Buffer controlled_buffer_17
  Shifter #(.width(30), .shift("lr")) shifter_17 (
    .in(pull_resistor_19_node), .\dist (adder_3_out), .out(shifter_17_out));
  Pull_Resistor pull_resistor_20 (.node(pull_resistor_20_node));
  assign pull_resistor_20_node = or_2_out ? 30'h3f7ba9f : 30'bz;  // Controlled_Buffer controlled_buffer_18
  Shifter #(.width(30), .shift("lr")) shifter_18 (
    .in(pull_resistor_20_node), .\dist (adder_3_out), .out(shifter_18_out));
  assign controlled_buffer_19_out = or_2_out ? {30{1'b1}} : 30'bz;  // Controlled_Buffer controlled_buffer_19
  Pull_Resistor pull_resistor_21 (.node(controlled_buffer_19_out));
  Shifter #(.width(30), .shift("lr")) shifter_19 (
    .in(controlled_buffer_19_out), .\dist (adder_3_out), .out(shifter_19_out));
  Pull_Resistor pull_resistor_22 (.node(pull_resistor_22_node));
  assign pull_resistor_22_node = or_2_out ? {30{1'b0}} : 30'bz;  // Controlled_Buffer controlled_buffer_20
  Shifter #(.width(30), .shift("lr")) shifter_20 (
    .in(pull_resistor_22_node), .\dist (adder_3_out), .out(shifter_20_out));
  Pull_Resistor pull_resistor_23 (.node(or_2_out));
  Adder #(.width(2)) adder_4 (.a(inPlayerShiftD), .b(2'b01), .out(outPlayerShiftD));  // open: cin, cout
  Pull_Resistor pull_resistor_24 (.node(inPlayerShiftM));
  assign toBackground = shifter_1_out | shifter_11_out;  // OR_Gate or_3, 30 bits wide
  assign toBackground_2 = shifter_2_out | shifter_12_out;  // OR_Gate or_4, 30 bits wide
  assign toBackground_3 = shifter_3_out | shifter_13_out;  // OR_Gate or_5, 30 bits wide
  assign toBackground_4 = shifter_4_out | shifter_14_out;  // OR_Gate or_6, 30 bits wide
  assign toBackground_5 = shifter_5_out | shifter_15_out;  // OR_Gate or_7, 30 bits wide
  assign toBackground_6 = shifter_6_out | shifter_16_out;  // OR_Gate or_8, 30 bits wide
  // Probe on adder_5_out
  Adder #(.width(5)) adder_5 (.a(inPlayerShiftM), .b(5'b00001), .out(adder_5_out));  // open: cin, cout
  Comparator #(.width(5), .mode("unsigned")) comparator_5 (
    .a(inPlayerShiftM), .b(5'b11110), .eq(comparator_5_eq));  // open: gt, lt
  assign toBackground_7 = shifter_7_out | shifter_17_out;  // OR_Gate or_9, 30 bits wide
  assign toBackground_8 = shifter_8_out | shifter_18_out;  // OR_Gate or_10, 30 bits wide
  assign toBackground_9 = shifter_9_out | shifter_19_out;  // OR_Gate or_11, 30 bits wide
  assign toBackground_10 = shifter_10_out | shifter_20_out;  // OR_Gate or_12, 30 bits wide
  // Probe on multiplexer_1_out
  Multiplexer #(.width(2), .disabled(0), .enable("false")) multiplexer_1 (
    .in0(inPlayerShiftD), .in1(outPlayerShiftD), .out(multiplexer_1_out), .sel(comparator_5_eq));
  Comparator #(.width(2)) comparator_6 (.a(2'b00), .b(multiplexer_1_out), .eq(comparator_6_eq));  // open: gt, lt
  assign controlled_buffer_21_out = inFlag ? comparator_6_eq : 1'bz;  // Controlled_Buffer controlled_buffer_21
  Comparator #(.width(2)) comparator_7 (.a(2'b00), .b(adder_6_out), .eq(comparator_7_eq));  // open: gt, lt
  assign controlled_buffer_22_out = inFlag ? comparator_7_eq : 1'bz;  // Controlled_Buffer controlled_buffer_22
  Adder #(.width(2)) adder_6 (.a(multiplexer_1_out), .b(2'b01), .out(adder_6_out));  // open: cin, cout
  Pull_Resistor pull_resistor_25 (.node(controlled_buffer_21_out));
  Pull_Resistor pull_resistor_26 (.node(pull_resistor_26_node));
  assign pull_resistor_26_node = controlled_buffer_21_out ? 30'h279 : 30'bz;  // Controlled_Buffer controlled_buffer_23
  Pull_Resistor pull_resistor_27 (.node(pull_resistor_27_node));
  assign pull_resistor_27_node = controlled_buffer_21_out ? 30'h231 : 30'bz;  // Controlled_Buffer controlled_buffer_24
  Pull_Resistor pull_resistor_28 (.node(pull_resistor_28_node));
  assign pull_resistor_28_node = controlled_buffer_21_out ? 30'h279 : 30'bz;  // Controlled_Buffer controlled_buffer_25
  Pull_Resistor pull_resistor_29 (.node(pull_resistor_29_node));
  assign pull_resistor_29_node = controlled_buffer_21_out ? 30'h3ff : 30'bz;  // Controlled_Buffer controlled_buffer_26
  Pull_Resistor pull_resistor_30 (.node(pull_resistor_30_node));
  assign pull_resistor_30_node = controlled_buffer_21_out ? 30'hfc : 30'bz;  // Controlled_Buffer controlled_buffer_27
  Pull_Resistor pull_resistor_31 (.node(pull_resistor_31_node));
  assign pull_resistor_31_node = controlled_buffer_21_out ? 30'hfc : 30'bz;  // Controlled_Buffer controlled_buffer_28
  assign controlled_buffer_29_out = controlled_buffer_21_out ? 30'h3ff : 30'bz;  // Controlled_Buffer controlled_buffer_29
  Pull_Resistor pull_resistor_32 (.node(controlled_buffer_29_out));
  assign controlled_buffer_30_out = controlled_buffer_21_out ? 30'h279 : 30'bz;  // Controlled_Buffer controlled_buffer_30
  Pull_Resistor pull_resistor_33 (.node(controlled_buffer_30_out));
  assign controlled_buffer_31_out = controlled_buffer_21_out ? 30'h231 : 30'bz;  // Controlled_Buffer controlled_buffer_31
  Pull_Resistor pull_resistor_34 (.node(controlled_buffer_31_out));
  assign controlled_buffer_32_out = controlled_buffer_21_out ? 30'h201 : 30'bz;  // Controlled_Buffer controlled_buffer_32
  Pull_Resistor pull_resistor_35 (.node(controlled_buffer_32_out));
  Shifter #(.width(30)) shifter_21 (.in(pull_resistor_26_node), .\dist (adder_5_out), .out(shifter_21_out));
  Shifter #(.width(30)) shifter_22 (.in(pull_resistor_27_node), .\dist (adder_5_out), .out(shifter_22_out));
  Shifter #(.width(30)) shifter_23 (.in(pull_resistor_28_node), .\dist (adder_5_out), .out(shifter_23_out));
  Shifter #(.width(30)) shifter_24 (.in(pull_resistor_29_node), .\dist (adder_5_out), .out(shifter_24_out));
  Shifter #(.width(30)) shifter_25 (.in(pull_resistor_30_node), .\dist (adder_5_out), .out(shifter_25_out));
  Shifter #(.width(30)) shifter_26 (.in(pull_resistor_31_node), .\dist (adder_5_out), .out(shifter_26_out));
  Shifter #(.width(30)) shifter_27 (.in(controlled_buffer_29_out), .\dist (adder_5_out), .out(shifter_27_out));
  Shifter #(.width(30)) shifter_28 (.in(controlled_buffer_30_out), .\dist (adder_5_out), .out(shifter_28_out));
  Shifter #(.width(30)) shifter_29 (.in(controlled_buffer_31_out), .\dist (adder_5_out), .out(shifter_29_out));
  Shifter #(.width(30)) shifter_30 (.in(controlled_buffer_32_out), .\dist (adder_5_out), .out(shifter_30_out));
  assign not_2_out = ~adder_5_out;  // NOT_Gate not_2, 5 bits wide
  Adder #(.width(5)) adder_7 (.a(not_2_out), .b(5'b00001), .out(adder_7_out));  // open: cin, cout
  Pull_Resistor pull_resistor_36 (.node(controlled_buffer_22_out));
  Adder #(.width(5)) adder_8 (.a(5'b11110), .b(adder_7_out), .out(adder_8_out));  // open: cin, cout
  assign controlled_buffer_33_out = controlled_buffer_22_out ? 30'h279 : 30'bz;  // Controlled_Buffer controlled_buffer_33
  Pull_Resistor pull_resistor_37 (.node(controlled_buffer_33_out));
  Shifter #(.width(30), .shift("lr")) shifter_31 (
    .in(controlled_buffer_33_out), .\dist (adder_8_out), .out(shifter_31_out));
  assign controlled_buffer_34_out = controlled_buffer_22_out ? 30'h231 : 30'bz;  // Controlled_Buffer controlled_buffer_34
  Pull_Resistor pull_resistor_38 (.node(controlled_buffer_34_out));
  Shifter #(.width(30), .shift("lr")) shifter_32 (
    .in(controlled_buffer_34_out), .\dist (adder_8_out), .out(shifter_32_out));
  Pull_Resistor pull_resistor_39 (.node(pull_resistor_39_node));
  assign pull_resistor_39_node = controlled_buffer_22_out ? 30'h279 : 30'bz;  // Controlled_Buffer controlled_buffer_35
  Shifter #(.width(30), .shift("lr")) shifter_33 (
    .in(pull_resistor_39_node), .\dist (adder_8_out), .out(shifter_33_out));
  assign controlled_buffer_36_out = controlled_buffer_22_out ? 30'h3ff : 30'bz;  // Controlled_Buffer controlled_buffer_36
  Pull_Resistor pull_resistor_40 (.node(controlled_buffer_36_out));
  Shifter #(.width(30), .shift("lr")) shifter_34 (
    .in(controlled_buffer_36_out), .\dist (adder_8_out), .out(shifter_34_out));
  assign controlled_buffer_37_out = controlled_buffer_22_out ? 30'hfc : 30'bz;  // Controlled_Buffer controlled_buffer_37
  Pull_Resistor pull_resistor_41 (.node(controlled_buffer_37_out));
  Shifter #(.width(30), .shift("lr")) shifter_35 (
    .in(controlled_buffer_37_out), .\dist (adder_8_out), .out(shifter_35_out));
  assign controlled_buffer_38_out = controlled_buffer_22_out ? 30'hfc : 30'bz;  // Controlled_Buffer controlled_buffer_38
  Pull_Resistor pull_resistor_42 (.node(controlled_buffer_38_out));
  Shifter #(.width(30), .shift("lr")) shifter_36 (
    .in(controlled_buffer_38_out), .\dist (adder_8_out), .out(shifter_36_out));
  assign controlled_buffer_39_out = controlled_buffer_22_out ? 30'h3ff : 30'bz;  // Controlled_Buffer controlled_buffer_39
  Pull_Resistor pull_resistor_43 (.node(controlled_buffer_39_out));
  Shifter #(.width(30), .shift("lr")) shifter_37 (
    .in(controlled_buffer_39_out), .\dist (adder_8_out), .out(shifter_37_out));
  Pull_Resistor pull_resistor_44 (.node(pull_resistor_44_node));
  assign pull_resistor_44_node = controlled_buffer_22_out ? 30'h279 : 30'bz;  // Controlled_Buffer controlled_buffer_40
  Shifter #(.width(30), .shift("lr")) shifter_38 (
    .in(pull_resistor_44_node), .\dist (adder_8_out), .out(shifter_38_out));
  Pull_Resistor pull_resistor_45 (.node(pull_resistor_45_node));
  assign pull_resistor_45_node = controlled_buffer_22_out ? 30'h231 : 30'bz;  // Controlled_Buffer controlled_buffer_41
  Shifter #(.width(30), .shift("lr")) shifter_39 (
    .in(pull_resistor_45_node), .\dist (adder_8_out), .out(shifter_39_out));
  Pull_Resistor pull_resistor_46 (.node(pull_resistor_46_node));
  assign pull_resistor_46_node = controlled_buffer_22_out ? 30'h201 : 30'bz;  // Controlled_Buffer controlled_buffer_42
  Shifter #(.width(30), .shift("lr")) shifter_40 (
    .in(pull_resistor_46_node), .\dist (adder_8_out), .out(shifter_40_out));
  assign toFront = shifter_21_out | shifter_31_out;  // OR_Gate or_13, 30 bits wide
  assign toFront_2 = shifter_22_out | shifter_32_out;  // OR_Gate or_14, 30 bits wide
  assign toFront_3 = shifter_23_out | shifter_33_out;  // OR_Gate or_15, 30 bits wide
  assign toFront_4 = shifter_24_out | shifter_34_out;  // OR_Gate or_16, 30 bits wide
  assign toFront_5 = shifter_25_out | shifter_35_out;  // OR_Gate or_17, 30 bits wide
  assign toFront_6 = shifter_26_out | shifter_36_out;  // OR_Gate or_18, 30 bits wide
  assign toFront_7 = shifter_27_out | shifter_37_out;  // OR_Gate or_19, 30 bits wide
  assign toFront_8 = shifter_28_out | shifter_38_out;  // OR_Gate or_20, 30 bits wide
  assign toFront_9 = shifter_29_out | shifter_39_out;  // OR_Gate or_21, 30 bits wide
  assign toFront_10 = shifter_30_out | shifter_40_out;  // OR_Gate or_22, 30 bits wide

  assign outFlag = inFlag;
  assign outPlayerShiftM = inPlayerShiftM;
  assign outputBackShiftM = inputBackShiftM;

  // Notes on the sheet:
  //   MAKE SHIFT BY NEXT MATRICE
  //   MAKE SHIFT IN CURRENT MATRICE
  //   MAKE SHIFT IN CURRENT MATRICE
  //   MAKE SHIFT BY NEXT MATRICE
endmodule
