// Logisim project service.circ as structural Verilog: 9 circuits, main circuit leftShifter
// L
module leftShifter (
  input  [2:0] shiftCounts,
  input  [1:0] startShift,
  input  tactGen,
  input  reset,
  input  isSameLvl,
  output [4:0] shiftM,
  output [1:0] shiftD,
  output [2:0] keyBorder
);

  wire and_1_out, and_2_out, and_3_out, comparator_1_lt, comparator_2_eq, comparator_3_eq, comparator_4_lt,
       comparator_5_eq, comparator_6_eq, not_1_out, not_2_out, or_1_out, or_2_out, ticter;
  wire [1:0] displayPos_q;
  wire [2:0] controlled_buffer_2_out, or_3_out, pull_resistor_2_node;
  wire [4:0] matricePos_q;

  Counter #(.width(6), .max('h3f)) matricePos (
    .Q({matricePos_q, ticter}), .clk(tactGen), .clr(or_2_out));  // open: load, D, count, carry
  Pull_Resistor pull_resistor_1 (.node(tactGen));
  Shifter #(.width(5)) shifter_1 (.in(matricePos_q), .\dist (shiftCounts), .out(shiftM));
  Comparator #(.width(5), .mode("unsigned")) comparator_1 (
    .a(shiftM), .b(5'b11100), .lt(comparator_1_lt));  // open: gt, eq
  not not_1 (not_1_out, comparator_1_lt);
  Comparator #(.width(3), .mode("unsigned")) comparator_2 (
    .a(shiftCounts), .b(3'b010), .eq(comparator_2_eq));  // open: gt, lt
  Comparator #(.width(5), .mode("unsigned")) comparator_3 (
    .a(shiftM), .b(5'b11110), .eq(comparator_3_eq));  // open: gt, lt
  Comparator #(.width(3), .mode("unsigned")) comparator_4 (
    .a(shiftCounts), .b(3'b000), .lt(comparator_4_lt));  // open: gt, eq
  not not_2 (not_2_out, comparator_4_lt);
  Pull_Resistor pull_resistor_2 (.node(pull_resistor_2_node));
  assign pull_resistor_2_node = comparator_5_eq ? 3'b001 : 3'bz;  // Controlled_Buffer controlled_buffer_1
  Comparator #(.width(3), .mode("unsigned")) comparator_5 (
    .a(shiftCounts), .b(3'b000), .eq(comparator_5_eq));  // open: gt, lt
  assign controlled_buffer_2_out = comparator_6_eq ? 3'b010 : 3'bz;  // Controlled_Buffer controlled_buffer_2
  Comparator #(.width(3), .mode("unsigned")) comparator_6 (
    .a(shiftCounts), .b(3'b001), .eq(comparator_6_eq));  // open: gt, lt
  Pull_Resistor pull_resistor_3 (.node(controlled_buffer_2_out));
  and and_1 (and_1_out, ticter, isSameLvl);
  and and_2 (and_2_out, not_1_out, comparator_2_eq);
  or or_1 (or_1_out, and_2_out, and_3_out);
  and and_3 (and_3_out, comparator_3_eq, not_2_out);
  or or_2 (or_2_out, or_1_out, reset);
  assign or_3_out = pull_resistor_2_node | controlled_buffer_2_out;  // OR_Gate or_3, 3 bits wide
  Counter #(.width(2), .max('h3)) displayPos (
    .Q(displayPos_q), .clk(or_1_out), .clr(reset));  // open: load, D, count, carry
  Pull_Resistor pull_resistor_4 (.node(reset));
  assign keyBorder = and_1_out ? or_3_out : 3'bz;  // Controlled_Buffer controlled_buffer_3
  Pull_Resistor pull_resistor_5 (.node(keyBorder));
  Adder #(.width(2)) adder_1 (.a(displayPos_q), .b(startShift), .out(shiftD));  // open: cin, cout
endmodule

// R
module rightShifter (
  input  [1:0] shiftCounts,
  input  [1:0] startShift,
  input  tactGen,
  input  reset,
  input  isSameLvl,
  output [4:0] shiftM,
  output [1:0] shiftD,
  output [2:0] rKB
);

  wire _1_2tic, _1_4tic, and_1_out, comparator_1_eq, comparator_2_eq, comparator_3_eq, comparator_4_gt,
       comparator_5_eq, multiplexer_1_out, or_2_out, pull_resistor_2_node;
  wire [1:0] adder_2_out, displayPos_q, not_2_out;
  wire [4:0] controlled_buffer_3_out, controlled_buffer_4_out, not_1_out, or_1_out, pull_resistor_4_node,
       pull_resistor_7_node;
  wire [6:2] matricePos_q;
  wire [7:7] matricePos_q_2;

  Pull_Resistor pull_resistor_1 (.node(tactGen));
  Counter matricePos (
    .Q({matricePos_q_2[7], matricePos_q, _1_4tic, _1_2tic}), .clk(tactGen), .clr(or_2_out));  // open: load, D, count, carry
  Comparator #(.width(2), .mode("unsigned")) comparator_1 (
    .a(shiftCounts), .b(2'b00), .eq(comparator_1_eq));  // open: gt, lt
  Comparator #(.width(2), .mode("unsigned")) comparator_2 (
    .a(shiftCounts), .b(2'b01), .eq(comparator_2_eq));  // open: gt, lt
  Comparator #(.width(2), .mode("unsigned")) comparator_3 (
    .a(shiftCounts), .b(2'b10), .eq(comparator_3_eq));  // open: gt, lt
  Comparator #(.width(2), .mode("unsigned")) comparator_4 (
    .a(shiftCounts), .b(2'b10), .gt(comparator_4_gt));  // open: eq, lt
  Pull_Resistor pull_resistor_2 (.node(pull_resistor_2_node));
  Multiplexer #(.select(2), .disabled(0), .enable("false")) multiplexer_1 (
    .in0(tactGen), .in1(_1_2tic), .in2(_1_4tic), .in3(pull_resistor_2_node), .out(multiplexer_1_out),
    .sel(shiftCounts));
  Pull_Resistor pull_resistor_3 (.node(rKB));
  assign rKB = and_1_out ? 3'b001 : 3'bz;  // Controlled_Buffer controlled_buffer_1
  and and_1 (and_1_out, multiplexer_1_out, isSameLvl);
  Pull_Resistor pull_resistor_4 (.node(pull_resistor_4_node));
  assign pull_resistor_4_node = comparator_1_eq ? {matricePos_q[4:2], _1_4tic, _1_2tic} : 5'bz;  // Controlled_Buffer controlled_buffer_2
  assign or_1_out = pull_resistor_4_node | controlled_buffer_3_out | controlled_buffer_4_out;  // OR_Gate or_1, 5 bits wide
  assign controlled_buffer_3_out = comparator_2_eq ? {matricePos_q[5:2], _1_4tic} : 5'bz;  // Controlled_Buffer controlled_buffer_3
  Pull_Resistor pull_resistor_5 (.node(controlled_buffer_3_out));
  assign controlled_buffer_4_out = comparator_3_eq ? matricePos_q : 5'bz;  // Controlled_Buffer controlled_buffer_4
  Pull_Resistor pull_resistor_6 (.node(controlled_buffer_4_out));
  Pull_Resistor pull_resistor_7 (.node(pull_resistor_7_node));
  assign pull_resistor_7_node = comparator_4_gt ? matricePos_q : 5'bz;  // Controlled_Buffer controlled_buffer_5
  assign not_1_out = ~or_1_out;  // NOT_Gate not_1, 5 bits wide
  Comparator #(.width(5), .mode("unsigned")) comparator_5 (
    .a(or_1_out), .b(5'b11110), .eq(comparator_5_eq));  // open: gt, lt
  or or_2 (or_2_out, comparator_5_eq, reset);
  Adder #(.width(5)) adder_1 (.a(not_1_out), .b(5'b11110), .out(shiftM));  // open: cin, cout
  assign not_2_out = ~displayPos_q;  // NOT_Gate not_2, 2 bits wide
  Counter #(.width(2), .max('h3)) displayPos (
    .Q(displayPos_q), .clk(comparator_5_eq), .clr(reset));  // open: load, D, count, carry
  Pull_Resistor pull_resistor_8 (.node(reset));
  Adder #(.width(2)) adder_2 (.a(not_2_out), .b(2'b01), .out(adder_2_out));  // open: cin, cout
  Adder #(.width(2)) adder_3 (.a(adder_2_out), .b(startShift), .out(shiftD));  // open: cin, cout

  // Other names for the same wires on the sheet: _1tic = tactGen
endmodule

// cross
module computeIntresection (
  input  [4:0] backLen,
  input  [4:0] inBackM,
  input  [1:0] inBackD,
  input  [4:0] inFrogM,
  input  [1:0] inFrogD,
  input  inIntersect,
  input  doCompute,
  output outIntersect
);

  wire and_1_out, and_2_out, and_3_out, and_4_out, and_5_out, and_6_out, comparator_1_eq, comparator_2_eq,
       comparator_3_eq, comparator_4_gt, comparator_5_gt, comparator_6_lt, comparator_7_gt, comparator_8_lt,
       comparator_9_gt, comparator_10_gt, latency_1_out, latency_2_out, latency_3_out, latency_4_out,
       not_3_out, not_4_out, not_5_out, not_6_out, not_7_out, or_1_out;
  wire [1:0] adder_2_out, adder_3_out;
  wire [6:0] adder_1_out, adder_4_out, adder_5_out, adder_6_out, adder_7_out, adder_8_out, adder_9_out,
       adder_10_out, adder_11_out, adder_12_out, adder_13_out, bit_extender_1_out, bit_extender_2_out,
       bit_extender_3_out, bit_extender_4_out, bit_extender_5_out, controlled_buffer_1_out,
       controlled_buffer_2_out, multiplexer_1_out, multiplier_1_out, multiplier_2_out, not_1_out, not_2_out,
       subtractor_1_out, undriven, undriven_2;

  assign bit_extender_1_out = {{2{1'b0}}, backLen};  // Bit_Extender bit_extender_1
  assign bit_extender_2_out = {{2{1'b0}}, inBackM};  // Bit_Extender bit_extender_2
  Comparator #(.width(7), .mode("unsigned")) comparator_1 (
    .a(bit_extender_1_out), .b(7'b0010001), .eq(comparator_1_eq));  // open: gt, lt
  assign bit_extender_3_out = {{5{1'b0}}, inBackD};  // Bit_Extender bit_extender_3
  Adder #(.width(7)) adder_1 (.a(7'b0001100), .b(bit_extender_2_out), .out(adder_1_out));  // open: cin, cout
  Multiplexer #(.width(7), .disabled(0), .enable("false")) multiplexer_1 (
    .in0(bit_extender_2_out), .in1(adder_1_out), .out(multiplexer_1_out), .sel(comparator_1_eq));
  // Probe on inFrogD
  // Probe on bit_extender_3_out
  // Probe on bit_extender_4_out
  assign bit_extender_4_out = {{2{1'b0}}, inFrogM};  // Bit_Extender bit_extender_4
  assign bit_extender_5_out = {{5{1'b0}}, inFrogD};  // Bit_Extender bit_extender_5
  Multiplier #(.width(7)) multiplier_1 (
    .a(bit_extender_3_out), .b(7'b0011110), .out(multiplier_1_out));  // open: cin, cout
  Multiplier #(.width(7)) multiplier_2 (
    .a(bit_extender_5_out), .b(7'b0011110), .out(multiplier_2_out));  // open: cin, cout
  assign not_1_out = ~multiplexer_1_out;  // NOT_Gate not_1, 7 bits wide
  Adder #(.width(2)) adder_2 (.a(inFrogD), .b(2'b01), .out(adder_2_out));  // open: cin, cout
  assign not_2_out = ~bit_extender_4_out;  // NOT_Gate not_2, 7 bits wide
  Adder #(.width(2)) adder_3 (.a(inBackD), .b(2'b01), .out(adder_3_out));  // open: cin, cout
  // Probe on bit_extender_1_out
  // Probe on multiplexer_1_out
  Adder #(.width(7)) adder_4 (.a(bit_extender_1_out), .b(adder_5_out), .out(adder_4_out));  // open: cin, cout
  Adder #(.width(7)) adder_5 (.a(multiplexer_1_out), .b(multiplier_1_out), .out(adder_5_out));  // open: cin, cout
  Adder #(.width(7)) adder_6 (.a(7'b0001010), .b(adder_7_out), .out(adder_6_out));  // open: cin, cout
  Adder #(.width(7)) adder_7 (.a(bit_extender_4_out), .b(multiplier_2_out), .out(adder_7_out));  // open: cin, cout
  Adder #(.width(7)) adder_8 (.a(7'b0001010), .b(bit_extender_4_out), .out(adder_8_out));  // open: cin, cout
  Adder #(.width(7)) adder_9 (.a(adder_8_out), .b(adder_10_out), .out(adder_9_out));  // open: cin, cout
  Adder #(.width(7)) adder_10 (.a(7'b0000001), .b(not_1_out), .out(adder_10_out));  // open: cin, cout
  Comparator #(.width(2), .mode("unsigned")) comparator_2 (
    .a(inBackD), .b(adder_2_out), .eq(comparator_2_eq));  // open: gt, lt
  Adder #(.width(7)) adder_11 (.a(bit_extender_1_out), .b(multiplexer_1_out), .out(adder_11_out));  // open: cin, cout
  Adder #(.width(7)) adder_12 (.a(adder_11_out), .b(adder_13_out), .out(adder_12_out));  // open: cin, cout
  Adder #(.width(7)) adder_13 (.a(7'b0000001), .b(not_2_out), .out(adder_13_out));  // open: cin, cout
  Comparator #(.width(2), .mode("unsigned")) comparator_3 (
    .a(inFrogD), .b(adder_3_out), .eq(comparator_3_eq));  // open: gt, lt
  // Probe on adder_4_out
  Comparator #(.width(7)) comparator_4 (.a(adder_9_out), .b(7'b0011110), .gt(comparator_4_gt));  // open: eq, lt
  Comparator #(.width(7)) comparator_5 (.a(adder_12_out), .b(7'b0011110), .gt(comparator_5_gt));  // open: eq, lt
  and and_1 (and_1_out, comparator_4_gt, comparator_2_eq);
  and and_2 (and_2_out, comparator_5_gt, comparator_3_eq);
  Comparator #(.width(7), .mode("unsigned")) comparator_6 (
    .a(adder_6_out), .b(adder_5_out), .lt(comparator_6_lt));  // open: gt, eq
  not not_3 (not_3_out, comparator_6_lt);
  not not_4 (not_4_out, comparator_7_gt);
  Comparator #(.width(7), .mode("unsigned")) comparator_7 (
    .a(adder_6_out), .b(adder_4_out), .gt(comparator_7_gt));  // open: eq, lt
  Comparator #(.width(7), .mode("unsigned")) comparator_8 (
    .a(adder_7_out), .b(adder_5_out), .lt(comparator_8_lt));  // open: gt, eq
  not not_5 (not_5_out, comparator_8_lt);
  not not_6 (not_6_out, comparator_9_gt);
  Comparator #(.width(7), .mode("unsigned")) comparator_9 (
    .a(adder_7_out), .b(adder_4_out), .gt(comparator_9_gt));  // open: eq, lt
  Comparator #(.width(7), .mode("unsigned")) comparator_10 (
    .a(undriven), .b(7'b0011110), .gt(comparator_10_gt));  // open: eq, lt
  and and_3 (and_3_out, not_3_out, not_4_out);
  and and_4 (and_4_out, not_5_out, not_6_out);
  assign controlled_buffer_1_out = comparator_10_gt ? subtractor_1_out : 7'bz;  // Controlled_Buffer controlled_buffer_1
  Subtractor #(.width(7)) subtractor_1 (.a(undriven_2), .b(7'b0011110), .out(subtractor_1_out));  // open: bin, bout
  assign controlled_buffer_2_out = not_7_out ? undriven_2 : 7'bz;  // Controlled_Buffer controlled_buffer_2
  not not_7 (not_7_out, comparator_10_gt);
  or or_1 (or_1_out, and_3_out, and_4_out, and_1_out, and_2_out);
  Pull_Resistor pull_resistor_1 (.node(doCompute));
  Pull_Resistor pull_resistor_2 (.node(controlled_buffer_1_out));
  // OR_Gate or_2 has open pins: in0=controlled_buffer_1_out, in1=controlled_buffer_2_out, out=open
  Pull_Resistor pull_resistor_3 (.node(controlled_buffer_2_out));
  and and_5 (and_5_out, or_1_out, doCompute);
  Pull_Resistor pull_resistor_4 (.node(and_5_out));
  and and_6 (and_6_out, and_5_out, latency_1_out, latency_4_out);
  latency latency_1 (.in(and_5_out), .out(latency_1_out));
  latency latency_2 (.in(latency_3_out), .out(latency_2_out));
  latency latency_3 (.in(and_5_out), .out(latency_3_out));
  latency latency_4 (.in(latency_2_out), .out(latency_4_out));
  Pull_Resistor pull_resistor_5 (.node(inIntersect));
  or or_3 (outIntersect, inIntersect, and_6_out);
endmodule

// Y
module heightFlag (
  input  [3:0] height,
  input  [3:0] playerY,
  output eqY
);

  Comparator #(.width(4), .mode("unsigned")) comparator_1 (.a(height), .b(playerY), .eq(eqY));  // open: gt, lt
endmodule

module waterIntersect (
  input  [4:0] backLen,
  input  [4:0] inBackM,
  input  [1:0] inBackD,
  input  [4:0] inFrogM,
  input  [1:0] inFrogD,
  input  inIntersect,
  input  doIntersect,
  input  \event ,
  input  tact,
  output outIntersect,
  output A
);

  wire and_1_out, and_2_out, and_3_out, and_4_out, and_5_out, and_6_out, and_7_out, and_8_out, and_9_out,
       and_10_out, and_11_out, comparator_1_eq, comparator_2_eq, comparator_3_gt, comparator_4_gt,
       comparator_5_eq, comparator_6_eq, comparator_7_gt, comparator_8_gt, comparator_9_lt, comparator_10_gt,
       comparator_11_lt, comparator_12_gt, comparator_13_lt, comparator_14_gt, comparator_15_lt,
       comparator_16_gt, comparator_17_eq, comparator_18_eq, comparator_19_eq, latency_1_out, latency_2_out,
       latency_3_out, latency_4_out, latency_5_out, latency_6_out, not_5_out, not_6_out, not_7_out,
       not_8_out, not_9_out, not_10_out, not_11_out, not_12_out, not_13_out, or_1_out, or_2_out, or_3_out,
       or_4_out, or_6_out;
  wire [1:0] adder_1_out, adder_2_out, adder_9_out, adder_10_out, subtractor_1_out;
  wire [4:0] counter_1_q, subtractor_2_out;
  wire [6:0] adder_3_out, adder_4_out, adder_5_out, adder_6_out, adder_7_out, adder_8_out, adder_11_out,
       adder_12_out, adder_13_out, adder_14_out, adder_15_out, adder_16_out, adder_17_out, adder_18_out,
       adder_19_out, adder_20_out, adder_21_out, adder_22_out, adder_23_out, adder_24_out,
       bit_extender_1_out, bit_extender_2_out, bit_extender_3_out, bit_extender_4_out, bit_extender_5_out,
       bit_extender_6_out, bit_extender_7_out, multiplier_1_out, multiplier_2_out, multiplier_3_out,
       multiplier_4_out, not_1_out, not_2_out, not_3_out, not_4_out;

  assign not_1_out = ~bit_extender_2_out;  // NOT_Gate not_1, 7 bits wide
  Adder #(.width(2)) adder_1 (.a(inFrogD), .b(2'b01), .out(adder_1_out));  // open: cin, cout
  assign not_2_out = ~bit_extender_7_out;  // NOT_Gate not_2, 7 bits wide
  Adder #(.width(2)) adder_2 (.a(inBackD), .b(2'b01), .out(adder_2_out));  // open: cin, cout
  // Probe on subtractor_1_out
  Subtractor #(.width(2)) subtractor_1 (.a(inBackD), .b(2'b10), .out(subtractor_1_out));  // open: bin, bout
  // Probe on subtractor_1_out
  assign bit_extender_1_out = {{2{1'b0}}, backLen};  // Bit_Extender bit_extender_1
  assign bit_extender_2_out = {{2{1'b0}}, inBackM};  // Bit_Extender bit_extender_2
  assign bit_extender_3_out = {{5{1'b0}}, inBackD};  // Bit_Extender bit_extender_3
  Subtractor #(.width(5)) subtractor_2 (.a(inFrogM), .b({5{1'b0}}), .out(subtractor_2_out));  // open: bin, bout
  assign bit_extender_4_out = {{5{1'b0}}, inFrogD};  // Bit_Extender bit_extender_4
  Adder #(.width(7)) adder_3 (.a(7'b0000101), .b(bit_extender_7_out), .out(adder_3_out));  // open: cin, cout
  Adder #(.width(7)) adder_4 (.a(adder_3_out), .b(adder_5_out), .out(adder_4_out));  // open: cin, cout
  Adder #(.width(7)) adder_5 (.a(7'b0000001), .b(not_1_out), .out(adder_5_out));  // open: cin, cout
  Comparator #(.width(2), .mode("unsigned")) comparator_1 (
    .a(inBackD), .b(adder_1_out), .eq(comparator_1_eq));  // open: gt, lt
  Adder #(.width(7)) adder_6 (.a(bit_extender_1_out), .b(bit_extender_2_out), .out(adder_6_out));  // open: cin, cout
  Adder #(.width(7)) adder_7 (.a(adder_6_out), .b(adder_8_out), .out(adder_7_out));  // open: cin, cout
  Adder #(.width(7)) adder_8 (.a(7'b0000001), .b(not_2_out), .out(adder_8_out));  // open: cin, cout
  Comparator #(.width(2), .mode("unsigned")) comparator_2 (
    .a(inFrogD), .b(adder_2_out), .eq(comparator_2_eq));  // open: gt, lt
  assign bit_extender_5_out = {{5{1'b0}}, subtractor_1_out};  // Bit_Extender bit_extender_5
  assign bit_extender_6_out = {{5{1'b0}}, inFrogD};  // Bit_Extender bit_extender_6
  assign not_3_out = ~bit_extender_2_out;  // NOT_Gate not_3, 7 bits wide
  Adder #(.width(2)) adder_9 (.a(inFrogD), .b(2'b01), .out(adder_9_out));  // open: cin, cout
  assign not_4_out = ~bit_extender_7_out;  // NOT_Gate not_4, 7 bits wide
  Adder #(.width(2)) adder_10 (.a(subtractor_1_out), .b(2'b01), .out(adder_10_out));  // open: cin, cout
  assign bit_extender_7_out = {{2{1'b0}}, subtractor_2_out};  // Bit_Extender bit_extender_7
  Comparator #(.width(7)) comparator_3 (.a(adder_4_out), .b(7'b0011110), .gt(comparator_3_gt));  // open: eq, lt
  Comparator #(.width(7)) comparator_4 (.a(adder_7_out), .b(7'b0011110), .gt(comparator_4_gt));  // open: eq, lt
  Adder #(.width(7)) adder_11 (.a(7'b0000110), .b(bit_extender_7_out), .out(adder_11_out));  // open: cin, cout
  Adder #(.width(7)) adder_12 (.a(adder_11_out), .b(adder_13_out), .out(adder_12_out));  // open: cin, cout
  Adder #(.width(7)) adder_13 (.a(7'b0000001), .b(not_3_out), .out(adder_13_out));  // open: cin, cout
  Comparator #(.width(2), .mode("unsigned")) comparator_5 (
    .a(subtractor_1_out), .b(adder_9_out), .eq(comparator_5_eq));  // open: gt, lt
  Adder #(.width(7)) adder_14 (.a(bit_extender_1_out), .b(bit_extender_2_out), .out(adder_14_out));  // open: cin, cout
  Adder #(.width(7)) adder_15 (.a(adder_14_out), .b(adder_16_out), .out(adder_15_out));  // open: cin, cout
  Adder #(.width(7)) adder_16 (.a(7'b0000001), .b(not_4_out), .out(adder_16_out));  // open: cin, cout
  Comparator #(.width(2), .mode("unsigned")) comparator_6 (
    .a(inFrogD), .b(adder_10_out), .eq(comparator_6_eq));  // open: gt, lt
  Multiplier #(.width(7)) multiplier_1 (
    .a(bit_extender_3_out), .b(7'b0011110), .out(multiplier_1_out));  // open: cin, cout
  Multiplier #(.width(7)) multiplier_2 (
    .a(bit_extender_4_out), .b(7'b0011110), .out(multiplier_2_out));  // open: cin, cout
  and and_1 (and_1_out, comparator_3_gt, comparator_1_eq);
  and and_2 (and_2_out, comparator_4_gt, comparator_2_eq);
  and and_3 (and_3_out, comparator_7_gt, comparator_5_eq);
  Comparator #(.width(7)) comparator_7 (.a(adder_12_out), .b(7'b0011110), .gt(comparator_7_gt));  // open: eq, lt
  Comparator #(.width(7)) comparator_8 (.a(adder_15_out), .b(7'b0011110), .gt(comparator_8_gt));  // open: eq, lt
  and and_4 (and_4_out, comparator_8_gt, comparator_6_eq);
  // Probe on adder_17_out
  Adder #(.width(7)) adder_17 (.a(bit_extender_2_out), .b(multiplier_1_out), .out(adder_17_out));  // open: cin, cout
  Adder #(.width(7)) adder_18 (.a(bit_extender_7_out), .b(multiplier_2_out), .out(adder_18_out));  // open: cin, cout
  Multiplier #(.width(7)) multiplier_3 (
    .a(bit_extender_5_out), .b(7'b0011110), .out(multiplier_3_out));  // open: cin, cout
  // Probe on bit_extender_7_out
  Multiplier #(.width(7)) multiplier_4 (
    .a(bit_extender_6_out), .b(7'b0011110), .out(multiplier_4_out));  // open: cin, cout
  // Probe on adder_19_out
  // Probe on adder_20_out
  Adder #(.width(7)) adder_19 (.a(bit_extender_1_out), .b(adder_17_out), .out(adder_19_out));  // open: cin, cout
  Adder #(.width(7)) adder_20 (.a(7'b0000110), .b(adder_18_out), .out(adder_20_out));  // open: cin, cout
  Adder #(.width(7)) adder_21 (.a(bit_extender_2_out), .b(multiplier_3_out), .out(adder_21_out));  // open: cin, cout
  Adder #(.width(7)) adder_22 (.a(bit_extender_7_out), .b(multiplier_4_out), .out(adder_22_out));  // open: cin, cout
  // Probe on adder_18_out
  Comparator #(.width(7), .mode("unsigned")) comparator_9 (
    .a(adder_20_out), .b(adder_17_out), .lt(comparator_9_lt));  // open: gt, eq
  not not_5 (not_5_out, comparator_9_lt);
  and and_5 (and_5_out, not_5_out, not_6_out);
  not not_6 (not_6_out, comparator_10_gt);
  Comparator #(.width(7), .mode("unsigned")) comparator_10 (
    .a(adder_20_out), .b(adder_19_out), .gt(comparator_10_gt));  // open: eq, lt
  Comparator #(.width(7), .mode("unsigned")) comparator_11 (
    .a(adder_18_out), .b(adder_17_out), .lt(comparator_11_lt));  // open: gt, eq
  not not_7 (not_7_out, comparator_11_lt);
  and and_6 (and_6_out, not_7_out, not_8_out);
  not not_8 (not_8_out, comparator_12_gt);
  Comparator #(.width(7), .mode("unsigned")) comparator_12 (
    .a(adder_18_out), .b(adder_19_out), .gt(comparator_12_gt));  // open: eq, lt
  Adder #(.width(7)) adder_23 (.a(bit_extender_1_out), .b(adder_21_out), .out(adder_23_out));  // open: cin, cout
  Adder #(.width(7)) adder_24 (.a(7'b0000110), .b(adder_22_out), .out(adder_24_out));  // open: cin, cout
  Comparator #(.width(7), .mode("unsigned")) comparator_13 (
    .a(adder_24_out), .b(adder_21_out), .lt(comparator_13_lt));  // open: gt, eq
  not not_9 (not_9_out, comparator_13_lt);
  and and_7 (and_7_out, not_9_out, not_10_out);
  not not_10 (not_10_out, comparator_14_gt);
  Comparator #(.width(7), .mode("unsigned")) comparator_14 (
    .a(adder_24_out), .b(adder_23_out), .gt(comparator_14_gt));  // open: eq, lt
  Comparator #(.width(7), .mode("unsigned")) comparator_15 (
    .a(adder_22_out), .b(adder_21_out), .lt(comparator_15_lt));  // open: gt, eq
  not not_11 (not_11_out, comparator_15_lt);
  and and_8 (and_8_out, not_11_out, not_12_out);
  not not_12 (not_12_out, comparator_16_gt);
  Comparator #(.width(7), .mode("unsigned")) comparator_16 (
    .a(adder_22_out), .b(adder_23_out), .gt(comparator_16_gt));  // open: eq, lt
  or or_1 (or_1_out, and_5_out, and_6_out, and_1_out, and_2_out);
  not not_13 (not_13_out, or_2_out);
  or or_2 (or_2_out, or_1_out, or_4_out);
  or or_3 (or_3_out, doIntersect, \event );
  or or_4 (or_4_out, and_7_out, and_8_out, and_3_out, and_4_out);
  Counter #(.width(5), .max('h1f)) counter_1 (
    .load(and_11_out), .D(inFrogM), .Q(counter_1_q), .clk(and_9_out), .clr(A));  // open: count, carry
  and and_9 (and_9_out, tact, doIntersect);
  and and_10 (and_10_out, not_13_out, doIntersect);
  and and_11 (and_11_out, and_10_out, or_3_out);
  Comparator #(.width(5), .mode("unsigned")) comparator_17 (
    .a(counter_1_q), .b(5'b01010), .eq(comparator_17_eq));  // open: gt, lt
  or or_5 (A, comparator_17_eq, comparator_18_eq);
  Comparator #(.width(5), .mode("unsigned")) comparator_18 (
    .a(counter_1_q), .b(5'b10100), .eq(comparator_18_eq));  // open: gt, lt
  Comparator #(.width(5), .mode("unsigned")) comparator_19 (
    .a(counter_1_q), .b(5'b11110), .eq(comparator_19_eq));  // open: gt, lt
  or or_6 (or_6_out, inIntersect, and_10_out);
  latency latency_1 (.in(latency_2_out), .out(latency_1_out));
  latency latency_2 (.in(or_6_out), .out(latency_2_out));
  Pull_Resistor pull_resistor_1 (.node(inIntersect));
  latency latency_3 (.in(latency_4_out), .out(latency_3_out));
  latency latency_4 (.in(or_6_out), .out(latency_4_out));
  and and_12 (outIntersect, latency_3_out, or_6_out, latency_5_out, latency_6_out);
  latency latency_5 (.in(latency_1_out), .out(latency_5_out));
  latency latency_6 (.in(or_6_out), .out(latency_6_out));

  // Notes on the sheet:
  //   len+shift
  //   -shiftPM
  //   len+shift
  //   -shiftPM
  //   -shiftPM
  //   len+shift
  //   -shiftPM
  //   len-shiftPm+shiftBm>30
  //   len-shiftPm+shiftBm>30
  //   len-shiftPm+shiftBm>30
  //   Fl
  //   Bl
  //   Fl
endmodule

module smallLogIntersect (
  input  [4:0] backLen,
  input  [4:0] inBackM,
  input  [4:0] inFrogM,
  input  doIntersect,
  input  inIntersect,
  output outIntersect
);

  wire and_1_out, and_2_out, and_3_out, and_4_out, and_5_out, comparator_1_lt, comparator_2_gt,
       comparator_3_lt, comparator_4_gt, comparator_5_lt, comparator_6_gt, comparator_7_lt, comparator_8_gt,
       not_1_out, not_2_out, not_3_out, not_4_out, not_5_out, not_6_out, not_7_out, not_8_out, not_9_out,
       or_1_out, or_2_out;
  wire [6:0] adder_1_out, adder_2_out, adder_3_out, adder_4_out, adder_5_out, bit_extender_1_out,
       bit_extender_2_out, bit_extender_3_out;

  assign bit_extender_1_out = {{2{1'b0}}, inBackM};  // Bit_Extender bit_extender_1
  assign bit_extender_2_out = {{2{1'b0}}, inFrogM};  // Bit_Extender bit_extender_2
  assign bit_extender_3_out = {{2{1'b0}}, backLen};  // Bit_Extender bit_extender_3
  // Probe on bit_extender_2_out
  // Probe on 7'b0000111
  Adder #(.width(7)) adder_1 (.a(bit_extender_2_out), .b(7'b0011110), .out(adder_1_out));  // open: cin, cout
  // Probe on bit_extender_3_out
  // Probe on bit_extender_1_out
  // Probe on 7'b0000111
  // Probe on bit_extender_3_out
  // Probe on bit_extender_1_out
  Adder #(.width(7)) adder_2 (.a(7'b0000111), .b(adder_1_out), .out(adder_2_out));  // open: cin, cout
  Adder #(.width(7)) adder_3 (.a(bit_extender_3_out), .b(bit_extender_1_out), .out(adder_3_out));  // open: cin, cout
  Adder #(.width(7)) adder_4 (.a(7'b0000111), .b(bit_extender_2_out), .out(adder_4_out));  // open: cin, cout
  Adder #(.width(7)) adder_5 (.a(bit_extender_3_out), .b(bit_extender_1_out), .out(adder_5_out));  // open: cin, cout
  Comparator #(.width(7), .mode("unsigned")) comparator_1 (
    .a(adder_2_out), .b(bit_extender_1_out), .lt(comparator_1_lt));  // open: gt, eq
  Comparator #(.width(7), .mode("unsigned")) comparator_2 (
    .a(adder_2_out), .b(adder_5_out), .gt(comparator_2_gt));  // open: eq, lt
  Comparator #(.width(7), .mode("unsigned")) comparator_3 (
    .a(adder_1_out), .b(bit_extender_1_out), .lt(comparator_3_lt));  // open: gt, eq
  Comparator #(.width(7), .mode("unsigned")) comparator_4 (
    .a(adder_1_out), .b(adder_5_out), .gt(comparator_4_gt));  // open: eq, lt
  Comparator #(.width(7), .mode("unsigned")) comparator_5 (
    .a(adder_4_out), .b(bit_extender_1_out), .lt(comparator_5_lt));  // open: gt, eq
  not not_1 (not_1_out, comparator_5_lt);
  and and_1 (and_1_out, not_1_out, not_2_out);
  not not_2 (not_2_out, comparator_6_gt);
  Comparator #(.width(7), .mode("unsigned")) comparator_6 (
    .a(adder_4_out), .b(adder_3_out), .gt(comparator_6_gt));  // open: eq, lt
  Comparator #(.width(7), .mode("unsigned")) comparator_7 (
    .a(bit_extender_2_out), .b(bit_extender_1_out), .lt(comparator_7_lt));  // open: gt, eq
  not not_3 (not_3_out, comparator_7_lt);
  and and_2 (and_2_out, not_3_out, not_4_out);
  not not_4 (not_4_out, comparator_8_gt);
  Comparator #(.width(7), .mode("unsigned")) comparator_8 (
    .a(bit_extender_2_out), .b(adder_3_out), .gt(comparator_8_gt));  // open: eq, lt
  not not_5 (not_5_out, comparator_1_lt);
  and and_3 (and_3_out, not_5_out, not_6_out);
  not not_6 (not_6_out, comparator_2_gt);
  not not_7 (not_7_out, comparator_3_lt);
  and and_4 (and_4_out, not_7_out, not_8_out);
  not not_8 (not_8_out, comparator_4_gt);
  or or_1 (or_1_out, and_1_out, and_2_out);
  not not_9 (not_9_out, or_2_out);
  or or_2 (or_2_out, or_1_out, and_3_out, and_4_out);
  and and_5 (and_5_out, not_9_out, doIntersect);
  or or_3 (outIntersect, and_5_out, inIntersect);
  Pull_Resistor pull_resistor_1 (.node(inIntersect));

  // Notes on the sheet:
  //   BD * 30 + BM
  //   BD * 30 + BM
  //   Bh
  //   Bl
  //   Fl
  //   Bh
  //   Bl
  //   Fl
  //   Fh >= Bl && Fh <= Bh
  //   Fl >= Bl && Fl <= Bh
  //   Fh >= Bl && Fh <= Bh
  //   Fl >= Bl && Fl <= Bh
endmodule

module latency (
  input  in,
  output out
);

  wire not_1_out, not_2_out, not_3_out, not_4_out, not_5_out, not_6_out, not_7_out, not_8_out, not_9_out,
       not_10_out, not_11_out, not_12_out, not_13_out, not_14_out, not_15_out, not_16_out, not_17_out,
       not_18_out, not_19_out, not_20_out, not_21_out, not_22_out, not_23_out, not_24_out, not_25_out,
       not_26_out, not_27_out, not_28_out, not_29_out, not_30_out, not_31_out, not_32_out, not_33_out,
       not_34_out, not_35_out, not_36_out, not_37_out, not_38_out, not_39_out, not_40_out, not_41_out,
       not_42_out, not_43_out, not_44_out, not_45_out, not_46_out, not_47_out, not_48_out, not_49_out,
       not_50_out, not_51_out, not_53_out, not_54_out;

  not not_1 (not_1_out, not_2_out);
  not not_2 (not_2_out, in);
  not not_3 (not_3_out, not_6_out);
  not not_4 (not_4_out, not_3_out);
  not not_5 (not_5_out, not_4_out);
  not not_6 (not_6_out, not_1_out);
  not not_7 (not_7_out, not_5_out);
  not not_8 (not_8_out, not_9_out);
  not not_9 (not_9_out, not_7_out);
  not not_10 (not_10_out, not_8_out);
  not not_11 (not_11_out, not_10_out);
  not not_12 (not_12_out, not_13_out);
  not not_13 (not_13_out, not_11_out);
  not not_14 (not_14_out, not_12_out);
  not not_15 (not_15_out, not_14_out);
  not not_16 (not_16_out, not_18_out);
  not not_17 (not_17_out, not_16_out);
  not not_18 (not_18_out, not_15_out);
  not not_19 (not_19_out, not_21_out);
  not not_20 (not_20_out, not_17_out);
  not not_21 (not_21_out, not_20_out);
  not not_22 (not_22_out, not_19_out);
  not not_23 (not_23_out, not_24_out);
  not not_24 (not_24_out, not_26_out);
  not not_25 (not_25_out, not_23_out);
  not not_26 (not_26_out, not_22_out);
  not not_27 (not_27_out, not_28_out);
  not not_28 (not_28_out, not_25_out);
  not not_29 (not_29_out, not_30_out);
  not not_30 (not_30_out, not_27_out);
  not not_31 (not_31_out, not_32_out);
  not not_32 (not_32_out, not_29_out);
  not not_33 (not_33_out, not_31_out);
  not not_34 (not_34_out, not_33_out);
  not not_35 (not_35_out, not_34_out);
  not not_36 (not_36_out, not_37_out);
  not not_37 (not_37_out, not_35_out);
  not not_38 (not_38_out, not_36_out);
  not not_39 (not_39_out, not_40_out);
  not not_40 (not_40_out, not_42_out);
  not not_41 (not_41_out, not_39_out);
  not not_42 (not_42_out, not_38_out);
  not not_43 (not_43_out, not_41_out);
  not not_44 (not_44_out, not_45_out);
  not not_45 (not_45_out, not_43_out);
  not not_46 (not_46_out, not_44_out);
  not not_47 (not_47_out, not_48_out);
  not not_48 (not_48_out, not_49_out);
  not not_49 (not_49_out, not_50_out);
  not not_50 (not_50_out, not_46_out);
  not not_51 (not_51_out, not_53_out);
  not not_52 (out, not_51_out);
  not not_53 (not_53_out, not_54_out);
  not not_54 (not_54_out, not_47_out);
endmodule

module finishComputer (
  input  res,
  input  [1:0] playerD,
  input  isSameLvl,
  input  [4:0] playerM,
  output win,
  output [3:0] positions,
  output ok,
  output die
);

  wire and_1_out, and_2_out, and_3_out, and_4_out, and_5_out, and_6_out, and_7_out, and_8_out, and_9_out,
       and_10_out, and_11_out, and_12_out, and_13_out, and_14_out, comparator_1_eq, comparator_2_eq,
       comparator_3_eq, comparator_4_eq, comparator_5_lt, comparator_6_gt, not_1_out, not_2_out, not_3_out,
       not_4_out, not_5_out, not_6_out, or_1_out, or_2_out, register_1_q;

  not not_1 (not_1_out, not_1_out);
  Comparator #(.width(2), .mode("unsigned")) comparator_1 (
    .a(playerD), .b(2'b00), .eq(comparator_1_eq));  // open: gt, lt
  Comparator #(.width(2), .mode("unsigned")) comparator_2 (
    .a(playerD), .b(2'b11), .eq(comparator_2_eq));  // open: gt, lt
  Comparator #(.width(2), .mode("unsigned")) comparator_3 (
    .a(playerD), .b(2'b10), .eq(comparator_3_eq));  // open: gt, lt
  Comparator #(.width(2), .mode("unsigned")) comparator_4 (
    .a(playerD), .b(2'b01), .eq(comparator_4_eq));  // open: gt, lt
  Comparator #(.width(5), .mode("unsigned")) comparator_5 (
    .a(playerM), .b(5'b00100), .lt(comparator_5_lt));  // open: gt, eq
  Comparator #(.width(5), .mode("unsigned")) comparator_6 (
    .a(playerM), .b(5'b10011), .gt(comparator_6_gt));  // open: eq, lt
  Counter #(.width(1), .max('h1), .ongoal("stay")) counter_1 (
    .count(and_2_out), .Q(positions[0]), .clk(and_2_out), .clr(res));  // open: load, D, carry
  and and_1 (and_1_out, and_2_out, not_2_out);
  not not_2 (not_2_out, and_2_out);
  and and_2 (and_2_out, comparator_1_eq, ~or_1_out, isSameLvl);  // AND_Gate
  or or_1 (or_1_out, comparator_5_lt, comparator_6_gt);
  Counter #(.width(1), .max('h1), .ongoal("stay")) counter_2 (
    .count(and_5_out), .Q(positions[1]), .clk(and_5_out), .clr(res));  // open: load, D, carry
  and and_3 (and_3_out, and_5_out, not_3_out);
  not not_3 (not_3_out, and_5_out);
  and and_4 (and_4_out, comparator_3_eq, ~or_1_out, isSameLvl);  // AND_Gate
  and and_5 (and_5_out, comparator_2_eq, ~or_1_out, isSameLvl);  // AND_Gate
  and and_6 (and_6_out, isSameLvl, or_1_out);
  and and_7 (and_7_out, isSameLvl, not_4_out);
  not not_4 (not_4_out, isSameLvl);
  Counter #(.width(1), .max('h1), .ongoal("stay")) counter_3 (
    .count(and_4_out), .Q(positions[2]), .clk(and_4_out), .clr(res));  // open: load, D, carry
  and and_8 (and_8_out, and_4_out, not_5_out);
  not not_5 (not_5_out, and_4_out);
  and and_9 (and_9_out, comparator_4_eq, ~or_1_out, isSameLvl);  // AND_Gate
  Counter #(.width(1), .max('h1), .ongoal("stay")) counter_4 (
    .count(and_9_out), .Q(positions[3]), .clk(and_9_out), .clr(res));  // open: load, D, carry
  and and_10 (and_10_out, and_9_out, not_6_out);
  not not_6 (not_6_out, and_9_out);
  and and_11 (and_11_out, and_10_out, positions[3]);
  and and_12 (and_12_out, and_3_out, positions[1]);
  and and_13 (and_13_out, and_8_out, positions[2]);
  or or_2 (or_2_out, and_11_out, and_13_out, and_12_out, and_14_out);
  and and_14 (and_14_out, and_1_out, positions[0]);
  Register #(.width(1)) register_1 (.D(die), .en(die), .Q(register_1_q), .clk(die), .clr(and_7_out));
  or or_3 (die, or_2_out, and_6_out);
  and and_15 (win, positions[0], positions[1], positions[2], positions[3]);
  and and_16 (ok, isSameLvl, ~register_1_q);  // AND_Gate
endmodule

module _2_1turtlesIntersector (
  input  [4:0] backLen,
  input  [4:0] inBackM,
  input  [4:0] inFrogM,
  input  doIntersect,
  input  \event ,
  input  tact,
  input  inIntersect,
  input  tic,
  input  res,
  output outIntersect,
  output A,
  output [3:0] animState,
  output animState_2
);

  wire and_1_out, and_2_out, and_3_out, and_4_out, and_5_out, and_6_out, and_7_out, and_8_out,
       comparator_1_lt, comparator_2_gt, comparator_3_lt, comparator_4_gt, comparator_5_lt, comparator_6_gt,
       comparator_7_lt, comparator_8_gt, comparator_9_lt, comparator_10_gt, comparator_11_eq,
       comparator_12_eq, comparator_13_eq, latency_1_out, latency_2_out, latency_3_out, latency_4_out,
       latency_5_out, latency_6_out, not_1_out, not_2_out, not_3_out, not_4_out, not_5_out, not_6_out,
       not_7_out, not_8_out, not_9_out, or_1_out, or_2_out, or_3_out, or_4_out, or_5_out;
  wire [1:0] counter_1_q;
  wire [4:0] counter_2_q;
  wire [6:0] adder_1_out, adder_2_out, adder_3_out, adder_4_out, adder_5_out, bit_extender_1_out,
       bit_extender_2_out, bit_extender_3_out;

  Counter #(.width(6), .max('h3f)) counter_1 (
    .Q({animState, counter_1_q}), .clk(tic), .clr(res));  // open: load, D, count, carry
  // Probe on {animState, counter_1_q}
  // Probe on animState
  assign bit_extender_1_out = {{2{1'b0}}, backLen};  // Bit_Extender bit_extender_1
  assign bit_extender_2_out = {{2{1'b0}}, inBackM};  // Bit_Extender bit_extender_2
  assign bit_extender_3_out = {{2{1'b0}}, inFrogM};  // Bit_Extender bit_extender_3
  Adder #(.width(7)) adder_1 (.a(bit_extender_3_out), .b(7'b0011110), .out(adder_1_out));  // open: cin, cout
  Comparator #(.width(4), .mode("unsigned")) comparator_1 (
    .a(4'b0101), .b(animState), .lt(comparator_1_lt));  // open: gt, eq
  and and_1 (and_1_out, comparator_1_lt, comparator_2_gt);
  Comparator #(.width(4), .mode("unsigned")) comparator_2 (
    .a(4'b1010), .b(animState), .gt(comparator_2_gt));  // open: eq, lt
  // Probe on bit_extender_1_out
  // Probe on bit_extender_2_out
  // Probe on 7'b0000111
  // Probe on bit_extender_3_out
  // Probe on bit_extender_1_out
  // Probe on bit_extender_2_out
  // Probe on 7'b0000111
  // Probe on adder_2_out
  Adder #(.width(7)) adder_2 (.a(bit_extender_1_out), .b(bit_extender_2_out), .out(adder_2_out));  // open: cin, cout
  Adder #(.width(7)) adder_3 (.a(7'b0000111), .b(bit_extender_3_out), .out(adder_3_out));  // open: cin, cout
  Adder #(.width(7)) adder_4 (.a(bit_extender_1_out), .b(bit_extender_2_out), .out(adder_4_out));  // open: cin, cout
  Adder #(.width(7)) adder_5 (.a(7'b0000111), .b(adder_1_out), .out(adder_5_out));  // open: cin, cout
  // Probe on bit_extender_3_out
  // Probe on adder_3_out
  Comparator #(.width(7), .mode("unsigned")) comparator_3 (
    .a(adder_3_out), .b(bit_extender_2_out), .lt(comparator_3_lt));  // open: gt, eq
  not not_1 (not_1_out, comparator_3_lt);
  not not_2 (not_2_out, comparator_4_gt);
  Comparator #(.width(7), .mode("unsigned")) comparator_4 (
    .a(adder_3_out), .b(adder_2_out), .gt(comparator_4_gt));  // open: eq, lt
  Comparator #(.width(7), .mode("unsigned")) comparator_5 (
    .a(bit_extender_3_out), .b(bit_extender_2_out), .lt(comparator_5_lt));  // open: gt, eq
  not not_3 (not_3_out, comparator_5_lt);
  not not_4 (not_4_out, comparator_6_gt);
  Comparator #(.width(7), .mode("unsigned")) comparator_6 (
    .a(bit_extender_3_out), .b(adder_2_out), .gt(comparator_6_gt));  // open: eq, lt
  Comparator #(.width(7), .mode("unsigned")) comparator_7 (
    .a(adder_5_out), .b(bit_extender_2_out), .lt(comparator_7_lt));  // open: gt, eq
  not not_5 (not_5_out, comparator_7_lt);
  and and_2 (and_2_out, not_5_out, not_6_out);
  not not_6 (not_6_out, comparator_8_gt);
  Comparator #(.width(7), .mode("unsigned")) comparator_8 (
    .a(adder_5_out), .b(adder_4_out), .gt(comparator_8_gt));  // open: eq, lt
  Comparator #(.width(7), .mode("unsigned")) comparator_9 (
    .a(adder_1_out), .b(bit_extender_2_out), .lt(comparator_9_lt));  // open: gt, eq
  not not_7 (not_7_out, comparator_9_lt);
  and and_3 (and_3_out, not_7_out, not_8_out);
  not not_8 (not_8_out, comparator_10_gt);
  Comparator #(.width(7), .mode("unsigned")) comparator_10 (
    .a(adder_1_out), .b(adder_4_out), .gt(comparator_10_gt));  // open: eq, lt
  and and_4 (and_4_out, not_1_out, not_2_out);
  and and_5 (and_5_out, not_3_out, not_4_out);
  or or_1 (or_1_out, and_5_out, and_2_out, and_3_out);
  or or_2 (or_2_out, and_4_out, or_1_out);
  not not_9 (not_9_out, or_2_out);
  or or_3 (or_3_out, doIntersect, \event );
  Pull_Resistor pull_resistor_1 (.node(\event ));
  or or_4 (or_4_out, and_1_out, not_9_out);
  Counter #(.width(5), .max('h1f)) counter_2 (
    .load(and_8_out), .Q(counter_2_q), .clk(and_6_out), .clr(A));  // open: D, count, carry
  and and_6 (and_6_out, tact, doIntersect);
  and and_7 (and_7_out, or_4_out, doIntersect);
  and and_8 (and_8_out, and_7_out, or_3_out);
  Comparator #(.width(5), .mode("unsigned")) comparator_11 (
    .a(counter_2_q), .b(5'b01010), .eq(comparator_11_eq));  // open: gt, lt
  Comparator #(.width(5), .mode("unsigned")) comparator_12 (
    .a(counter_2_q), .b(5'b10100), .eq(comparator_12_eq));  // open: gt, lt
  Comparator #(.width(5), .mode("unsigned")) comparator_13 (
    .a(counter_2_q), .b(5'b11110), .eq(comparator_13_eq));  // open: gt, lt
  or or_5 (or_5_out, and_7_out, inIntersect);
  latency latency_1 (.in(or_5_out), .out(latency_1_out));
  or or_6 (A, comparator_11_eq, comparator_12_eq);
  latency latency_2 (.in(or_5_out), .out(latency_2_out));
  latency latency_3 (.in(latency_2_out), .out(latency_3_out));
  and and_9 (outIntersect, latency_3_out, or_5_out, or_5_out, latency_4_out, latency_6_out);
  latency latency_4 (.in(latency_5_out), .out(latency_4_out));
  latency latency_5 (.in(latency_1_out), .out(latency_5_out));
  latency latency_6 (.in(or_5_out), .out(latency_6_out));

  assign animState_2 = animState[1];

  // Notes on the sheet:
  //   BD * 30 + BM
  //   Fl
  //   Bh
  //   Bl
  //   Fl
  //   Fh >= Bl && Fh <= Bh
  //   Fl >= Bl && Fl <= Bh
endmodule
