// Logisim project statistics.circ as structural Verilog: 21 circuits, main circuit CdM-8
module CdM_8 (
  input  IRQ,
  input  [2:0] vector,
  input  clock,
  input  clear,
  output lAck,
  output in_out,
  output [3:0] I_Oadr,
  output I_Osel,
  output [7:0] I_Odat
);

  wire and_2_out, cdm_8_1_p2, cdm_8_1_p4, cdm_8_1_p5, cdm_8_1_p6, cdm_8_1_p7, cdm_8_1_p8, cdm_8_1_p9,
       cdm_8_1_p10, code, data, mem, not_1_out;
  wire [7:0] cdm_8_1_p14, cdm_8_1_p15;
  wire [7:4] cdm_8_1_p13;

  // Probe on cdm_8_1_p4
  // Probe on cdm_8_1_p2
  // Probe on cdm_8_1_p5
  // Probe on cdm_8_1_p6
  // Probe on cdm_8_1_p9
  // Probe on cdm_8_1_p7
  // Probe on cdm_8_1_p8
  Decoder decoder_1 (.out0(code), .out1(data), .sel(cdm_8_1_p10), .en(mem));
  assign I_Odat = not_1_out ? cdm_8_1_p14 : 8'bz;  // Controlled_Buffer controlled_buffer_1
  // Cdm_8_mark4_CdM_8 cdm_8_1: pin names not known; wires that end beside it: clock, cdm_8_1_p2, clear, cdm_8_1_p4, cdm_8_1_p5, cdm_8_1_p6, cdm_8_1_p7, cdm_8_1_p8, cdm_8_1_p9, cdm_8_1_p10, mem, in_out, {cdm_8_1_p13, I_Oadr}, cdm_8_1_p14, cdm_8_1_p15
  not not_1 (not_1_out, in_out);
  assign cdm_8_1_p15 = in_out ? I_Odat : 8'bz;  // Controlled_Buffer controlled_buffer_2
  Pull_Resistor pull_resistor_1 (.node(code));
  Pull_Resistor pull_resistor_2 (.node(data));
  and and_1 (I_Osel, and_2_out, clock, data);
  and and_2 (and_2_out, cdm_8_1_p13[4], cdm_8_1_p13[5], cdm_8_1_p13[6], cdm_8_1_p13[7]);
  ROM rom_1 (.addr({cdm_8_1_p13, I_Oadr}), .data(I_Odat), .sel(code));
  RAM ram_1 (.addr({cdm_8_1_p13, I_Oadr}), .data(I_Odat), .sel(data), .clk(clock), .ld(in_out), .clr(clear));

  // Other names for the same wires on the sheet: rd_wr = in_out

  // Notes on the sheet:
  //   contents of rom_1 (hex, n*v repeats v):
  //   c1 d1 8 c1 d1 80 c1 d9 c5 d0 f8 d1 3 a1 ee 10 d0 f1 b1 5 e1 49 d0 f3 b1 5 e1 33 d0 f5 b1 5 e1 27 d5
  //   ee 10 ee 31 d6 87 d6 97 35 d0 f5 a1 ee 10 ee 47 b0 88 eb 3d d1 10 d6 87 ee 34 d6 97 d6 b4 35 d0 f3
  //   a1 ee 71 ee 5d b0 88 eb 53 d1 f6 d6 87 ee 4a d6 97 d6 a1 35 d0 f1 a1 ee 5d d0 f8 b1 5 e1 6f c1 d1 6b
  //   c1 d1 0 c1 d9 c5 d4 ee 71 ee 10 d0 f9 b1 d0 4 74 e1 85 c1 d1 81 c1 d1 0 c1 d9 c5 d4 ee 87 ee 10 d0
  //   f6 b0 11 ea 93 35 d0 f6 a1 ee 96 d0 f6 a1 d7 d0 f7 b0 71 ea a0 d0 f7 a1 d7 d1 f1 b5 d0 f8 b0 31 ea
  //   b0 35 d0 f8 a1 ee b3 d0 f8 a1 d7 d1 f3 b5 d0 f9 b0 11 d0 f9 a1 d7 d2 f1 bb 8f ab d9 d2 f3 bb 8f ab
  //   d9 d2 f5 bb 8f ab d9 31*0 bf 0 c5 0 cb
endmodule

module timer (
  input  clock,
  input  clear,
  output [31:0] the_1_st_line_of_the_picture,
  output [31:0] the_11_th_line_of_the_picture,
  output [31:0] the_1_st_line_of_the_picture_2,
  output [31:0] the_11_th_line_of_the_picture_2,
  output [31:0] the_2_nd_line_of_the_picture,
  output [31:0] the_12_th_line_of_the_picture,
  output [31:0] the_2_nd_line_of_the_picture_2,
  output [31:0] the_12_th_line_of_the_picture_2,
  output [31:0] the_1_st_line_of_the_picture_3,
  output [31:0] the_17_th_line_of_the_picture,
  output [31:0] the_1_st_line_of_the_picture_4,
  output [31:0] the_17_th_line_of_the_picture_2,
  output [31:0] the_3_rd_line_of_the_picture,
  output [31:0] the_13_th_line_of_the_picture,
  output [31:0] the_3_rd_line_of_the_picture_2,
  output [31:0] the_13_th_line_of_the_picture_2,
  output [31:0] the_2_nd_line_of_the_picture_3,
  output [31:0] the_18_th_line_of_the_picture,
  output [31:0] the_2_nd_line_of_the_picture_4,
  output [31:0] the_18_th_line_of_the_picture_2,
  output [31:0] the_4_th_line_of_the_picture,
  output [31:0] the_14_th_line_of_the_picture,
  output [31:0] the_4_th_line_of_the_picture_2,
  output [31:0] the_14_th_line_of_the_picture_2,
  output [31:0] the_3_rd_line_of_the_picture_3,
  output [31:0] the_19_th_line_of_the_picture,
  output [31:0] the_3_rd_line_of_the_picture_4,
  output [31:0] the_19_th_line_of_the_picture_2,
  output [31:0] the_5_th_line_of_the_picture,
  output [31:0] the_15_th_line_of_the_picture,
  output [31:0] the_5_th_line_of_the_picture_2,
  output [31:0] the_15_th_line_of_the_picture_2,
  output [31:0] the_4_th_line_of_the_picture_3,
  output [31:0] the_20_th_line_of_the_picture,
  output [31:0] the_4_th_line_of_the_picture_4,
  output [31:0] the_20_th_line_of_the_picture_2,
  output [31:0] the_6_th_line_of_the_picture,
  output [31:0] the_16_th_line_of_the_picture,
  output [31:0] the_6_th_line_of_the_picture_2,
  output [31:0] the_16_th_line_of_the_picture_2,
  output [31:0] the_5_th_line_of_the_picture_3,
  output [31:0] the_21_st_line_of_the_picture,
  output [31:0] the_5_th_line_of_the_picture_4,
  output [31:0] the_21_st_line_of_the_picture_2,
  output [31:0] the_7_th_line_of_the_picture,
  output [31:0] the_17_th_line_of_the_picture_3,
  output [31:0] the_7_th_line_of_the_picture_2,
  output [31:0] the_17_th_line_of_the_picture_4,
  output [31:0] the_6_th_line_of_the_picture_3,
  output [31:0] the_22_nd_line_of_the_picture,
  output [31:0] the_6_th_line_of_the_picture_4,
  output [31:0] the_22_nd_line_of_the_picture_2,
  output [31:0] the_8_th_line_of_the_picture,
  output [31:0] the_18_th_line_of_the_picture_3,
  output [31:0] the_8_th_line_of_the_picture_2,
  output [31:0] the_18_th_line_of_the_picture_4,
  output [31:0] the_7_th_line_of_the_picture_3,
  output [31:0] the_23_rd_line_of_the_picture,
  output [31:0] the_7_th_line_of_the_picture_4,
  output [31:0] the_23_rd_line_of_the_picture_2,
  output [31:0] the_9_th_line_of_the_picture,
  output [31:0] the_19_th_line_of_the_picture_3,
  output [31:0] the_9_th_line_of_the_picture_2,
  output [31:0] the_19_th_line_of_the_picture_4,
  output [31:0] the_8_th_line_of_the_picture_3,
  output [31:0] the_24_th_line_of_the_picture,
  output [31:0] the_8_th_line_of_the_picture_4,
  output [31:0] the_24_th_line_of_the_picture_2,
  output [31:0] the_10_th_line_of_the_picture,
  output [31:0] the_20_th_line_of_the_picture_3,
  output [31:0] the_10_th_line_of_the_picture_2,
  output [31:0] the_20_th_line_of_the_picture_4,
  output [31:0] the_9_th_line_of_the_picture_3,
  output [31:0] the_25_th_line_of_the_picture,
  output [31:0] the_9_th_line_of_the_picture_4,
  output [31:0] the_25_th_line_of_the_picture_2,
  output [31:0] the_10_th_line_of_the_picture_3,
  output [31:0] the_26_th_line_of_the_picture,
  output [31:0] the_10_th_line_of_the_picture_4,
  output [31:0] the_26_th_line_of_the_picture_2,
  output [3:0] the_first_digit,
  output [3:0] the_second_digit,
  output [31:0] the_11_th_line_of_the_picture_3,
  output [31:0] the_27_th_line_of_the_picture,
  output [31:0] the_11_th_line_of_the_picture_4,
  output [31:0] the_27_th_line_of_the_picture_2,
  output [31:0] time_flow__time_shift____right,
  output [31:0] the_12_th_line_of_the_picture_3,
  output [31:0] the_28_th_line_of_the_picture,
  output [31:0] the_12_th_line_of_the_picture_4,
  output [31:0] the_28_th_line_of_the_picture_2,
  output [31:0] time_flow__time_shift____left,
  output [31:0] the_13_th_line_of_the_picture_3,
  output [31:0] the_29_th_line_of_the_picture,
  output [31:0] the_13_th_line_of_the_picture_4,
  output [31:0] the_29_th_line_of_the_picture_2,
  output time_is_gone,
  output [31:0] the_14_th_line_of_the_picture_3,
  output [31:0] the_30_th_line_of_the_picture,
  output [31:0] the_14_th_line_of_the_picture_4,
  output [31:0] the_30_th_line_of_the_picture_2,
  output [31:0] the_15_th_line_of_the_picture_3,
  output [31:0] the_31_st_line_of_the_picture,
  output [31:0] the_15_th_line_of_the_picture_4,
  output [31:0] the_31_st_line_of_the_picture_2,
  output [31:0] the_16_th_line_of_the_picture_3,
  output [31:0] the_32_nd_line_of_the_picture,
  output [31:0] the_16_th_line_of_the_picture_4,
  output [31:0] the_32_nd_line_of_the_picture_2
);

  wire clock_t, comparator_1_gt, latency_2_carry, latency_carry, not_1_out, not_2_out, not_3_out, not_4_out,
       or_1_out, out, small_latency_1_delayed_signal, time_is_gone_t;
  wire [4:0] multiplier_1_out, multiplier_2_out;
  wire [5:0] pull_resistor_12_node, subtractor_1_out, time_q;
  wire [7:0] bit_extender_1_out;
  wire [31:0] shifter_1_out, shifter_2_out;

  DotMatrix #(.inputtype("row"), .matrixcols(32), .matrixrows(32)) dotmatrix_1 (
    .row0({32{1'b0}}), .row1({32{1'b0}}), .row2(32'h7ffe7ffe), .row3(32'h7ffe7ffe), .row4(32'h7ffe7ffe),
    .row5(32'h7ffe7ffe), .row6(32'h7ffe7ffe), .row7(32'h7ffe7ffe), .row8(32'h7e007e0), .row9(32'h7e007e0),
    .row10(32'h7e007e0), .row11(32'h7e007e0), .row12(32'h7e007e0), .row13(32'h7e007e0), .row14(32'h7e007e0),
    .row15(32'h7e007e0), .row16(32'h7e007e0), .row17(32'h7e007e0), .row18(32'h7e007e0), .row19(32'h7e007e0),
    .row20(32'h7e007e0), .row21(32'h7e007e0), .row22(32'h7e007e0), .row23(32'h7e007e0), .row24(32'h7e007e0),
    .row25(32'h7e07ffe), .row26(32'h7e07ffe), .row27(32'h7e07ffe), .row28(32'h7e07ffe), .row29(32'h7e07ffe),
    .row30(32'h7e07ffe), .row31({32{1'b0}}));
  DotMatrix #(.inputtype("row"), .matrixcols(32), .matrixrows(32)) dotmatrix_2 (
    .row0({32{1'b0}}), .row1({32{1'b0}}), .row2(32'h7e07e7fe), .row3(32'h7e07e7fe), .row4(32'h7f0fe7fe),
    .row5(32'h7f0fe7fe), .row6(32'h7f0fe7fe), .row7(32'h7f9fe7e0), .row8(32'h7f9fe7e0), .row9(32'h7f9fe7e0),
    .row10(32'h7ef7e7e0), .row11(32'h7ef7e7e0), .row12(32'h7ef7e7e0), .row13(32'h7e67e7fe),
    .row14(32'h7e67e7fe), .row15(32'h7e67e7fe), .row16(32'h7e07e7fe), .row17(32'h7e07e7fe),
    .row18(32'h7e07e7fe), .row19(32'h7e07e7e0), .row20(32'h7e07e7e0), .row21(32'h7e07e7e0),
    .row22(32'h7e07e7e0), .row23(32'h7e07e7e0), .row24(32'h7e07e7e0), .row25(32'h7e07e7fe),
    .row26(32'h7e07e7fe), .row27(32'h7e07e7fe), .row28(32'h7e07e7fe), .row29(32'h7e07e7fe),
    .row30(32'h7e07e7fe), .row31({32{1'b0}}));
  not not_1 (not_1_out, time_is_gone_t);
  assign clock_t = not_1_out ? clock : 1'bz;  // Controlled_Buffer controlled_buffer_1
  Pull_Resistor pull_resistor_1 (.node(clock_t));
  Counter #(.width(6), .max('h20)) \time  (
    .count(latency_carry), .Q(time_q), .carry(out), .clk(latency_carry), .clr(clear));  // open: load, D
  Counter #(.width(5), .max('h1f)) latency (
    .count(clock_t), .carry(latency_carry), .clk(clock_t), .clr(clear));  // open: load, D, Q
  DotMatrix #(.inputtype("row"), .matrixcols(32), .matrixrows(20)) dotmatrix_3 (
    .row0({32{1'b0}}), .row1({32{1'b0}}), .row2(32'h3f03fe0), .row3(32'hff81fe0), .row4(32'h1ffc0fe0),
    .row5(32'h3ffe07f0), .row6(32'h3f3e03f0), .row7(32'h3e1e01f0), .row8(32'h3c1e01f0), .row9(32'h3c1e00f8),
    .row10(32'h3c1e00f8), .row11(32'h3c1e0078), .row12(32'h3c1e0038), .row13(32'h3c3e0038),
    .row14(32'h3e7e0038), .row15(32'h3ffe001c), .row16(32'h1ffc001c), .row17(32'hff8000e),
    .row18(32'h7e00007), .row19({32{1'b0}}));
  assign the_1_st_line_of_the_picture = out ? {32{1'b0}} : 32'bz;  // Controlled_Buffer controlled_buffer_2
  Pull_Resistor pull_resistor_2 (.node(the_1_st_line_of_the_picture));
  Pull_Resistor pull_resistor_3 (.node(the_2_nd_line_of_the_picture));
  assign the_2_nd_line_of_the_picture = out ? {32{1'b0}} : 32'bz;  // Controlled_Buffer controlled_buffer_3
  assign the_3_rd_line_of_the_picture = out ? 32'h3f03fe0 : 32'bz;  // Controlled_Buffer controlled_buffer_4
  Pull_Resistor pull_resistor_4 (.node(the_3_rd_line_of_the_picture));
  Pull_Resistor pull_resistor_5 (.node(the_4_th_line_of_the_picture));
  assign the_4_th_line_of_the_picture = out ? 32'hff81fe0 : 32'bz;  // Controlled_Buffer controlled_buffer_5
  Pull_Resistor pull_resistor_6 (.node(the_5_th_line_of_the_picture));
  assign the_5_th_line_of_the_picture = out ? 32'h1ffc0fe0 : 32'bz;  // Controlled_Buffer controlled_buffer_6
  assign the_6_th_line_of_the_picture = out ? 32'h3ffe07f0 : 32'bz;  // Controlled_Buffer controlled_buffer_7
  Pull_Resistor pull_resistor_7 (.node(the_6_th_line_of_the_picture));
  assign the_7_th_line_of_the_picture = out ? 32'h3f3e03f0 : 32'bz;  // Controlled_Buffer controlled_buffer_8
  Pull_Resistor pull_resistor_8 (.node(the_7_th_line_of_the_picture));
  Pull_Resistor pull_resistor_9 (.node(the_8_th_line_of_the_picture));
  assign the_8_th_line_of_the_picture = out ? 32'h3e1e01f0 : 32'bz;  // Controlled_Buffer controlled_buffer_9
  Pull_Resistor pull_resistor_10 (.node(the_9_th_line_of_the_picture));
  assign the_9_th_line_of_the_picture = out ? 32'h3c1e01f0 : 32'bz;  // Controlled_Buffer controlled_buffer_10
  assign the_10_th_line_of_the_picture = out ? 32'h3c1e00f8 : 32'bz;  // Controlled_Buffer controlled_buffer_11
  Pull_Resistor pull_resistor_11 (.node(the_10_th_line_of_the_picture));
  Subtractor #(.width(6)) subtractor_1 (.a(6'b100000), .b(time_q), .out(subtractor_1_out));  // open: bin, bout
  not not_2 (not_2_out, out);
  and and_1 (time_is_gone, not_2_out, out);
  get_the_second_digit get_the_second_digit_1 (.number(bit_extender_1_out), .digit(the_first_digit));
  assign bit_extender_1_out = {{2{1'b0}}, subtractor_1_out};  // Bit_Extender bit_extender_1
  get_the_third_digit get_the_third_digit_1 (.number(bit_extender_1_out), .digit(the_second_digit));
  Comparator #(.width(6), .mode("unsigned")) comparator_1 (
    .a(6'b010000), .b(time_q), .gt(comparator_1_gt));  // open: eq, lt
  not not_3 (not_3_out, comparator_1_gt);
  Pull_Resistor pull_resistor_12 (.node(pull_resistor_12_node));
  assign pull_resistor_12_node = not_3_out ? time_q : 6'bz;  // Controlled_Buffer controlled_buffer_12
  Pull_Resistor pull_resistor_13 (.node(the_11_th_line_of_the_picture));
  assign the_11_th_line_of_the_picture = out ? 32'h3c1e00f8 : 32'bz;  // Controlled_Buffer controlled_buffer_13
  Pull_Resistor pull_resistor_14 (.node(the_12_th_line_of_the_picture));
  assign the_12_th_line_of_the_picture = out ? 32'h3c1e0078 : 32'bz;  // Controlled_Buffer controlled_buffer_14
  assign the_13_th_line_of_the_picture = out ? 32'h3c1e0038 : 32'bz;  // Controlled_Buffer controlled_buffer_15
  Pull_Resistor pull_resistor_15 (.node(the_13_th_line_of_the_picture));
  Pull_Resistor pull_resistor_16 (.node(the_14_th_line_of_the_picture));
  assign the_14_th_line_of_the_picture = out ? 32'h3c3e0038 : 32'bz;  // Controlled_Buffer controlled_buffer_16
  Pull_Resistor pull_resistor_17 (.node(the_15_th_line_of_the_picture));
  assign the_15_th_line_of_the_picture = out ? 32'h3e7e0038 : 32'bz;  // Controlled_Buffer controlled_buffer_17
  Pull_Resistor pull_resistor_18 (.node(the_16_th_line_of_the_picture));
  assign the_16_th_line_of_the_picture = out ? 32'h3ffe001c : 32'bz;  // Controlled_Buffer controlled_buffer_18
  Pull_Resistor pull_resistor_19 (.node(the_17_th_line_of_the_picture_3));
  assign the_17_th_line_of_the_picture_3 = out ? 32'h1ffc001c : 32'bz;  // Controlled_Buffer controlled_buffer_19
  Pull_Resistor pull_resistor_20 (.node(the_18_th_line_of_the_picture_3));
  assign the_18_th_line_of_the_picture_3 = out ? 32'hff8000e : 32'bz;  // Controlled_Buffer controlled_buffer_20
  assign the_19_th_line_of_the_picture_3 = out ? 32'h7e00007 : 32'bz;  // Controlled_Buffer controlled_buffer_21
  Pull_Resistor pull_resistor_21 (.node(the_19_th_line_of_the_picture_3));
  Pull_Resistor pull_resistor_22 (.node(the_20_th_line_of_the_picture_3));
  assign the_20_th_line_of_the_picture_3 = out ? {32{1'b0}} : 32'bz;  // Controlled_Buffer controlled_buffer_22
  Multiplier #(.width(5)) multiplier_1 (.a(time_q[4:0]), .b(5'b00010), .out(multiplier_1_out));  // open: cin, cout
  Shifter #(.width(32)) shifter_1 (.in({32{1'b1}}), .\dist (multiplier_1_out), .out(shifter_1_out));
  Shifter #(.width(32)) shifter_2 (.in({32{1'b1}}), .\dist (multiplier_2_out), .out(shifter_2_out));
  Multiplier #(.width(5)) multiplier_2 (
    .a(pull_resistor_12_node[4:0]), .b(5'b00010), .out(multiplier_2_out));  // open: cin, cout
  Counter #(.width(2), .max('h3)) latency_2 (
    .count(clock), .carry(latency_2_carry), .clk(clock), .clr(clear));  // open: load, D, Q
  Pull_Resistor pull_resistor_23 (.node(time_flow__time_shift____right));
  assign time_flow__time_shift____right = comparator_1_gt ? shifter_1_out : 32'bz;  // Controlled_Buffer controlled_buffer_23
  Pull_Resistor pull_resistor_24 (.node(time_flow__time_shift____left));
  assign time_flow__time_shift____left = not_4_out ? shifter_2_out : 32'bz;  // Controlled_Buffer controlled_buffer_24
  not not_4 (not_4_out, out);
  Register #(.width(1)) u_time_is_gone (
    .D(out), .Q(time_is_gone_t), .clk(small_latency_1_delayed_signal), .clr(or_1_out));  // open: en
  small_latency small_latency_1 (.signal(clock_t), .delayed_signal(small_latency_1_delayed_signal));
  or or_1 (or_1_out, clear, latency_2_carry);
  DotMatrix #(.inputtype("row"), .matrixcols(32), .matrixrows(20)) dotmatrix_4 (
    .row0({32{1'b0}}), .row1({32{1'b0}}), .row2(32'h7fc7ffc), .row3(32'h7f8fff8), .row4(32'h7f1fff0),
    .row5(32'hfe1fff0), .row6(32'hfc01ff0), .row7(32'hf801f00), .row8(32'h1f801f00), .row9(32'h1f003e00),
    .row10(32'h1f003e00), .row11(32'h1e003e00), .row12(32'h1c007c00), .row13(32'h1c007c00),
    .row14(32'h1c007c00), .row15(32'h3800f800), .row16(32'h3800f800), .row17(32'h7000f800),
    .row18(32'he000f800), .row19({32{1'b0}}));
  Pull_Resistor pull_resistor_25 (.node(the_1_st_line_of_the_picture_2));
  assign the_1_st_line_of_the_picture_2 = out ? {32{1'b0}} : 32'bz;  // Controlled_Buffer controlled_buffer_25
  Pull_Resistor pull_resistor_26 (.node(the_2_nd_line_of_the_picture_2));
  assign the_2_nd_line_of_the_picture_2 = out ? {32{1'b0}} : 32'bz;  // Controlled_Buffer controlled_buffer_26
  Pull_Resistor pull_resistor_27 (.node(the_3_rd_line_of_the_picture_2));
  assign the_3_rd_line_of_the_picture_2 = out ? 32'h7fc7ffc : 32'bz;  // Controlled_Buffer controlled_buffer_27
  Pull_Resistor pull_resistor_28 (.node(the_4_th_line_of_the_picture_2));
  assign the_4_th_line_of_the_picture_2 = out ? 32'h7f8fff8 : 32'bz;  // Controlled_Buffer controlled_buffer_28
  assign the_5_th_line_of_the_picture_2 = out ? 32'h7f1fff0 : 32'bz;  // Controlled_Buffer controlled_buffer_29
  Pull_Resistor pull_resistor_29 (.node(the_5_th_line_of_the_picture_2));
  assign the_6_th_line_of_the_picture_2 = out ? 32'hfe1fff0 : 32'bz;  // Controlled_Buffer controlled_buffer_30
  Pull_Resistor pull_resistor_30 (.node(the_6_th_line_of_the_picture_2));
  Pull_Resistor pull_resistor_31 (.node(the_7_th_line_of_the_picture_2));
  assign the_7_th_line_of_the_picture_2 = out ? 32'hfc01ff0 : 32'bz;  // Controlled_Buffer controlled_buffer_31
  assign the_8_th_line_of_the_picture_2 = out ? 32'hf801f00 : 32'bz;  // Controlled_Buffer controlled_buffer_32
  Pull_Resistor pull_resistor_32 (.node(the_8_th_line_of_the_picture_2));
  assign the_9_th_line_of_the_picture_2 = out ? 32'h1f801f00 : 32'bz;  // Controlled_Buffer controlled_buffer_33
  Pull_Resistor pull_resistor_33 (.node(the_9_th_line_of_the_picture_2));
  Pull_Resistor pull_resistor_34 (.node(the_10_th_line_of_the_picture_2));
  assign the_10_th_line_of_the_picture_2 = out ? 32'h1f003e00 : 32'bz;  // Controlled_Buffer controlled_buffer_34
  assign the_11_th_line_of_the_picture_2 = out ? 32'h1f003e00 : 32'bz;  // Controlled_Buffer controlled_buffer_35
  Pull_Resistor pull_resistor_35 (.node(the_11_th_line_of_the_picture_2));
  Pull_Resistor pull_resistor_36 (.node(the_12_th_line_of_the_picture_2));
  assign the_12_th_line_of_the_picture_2 = out ? 32'h1e003e00 : 32'bz;  // Controlled_Buffer controlled_buffer_36
  assign the_13_th_line_of_the_picture_2 = out ? 32'h1c007c00 : 32'bz;  // Controlled_Buffer controlled_buffer_37
  Pull_Resistor pull_resistor_37 (.node(the_13_th_line_of_the_picture_2));
  Pull_Resistor pull_resistor_38 (.node(the_14_th_line_of_the_picture_2));
  assign the_14_th_line_of_the_picture_2 = out ? 32'h1c007c00 : 32'bz;  // Controlled_Buffer controlled_buffer_38
  Pull_Resistor pull_resistor_39 (.node(the_15_th_line_of_the_picture_2));
  assign the_15_th_line_of_the_picture_2 = out ? 32'h1c007c00 : 32'bz;  // Controlled_Buffer controlled_buffer_39
  Pull_Resistor pull_resistor_40 (.node(the_16_th_line_of_the_picture_2));
  assign the_16_th_line_of_the_picture_2 = out ? 32'h3800f800 : 32'bz;  // Controlled_Buffer controlled_buffer_40
  Pull_Resistor pull_resistor_41 (.node(the_17_th_line_of_the_picture_4));
  assign the_17_th_line_of_the_picture_4 = out ? 32'h3800f800 : 32'bz;  // Controlled_Buffer controlled_buffer_41
  assign the_18_th_line_of_the_picture_4 = out ? 32'h7000f800 : 32'bz;  // Controlled_Buffer controlled_buffer_42
  Pull_Resistor pull_resistor_42 (.node(the_18_th_line_of_the_picture_4));
  Pull_Resistor pull_resistor_43 (.node(the_19_th_line_of_the_picture_4));
  assign the_19_th_line_of_the_picture_4 = out ? 32'he000f800 : 32'bz;  // Controlled_Buffer controlled_buffer_43
  Pull_Resistor pull_resistor_44 (.node(the_20_th_line_of_the_picture_4));
  assign the_20_th_line_of_the_picture_4 = out ? {32{1'b0}} : 32'bz;  // Controlled_Buffer controlled_buffer_44

  assign the_1_st_line_of_the_picture_3 = {32{1'b0}};
  assign the_1_st_line_of_the_picture_4 = {32{1'b0}};
  assign the_2_nd_line_of_the_picture_3 = {32{1'b0}};
  assign the_2_nd_line_of_the_picture_4 = {32{1'b0}};
  assign the_3_rd_line_of_the_picture_3 = 32'h7ffe7ffe;
  assign the_3_rd_line_of_the_picture_4 = 32'h7e07e7fe;
  assign the_4_th_line_of_the_picture_3 = 32'h7ffe7ffe;
  assign the_4_th_line_of_the_picture_4 = 32'h7e07e7fe;
  assign the_5_th_line_of_the_picture_3 = 32'h7ffe7ffe;
  assign the_5_th_line_of_the_picture_4 = 32'h7f0fe7fe;
  assign the_6_th_line_of_the_picture_3 = 32'h7ffe7ffe;
  assign the_6_th_line_of_the_picture_4 = 32'h7f0fe7fe;
  assign the_7_th_line_of_the_picture_3 = 32'h7ffe7ffe;
  assign the_7_th_line_of_the_picture_4 = 32'h7f0fe7fe;
  assign the_8_th_line_of_the_picture_3 = 32'h7ffe7ffe;
  assign the_8_th_line_of_the_picture_4 = 32'h7f9fe7e0;
  assign the_9_th_line_of_the_picture_3 = 32'h7e007e0;
  assign the_9_th_line_of_the_picture_4 = 32'h7f9fe7e0;
  assign the_10_th_line_of_the_picture_3 = 32'h7e007e0;
  assign the_10_th_line_of_the_picture_4 = 32'h7f9fe7e0;
  assign the_11_th_line_of_the_picture_3 = 32'h7e007e0;
  assign the_11_th_line_of_the_picture_4 = 32'h7ef7e7e0;
  assign the_12_th_line_of_the_picture_3 = 32'h7e007e0;
  assign the_12_th_line_of_the_picture_4 = 32'h7ef7e7e0;
  assign the_13_th_line_of_the_picture_3 = 32'h7e007e0;
  assign the_13_th_line_of_the_picture_4 = 32'h7ef7e7e0;
  assign the_14_th_line_of_the_picture_3 = 32'h7e007e0;
  assign the_14_th_line_of_the_picture_4 = 32'h7e67e7fe;
  assign the_15_th_line_of_the_picture_3 = 32'h7e007e0;
  assign the_15_th_line_of_the_picture_4 = 32'h7e67e7fe;
  assign the_16_th_line_of_the_picture_3 = 32'h7e007e0;
  assign the_16_th_line_of_the_picture_4 = 32'h7e67e7fe;
  assign the_17_th_line_of_the_picture = 32'h7e007e0;
  assign the_17_th_line_of_the_picture_2 = 32'h7e07e7fe;
  assign the_18_th_line_of_the_picture = 32'h7e007e0;
  assign the_18_th_line_of_the_picture_2 = 32'h7e07e7fe;
  assign the_19_th_line_of_the_picture = 32'h7e007e0;
  assign the_19_th_line_of_the_picture_2 = 32'h7e07e7fe;
  assign the_20_th_line_of_the_picture = 32'h7e007e0;
  assign the_20_th_line_of_the_picture_2 = 32'h7e07e7e0;
  assign the_21_st_line_of_the_picture = 32'h7e007e0;
  assign the_21_st_line_of_the_picture_2 = 32'h7e07e7e0;
  assign the_22_nd_line_of_the_picture = 32'h7e007e0;
  assign the_22_nd_line_of_the_picture_2 = 32'h7e07e7e0;
  assign the_23_rd_line_of_the_picture = 32'h7e007e0;
  assign the_23_rd_line_of_the_picture_2 = 32'h7e07e7e0;
  assign the_24_th_line_of_the_picture = 32'h7e007e0;
  assign the_24_th_line_of_the_picture_2 = 32'h7e07e7e0;
  assign the_25_th_line_of_the_picture = 32'h7e007e0;
  assign the_25_th_line_of_the_picture_2 = 32'h7e07e7e0;
  assign the_26_th_line_of_the_picture = 32'h7e07ffe;
  assign the_26_th_line_of_the_picture_2 = 32'h7e07e7fe;
  assign the_27_th_line_of_the_picture = 32'h7e07ffe;
  assign the_27_th_line_of_the_picture_2 = 32'h7e07e7fe;
  assign the_28_th_line_of_the_picture = 32'h7e07ffe;
  assign the_28_th_line_of_the_picture_2 = 32'h7e07e7fe;
  assign the_29_th_line_of_the_picture = 32'h7e07ffe;
  assign the_29_th_line_of_the_picture_2 = 32'h7e07e7fe;
  assign the_30_th_line_of_the_picture = 32'h7e07ffe;
  assign the_30_th_line_of_the_picture_2 = 32'h7e07e7fe;
  assign the_31_st_line_of_the_picture = 32'h7e07ffe;
  assign the_31_st_line_of_the_picture_2 = 32'h7e07e7fe;
  assign the_32_nd_line_of_the_picture = {32{1'b0}};
  assign the_32_nd_line_of_the_picture_2 = {32{1'b0}};

  // Other names for the same wires on the sheet: temp_clock = clock

  // Notes on the sheet:
  //   Timer's line
endmodule

module lives (
  input  in_out,
  input  [3:0] I_Oadr,
  input  I_Osel,
  input  [7:0] I_Odat,
  input  clock,
  input  clear,
  output [14:0] the_1_st_line_of_the_picture,
  output [14:0] the_1_st_line_of_the_picture_2,
  output [14:0] the_1_st_line_of_the_picture_3,
  output [14:0] the_2_nd_line_of_the_picture,
  output [14:0] the_2_nd_line_of_the_picture_2,
  output [14:0] the_2_nd_line_of_the_picture_3,
  output [14:0] the_3_rd_line_of_the_picture,
  output [14:0] the_3_rd_line_of_the_picture_2,
  output [14:0] the_3_rd_line_of_the_picture_3,
  output [31:0] the_1_st_line_of_the_picture_4,
  output [31:0] the_17_th_line_of_the_picture,
  output [14:0] the_4_th_line_of_the_picture,
  output [14:0] the_4_th_line_of_the_picture_2,
  output [14:0] the_4_th_line_of_the_picture_3,
  output [31:0] the_2_nd_line_of_the_picture_4,
  output [31:0] the_18_th_line_of_the_picture,
  output [14:0] the_5_th_line_of_the_picture,
  output [14:0] the_5_th_line_of_the_picture_2,
  output [14:0] the_5_th_line_of_the_picture_3,
  output [31:0] the_3_rd_line_of_the_picture_4,
  output [31:0] the_19_th_line_of_the_picture,
  output [14:0] the_6_th_line_of_the_picture,
  output [14:0] the_6_th_line_of_the_picture_2,
  output [14:0] the_6_th_line_of_the_picture_3,
  output [14:0] the_7_th_line_of_the_picture,
  output [14:0] the_7_th_line_of_the_picture_2,
  output [14:0] the_7_th_line_of_the_picture_3,
  output [31:0] the_4_th_line_of_the_picture_4,
  output [31:0] the_20_th_line_of_the_picture,
  output [14:0] the_8_th_line_of_the_picture,
  output [14:0] the_8_th_line_of_the_picture_2,
  output [14:0] the_8_th_line_of_the_picture_3,
  output [31:0] the_5_th_line_of_the_picture_4,
  output [31:0] the_21_st_line_of_the_picture,
  output [14:0] the_9_th_line_of_the_picture,
  output [14:0] the_9_th_line_of_the_picture_2,
  output [14:0] the_9_th_line_of_the_picture_3,
  output [31:0] the_6_th_line_of_the_picture_4,
  output [31:0] the_22_nd_line_of_the_picture,
  output [14:0] the_10_th_line_of_the_picture,
  output [14:0] the_10_th_line_of_the_picture_2,
  output [14:0] the_10_th_line_of_the_picture_3,
  output [14:0] the_11_th_line_of_the_picture,
  output [14:0] the_11_th_line_of_the_picture_2,
  output [14:0] the_11_th_line_of_the_picture_3,
  output [31:0] the_7_th_line_of_the_picture_4,
  output [31:0] the_23_rd_line_of_the_picture,
  output [14:0] the_12_th_line_of_the_picture,
  output [14:0] the_12_th_line_of_the_picture_2,
  output [14:0] the_12_th_line_of_the_picture_3,
  output [31:0] the_8_th_line_of_the_picture_4,
  output [31:0] the_24_th_line_of_the_picture,
  output [14:0] the_13_th_line_of_the_picture,
  output [14:0] the_13_th_line_of_the_picture_2,
  output [14:0] the_13_th_line_of_the_picture_3,
  output [31:0] the_9_th_line_of_the_picture_4,
  output [31:0] the_25_th_line_of_the_picture,
  output [14:0] the_14_th_line_of_the_picture,
  output [14:0] the_14_th_line_of_the_picture_2,
  output [14:0] the_14_th_line_of_the_picture_3,
  output [14:0] the_15_th_line_of_the_picture,
  output [14:0] the_15_th_line_of_the_picture_2,
  output [14:0] the_15_th_line_of_the_picture_3,
  output [31:0] the_10_th_line_of_the_picture_4,
  output [31:0] the_26_th_line_of_the_picture,
  output [31:0] the_11_th_line_of_the_picture_4,
  output [31:0] the_27_th_line_of_the_picture,
  output [31:0] the_12_th_line_of_the_picture_4,
  output [31:0] the_28_th_line_of_the_picture,
  output [31:0] the_13_th_line_of_the_picture_4,
  output [31:0] the_29_th_line_of_the_picture,
  output [3:0] number_of_lives,
  output [31:0] the_14_th_line_of_the_picture_4,
  output [31:0] the_30_th_line_of_the_picture,
  output [31:0] the_15_th_line_of_the_picture_4,
  output [31:0] the_31_st_line_of_the_picture,
  output [31:0] the_16_th_line_of_the_picture,
  output [31:0] the_32_nd_line_of_the_picture
);

  wire _1_break, _1_small_lose, _1_small_play, _2_break, _2_small_lose, _2_small_play, _3_break,
       _3_small_lose, _3_small_play, big_lose, big_play;
  wire [1:0] get_number_of_lives_1_number_of_lives;

  assign the_1_st_line_of_the_picture = _1_small_play ? {15{1'b0}} : 15'bz;  // Controlled_Buffer controlled_buffer_1
  assign the_1_st_line_of_the_picture = _1_small_lose ? 15'h8 : 15'bz;  // Controlled_Buffer controlled_buffer_2
  assign the_2_nd_line_of_the_picture = _1_small_play ? {15{1'b0}} : 15'bz;  // Controlled_Buffer controlled_buffer_3
  assign the_2_nd_line_of_the_picture = _1_small_lose ? 15'h202 : 15'bz;  // Controlled_Buffer controlled_buffer_4
  assign the_3_rd_line_of_the_picture = _1_small_lose ? 15'h40 : 15'bz;  // Controlled_Buffer controlled_buffer_5
  assign the_3_rd_line_of_the_picture = _1_small_play ? {15{1'b0}} : 15'bz;  // Controlled_Buffer controlled_buffer_6
  assign the_4_th_line_of_the_picture = _1_small_play ? 15'h1c1c : 15'bz;  // Controlled_Buffer controlled_buffer_7
  assign the_4_th_line_of_the_picture = _1_small_lose ? 15'h1c0c : 15'bz;  // Controlled_Buffer controlled_buffer_8
  assign the_5_th_line_of_the_picture = _1_small_lose ? 15'h3e1e : 15'bz;  // Controlled_Buffer controlled_buffer_9
  assign the_5_th_line_of_the_picture = _1_small_play ? 15'h3e3e : 15'bz;  // Controlled_Buffer controlled_buffer_10
  assign the_6_th_line_of_the_picture = _1_small_lose ? 15'h3ebe : 15'bz;  // Controlled_Buffer controlled_buffer_11
  assign the_6_th_line_of_the_picture = _1_small_play ? 15'h3f7e : 15'bz;  // Controlled_Buffer controlled_buffer_12
  assign the_7_th_line_of_the_picture = _1_small_lose ? 15'h3c3e : 15'bz;  // Controlled_Buffer controlled_buffer_13
  assign the_7_th_line_of_the_picture = _1_small_play ? 15'h3ffe : 15'bz;  // Controlled_Buffer controlled_buffer_14
  assign the_8_th_line_of_the_picture = _1_small_lose ? 15'h397e : 15'bz;  // Controlled_Buffer controlled_buffer_15
  assign the_8_th_line_of_the_picture = _1_small_play ? 15'h3ffe : 15'bz;  // Controlled_Buffer controlled_buffer_16
  assign the_9_th_line_of_the_picture = _1_small_play ? 15'h1ffc : 15'bz;  // Controlled_Buffer controlled_buffer_17
  assign the_9_th_line_of_the_picture = _1_small_lose ? 15'h1c3c : 15'bz;  // Controlled_Buffer controlled_buffer_18
  assign the_10_th_line_of_the_picture = _1_small_lose ? 15'he18 : 15'bz;  // Controlled_Buffer controlled_buffer_19
  assign the_10_th_line_of_the_picture = _1_small_play ? 15'hff8 : 15'bz;  // Controlled_Buffer controlled_buffer_20
  assign the_11_th_line_of_the_picture = _1_small_play ? 15'h7f0 : 15'bz;  // Controlled_Buffer controlled_buffer_21
  assign the_11_th_line_of_the_picture = _1_small_lose ? 15'h701 : 15'bz;  // Controlled_Buffer controlled_buffer_22
  assign the_12_th_line_of_the_picture = _1_small_play ? 15'h3e0 : 15'bz;  // Controlled_Buffer controlled_buffer_23
  assign the_12_th_line_of_the_picture = _1_small_lose ? 15'h390 : 15'bz;  // Controlled_Buffer controlled_buffer_24
  assign the_13_th_line_of_the_picture = _1_small_lose ? 15'h1c4 : 15'bz;  // Controlled_Buffer controlled_buffer_25
  assign the_13_th_line_of_the_picture = _1_small_play ? 15'h1c0 : 15'bz;  // Controlled_Buffer controlled_buffer_26
  assign the_14_th_line_of_the_picture = _1_small_play ? 15'h80 : 15'bz;  // Controlled_Buffer controlled_buffer_27
  assign the_14_th_line_of_the_picture = _1_small_lose ? 15'h90 : 15'bz;  // Controlled_Buffer controlled_buffer_28
  assign the_15_th_line_of_the_picture = _1_small_lose ? 15'h2 : 15'bz;  // Controlled_Buffer controlled_buffer_29
  assign the_15_th_line_of_the_picture = _1_small_play ? {15{1'b0}} : 15'bz;  // Controlled_Buffer controlled_buffer_30
  S_R_Flip_Flop s_r_ff_1 (
    .clk(clock), .Q(_1_small_lose), .Qn(_1_small_play), .preset(_1_break), .reset(clear));  // open: S, R, en
  get_number_of_lives get_number_of_lives_1 (
    .in_out(in_out), .I_Oadr(I_Oadr), .I_Osel(I_Osel), .I_Odat(I_Odat), .clock(clock), .clear(clear),
    .number_of_lives(get_number_of_lives_1_number_of_lives));
  assign number_of_lives = {{2{1'b0}}, get_number_of_lives_1_number_of_lives};  // Bit_Extender bit_extender_1
  DotMatrix #(.inputtype("row"), .matrixcols(15), .matrixrows(15)) dotmatrix_1 (
    .row0({15{1'b0}}), .row1({15{1'b0}}), .row2({15{1'b0}}), .row3(15'h1c1c), .row4(15'h3e3e),
    .row5(15'h3f7e), .row6(15'h3ffe), .row7(15'h3ffe), .row8(15'h1ffc), .row9(15'hff8), .row10(15'h7f0),
    .row11(15'h3e0), .row12(15'h1c0), .row13(15'h80), .row14({15{1'b0}}));
  assign the_1_st_line_of_the_picture_2 = _2_small_play ? {15{1'b0}} : 15'bz;  // Controlled_Buffer controlled_buffer_31
  assign the_2_nd_line_of_the_picture_2 = _2_small_play ? {15{1'b0}} : 15'bz;  // Controlled_Buffer controlled_buffer_32
  assign the_3_rd_line_of_the_picture_2 = _2_small_play ? {15{1'b0}} : 15'bz;  // Controlled_Buffer controlled_buffer_33
  assign the_4_th_line_of_the_picture_2 = _2_small_play ? 15'h1c1c : 15'bz;  // Controlled_Buffer controlled_buffer_34
  assign the_5_th_line_of_the_picture_2 = _2_small_play ? 15'h3e3e : 15'bz;  // Controlled_Buffer controlled_buffer_35
  assign the_6_th_line_of_the_picture_2 = _2_small_play ? 15'h3f7e : 15'bz;  // Controlled_Buffer controlled_buffer_36
  assign the_7_th_line_of_the_picture_2 = _2_small_play ? 15'h3ffe : 15'bz;  // Controlled_Buffer controlled_buffer_37
  assign the_8_th_line_of_the_picture_2 = _2_small_play ? 15'h3ffe : 15'bz;  // Controlled_Buffer controlled_buffer_38
  assign the_9_th_line_of_the_picture_2 = _2_small_play ? 15'h1ffc : 15'bz;  // Controlled_Buffer controlled_buffer_39
  assign the_10_th_line_of_the_picture_2 = _2_small_play ? 15'hff8 : 15'bz;  // Controlled_Buffer controlled_buffer_40
  assign the_11_th_line_of_the_picture_2 = _2_small_play ? 15'h7f0 : 15'bz;  // Controlled_Buffer controlled_buffer_41
  assign the_12_th_line_of_the_picture_2 = _2_small_play ? 15'h3e0 : 15'bz;  // Controlled_Buffer controlled_buffer_42
  assign the_13_th_line_of_the_picture_2 = _2_small_play ? 15'h1c0 : 15'bz;  // Controlled_Buffer controlled_buffer_43
  assign the_14_th_line_of_the_picture_2 = _2_small_play ? 15'h80 : 15'bz;  // Controlled_Buffer controlled_buffer_44
  assign the_15_th_line_of_the_picture_2 = _2_small_play ? {15{1'b0}} : 15'bz;  // Controlled_Buffer controlled_buffer_45
  set_break_flags set_break_flags_1 (
    .in_out(in_out), .I_Oadr(I_Oadr), .I_Osel(I_Osel), .I_Odat(I_Odat), .clock(clock), .clear(clear),
    ._3_break(_3_break), ._2_break(_2_break), ._1_break(_1_break));
  assign the_1_st_line_of_the_picture_2 = _2_small_lose ? 15'h8 : 15'bz;  // Controlled_Buffer controlled_buffer_46
  assign the_2_nd_line_of_the_picture_2 = _2_small_lose ? 15'h202 : 15'bz;  // Controlled_Buffer controlled_buffer_47
  assign the_3_rd_line_of_the_picture_2 = _2_small_lose ? 15'h40 : 15'bz;  // Controlled_Buffer controlled_buffer_48
  assign the_4_th_line_of_the_picture_2 = _2_small_lose ? 15'h1c0c : 15'bz;  // Controlled_Buffer controlled_buffer_49
  assign the_5_th_line_of_the_picture_2 = _2_small_lose ? 15'h3e1e : 15'bz;  // Controlled_Buffer controlled_buffer_50
  assign the_6_th_line_of_the_picture_2 = _2_small_lose ? 15'h3ebe : 15'bz;  // Controlled_Buffer controlled_buffer_51
  assign the_7_th_line_of_the_picture_2 = _2_small_lose ? 15'h3c3e : 15'bz;  // Controlled_Buffer controlled_buffer_52
  assign the_8_th_line_of_the_picture_2 = _2_small_lose ? 15'h397e : 15'bz;  // Controlled_Buffer controlled_buffer_53
  assign the_9_th_line_of_the_picture_2 = _2_small_lose ? 15'h1c3c : 15'bz;  // Controlled_Buffer controlled_buffer_54
  assign the_10_th_line_of_the_picture_2 = _2_small_lose ? 15'he18 : 15'bz;  // Controlled_Buffer controlled_buffer_55
  assign the_11_th_line_of_the_picture_2 = _2_small_lose ? 15'h701 : 15'bz;  // Controlled_Buffer controlled_buffer_56
  assign the_12_th_line_of_the_picture_2 = _2_small_lose ? 15'h390 : 15'bz;  // Controlled_Buffer controlled_buffer_57
  assign the_13_th_line_of_the_picture_2 = _2_small_lose ? 15'h1c4 : 15'bz;  // Controlled_Buffer controlled_buffer_58
  assign the_14_th_line_of_the_picture_2 = _2_small_lose ? 15'h90 : 15'bz;  // Controlled_Buffer controlled_buffer_59
  assign the_15_th_line_of_the_picture_2 = _2_small_lose ? 15'h2 : 15'bz;  // Controlled_Buffer controlled_buffer_60
  S_R_Flip_Flop s_r_ff_2 (
    .clk(clock), .Q(_2_small_lose), .Qn(_2_small_play), .preset(_2_break), .reset(clear));  // open: S, R, en
  DotMatrix #(.inputtype("row"), .matrixcols(15), .matrixrows(15)) dotmatrix_2 (
    .row0(15'h8), .row1(15'h202), .row2(15'h40), .row3(15'h1c0c), .row4(15'h3e1e), .row5(15'h3ebe),
    .row6(15'h3c3e), .row7(15'h397e), .row8(15'h1c3c), .row9(15'he18), .row10(15'h701), .row11(15'h390),
    .row12(15'h1c4), .row13(15'h90), .row14(15'h2));
  assign the_1_st_line_of_the_picture_3 = _3_small_play ? {15{1'b0}} : 15'bz;  // Controlled_Buffer controlled_buffer_61
  assign the_2_nd_line_of_the_picture_3 = _3_small_play ? {15{1'b0}} : 15'bz;  // Controlled_Buffer controlled_buffer_62
  assign the_3_rd_line_of_the_picture_3 = _3_small_play ? {15{1'b0}} : 15'bz;  // Controlled_Buffer controlled_buffer_63
  assign the_4_th_line_of_the_picture_3 = _3_small_play ? 15'h1c1c : 15'bz;  // Controlled_Buffer controlled_buffer_64
  assign the_5_th_line_of_the_picture_3 = _3_small_play ? 15'h3e3e : 15'bz;  // Controlled_Buffer controlled_buffer_65
  assign the_6_th_line_of_the_picture_3 = _3_small_play ? 15'h3f7e : 15'bz;  // Controlled_Buffer controlled_buffer_66
  assign the_7_th_line_of_the_picture_3 = _3_small_play ? 15'h3ffe : 15'bz;  // Controlled_Buffer controlled_buffer_67
  assign the_8_th_line_of_the_picture_3 = _3_small_play ? 15'h3ffe : 15'bz;  // Controlled_Buffer controlled_buffer_68
  assign the_9_th_line_of_the_picture_3 = _3_small_play ? 15'h1ffc : 15'bz;  // Controlled_Buffer controlled_buffer_69
  assign the_10_th_line_of_the_picture_3 = _3_small_play ? 15'hff8 : 15'bz;  // Controlled_Buffer controlled_buffer_70
  assign the_11_th_line_of_the_picture_3 = _3_small_play ? 15'h7f0 : 15'bz;  // Controlled_Buffer controlled_buffer_71
  assign the_12_th_line_of_the_picture_3 = _3_small_play ? 15'h3e0 : 15'bz;  // Controlled_Buffer controlled_buffer_72
  assign the_13_th_line_of_the_picture_3 = _3_small_play ? 15'h1c0 : 15'bz;  // Controlled_Buffer controlled_buffer_73
  assign the_14_th_line_of_the_picture_3 = _3_small_play ? 15'h80 : 15'bz;  // Controlled_Buffer controlled_buffer_74
  assign the_15_th_line_of_the_picture_3 = _3_small_play ? {15{1'b0}} : 15'bz;  // Controlled_Buffer controlled_buffer_75
  assign the_1_st_line_of_the_picture_3 = _3_small_lose ? 15'h8 : 15'bz;  // Controlled_Buffer controlled_buffer_76
  assign the_2_nd_line_of_the_picture_3 = _3_small_lose ? 15'h202 : 15'bz;  // Controlled_Buffer controlled_buffer_77
  assign the_3_rd_line_of_the_picture_3 = _3_small_lose ? 15'h40 : 15'bz;  // Controlled_Buffer controlled_buffer_78
  assign the_4_th_line_of_the_picture_3 = _3_small_lose ? 15'h1c0c : 15'bz;  // Controlled_Buffer controlled_buffer_79
  assign the_5_th_line_of_the_picture_3 = _3_small_lose ? 15'h3e1e : 15'bz;  // Controlled_Buffer controlled_buffer_80
  assign the_6_th_line_of_the_picture_3 = _3_small_lose ? 15'h3ebe : 15'bz;  // Controlled_Buffer controlled_buffer_81
  assign the_7_th_line_of_the_picture_3 = _3_small_lose ? 15'h3c3e : 15'bz;  // Controlled_Buffer controlled_buffer_82
  assign the_8_th_line_of_the_picture_3 = _3_small_lose ? 15'h397e : 15'bz;  // Controlled_Buffer controlled_buffer_83
  assign the_9_th_line_of_the_picture_3 = _3_small_lose ? 15'h1c3c : 15'bz;  // Controlled_Buffer controlled_buffer_84
  assign the_10_th_line_of_the_picture_3 = _3_small_lose ? 15'he18 : 15'bz;  // Controlled_Buffer controlled_buffer_85
  assign the_11_th_line_of_the_picture_3 = _3_small_lose ? 15'h701 : 15'bz;  // Controlled_Buffer controlled_buffer_86
  assign the_12_th_line_of_the_picture_3 = _3_small_lose ? 15'h390 : 15'bz;  // Controlled_Buffer controlled_buffer_87
  assign the_13_th_line_of_the_picture_3 = _3_small_lose ? 15'h1c4 : 15'bz;  // Controlled_Buffer controlled_buffer_88
  assign the_14_th_line_of_the_picture_3 = _3_small_lose ? 15'h90 : 15'bz;  // Controlled_Buffer controlled_buffer_89
  assign the_15_th_line_of_the_picture_3 = _3_small_lose ? 15'h2 : 15'bz;  // Controlled_Buffer controlled_buffer_90
  S_R_Flip_Flop s_r_ff_3 (
    .clk(clock), .Q(_3_small_lose), .Qn(_3_small_play), .preset(_3_break), .reset(clear));  // open: S, R, en
  DotMatrix #(.inputtype("row"), .matrixcols(32), .matrixrows(32)) dotmatrix_3 (
    .row0({32{1'b0}}), .row1({32{1'b0}}), .row2({32{1'b0}}), .row3({32{1'b0}}), .row4({32{1'b0}}),
    .row5(32'h3f00fc0), .row6(32'h7f81fe0), .row7(32'hffc3ff0), .row8(32'h1ffe7ff8), .row9(32'h3ffffffc),
    .row10(32'h3ffffffc), .row11(32'h3ffffffc), .row12(32'h3ffffffc), .row13(32'h3ffffffc),
    .row14(32'h3ffffffc), .row15(32'h3ffffffc), .row16(32'h3ffffffc), .row17(32'h1ffffff8),
    .row18(32'hffffff0), .row19(32'h7ffffe0), .row20(32'h3ffffc0), .row21(32'h1ffff80), .row22(32'hffff00),
    .row23(32'h7ffe00), .row24(32'h3ffc00), .row25(32'h1ff800), .row26(32'hff000), .row27(32'h7e000),
    .row28(32'h3c000), .row29(32'h18000), .row30({32{1'b0}}), .row31({32{1'b0}}));
  S_R_Flip_Flop s_r_ff_4 (
    .clk(clock), .Q(big_lose), .Qn(big_play), .preset(_3_break), .reset(clear));  // open: S, R, en
  assign the_1_st_line_of_the_picture_4 = big_play ? {32{1'b0}} : 32'bz;  // Controlled_Buffer controlled_buffer_91
  assign the_2_nd_line_of_the_picture_4 = big_play ? {32{1'b0}} : 32'bz;  // Controlled_Buffer controlled_buffer_92
  assign the_3_rd_line_of_the_picture_4 = big_play ? {32{1'b0}} : 32'bz;  // Controlled_Buffer controlled_buffer_93
  assign the_4_th_line_of_the_picture_4 = big_play ? {32{1'b0}} : 32'bz;  // Controlled_Buffer controlled_buffer_94
  assign the_5_th_line_of_the_picture_4 = big_play ? {32{1'b0}} : 32'bz;  // Controlled_Buffer controlled_buffer_95
  assign the_9_th_line_of_the_picture_4 = big_play ? 32'h1ffe7ff8 : 32'bz;  // Controlled_Buffer controlled_buffer_96
  assign the_10_th_line_of_the_picture_4 = big_play ? 32'h3ffffffc : 32'bz;  // Controlled_Buffer controlled_buffer_97
  assign the_11_th_line_of_the_picture_4 = big_play ? 32'h3ffffffc : 32'bz;  // Controlled_Buffer controlled_buffer_98
  assign the_12_th_line_of_the_picture_4 = big_play ? 32'h3ffffffc : 32'bz;  // Controlled_Buffer controlled_buffer_99
  assign the_13_th_line_of_the_picture_4 = big_play ? 32'h3ffffffc : 32'bz;  // Controlled_Buffer controlled_buffer_100
  assign the_14_th_line_of_the_picture_4 = big_play ? 32'h3ffffffc : 32'bz;  // Controlled_Buffer controlled_buffer_101
  assign the_15_th_line_of_the_picture_4 = big_play ? 32'h3ffffffc : 32'bz;  // Controlled_Buffer controlled_buffer_102
  assign the_16_th_line_of_the_picture = big_play ? 32'h3ffffffc : 32'bz;  // Controlled_Buffer controlled_buffer_103
  assign the_1_st_line_of_the_picture_4 = big_lose ? 32'h240000 : 32'bz;  // Controlled_Buffer controlled_buffer_104
  assign the_2_nd_line_of_the_picture_4 = big_lose ? 32'h200 : 32'bz;  // Controlled_Buffer controlled_buffer_105
  assign the_3_rd_line_of_the_picture_4 = big_lose ? 32'h810 : 32'bz;  // Controlled_Buffer controlled_buffer_106
  assign the_4_th_line_of_the_picture_4 = big_lose ? 32'h48000 : 32'bz;  // Controlled_Buffer controlled_buffer_107
  assign the_5_th_line_of_the_picture_4 = big_lose ? 32'h2000 : 32'bz;  // Controlled_Buffer controlled_buffer_108
  assign the_9_th_line_of_the_picture_4 = big_lose ? 32'h1ffe1ff8 : 32'bz;  // Controlled_Buffer controlled_buffer_109
  assign the_10_th_line_of_the_picture_4 = big_lose ? 32'h3fff0ffc : 32'bz;  // Controlled_Buffer controlled_buffer_110
  assign the_11_th_line_of_the_picture_4 = big_lose ? 32'h3fff87fc : 32'bz;  // Controlled_Buffer controlled_buffer_111
  assign the_12_th_line_of_the_picture_4 = big_lose ? 32'h3fff83fc : 32'bz;  // Controlled_Buffer controlled_buffer_112
  assign the_13_th_line_of_the_picture_4 = big_lose ? 32'h3fff03fc : 32'bz;  // Controlled_Buffer controlled_buffer_113
  assign the_14_th_line_of_the_picture_4 = big_lose ? 32'h3ffe07fc : 32'bz;  // Controlled_Buffer controlled_buffer_114
  assign the_15_th_line_of_the_picture_4 = big_lose ? 32'h3fff0ffc : 32'bz;  // Controlled_Buffer controlled_buffer_115
  assign the_16_th_line_of_the_picture = big_lose ? 32'h3fff87fc : 32'bz;  // Controlled_Buffer controlled_buffer_116
  DotMatrix #(.inputtype("row"), .matrixcols(32), .matrixrows(32)) dotmatrix_4 (
    .row0(32'h240000), .row1(32'h200), .row2(32'h810), .row3(32'h48000), .row4(32'h2000), .row5(32'h3f00fc0),
    .row6(32'h7f81fe0), .row7(32'hffc3ff0), .row8(32'h1ffe1ff8), .row9(32'h3fff0ffc), .row10(32'h3fff87fc),
    .row11(32'h3fff83fc), .row12(32'h3fff03fc), .row13(32'h3ffe07fc), .row14(32'h3fff0ffc),
    .row15(32'h3fff87fc), .row16(32'h3fffc3fc), .row17(32'h1fff87f8), .row18(32'hffe1ff0),
    .row19(32'h7fc3fe0), .row20(32'h3f87fc0), .row21(32'h1fc3f80), .row22(32'hfe1f00), .row23(32'h7f0e00),
    .row24(32'h3f8400), .row25(32'h1fc010), .row26(32'hfe200), .row27(32'h7e024), .row28(32'h3c080),
    .row29(32'h18800), .row30(32'h4), .row31({32{1'b0}}));
  assign the_17_th_line_of_the_picture = big_play ? 32'h3ffffffc : 32'bz;  // Controlled_Buffer controlled_buffer_117
  assign the_18_th_line_of_the_picture = big_play ? 32'h1ffffff8 : 32'bz;  // Controlled_Buffer controlled_buffer_118
  assign the_19_th_line_of_the_picture = big_play ? 32'hffffff0 : 32'bz;  // Controlled_Buffer controlled_buffer_119
  assign the_20_th_line_of_the_picture = big_play ? 32'h7ffffe0 : 32'bz;  // Controlled_Buffer controlled_buffer_120
  assign the_21_st_line_of_the_picture = big_play ? 32'h3ffffc0 : 32'bz;  // Controlled_Buffer controlled_buffer_121
  assign the_22_nd_line_of_the_picture = big_play ? 32'h1ffff80 : 32'bz;  // Controlled_Buffer controlled_buffer_122
  assign the_23_rd_line_of_the_picture = big_play ? 32'hffff00 : 32'bz;  // Controlled_Buffer controlled_buffer_123
  assign the_24_th_line_of_the_picture = big_play ? 32'h7ffe00 : 32'bz;  // Controlled_Buffer controlled_buffer_124
  assign the_25_th_line_of_the_picture = big_play ? 32'h3ffc00 : 32'bz;  // Controlled_Buffer controlled_buffer_125
  assign the_26_th_line_of_the_picture = big_play ? 32'h1ff800 : 32'bz;  // Controlled_Buffer controlled_buffer_126
  assign the_27_th_line_of_the_picture = big_play ? 32'hff000 : 32'bz;  // Controlled_Buffer controlled_buffer_127
  assign the_28_th_line_of_the_picture = big_play ? 32'h7e000 : 32'bz;  // Controlled_Buffer controlled_buffer_128
  assign the_29_th_line_of_the_picture = big_play ? 32'h3c000 : 32'bz;  // Controlled_Buffer controlled_buffer_129
  assign the_30_th_line_of_the_picture = big_play ? 32'h18000 : 32'bz;  // Controlled_Buffer controlled_buffer_130
  assign the_31_st_line_of_the_picture = big_play ? {32{1'b0}} : 32'bz;  // Controlled_Buffer controlled_buffer_131
  assign the_17_th_line_of_the_picture = big_lose ? 32'h3fffc3fc : 32'bz;  // Controlled_Buffer controlled_buffer_132
  assign the_18_th_line_of_the_picture = big_lose ? 32'h1fff87f8 : 32'bz;  // Controlled_Buffer controlled_buffer_133
  assign the_19_th_line_of_the_picture = big_lose ? 32'hffe1ff0 : 32'bz;  // Controlled_Buffer controlled_buffer_134
  assign the_20_th_line_of_the_picture = big_lose ? 32'h7fc3fe0 : 32'bz;  // Controlled_Buffer controlled_buffer_135
  assign the_21_st_line_of_the_picture = big_lose ? 32'h3f87fc0 : 32'bz;  // Controlled_Buffer controlled_buffer_136
  assign the_22_nd_line_of_the_picture = big_lose ? 32'h1fc3f80 : 32'bz;  // Controlled_Buffer controlled_buffer_137
  assign the_23_rd_line_of_the_picture = big_lose ? 32'hfe1f00 : 32'bz;  // Controlled_Buffer controlled_buffer_138
  assign the_24_th_line_of_the_picture = big_lose ? 32'h7f0e00 : 32'bz;  // Controlled_Buffer controlled_buffer_139
  assign the_25_th_line_of_the_picture = big_lose ? 32'h3f8400 : 32'bz;  // Controlled_Buffer controlled_buffer_140
  assign the_26_th_line_of_the_picture = big_lose ? 32'h1fc010 : 32'bz;  // Controlled_Buffer controlled_buffer_141
  assign the_27_th_line_of_the_picture = big_lose ? 32'hfe200 : 32'bz;  // Controlled_Buffer controlled_buffer_142
  assign the_28_th_line_of_the_picture = big_lose ? 32'h7e024 : 32'bz;  // Controlled_Buffer controlled_buffer_143
  assign the_29_th_line_of_the_picture = big_lose ? 32'h3c080 : 32'bz;  // Controlled_Buffer controlled_buffer_144
  assign the_30_th_line_of_the_picture = big_lose ? 32'h18800 : 32'bz;  // Controlled_Buffer controlled_buffer_145
  assign the_31_st_line_of_the_picture = big_lose ? 32'h4 : 32'bz;  // Controlled_Buffer controlled_buffer_146

  assign the_6_th_line_of_the_picture_4 = 32'h3f00fc0;
  assign the_7_th_line_of_the_picture_4 = 32'h7f81fe0;
  assign the_8_th_line_of_the_picture_4 = 32'hffc3ff0;
  assign the_32_nd_line_of_the_picture = {32{1'b0}};

  // Other names for the same wires on the sheet: break = _3_break

  // Notes on the sheet:
  //   The first small heart
  //   Reading number of lives
  //   The second small heart
  //   Set break flags
  //   The third small heart
endmodule

module number_of_saved_frogs___victory___lose (
  input  in_out,
  input  [3:0] I_Oadr,
  input  I_Osel,
  input  [7:0] I_Odat,
  input  clock,
  input  clear,
  output [26:0] the_17_th_line_of_the_picture,
  output \event ,
  output [26:0] the_1_st_line_of_the_picture,
  output [26:0] the_9_th_line_of_the_picture,
  output [26:0] the_18_th_line_of_the_picture,
  output [26:0] the_2_nd_line_of_the_picture,
  output [26:0] the_10_th_line_of_the_picture,
  output [26:0] the_19_th_line_of_the_picture,
  output [26:0] the_3_rd_line_of_the_picture,
  output [26:0] the_11_th_line_of_the_picture,
  output [26:0] the_20_th_line_of_the_picture,
  output [26:0] the_4_th_line_of_the_picture,
  output [26:0] the_12_th_line_of_the_picture,
  output [26:0] the_21_st_line_of_the_picture,
  output [26:0] the_5_th_line_of_the_picture,
  output [26:0] the_13_th_line_of_the_picture,
  output [26:0] the_22_nd_line_of_the_picture,
  output [26:0] the_6_th_line_of_the_picture,
  output [26:0] the_14_th_line_of_the_picture,
  output [26:0] the_23_rd_line_of_the_picture,
  output [26:0] the_7_th_line_of_the_picture,
  output [26:0] the_15_th_line_of_the_picture,
  output [26:0] the_8_th_line_of_the_picture,
  output [26:0] the_16_th_line_of_the_picture,
  output [3:0] number_of_survivors
);

  wire lose, play, victory;
  wire [2:0] get_number_of_survivors_1_number_of_survivors;

  game_state game_state_1 (
    .in_out(in_out), .I_Oadr(I_Oadr), .I_Osel(I_Osel), .I_Odat(I_Odat), .clock(clock), .clear(clear),
    .lose(lose), .play(play), .victory(victory));
  or or_1 (\event , lose, victory);
  assign the_2_nd_line_of_the_picture = play ? 27'h6140 : 27'bz;  // Controlled_Buffer controlled_buffer_1
  assign the_3_rd_line_of_the_picture = play ? 27'hf0c0 : 27'bz;  // Controlled_Buffer controlled_buffer_2
  assign the_4_th_line_of_the_picture = play ? 27'h1f9e0 : 27'bz;  // Controlled_Buffer controlled_buffer_3
  assign the_5_th_line_of_the_picture = play ? 27'h2b6c60 : 27'bz;  // Controlled_Buffer controlled_buffer_4
  assign the_6_th_line_of_the_picture = play ? 27'h33fc60 : 27'bz;  // Controlled_Buffer controlled_buffer_5
  assign the_7_th_line_of_the_picture = play ? 27'h79f8e0 : 27'bz;  // Controlled_Buffer controlled_buffer_6
  assign the_8_th_line_of_the_picture = play ? 27'h60f3c0 : 27'bz;  // Controlled_Buffer controlled_buffer_7
  assign the_2_nd_line_of_the_picture = victory ? 27'h202fb1a : 27'bz;  // Controlled_Buffer controlled_buffer_8
  assign the_3_rd_line_of_the_picture = victory ? 27'h222239a : 27'bz;  // Controlled_Buffer controlled_buffer_9
  assign the_4_th_line_of_the_picture = victory ? 27'h37623da : 27'bz;  // Controlled_Buffer controlled_buffer_10
  assign the_5_th_line_of_the_picture = victory ? 27'h154237a : 27'bz;  // Controlled_Buffer controlled_buffer_11
  assign the_6_th_line_of_the_picture = victory ? 27'h1dc2338 : 27'bz;  // Controlled_Buffer controlled_buffer_12
  assign the_7_th_line_of_the_picture = victory ? 27'h88fb1a : 27'bz;  // Controlled_Buffer controlled_buffer_13
  assign the_8_th_line_of_the_picture = victory ? {27{1'b0}} : 27'bz;  // Controlled_Buffer controlled_buffer_14
  DotMatrix #(.inputtype("row"), .matrixcols(27), .matrixrows(23)) dotmatrix_1 (
    .row0({27{1'b0}}), .row1(27'h6140), .row2(27'hf0c0), .row3(27'h1f9e0), .row4(27'h2b6c60),
    .row5(27'h33fc60), .row6(27'h79f8e0), .row7(27'h60f3c0), .row8(27'h7dff80), .row9(27'h3ffe00),
    .row10(27'h7fc00), .row11(27'hf3fc00), .row12(27'h1bbfcf0), .row13(27'h1dfffd8), .row14(27'hefffb8),
    .row15(27'h73fe70), .row16(27'h79f8e0), .row17(27'hf0f1e0), .row18(27'h1e000f0), .row19(27'h2a00078),
    .row20(27'h3c), .row21(27'h2a), .row22({27{1'b0}}));
  assign the_2_nd_line_of_the_picture = lose ? 27'h3070f7c : 27'bz;  // Controlled_Buffer controlled_buffer_15
  assign the_3_rd_line_of_the_picture = lose ? 27'h30f9940 : 27'bz;  // Controlled_Buffer controlled_buffer_16
  assign the_4_th_line_of_the_picture = lose ? 27'h30d8c78 : 27'bz;  // Controlled_Buffer controlled_buffer_17
  assign the_5_th_line_of_the_picture = lose ? 27'h30d8640 : 27'bz;  // Controlled_Buffer controlled_buffer_18
  assign the_6_th_line_of_the_picture = lose ? 27'h3efb67c : 27'bz;  // Controlled_Buffer controlled_buffer_19
  assign the_7_th_line_of_the_picture = lose ? 27'h3e71c7c : 27'bz;  // Controlled_Buffer controlled_buffer_20
  assign the_8_th_line_of_the_picture = lose ? {27{1'b0}} : 27'bz;  // Controlled_Buffer controlled_buffer_21
  assign the_9_th_line_of_the_picture = play ? 27'h7dff80 : 27'bz;  // Controlled_Buffer controlled_buffer_22
  assign the_10_th_line_of_the_picture = play ? 27'h3ffe00 : 27'bz;  // Controlled_Buffer controlled_buffer_23
  assign the_11_th_line_of_the_picture = play ? 27'h7fc00 : 27'bz;  // Controlled_Buffer controlled_buffer_24
  assign the_12_th_line_of_the_picture = play ? 27'hf3fc00 : 27'bz;  // Controlled_Buffer controlled_buffer_25
  assign the_13_th_line_of_the_picture = play ? 27'h1bbfcf0 : 27'bz;  // Controlled_Buffer controlled_buffer_26
  assign the_14_th_line_of_the_picture = play ? 27'h1dfffd8 : 27'bz;  // Controlled_Buffer controlled_buffer_27
  assign the_15_th_line_of_the_picture = play ? 27'hefffb8 : 27'bz;  // Controlled_Buffer controlled_buffer_28
  assign the_16_th_line_of_the_picture = play ? 27'h73fe70 : 27'bz;  // Controlled_Buffer controlled_buffer_29
  DotMatrix #(.inputtype("row"), .matrixcols(27), .matrixrows(23)) dotmatrix_2 (
    .row0({27{1'b0}}), .row1(27'h202fb1a), .row2(27'h222239a), .row3(27'h37623da), .row4(27'h154237a),
    .row5(27'h1dc2338), .row6(27'h88fb1a), .row7({27{1'b0}}), .row8({27{1'b0}}), .row9(27'ha00),
    .row10(27'h400), .row11(27'ha0a00), .row12(27'h40000), .row13(27'ha0000), .row14({27{1'b0}}),
    .row15({27{1'b0}}), .row16(27'h28), .row17(27'h280010), .row18(27'h105028), .row19(27'h282000),
    .row20(27'h5000), .row21({27{1'b0}}), .row22({27{1'b0}}));
  assign the_9_th_line_of_the_picture = victory ? {27{1'b0}} : 27'bz;  // Controlled_Buffer controlled_buffer_30
  assign the_10_th_line_of_the_picture = victory ? 27'ha00 : 27'bz;  // Controlled_Buffer controlled_buffer_31
  assign the_11_th_line_of_the_picture = victory ? 27'h400 : 27'bz;  // Controlled_Buffer controlled_buffer_32
  assign the_12_th_line_of_the_picture = victory ? 27'ha0a00 : 27'bz;  // Controlled_Buffer controlled_buffer_33
  assign the_13_th_line_of_the_picture = victory ? 27'h40000 : 27'bz;  // Controlled_Buffer controlled_buffer_34
  assign the_14_th_line_of_the_picture = victory ? 27'ha0000 : 27'bz;  // Controlled_Buffer controlled_buffer_35
  assign the_15_th_line_of_the_picture = victory ? {27{1'b0}} : 27'bz;  // Controlled_Buffer controlled_buffer_36
  assign the_16_th_line_of_the_picture = victory ? {27{1'b0}} : 27'bz;  // Controlled_Buffer controlled_buffer_37
  assign the_9_th_line_of_the_picture = lose ? {27{1'b0}} : 27'bz;  // Controlled_Buffer controlled_buffer_38
  assign the_10_th_line_of_the_picture = lose ? {27{1'b0}} : 27'bz;  // Controlled_Buffer controlled_buffer_39
  assign the_11_th_line_of_the_picture = lose ? {27{1'b0}} : 27'bz;  // Controlled_Buffer controlled_buffer_40
  assign the_12_th_line_of_the_picture = lose ? 27'h20800 : 27'bz;  // Controlled_Buffer controlled_buffer_41
  assign the_13_th_line_of_the_picture = lose ? 27'h40400 : 27'bz;  // Controlled_Buffer controlled_buffer_42
  assign the_14_th_line_of_the_picture = lose ? 27'h980320 : 27'bz;  // Controlled_Buffer controlled_buffer_43
  assign the_15_th_line_of_the_picture = lose ? 27'h6000c0 : 27'bz;  // Controlled_Buffer controlled_buffer_44
  assign the_16_th_line_of_the_picture = lose ? 27'h71c00 : 27'bz;  // Controlled_Buffer controlled_buffer_45
  assign the_17_th_line_of_the_picture = play ? 27'h79f8e0 : 27'bz;  // Controlled_Buffer controlled_buffer_46
  assign the_18_th_line_of_the_picture = play ? 27'hf0f1e0 : 27'bz;  // Controlled_Buffer controlled_buffer_47
  assign the_19_th_line_of_the_picture = play ? 27'h1e000f0 : 27'bz;  // Controlled_Buffer controlled_buffer_48
  assign the_20_th_line_of_the_picture = play ? 27'h2a00078 : 27'bz;  // Controlled_Buffer controlled_buffer_49
  assign the_21_st_line_of_the_picture = play ? 27'h3c : 27'bz;  // Controlled_Buffer controlled_buffer_50
  assign the_22_nd_line_of_the_picture = play ? 27'h2a : 27'bz;  // Controlled_Buffer controlled_buffer_51
  get_number_of_survivors get_number_of_survivors_1 (
    .number_of_survivors(get_number_of_survivors_1_number_of_survivors), .in_out(in_out), .I_Oadr(I_Oadr),
    .I_Osel(I_Osel), .I_Odat(I_Odat), .clock(clock), .clear(clear));
  DotMatrix #(.inputtype("row"), .matrixcols(27), .matrixrows(23)) dotmatrix_3 (
    .row0({27{1'b0}}), .row1(27'h3070f7c), .row2(27'h30f9940), .row3(27'h30d8c78), .row4(27'h30d8640),
    .row5(27'h3efb67c), .row6(27'h3e71c7c), .row7({27{1'b0}}), .row8({27{1'b0}}), .row9({27{1'b0}}),
    .row10({27{1'b0}}), .row11(27'h20800), .row12(27'h40400), .row13(27'h980320), .row14(27'h6000c0),
    .row15(27'h71c00), .row16(27'h71c00), .row17({27{1'b0}}), .row18({27{1'b0}}), .row19(27'h7000),
    .row20(27'h8800), .row21({27{1'b0}}), .row22({27{1'b0}}));
  assign the_17_th_line_of_the_picture = victory ? 27'h28 : 27'bz;  // Controlled_Buffer controlled_buffer_52
  assign the_18_th_line_of_the_picture = victory ? 27'h280010 : 27'bz;  // Controlled_Buffer controlled_buffer_53
  assign the_19_th_line_of_the_picture = victory ? 27'h105028 : 27'bz;  // Controlled_Buffer controlled_buffer_54
  assign the_20_th_line_of_the_picture = victory ? 27'h282000 : 27'bz;  // Controlled_Buffer controlled_buffer_55
  assign the_21_st_line_of_the_picture = victory ? 27'h5000 : 27'bz;  // Controlled_Buffer controlled_buffer_56
  assign the_22_nd_line_of_the_picture = victory ? {27{1'b0}} : 27'bz;  // Controlled_Buffer controlled_buffer_57
  assign number_of_survivors = {{1{1'b0}}, get_number_of_survivors_1_number_of_survivors};  // Bit_Extender bit_extender_1
  assign the_17_th_line_of_the_picture = lose ? 27'h71c00 : 27'bz;  // Controlled_Buffer controlled_buffer_58
  assign the_18_th_line_of_the_picture = lose ? {27{1'b0}} : 27'bz;  // Controlled_Buffer controlled_buffer_59
  assign the_19_th_line_of_the_picture = lose ? {27{1'b0}} : 27'bz;  // Controlled_Buffer controlled_buffer_60
  assign the_20_th_line_of_the_picture = lose ? 27'h7000 : 27'bz;  // Controlled_Buffer controlled_buffer_61
  assign the_21_st_line_of_the_picture = lose ? 27'h8800 : 27'bz;  // Controlled_Buffer controlled_buffer_62
  assign the_22_nd_line_of_the_picture = lose ? {27{1'b0}} : 27'bz;  // Controlled_Buffer controlled_buffer_63

  assign the_1_st_line_of_the_picture = {27{1'b0}};
  assign the_23_rd_line_of_the_picture = {27{1'b0}};
endmodule

module record_score (
  input  in_out,
  input  [3:0] I_Oadr,
  input  I_Osel,
  input  [7:0] I_Odat,
  input  clock,
  input  clear,
  output [3:0] the_first_digit,
  output [3:0] the_second_digit,
  output [3:0] the_third_digit,
  output [31:0] the_1_st_line_of_the_picture,
  output [31:0] the_17_th_line_of_the_picture,
  output [31:0] the_1_st_line_of_the_picture_2,
  output [31:0] the_17_th_line_of_the_picture_2,
  output [31:0] the_2_nd_line_of_the_picture,
  output [31:0] the_18_th_line_of_the_picture,
  output [31:0] the_2_nd_line_of_the_picture_2,
  output [31:0] the_18_th_line_of_the_picture_2,
  output [31:0] the_3_rd_line_of_the_picture,
  output [31:0] the_19_th_line_of_the_picture,
  output [31:0] the_3_rd_line_of_the_picture_2,
  output [31:0] the_19_th_line_of_the_picture_2,
  output [31:0] the_4_th_line_of_the_picture,
  output [31:0] the_20_th_line_of_the_picture,
  output [31:0] the_4_th_line_of_the_picture_2,
  output [31:0] the_20_th_line_of_the_picture_2,
  output [31:0] the_5_th_line_of_the_picture,
  output [31:0] the_21_st_line_of_the_picture,
  output [31:0] the_5_th_line_of_the_picture_2,
  output [31:0] the_21_st_line_of_the_picture_2,
  output [31:0] the_6_th_line_of_the_picture,
  output [31:0] the_22_nd_line_of_the_picture,
  output [31:0] the_6_th_line_of_the_picture_2,
  output [31:0] the_22_nd_line_of_the_picture_2,
  output [31:0] the_7_th_line_of_the_picture,
  output [31:0] the_23_rd_line_of_the_picture,
  output [31:0] the_7_th_line_of_the_picture_2,
  output [31:0] the_23_rd_line_of_the_picture_2,
  output [31:0] the_8_th_line_of_the_picture,
  output [31:0] the_24_th_line_of_the_picture,
  output [31:0] the_8_th_line_of_the_picture_2,
  output [31:0] the_24_th_line_of_the_picture_2,
  output [31:0] the_9_th_line_of_the_picture,
  output [31:0] the_25_th_line_of_the_picture,
  output [31:0] the_9_th_line_of_the_picture_2,
  output [31:0] the_25_th_line_of_the_picture_2,
  output [31:0] the_10_th_line_of_the_picture,
  output [31:0] the_26_th_line_of_the_picture,
  output [31:0] the_10_th_line_of_the_picture_2,
  output [31:0] the_26_th_line_of_the_picture_2,
  output [31:0] the_11_th_line_of_the_picture,
  output [31:0] the_27_th_line_of_the_picture,
  output [31:0] the_11_th_line_of_the_picture_2,
  output [31:0] the_27_th_line_of_the_picture_2,
  output [31:0] the_12_th_line_of_the_picture,
  output [31:0] the_28_th_line_of_the_picture,
  output [31:0] the_12_th_line_of_the_picture_2,
  output [31:0] the_28_th_line_of_the_picture_2,
  output [31:0] the_13_th_line_of_the_picture,
  output [31:0] the_29_th_line_of_the_picture,
  output [31:0] the_13_th_line_of_the_picture_2,
  output [31:0] the_29_th_line_of_the_picture_2,
  output [31:0] the_14_th_line_of_the_picture,
  output [31:0] the_30_th_line_of_the_picture,
  output [31:0] the_14_th_line_of_the_picture_2,
  output [31:0] the_30_th_line_of_the_picture_2,
  output [31:0] the_15_th_line_of_the_picture,
  output [31:0] the_31_st_line_of_the_picture,
  output [31:0] the_15_th_line_of_the_picture_2,
  output [31:0] the_31_st_line_of_the_picture_2,
  output [31:0] the_16_th_line_of_the_picture,
  output [31:0] the_32_nd_line_of_the_picture,
  output [31:0] the_16_th_line_of_the_picture_2,
  output [31:0] the_32_nd_line_of_the_picture_2
);

  DotMatrix #(.inputtype("row"), .matrixcols(32), .matrixrows(32)) dotmatrix_1 (
    .row0({32{1'b0}}), .row1(32'h3e07e1f0), .row2(32'h7f8ff1f0), .row3(32'h71dff3f8), .row4(32'h60dfe3b8),
    .row5(32'h60dc071c), .row6(32'h60dc070d), .row7(32'h719fee01), .row8(32'h7f1fce01), .row9(32'h7e1c070d),
    .row10(32'h7c1c071c), .row11(32'h6e1fe3b8), .row12(32'h6e5ff3f8), .row13(32'h679ff1f0),
    .row14(32'h630fe1f0), .row15({32{1'b0}}), .row16({32{1'b0}}), .row17(32'hf81f007), .row18(32'h1fc1f01f),
    .row19(32'h3fe3f83f), .row20(32'h38e3b87c), .row21(32'h3c671cf8), .row22(32'h1e270cf8),
    .row23(32'hf0e01f0), .row24(32'h78e01f0), .row25(32'h43c70cf8), .row26(32'h61e71cf8),
    .row27(32'h70e3b87c), .row28(32'h79e3f83f), .row29(32'h3fe1f01f), .row30(32'h1fc1f007), .row31({32{1'b0}}));
  DotMatrix #(.inputtype("row"), .matrixcols(32), .matrixrows(32)) dotmatrix_2 (
    .row0({32{1'b0}}), .row1(32'h1f03e1f0), .row2(32'h3f87f9f8), .row3(32'h7fc71d98), .row4(32'hffe60d8c),
    .row5(32'hf1e60d8c), .row6(32'he0f60d86), .row7(32'hc0771986), .row8(32'hc077f186), .row9(32'he0f7e186),
    .row10(32'hf1e7c18c), .row11(32'hffe6e18c), .row12(32'h7fc6e598), .row13(32'h3f8679f8),
    .row14(32'h1f0631f0), .row15({32{1'b0}}), .row16({32{1'b0}}), .row17(32'he01f81fc), .row18(32'hf83fe3fe),
    .row19(32'hfc3c77fe), .row20(32'h3e3837fc), .row21(32'h1f383780), .row22(32'h1f383780),
    .row23(32'hfbc67fc), .row24(32'hfbfc7f8), .row25(32'h1f3f8780), .row26(32'h1f3f0780),
    .row27(32'h3e3b87fc), .row28(32'hfc3b97fe), .row29(32'hf839e7fe), .row30(32'he038c3fc), .row31({32{1'b0}}));
  get_record_score get_record_score_1 (
    .in_out(in_out), .I_Oadr(I_Oadr), .I_Osel(I_Osel), .I_Odat(I_Odat), .clock(clock), .clear(clear),
    .the_first_digit(the_first_digit), .the_second_digit(the_second_digit), .the_third_digit(the_third_digit));

  assign the_1_st_line_of_the_picture = {32{1'b0}};
  assign the_1_st_line_of_the_picture_2 = {32{1'b0}};
  assign the_2_nd_line_of_the_picture = 32'h3e07e1f0;
  assign the_2_nd_line_of_the_picture_2 = 32'h1f03e1f0;
  assign the_3_rd_line_of_the_picture = 32'h7f8ff1f0;
  assign the_3_rd_line_of_the_picture_2 = 32'h3f87f9f8;
  assign the_4_th_line_of_the_picture = 32'h71dff3f8;
  assign the_4_th_line_of_the_picture_2 = 32'h7fc71d98;
  assign the_5_th_line_of_the_picture = 32'h60dfe3b8;
  assign the_5_th_line_of_the_picture_2 = 32'hffe60d8c;
  assign the_6_th_line_of_the_picture = 32'h60dc071c;
  assign the_6_th_line_of_the_picture_2 = 32'hf1e60d8c;
  assign the_7_th_line_of_the_picture = 32'h60dc070d;
  assign the_7_th_line_of_the_picture_2 = 32'he0f60d86;
  assign the_8_th_line_of_the_picture = 32'h719fee01;
  assign the_8_th_line_of_the_picture_2 = 32'hc0771986;
  assign the_9_th_line_of_the_picture = 32'h7f1fce01;
  assign the_9_th_line_of_the_picture_2 = 32'hc077f186;
  assign the_10_th_line_of_the_picture = 32'h7e1c070d;
  assign the_10_th_line_of_the_picture_2 = 32'he0f7e186;
  assign the_11_th_line_of_the_picture = 32'h7c1c071c;
  assign the_11_th_line_of_the_picture_2 = 32'hf1e7c18c;
  assign the_12_th_line_of_the_picture = 32'h6e1fe3b8;
  assign the_12_th_line_of_the_picture_2 = 32'hffe6e18c;
  assign the_13_th_line_of_the_picture = 32'h6e5ff3f8;
  assign the_13_th_line_of_the_picture_2 = 32'h7fc6e598;
  assign the_14_th_line_of_the_picture = 32'h679ff1f0;
  assign the_14_th_line_of_the_picture_2 = 32'h3f8679f8;
  assign the_15_th_line_of_the_picture = 32'h630fe1f0;
  assign the_15_th_line_of_the_picture_2 = 32'h1f0631f0;
  assign the_16_th_line_of_the_picture = {32{1'b0}};
  assign the_16_th_line_of_the_picture_2 = {32{1'b0}};
  assign the_17_th_line_of_the_picture = {32{1'b0}};
  assign the_17_th_line_of_the_picture_2 = {32{1'b0}};
  assign the_18_th_line_of_the_picture = 32'hf81f007;
  assign the_18_th_line_of_the_picture_2 = 32'he01f81fc;
  assign the_19_th_line_of_the_picture = 32'h1fc1f01f;
  assign the_19_th_line_of_the_picture_2 = 32'hf83fe3fe;
  assign the_20_th_line_of_the_picture = 32'h3fe3f83f;
  assign the_20_th_line_of_the_picture_2 = 32'hfc3c77fe;
  assign the_21_st_line_of_the_picture = 32'h38e3b87c;
  assign the_21_st_line_of_the_picture_2 = 32'h3e3837fc;
  assign the_22_nd_line_of_the_picture = 32'h3c671cf8;
  assign the_22_nd_line_of_the_picture_2 = 32'h1f383780;
  assign the_23_rd_line_of_the_picture = 32'h1e270cf8;
  assign the_23_rd_line_of_the_picture_2 = 32'h1f383780;
  assign the_24_th_line_of_the_picture = 32'hf0e01f0;
  assign the_24_th_line_of_the_picture_2 = 32'hfbc67fc;
  assign the_25_th_line_of_the_picture = 32'h78e01f0;
  assign the_25_th_line_of_the_picture_2 = 32'hfbfc7f8;
  assign the_26_th_line_of_the_picture = 32'h43c70cf8;
  assign the_26_th_line_of_the_picture_2 = 32'h1f3f8780;
  assign the_27_th_line_of_the_picture = 32'h61e71cf8;
  assign the_27_th_line_of_the_picture_2 = 32'h1f3f0780;
  assign the_28_th_line_of_the_picture = 32'h70e3b87c;
  assign the_28_th_line_of_the_picture_2 = 32'h3e3b87fc;
  assign the_29_th_line_of_the_picture = 32'h79e3f83f;
  assign the_29_th_line_of_the_picture_2 = 32'hfc3b97fe;
  assign the_30_th_line_of_the_picture = 32'h3fe1f01f;
  assign the_30_th_line_of_the_picture_2 = 32'hf839e7fe;
  assign the_31_st_line_of_the_picture = 32'h1fc1f007;
  assign the_31_st_line_of_the_picture_2 = 32'he038c3fc;
  assign the_32_nd_line_of_the_picture = {32{1'b0}};
  assign the_32_nd_line_of_the_picture_2 = {32{1'b0}};
endmodule

module current_score (
  input  in_out,
  input  [3:0] I_Oadr,
  input  I_Osel,
  input  [7:0] I_Odat,
  input  clock,
  input  clear,
  output [3:0] the_first_digit,
  output [3:0] the_second_digit,
  output [3:0] the_third_digit,
  output [31:0] the_1_st_line_of_the_picture,
  output [31:0] the_17_th_line_of_the_picture,
  output [31:0] the_1_st_line_of_the_picture_2,
  output [31:0] the_17_th_line_of_the_picture_2,
  output [31:0] the_2_nd_line_of_the_picture,
  output [31:0] the_18_th_line_of_the_picture,
  output [31:0] the_2_nd_line_of_the_picture_2,
  output [31:0] the_18_th_line_of_the_picture_2,
  output [31:0] the_3_rd_line_of_the_picture,
  output [31:0] the_19_th_line_of_the_picture,
  output [31:0] the_3_rd_line_of_the_picture_2,
  output [31:0] the_19_th_line_of_the_picture_2,
  output [31:0] the_4_th_line_of_the_picture,
  output [31:0] the_20_th_line_of_the_picture,
  output [31:0] the_4_th_line_of_the_picture_2,
  output [31:0] the_20_th_line_of_the_picture_2,
  output [31:0] the_5_th_line_of_the_picture,
  output [31:0] the_21_st_line_of_the_picture,
  output [31:0] the_5_th_line_of_the_picture_2,
  output [31:0] the_21_st_line_of_the_picture_2,
  output [31:0] the_6_th_line_of_the_picture,
  output [31:0] the_22_nd_line_of_the_picture,
  output [31:0] the_6_th_line_of_the_picture_2,
  output [31:0] the_22_nd_line_of_the_picture_2,
  output [31:0] the_7_th_line_of_the_picture,
  output [31:0] the_23_rd_line_of_the_picture,
  output [31:0] the_7_th_line_of_the_picture_2,
  output [31:0] the_23_rd_line_of_the_picture_2,
  output [31:0] the_8_th_line_of_the_picture,
  output [31:0] the_24_th_line_of_the_picture,
  output [31:0] the_8_th_line_of_the_picture_2,
  output [31:0] the_24_th_line_of_the_picture_2,
  output [31:0] the_9_th_line_of_the_picture,
  output [31:0] the_25_th_line_of_the_picture,
  output [31:0] the_9_th_line_of_the_picture_2,
  output [31:0] the_25_th_line_of_the_picture_2,
  output [31:0] the_10_th_line_of_the_picture,
  output [31:0] the_26_th_line_of_the_picture,
  output [31:0] the_10_th_line_of_the_picture_2,
  output [31:0] the_26_th_line_of_the_picture_2,
  output [31:0] the_11_th_line_of_the_picture,
  output [31:0] the_27_th_line_of_the_picture,
  output [31:0] the_11_th_line_of_the_picture_2,
  output [31:0] the_27_th_line_of_the_picture_2,
  output [31:0] the_12_th_line_of_the_picture,
  output [31:0] the_28_th_line_of_the_picture,
  output [31:0] the_12_th_line_of_the_picture_2,
  output [31:0] the_28_th_line_of_the_picture_2,
  output [31:0] the_13_th_line_of_the_picture,
  output [31:0] the_29_th_line_of_the_picture,
  output [31:0] the_13_th_line_of_the_picture_2,
  output [31:0] the_29_th_line_of_the_picture_2,
  output [31:0] the_14_th_line_of_the_picture,
  output [31:0] the_30_th_line_of_the_picture,
  output [31:0] the_14_th_line_of_the_picture_2,
  output [31:0] the_30_th_line_of_the_picture_2,
  output [31:0] the_15_th_line_of_the_picture,
  output [31:0] the_31_st_line_of_the_picture,
  output [31:0] the_15_th_line_of_the_picture_2,
  output [31:0] the_31_st_line_of_the_picture_2,
  output [31:0] the_16_th_line_of_the_picture,
  output [31:0] the_32_nd_line_of_the_picture,
  output [31:0] the_16_th_line_of_the_picture_2,
  output [31:0] the_32_nd_line_of_the_picture_2
);

  DotMatrix #(.inputtype("row"), .matrixcols(32), .matrixrows(32)) dotmatrix_1 (
    .row0({32{1'b0}}), .row1(32'he663e0f), .row2(32'he777f9f), .row3(32'h1f3371dc), .row4(32'h1b3360d8),
    .row5(32'h31b360d8), .row6(32'h30b360d8), .row7(32'h6033719c), .row8(32'h60337f1f), .row9(32'h30b37e1f),
    .row10(32'h31b37c1f), .row11(32'h1b336e1b), .row12(32'h1f3f6e5b), .row13(32'he3f6799),
    .row14(32'he1e6318), .row15({32{1'b0}}), .row16({32{1'b0}}), .row17(32'hf81f007), .row18(32'h1fc1f01f),
    .row19(32'h3fe3f83f), .row20(32'h38e3b87c), .row21(32'h3c671cf8), .row22(32'h1e270cf8),
    .row23(32'hf0e01f0), .row24(32'h78e01f0), .row25(32'h43c70cf8), .row26(32'h61e71cf8),
    .row27(32'h70e3b87c), .row28(32'h79e3f83f), .row29(32'h3fe1f01f), .row30(32'h1fc1f007), .row31({32{1'b0}}));
  DotMatrix #(.inputtype("row"), .matrixcols(32), .matrixrows(32)) dotmatrix_2 (
    .row0({32{1'b0}}), .row1(32'h81f33d00), .row2(32'he3fb9dc0), .row3(32'h77fb8dfc), .row4(32'h37f3ccfe),
    .row5(32'h3703cc3e), .row6(32'h3703ec30), .row7(32'h67f36c30), .row8(32'hc7e37c30), .row9(32'h87033c30),
    .row10(32'h7033c30), .row11(32'h87f31c30), .row12(32'h17fb1c30), .row13(32'he7fb8c30),
    .row14(32'hc3f3cc30), .row15({32{1'b0}}), .row16({32{1'b0}}), .row17(32'he01f81fc), .row18(32'hf83fe3fe),
    .row19(32'hfc3c77fe), .row20(32'h3e3837fc), .row21(32'h1f383780), .row22(32'h1f383780),
    .row23(32'hfbc67fc), .row24(32'hfbfc7f8), .row25(32'h1f3f8780), .row26(32'h1f3f0780),
    .row27(32'h3e3b87fc), .row28(32'hfc3b97fe), .row29(32'hf839e7fe), .row30(32'he038c3fc), .row31({32{1'b0}}));
  get_current_score get_current_score_1 (
    .in_out(in_out), .I_Oadr(I_Oadr), .I_Osel(I_Osel), .I_Odat(I_Odat), .clock(clock), .clear(clear),
    .the_first_digit(the_first_digit), .the_second_digit(the_second_digit), .the_third_digit(the_third_digit));

  assign the_1_st_line_of_the_picture = {32{1'b0}};
  assign the_1_st_line_of_the_picture_2 = {32{1'b0}};
  assign the_2_nd_line_of_the_picture = 32'he663e0f;
  assign the_2_nd_line_of_the_picture_2 = 32'h81f33d00;
  assign the_3_rd_line_of_the_picture = 32'he777f9f;
  assign the_3_rd_line_of_the_picture_2 = 32'he3fb9dc0;
  assign the_4_th_line_of_the_picture = 32'h1f3371dc;
  assign the_4_th_line_of_the_picture_2 = 32'h77fb8dfc;
  assign the_5_th_line_of_the_picture = 32'h1b3360d8;
  assign the_5_th_line_of_the_picture_2 = 32'h37f3ccfe;
  assign the_6_th_line_of_the_picture = 32'h31b360d8;
  assign the_6_th_line_of_the_picture_2 = 32'h3703cc3e;
  assign the_7_th_line_of_the_picture = 32'h30b360d8;
  assign the_7_th_line_of_the_picture_2 = 32'h3703ec30;
  assign the_8_th_line_of_the_picture = 32'h6033719c;
  assign the_8_th_line_of_the_picture_2 = 32'h67f36c30;
  assign the_9_th_line_of_the_picture = 32'h60337f1f;
  assign the_9_th_line_of_the_picture_2 = 32'hc7e37c30;
  assign the_10_th_line_of_the_picture = 32'h30b37e1f;
  assign the_10_th_line_of_the_picture_2 = 32'h87033c30;
  assign the_11_th_line_of_the_picture = 32'h31b37c1f;
  assign the_11_th_line_of_the_picture_2 = 32'h7033c30;
  assign the_12_th_line_of_the_picture = 32'h1b336e1b;
  assign the_12_th_line_of_the_picture_2 = 32'h87f31c30;
  assign the_13_th_line_of_the_picture = 32'h1f3f6e5b;
  assign the_13_th_line_of_the_picture_2 = 32'h17fb1c30;
  assign the_14_th_line_of_the_picture = 32'he3f6799;
  assign the_14_th_line_of_the_picture_2 = 32'he7fb8c30;
  assign the_15_th_line_of_the_picture = 32'he1e6318;
  assign the_15_th_line_of_the_picture_2 = 32'hc3f3cc30;
  assign the_16_th_line_of_the_picture = {32{1'b0}};
  assign the_16_th_line_of_the_picture_2 = {32{1'b0}};
  assign the_17_th_line_of_the_picture = {32{1'b0}};
  assign the_17_th_line_of_the_picture_2 = {32{1'b0}};
  assign the_18_th_line_of_the_picture = 32'hf81f007;
  assign the_18_th_line_of_the_picture_2 = 32'he01f81fc;
  assign the_19_th_line_of_the_picture = 32'h1fc1f01f;
  assign the_19_th_line_of_the_picture_2 = 32'hf83fe3fe;
  assign the_20_th_line_of_the_picture = 32'h3fe3f83f;
  assign the_20_th_line_of_the_picture_2 = 32'hfc3c77fe;
  assign the_21_st_line_of_the_picture = 32'h38e3b87c;
  assign the_21_st_line_of_the_picture_2 = 32'h3e3837fc;
  assign the_22_nd_line_of_the_picture = 32'h3c671cf8;
  assign the_22_nd_line_of_the_picture_2 = 32'h1f383780;
  assign the_23_rd_line_of_the_picture = 32'h1e270cf8;
  assign the_23_rd_line_of_the_picture_2 = 32'h1f383780;
  assign the_24_th_line_of_the_picture = 32'hf0e01f0;
  assign the_24_th_line_of_the_picture_2 = 32'hfbc67fc;
  assign the_25_th_line_of_the_picture = 32'h78e01f0;
  assign the_25_th_line_of_the_picture_2 = 32'hfbfc7f8;
  assign the_26_th_line_of_the_picture = 32'h43c70cf8;
  assign the_26_th_line_of_the_picture_2 = 32'h1f3f8780;
  assign the_27_th_line_of_the_picture = 32'h61e71cf8;
  assign the_27_th_line_of_the_picture_2 = 32'h1f3f0780;
  assign the_28_th_line_of_the_picture = 32'h70e3b87c;
  assign the_28_th_line_of_the_picture_2 = 32'h3e3b87fc;
  assign the_29_th_line_of_the_picture = 32'h79e3f83f;
  assign the_29_th_line_of_the_picture_2 = 32'hfc3b97fe;
  assign the_30_th_line_of_the_picture = 32'h3fe1f01f;
  assign the_30_th_line_of_the_picture_2 = 32'hf839e7fe;
  assign the_31_st_line_of_the_picture = 32'h1fc1f007;
  assign the_31_st_line_of_the_picture_2 = 32'he038c3fc;
  assign the_32_nd_line_of_the_picture = {32{1'b0}};
  assign the_32_nd_line_of_the_picture_2 = {32{1'b0}};
endmodule
module digits (
  input  [3:0] digit,
  output [19:0] the_1_st_line_of_the_picture,
  output [19:0] the_16_th_line_of_the_picture,
  output [19:0] the_2_nd_line_of_the_picture,
  output [19:0] the_17_th_line_of_the_picture,
  output [19:0] the_3_rd_line_of_the_picture,
  output [19:0] the_18_th_line_of_the_picture,
  output [19:0] the_4_th_line_of_the_picture,
  output [19:0] the_19_th_line_of_the_picture,
  output [19:0] the_5_th_line_of_the_picture,
  output [19:0] the_20_th_line_of_the_picture,
  output [19:0] the_6_th_line_of_the_picture,
  output [19:0] the_21_st_line_of_the_picture,
  output [19:0] the_7_th_line_of_the_picture,
  output [19:0] the_22_nd_line_of_the_picture,
  output [19:0] the_8_th_line_of_the_picture,
  output [19:0] the_23_rd_line_of_the_picture,
  output [19:0] the_9_th_line_of_the_picture,
  output [19:0] the_24_th_line_of_the_picture,
  output [19:0] the_10_th_line_of_the_picture,
  output [19:0] the_25_th_line_of_the_picture,
  output [19:0] the_11_th_line_of_the_picture,
  output [19:0] the_26_th_line_of_the_picture,
  output [19:0] the_12_th_line_of_the_picture,
  output [19:0] the_27_th_line_of_the_picture,
  output [19:0] the_13_th_line_of_the_picture,
  output [19:0] the_28_th_line_of_the_picture,
  output [19:0] the_14_th_line_of_the_picture,
  output [19:0] the_29_th_line_of_the_picture,
  output [19:0] the_15_th_line_of_the_picture,
  output [19:0] the_30_th_line_of_the_picture
);

  wire _0, _1, _2, _3, _4, _5, _6, _7, _8, _9;

  DotMatrix #(.inputtype("row"), .matrixcols(20), .matrixrows(30)) dotmatrix_1 (
    .row0({20{1'b0}}), .row1({20{1'b0}}), .row2({20{1'b0}}), .row3(20'h3fc0), .row4(20'h7fe0),
    .row5(20'hfff0), .row6(20'h1fff8), .row7(20'h1f0f8), .row8(20'h1e078), .row9(20'h1c038),
    .row10(20'h1c038), .row11(20'h1c038), .row12(20'h1c038), .row13(20'h1c038), .row14(20'h1c038),
    .row15(20'h1c038), .row16(20'h1c038), .row17(20'h1c038), .row18(20'h1c038), .row19(20'h1c038),
    .row20(20'h1c038), .row21(20'h1e078), .row22(20'h1f0f8), .row23(20'h1fff8), .row24(20'hfff0),
    .row25(20'h7fe0), .row26(20'h3fc0), .row27({20{1'b0}}), .row28({20{1'b0}}), .row29({20{1'b0}}));
  DotMatrix #(.inputtype("row"), .matrixcols(20), .matrixrows(30)) dotmatrix_2 (
    .row0({20{1'b0}}), .row1({20{1'b0}}), .row2({20{1'b0}}), .row3(20'h1f80), .row4(20'h3fc0),
    .row5(20'h7fe0), .row6(20'hfff0), .row7(20'h1f9f8), .row8(20'h1f0f8), .row9(20'h1e0f8), .row10(20'he1f8),
    .row11(20'h3f8), .row12(20'h3f0), .row13(20'h7e0), .row14(20'h7c0), .row15(20'h7c0), .row16(20'h7e0),
    .row17(20'h3f0), .row18(20'h3f8), .row19(20'he1f8), .row20(20'h1e0f8), .row21(20'h1f0f8),
    .row22(20'h1f9f8), .row23(20'hfff0), .row24(20'h7fe0), .row25(20'h3fc0), .row26(20'h1f80),
    .row27({20{1'b0}}), .row28({20{1'b0}}), .row29({20{1'b0}}));
  DotMatrix #(.inputtype("row"), .matrixcols(20), .matrixrows(30)) dotmatrix_3 (
    .row0({20{1'b0}}), .row1({20{1'b0}}), .row2({20{1'b0}}), .row3(20'h1f80), .row4(20'h3fc0),
    .row5(20'h7fe0), .row6(20'h7ff0), .row7(20'hfff8), .row8(20'hfc78), .row9(20'h1f838), .row10(20'h1f800),
    .row11(20'h1f000), .row12(20'h1f780), .row13(20'h1ffc0), .row14(20'h1ffe0), .row15(20'h1fff0),
    .row16(20'h1f9f8), .row17(20'h1f0f8), .row18(20'h1e078), .row19(20'h1e078), .row20(20'h1e078),
    .row21(20'h1f0f8), .row22(20'h1f9f8), .row23(20'hfff0), .row24(20'h7fe0), .row25(20'h3fc0),
    .row26(20'h1f80), .row27({20{1'b0}}), .row28({20{1'b0}}), .row29({20{1'b0}}));
  DotMatrix #(.inputtype("row"), .matrixcols(20), .matrixrows(30)) dotmatrix_4 (
    .row0({20{1'b0}}), .row1({20{1'b0}}), .row2({20{1'b0}}), .row3(20'h1f80), .row4(20'h3fc0),
    .row5(20'h7fe0), .row6(20'hfff0), .row7(20'h1f9f8), .row8(20'h1f0f8), .row9(20'h1e078),
    .row10(20'h1e078), .row11(20'h1e078), .row12(20'h1f0f8), .row13(20'h1f9f8), .row14(20'hfff8),
    .row15(20'h7ff8), .row16(20'h3ff8), .row17(20'h1ef8), .row18(20'hf8), .row19(20'h1f8), .row20(20'h1c1f8),
    .row21(20'h1e3f0), .row22(20'h1fff0), .row23(20'hffe0), .row24(20'h7fe0), .row25(20'h3fc0),
    .row26(20'h1f80), .row27({20{1'b0}}), .row28({20{1'b0}}), .row29({20{1'b0}}));
  DotMatrix #(.inputtype("row"), .matrixcols(20), .matrixrows(30)) dotmatrix_5 (
    .row0({20{1'b0}}), .row1({20{1'b0}}), .row2({20{1'b0}}), .row3(20'h780), .row4(20'hf80), .row5(20'h1f80),
    .row6(20'h3f80), .row7(20'h7f80), .row8(20'hff80), .row9(20'h1ff80), .row10(20'h3ef80),
    .row11(20'h3cf80), .row12(20'h38f80), .row13(20'hf80), .row14(20'hf80), .row15(20'hf80), .row16(20'hf80),
    .row17(20'hf80), .row18(20'hf80), .row19(20'hf80), .row20(20'hf80), .row21(20'hf80), .row22(20'hf80),
    .row23(20'h7f80), .row24(20'hfff0), .row25(20'h1fff8), .row26(20'h3fffc), .row27({20{1'b0}}),
    .row28({20{1'b0}}), .row29({20{1'b0}}));
  DotMatrix #(.inputtype("row"), .matrixcols(20), .matrixrows(30)) dotmatrix_6 (
    .row0({20{1'b0}}), .row1({20{1'b0}}), .row2({20{1'b0}}), .row3(20'he000), .row4(20'h1e1e0),
    .row5(20'h1e1e0), .row6(20'h1e1e0), .row7(20'h1e1e0), .row8(20'h1e1e0), .row9(20'h1e1e0),
    .row10(20'h1e1e0), .row11(20'h1fff0), .row12(20'h1fff8), .row13(20'hfff8), .row14(20'h1e0),
    .row15(20'h1e0), .row16(20'h1e0), .row17(20'h1e0), .row18(20'h1e0), .row19(20'h1e0), .row20(20'h1e0),
    .row21(20'h1e0), .row22(20'h1e0), .row23(20'h3f0), .row24(20'h7f8), .row25(20'hff8), .row26(20'h1ff8),
    .row27({20{1'b0}}), .row28({20{1'b0}}), .row29({20{1'b0}}));
  DotMatrix #(.inputtype("row"), .matrixcols(20), .matrixrows(30)) dotmatrix_7 (
    .row0({20{1'b0}}), .row1({20{1'b0}}), .row2({20{1'b0}}), .row3(20'hfff8), .row4(20'h1fff8),
    .row5(20'h1fff8), .row6(20'h1fff8), .row7(20'hfff0), .row8(20'h3e0), .row9(20'h7c0), .row10(20'hf80),
    .row11(20'h38f80), .row12(20'h3cf80), .row13(20'h3ef80), .row14(20'h1ffe0), .row15(20'hfff0),
    .row16(20'h7ff8), .row17(20'h1f7c), .row18(20'h3e3c), .row19(20'h3e1c), .row20(20'h3e00),
    .row21(20'h3e00), .row22(20'h7c00), .row23(20'h7c00), .row24(20'h7c00), .row25(20'hf800),
    .row26(20'hf800), .row27({20{1'b0}}), .row28({20{1'b0}}), .row29({20{1'b0}}));
  DotMatrix #(.inputtype("row"), .matrixcols(20), .matrixrows(30)) dotmatrix_8 (
    .row0({20{1'b0}}), .row1({20{1'b0}}), .row2({20{1'b0}}), .row3(20'h1fc0), .row4(20'h3fe0),
    .row5(20'h7ff0), .row6(20'hfff8), .row7(20'h1fff8), .row8(20'h1fff8), .row9(20'h1fff8),
    .row10(20'h1f3f8), .row11(20'h1e1f8), .row12(20'h1e1f8), .row13(20'he1f8), .row14(20'h3f8),
    .row15(20'h7f8), .row16(20'hff0), .row17(20'h1fe0), .row18(20'h3fc0), .row19(20'h7f80), .row20(20'hff00),
    .row21(20'h1fff8), .row22(20'h1fff8), .row23(20'h1fff8), .row24(20'h1fff8), .row25(20'h1fff8),
    .row26(20'h1fff8), .row27({20{1'b0}}), .row28({20{1'b0}}), .row29({20{1'b0}}));
  DotMatrix #(.inputtype("row"), .matrixcols(20), .matrixrows(30)) dotmatrix_9 (
    .row0({20{1'b0}}), .row1({20{1'b0}}), .row2({20{1'b0}}), .row3(20'h1f8), .row4(20'hfff8),
    .row5(20'h1fff8), .row6(20'h1fff8), .row7(20'h1fff8), .row8(20'h1fff0), .row9(20'h1f000),
    .row10(20'h1f000), .row11(20'h1f800), .row12(20'h1ffe0), .row13(20'hfff0), .row14(20'h7ff8),
    .row15(20'h1f8), .row16(20'hf8), .row17(20'hf8), .row18(20'h1c0f8), .row19(20'h1e0f8), .row20(20'h1f1f8),
    .row21(20'h1fff8), .row22(20'h1fff8), .row23(20'h1fff0), .row24(20'hffe0), .row25(20'h7fc0),
    .row26(20'h3f80), .row27({20{1'b0}}), .row28({20{1'b0}}), .row29({20{1'b0}}));
  DotMatrix #(.inputtype("row"), .matrixcols(20), .matrixrows(30)) dotmatrix_10 (
    .row0({20{1'b0}}), .row1({20{1'b0}}), .row2({20{1'b0}}), .row3(20'h7fe0), .row4(20'hfff0),
    .row5(20'h1fff8), .row6(20'h1f0f8), .row7(20'h1e078), .row8(20'h1c038), .row9(20'h1c038),
    .row10(20'h1e078), .row11(20'hf0f0), .row12(20'h79e0), .row13(20'h3fc0), .row14(20'h1f80),
    .row15(20'h1f80), .row16(20'h3fc0), .row17(20'h79e0), .row18(20'hf0f0), .row19(20'h1e078),
    .row20(20'h1c038), .row21(20'h1c038), .row22(20'h1e078), .row23(20'h1f0f8), .row24(20'h1fff8),
    .row25(20'hfff0), .row26(20'h7fe0), .row27({20{1'b0}}), .row28({20{1'b0}}), .row29({20{1'b0}}));
  Demultiplexer #(.select(4), .disabled(0), .enable("false")) demultiplexer_1 (
    .out0(_0), .out1(_1), .out2(_2), .out3(_3), .out4(_4), .out5(_5), .out6(_6), .out7(_7), .out8(_8),
    .out9(_9), .in(1'b1), .sel(digit));  // open: out10, out11, out12, out13, out14, out15
  assign the_4_th_line_of_the_picture = _1 ? 20'h780 : 20'bz;  // Controlled_Buffer controlled_buffer_1
  assign the_4_th_line_of_the_picture = _0 ? 20'h3fc0 : 20'bz;  // Controlled_Buffer controlled_buffer_2
  assign the_5_th_line_of_the_picture = _0 ? 20'h7fe0 : 20'bz;  // Controlled_Buffer controlled_buffer_3
  assign the_5_th_line_of_the_picture = _1 ? 20'hf80 : 20'bz;  // Controlled_Buffer controlled_buffer_4
  assign the_6_th_line_of_the_picture = _0 ? 20'hfff0 : 20'bz;  // Controlled_Buffer controlled_buffer_5
  assign the_6_th_line_of_the_picture = _1 ? 20'h1f80 : 20'bz;  // Controlled_Buffer controlled_buffer_6
  assign the_7_th_line_of_the_picture = _0 ? 20'h1fff8 : 20'bz;  // Controlled_Buffer controlled_buffer_7
  assign the_7_th_line_of_the_picture = _1 ? 20'h3f80 : 20'bz;  // Controlled_Buffer controlled_buffer_8
  assign the_8_th_line_of_the_picture = _0 ? 20'h1f0f8 : 20'bz;  // Controlled_Buffer controlled_buffer_9
  assign the_8_th_line_of_the_picture = _1 ? 20'h7f80 : 20'bz;  // Controlled_Buffer controlled_buffer_10
  assign the_9_th_line_of_the_picture = _0 ? 20'h1e078 : 20'bz;  // Controlled_Buffer controlled_buffer_11
  assign the_9_th_line_of_the_picture = _1 ? 20'hff80 : 20'bz;  // Controlled_Buffer controlled_buffer_12
  assign the_10_th_line_of_the_picture = _1 ? 20'h1ff80 : 20'bz;  // Controlled_Buffer controlled_buffer_13
  assign the_10_th_line_of_the_picture = _0 ? 20'h1c038 : 20'bz;  // Controlled_Buffer controlled_buffer_14
  assign the_11_th_line_of_the_picture = _1 ? 20'h3ef80 : 20'bz;  // Controlled_Buffer controlled_buffer_15
  assign the_11_th_line_of_the_picture = _0 ? 20'h1c038 : 20'bz;  // Controlled_Buffer controlled_buffer_16
  assign the_12_th_line_of_the_picture = _0 ? 20'h1c038 : 20'bz;  // Controlled_Buffer controlled_buffer_17
  assign the_12_th_line_of_the_picture = _1 ? 20'h3cf80 : 20'bz;  // Controlled_Buffer controlled_buffer_18
  assign the_13_th_line_of_the_picture = _0 ? 20'h1c038 : 20'bz;  // Controlled_Buffer controlled_buffer_19
  assign the_13_th_line_of_the_picture = _1 ? 20'h38f80 : 20'bz;  // Controlled_Buffer controlled_buffer_20
  assign the_14_th_line_of_the_picture = _1 ? 20'hf80 : 20'bz;  // Controlled_Buffer controlled_buffer_21
  assign the_14_th_line_of_the_picture = _0 ? 20'h1c038 : 20'bz;  // Controlled_Buffer controlled_buffer_22
  assign the_15_th_line_of_the_picture = _1 ? 20'hf80 : 20'bz;  // Controlled_Buffer controlled_buffer_23
  assign the_15_th_line_of_the_picture = _0 ? 20'h1c038 : 20'bz;  // Controlled_Buffer controlled_buffer_24
  assign the_4_th_line_of_the_picture = _2 ? 20'h1fc0 : 20'bz;  // Controlled_Buffer controlled_buffer_25
  assign the_5_th_line_of_the_picture = _2 ? 20'h3fe0 : 20'bz;  // Controlled_Buffer controlled_buffer_26
  assign the_6_th_line_of_the_picture = _2 ? 20'h7ff0 : 20'bz;  // Controlled_Buffer controlled_buffer_27
  assign the_7_th_line_of_the_picture = _2 ? 20'hfff8 : 20'bz;  // Controlled_Buffer controlled_buffer_28
  assign the_8_th_line_of_the_picture = _2 ? 20'h1fff8 : 20'bz;  // Controlled_Buffer controlled_buffer_29
  assign the_9_th_line_of_the_picture = _2 ? 20'h1fff8 : 20'bz;  // Controlled_Buffer controlled_buffer_30
  assign the_10_th_line_of_the_picture = _2 ? 20'h1fff8 : 20'bz;  // Controlled_Buffer controlled_buffer_31
  assign the_11_th_line_of_the_picture = _2 ? 20'h1f3f8 : 20'bz;  // Controlled_Buffer controlled_buffer_32
  assign the_12_th_line_of_the_picture = _2 ? 20'h1e1f8 : 20'bz;  // Controlled_Buffer controlled_buffer_33
  assign the_13_th_line_of_the_picture = _2 ? 20'h1e1f8 : 20'bz;  // Controlled_Buffer controlled_buffer_34
  assign the_14_th_line_of_the_picture = _2 ? 20'he1f8 : 20'bz;  // Controlled_Buffer controlled_buffer_35
  assign the_15_th_line_of_the_picture = _2 ? 20'h3f8 : 20'bz;  // Controlled_Buffer controlled_buffer_36
  assign the_4_th_line_of_the_picture = _3 ? 20'h1f80 : 20'bz;  // Controlled_Buffer controlled_buffer_37
  assign the_5_th_line_of_the_picture = _3 ? 20'h3fc0 : 20'bz;  // Controlled_Buffer controlled_buffer_38
  assign the_6_th_line_of_the_picture = _3 ? 20'h7fe0 : 20'bz;  // Controlled_Buffer controlled_buffer_39
  assign the_7_th_line_of_the_picture = _3 ? 20'hfff0 : 20'bz;  // Controlled_Buffer controlled_buffer_40
  assign the_8_th_line_of_the_picture = _3 ? 20'h1f9f8 : 20'bz;  // Controlled_Buffer controlled_buffer_41
  assign the_9_th_line_of_the_picture = _3 ? 20'h1f0f8 : 20'bz;  // Controlled_Buffer controlled_buffer_42
  assign the_10_th_line_of_the_picture = _3 ? 20'h1e0f8 : 20'bz;  // Controlled_Buffer controlled_buffer_43
  assign the_11_th_line_of_the_picture = _3 ? 20'he1f8 : 20'bz;  // Controlled_Buffer controlled_buffer_44
  assign the_12_th_line_of_the_picture = _3 ? 20'h3f8 : 20'bz;  // Controlled_Buffer controlled_buffer_45
  assign the_13_th_line_of_the_picture = _3 ? 20'h3f0 : 20'bz;  // Controlled_Buffer controlled_buffer_46
  assign the_14_th_line_of_the_picture = _3 ? 20'h7e0 : 20'bz;  // Controlled_Buffer controlled_buffer_47
  assign the_15_th_line_of_the_picture = _3 ? 20'h7c0 : 20'bz;  // Controlled_Buffer controlled_buffer_48
  assign the_4_th_line_of_the_picture = _4 ? 20'he000 : 20'bz;  // Controlled_Buffer controlled_buffer_49
  assign the_5_th_line_of_the_picture = _4 ? 20'h1e1e0 : 20'bz;  // Controlled_Buffer controlled_buffer_50
  assign the_6_th_line_of_the_picture = _4 ? 20'h1e1e0 : 20'bz;  // Controlled_Buffer controlled_buffer_51
  assign the_7_th_line_of_the_picture = _4 ? 20'h1e1e0 : 20'bz;  // Controlled_Buffer controlled_buffer_52
  assign the_8_th_line_of_the_picture = _4 ? 20'h1e1e0 : 20'bz;  // Controlled_Buffer controlled_buffer_53
  assign the_9_th_line_of_the_picture = _4 ? 20'h1e1e0 : 20'bz;  // Controlled_Buffer controlled_buffer_54
  assign the_10_th_line_of_the_picture = _4 ? 20'h1e1e0 : 20'bz;  // Controlled_Buffer controlled_buffer_55
  assign the_11_th_line_of_the_picture = _4 ? 20'h1e1e0 : 20'bz;  // Controlled_Buffer controlled_buffer_56
  assign the_12_th_line_of_the_picture = _4 ? 20'h1fff0 : 20'bz;  // Controlled_Buffer controlled_buffer_57
  assign the_13_th_line_of_the_picture = _4 ? 20'h1fff8 : 20'bz;  // Controlled_Buffer controlled_buffer_58
  assign the_14_th_line_of_the_picture = _4 ? 20'hfff8 : 20'bz;  // Controlled_Buffer controlled_buffer_59
  assign the_15_th_line_of_the_picture = _4 ? 20'h1e0 : 20'bz;  // Controlled_Buffer controlled_buffer_60
  assign the_4_th_line_of_the_picture = _5 ? 20'h1f8 : 20'bz;  // Controlled_Buffer controlled_buffer_61
  assign the_5_th_line_of_the_picture = _5 ? 20'hfff8 : 20'bz;  // Controlled_Buffer controlled_buffer_62
  assign the_6_th_line_of_the_picture = _5 ? 20'h1fff8 : 20'bz;  // Controlled_Buffer controlled_buffer_63
  assign the_7_th_line_of_the_picture = _5 ? 20'h1fff8 : 20'bz;  // Controlled_Buffer controlled_buffer_64
  assign the_8_th_line_of_the_picture = _5 ? 20'h1fff8 : 20'bz;  // Controlled_Buffer controlled_buffer_65
  assign the_9_th_line_of_the_picture = _5 ? 20'h1fff0 : 20'bz;  // Controlled_Buffer controlled_buffer_66
  assign the_10_th_line_of_the_picture = _5 ? 20'h1f000 : 20'bz;  // Controlled_Buffer controlled_buffer_67
  assign the_11_th_line_of_the_picture = _5 ? 20'h1f000 : 20'bz;  // Controlled_Buffer controlled_buffer_68
  assign the_12_th_line_of_the_picture = _5 ? 20'h1f800 : 20'bz;  // Controlled_Buffer controlled_buffer_69
  assign the_13_th_line_of_the_picture = _5 ? 20'h1ffe0 : 20'bz;  // Controlled_Buffer controlled_buffer_70
  assign the_14_th_line_of_the_picture = _5 ? 20'hfff0 : 20'bz;  // Controlled_Buffer controlled_buffer_71
  assign the_15_th_line_of_the_picture = _5 ? 20'h7ff8 : 20'bz;  // Controlled_Buffer controlled_buffer_72
  assign the_4_th_line_of_the_picture = _6 ? 20'h1f80 : 20'bz;  // Controlled_Buffer controlled_buffer_73
  assign the_5_th_line_of_the_picture = _6 ? 20'h3fc0 : 20'bz;  // Controlled_Buffer controlled_buffer_74
  assign the_6_th_line_of_the_picture = _6 ? 20'h7fe0 : 20'bz;  // Controlled_Buffer controlled_buffer_75
  assign the_7_th_line_of_the_picture = _6 ? 20'h7ff0 : 20'bz;  // Controlled_Buffer controlled_buffer_76
  assign the_8_th_line_of_the_picture = _6 ? 20'hfff8 : 20'bz;  // Controlled_Buffer controlled_buffer_77
  assign the_9_th_line_of_the_picture = _6 ? 20'hfc78 : 20'bz;  // Controlled_Buffer controlled_buffer_78
  assign the_10_th_line_of_the_picture = _6 ? 20'h1f838 : 20'bz;  // Controlled_Buffer controlled_buffer_79
  assign the_11_th_line_of_the_picture = _6 ? 20'h1f800 : 20'bz;  // Controlled_Buffer controlled_buffer_80
  assign the_12_th_line_of_the_picture = _6 ? 20'h1f000 : 20'bz;  // Controlled_Buffer controlled_buffer_81
  assign the_13_th_line_of_the_picture = _6 ? 20'h1f780 : 20'bz;  // Controlled_Buffer controlled_buffer_82
  assign the_14_th_line_of_the_picture = _6 ? 20'h1ffc0 : 20'bz;  // Controlled_Buffer controlled_buffer_83
  assign the_15_th_line_of_the_picture = _6 ? 20'h1ffe0 : 20'bz;  // Controlled_Buffer controlled_buffer_84
  assign the_4_th_line_of_the_picture = _7 ? 20'hfff8 : 20'bz;  // Controlled_Buffer controlled_buffer_85
  assign the_5_th_line_of_the_picture = _7 ? 20'h1fff8 : 20'bz;  // Controlled_Buffer controlled_buffer_86
  assign the_6_th_line_of_the_picture = _7 ? 20'h1fff8 : 20'bz;  // Controlled_Buffer controlled_buffer_87
  assign the_7_th_line_of_the_picture = _7 ? 20'h1fff8 : 20'bz;  // Controlled_Buffer controlled_buffer_88
  assign the_8_th_line_of_the_picture = _7 ? 20'hfff0 : 20'bz;  // Controlled_Buffer controlled_buffer_89
  assign the_9_th_line_of_the_picture = _7 ? 20'h3e0 : 20'bz;  // Controlled_Buffer controlled_buffer_90
  assign the_10_th_line_of_the_picture = _7 ? 20'h7c0 : 20'bz;  // Controlled_Buffer controlled_buffer_91
  assign the_11_th_line_of_the_picture = _7 ? 20'hf80 : 20'bz;  // Controlled_Buffer controlled_buffer_92
  assign the_12_th_line_of_the_picture = _7 ? 20'h38f80 : 20'bz;  // Controlled_Buffer controlled_buffer_93
  assign the_13_th_line_of_the_picture = _7 ? 20'h3cf80 : 20'bz;  // Controlled_Buffer controlled_buffer_94
  assign the_14_th_line_of_the_picture = _7 ? 20'h3ef80 : 20'bz;  // Controlled_Buffer controlled_buffer_95
  assign the_15_th_line_of_the_picture = _7 ? 20'h1ffe0 : 20'bz;  // Controlled_Buffer controlled_buffer_96
  assign the_4_th_line_of_the_picture = _8 ? 20'h7fe0 : 20'bz;  // Controlled_Buffer controlled_buffer_97
  assign the_5_th_line_of_the_picture = _8 ? 20'hfff0 : 20'bz;  // Controlled_Buffer controlled_buffer_98
  assign the_6_th_line_of_the_picture = _8 ? 20'h1fff8 : 20'bz;  // Controlled_Buffer controlled_buffer_99
  assign the_7_th_line_of_the_picture = _8 ? 20'h1f0f8 : 20'bz;  // Controlled_Buffer controlled_buffer_100
  assign the_8_th_line_of_the_picture = _8 ? 20'h1e078 : 20'bz;  // Controlled_Buffer controlled_buffer_101
  assign the_9_th_line_of_the_picture = _8 ? 20'h1c038 : 20'bz;  // Controlled_Buffer controlled_buffer_102
  assign the_10_th_line_of_the_picture = _8 ? 20'h1c038 : 20'bz;  // Controlled_Buffer controlled_buffer_103
  assign the_11_th_line_of_the_picture = _8 ? 20'h1e078 : 20'bz;  // Controlled_Buffer controlled_buffer_104
  assign the_12_th_line_of_the_picture = _8 ? 20'hf0f0 : 20'bz;  // Controlled_Buffer controlled_buffer_105
  assign the_13_th_line_of_the_picture = _8 ? 20'h79e0 : 20'bz;  // Controlled_Buffer controlled_buffer_106
  assign the_14_th_line_of_the_picture = _8 ? 20'h3fc0 : 20'bz;  // Controlled_Buffer controlled_buffer_107
  assign the_15_th_line_of_the_picture = _8 ? 20'h1f80 : 20'bz;  // Controlled_Buffer controlled_buffer_108
  assign the_4_th_line_of_the_picture = _9 ? 20'h1f80 : 20'bz;  // Controlled_Buffer controlled_buffer_109
  assign the_5_th_line_of_the_picture = _9 ? 20'h3fc0 : 20'bz;  // Controlled_Buffer controlled_buffer_110
  assign the_6_th_line_of_the_picture = _9 ? 20'h7fe0 : 20'bz;  // Controlled_Buffer controlled_buffer_111
  assign the_7_th_line_of_the_picture = _9 ? 20'hfff0 : 20'bz;  // Controlled_Buffer controlled_buffer_112
  assign the_8_th_line_of_the_picture = _9 ? 20'h1f9f8 : 20'bz;  // Controlled_Buffer controlled_buffer_113
  assign the_9_th_line_of_the_picture = _9 ? 20'h1f0f8 : 20'bz;  // Controlled_Buffer controlled_buffer_114
  assign the_10_th_line_of_the_picture = _9 ? 20'h1e078 : 20'bz;  // Controlled_Buffer controlled_buffer_115
  assign the_11_th_line_of_the_picture = _9 ? 20'h1e078 : 20'bz;  // Controlled_Buffer controlled_buffer_116
  assign the_12_th_line_of_the_picture = _9 ? 20'h1e078 : 20'bz;  // Controlled_Buffer controlled_buffer_117
  assign the_13_th_line_of_the_picture = _9 ? 20'h1f0f8 : 20'bz;  // Controlled_Buffer controlled_buffer_118
  assign the_14_th_line_of_the_picture = _9 ? 20'h1f9f8 : 20'bz;  // Controlled_Buffer controlled_buffer_119
  assign the_15_th_line_of_the_picture = _9 ? 20'hfff8 : 20'bz;  // Controlled_Buffer controlled_buffer_120
  assign the_16_th_line_of_the_picture = _0 ? 20'h1c038 : 20'bz;  // Controlled_Buffer controlled_buffer_121
  assign the_17_th_line_of_the_picture = _0 ? 20'h1c038 : 20'bz;  // Controlled_Buffer controlled_buffer_122
  assign the_18_th_line_of_the_picture = _0 ? 20'h1c038 : 20'bz;  // Controlled_Buffer controlled_buffer_123
  assign the_19_th_line_of_the_picture = _0 ? 20'h1c038 : 20'bz;  // Controlled_Buffer controlled_buffer_124
  assign the_20_th_line_of_the_picture = _0 ? 20'h1c038 : 20'bz;  // Controlled_Buffer controlled_buffer_125
  assign the_21_st_line_of_the_picture = _0 ? 20'h1c038 : 20'bz;  // Controlled_Buffer controlled_buffer_126
  assign the_22_nd_line_of_the_picture = _0 ? 20'h1e078 : 20'bz;  // Controlled_Buffer controlled_buffer_127
  assign the_23_rd_line_of_the_picture = _0 ? 20'h1f0f8 : 20'bz;  // Controlled_Buffer controlled_buffer_128
  assign the_24_th_line_of_the_picture = _0 ? 20'h1fff8 : 20'bz;  // Controlled_Buffer controlled_buffer_129
  assign the_25_th_line_of_the_picture = _0 ? 20'hfff0 : 20'bz;  // Controlled_Buffer controlled_buffer_130
  assign the_26_th_line_of_the_picture = _0 ? 20'h7fe0 : 20'bz;  // Controlled_Buffer controlled_buffer_131
  assign the_27_th_line_of_the_picture = _0 ? 20'h3fc0 : 20'bz;  // Controlled_Buffer controlled_buffer_132
  assign the_16_th_line_of_the_picture = _2 ? 20'h7f8 : 20'bz;  // Controlled_Buffer controlled_buffer_133
  assign the_16_th_line_of_the_picture = _1 ? 20'hf80 : 20'bz;  // Controlled_Buffer controlled_buffer_134
  assign the_17_th_line_of_the_picture = _1 ? 20'hf80 : 20'bz;  // Controlled_Buffer controlled_buffer_135
  assign the_17_th_line_of_the_picture = _2 ? 20'hff0 : 20'bz;  // Controlled_Buffer controlled_buffer_136
  assign the_18_th_line_of_the_picture = _2 ? 20'h1fe0 : 20'bz;  // Controlled_Buffer controlled_buffer_137
  assign the_18_th_line_of_the_picture = _1 ? 20'hf80 : 20'bz;  // Controlled_Buffer controlled_buffer_138
  assign the_19_th_line_of_the_picture = _1 ? 20'hf80 : 20'bz;  // Controlled_Buffer controlled_buffer_139
  assign the_19_th_line_of_the_picture = _2 ? 20'h3fc0 : 20'bz;  // Controlled_Buffer controlled_buffer_140
  assign the_20_th_line_of_the_picture = _2 ? 20'h7f80 : 20'bz;  // Controlled_Buffer controlled_buffer_141
  assign the_20_th_line_of_the_picture = _1 ? 20'hf80 : 20'bz;  // Controlled_Buffer controlled_buffer_142
  assign the_21_st_line_of_the_picture = _1 ? 20'hf80 : 20'bz;  // Controlled_Buffer controlled_buffer_143
  assign the_21_st_line_of_the_picture = _2 ? 20'hff00 : 20'bz;  // Controlled_Buffer controlled_buffer_144
  assign the_22_nd_line_of_the_picture = _2 ? 20'h1fff8 : 20'bz;  // Controlled_Buffer controlled_buffer_145
  assign the_22_nd_line_of_the_picture = _1 ? 20'hf80 : 20'bz;  // Controlled_Buffer controlled_buffer_146
  assign the_23_rd_line_of_the_picture = _2 ? 20'h1fff8 : 20'bz;  // Controlled_Buffer controlled_buffer_147
  assign the_23_rd_line_of_the_picture = _1 ? 20'hf80 : 20'bz;  // Controlled_Buffer controlled_buffer_148
  assign the_24_th_line_of_the_picture = _1 ? 20'h7f80 : 20'bz;  // Controlled_Buffer controlled_buffer_149
  assign the_24_th_line_of_the_picture = _2 ? 20'h1fff8 : 20'bz;  // Controlled_Buffer controlled_buffer_150
  assign the_25_th_line_of_the_picture = _2 ? 20'h1fff8 : 20'bz;  // Controlled_Buffer controlled_buffer_151
  assign the_25_th_line_of_the_picture = _1 ? 20'hfff0 : 20'bz;  // Controlled_Buffer controlled_buffer_152
  assign the_26_th_line_of_the_picture = _1 ? 20'h1fff8 : 20'bz;  // Controlled_Buffer controlled_buffer_153
  assign the_26_th_line_of_the_picture = _2 ? 20'h1fff8 : 20'bz;  // Controlled_Buffer controlled_buffer_154
  assign the_27_th_line_of_the_picture = _1 ? 20'h3fffc : 20'bz;  // Controlled_Buffer controlled_buffer_155
  assign the_27_th_line_of_the_picture = _2 ? 20'h1fff8 : 20'bz;  // Controlled_Buffer controlled_buffer_156
  assign the_16_th_line_of_the_picture = _3 ? 20'h7c0 : 20'bz;  // Controlled_Buffer controlled_buffer_157
  assign the_17_th_line_of_the_picture = _3 ? 20'h7e0 : 20'bz;  // Controlled_Buffer controlled_buffer_158
  assign the_18_th_line_of_the_picture = _3 ? 20'h3f0 : 20'bz;  // Controlled_Buffer controlled_buffer_159
  assign the_19_th_line_of_the_picture = _3 ? 20'h3f8 : 20'bz;  // Controlled_Buffer controlled_buffer_160
  assign the_20_th_line_of_the_picture = _3 ? 20'he1f8 : 20'bz;  // Controlled_Buffer controlled_buffer_161
  assign the_21_st_line_of_the_picture = _3 ? 20'h1e0f8 : 20'bz;  // Controlled_Buffer controlled_buffer_162
  assign the_22_nd_line_of_the_picture = _3 ? 20'h1f0f8 : 20'bz;  // Controlled_Buffer controlled_buffer_163
  assign the_23_rd_line_of_the_picture = _3 ? 20'h1f9f8 : 20'bz;  // Controlled_Buffer controlled_buffer_164
  assign the_24_th_line_of_the_picture = _3 ? 20'hfff0 : 20'bz;  // Controlled_Buffer controlled_buffer_165
  assign the_25_th_line_of_the_picture = _3 ? 20'h7fe0 : 20'bz;  // Controlled_Buffer controlled_buffer_166
  assign the_26_th_line_of_the_picture = _3 ? 20'h3fc0 : 20'bz;  // Controlled_Buffer controlled_buffer_167
  assign the_27_th_line_of_the_picture = _3 ? 20'h1f80 : 20'bz;  // Controlled_Buffer controlled_buffer_168
  assign the_16_th_line_of_the_picture = _4 ? 20'h1e0 : 20'bz;  // Controlled_Buffer controlled_buffer_169
  assign the_17_th_line_of_the_picture = _4 ? 20'h1e0 : 20'bz;  // Controlled_Buffer controlled_buffer_170
  assign the_18_th_line_of_the_picture = _4 ? 20'h1e0 : 20'bz;  // Controlled_Buffer controlled_buffer_171
  assign the_19_th_line_of_the_picture = _4 ? 20'h1e0 : 20'bz;  // Controlled_Buffer controlled_buffer_172
  assign the_20_th_line_of_the_picture = _4 ? 20'h1e0 : 20'bz;  // Controlled_Buffer controlled_buffer_173
  assign the_21_st_line_of_the_picture = _4 ? 20'h1e0 : 20'bz;  // Controlled_Buffer controlled_buffer_174
  assign the_22_nd_line_of_the_picture = _4 ? 20'h1e0 : 20'bz;  // Controlled_Buffer controlled_buffer_175
  assign the_23_rd_line_of_the_picture = _4 ? 20'h1e0 : 20'bz;  // Controlled_Buffer controlled_buffer_176
  assign the_24_th_line_of_the_picture = _4 ? 20'h3f0 : 20'bz;  // Controlled_Buffer controlled_buffer_177
  assign the_25_th_line_of_the_picture = _4 ? 20'h7f8 : 20'bz;  // Controlled_Buffer controlled_buffer_178
  assign the_26_th_line_of_the_picture = _4 ? 20'hff8 : 20'bz;  // Controlled_Buffer controlled_buffer_179
  assign the_27_th_line_of_the_picture = _4 ? 20'h1ff8 : 20'bz;  // Controlled_Buffer controlled_buffer_180
  assign the_16_th_line_of_the_picture = _5 ? 20'h1f8 : 20'bz;  // Controlled_Buffer controlled_buffer_181
  assign the_17_th_line_of_the_picture = _5 ? 20'hf8 : 20'bz;  // Controlled_Buffer controlled_buffer_182
  assign the_18_th_line_of_the_picture = _5 ? 20'hf8 : 20'bz;  // Controlled_Buffer controlled_buffer_183
  assign the_19_th_line_of_the_picture = _5 ? 20'h1c0f8 : 20'bz;  // Controlled_Buffer controlled_buffer_184
  assign the_20_th_line_of_the_picture = _5 ? 20'h1e0f8 : 20'bz;  // Controlled_Buffer controlled_buffer_185
  assign the_21_st_line_of_the_picture = _5 ? 20'h1f1f8 : 20'bz;  // Controlled_Buffer controlled_buffer_186
  assign the_22_nd_line_of_the_picture = _5 ? 20'h1fff8 : 20'bz;  // Controlled_Buffer controlled_buffer_187
  assign the_23_rd_line_of_the_picture = _5 ? 20'h1fff8 : 20'bz;  // Controlled_Buffer controlled_buffer_188
  assign the_24_th_line_of_the_picture = _5 ? 20'h1fff0 : 20'bz;  // Controlled_Buffer controlled_buffer_189
  assign the_25_th_line_of_the_picture = _5 ? 20'hffe0 : 20'bz;  // Controlled_Buffer controlled_buffer_190
  assign the_26_th_line_of_the_picture = _5 ? 20'h7fc0 : 20'bz;  // Controlled_Buffer controlled_buffer_191
  assign the_27_th_line_of_the_picture = _5 ? 20'h3f80 : 20'bz;  // Controlled_Buffer controlled_buffer_192
  assign the_16_th_line_of_the_picture = _6 ? 20'h1fff0 : 20'bz;  // Controlled_Buffer controlled_buffer_193
  assign the_17_th_line_of_the_picture = _6 ? 20'h1f9f8 : 20'bz;  // Controlled_Buffer controlled_buffer_194
  assign the_18_th_line_of_the_picture = _6 ? 20'h1f0f8 : 20'bz;  // Controlled_Buffer controlled_buffer_195
  assign the_19_th_line_of_the_picture = _6 ? 20'h1e078 : 20'bz;  // Controlled_Buffer controlled_buffer_196
  assign the_20_th_line_of_the_picture = _6 ? 20'h1e078 : 20'bz;  // Controlled_Buffer controlled_buffer_197
  assign the_21_st_line_of_the_picture = _6 ? 20'h1e078 : 20'bz;  // Controlled_Buffer controlled_buffer_198
  assign the_22_nd_line_of_the_picture = _6 ? 20'h1f0f8 : 20'bz;  // Controlled_Buffer controlled_buffer_199
  assign the_23_rd_line_of_the_picture = _6 ? 20'h1f9f8 : 20'bz;  // Controlled_Buffer controlled_buffer_200
  assign the_24_th_line_of_the_picture = _6 ? 20'hfff0 : 20'bz;  // Controlled_Buffer controlled_buffer_201
  assign the_25_th_line_of_the_picture = _6 ? 20'h7fe0 : 20'bz;  // Controlled_Buffer controlled_buffer_202
  assign the_26_th_line_of_the_picture = _6 ? 20'h3fc0 : 20'bz;  // Controlled_Buffer controlled_buffer_203
  assign the_27_th_line_of_the_picture = _6 ? 20'h1f80 : 20'bz;  // Controlled_Buffer controlled_buffer_204
  assign the_16_th_line_of_the_picture = _7 ? 20'hfff0 : 20'bz;  // Controlled_Buffer controlled_buffer_205
  assign the_17_th_line_of_the_picture = _7 ? 20'h7ff8 : 20'bz;  // Controlled_Buffer controlled_buffer_206
  assign the_18_th_line_of_the_picture = _7 ? 20'h1f7c : 20'bz;  // Controlled_Buffer controlled_buffer_207
  assign the_19_th_line_of_the_picture = _7 ? 20'h3e3c : 20'bz;  // Controlled_Buffer controlled_buffer_208
  assign the_20_th_line_of_the_picture = _7 ? 20'h3e1c : 20'bz;  // Controlled_Buffer controlled_buffer_209
  assign the_21_st_line_of_the_picture = _7 ? 20'h3e00 : 20'bz;  // Controlled_Buffer controlled_buffer_210
  assign the_22_nd_line_of_the_picture = _7 ? 20'h3e00 : 20'bz;  // Controlled_Buffer controlled_buffer_211
  assign the_23_rd_line_of_the_picture = _7 ? 20'h7c00 : 20'bz;  // Controlled_Buffer controlled_buffer_212
  assign the_24_th_line_of_the_picture = _7 ? 20'h7c00 : 20'bz;  // Controlled_Buffer controlled_buffer_213
  assign the_25_th_line_of_the_picture = _7 ? 20'h7c00 : 20'bz;  // Controlled_Buffer controlled_buffer_214
  assign the_26_th_line_of_the_picture = _7 ? 20'hf800 : 20'bz;  // Controlled_Buffer controlled_buffer_215
  assign the_27_th_line_of_the_picture = _7 ? 20'hf800 : 20'bz;  // Controlled_Buffer controlled_buffer_216
  assign the_16_th_line_of_the_picture = _8 ? 20'h1f80 : 20'bz;  // Controlled_Buffer controlled_buffer_217
  assign the_17_th_line_of_the_picture = _8 ? 20'h3fc0 : 20'bz;  // Controlled_Buffer controlled_buffer_218
  assign the_18_th_line_of_the_picture = _8 ? 20'h79e0 : 20'bz;  // Controlled_Buffer controlled_buffer_219
  assign the_19_th_line_of_the_picture = _8 ? 20'hf0f0 : 20'bz;  // Controlled_Buffer controlled_buffer_220
  assign the_20_th_line_of_the_picture = _8 ? 20'h1e078 : 20'bz;  // Controlled_Buffer controlled_buffer_221
  assign the_21_st_line_of_the_picture = _8 ? 20'h1c038 : 20'bz;  // Controlled_Buffer controlled_buffer_222
  assign the_22_nd_line_of_the_picture = _8 ? 20'h1c038 : 20'bz;  // Controlled_Buffer controlled_buffer_223
  assign the_23_rd_line_of_the_picture = _8 ? 20'h1e078 : 20'bz;  // Controlled_Buffer controlled_buffer_224
  assign the_24_th_line_of_the_picture = _8 ? 20'h1f0f8 : 20'bz;  // Controlled_Buffer controlled_buffer_225
  assign the_25_th_line_of_the_picture = _8 ? 20'h1fff8 : 20'bz;  // Controlled_Buffer controlled_buffer_226
  assign the_26_th_line_of_the_picture = _8 ? 20'hfff0 : 20'bz;  // Controlled_Buffer controlled_buffer_227
  assign the_27_th_line_of_the_picture = _8 ? 20'h7fe0 : 20'bz;  // Controlled_Buffer controlled_buffer_228
  assign the_16_th_line_of_the_picture = _9 ? 20'h7ff8 : 20'bz;  // Controlled_Buffer controlled_buffer_229
  assign the_17_th_line_of_the_picture = _9 ? 20'h3ff8 : 20'bz;  // Controlled_Buffer controlled_buffer_230
  assign the_18_th_line_of_the_picture = _9 ? 20'h1ef8 : 20'bz;  // Controlled_Buffer controlled_buffer_231
  assign the_19_th_line_of_the_picture = _9 ? 20'hf8 : 20'bz;  // Controlled_Buffer controlled_buffer_232
  assign the_20_th_line_of_the_picture = _9 ? 20'h1f8 : 20'bz;  // Controlled_Buffer controlled_buffer_233
  assign the_21_st_line_of_the_picture = _9 ? 20'h1c1f8 : 20'bz;  // Controlled_Buffer controlled_buffer_234
  assign the_22_nd_line_of_the_picture = _9 ? 20'h1e3f0 : 20'bz;  // Controlled_Buffer controlled_buffer_235
  assign the_23_rd_line_of_the_picture = _9 ? 20'h1fff0 : 20'bz;  // Controlled_Buffer controlled_buffer_236
  assign the_24_th_line_of_the_picture = _9 ? 20'hffe0 : 20'bz;  // Controlled_Buffer controlled_buffer_237
  assign the_25_th_line_of_the_picture = _9 ? 20'h7fe0 : 20'bz;  // Controlled_Buffer controlled_buffer_238
  assign the_26_th_line_of_the_picture = _9 ? 20'h3fc0 : 20'bz;  // Controlled_Buffer controlled_buffer_239
  assign the_27_th_line_of_the_picture = _9 ? 20'h1f80 : 20'bz;  // Controlled_Buffer controlled_buffer_240

  assign the_1_st_line_of_the_picture = {20{1'b0}};
  assign the_2_nd_line_of_the_picture = {20{1'b0}};
  assign the_3_rd_line_of_the_picture = {20{1'b0}};
  assign the_28_th_line_of_the_picture = {20{1'b0}};
  assign the_29_th_line_of_the_picture = {20{1'b0}};
  assign the_30_th_line_of_the_picture = {20{1'b0}};

  // Notes on the sheet:
  //   digit selection
endmodule

// SI
module set_interrupts (
  input  IAck,
  input  clock,
  input  reset,
  input  bump,
  input  rescue,
  input  good_jump,
  output IRQ,
  output [2:0] vector
);

  wire and_1_out, IRQ_t, or_1_out, or_2_out, or_3_out, or_5_out, s_r_ff_1_q, s_r_ff_2_q, s_r_ff_3_q,
       small_latency_1_delayed_signal;
  wire [2:0] controlled_buffer_1_out;

  S_R_Flip_Flop s_r_ff_1 (.clk(bump), .Q(s_r_ff_1_q), .preset(bump), .reset(or_1_out));  // open: S, R, Qn, en
  or or_1 (or_1_out, IAck, reset);
  S_R_Flip_Flop s_r_ff_2 (.clk(rescue), .Q(s_r_ff_2_q), .preset(rescue), .reset(or_2_out));  // open: S, R, Qn, en
  or or_2 (or_2_out, IAck, reset);
  S_R_Flip_Flop s_r_ff_3 (.clk(good_jump), .Q(s_r_ff_3_q), .preset(good_jump), .reset(or_3_out));  // open: S, R, Qn, en
  or or_3 (or_3_out, IAck, reset);
  or or_4 (IRQ_t, s_r_ff_1_q, s_r_ff_2_q, s_r_ff_3_q);
  S_R_Flip_Flop s_r_ff_4 (.clk(clock), .Q(IRQ), .preset(IRQ_t), .reset(or_5_out));  // open: S, R, Qn, en
  or or_5 (or_5_out, IAck, reset);
  assign controlled_buffer_1_out = s_r_ff_1_q ? 3'b000 : 3'bz;  // Controlled_Buffer controlled_buffer_1
  assign controlled_buffer_1_out = s_r_ff_2_q ? 3'b001 : 3'bz;  // Controlled_Buffer controlled_buffer_2
  and and_1 (and_1_out, s_r_ff_3_q, ~s_r_ff_1_q);  // AND_Gate
  Register #(.width(3), .trigger("high")) register_1 (
    .D(controlled_buffer_1_out), .en(IRQ_t), .Q(vector), .clk(small_latency_1_delayed_signal), .clr(reset));
  assign controlled_buffer_1_out = and_1_out ? 3'b010 : 3'bz;  // Controlled_Buffer controlled_buffer_3
  small_latency small_latency_1 (.signal(clock), .delayed_signal(small_latency_1_delayed_signal));
endmodule

// GS
module game_state (
  input  in_out,
  input  [3:0] I_Oadr,
  input  I_Osel,
  input  [7:0] I_Odat,
  input  clock,
  input  clear,
  output lose,
  output victory,
  output play
);

  wire [1:0] number_of_lives;
  wire [2:0] number_of_survivors;

  get_number_of_lives get_number_of_lives_1 (
    .in_out(in_out), .I_Oadr(I_Oadr), .I_Osel(I_Osel), .I_Odat(I_Odat), .clock(clock), .clear(clear),
    .number_of_lives(number_of_lives));
  Comparator #(.width(2), .mode("unsigned")) comparator_1 (.a(number_of_lives), .b(2'b00), .eq(lose));  // open: gt, lt
  Comparator #(.width(3), .mode("unsigned")) comparator_2 (
    .a(number_of_survivors), .b(3'b100), .eq(victory));  // open: gt, lt
  and and_1 (play, ~victory, ~lose);  // AND_Gate
  get_number_of_survivors get_number_of_survivors_1 (
    .number_of_survivors(number_of_survivors), .in_out(in_out), .I_Oadr(I_Oadr), .I_Osel(I_Osel),
    .I_Odat(I_Odat), .clock(clock), .clear(clear));
endmodule

// LIVES
module get_number_of_lives (
  input  in_out,
  input  [3:0] I_Oadr,
  input  I_Osel,
  input  [7:0] I_Odat,
  input  clock,
  input  clear,
  output [1:0] number_of_lives
);

  wire and_1_out, nor_1_out, s_r_ff_1_q, s_r_ff_1_qn, small_latency_1_delayed_signal,
       small_latency_2_delayed_signal;
  wire [1:0] register_1_q;

  and and_1 (and_1_out, I_Osel, nor_1_out, ~in_out);  // AND_Gate
  nor nor_1 (nor_1_out, ~I_Oadr[3], I_Oadr[2], I_Oadr[1], I_Oadr[0]);  // NOR_Gate
  Register #(.width(2)) register_1 (
    .D(I_Odat[1:0]), .en(and_1_out), .Q(register_1_q), .clk(small_latency_1_delayed_signal), .clr(clear));
  small_latency small_latency_1 (.signal(clock), .delayed_signal(small_latency_1_delayed_signal));
  small_latency small_latency_2 (.signal(and_1_out), .delayed_signal(small_latency_2_delayed_signal));
  assign number_of_lives = s_r_ff_1_qn ? 2'b11 : 2'bz;  // Controlled_Buffer controlled_buffer_1
  assign number_of_lives = s_r_ff_1_q ? register_1_q : 2'bz;  // Controlled_Buffer controlled_buffer_2
  S_R_Flip_Flop s_r_ff_1 (
    .clk(clock), .Q(s_r_ff_1_q), .Qn(s_r_ff_1_qn), .preset(small_latency_2_delayed_signal), .reset(clear));  // open: S, R, en
endmodule

// SURV
module get_number_of_survivors (
  input  in_out,
  input  [3:0] I_Oadr,
  input  I_Osel,
  input  [7:0] I_Odat,
  input  clock,
  input  clear,
  output [2:0] number_of_survivors
);

  wire and_1_out, nor_1_out, small_latency_1_delayed_signal;

  and and_1 (and_1_out, I_Osel, nor_1_out, ~in_out);  // AND_Gate
  nor nor_1 (nor_1_out, ~I_Oadr[3], I_Oadr[2], I_Oadr[1], ~I_Oadr[0]);  // NOR_Gate
  small_latency small_latency_1 (.signal(clock), .delayed_signal(small_latency_1_delayed_signal));
  Register #(.width(3)) register_1 (
    .D(I_Odat[2:0]), .en(and_1_out), .Q(number_of_survivors), .clk(small_latency_1_delayed_signal),
    .clr(clear));
endmodule

// GCS
module get_current_score (
  input  in_out,
  input  [3:0] I_Oadr,
  input  I_Osel,
  input  [7:0] I_Odat,
  input  clock,
  input  clear,
  output [3:0] the_first_digit,
  output [3:0] the_second_digit,
  output [3:0] the_third_digit
);

  wire and_1_out, nor_1_out, small_latency_1_delayed_signal;
  wire [7:0] register_1_q;

  and and_1 (and_1_out, I_Osel, nor_1_out, ~in_out);  // AND_Gate
  nor nor_1 (nor_1_out, I_Oadr[3], ~I_Oadr[2], ~I_Oadr[1], I_Oadr[0]);  // NOR_Gate
  Register register_1 (.D(I_Odat), .en(and_1_out), .Q(register_1_q), .clk(small_latency_1_delayed_signal), .clr(clear));
  small_latency small_latency_1 (.signal(clock), .delayed_signal(small_latency_1_delayed_signal));
  get_the_first_digit get_the_first_digit_1 (.number(register_1_q), .digit(the_first_digit));
  get_the_second_digit get_the_second_digit_1 (.number(register_1_q), .digit(the_second_digit));
  get_the_third_digit get_the_third_digit_1 (.number(register_1_q), .digit(the_third_digit));
endmodule

// GRS
module get_record_score (
  input  in_out,
  input  [3:0] I_Oadr,
  input  I_Osel,
  input  [7:0] I_Odat,
  input  clock,
  input  clear,
  output [3:0] the_first_digit,
  output [3:0] the_second_digit,
  output [3:0] the_third_digit
);

  wire and_1_out, nor_1_out, small_latency_1_delayed_signal;
  wire [7:0] register_1_q;

  and and_1 (and_1_out, I_Osel, nor_1_out, ~in_out);  // AND_Gate
  nor nor_1 (nor_1_out, I_Oadr[3], ~I_Oadr[2], ~I_Oadr[1], ~I_Oadr[0]);  // NOR_Gate
  Register register_1 (.D(I_Odat), .en(and_1_out), .Q(register_1_q), .clk(small_latency_1_delayed_signal), .clr(clear));
  small_latency small_latency_1 (.signal(clock), .delayed_signal(small_latency_1_delayed_signal));
  get_the_first_digit get_the_first_digit_1 (.number(register_1_q), .digit(the_first_digit));
  get_the_second_digit get_the_second_digit_1 (.number(register_1_q), .digit(the_second_digit));
  get_the_third_digit get_the_third_digit_1 (.number(register_1_q), .digit(the_third_digit));
endmodule

// SBF
module set_break_flags (
  input  in_out,
  input  [3:0] I_Oadr,
  input  I_Osel,
  input  [7:0] I_Odat,
  input  clock,
  input  clear,
  output _3_break,
  output _2_break,
  output _1_break
);

  wire comparator_2_lt, comparator_3_lt;
  wire [1:0] get_number_of_lives_1_number_of_lives;

  get_number_of_lives get_number_of_lives_1 (
    .in_out(in_out), .I_Oadr(I_Oadr), .I_Osel(I_Osel), .I_Odat(I_Odat), .clock(clock), .clear(clear),
    .number_of_lives(get_number_of_lives_1_number_of_lives));
  Comparator #(.width(2), .mode("unsigned")) comparator_1 (
    .a(get_number_of_lives_1_number_of_lives), .b(2'b01), .lt(_3_break));  // open: gt, eq
  Comparator #(.width(2), .mode("unsigned")) comparator_2 (
    .a(get_number_of_lives_1_number_of_lives), .b(2'b10), .lt(comparator_2_lt));  // open: gt, eq
  Comparator #(.width(2), .mode("unsigned")) comparator_3 (
    .a(get_number_of_lives_1_number_of_lives), .b(2'b11), .lt(comparator_3_lt));  // open: gt, eq
  or or_1 (_2_break, _3_break, comparator_2_lt);
  or or_2 (_1_break, _2_break, comparator_3_lt);
endmodule

// 1
module get_the_first_digit (
  input  [7:0] number,
  output [3:0] digit
);

  wire and_1_out, comparator_1_eq, comparator_1_gt, comparator_1_lt, comparator_2_eq, comparator_2_gt,
       comparator_2_lt, or_1_out, or_2_out;

  or or_1 (or_1_out, comparator_1_gt, comparator_1_eq);
  Comparator #(.mode("unsigned")) comparator_1 (
    .a(number), .b(8'hc8), .gt(comparator_1_gt), .eq(comparator_1_eq), .lt(comparator_1_lt));
  or or_2 (or_2_out, comparator_2_gt, comparator_2_eq);
  Comparator #(.mode("unsigned")) comparator_2 (
    .a(number), .b(8'h64), .gt(comparator_2_gt), .eq(comparator_2_eq), .lt(comparator_2_lt));
  assign digit = and_1_out ? 4'b0001 : 4'bz;  // Controlled_Buffer controlled_buffer_1
  assign digit = or_1_out ? 4'b0010 : 4'bz;  // Controlled_Buffer controlled_buffer_2
  and and_1 (and_1_out, comparator_1_lt, or_2_out);
  assign digit = comparator_2_lt ? 4'b0000 : 4'bz;  // Controlled_Buffer controlled_buffer_3
endmodule

// 2
module get_the_second_digit (
  input  [7:0] number,
  output [3:0] digit
);

  wire and_1_out, and_2_out, and_3_out, and_4_out, and_5_out, and_6_out, and_7_out, and_8_out,
       comparator_1_eq, comparator_1_gt, comparator_1_lt, comparator_2_lt, comparator_3_lt, comparator_4_lt,
       comparator_5_lt, comparator_6_lt, comparator_7_lt, comparator_8_lt, comparator_9_eq, comparator_9_gt,
       comparator_9_lt, or_1_out, or_2_out;
  wire [3:0] get_the_first_digit_1_digit;
  wire [7:0] bit_extender_1_out, multiplier_1_out, subtractor_1_out;

  get_the_first_digit get_the_first_digit_1 (.number(number), .digit(get_the_first_digit_1_digit));
  assign bit_extender_1_out = {{4{1'b0}}, get_the_first_digit_1_digit};  // Bit_Extender bit_extender_1
  Multiplier multiplier_1 (.a(8'h64), .b(bit_extender_1_out), .out(multiplier_1_out));  // open: cin, cout
  Subtractor subtractor_1 (.a(number), .b(multiplier_1_out), .out(subtractor_1_out));  // open: bin, bout
  Comparator #(.mode("unsigned")) comparator_1 (
    .a(subtractor_1_out), .b(8'h5a), .gt(comparator_1_gt), .eq(comparator_1_eq), .lt(comparator_1_lt));
  Comparator #(.mode("unsigned")) comparator_2 (.a(subtractor_1_out), .b(8'h50), .lt(comparator_2_lt));  // open: gt, eq
  Comparator #(.mode("unsigned")) comparator_3 (.a(subtractor_1_out), .b(8'h46), .lt(comparator_3_lt));  // open: gt, eq
  Comparator #(.mode("unsigned")) comparator_4 (.a(subtractor_1_out), .b(8'h3c), .lt(comparator_4_lt));  // open: gt, eq
  Comparator #(.mode("unsigned")) comparator_5 (.a(subtractor_1_out), .b(8'h32), .lt(comparator_5_lt));  // open: gt, eq
  Comparator #(.mode("unsigned")) comparator_6 (.a(subtractor_1_out), .b(8'h28), .lt(comparator_6_lt));  // open: gt, eq
  Comparator #(.mode("unsigned")) comparator_7 (.a(subtractor_1_out), .b(8'h1e), .lt(comparator_7_lt));  // open: gt, eq
  Comparator #(.mode("unsigned")) comparator_8 (.a(subtractor_1_out), .b(8'h14), .lt(comparator_8_lt));  // open: gt, eq
  Comparator #(.mode("unsigned")) comparator_9 (
    .a(subtractor_1_out), .b(8'ha), .gt(comparator_9_gt), .eq(comparator_9_eq), .lt(comparator_9_lt));
  assign digit = or_1_out ? 4'b1001 : 4'bz;  // Controlled_Buffer controlled_buffer_1
  or or_1 (or_1_out, comparator_1_gt, comparator_1_eq);
  and and_1 (and_1_out, comparator_1_lt, ~comparator_2_lt);  // AND_Gate
  and and_2 (and_2_out, comparator_2_lt, ~comparator_3_lt);  // AND_Gate
  and and_3 (and_3_out, comparator_3_lt, ~comparator_4_lt);  // AND_Gate
  and and_4 (and_4_out, comparator_4_lt, ~comparator_5_lt);  // AND_Gate
  and and_5 (and_5_out, comparator_5_lt, ~comparator_6_lt);  // AND_Gate
  and and_6 (and_6_out, comparator_6_lt, ~comparator_7_lt);  // AND_Gate
  and and_7 (and_7_out, comparator_7_lt, ~comparator_8_lt);  // AND_Gate
  or or_2 (or_2_out, comparator_9_gt, comparator_9_eq);
  assign digit = and_1_out ? 4'b1000 : 4'bz;  // Controlled_Buffer controlled_buffer_2
  and and_8 (and_8_out, comparator_8_lt, or_2_out);
  assign digit = and_2_out ? 4'b0111 : 4'bz;  // Controlled_Buffer controlled_buffer_3
  assign digit = and_4_out ? 4'b0101 : 4'bz;  // Controlled_Buffer controlled_buffer_4
  assign digit = and_3_out ? 4'b0110 : 4'bz;  // Controlled_Buffer controlled_buffer_5
  assign digit = and_5_out ? 4'b0100 : 4'bz;  // Controlled_Buffer controlled_buffer_6
  assign digit = and_6_out ? 4'b0011 : 4'bz;  // Controlled_Buffer controlled_buffer_7
  assign digit = and_7_out ? 4'b0010 : 4'bz;  // Controlled_Buffer controlled_buffer_8
  assign digit = and_8_out ? 4'b0001 : 4'bz;  // Controlled_Buffer controlled_buffer_9
  assign digit = comparator_9_lt ? 4'b0000 : 4'bz;  // Controlled_Buffer controlled_buffer_10
endmodule

// 3
module get_the_third_digit (
  input  [7:0] number,
  output [3:0] digit
);

  wire [3:0] get_the_first_digit_1_digit, get_the_second_digit_1_digit, multiplier_2_out;
  wire [7:0] bit_extender_1_out, multiplier_1_out, subtractor_1_out;

  get_the_first_digit get_the_first_digit_1 (.number(number), .digit(get_the_first_digit_1_digit));
  assign bit_extender_1_out = {{4{1'b0}}, get_the_first_digit_1_digit};  // Bit_Extender bit_extender_1
  Multiplier multiplier_1 (.a(8'h64), .b(bit_extender_1_out), .out(multiplier_1_out));  // open: cin, cout
  Subtractor subtractor_1 (.a(number), .b(multiplier_1_out), .out(subtractor_1_out));  // open: bin, bout
  get_the_second_digit get_the_second_digit_1 (.number(subtractor_1_out), .digit(get_the_second_digit_1_digit));
  Multiplier #(.width(4)) multiplier_2 (
    .a(4'b1010), .b(get_the_second_digit_1_digit), .out(multiplier_2_out));  // open: cin, cout
  Subtractor #(.width(4)) subtractor_2 (
    .a(subtractor_1_out[3:0]), .b(multiplier_2_out), .out(digit));  // open: bin, bout
endmodule

// MH
module max_height (
  input  [3:0] current_height,
  input  clock,
  input  reset,
  output [3:0] max_height
);

  wire comparator_1_gt, small_latency_1_delayed_signal;

  Register #(.width(4)) u_max_height (
    .D(current_height), .en(comparator_1_gt), .Q(max_height), .clk(small_latency_1_delayed_signal),
    .clr(reset));
  small_latency small_latency_1 (.signal(clock), .delayed_signal(small_latency_1_delayed_signal));
  Comparator #(.width(4), .mode("unsigned")) comparator_1 (
    .a(current_height), .b(max_height), .gt(comparator_1_gt));  // open: eq, lt
endmodule

// GJ
module good_jump (
  input  [3:0] current_max_height,
  input  clock,
  input  clear,
  output good_jump
);

  wire comparator_1_eq, comparator_2_eq, not_1_out, not_2_out, small_latency_1_delayed_signal;
  wire [3:0] previous_max_height_q;

  Comparator #(.width(4), .mode("unsigned")) comparator_1 (
    .a(current_max_height), .b(previous_max_height_q), .eq(comparator_1_eq));  // open: gt, lt
  Comparator #(.width(4), .mode("unsigned")) comparator_2 (
    .a(current_max_height), .b(4'b1011), .eq(comparator_2_eq));  // open: gt, lt
  and and_1 (good_jump, not_1_out, not_2_out);
  not not_1 (not_1_out, comparator_1_eq);
  not not_2 (not_2_out, comparator_2_eq);
  Register #(.width(4)) previous_max_height (
    .D(current_max_height), .en(good_jump), .Q(previous_max_height_q), .clk(small_latency_1_delayed_signal),
    .clr(clear));
  small_latency small_latency_1 (.signal(clock), .delayed_signal(small_latency_1_delayed_signal));
endmodule

// TBL
module tact_by_level (
  input  new_level,
  input  clear,
  input  tact,
  output tact_by_level
);

  wire _1_level_carry, _2_level_carry, _3_level_carry, clear_t, small_latency_1_delayed_signal;
  wire [1:0] current_level_q;

  or or_1 (clear_t, clear, new_level);
  Counter #(.width(2), .max('h3)) current_level (
    .count(new_level), .Q(current_level_q), .clk(small_latency_1_delayed_signal), .clr(clear));  // open: load, D, carry
  small_latency small_latency_1 (.signal(tact), .delayed_signal(small_latency_1_delayed_signal));
  Counter #(.width(2), .max('h3)) _1_level (
    .count(tact), .carry(_1_level_carry), .clk(tact), .clr(clear_t));  // open: load, D, Q
  Counter #(.width(2), .max('h2)) _2_level (
    .count(tact), .carry(_2_level_carry), .clk(tact), .clr(clear_t));  // open: load, D, Q
  Counter #(.width(1), .max('h1)) _3_level (
    .count(tact), .carry(_3_level_carry), .clk(tact), .clr(clear_t));  // open: load, D, Q
  Multiplexer #(.select(2), .disabled(0), .enable("false")) multiplexer_1 (
    .in0(_1_level_carry), .in1(_2_level_carry), .in2(_3_level_carry), .in3(tact), .out(tact_by_level),
    .sel(current_level_q));
endmodule

// SL
module small_latency (
  input  signal,
  output delayed_signal
);

  wire not_1_out, not_2_out, not_3_out;

  not not_1 (not_1_out, not_2_out);
  not not_2 (not_2_out, signal);
  not not_3 (not_3_out, not_1_out);
  not not_4 (delayed_signal, not_3_out);
endmodule
